// Logisim project YM6045C.circ as structural Verilog: 3 circuits, main circuit main
module main (
  input  MCLK,
  input  VCLK,
  input  ZCLK,
  input  D8,
  input  nCART,
  input  FC0,
  input  FC1,
  input  nLDS,
  input  nUDS,
  input  nOE0,
  input  nHSYNC,
  input  nWRES,
  input  nZWR,
  input  nZRD,
  input  nZBAK,
  input  nIREQ,
  input  nMREQ,
  input  nWAIT,
  input  nM1,
  input  nM3,
  input  RW,
  input  nBG,
  input  nBGACK,
  input  nAS,
  input  nDTACK,
  input  ZD0,
  input  VA8,
  input  VA9,
  input  VA10,
  input  VA11,
  input  VA12,
  input  VA13,
  input  VA14,
  input  VA15,
  input  VA16,
  input  VA17,
  input  VA18,
  input  VA19,
  input  VA20,
  input  VA21,
  input  VA22,
  input  VA23,
  input  ZA0,
  input  ZA7,
  input  ZA8,
  input  ZA9,
  input  ZA10,
  input  ZA11,
  input  ZA12,
  input  ZA13,
  input  ZA14,
  input  ZA15,
  input  nSRES,
  input  TPAL,
  input  nCAS0,
  output PIN100,
  output PIN99,
  output nZRAM,
  output nSOUND,
  output nVDPM,
  output EDCLK,
  output nUDS_o,
  output nLDS_o,
  output nAS_o,
  output nWAIT_o,
  output nIA14,
  output nVTOZ,
  output nZTOV,
  output RW_o,
  output nBR,
  output nBGACK_o,
  output VA23_o,
  output VA22_o,
  output VA21_o,
  output VA20_o,
  output VA19_o,
  output VA18_o,
  output VA17_o,
  output VA16_o,
  output VA15_o,
  output VA14_o,
  output VA13_o,
  output VA12_o,
  output VA11_o,
  output VA10_o,
  output VA9_o,
  output VA8_o,
  output ZA15_o,
  output ZA14_o,
  output ZA13_o,
  output ZA12_o,
  output ZA11_o,
  output ZA10_o,
  output ZA9_o,
  output ZA8_o,
  output ZA0_o,
  output nZ_RES,
  output nVRES,
  output nHALT,
  output nZBR,
  output nZNMI,
  output nZWR_o,
  output nZRD_o,
  output nCAS2,
  output nINTACK,
  output nVPA,
  output nIO,
  output nCE0,
  output nRAS2,
  output nROM,
  output nFDC,
  output nFDWR,
  output nDTACK_o,
  output nTIME,
  output nASEL,
  output nMREQ_o,
  output nZREF,
  output nNOE,
  output nEOE
);

  wire _2_out, _6_out, _13_out, _15_out, _28_out, _29_out, _30_out, _32_out, _35_out, _38_out, _41_out,
       _45_out, _47_out, _49_out, _51_out, _52_out, _56_out, _57_out, _61_out, _68_out, _70_out, _71_out,
       _73_out, _76_out, _77_out, _79_out, _80_out, _82_out, _83_out, _87_out, _88_out, _91_out, _94_out,
       _95_out, _100_out, _102_out, _105_out, _106_out, _107_out, _110_out, _111_out, _115_out, _120_out,
       _122_out, _123_out, _124_out, _127_out, _128_out, _130_out, _132_out, _134_out, _137_out, _138_out,
       _141_out, _143_out, _151_out, _156_out, _157_out, _158_out, _163_out, _164_out, _165_out, _167_out,
       _168_out, _169_out, _170_2_out, _170_out, _171_out, _172_out, _173_out, _176_2_out, _176_out,
       _177_out, _178_out, _179_out, _182_out, _187_out, _189_out, _190_out, _192_out, _194_out, _195_out,
       _196_out, _197_out, _201_out, _203_out, _207_out, _212_out, _213_out, _216_out, _218_out, _219_out,
       _224_out, _225_out, _229_out, _234_out, _235_out, _239_out, _241_out, _244_out, _248_out, _251_2_out,
       _251_out, _262_out, _263_out, _270_out, _273_out, _274_out, _275_out, _276_out, _281_out, _282_out,
       _283_out, _284_out, _285_out, _286_out, _287_out, _288_out, _292_out, _295_out, _296_out, _302_out,
       _304_out, _306_out, _310_out, _316_out, _317_out, _319_out, _323_out, _325_out, _326_out, _327_out,
       _335_out, _336_out, _339_out, _342_out, _343_out, buffer_1_out, buffer_2_out, buffer_3_out,
       buffer_5_out, buffer_6_out, buffer_7_out, buffer_8_out, buffer_9_out, buffer_10_out, buffer_11_out,
       buffer_12_out, buffer_14_out, CAS0, d_ff_1_q, d_ff_2_q, d_ff_3_qn, d_ff_4_q, d_ff_5_q, d_ff_6_q,
       d_ff_6_qn, d_ff_7_q, d_ff_8_q, d_ff_8_qn, d_ff_9_q, d_ff_9_qn, d_ff_10_qn, d_ff_11_q, d_ff_12_q,
       d_ff_13_q, d_ff_14_q, d_ff_15_q, d_ff_16_q, d_ff_17_q, d_ff_18_q, d_ff_19_q, d_ff_21_q, d_ff_21_qn,
       d_ff_22_q, d_ff_23_q, d_ff_24_q, d_ff_25_q, d_ff_25_qn, d_ff_26_q, d_ff_27_q, d_ff_28_qn, d_ff_29_q,
       d_ff_29_qn, d_ff_30_q, d_ff_31_q, d_ff_31_qn, d_ff_32_qn, d_ff_33_q, d_ff_34_qn, d_ff_35_q, d_ff_36_q,
       d_ff_37_q, d_ff_37_qn, d_ff_38_qn, d_ff_39_q, d_ff_40_q, d_ff_40_qn, d_ff_41_q, d_ff_42_q, d_ff_43_q,
       d_ff_44_q, d_ff_44_qn, d_ff_45_q, d_ff_46_q, d_ff_47_q, d_ff_47_qn, d_ff_48_qn, d_ff_49_q, d_ff_52_q,
       d_ff_53_q, d_ff_55_q, DCA0, DCA1, DCA2, DCA3, DCA4, DCA5, DCA6, DCA7, decoder_1_out0, decoder_1_out1,
       decoder_1_out2, decoder_1_out3, decoder_2_out0, decoder_2_out1, decoder_2_out2, decoder_3_out0,
       decoder_3_out1, decoder_3_out2, decoder_3_out3, FFRES, G129, G133, G135, G202, G205, G206, G211, G214,
       G240, G257, G289, j_k_ff_1_q, j_k_ff_1_qn, M1DELAY, M1DELAY2, multiplexer_1_out, n1_bit_cnt_1_nq,
       n1_bit_cnt_1_q, n1_bit_cnt_2_nq, n1_bit_cnt_2_q, n1_bit_cnt_3_nq, n1_bit_cnt_3_q, n4_bit_cnt_1_nq0,
       n4_bit_cnt_1_nq1, n4_bit_cnt_1_nq2, n4_bit_cnt_1_nq3, n4_bit_cnt_2_nq0, n4_bit_cnt_2_nq1,
       n4_bit_cnt_2_nq2, n4_bit_cnt_2_nq3, n4_bit_cnt_3_nq0, n4_bit_cnt_3_nq1, n4_bit_cnt_3_nq2,
       n4_bit_cnt_3_nq3, nFFRES, not_6_out, not_7_out, not_8_out, not_9_out, not_10_out, not_11_out,
       not_12_out, not_13_out, not_14_out, not_15_out, not_16_out, not_17_out, not_18_out, not_19_out,
       not_20_out, not_21_out, not_22_out, not_23_out, not_24_out, not_25_out, not_26_out, not_27_out,
       not_28_out, not_29_out, not_30_out, not_31_out, not_32_out, not_33_out, not_34_out, not_35_out,
       not_36_out, not_37_out, not_38_out, not_39_out, not_40_out, not_41_out, not_42_out, not_43_out,
       not_44_out, not_45_out, not_46_out, not_47_out, not_48_out, not_49_out, not_50_out, not_51_out,
       not_52_out, not_53_out, not_54_out, not_55_out, not_56_out, not_57_out, not_58_out, not_59_out,
       not_60_out, not_61_out, not_62_out, not_63_out, not_64_out, not_65_out, not_66_out, not_67_out,
       not_68_out, not_69_out, not_70_out, not_71_out, not_72_out, not_73_out, not_74_out, not_75_out,
       not_76_out, not_77_out, not_78_out, not_79_out, not_80_out, not_81_out, not_82_out, not_83_out,
       not_84_out, not_85_out, not_86_out, not_88_out, not_89_out, not_90_out, not_91_out, not_92_out,
       not_93_out, not_94_out, not_95_out, not_96_out, not_97_out, not_98_out, not_99_out, not_100_out,
       not_101_out, not_103_out, not_104_out, not_105_out, not_106_out, not_107_out, not_108_out, nTPAL,
       nVCLK, nZA15, RWd, SRES, t_ff_1_q, t_ff_2_q, t_ff_3_q, t_ff_4_q, t_ff_5_q, t_ff_6_q, t_ff_7_q,
       t_ff_8_q, t_ff_9_qn;
  wire [0:0] _50_out;
  wire [2:2] _299_out;
  wire [3:0] _221_out, _312_out, multiplexer_2_out, multiplexer_3_out, multiplexer_4_out, multiplexer_5_out;

  not not_1 (nVCLK, VCLK);
  not not_2 (nZA15, ZA15);
  not not_3 (SRES, nSRES);
  not not_4 (nTPAL, TPAL);
  not not_5 (CAS0, nCAS0);
  Decoder #(.select(2), .disabled(0), .enable("false")) decoder_1 (
    .out0(decoder_1_out0), .out1(decoder_1_out1), .out2(decoder_1_out2), .out3(decoder_1_out3),
    .sel({FC1, FC0}));
  D_Flip_Flop d_ff_1 (.clk(ZCLK), .D(nM1), .Q(d_ff_1_q));  // open: Qn, preset, en, reset
  not not_6 (not_6_out, decoder_1_out0);
  not not_7 (not_7_out, decoder_1_out1);
  not not_8 (not_8_out, decoder_1_out2);
  nand _332 (nINTACK, decoder_1_out3, nZTOV);
  buf buffer_1 (buffer_1_out, nM3);
  or _190 (_190_out, nBGACK, _189_out);
  and _189 (_189_out, _190_out, nZTOV);
  not not_9 (not_9_out, nHSYNC);
  not not_10 (not_10_out, ZCLK);
  D_Flip_Flop d_ff_2 (.clk(ZCLK), .D(d_ff_1_q), .Q(d_ff_2_q));  // open: Qn, preset, en, reset
  nor _240 (G240, _295_out, _319_out);
  not not_11 (not_11_out, G257);
  not not_12 (not_12_out, not_11_out);
  not not_13 (not_13_out, G257);
  nor _77 (_77_out, d_ff_8_q, nAS);
  nor _241 (_241_out, G240, nFFRES);
  not not_14 (not_14_out, buffer_10_out);
  buf buffer_2 (buffer_2_out, nSRES);
  J_K_Flip_Flop j_k_ff_1 (
    .J(1'b0), .clk(not_14_out), .K(not_9_out), .Q(j_k_ff_1_q), .Qn(j_k_ff_1_qn), .preset(not_15_out));  // open: en, reset
  not not_15 (not_15_out, buffer_12_out);
  not not_16 (not_16_out, ZA8);
  not not_17 (not_17_out, ZA9);
  not not_18 (not_18_out, ZA10);
  not not_19 (not_19_out, ZA11);
  not not_20 (not_20_out, ZA12);
  not not_21 (not_21_out, ZA15);
  not not_22 (not_22_out, VA22);
  not not_23 (not_23_out, G257);
  nor _319 (_319_out, not_6_out, buffer_1_out);
  nor _327 (_327_out, not_7_out, buffer_1_out);
  nor _325 (_325_out, not_8_out, buffer_1_out);
  not not_24 (not_24_out, nM3);
  not not_25 (not_25_out, _189_out);
  not not_26 (not_26_out, not_12_out);
  not not_27 (not_27_out, not_28_out);
  not not_28 (not_28_out, not_26_out);
  not not_29 (not_29_out, not_13_out);
  nor _158 (_158_out, _77_out, _241_out);
  or _82 (_82_out, nZBR, nZBAK);
  _1_bit_cnt u_1_bit_cnt_1 (
    .C(MCLK), .CIN(_2_out), .VAL(1'b1), .nLD(_6_out), .nRES(buffer_3_out), .Q(n1_bit_cnt_1_q),
    .nQ(n1_bit_cnt_1_nq));  // open: CO
  _1_bit_cnt u_1_bit_cnt_2 (
    .C(MCLK), .CIN(1'b1), .VAL(j_k_ff_1_q), .nLD(_6_out), .nRES(buffer_3_out), .Q(n1_bit_cnt_2_q),
    .nQ(n1_bit_cnt_2_nq));  // open: CO
  _1_bit_cnt u_1_bit_cnt_3 (
    .C(MCLK), .CIN(n1_bit_cnt_2_q), .VAL(1'b0), .nLD(_6_out), .nRES(buffer_3_out), .Q(n1_bit_cnt_3_q),
    .nQ(n1_bit_cnt_3_nq));  // open: CO
  buf buffer_3 (buffer_3_out, nSRES);
  buf buffer_4 (EDCLK, buffer_10_out);
  _4_bit_cnt u_4_bit_cnt_1 (
    .C(buffer_5_out), .nLD(j_k_ff_1_qn), .nRES(buffer_2_out), .CIN(j_k_ff_1_qn), .VAL0(1'b1), .VAL1(1'b0),
    .VAL2(1'b0), .VAL3(1'b0), .nQ0(n4_bit_cnt_1_nq0), .nQ1(n4_bit_cnt_1_nq1), .nQ2(n4_bit_cnt_1_nq2),
    .nQ3(n4_bit_cnt_1_nq3));  // open: CO
  buf buffer_5 (buffer_5_out, buffer_10_out);
  D_Flip_Flop d_ff_3 (.clk(not_10_out), .D(d_ff_2_q), .Q(M1DELAY2), .Qn(d_ff_3_qn));  // open: preset, en, reset
  nand _38 (_38_out, not_16_out, not_17_out, 1'b1, not_18_out, not_19_out, not_20_out);
  nand _51 (_51_out, nM3, not_21_out, ZA14, ZA13);
  nand _41 (_41_out, ZA12, ZA11, ZA10, 1'b1, ZA9, ZA8);
  or _216 (_216_out, VA10, VA11, VA14, VA15);
  nand _306 (_306_out, VA21, not_22_out, VA23, nM3);
  or _225 (_225_out, VA17, VA18, VA19, VA20);
  buf buffer_6 (buffer_6_out, _239_out);
  nor _239 (_239_out, nFFRES, _295_out);
  nor _310 (_310_out, d_ff_21_qn, _325_out);
  not not_30 (not_30_out, nFFRES);
  not not_31 (not_31_out, nFFRES);
  buf buffer_7 (buffer_7_out, FFRES);
  or _257 (G257, not_24_out, nBGACK, not_25_out);
  not not_32 (not_32_out, not_27_out);
  D_Flip_Flop d_ff_4 (.clk(CAS0), .D(VA23), .Q(d_ff_4_q), .preset(not_29_out));  // open: Qn, en, reset
  not not_33 (not_33_out, _83_out);
  nand _83 (_83_out, nZ_RES, _82_out);
  buf buffer_8 (buffer_8_out, nSRES);
  D_Flip_Flop d_ff_5 (.clk(VCLK), .D(d_ff_40_q), .Q(d_ff_5_q), .reset(not_60_out));  // open: Qn, preset, en
  nand _6 (_6_out, n1_bit_cnt_3_nq, n1_bit_cnt_2_nq, n1_bit_cnt_1_nq);
  not not_34 (not_34_out, buffer_2_out);
  or _318 (M1DELAY, d_ff_3_qn, nMREQ);
  or _49 (_49_out, _51_out, _41_out);
  Decoder #(.select(2), .disabled(0), .enable("false")) decoder_2 (
    .out0(decoder_2_out0), .out1(decoder_2_out1), .out2(decoder_2_out2), .sel({VA9, VA8}));  // open: out3
  nor _302 (_302_out, d_ff_21_q, _336_out, not_23_out, d_ff_23_q);
  not not_35 (not_35_out, nM3);
  D_Flip_Flop d_ff_6 (
    .clk(t_ff_9_qn), .D(nWRES), .Q(d_ff_6_q), .Qn(d_ff_6_qn), .reset(not_62_out));  // open: preset, en
  T_Flip_Flop t_ff_1 (.clk(_310_out), .T(not_30_out), .Q(t_ff_1_q));  // open: Qn, preset, reset, en
  T_Flip_Flop t_ff_2 (.clk(_326_out), .T(not_31_out), .Q(t_ff_2_q));  // open: Qn, preset, reset, en
  or _45 (_45_out, M1DELAY, ZA14, nZA15, nM3);
  or _244 (_244_out, nCAS0, G257);
  nand _270 (_270_out, G257, not_32_out);
  and _296 (_296_out, CAS0, d_ff_4_q, VA23);
  D_Flip_Flop d_ff_7 (.clk(nVCLK), .D(_178_out), .Q(d_ff_7_q));  // open: Qn, preset, en, reset
  D_Flip_Flop d_ff_8 (.clk(nVCLK), .D(_158_out), .Q(d_ff_8_q), .Qn(d_ff_8_qn), .preset(not_33_out));  // open: en, reset
  buf buffer_9 (buffer_9_out, buffer_8_out);
  D_Flip_Flop d_ff_9 (.clk(not_59_out), .D(d_ff_5_q), .Q(d_ff_9_q), .Qn(d_ff_9_qn));  // open: preset, en, reset
  and _2 (_2_out, n1_bit_cnt_2_q, n1_bit_cnt_3_q);
  buf buffer_10 (buffer_10_out, n1_bit_cnt_3_q);
  nor _15 (_15_out, n4_bit_cnt_1_nq3, n4_bit_cnt_1_nq2, n4_bit_cnt_1_nq1, n4_bit_cnt_1_nq0);
  D_Flip_Flop d_ff_10 (.clk(buffer_5_out), .D(_15_out), .Qn(d_ff_10_qn), .preset(not_34_out));  // open: Q, en, reset
  buf buffer_11 (buffer_11_out, d_ff_10_qn);
  or _52 (_52_out, M1DELAY, nZWR, _38_out, _51_out);
  nor _229 (_229_out, _216_out, _306_out, _225_out);
  or _230 (DCA6, _306_out, _225_out, VA16);
  and _342 (_342_out, 1'b1, 1'b1, buffer_6_out);
  nor _304 (_304_out, _295_out, _302_out, _319_out);
  or _292 (_292_out, nAS, not_35_out);
  not not_36 (not_36_out, d_ff_21_qn);
  T_Flip_Flop t_ff_3 (.clk(t_ff_1_q), .T(not_30_out), .Q(t_ff_3_q));  // open: Qn, preset, reset, en
  T_Flip_Flop t_ff_4 (.clk(t_ff_2_q), .T(not_31_out), .Q(t_ff_4_q));  // open: Qn, preset, reset, en
  and _44 (nCAS2, G129, _45_out, _244_out);
  not not_37 (not_37_out, not_39_out);
  not not_38 (not_38_out, _244_out);
  not not_39 (not_39_out, not_38_out);
  and _323 (_323_out, _270_out, VA23);
  or _133 (G133, VA23, G257);
  or _212 (_212_out, G257, _296_out);
  nand _178 (_178_out, d_ff_8_qn, nAS);
  or _251 (_251_out, d_ff_9_qn, d_ff_5_q);
  buf buffer_12 (buffer_12_out, buffer_11_out);
  D_Flip_Flop d_ff_11 (.clk(_52_out), .D(ZD0), .Q(d_ff_11_q), .reset(not_40_out));  // open: Qn, preset, en
  D_Flip_Flop d_ff_12 (.clk(_52_out), .D(d_ff_11_q), .Q(d_ff_12_q), .reset(not_40_out));  // open: Qn, preset, en
  D_Flip_Flop d_ff_13 (.clk(_52_out), .D(d_ff_12_q), .Q(d_ff_13_q), .reset(not_40_out));  // open: Qn, preset, en
  D_Flip_Flop d_ff_14 (.clk(_52_out), .D(d_ff_13_q), .Q(d_ff_14_q), .reset(not_40_out));  // open: Qn, preset, en
  D_Flip_Flop d_ff_15 (.clk(_52_out), .D(d_ff_14_q), .Q(d_ff_15_q), .reset(not_40_out));  // open: Qn, preset, en
  D_Flip_Flop d_ff_16 (.clk(_52_out), .D(d_ff_15_q), .Q(d_ff_16_q), .reset(not_40_out));  // open: Qn, preset, en
  D_Flip_Flop d_ff_17 (.clk(_52_out), .D(d_ff_16_q), .Q(d_ff_17_q), .reset(not_40_out));  // open: Qn, preset, en
  D_Flip_Flop d_ff_18 (.clk(_52_out), .D(d_ff_17_q), .Q(d_ff_18_q), .reset(not_40_out));  // open: Qn, preset, en
  D_Flip_Flop d_ff_19 (.clk(_52_out), .D(d_ff_18_q), .Q(d_ff_19_q), .reset(not_40_out));  // open: Qn, preset, en
  not not_40 (not_40_out, FFRES);
  D_Flip_Flop d_ff_20 (.clk(VCLK), .D(nSRES), .Q(FFRES), .Qn(nFFRES));  // open: preset, en, reset
  or _65 (nVTOZ, DCA6, nZBAK);
  _4_bit_cnt u_4_bit_cnt_2 (
    .C(VCLK), .nLD(buffer_6_out), .nRES(1'b1), .CIN(_342_out), .VAL0(1'b0), .VAL1(1'b0), .VAL2(1'b0),
    .VAL3(1'b0), .nQ0(n4_bit_cnt_2_nq0), .nQ1(n4_bit_cnt_2_nq1), .nQ2(n4_bit_cnt_2_nq2),
    .nQ3(n4_bit_cnt_2_nq3));  // open: CO
  or _213 (_213_out, VA23, G214, _292_out);
  not not_41 (not_41_out, _292_out);
  not not_42 (not_42_out, d_ff_21_qn);
  not not_43 (not_43_out, not_37_out);
  not not_44 (not_44_out, not_43_out);
  not not_45 (not_45_out, _323_out);
  not not_46 (not_46_out, nBGACK);
  nand _251_2 (_251_2_out, buffer_9_out, _251_out);
  not not_47 (not_47_out, nM3);
  Decoder #(.select(2), .disabled(0), .enable("false")) decoder_3 (
    .out0(decoder_3_out0), .out1(decoder_3_out1), .out2(decoder_3_out2), .out3(decoder_3_out3),
    .sel({VA13, VA12}));
  nor _339 (_339_out, n4_bit_cnt_2_nq3, n4_bit_cnt_2_nq2, n4_bit_cnt_2_nq1, n4_bit_cnt_2_nq0);
  D_Flip_Flop d_ff_21 (.clk(VCLK), .D(_304_out), .Q(d_ff_21_q), .Qn(d_ff_21_qn), .preset(FFRES));  // open: en, reset
  D_Flip_Flop d_ff_22 (.clk(VCLK), .D(_213_out), .Q(d_ff_22_q));  // open: Qn, preset, en, reset
  D_Flip_Flop d_ff_23 (
    .clk(not_41_out), .D(d_ff_21_qn), .Q(d_ff_23_q), .Qn(G289), .reset(not_42_out));  // open: preset, en
  D_Flip_Flop d_ff_24 (.clk(not_36_out), .D(d_ff_6_q), .Q(d_ff_24_q), .reset(not_62_out));  // open: Qn, preset, en
  not not_48 (not_48_out, not_62_out);
  T_Flip_Flop t_ff_5 (.clk(t_ff_3_q), .T(not_30_out), .Q(t_ff_5_q));  // open: Qn, preset, reset, en
  T_Flip_Flop t_ff_6 (.clk(t_ff_4_q), .T(not_31_out), .Q(t_ff_6_q));  // open: Qn, preset, reset, en
  not not_49 (not_49_out, nM1);
  not not_50 (not_50_out, not_44_out);
  D_Flip_Flop d_ff_25 (
    .clk(CAS0), .D(d_ff_25_qn), .Q(d_ff_25_q), .Qn(d_ff_25_qn), .preset(not_45_out));  // open: en, reset
  xnor _120 (_120_out, nCART, VA22);
  nand _262 (_262_out, d_ff_7_q, _178_out);
  nand _263 (_263_out, d_ff_28_qn, d_ff_7_q, _178_out);
  D_Flip_Flop d_ff_26 (.clk(not_46_out), .D(nWAIT), .Q(d_ff_26_q), .reset(not_51_out));  // open: Qn, preset, en
  not not_51 (not_51_out, not_52_out);
  not not_52 (not_52_out, _251_2_out);
  not not_53 (not_53_out, nAS);
  or _151 (_151_out, nZA15, not_47_out, M1DELAY);
  or _156 (_156_out, M1DELAY, _49_out);
  not not_54 (not_54_out, _49_out);
  and _234 (_234_out, d_ff_11_q, _49_out);
  and _235 (_235_out, d_ff_12_q, _49_out);
  and _236 (_312_out[2], d_ff_13_q, _49_out);
  and _237 (_312_out[3], d_ff_14_q, _49_out);
  and _221 (_221_out[0], d_ff_15_q, _49_out);
  and _222 (_221_out[1], d_ff_16_q, _49_out);
  and _223 (_221_out[2], d_ff_17_q, _49_out);
  and _220 (_221_out[3], d_ff_18_q, _49_out);
  and _50 (_50_out[0], d_ff_19_q, _49_out);
  not not_55 (not_55_out, nUDS);
  or _205 (G205, d_ff_22_q, _213_out);
  or _207 (_207_out, G289, VA23);
  D_Flip_Flop d_ff_27 (.clk(t_ff_9_qn), .D(not_48_out), .Q(d_ff_27_q), .reset(not_62_out));  // open: Qn, preset, en
  nor _68 (_68_out, d_ff_24_q, d_ff_6_qn);
  T_Flip_Flop t_ff_7 (.clk(t_ff_5_q), .T(not_30_out), .Q(t_ff_7_q));  // open: Qn, preset, reset, en
  T_Flip_Flop t_ff_8 (.clk(t_ff_6_q), .T(not_31_out), .Q(t_ff_8_q));  // open: Qn, preset, reset, en
  or _70 (_70_out, nM3, not_49_out, nIREQ);
  or _141 (_141_out, not_50_out, d_ff_25_q);
  D_Flip_Flop d_ff_28 (.clk(nVCLK), .D(_262_out), .Qn(d_ff_28_qn));  // open: Q, preset, en, reset
  D_Flip_Flop d_ff_29 (.clk(nVCLK), .D(_263_out), .Q(d_ff_29_q), .Qn(d_ff_29_qn));  // open: preset, en, reset
  D_Flip_Flop d_ff_30 (.clk(VCLK), .D(nAS), .Q(d_ff_30_q));  // open: Qn, preset, en, reset
  not not_56 (not_56_out, G133);
  not not_57 (not_57_out, not_58_out);
  not not_58 (not_58_out, not_56_out);
  not not_59 (not_59_out, VCLK);
  D_Flip_Flop d_ff_31 (
    .clk(VCLK), .D(not_46_out), .Q(d_ff_31_q), .Qn(d_ff_31_qn), .reset(not_60_out));  // open: preset, en
  not not_60 (not_60_out, d_ff_26_q);
  and _157 (_157_out, _151_out, _156_out);
  or _312 (_312_out[0], _234_out, not_54_out);
  or _313 (_312_out[1], _235_out, not_54_out);
  not not_61 (not_61_out, DCA7);
  nor _73 (_73_out, nUDS, RW);
  and _336 (_336_out, _339_out, 1'b1);
  and _295 (_295_out, _336_out, _195_out);
  and _197 (_197_out, _207_out, _196_out);
  nand _196 (_196_out, d_ff_37_qn, d_ff_44_q);
  D_Flip_Flop d_ff_32 (.clk(t_ff_9_qn), .D(d_ff_27_q), .Qn(d_ff_32_qn));  // open: Q, preset, en, reset
  not not_62 (not_62_out, buffer_7_out);
  nor _326 (_326_out, _327_out, t_ff_7_q);
  T_Flip_Flop t_ff_9 (.clk(t_ff_8_q), .T(buffer_7_out), .Qn(t_ff_9_qn));  // open: Q, preset, reset, en
  D_Flip_Flop d_ff_33 (.clk(ZCLK), .D(_70_out), .Q(d_ff_33_q));  // open: Qn, preset, en, reset
  not not_63 (not_63_out, not_65_out);
  not not_64 (not_64_out, not_63_out);
  not not_65 (not_65_out, _141_out);
  D_Flip_Flop d_ff_34 (.clk(DCA3), .D(D8), .Qn(d_ff_34_qn), .reset(not_66_out));  // open: Q, preset, en
  not not_66 (not_66_out, FFRES);
  not not_67 (not_67_out, VA21);
  or _127 (_127_out, _212_out, _120_out, VA21);
  or _124 (_124_out, VA21, _120_out, G135);
  or _192 (_192_out, d_ff_29_q, nAS, d_ff_30_q);
  not not_68 (not_68_out, not_69_out);
  not not_69 (not_69_out, not_57_out);
  nand _87 (_87_out, nLDS, nUDS);
  not not_70 (not_70_out, nAS);
  not not_71 (not_71_out, nBGACK);
  D_Flip_Flop d_ff_35 (.clk(ZCLK), .D(_157_out), .Q(d_ff_35_q));  // open: Qn, preset, en, reset
  nand _148 (DCA0, decoder_2_out0, decoder_3_out0, VA16, _229_out);
  nand _145 (DCA7, _229_out, VA16, decoder_3_out1);
  nand _146 (DCA1, decoder_2_out0, decoder_3_out2, VA16, _229_out);
  nand _147 (DCA2, decoder_2_out0, decoder_3_out3, VA16, _229_out);
  nand _154 (DCA3, decoder_2_out0, not_61_out, _73_out);
  nand _160 (DCA4, decoder_2_out1, not_61_out, not_55_out);
  nand _153 (DCA5, decoder_2_out2, not_61_out, _73_out);
  D_Flip_Flop d_ff_36 (.clk(nVCLK), .D(G205), .Q(d_ff_36_q));  // open: Qn, preset, en, reset
  D_Flip_Flop d_ff_37 (
    .clk(VCLK), .D(_197_out), .Q(d_ff_37_q), .Qn(d_ff_37_qn), .preset(not_95_out));  // open: en, reset
  nor _143 (_143_out, d_ff_32_qn, _68_out);
  nor _138 (_138_out, buffer_7_out, buffer_1_out);
  not not_72 (not_72_out, not_64_out);
  Multiplexer #(.disabled(0), .enable("false")) multiplexer_1 (
    .in0(G133), .in1(_212_out), .out(multiplexer_1_out), .sel(d_ff_34_qn));
  not not_73 (not_73_out, _120_out);
  D_Flip_Flop d_ff_38 (.clk(VCLK), .D(_192_out), .Qn(d_ff_38_qn));  // open: Q, preset, en, reset
  not not_74 (not_74_out, not_68_out);
  not not_75 (not_75_out, not_74_out);
  D_Flip_Flop d_ff_39 (.clk(VCLK), .D(_87_out), .Q(d_ff_39_q));  // open: Qn, preset, en, reset
  D_Flip_Flop d_ff_40 (
    .clk(not_59_out), .D(d_ff_31_q), .Q(d_ff_40_q), .Qn(d_ff_40_qn), .reset(not_60_out));  // open: preset, en
  nor _224 (_224_out, VA22, VA20, VA19, VA18, VA17, VA15, VA13, VA12);
  and _13 (_13_out, not_53_out, 1'b1, VA14, VA16, VA21, VA23);
  and _187 (_187_out, _157_out, d_ff_35_q);
  or _299 (_299_out[2], nMREQ, VA21);
  _4_bit_cnt u_4_bit_cnt_3 (
    .C(VCLK), .nLD(buffer_6_out), .nRES(1'b1), .CIN(_285_out), .VAL0(1'b0), .VAL1(1'b0), .VAL2(1'b0),
    .VAL3(nM3), .nQ0(n4_bit_cnt_3_nq0), .nQ1(n4_bit_cnt_3_nq1), .nQ2(n4_bit_cnt_3_nq2), .nQ3(n4_bit_cnt_3_nq3));  // open: CO
  and _285 (_285_out, buffer_6_out, _336_out, _336_out);
  nand _288 (_288_out, _336_out, d_ff_21_qn, G289);
  nand _286 (_286_out, VA23, d_ff_23_q);
  or _203 (_203_out, _213_out, d_ff_36_q);
  nor _137 (_137_out, _138_out, buffer_1_out);
  and _71 (_71_out, d_ff_33_q, _70_out);
  or _132 (_132_out, not_72_out, d_ff_34_qn);
  or _130 (_130_out, multiplexer_1_out, not_73_out);
  not not_76 (not_76_out, _120_out);
  or _122 (_122_out, _120_out, G133, not_67_out);
  and _43 (nROM, _127_out, _124_out);
  or _163 (_163_out, DCA6, nAS);
  not not_77 (not_77_out, not_79_out);
  not not_78 (not_78_out, not_75_out);
  not not_79 (not_79_out, not_78_out);
  and _88 (_88_out, nOE0, d_ff_40_qn);
  and _248 (_248_out, nCAS0, d_ff_5_q);
  nand _61 (_61_out, _224_out, _13_out);
  D_Flip_Flop d_ff_41 (.clk(VCLK), .D(_102_out), .Q(d_ff_41_q));  // open: Qn, preset, en, reset
  D_Flip_Flop d_ff_42 (.clk(VCLK), .D(_177_out), .Q(d_ff_42_q));  // open: Qn, preset, en, reset
  or _100 (_100_out, nBG, not_70_out, not_71_out, _187_out);
  and _287 (_287_out, _288_out, _286_out);
  or _201 (_201_out, _203_out, d_ff_37_q);
  or _206 (G206, G205, d_ff_37_qn);
  and _69 (nIO, _71_out, DCA0);
  and _128 (_128_out, _132_out, _130_out);
  nand _168 (_168_out, nWAIT, d_ff_38_qn);
  nand _80 (_80_out, d_ff_29_qn, d_ff_39_q, _87_out);
  or _169 (_169_out, _88_out, _248_out);
  or _95 (_95_out, d_ff_42_q, _187_out);
  and _182 (_182_out, _100_out, _177_out);
  or _177 (_177_out, _187_out, SRES, d_ff_46_q);
  or _176 (_176_out, d_ff_46_q, SRES);
  Multiplexer #(.width(4), .disabled(0), .enable("false")) multiplexer_2 (
    .in0(_312_out), .in1({nZ_RES, 3'b000}), .out(multiplexer_2_out), .sel(nM3));
  Multiplexer #(.width(4), .disabled(0), .enable("false")) multiplexer_3 (
    .in0(_221_out), .in1({ZA15, _299_out[2], nMREQ, nIREQ}), .out(multiplexer_3_out), .sel(nM3));
  Multiplexer #(.width(4), .disabled(0), .enable("false")) multiplexer_4 (
    .in0({ZA12, ZA13, ZA14, _50_out[0]}), .in1({ZA11, ZA12, ZA13, ZA14}), .out(multiplexer_4_out), .sel(nM3));
  Multiplexer #(.width(4), .disabled(0), .enable("false")) multiplexer_5 (
    .in0({ZA8, ZA9, ZA10, ZA11}), .in1({ZA7, ZA8, ZA9, ZA10}), .out(multiplexer_5_out), .sel(nM3));
  not not_80 (not_80_out, not_81_out);
  not not_81 (not_81_out, _49_out);
  nor _195 (_195_out, n4_bit_cnt_3_nq3, n4_bit_cnt_3_nq2, n4_bit_cnt_3_nq1, n4_bit_cnt_3_nq0);
  D_Flip_Flop d_ff_43 (.clk(VCLK), .D(_287_out), .Q(d_ff_43_q), .preset(not_95_out));  // open: Qn, en, reset
  D_Flip_Flop d_ff_44 (.clk(nVCLK), .D(_201_out), .Q(d_ff_44_q), .Qn(d_ff_44_qn));  // open: preset, en, reset
  or _79 (_79_out, DCA4, RW);
  not not_82 (not_82_out, FFRES);
  and _123 (_123_out, not_72_out, _122_out);
  or _149 (nFDC, DCA1, nAS);
  or _134 (_134_out, G135, G206);
  or _167 (_167_out, _163_out, _168_out);
  or _164 (_164_out, DCA7, nAS);
  or _166 (nTIME, DCA2, nAS);
  and _25 (nASEL, not_77_out, G205);
  or _170 (_170_out, d_ff_31_qn, d_ff_9_q);
  or _139 (PIN99, VA8, VA9, VA10, VA11, 1'b0, nUDS, nLDS, _61_out);
  not not_83 (not_83_out, M1DELAY);
  or _106 (_106_out, nZRD, _102_out);
  and _107 (_107_out, _106_out, _105_out);
  or _105 (_105_out, nZWR, d_ff_41_q);
  D_Flip_Flop d_ff_45 (.clk(VCLK), .D(_95_out), .Q(d_ff_45_q));  // open: Qn, preset, en, reset
  nor _179 (_179_out, _177_out, nDTACK);
  D_Flip_Flop d_ff_46 (.clk(nVCLK), .D(_182_out), .Q(d_ff_46_q));  // open: Qn, preset, en, reset
  D_Flip_Flop d_ff_47 (
    .clk(nVCLK), .D(d_ff_43_q), .Q(d_ff_47_q), .Qn(d_ff_47_qn), .preset(not_95_out));  // open: en, reset
  D_Flip_Flop d_ff_48 (.clk(nVCLK), .D(d_ff_44_qn), .Qn(d_ff_48_qn), .reset(not_95_out));  // open: Q, preset, en
  nor _202 (G202, d_ff_44_qn, _213_out);
  D_Flip_Flop d_ff_49 (.clk(DCA5), .D(D8), .Q(d_ff_49_q), .reset(not_84_out));  // open: Qn, preset, en
  not not_84 (not_84_out, _143_out);
  D_Flip_Flop d_ff_50 (.clk(_79_out), .D(D8), .Qn(nZBR), .reset(not_82_out));  // open: Q, preset, en
  D_Flip_Flop d_ff_51 (.clk(t_ff_9_qn), .D(VA23), .Q(nZNMI), .preset(not_85_out));  // open: Qn, en, reset
  not not_85 (not_85_out, _137_out);
  or _28 (_28_out, G211, d_ff_34_qn);
  nor _29 (_29_out, d_ff_34_qn, G202);
  not not_86 (not_86_out, nM3);
  not not_87 (nNOE, _170_2_out);
  nand _170_2 (_170_2_out, _169_out, _170_out);
  not not_88 (not_88_out, ZA0);
  not not_89 (not_89_out, _177_out);
  buf buffer_13 (RWd, _176_out);
  buf buffer_14 (buffer_14_out, _176_out);
  and _218 (_218_out, d_ff_43_q, d_ff_47_q);
  nor _211 (G211, d_ff_47_qn, d_ff_48_qn);
  or _35 (_35_out, nM3, M1DELAY, ZA15);
  or _135 (G135, VA23, not_86_out, nAS);
  not not_90 (not_90_out, G135);
  nand _165 (_165_out, nFDC, _134_out, DCA0, _167_out, _164_out, nTIME);
  not not_91 (not_91_out, nM3);
  not not_92 (not_92_out, VA21);
  not not_93 (not_93_out, ZA14);
  not not_94 (not_94_out, ZA13);
  or _171 (_171_out, nMREQ, nM3, D8, VA22);
  or _343 (_343_out, RWd, nTPAL);
  or _110 (_110_out, _107_out, ZA0);
  or _111 (_111_out, _107_out, not_88_out);
  or _102 (_102_out, d_ff_45_q, _187_out);
  or _94 (_94_out, nTPAL, _187_out, _179_out);
  or _176_2 (_176_2_out, SRES, d_ff_46_q);
  or _91 (_91_out, not_89_out, SRES, _187_out);
  or _115 (_115_out, RWd, nTPAL);
  or _317 (_317_out, buffer_14_out, nTPAL);
  or _316 (_316_out, nTPAL, nZTOV);
  and _284 (_284_out, multiplexer_4_out[0], not_80_out);
  and _283 (_283_out, multiplexer_4_out[1], not_80_out);
  and _282 (_282_out, multiplexer_4_out[2], not_80_out);
  and _281 (_281_out, multiplexer_4_out[3], not_80_out);
  and _273 (_273_out, multiplexer_5_out[0], not_80_out);
  and _276 (_276_out, multiplexer_5_out[1], not_80_out);
  and _275 (_275_out, multiplexer_5_out[2], not_80_out);
  and _274 (_274_out, multiplexer_5_out[3], not_80_out);
  D_Flip_Flop d_ff_52 (.clk(nVCLK), .D(nUDS), .Q(d_ff_52_q));  // open: Qn, preset, en, reset
  and _57 (_57_out, d_ff_52_q, nUDS);
  D_Flip_Flop d_ff_53 (.clk(nVCLK), .D(_218_out), .Q(d_ff_53_q), .preset(not_95_out));  // open: Qn, en, reset
  not not_95 (not_95_out, _219_out);
  Multiplexer #(.disabled(0), .enable("false")) multiplexer_6 (
    .in0(_143_out), .in1(d_ff_49_q), .out(nZ_RES), .sel(nM3));
  and _335 (_335_out, nM3, _143_out);
  not not_96 (not_96_out, RW);
  or _30 (_30_out, _29_out, not_76_out, G135);
  nand _32 (_32_out, G202, not_90_out, VA21, not_76_out);
  nor _47 (_47_out, d_ff_55_q, nFDC, RW);
  nand _194 (_194_out, _165_out, nINTACK);
  nor _173 (_173_out, d_ff_7_q, not_91_out);
  nor _172 (_172_out, not_91_out, nMREQ, M1DELAY2);
  not not_97 (not_97_out, nNOE);
  or _108 (nVDPM, _171_out, D8);
  not not_98 (not_98_out, _343_out);
  assign nUDS_o = not_98_out ? _110_out : 1'bz;  // Controlled_Buffer controlled_buffer_1
  assign nLDS_o = not_98_out ? _111_out : 1'bz;  // Controlled_Buffer controlled_buffer_2
  assign nAS_o = not_98_out ? _102_out : 1'bz;  // Controlled_Buffer controlled_buffer_3
  assign nWAIT_o = not_99_out ? 1'b0 : 1'bz;  // Controlled_Buffer controlled_buffer_4
  not not_99 (not_99_out, _94_out);
  nand _5 (nIA14, nM3, VA14);
  and _175 (nZTOV, _176_2_out, nM3);
  assign RW_o = not_100_out ? nZWR : 1'bz;  // Controlled_Buffer controlled_buffer_5
  not not_100 (not_100_out, RWd);
  D_Flip_Flop d_ff_54 (.clk(VCLK), .D(_91_out), .Q(nBR));  // open: Qn, preset, en, reset
  assign nBGACK_o = not_101_out ? 1'b0 : 1'bz;  // Controlled_Buffer controlled_buffer_6
  not not_101 (not_101_out, _115_out);
  // NOT_Gate not_102 is placed but not wired
  assign VA23_o = not_103_out ? multiplexer_2_out[0] : 1'bz;  // Controlled_Buffer controlled_buffer_7
  assign VA22_o = not_103_out ? multiplexer_2_out[1] : 1'bz;  // Controlled_Buffer controlled_buffer_8
  assign VA21_o = not_103_out ? multiplexer_2_out[2] : 1'bz;  // Controlled_Buffer controlled_buffer_9
  not not_103 (not_103_out, _317_out);
  not not_104 (not_104_out, _316_out);
  assign VA20_o = not_104_out ? multiplexer_2_out[3] : 1'bz;  // Controlled_Buffer controlled_buffer_10
  assign VA19_o = not_104_out ? multiplexer_3_out[0] : 1'bz;  // Controlled_Buffer controlled_buffer_11
  assign VA18_o = not_104_out ? multiplexer_3_out[1] : 1'bz;  // Controlled_Buffer controlled_buffer_12
  assign VA17_o = not_104_out ? multiplexer_3_out[2] : 1'bz;  // Controlled_Buffer controlled_buffer_13
  assign VA16_o = not_104_out ? multiplexer_3_out[3] : 1'bz;  // Controlled_Buffer controlled_buffer_14
  assign VA15_o = not_104_out ? _284_out : 1'bz;  // Controlled_Buffer controlled_buffer_15
  assign VA14_o = not_104_out ? _283_out : 1'bz;  // Controlled_Buffer controlled_buffer_16
  assign VA13_o = not_104_out ? _282_out : 1'bz;  // Controlled_Buffer controlled_buffer_17
  assign VA12_o = not_104_out ? _281_out : 1'bz;  // Controlled_Buffer controlled_buffer_18
  assign VA11_o = not_104_out ? _273_out : 1'bz;  // Controlled_Buffer controlled_buffer_19
  assign VA10_o = not_104_out ? _276_out : 1'bz;  // Controlled_Buffer controlled_buffer_20
  assign VA9_o = not_104_out ? _275_out : 1'bz;  // Controlled_Buffer controlled_buffer_21
  assign VA8_o = not_104_out ? _274_out : 1'bz;  // Controlled_Buffer controlled_buffer_22
  not not_105 (not_105_out, nVTOZ);
  assign ZA15_o = not_105_out ? 1'b0 : 1'bz;  // Controlled_Buffer controlled_buffer_23
  assign ZA14_o = not_105_out ? VA14 : 1'bz;  // Controlled_Buffer controlled_buffer_24
  assign ZA13_o = not_105_out ? VA13 : 1'bz;  // Controlled_Buffer controlled_buffer_25
  assign ZA12_o = not_105_out ? VA12 : 1'bz;  // Controlled_Buffer controlled_buffer_26
  assign ZA11_o = not_105_out ? VA11 : 1'bz;  // Controlled_Buffer controlled_buffer_27
  assign ZA10_o = not_105_out ? VA10 : 1'bz;  // Controlled_Buffer controlled_buffer_28
  assign ZA9_o = not_105_out ? VA9 : 1'bz;  // Controlled_Buffer controlled_buffer_29
  assign ZA8_o = not_105_out ? VA8 : 1'bz;  // Controlled_Buffer controlled_buffer_30
  assign ZA0_o = not_105_out ? _57_out : 1'bz;  // Controlled_Buffer controlled_buffer_31
  nand _214 (G214, d_ff_53_q, _218_out);
  and _129 (G129, _218_out, _203_out);
  and _219 (_219_out, FFRES, nM3);
  not not_106 (not_106_out, nVTOZ);
  or _56 (_56_out, RW, nAS);
  or _76 (_76_out, not_96_out, nAS);
  or _333 (nVPA, nINTACK, nAS);
  and _33 (nRAS2, G211, _32_out, _123_out);
  D_Flip_Flop d_ff_55 (.clk(VCLK), .D(_47_out), .Q(d_ff_55_q), .Qn(nFDWR));  // open: preset, en, reset
  nor _85 (nZREF, _173_out, _172_out);
  nand _3 (nEOE, not_97_out, nM3);
  nand _209 (PIN100, not_92_out, not_53_out, VA22, VA23);
  nand _63 (nZRAM, not_93_out, nZA15, nM3, not_83_out);
  nand _62 (nSOUND, not_94_out, ZA14, 1'b1, nZA15, not_83_out, nM3);
  assign nVRES = _335_out ? 1'b0 : 1'bz;  // Controlled_Buffer controlled_buffer_32
  assign nHALT = _335_out ? 1'b0 : 1'bz;  // Controlled_Buffer controlled_buffer_33
  assign nZWR_o = not_106_out ? _56_out : 1'bz;  // Controlled_Buffer controlled_buffer_34
  assign nZRD_o = not_106_out ? _76_out : 1'bz;  // Controlled_Buffer controlled_buffer_35
  and _27 (nCE0, _128_out, _28_out, _35_out, _30_out);
  assign nDTACK_o = not_107_out ? 1'b0 : 1'bz;  // Controlled_Buffer controlled_buffer_36
  not not_107 (not_107_out, _194_out);
  assign nMREQ_o = not_108_out ? _80_out : 1'bz;  // Controlled_Buffer controlled_buffer_37
  not not_108 (not_108_out, nVTOZ);

  // Notes on the sheet:
  //   84
  //   48
  //   90
  //   114
  //   243
  //   331
  //   180
  //   328
  //   329
  //   330
  //   324
  //   11
  //   259
  //   181
  //   298
  //   !
  //   22
  //   22
  //   14
  //   10
  //   97
  //   21
  //   !
  //   260
  //   36
  //   42
  //   37
  //   40
  //   39
  //   48
  //   305
  //   301
  //   256
  //   258
  //   269
  //   297
  //   321
  //   EDCLK DIVIDER
  //   238
  //   315
  //   320
  //   232
  //   264
  //   162
  //   !
  //   12
  //   250
  //   9
  //   8
  //   19
  //   98,18,17,16
  //   20
  //   !
  //   152
  //   291
  //   66
  //   309
  //   334
  //   89
  //   7
  //   112
  //   4
  //   140
  //   D
  //   53
  //   75
  //   233
  //   308
  //   267
  //   142
  //   150
  //   Q7
  //   Q6
  //   Q5
  //   Q4
  //   Q3
  //   Q2
  //   Q1
  //   Q0
  //   !
  //   144
  //   337,338,340,341
  //   303
  //   204
  //   290
  //   289
  //   67
  //   307
  //   268
  //   242
  //   !
  //   255
  //   251
  //   !
  //   311
  //   322
  //   74
  //   261
  //   184
  //   193
  //   247
  //   !
  //   246
  //   96
  //   226
  //   161
  //   228
  //   34
  //   254
  //   252
  //   !
  //   159
  //   227
  //   !
  //   231
  //   72
  //   54
  //   155
  //   !
  //   131
  //   121
  //   191
  //   249
  //   99
  //   185
  //   186
  //   199
  //   198
  //   126
  //   26
  //   81
  //   119
  //   104
  //   93
  //   226
  //   $A100xx R/W
  //   $A120xx R/W
  //   $A130xx R/W
  //    $A12xxx R/W
  //   $A110xx  W
  //   $A111xx  W
  //   $A112xx  W
  //   $A0xxxx R/W
  //   277-280
  //   294
  //   200
  //   60
  //   314
  //   300
  //   125
  //   118
  //   293
  //   !
  //   170
  //   101
  //   183
  //   188
  //   245
  //   217
  //   210
  //   266
  //   78
  //   55
  //   !
  //   136
  //   1
  //   109
  //   92
  //   58
  //   265
  //   31
  //   174
  //   208
  //   64
  //   59
  //   !
  //   !
  //   215
  //   86
  //   103
  //   !
  //   !
  //   113
  //   !
  //   !
  //   !
  //   !
  //   !
  //   !
  //   46
  //   !
  //   !
  //   TO TMSS
endmodule

// CONTER 4 BIT
module _4_bit_cnt (
  input  C,
  input  nLD,
  input  nRES,
  input  CIN,
  input  VAL0,
  input  VAL1,
  input  VAL2,
  input  VAL3,
  output nQ0,
  output nQ1,
  output nQ2,
  output nQ3,
  output CO
);

  wire and_1_out, and_2_out, and_3_out, d_ff_1_q, d_ff_2_q, d_ff_3_q, d_ff_4_q, d_ff_5_q, d_ff_6_q, d_ff_7_q,
       d_ff_8_q, multiplexer_1_out, multiplexer_2_out, multiplexer_3_out, multiplexer_4_out, not_1_out,
       not_2_out, not_3_out, not_4_out, not_5_out, not_6_out, not_7_out, not_8_out, xor_1_out, xor_2_out,
       xor_3_out, xor_4_out;

  not not_1 (not_1_out, nRES);
  xor xor_1 (xor_1_out, d_ff_5_q, CIN);
  and and_1 (and_1_out, d_ff_5_q, CIN);
  not not_2 (not_2_out, nRES);
  xor xor_2 (xor_2_out, d_ff_6_q, and_1_out);
  and and_2 (and_2_out, d_ff_6_q, and_1_out);
  not not_3 (not_3_out, nRES);
  xor xor_3 (xor_3_out, d_ff_7_q, and_2_out);
  and and_3 (and_3_out, d_ff_7_q, and_2_out);
  not not_4 (not_4_out, nRES);
  xor xor_4 (xor_4_out, d_ff_8_q, and_3_out);
  and and_4 (CO, d_ff_8_q, and_3_out);
  Multiplexer #(.disabled(0), .enable("false")) multiplexer_1 (
    .in0(VAL0), .in1(xor_1_out), .out(multiplexer_1_out), .sel(nLD));
  Multiplexer #(.disabled(0), .enable("false")) multiplexer_2 (
    .in0(VAL1), .in1(xor_2_out), .out(multiplexer_2_out), .sel(nLD));
  Multiplexer #(.disabled(0), .enable("false")) multiplexer_3 (
    .in0(VAL2), .in1(xor_3_out), .out(multiplexer_3_out), .sel(nLD));
  Multiplexer #(.disabled(0), .enable("false")) multiplexer_4 (
    .in0(VAL3), .in1(xor_4_out), .out(multiplexer_4_out), .sel(nLD));
  not not_5 (not_5_out, C);
  D_Flip_Flop #(.trigger("high")) d_ff_1 (
    .clk(C), .D(multiplexer_1_out), .Q(d_ff_1_q), .reset(not_1_out));  // open: Qn, preset, en
  not not_6 (not_6_out, C);
  D_Flip_Flop #(.trigger("high")) d_ff_2 (
    .clk(C), .D(multiplexer_2_out), .Q(d_ff_2_q), .reset(not_2_out));  // open: Qn, preset, en
  not not_7 (not_7_out, C);
  D_Flip_Flop #(.trigger("high")) d_ff_3 (
    .clk(C), .D(multiplexer_3_out), .Q(d_ff_3_q), .reset(not_3_out));  // open: Qn, preset, en
  not not_8 (not_8_out, C);
  D_Flip_Flop #(.trigger("high")) d_ff_4 (
    .clk(C), .D(multiplexer_4_out), .Q(d_ff_4_q), .reset(not_4_out));  // open: Qn, preset, en
  D_Flip_Flop #(.trigger("high")) d_ff_5 (
    .clk(not_5_out), .D(d_ff_1_q), .Q(d_ff_5_q), .Qn(nQ0), .reset(not_1_out));  // open: preset, en
  D_Flip_Flop #(.trigger("high")) d_ff_6 (
    .clk(not_6_out), .D(d_ff_2_q), .Q(d_ff_6_q), .Qn(nQ1), .reset(not_2_out));  // open: preset, en
  D_Flip_Flop #(.trigger("high")) d_ff_7 (
    .clk(not_7_out), .D(d_ff_3_q), .Q(d_ff_7_q), .Qn(nQ2), .reset(not_3_out));  // open: preset, en
  D_Flip_Flop #(.trigger("high")) d_ff_8 (
    .clk(not_8_out), .D(d_ff_4_q), .Q(d_ff_8_q), .Qn(nQ3), .reset(not_4_out));  // open: preset, en

  // Notes on the sheet:
  //   C
  //   VAL
  //   LD
  //   /RES
  //   C
  //   VAL
  //   LD
  //   /RES
  //   C
  //   VAL
  //   LD
  //   /RES
  //   C
  //   VAL
  //   LD
  //   /RES
  //   CIN
  //   CO
  //   CIN
  //   CO
  //   CIN
  //   CO
  //   CIN
  //   CO
  //   CNT BIT
  //   Q
  //   nQ
  //   CNT BIT
  //   Q
  //   nQ
  //   CNT BIT
  //   Q
  //   nQ
  //   CNT BIT
  //   Q
  //   nQ
endmodule

// COUNTER 1BIT
module _1_bit_cnt (
  input  C,
  input  CIN,
  input  VAL,
  input  nLD,
  input  nRES,
  output Q,
  output nQ,
  output CO
);

  wire d_ff_1_q, multiplexer_1_out, not_1_out, not_2_out, xor_1_out;

  not not_1 (not_1_out, nRES);
  xor xor_1 (xor_1_out, Q, CIN);
  and and_1 (CO, Q, CIN);
  Multiplexer #(.disabled(0), .enable("false")) multiplexer_1 (
    .in0(VAL), .in1(xor_1_out), .out(multiplexer_1_out), .sel(nLD));
  not not_2 (not_2_out, C);
  D_Flip_Flop #(.trigger("high")) d_ff_1 (
    .clk(C), .D(multiplexer_1_out), .Q(d_ff_1_q), .reset(not_1_out));  // open: Qn, preset, en
  D_Flip_Flop #(.trigger("high")) d_ff_2 (
    .clk(not_2_out), .D(d_ff_1_q), .Q(Q), .Qn(nQ), .reset(not_1_out));  // open: preset, en

  // Notes on the sheet:
  //   C
  //   VAL
  //   LD
  //   /RES
  //   CIN
  //   CNT BIT
  //   Q
  //   nQ
  //   CO
endmodule
