// Logisim project cnt_bit.circ as structural Verilog: 1 circuit, main circuit main
module main (
  input  CLK,
  input  nLD,
  input  VAL,
  input  CIN,
  input  nRES,
  output COUT,
  output nQ,
  output Q
);

  wire multiplexer_1_out, multiplexer_2_out, multiplexer_3_out, multiplexer_4_out, nand_1_out, nand_2_out,
       nand_3_out, nor_1_out, not_1_out, not_2_out, not_3_out, not_4_out, not_5_out, not_6_out;

  not not_1 (not_1_out, VAL);
  nand nand_1 (nand_1_out, CIN, not_6_out);
  Multiplexer multiplexer_1 (.in0(1'b1), .in1(nor_1_out), .out(multiplexer_1_out), .sel(nand_1_out));
  nor nor_1 (nor_1_out, not_6_out, CIN);
  Multiplexer multiplexer_2 (.in0(not_1_out), .in1(multiplexer_1_out), .out(multiplexer_2_out), .sel(nLD));
  not not_2 (not_2_out, nand_2_out);
  not not_3 (not_3_out, multiplexer_2_out);
  Multiplexer multiplexer_3 (.in0(not_2_out), .in1(not_3_out), .out(multiplexer_3_out), .sel(CLK));
  nand nand_2 (nand_2_out, multiplexer_3_out, nRES);
  not not_4 (not_4_out, nand_2_out);
  not not_5 (not_5_out, nand_3_out);
  Multiplexer multiplexer_4 (.in0(not_4_out), .in1(not_5_out), .out(multiplexer_4_out), .sel(CLK));
  nand nand_3 (nand_3_out, multiplexer_4_out, nRES);
  not not_6 (not_6_out, nand_3_out);
  not not_7 (Q, nand_3_out);
  not not_8 (COUT, nand_1_out);
  not not_9 (nQ, not_6_out);
endmodule
