// Logisim project dffpos.circ as structural Verilog: 1 circuit, main circuit main
module main (
  input  clk,
  input  d,
  output nq,
  output q
);

  wire multiplexer_1_out, multiplexer_2_out, not_2_out, not_4_out, not_5_out, not_6_out, not_7_out, not_8_out;

  not not_1 (nq, not_4_out);
  not not_2 (not_2_out, not_4_out);
  Multiplexer multiplexer_1 (.in0(not_2_out), .in1(not_8_out), .out(multiplexer_1_out), .sel(clk));
  not not_3 (q, multiplexer_1_out);
  not not_4 (not_4_out, multiplexer_1_out);
  not not_5 (not_5_out, d);
  not not_6 (not_6_out, not_5_out);
  not not_7 (not_7_out, not_8_out);
  Multiplexer multiplexer_2 (.in0(not_6_out), .in1(not_7_out), .out(multiplexer_2_out), .sel(clk));
  not not_8 (not_8_out, multiplexer_2_out);
endmodule
