// Logisim project dffrpos.circ as structural Verilog: 1 circuit, main circuit main
module main (
  input  clk,
  input  b,
  input  nres,
  output nq,
  output q
);

  wire multiplexer_1_out, multiplexer_2_out, nand_1_out, nand_2_out, not_1_out, not_3_out, not_5_out,
       not_6_out, not_7_out, not_8_out;

  not not_1 (not_1_out, nand_1_out);
  not not_2 (nq, not_1_out);
  not not_3 (not_3_out, nand_1_out);
  not not_4 (q, nand_1_out);
  Multiplexer multiplexer_1 (.in0(not_3_out), .in1(not_5_out), .out(multiplexer_1_out), .sel(clk));
  not not_5 (not_5_out, nand_2_out);
  nand nand_1 (nand_1_out, multiplexer_1_out, nres);
  not not_6 (not_6_out, nand_2_out);
  Multiplexer multiplexer_2 (.in0(not_7_out), .in1(not_6_out), .out(multiplexer_2_out), .sel(clk));
  nand nand_2 (nand_2_out, multiplexer_2_out, nres);
  not not_7 (not_7_out, not_8_out);
  not not_8 (not_8_out, b);
endmodule
