// Logisim project sr8.circ as structural Verilog: 1 circuit, main circuit main
module main (
  input  d,
  input  nres,
  input  clk,
  output [7:0] q
);

  wire not_1_out;

  D_Flip_Flop d_ff_1 (.D(d), .clk(clk), .Q(q[7]), .reset(not_1_out));  // open: Qn, preset
  not not_1 (not_1_out, nres);
  D_Flip_Flop d_ff_2 (.D(q[7]), .clk(clk), .Q(q[6]), .reset(not_1_out));  // open: Qn, preset
  D_Flip_Flop d_ff_3 (.D(q[6]), .clk(clk), .Q(q[5]), .reset(not_1_out));  // open: Qn, preset
  D_Flip_Flop d_ff_4 (.D(q[5]), .clk(clk), .Q(q[4]), .reset(not_1_out));  // open: Qn, preset
  D_Flip_Flop d_ff_5 (.D(q[4]), .clk(clk), .Q(q[3]), .reset(not_1_out));  // open: Qn, preset
  D_Flip_Flop d_ff_6 (.D(q[3]), .clk(clk), .Q(q[2]), .reset(not_1_out));  // open: Qn, preset
  D_Flip_Flop d_ff_7 (.D(q[2]), .clk(clk), .Q(q[1]), .reset(not_1_out));  // open: Qn, preset
  D_Flip_Flop d_ff_8 (.D(q[1]), .clk(clk), .Q(q[0]), .reset(not_1_out));  // open: Qn, preset
endmodule
