// Logisim project ym6045b.circ as structural Verilog: 5 circuits, main circuit main
module main (
  input  m3,
  input  ZD0,
  output [15:0] VA8_23_out
);

  wire and_1_out, and_2_out, dff_8bit_sr_1_b0, dff_8bit_sr_1_b1, dff_8bit_sr_1_b2, dff_8bit_sr_1_b3,
       dff_8bit_sr_1_b4, dff_8bit_sr_1_b5, dff_8bit_sr_1_b6, dff_8bit_sr_1_b7, dffres_1_q, nand_1_out,
       not_1_out, undriven, undriven_2, undriven_3, undriven_4, undriven_5, undriven_6, undriven_13;
  wire [0:0] undriven_7;
  wire [3:0] and_4_out, and_8_out, multiplexer_3_out, multiplexer_4_out, undriven_8, undriven_9, undriven_10,
       undriven_11, undriven_12;

  nand nand_1 (nand_1_out, undriven, undriven_2, undriven_3, undriven_4);
  dff_8bit_sr dff_8bit_sr_1 (
    .val(ZD0), .clk(nand_1_out), .reset(undriven_5), .b0(dff_8bit_sr_1_b0), .b1(dff_8bit_sr_1_b1),
    .b2(dff_8bit_sr_1_b2), .b3(dff_8bit_sr_1_b3), .b4(dff_8bit_sr_1_b4), .b5(dff_8bit_sr_1_b5),
    .b6(dff_8bit_sr_1_b6), .b7(dff_8bit_sr_1_b7));
  dffres dffres_1 (.val(dff_8bit_sr_1_b7), .clk(nand_1_out), .reset(undriven_5), .q(dffres_1_q));  // open: nq
  not not_1 (not_1_out, undriven_6);
  and and_1 (and_1_out, undriven_6, dff_8bit_sr_1_b0);
  and and_2 (and_2_out, undriven_6, dff_8bit_sr_1_b1);
  and and_3 (and_4_out[1], undriven_6, dff_8bit_sr_1_b2);
  and and_4 (and_4_out[0], undriven_6, dff_8bit_sr_1_b3);
  and and_5 (and_8_out[3], undriven_6, dff_8bit_sr_1_b4);
  and and_6 (and_8_out[2], undriven_6, dff_8bit_sr_1_b5);
  and and_7 (and_8_out[1], undriven_6, dff_8bit_sr_1_b6);
  and and_8 (and_8_out[0], undriven_6, dff_8bit_sr_1_b7);
  and and_9 (undriven_9[3], undriven_6, dffres_1_q);
  or or_1 (and_4_out[3], not_1_out, and_1_out);
  or or_2 (and_4_out[2], not_1_out, and_2_out);
  Multiplexer #(.width(4)) multiplexer_1 (
    .in0({3'b000, undriven_7[0]}), .in1(and_4_out), .out(VA8_23_out[15:12]), .sel(m3));
  Multiplexer #(.width(4)) multiplexer_2 (.in0(undriven_8), .in1(and_8_out), .out(VA8_23_out[11:8]), .sel(m3));
  Multiplexer #(.width(4)) multiplexer_3 (.in0(undriven_10), .in1(undriven_9), .out(multiplexer_3_out), .sel(m3));
  Multiplexer #(.width(4)) multiplexer_4 (.in0(undriven_11), .in1(undriven_12), .out(multiplexer_4_out), .sel(m3));
  and and_10 (VA8_23_out[4], multiplexer_3_out[0], undriven_13);
  and and_11 (VA8_23_out[5], multiplexer_3_out[1], undriven_13);
  and and_12 (VA8_23_out[6], multiplexer_3_out[2], undriven_13);
  and and_13 (VA8_23_out[7], multiplexer_3_out[3], undriven_13);
  and and_14 (VA8_23_out[0], multiplexer_4_out[0], undriven_13);
  and and_15 (VA8_23_out[1], multiplexer_4_out[1], undriven_13);
  and and_16 (VA8_23_out[2], multiplexer_4_out[2], undriven_13);
  and and_17 (VA8_23_out[3], multiplexer_4_out[3], undriven_13);
endmodule

module dff_8bit_sr (
  input  val,
  input  clk,
  input  reset,
  output b0,
  output b1,
  output b2,
  output b3,
  output b4,
  output b5,
  output b6,
  output b7
);
endmodule

module dffres (
  input  val,
  input  clk,
  input  reset,
  output q,
  output nq
);
endmodule

module dff (
  input  val,
  input  clk,
  output q,
  output nq
);
endmodule

module dffset (
  input  val,
  input  clk,
  input  set,
  output q,
  output nq
);
endmodule
