// Logisim project ym6045b.circ as structural Verilog: 5 circuits, main circuit main
module main (
  input  m3,
  input  zclk,
  input  ZWR_in,
  input  mreq_in,
  input  ZD0,
  input  m1,
  input  [8:0] ZA7_15_in,
  input  vclk,
  input  as_in,
  output [15:0] VA8_23_out
);

  wire and_1_out, and_2_out, dff_1_q, dff_2_q, dff_3_nq, dff_3_q, dff_4_q, dff_5_q, dff_8bit_sr_1_b0,
       dff_8bit_sr_1_b1, dff_8bit_sr_1_b2, dff_8bit_sr_1_b3, dff_8bit_sr_1_b4, dff_8bit_sr_1_b5,
       dff_8bit_sr_1_b6, dff_8bit_sr_1_b7, dffres_1_q, dffset_1_q, multiplexer_1_out, nand_1_out, nand_2_out,
       nand_3_out, nand_4_out, nand_5_out, nand_6_out, nor_1_out, nor_2_out, nor_3_out, nor_4_out, not_1_out,
       not_2_out, not_3_out, not_4_out, not_5_out, not_6_out, not_7_out, not_8_out, not_9_out, not_10_out,
       or_1_out, or_2_out, undriven, undriven_2, undriven_3, undriven_4, undriven_11;
  wire [0:0] undriven_5;
  wire [3:0] and_4_out, and_8_out, multiplexer_4_out, multiplexer_5_out, undriven_6, undriven_7, undriven_8,
       undriven_9, undriven_10;

  Multiplexer multiplexer_1 (.in0(undriven), .in1(undriven_2), .out(multiplexer_1_out), .sel(m3));
  dff dff_1 (.val(m1), .clk(zclk), .q(dff_1_q));  // open: nq
  dff dff_2 (.val(dff_1_q), .clk(zclk), .q(dff_2_q));  // open: nq
  not not_1 (not_1_out, vclk);
  not not_2 (not_2_out, zclk);
  // NOR_Gate nor_1 has open pins: out=nor_1_out
  or or_1 (or_1_out, mreq_in, dff_3_nq);
  not not_3 (not_3_out, ZA7_15_in[1]);
  not not_4 (not_4_out, ZA7_15_in[2]);
  not not_5 (not_5_out, ZA7_15_in[3]);
  not not_6 (not_6_out, ZA7_15_in[4]);
  not not_7 (not_7_out, ZA7_15_in[5]);
  not nand_1 (nand_1_out, as_in);  // NAND_Gate
  nor nor_2 (nor_2_out, dffset_1_q, as_in);
  not nor_3 (nor_3_out, nor_1_out);  // NOR_Gate
  or or_2 (or_2_out, ZWR_in, or_1_out, nand_6_out, nand_2_out);
  nand nand_2 (nand_2_out, not_3_out, not_4_out, not_5_out, not_6_out, not_7_out, 1'b1);
  nand nand_3 (nand_3_out, nand_1_out, dff_4_q);
  nand nand_4 (nand_4_out, nand_1_out, dff_4_q, dff_5_q);
  nor nor_4 (nor_4_out, nor_2_out, nor_3_out);
  not nand_5 (nand_5_out, multiplexer_1_out);  // NAND_Gate
  dff dff_3 (.val(dff_2_q), .clk(not_2_out), .q(dff_3_q), .nq(dff_3_nq));
  nand nand_6 (nand_6_out, ZA7_15_in[7], not_8_out, m3, ZA7_15_in[6]);
  not not_8 (not_8_out, ZA7_15_in[8]);
  dff dff_4 (.val(nand_1_out), .clk(not_1_out), .q(dff_4_q));  // open: nq
  dff dff_5 (.val(nand_3_out), .clk(not_1_out), .q(dff_5_q));  // open: nq
  dff dff_6 (.val(nand_4_out), .clk(not_1_out));  // open: q, nq
  dffset dffset_1 (.val(nor_4_out), .clk(not_1_out), .set(nand_5_out), .q(dffset_1_q));  // open: nq
  dff_8bit_sr dff_8bit_sr_1 (
    .val(ZD0), .clk(or_2_out), .reset(undriven_3), .b0(dff_8bit_sr_1_b0), .b1(dff_8bit_sr_1_b1),
    .b2(dff_8bit_sr_1_b2), .b3(dff_8bit_sr_1_b3), .b4(dff_8bit_sr_1_b4), .b5(dff_8bit_sr_1_b5),
    .b6(dff_8bit_sr_1_b6), .b7(dff_8bit_sr_1_b7));
  dffres dffres_1 (.val(dff_8bit_sr_1_b7), .clk(or_2_out), .reset(undriven_3), .q(dffres_1_q));  // open: nq
  not not_9 (not_9_out, m3);
  not not_10 (not_10_out, undriven_4);
  and and_1 (and_1_out, undriven_4, dff_8bit_sr_1_b0);
  and and_2 (and_2_out, undriven_4, dff_8bit_sr_1_b1);
  and and_3 (and_4_out[1], undriven_4, dff_8bit_sr_1_b2);
  and and_4 (and_4_out[0], undriven_4, dff_8bit_sr_1_b3);
  and and_5 (and_8_out[3], undriven_4, dff_8bit_sr_1_b4);
  and and_6 (and_8_out[2], undriven_4, dff_8bit_sr_1_b5);
  and and_7 (and_8_out[1], undriven_4, dff_8bit_sr_1_b6);
  and and_8 (and_8_out[0], undriven_4, dff_8bit_sr_1_b7);
  and and_9 (undriven_7[3], undriven_4, dffres_1_q);
  // NOR_Gate nor_5 has open pins: in0=dff_3_q, in1=mreq_in, in2=not_9_out, out=open
  // NOR_Gate nor_6 has open pins: in0=not_9_out, in1=dff_4_q, out=open
  or or_3 (and_4_out[3], not_10_out, and_1_out);
  or or_4 (and_4_out[2], not_10_out, and_2_out);
  Multiplexer #(.width(4)) multiplexer_2 (
    .in0({3'b000, undriven_5[0]}), .in1(and_4_out), .out(VA8_23_out[15:12]), .sel(m3));
  Multiplexer #(.width(4)) multiplexer_3 (.in0(undriven_6), .in1(and_8_out), .out(VA8_23_out[11:8]), .sel(m3));
  Multiplexer #(.width(4)) multiplexer_4 (.in0(undriven_8), .in1(undriven_7), .out(multiplexer_4_out), .sel(m3));
  Multiplexer #(.width(4)) multiplexer_5 (.in0(undriven_9), .in1(undriven_10), .out(multiplexer_5_out), .sel(m3));
  and and_10 (VA8_23_out[4], multiplexer_4_out[0], undriven_11);
  and and_11 (VA8_23_out[5], multiplexer_4_out[1], undriven_11);
  and and_12 (VA8_23_out[6], multiplexer_4_out[2], undriven_11);
  and and_13 (VA8_23_out[7], multiplexer_4_out[3], undriven_11);
  and and_14 (VA8_23_out[0], multiplexer_5_out[0], undriven_11);
  and and_15 (VA8_23_out[1], multiplexer_5_out[1], undriven_11);
  and and_16 (VA8_23_out[2], multiplexer_5_out[2], undriven_11);
  and and_17 (VA8_23_out[3], multiplexer_5_out[3], undriven_11);
endmodule

module dff_8bit_sr (
  input  val,
  input  clk,
  input  reset,
  output b0,
  output b1,
  output b2,
  output b3,
  output b4,
  output b5,
  output b6,
  output b7
);
endmodule

module dffres (
  input  val,
  input  clk,
  input  reset,
  output q,
  output nq
);
endmodule

module dff (
  input  val,
  input  clk,
  output q,
  output nq
);
endmodule

module dffset (
  input  val,
  input  clk,
  input  set,
  output q,
  output nq
);
endmodule
