// Logisim project 315_5339.circ as structural Verilog: 2 circuits, main circuit main
module main (
  input  Pin1,
  input  MCLK,
  input  M3,
  input  VA14,
  input  OE0,
  input  Pin13,
  input  Pin15,
  input  pin3,
  input  Pin14,
  input  HSYNC,
  output pin12,
  output EDCLK,
  output IA14,
  output EOE,
  output out_15
);

  wire and_1_out, and_2_out, and_3_out, and_4_out, and_5_out, and_6_out, and_7_out, and_8_out, and_9_out,
       and_10_out, and_11_out, and_12_out, cnt_bit_1_out_10, cnt_bit_1_out_11, cnt_bit_2_out_10,
       cnt_bit_2_out_11, cnt_bit_3_out_10, cnt_bit_3_out_11, cnt_bit_3_val, cnt_bit_4_out_10,
       cnt_bit_4_out_11, cnt_bit_4_val, cnt_bit_5_out_10, cnt_bit_5_out_11, cnt_bit_6_out_10,
       cnt_bit_6_out_11, cnt_bit_7_out_10, cnt_bit_7_out_11, cnt_bit_8_out_10, cnt_bit_8_out_11,
       cnt_bit_8_val, d_ff_1_qn, d_ff_2_qn, d_ff_3_qn, d_ff_4_qn, d_ff_5_qn, d_ff_6_q, d_ff_6_qn,
       multiplexer_1_out, multiplexer_2_out, nand_1_out, nand_2_out, nand_3_out, nand_4_out, nand_5_out,
       nand_6_out, nand_7_out, nand_8_out, nand_9_out, nand_10_out, nand_11_out, nand_12_out, nand_13_out,
       nand_14_out, nor_1_out, nor_2_out, nor_3_out, nor_4_out, nor_5_out, nor_6_out, nor_7_out, nor_8_out,
       nor_9_out, nor_10_out, not_1_out, not_2_out, not_4_out, not_5_out, not_6_out, not_7_out, not_8_out,
       not_9_out, not_10_out, not_11_out, not_12_out, not_13_out, not_14_out, not_15_out, not_16_out,
       not_17_out, not_18_out, not_19_out, not_20_out, not_21_out, not_22_out, not_23_out, not_24_out,
       not_25_out, not_29_out, not_30_out, not_31_out, not_33_out, not_34_out, not_35_out, not_36_out,
       not_37_out, not_38_out, not_39_out, not_40_out, not_41_out, not_42_out, not_43_out, not_44_out,
       or_1_out, or_2_out, or_3_out, or_4_out, or_5_out, or_6_out, or_7_out, or_8_out, w0_out, w1_out,
       w2_out, w3_out, w4_out, w5_out, w6_out, w7_out, w8_out, w9_out, w10_out, w11_out, w12_out, w13_out,
       w14_out, w15_out, w16_out, w17_out, w19_out, w20_out, w21_out, w22_out, w23_out, w24_out, w25_out,
       w26_out, w27_out, w28_out, w29_out, w30_out, w31_out, w32_out;

  not not_1 (not_1_out, Pin14);
  not not_2 (not_2_out, Pin15);
  not not_3 (out_15, HSYNC);
  not not_4 (not_4_out, M3);
  not not_5 (not_5_out, M3);
  not not_6 (not_6_out, VA14);
  not not_7 (not_7_out, VA14);
  not not_8 (not_8_out, OE0);
  not not_9 (not_9_out, OE0);
  not not_10 (not_10_out, Pin13);
  not not_11 (not_11_out, out_15);
  not not_12 (not_12_out, Pin1);
  not not_13 (not_13_out, not_5_out);
  not not_14 (not_14_out, not_6_out);
  not not_15 (not_15_out, w6_out);
  and w0 (w0_out, not_9_out, not_10_out);
  and w1 (w1_out, not_18_out, not_1_out);
  and w5 (w5_out, not_15_out, not_10_out);
  and w6 (w6_out, not_2_out, not_10_out);
  and w7 (w7_out, not_2_out, not_1_out);
  not w8 (w8_out, w14_out);
  or or_1 (or_1_out, w16_out, not_18_out);
  or or_2 (or_2_out, w15_out, not_25_out);
  D_Flip_Flop #(.trigger("falling")) d_ff_1 (.D(not_18_out), .clk(Pin1), .Qn(d_ff_1_qn));  // open: Q, preset, reset
  D_Flip_Flop #(.trigger("falling")) d_ff_2 (.D(w9_out), .clk(Pin1), .Qn(d_ff_2_qn));  // open: Q, preset, reset
  D_Flip_Flop #(.trigger("falling")) d_ff_3 (.D(w31_out), .clk(Pin1), .Qn(d_ff_3_qn));  // open: Q, preset, reset
  D_Flip_Flop #(.trigger("falling")) d_ff_4 (.D(w4_out), .clk(Pin1), .Qn(d_ff_4_qn));  // open: Q, preset, reset
  not not_16 (not_16_out, pin3);
  not not_17 (not_17_out, not_11_out);
  not not_18 (not_18_out, not_17_out);
  nor nor_1 (nor_1_out, 1'b0, not_12_out);
  nor nor_2 (nor_2_out, Pin1, 1'b0);
  nand nand_1 (nand_1_out, not_13_out, not_14_out);
  nand nand_2 (nand_2_out, not_13_out, not_8_out);
  or w2 (w2_out, w0_out, w1_out);
  not not_19 (not_19_out, w1_out);
  and w9 (w9_out, or_1_out, or_2_out);
  Multiplexer multiplexer_1 (.in0(nand_4_out), .in1(nand_6_out), .out(multiplexer_1_out), .sel(Pin1));
  and w3 (w3_out, not_19_out, not_1_out);
  nand w10 (w10_out, w0_out, w30_out);
  or w11 (w11_out, w30_out, w19_out);
  nand w12 (w12_out, w19_out, w1_out);
  or or_3 (or_3_out, w32_out, not_2_out);
  or or_4 (or_4_out, w3_out, w8_out);
  not not_20 (not_20_out, w28_out);
  not not_21 (not_21_out, w7_out);
  not not_22 (not_22_out, w21_out);
  nand nand_3 (nand_3_out, w29_out, multiplexer_1_out);
  and and_1 (and_1_out, d_ff_2_qn, nor_1_out);
  and and_2 (and_2_out, 1'b0, nor_2_out);
  and and_3 (and_3_out, d_ff_3_qn, nor_1_out);
  and and_4 (and_4_out, nand_1_out, nor_2_out);
  and and_5 (and_5_out, d_ff_1_qn, nor_1_out);
  and and_6 (and_6_out, nand_2_out, nor_2_out);
  and w4 (w4_out, or_3_out, or_4_out);
  nand w13 (w13_out, nand_6_out, w10_out, w11_out, w12_out);
  nand w14 (w14_out, w12_out, w10_out, w2_out, nand_6_out);
  and w15 (w15_out, not_20_out, not_16_out);
  and w16 (w16_out, not_21_out, not_1_out);
  and w17 (w17_out, not_22_out, not_4_out);
  and w19 (w19_out, not_16_out, not_18_out);
  not not_23 (not_23_out, w19_out);
  and w20 (w20_out, not_23_out, not_16_out);
  and w21 (w21_out, not_4_out, not_7_out);
  nand w22 (w22_out, w21_out, w28_out);
  nand w23 (w23_out, w22_out, w25_out, nand_6_out, w26_out);
  nand w24 (w24_out, w26_out, w25_out, w27_out, nand_6_out);
  or w25 (w25_out, w21_out, w6_out);
  nand w26 (w26_out, w6_out, w7_out);
  or w27 (w27_out, w7_out, w28_out);
  and w28 (w28_out, not_7_out, not_16_out);
  nand w29 (w29_out, not_9_out, not_18_out);
  and w30 (w30_out, not_9_out, not_4_out);
  nand nand_4 (nand_4_out, 1'b1, nand_3_out);
  nor nor_3 (nor_3_out, and_1_out, and_2_out);
  nor nor_4 (nor_4_out, and_3_out, and_4_out);
  nor nor_5 (nor_5_out, and_5_out, and_6_out);
  or or_5 (or_5_out, w17_out, not_9_out);
  or or_6 (or_6_out, w5_out, not_24_out);
  not not_24 (not_24_out, w23_out);
  not not_25 (not_25_out, w24_out);
  not not_26 (pin12, nor_3_out);
  not not_27 (IA14, nor_4_out);
  not not_28 (EOE, nor_5_out);
  and w18 (not_18_out, or_5_out, or_6_out);
  Multiplexer multiplexer_2 (.in0(nand_3_out), .in1(nand_6_out), .out(multiplexer_2_out), .sel(Pin1));
  nand nand_5 (nand_5_out, 1'b1, multiplexer_2_out);
  not not_29 (not_29_out, w30_out);
  nand nand_6 (nand_6_out, w29_out, nand_5_out);
  and and_7 (and_7_out, d_ff_4_qn, nor_1_out);
  and and_8 (and_8_out, cnt_bit_3_val, nor_2_out);
  not not_30 (not_30_out, w13_out);
  and and_9 (and_9_out, not_29_out, not_4_out);
  nor nor_6 (nor_6_out, and_7_out, and_8_out);
  and w32 (w32_out, not_10_out, not_31_out);
  not not_31 (not_31_out, w0_out);
  or or_7 (or_7_out, not_7_out, w20_out);
  or or_8 (or_8_out, not_30_out, and_9_out);
  not not_32 (EDCLK, nor_6_out);
  and w31 (w31_out, or_7_out, or_8_out);
  not not_33 (not_33_out, pin3);
  not not_34 (not_34_out, pin3);
  cnt_bit cnt_bit_1 (
    .in0(cnt_bit_1_out_10), .in1(cnt_bit_1_out_11), .sel1(nand_7_out), .sel2(not_35_out), .in2(d_ff_6_qn),
    .clk(MCLK), .reset(not_34_out), .out_10(cnt_bit_1_out_10), .out_11(cnt_bit_1_out_11));  // open: val, nval
  cnt_bit cnt_bit_2 (
    .in0(cnt_bit_2_out_10), .in1(cnt_bit_2_out_11), .sel1(nand_8_out), .sel2(not_35_out), .in2(1'b0),
    .clk(MCLK), .reset(not_34_out), .out_10(cnt_bit_2_out_10), .out_11(cnt_bit_2_out_11));  // open: val, nval
  cnt_bit cnt_bit_3 (
    .in0(cnt_bit_3_out_10), .in1(cnt_bit_3_out_11), .sel1(nand_9_out), .sel2(not_35_out), .in2(1'b1),
    .clk(MCLK), .reset(not_34_out), .val(cnt_bit_3_val), .out_10(cnt_bit_3_out_10), .out_11(cnt_bit_3_out_11));  // open: nval
  cnt_bit cnt_bit_4 (
    .in0(cnt_bit_4_out_10), .in1(cnt_bit_4_out_11), .sel1(nand_10_out), .sel2(not_35_out), .in2(1'b1),
    .clk(MCLK), .reset(not_34_out), .val(cnt_bit_4_val), .out_10(cnt_bit_4_out_10), .out_11(cnt_bit_4_out_11));  // open: nval
  and and_10 (and_10_out, 1'b0, d_ff_6_q);
  nor nor_7 (nor_7_out, not_17_out, d_ff_6_q);
  not not_35 (not_35_out, cnt_bit_4_val);
  nor nor_8 (nor_8_out, and_10_out, nor_7_out);
  nand nand_7 (nand_7_out, 1'b1, 1'b1);
  nand nand_8 (nand_8_out, cnt_bit_1_out_10, not_36_out);
  nand nand_9 (nand_9_out, not_36_out, cnt_bit_1_out_10, cnt_bit_2_out_10);
  nand nand_10 (nand_10_out, not_36_out, cnt_bit_1_out_10, cnt_bit_2_out_10, cnt_bit_3_out_10);
  and and_11 (and_11_out, nor_9_out, 1'b1);
  not not_36 (not_36_out, nand_7_out);
  nor nor_9 (nor_9_out, cnt_bit_1_out_11, cnt_bit_2_out_11, cnt_bit_3_out_11, cnt_bit_4_out_11);
  not not_37 (not_37_out, not_33_out);
  D_Flip_Flop d_ff_5 (.D(and_12_out), .clk(cnt_bit_3_val), .Qn(d_ff_5_qn), .preset(not_37_out));  // open: Q, reset
  and and_12 (and_12_out, nor_10_out, 1'b1);
  D_Flip_Flop d_ff_6 (
    .D(nor_8_out), .clk(cnt_bit_3_val), .Q(d_ff_6_q), .Qn(d_ff_6_qn), .reset(not_38_out));  // open: preset
  not not_38 (not_38_out, not_43_out);
  cnt_bit cnt_bit_5 (
    .in0(cnt_bit_5_out_10), .in1(cnt_bit_5_out_11), .sel1(nand_11_out), .sel2(not_40_out), .in2(1'b1),
    .clk(cnt_bit_3_val), .reset(not_33_out), .out_10(cnt_bit_5_out_10), .out_11(cnt_bit_5_out_11));  // open: val, nval
  cnt_bit cnt_bit_6 (
    .in0(cnt_bit_6_out_10), .in1(cnt_bit_6_out_11), .sel1(nand_12_out), .sel2(not_40_out), .in2(1'b0),
    .clk(cnt_bit_3_val), .reset(not_33_out), .out_10(cnt_bit_6_out_10), .out_11(cnt_bit_6_out_11));  // open: val, nval
  cnt_bit cnt_bit_7 (
    .in0(cnt_bit_7_out_10), .in1(cnt_bit_7_out_11), .sel1(nand_13_out), .sel2(not_40_out), .in2(1'b0),
    .clk(cnt_bit_3_val), .reset(not_33_out), .out_10(cnt_bit_7_out_10), .out_11(cnt_bit_7_out_11));  // open: val, nval
  cnt_bit cnt_bit_8 (
    .in0(cnt_bit_8_out_10), .in1(cnt_bit_8_out_11), .sel1(nand_14_out), .sel2(not_40_out), .in2(1'b0),
    .clk(cnt_bit_3_val), .reset(not_33_out), .val(cnt_bit_8_val), .out_10(cnt_bit_8_out_10),
    .out_11(cnt_bit_8_out_11));  // open: nval
  not not_39 (not_39_out, d_ff_5_qn);
  not not_40 (not_40_out, cnt_bit_8_val);
  not not_41 (not_41_out, not_39_out);
  not not_42 (not_42_out, not_41_out);
  not not_43 (not_43_out, not_42_out);
  nand nand_11 (nand_11_out, 1'b1, 1'b1);
  nand nand_12 (nand_12_out, cnt_bit_5_out_10, not_44_out);
  nand nand_13 (nand_13_out, not_44_out, cnt_bit_5_out_10, cnt_bit_6_out_10);
  nand nand_14 (nand_14_out, not_44_out, cnt_bit_5_out_10, cnt_bit_6_out_10, cnt_bit_7_out_10);
  not not_44 (not_44_out, nand_11_out);
  nor nor_10 (nor_10_out, cnt_bit_5_out_11, cnt_bit_6_out_11, cnt_bit_7_out_11, cnt_bit_8_out_11);
endmodule

module cnt_bit (
  input  in0,
  input  in1,
  input  sel1,
  input  sel2,
  input  in2,
  input  clk,
  input  reset,
  output val,
  output nval,
  output out_10,
  output out_11
);

  wire multiplexer_1_out, multiplexer_2_out, multiplexer_3_out, multiplexer_4_out, nand_1_out, not_1_out;

  Multiplexer multiplexer_1 (.in0(in0), .in1(in1), .out(multiplexer_1_out), .sel(sel1));
  Multiplexer multiplexer_2 (.in0(multiplexer_1_out), .in1(in2), .out(multiplexer_2_out), .sel(sel2));
  Multiplexer multiplexer_3 (.in0(multiplexer_2_out), .in1(not_1_out), .out(multiplexer_3_out), .sel(clk));
  nand nand_1 (nand_1_out, reset, multiplexer_3_out);
  not not_1 (not_1_out, nand_1_out);
  Multiplexer multiplexer_4 (.in0(out_11), .in1(nand_1_out), .out(multiplexer_4_out), .sel(clk));
  not not_2 (out_10, multiplexer_4_out);
  nand nand_2 (out_11, reset, out_10);
  not not_3 (val, out_11);
  not not_4 (nval, out_10);
endmodule
