// Logisim project iochip.circ as structural Verilog: 4 circuits, main circuit main
module main (
  input  TEST,
  input  SRES,
  input  VCLK,
  input  PAL,
  input  UART_A_clk1,
  input  UART_A_clk2,
  input  UART_B_clk1,
  input  UART_B_clk2,
  input  DISK,
  input  JAP,
  input  C0i,
  input  C1i,
  input  C2i,
  input  C3i,
  input  C4i,
  input  C5i,
  input  C6i,
  input  [7:0] ZD_in,
  input  [7:0] ZA_in,
  input  [6:0] VA_in,
  input  [15:0] VD_in,
  input  nM3,
  input  LWR,
  input  CAS0,
  input  IO,
  input  A0i,
  input  A1i,
  input  A2i,
  input  A3i,
  input  VZ,
  input  A5i,
  input  A6i,
  input  B5i,
  input  B6i,
  input  t1,
  input  A4i,
  input  B0i,
  input  ZV,
  input  P3b7,
  input  B1i,
  input  B2i,
  input  B3i,
  input  B4i,
  input  P5b7,
  output C4o,
  output out_46,
  output C0d,
  output out_48,
  output out_49,
  output out_50,
  output out_51,
  output out_52,
  output out_53,
  output [6:0] VA_out,
  output C0o,
  output C1o,
  output C2o,
  output C3o,
  output C5o,
  output C6o,
  output A5d,
  output A6d,
  output B5d,
  output B6d,
  output A5o,
  output A6o,
  output B5o,
  output B6o,
  output bc1,
  output bc2,
  output bc3,
  output bc4,
  output bc5,
  output HL
);

  wire and_1_out, and_2_out, and_3_out, and_4_out, and_5_out, and_6_out, and_7_out, and_8_out, and_9_out,
       and_10_out, and_11_out, and_12_out, and_13_out, and_14_out, and_15_out, and_16_out, and_18_out,
       and_19_out, and_20_out, and_21_out, and_22_out, and_23_out, and_24_out, and_25_out, and_46_out,
       and_47_out, and_48_out, and_49_out, and_50_out, and_51_out, and_52_out, and_53_out, buffer_9_out,
       buffer_10_out, clk_div_1_out_4, d_ff_6_q, d_ff_6_qn, d_ff_15_q, d_ff_16_q, d_ff_17_q, d_ff_18_q,
       d_ff_19_q, d_ff_20_q, d_ff_21_q, d_ff_23_q, d_ff_23_qn, d_ff_24_q, d_ff_24_qn, d_ff_25_qn, d_ff_26_qn,
       d_ff_27_qn, d_ff_28_qn, d_ff_29_qn, d_ff_30_qn, d_ff_31_qn, d_ff_32_qn, d_ff_33_q, d_ff_33_qn,
       d_ff_34_q, d_ff_34_qn, d_ff_35_q, d_ff_35_qn, d_ff_36_q, d_ff_36_qn, d_ff_37_q, d_ff_38_q, d_ff_39_q,
       d_ff_40_q, d_ff_41_q, d_ff_42_q, d_ff_43_q, d_ff_44_q, d_ff_45_q, d_ff_45_qn, d_ff_46_q, d_ff_46_qn,
       d_ff_47_q, d_ff_47_qn, d_ff_48_q, d_ff_49_q, d_ff_50_qn, d_ff_51_q, d_ff_52_q, d_ff_52_qn, d_ff_53_q,
       d_ff_54_q, d_ff_55_q, d_ff_55_qn, d_ff_56_q, d_ff_56_qn, d_ff_57_q, d_ff_58_qn, d_ff_59_q, d_ff_59_qn,
       d_ff_60_q, d_ff_60_qn, d_ff_61_q, d_ff_62_q, d_ff_63_q, d_ff_64_q, d_ff_64_qn, d_ff_65_q, d_ff_66_q,
       d_ff_67_q, d_ff_67_qn, d_ff_68_q, d_ff_69_q, d_ff_70_q, d_ff_71_q, d_ff_71_qn, d_ff_74_q, d_ff_77_q,
       d_ff_79_q, d_ff_80_q, d_ff_80_qn, d_ff_82_q, d_ff_83_q, d_ff_83_qn, d_ff_85_q, d_ff_87_q, d_ff_88_q,
       d_ff_88_qn, d_ff_90_q, d_ff_91_q, d_ff_91_qn, d_ff_93_q, multiplexer_12_out, multiplexer_13_out,
       multiplexer_14_out, multiplexer_15_out, multiplexer_16_out, multiplexer_17_out, multiplexer_18_out,
       multiplexer_19_out, multiplexer_20_out, nand_1_out, nand_2_out, nand_3_out, nand_4_out, nand_5_out,
       nand_6_out, nand_7_out, nand_8_out, nand_9_out, nand_10_out, nand_11_out, nand_12_out, nand_13_out,
       nand_14_out, nand_15_out, nand_16_out, nand_18_out, nand_19_out, nand_20_out, nand_21_out,
       nand_22_out, nand_23_out, nand_24_out, nand_25_out, nand_28_out, nand_31_out, nand_34_out,
       nand_35_out, nand_37_out, nand_38_out, nand_40_out, nand_41_out, nand_42_out, nand_43_out,
       nand_44_out, nand_45_out, nand_46_out, nand_47_out, nand_48_out, nand_49_out, nand_50_out,
       nand_51_out, nand_52_out, nand_53_out, nand_54_out, nand_55_out, nand_56_out, nand_57_out,
       nand_58_out, nand_59_out, nand_62_out, nand_63_out, nand_64_out, nand_65_out, nand_66_out,
       nand_67_out, nand_68_out, nand_69_out, nand_70_out, nor_1_out, nor_2_out, nor_3_out, nor_4_out,
       nor_5_out, nor_6_out, nor_7_out, nor_8_out, nor_9_out, nor_10_out, nor_11_out, nor_12_out, nor_13_out,
       nor_14_out, nor_15_out, nor_16_out, nor_17_out, nor_26_out, nor_27_out, nor_28_out, nor_29_out,
       nor_30_out, not_1_out, not_2_out, not_3_out, not_4_out, not_5_out, not_6_out, not_7_out, not_8_out,
       not_9_out, not_10_out, not_11_out, not_12_out, not_13_out, not_14_out, not_15_out, not_16_out,
       not_17_out, not_21_out, not_22_out, not_23_out, not_24_out, not_25_out, not_26_out, not_27_out,
       not_28_out, not_29_out, not_30_out, not_31_out, not_32_out, not_33_out, not_34_out, not_35_out,
       not_36_out, not_37_out, not_38_out, not_39_out, not_40_out, not_41_out, not_42_out, not_43_out,
       not_44_out, not_45_out, not_46_out, not_47_out, not_48_out, not_49_out, not_50_out, not_51_out,
       not_52_out, not_53_out, not_54_out, not_55_out, not_56_out, not_57_out, not_58_out, not_59_out,
       not_60_out, not_61_out, not_62_out, not_63_out, not_64_out, not_65_out, not_66_out, not_67_out,
       not_68_out, or_1_out, or_2_out, or_3_out, or_6_out, or_7_out, or_8_out, or_9_out, or_10_out,
       or_11_out, or_12_out, or_13_out, or_14_out, or_16_out, or_17_out, or_18_out, or_19_out, or_21_out,
       or_22_out, or_23_out, or_24_out, or_25_out, or_26_out, undriven, undriven_2, undriven_3, undriven_4,
       undriven_5, undriven_6, undriven_7, undriven_8, undriven_9, xor_delay_6x_1_out_2,
       xor_delay_6x_2_out_2, xor_delay_6x_3_out_2, xor_delay_6x_4_out_2, xor_delay_6x_5_out_2,
       xor_delay_6x_6_out_2, xor_delay_6x_7_out_2, xor_delay_6x_8_out_2;
  wire [2:0] xnor_1_out;
  wire [6:0] multiplexer_22_out, or_20_out;
  wire [7:0] and_30_out, and_31_out, and_32_out, and_33_out, and_34_out, and_35_out, and_36_out, and_37_out,
       and_38_out, and_39_out, and_40_out, and_41_out, and_42_out, and_43_out, and_44_out, and_45_out,
       bit_extender_1_out, bit_extender_2_out, bit_extender_3_out, bit_extender_4_out, bit_extender_5_out,
       bit_extender_6_out, buffer_1_out, d_ff_7_q, d_ff_25_q, d_ff_58_q, d_ff_92_q, multiplexer_1_out,
       multiplexer_10_out, multiplexer_11_out, multiplexer_21_out, multiplexer_29_out, multiplexer_30_out,
       multiplexer_45_out, nand_60_out, nand_61_out, nor_18_out, nor_19_out, nor_20_out, nor_21_out,
       nor_22_out, nor_23_out, nor_24_out, nor_25_out;
  wire [7:4] multiplexer_41_out;
  wire [8:8] multiplexer_31_out;

  buf buffer_1 (buffer_1_out[0], C0i);
  buf buffer_2 (buffer_1_out[1], C1i);
  buf buffer_3 (buffer_1_out[2], C2i);
  buf buffer_4 (buffer_1_out[3], C3i);
  buf buffer_5 (buffer_1_out[4], C4i);
  buf buffer_6 (buffer_1_out[5], C5i);
  buf buffer_7 (buffer_1_out[6], C6i);
  D_Flip_Flop d_ff_1 (
    .D(multiplexer_10_out[3]), .clk(nand_40_out), .Q(d_ff_58_q[3]), .reset(not_1_out));  // open: Qn, preset
  D_Flip_Flop d_ff_2 (
    .D(multiplexer_10_out[4]), .clk(nand_40_out), .Q(d_ff_58_q[4]), .reset(not_1_out));  // open: Qn, preset
  D_Flip_Flop d_ff_3 (
    .D(multiplexer_10_out[5]), .clk(nand_40_out), .Q(d_ff_58_q[5]), .reset(not_1_out));  // open: Qn, preset
  D_Flip_Flop d_ff_4 (
    .D(multiplexer_10_out[6]), .clk(nand_40_out), .Q(d_ff_58_q[6]), .reset(not_1_out));  // open: Qn, preset
  D_Flip_Flop d_ff_5 (
    .D(multiplexer_10_out[7]), .clk(nand_40_out), .Q(d_ff_58_q[7]), .reset(not_1_out));  // open: Qn, preset
  not not_1 (not_1_out, and_3_out);
  and and_1 (and_1_out, or_1_out, nand_1_out, or_6_out);
  and and_2 (and_2_out, or_3_out, or_2_out);
  nand nand_1 (nand_1_out, nM3, nor_1_out);
  not not_2 (not_2_out, d_ff_6_q);
  D_Flip_Flop d_ff_6 (.D(SRES), .clk(VCLK), .Q(d_ff_6_q), .Qn(d_ff_6_qn));  // open: preset, reset
  not not_3 (not_3_out, PAL);
  and and_3 (and_3_out, d_ff_6_q, nM3);
  and and_4 (and_4_out, and_1_out, nM3);
  not not_4 (not_4_out, multiplexer_20_out);
  not not_5 (not_5_out, d_ff_46_q);
  D_Flip_Flop d_ff_7 (
    .D(multiplexer_10_out[0]), .clk(nand_23_out), .Q(d_ff_7_q[0]), .reset(not_9_out));  // open: Qn, preset
  D_Flip_Flop d_ff_8 (
    .D(multiplexer_10_out[1]), .clk(nand_23_out), .Q(d_ff_7_q[1]), .reset(not_9_out));  // open: Qn, preset
  D_Flip_Flop d_ff_9 (
    .D(multiplexer_10_out[2]), .clk(nand_23_out), .Q(d_ff_7_q[2]), .reset(not_9_out));  // open: Qn, preset
  D_Flip_Flop d_ff_10 (
    .D(multiplexer_10_out[3]), .clk(nand_23_out), .Q(d_ff_7_q[3]), .reset(not_9_out));  // open: Qn, preset
  D_Flip_Flop d_ff_11 (
    .D(multiplexer_10_out[4]), .clk(nand_23_out), .Q(d_ff_7_q[4]), .reset(not_9_out));  // open: Qn, preset
  D_Flip_Flop d_ff_12 (
    .D(multiplexer_10_out[5]), .clk(nand_23_out), .Q(d_ff_7_q[5]), .reset(not_9_out));  // open: Qn, preset
  D_Flip_Flop d_ff_13 (
    .D(multiplexer_10_out[6]), .clk(nand_23_out), .Q(d_ff_7_q[6]), .reset(not_9_out));  // open: Qn, preset
  D_Flip_Flop d_ff_14 (
    .D(multiplexer_10_out[7]), .clk(nand_23_out), .Q(d_ff_7_q[7]), .reset(not_9_out));  // open: Qn, preset
  D_Flip_Flop d_ff_15 (
    .D(multiplexer_10_out[0]), .clk(nand_20_out), .Q(d_ff_15_q), .reset(not_6_out));  // open: Qn, preset
  D_Flip_Flop d_ff_16 (
    .D(multiplexer_10_out[1]), .clk(nand_20_out), .Q(d_ff_16_q), .reset(not_6_out));  // open: Qn, preset
  D_Flip_Flop d_ff_17 (
    .D(multiplexer_10_out[2]), .clk(nand_20_out), .Q(d_ff_17_q), .reset(not_6_out));  // open: Qn, preset
  D_Flip_Flop d_ff_18 (
    .D(multiplexer_10_out[3]), .clk(nand_20_out), .Q(d_ff_18_q), .reset(not_6_out));  // open: Qn, preset
  D_Flip_Flop d_ff_19 (
    .D(multiplexer_10_out[4]), .clk(nand_20_out), .Q(d_ff_19_q), .reset(not_6_out));  // open: Qn, preset
  D_Flip_Flop d_ff_20 (
    .D(multiplexer_10_out[5]), .clk(nand_20_out), .Q(d_ff_20_q), .reset(not_6_out));  // open: Qn, preset
  D_Flip_Flop d_ff_21 (
    .D(multiplexer_10_out[6]), .clk(nand_20_out), .Q(d_ff_21_q), .reset(not_6_out));  // open: Qn, preset
  D_Flip_Flop d_ff_22 (
    .D(multiplexer_10_out[7]), .clk(nand_20_out), .Q(buffer_1_out[7]), .reset(not_6_out));  // open: Qn, preset
  not not_6 (not_6_out, 1'b1);
  and and_5 (and_5_out, CAS0, IO);
  not not_7 (not_7_out, ZA_in[0]);
  not not_8 (not_8_out, CAS0);
  D_Flip_Flop d_ff_23 (
    .D(d_ff_23_qn), .clk(not_4_out), .Q(d_ff_23_q), .Qn(d_ff_23_qn), .reset(not_2_out));  // open: preset
  D_Flip_Flop d_ff_24 (
    .D(d_ff_24_qn), .clk(not_5_out), .Q(d_ff_24_q), .Qn(d_ff_24_qn), .reset(not_2_out));  // open: preset
  buf buffer_8 (out_46, d_ff_6_qn);
  not not_9 (not_9_out, and_3_out);
  nor nor_1 (nor_1_out, CAS0, IO, and_21_out);
  and and_6 (and_6_out, not_7_out, CAS0);
  or or_1 (or_1_out, CAS0, VZ);
  or or_2 (or_2_out, CAS0, ZV);
  or or_3 (or_3_out, not_8_out, VZ);
  nor nor_2 (nor_2_out, VZ, t1);
  or or_4 (bc2, and_1_out, t1);
  nor nor_3 (nor_3_out, and_4_out, t1);
  or or_5 (bc4, and_2_out, t1);
  or or_6 (or_6_out, not_8_out, ZV);
  nor nor_4 (nor_4_out, ZV, t1);
  not not_10 (not_10_out, d_ff_58_q[6]);
  buf buffer_9 (buffer_9_out, d_ff_58_q[6]);
  not not_11 (not_11_out, d_ff_58_q[7]);
  buf buffer_10 (buffer_10_out, d_ff_58_q[7]);
  D_Flip_Flop #(.trigger("high")) d_ff_25 (
    .D(multiplexer_10_out[0]), .clk(not_12_out), .Q(d_ff_25_q[0]), .Qn(d_ff_25_qn));  // open: preset, reset
  D_Flip_Flop #(.trigger("high")) d_ff_26 (
    .D(multiplexer_10_out[1]), .clk(not_12_out), .Q(d_ff_25_q[1]), .Qn(d_ff_26_qn));  // open: preset, reset
  D_Flip_Flop #(.trigger("high")) d_ff_27 (
    .D(multiplexer_10_out[2]), .clk(not_12_out), .Q(d_ff_25_q[2]), .Qn(d_ff_27_qn));  // open: preset, reset
  D_Flip_Flop #(.trigger("high")) d_ff_28 (
    .D(multiplexer_10_out[3]), .clk(not_12_out), .Q(d_ff_25_q[3]), .Qn(d_ff_28_qn));  // open: preset, reset
  D_Flip_Flop #(.trigger("high")) d_ff_29 (
    .D(multiplexer_10_out[4]), .clk(not_12_out), .Q(d_ff_25_q[4]), .Qn(d_ff_29_qn));  // open: preset, reset
  D_Flip_Flop #(.trigger("high")) d_ff_30 (
    .D(multiplexer_10_out[5]), .clk(not_12_out), .Q(d_ff_25_q[5]), .Qn(d_ff_30_qn));  // open: preset, reset
  D_Flip_Flop #(.trigger("high")) d_ff_31 (
    .D(multiplexer_10_out[6]), .clk(not_12_out), .Q(d_ff_25_q[6]), .Qn(d_ff_31_qn));  // open: preset, reset
  D_Flip_Flop #(.trigger("high")) d_ff_32 (
    .D(multiplexer_10_out[7]), .clk(not_12_out), .Q(d_ff_25_q[7]), .Qn(d_ff_32_qn));  // open: preset, reset
  not not_12 (not_12_out, nand_38_out);
  not not_13 (not_13_out, d_ff_23_q);
  not not_14 (not_14_out, d_ff_24_q);
  buf buffer_11 (C0o, d_ff_15_q);
  buf buffer_12 (C1o, d_ff_16_q);
  buf buffer_13 (C2o, d_ff_17_q);
  buf buffer_14 (C3o, d_ff_18_q);
  buf buffer_15 (C5o, d_ff_20_q);
  buf buffer_16 (C6o, d_ff_21_q);
  not not_15 (not_15_out, multiplexer_1_out[6]);
  not not_16 (not_16_out, multiplexer_1_out[7]);
  D_Flip_Flop d_ff_33 (
    .D(d_ff_33_qn), .clk(not_13_out), .Q(d_ff_33_q), .Qn(d_ff_33_qn), .reset(not_2_out));  // open: preset
  D_Flip_Flop d_ff_34 (
    .D(d_ff_34_qn), .clk(not_14_out), .Q(d_ff_34_q), .Qn(d_ff_34_qn), .reset(not_2_out));  // open: preset
  clk_div clk_div_1 (.VCLK(VCLK), .Reset(d_ff_6_qn), .PAL(not_3_out), .out_4(clk_div_1_out_4));
  not not_17 (not_17_out, d_ff_7_q[7]);
  Multiplexer multiplexer_1 (.in0(ZA_in[0]), .in1(VA_in[0]), .out(multiplexer_1_out[0]), .sel(nM3));
  Multiplexer multiplexer_2 (.in0(ZA_in[1]), .in1(VA_in[1]), .out(multiplexer_1_out[1]), .sel(nM3));
  Multiplexer multiplexer_3 (.in0(ZA_in[2]), .in1(VA_in[2]), .out(multiplexer_1_out[2]), .sel(nM3));
  Multiplexer multiplexer_4 (.in0(ZA_in[3]), .in1(VA_in[3]), .out(multiplexer_1_out[3]), .sel(nM3));
  Multiplexer multiplexer_5 (.in0(ZA_in[4]), .in1(VA_in[4]), .out(multiplexer_1_out[4]), .sel(nM3));
  Multiplexer multiplexer_6 (.in0(ZA_in[5]), .in1(VA_in[5]), .out(multiplexer_1_out[5]), .sel(nM3));
  Multiplexer multiplexer_7 (.in0(ZA_in[6]), .in1(VA_in[6]), .out(multiplexer_1_out[6]), .sel(nM3));
  Multiplexer multiplexer_8 (.in0(ZA_in[7]), .in1(1'b0), .out(multiplexer_1_out[7]), .sel(nM3));
  nor nor_5 (nor_5_out, multiplexer_1_out[4], multiplexer_1_out[5], multiplexer_1_out[6], multiplexer_1_out[7]);
  nand nand_2 (nand_2_out, 1'b1, multiplexer_1_out[1], multiplexer_1_out[2], multiplexer_1_out[3], multiplexer_1_out[4], multiplexer_1_out[5], not_15_out, not_16_out);
  nand nand_3 (nand_3_out, multiplexer_1_out[6], multiplexer_1_out[7]);
  nor nor_6 (nor_6_out, multiplexer_1_out[2], multiplexer_1_out[3], multiplexer_1_out[4]);
  and and_7 (and_7_out, multiplexer_1_out[2], multiplexer_1_out[3], multiplexer_1_out[4]);
  or or_7 (or_7_out, multiplexer_1_out[5], multiplexer_1_out[1]);
  not not_18 (bc1, nor_2_out);
  not not_19 (bc3, nor_3_out);
  not not_20 (bc5, nor_4_out);
  nor nor_7 (nor_7_out, not_17_out, buffer_1_out[6]);
  nor nor_8 (nor_8_out, nor_6_out, and_7_out);
  and and_8 (and_8_out, multiplexer_20_out, not_10_out, not_11_out);
  and and_9 (and_9_out, d_ff_23_q, buffer_9_out, not_11_out);
  and and_10 (and_10_out, d_ff_33_q, not_10_out, buffer_10_out);
  and and_11 (and_11_out, d_ff_46_q, buffer_9_out, buffer_10_out);
  and and_12 (and_12_out, d_ff_46_q, not_10_out, not_11_out);
  and and_13 (and_13_out, d_ff_24_q, buffer_9_out, not_11_out);
  and and_14 (and_14_out, d_ff_34_q, not_10_out, buffer_10_out);
  and and_15 (and_15_out, d_ff_47_q, buffer_9_out, buffer_10_out);
  not not_21 (not_21_out, d_ff_33_q);
  not not_22 (not_22_out, d_ff_34_q);
  Multiplexer multiplexer_9 (.in0(not_3_out), .in1(clk_div_1_out_4), .out(or_20_out[6]), .sel(TEST));
  not not_23 (not_23_out, d_ff_7_q[4]);
  not not_24 (not_24_out, d_ff_7_q[5]);
  not not_25 (not_25_out, multiplexer_1_out[0]);
  and and_16 (and_16_out, nM3, multiplexer_1_out[1]);
  and and_17 (xnor_1_out[2], nM3, multiplexer_1_out[2]);
  and and_18 (and_18_out, multiplexer_1_out[3], nM3);
  not not_26 (not_26_out, multiplexer_1_out[3]);
  nand nand_4 (nand_4_out, nM3, nor_5_out);
  not not_27 (not_27_out, multiplexer_1_out[3]);
  or or_8 (or_8_out, LWR, IO);
  Multiplexer #(.width(8)) multiplexer_10 (.in0(ZD_in), .in1(VD_in[7:0]), .out(multiplexer_10_out), .sel(nM3));
  Multiplexer #(.width(8)) multiplexer_11 (
    .in0(VD_in[7:0]), .in1(VD_in[15:8]), .out(multiplexer_11_out), .sel(and_6_out));
  Multiplexer multiplexer_12 (.in0(d_ff_25_qn), .in1(d_ff_38_q), .out(multiplexer_12_out), .sel(nand_5_out));
  Multiplexer multiplexer_13 (.in0(d_ff_26_qn), .in1(d_ff_39_q), .out(multiplexer_13_out), .sel(nand_5_out));
  Multiplexer multiplexer_14 (.in0(d_ff_27_qn), .in1(d_ff_40_q), .out(multiplexer_14_out), .sel(nand_5_out));
  Multiplexer multiplexer_15 (.in0(d_ff_28_qn), .in1(d_ff_41_q), .out(multiplexer_15_out), .sel(nand_5_out));
  Multiplexer multiplexer_16 (.in0(d_ff_29_qn), .in1(d_ff_42_q), .out(multiplexer_16_out), .sel(nand_5_out));
  Multiplexer multiplexer_17 (.in0(d_ff_30_qn), .in1(d_ff_43_q), .out(multiplexer_17_out), .sel(nand_5_out));
  Multiplexer multiplexer_18 (.in0(d_ff_31_qn), .in1(d_ff_44_q), .out(multiplexer_18_out), .sel(nand_5_out));
  Multiplexer multiplexer_19 (.in0(d_ff_32_qn), .in1(1'b0), .out(multiplexer_19_out), .sel(nand_5_out));
  or or_9 (or_9_out, 1'b0, or_14_out);
  D_Flip_Flop d_ff_35 (
    .D(d_ff_35_qn), .clk(not_21_out), .Q(d_ff_35_q), .Qn(d_ff_35_qn), .reset(not_2_out));  // open: preset
  D_Flip_Flop d_ff_36 (
    .D(d_ff_36_qn), .clk(not_22_out), .Q(d_ff_36_q), .Qn(d_ff_36_qn), .reset(not_2_out));  // open: preset
  Multiplexer multiplexer_20 (.in0(clk_div_1_out_4), .in1(VCLK), .out(multiplexer_20_out), .sel(TEST));
  not not_28 (not_28_out, d_ff_7_q[0]);
  not not_29 (not_29_out, d_ff_7_q[1]);
  not not_30 (not_30_out, d_ff_7_q[2]);
  not not_31 (not_31_out, d_ff_7_q[3]);
  and and_19 (and_19_out, not_23_out, not_52_out);
  or or_10 (or_10_out, not_24_out, d_ff_58_q[5]);
  not not_32 (not_32_out, d_ff_7_q[6]);
  xnor xnor_1 (xnor_1_out[0], multiplexer_1_out[0], nM3);
  nor nor_9 (nor_9_out, not_25_out, nM3);
  nor nor_10 (nor_10_out, not_26_out, nand_4_out, and_5_out);
  nor nor_11 (nor_11_out, not_27_out, or_8_out, nand_4_out);
  nor nor_12 (nor_12_out, multiplexer_1_out[3], or_8_out, nand_4_out);
  or or_11 (or_11_out, or_8_out, nM3, nand_2_out);
  or or_12 (or_12_out, nM3, nor_8_out, nand_3_out, or_7_out);
  D_Flip_Flop d_ff_37 (.D(multiplexer_12_out), .clk(or_9_out), .Q(d_ff_37_q), .reset(not_36_out));  // open: Qn, preset
  D_Flip_Flop d_ff_38 (.D(multiplexer_13_out), .clk(or_9_out), .Q(d_ff_38_q), .reset(not_36_out));  // open: Qn, preset
  D_Flip_Flop d_ff_39 (.D(multiplexer_14_out), .clk(or_9_out), .Q(d_ff_39_q), .reset(not_36_out));  // open: Qn, preset
  D_Flip_Flop d_ff_40 (.D(multiplexer_15_out), .clk(or_9_out), .Q(d_ff_40_q), .reset(not_36_out));  // open: Qn, preset
  D_Flip_Flop d_ff_41 (.D(multiplexer_16_out), .clk(or_9_out), .Q(d_ff_41_q), .reset(not_36_out));  // open: Qn, preset
  D_Flip_Flop d_ff_42 (.D(multiplexer_17_out), .clk(or_9_out), .Q(d_ff_42_q), .reset(not_36_out));  // open: Qn, preset
  D_Flip_Flop d_ff_43 (.D(multiplexer_18_out), .clk(or_9_out), .Q(d_ff_43_q), .reset(not_36_out));  // open: Qn, preset
  D_Flip_Flop d_ff_44 (.D(multiplexer_19_out), .clk(or_9_out), .Q(d_ff_44_q), .reset(not_36_out));  // open: Qn, preset
  or or_13 (or_13_out, and_8_out, and_9_out, and_10_out, and_11_out);
  or or_14 (or_14_out, and_12_out, and_13_out, and_14_out, and_15_out);
  buf buffer_17 (C0d, not_28_out);
  buf buffer_18 (out_48, not_29_out);
  buf buffer_19 (out_49, not_30_out);
  buf buffer_20 (out_50, not_31_out);
  buf buffer_21 (out_51, and_19_out);
  buf buffer_22 (out_52, or_10_out);
  buf buffer_23 (out_53, not_32_out);
  or or_15 (xnor_1_out[1], and_16_out, nor_9_out);
  Multiplexer #(.width(8)) multiplexer_21 (
    .in0(nand_60_out), .in1(nand_61_out), .out(multiplexer_21_out), .sel(and_18_out));
  not not_33 (not_33_out, d_ff_35_q);
  not not_34 (not_34_out, d_ff_36_q);
  Multiplexer multiplexer_22 (.in0(ZA_in[0]), .in1(ZA_in[1]), .out(multiplexer_22_out[0]), .sel(nM3));
  Multiplexer multiplexer_23 (.in0(ZA_in[1]), .in1(ZA_in[2]), .out(multiplexer_22_out[1]), .sel(nM3));
  Multiplexer multiplexer_24 (.in0(ZA_in[2]), .in1(ZA_in[3]), .out(multiplexer_22_out[2]), .sel(nM3));
  Multiplexer multiplexer_25 (.in0(ZA_in[3]), .in1(ZA_in[4]), .out(multiplexer_22_out[3]), .sel(nM3));
  Multiplexer multiplexer_26 (.in0(ZA_in[4]), .in1(ZA_in[5]), .out(multiplexer_22_out[4]), .sel(nM3));
  Multiplexer multiplexer_27 (.in0(ZA_in[5]), .in1(ZA_in[6]), .out(multiplexer_22_out[5]), .sel(nM3));
  Multiplexer multiplexer_28 (.in0(ZA_in[6]), .in1(ZA_in[7]), .out(multiplexer_22_out[6]), .sel(nM3));
  and and_20 (and_20_out, or_11_out, or_12_out);
  or or_16 (or_16_out, or_11_out, multiplexer_1_out[0]);
  or or_17 (or_17_out, or_11_out, not_25_out);
  not not_35 (not_35_out, d_ff_6_q);
  not not_36 (not_36_out, d_ff_58_q[4]);
  not not_37 (not_37_out, d_ff_37_q);
  D_Flip_Flop d_ff_45 (
    .D(nand_44_out), .clk(or_14_out), .Q(d_ff_45_q), .Qn(d_ff_45_qn), .reset(not_38_out));  // open: preset
  not not_38 (not_38_out, d_ff_6_q);
  or or_18 (or_18_out, d_ff_56_q, nor_16_out);
  or or_19 (or_19_out, nor_16_out, d_ff_50_qn);
  D_Flip_Flop d_ff_46 (
    .D(d_ff_46_qn), .clk(not_33_out), .Q(d_ff_46_q), .Qn(d_ff_46_qn), .reset(not_2_out));  // open: preset
  D_Flip_Flop d_ff_47 (
    .D(d_ff_47_qn), .clk(not_34_out), .Q(d_ff_47_q), .Qn(d_ff_47_qn), .reset(not_2_out));  // open: preset
  and and_21 (and_21_out, nand_4_out, and_20_out);
  D_Flip_Flop d_ff_48 (.D(VD_in[4]), .clk(or_16_out), .Q(d_ff_48_q), .reset(not_39_out));  // open: Qn, preset
  not not_39 (not_39_out, d_ff_6_q);
  D_Flip_Flop d_ff_49 (
    .D(multiplexer_10_out[7]), .clk(or_17_out), .Q(d_ff_49_q), .preset(not_35_out));  // open: Qn, reset
  Multiplexer #(.width(8)) multiplexer_29 (
    .in0(multiplexer_11_out), .in1(multiplexer_21_out), .out(multiplexer_29_out), .sel(nor_1_out));
  Multiplexer #(.width(8)) multiplexer_30 (
    .in0(ZD_in), .in1(multiplexer_21_out), .out(multiplexer_30_out), .sel(nor_1_out));
  Multiplexer multiplexer_31 (
    .in0(d_ff_48_q), .in1(multiplexer_30_out[0]), .out(multiplexer_31_out[8]), .sel(nor_1_out));
  nand nand_5 (nand_5_out, d_ff_66_q, 1'b1, d_ff_59_qn, d_ff_52_qn, d_ff_55_qn, d_ff_45_qn);
  nand nand_6 (nand_6_out, d_ff_59_q, d_ff_45_qn);
  nand nand_7 (nand_7_out, d_ff_59_qn, d_ff_66_q, d_ff_45_qn);
  nand nand_8 (nand_8_out, d_ff_59_q, d_ff_52_q, d_ff_45_q);
  nand nand_9 (nand_9_out, d_ff_45_q, d_ff_52_q);
  nand nand_10 (nand_10_out, d_ff_52_q, d_ff_59_q, d_ff_55_q);
  nand nand_11 (nand_11_out, d_ff_59_q, d_ff_55_q, d_ff_45_q);
  nand nand_12 (nand_12_out, d_ff_59_q, d_ff_45_q);
  nand nand_13 (nand_13_out, d_ff_59_q, d_ff_52_q);
  D_Flip_Flop d_ff_50 (.D(nand_14_out), .clk(or_13_out), .Qn(d_ff_50_qn), .reset(not_47_out));  // open: Q, preset
  nand nand_14 (nand_14_out, or_18_out, or_19_out);
  D_Flip_Flop d_ff_51 (
    .D(multiplexer_10_out[6]), .clk(or_17_out), .Q(d_ff_51_q), .preset(not_35_out));  // open: Qn, reset
  not not_40 (not_40_out, nand_5_out);
  and and_22 (and_22_out, not_37_out, nand_5_out);
  D_Flip_Flop d_ff_52 (
    .D(nand_45_out), .clk(or_14_out), .Q(d_ff_52_q), .Qn(d_ff_52_qn), .reset(not_38_out));  // open: preset
  nand nand_15 (nand_15_out, d_ff_52_qn, d_ff_45_qn, d_ff_55_q, d_ff_59_q);
  not not_41 (not_41_out, d_ff_56_q);
  not not_42 (not_42_out, TEST);
  assign VA_out = not_43_out ? multiplexer_22_out : 7'bz;  // Controlled_Buffer controlled_buffer_1
  not not_43 (not_43_out, undriven);
  assign bit_extender_1_out = {{7{xnor_1_out[2]}}, xnor_1_out[2]};  // Bit_Extender bit_extender_1
  assign bit_extender_2_out = {{7{xnor_1_out[1]}}, xnor_1_out[1]};  // Bit_Extender bit_extender_2
  assign bit_extender_3_out = {{7{xnor_1_out[0]}}, xnor_1_out[0]};  // Bit_Extender bit_extender_3
  not not_44 (not_44_out, multiplexer_1_out[0]);
  not not_45 (not_45_out, multiplexer_1_out[1]);
  not not_46 (not_46_out, multiplexer_1_out[2]);
  and and_23 (and_23_out, not_40_out, d_ff_58_q[0]);
  nor nor_13 (nor_13_out, d_ff_58_q[0], 1'b0);
  D_Flip_Flop d_ff_53 (.D(and_22_out), .clk(or_14_out), .Q(d_ff_53_q), .preset(not_36_out));  // open: Qn, reset
  not not_47 (not_47_out, d_ff_6_q);
  not not_48 (not_48_out, and_47_out);
  nor nor_14 (nor_14_out, and_48_out, nor_7_out);
  not not_49 (not_49_out, xnor_1_out[2]);
  not not_50 (not_50_out, xnor_1_out[1]);
  not not_51 (not_51_out, xnor_1_out[0]);
  D_Flip_Flop d_ff_54 (
    .D(multiplexer_10_out[5]), .clk(or_17_out), .Q(d_ff_54_q), .preset(not_35_out));  // open: Qn, reset
  nor nor_15 (nor_15_out, and_23_out, nor_13_out);
  not not_52 (not_52_out, d_ff_58_q[4]);
  D_Flip_Flop d_ff_55 (
    .D(nand_46_out), .clk(or_14_out), .Q(d_ff_55_q), .Qn(d_ff_55_qn), .reset(not_38_out));  // open: preset
  D_Flip_Flop d_ff_56 (
    .D(nand_56_out), .clk(or_13_out), .Q(d_ff_56_q), .Qn(d_ff_56_qn), .preset(not_47_out));  // open: reset
  nor nor_16 (nor_16_out, d_ff_50_qn, not_48_out, d_ff_71_q);
  nand nand_16 (nand_16_out, d_ff_60_q, d_ff_64_q);
  assign bit_extender_4_out = {{7{not_49_out}}, not_49_out};  // Bit_Extender bit_extender_4
  assign bit_extender_5_out = {{7{not_50_out}}, not_50_out};  // Bit_Extender bit_extender_5
  assign bit_extender_6_out = {{7{not_51_out}}, not_51_out};  // Bit_Extender bit_extender_6
  // NAND_Gate nand_17 has open pins: in0=nor_12_out, in1=not_44_out, in2=not_45_out, in3=not_46_out, out=open
  nand nand_18 (nand_18_out, nor_12_out, multiplexer_1_out[0], not_45_out, not_46_out);
  nand nand_19 (nand_19_out, nor_12_out, not_44_out, multiplexer_1_out[1], not_46_out);
  nand nand_20 (nand_20_out, nor_12_out, multiplexer_1_out[0], multiplexer_1_out[1], not_46_out);
  nand nand_21 (nand_21_out, nor_12_out, not_44_out, not_45_out, multiplexer_1_out[2]);
  nand nand_22 (nand_22_out, nor_12_out, multiplexer_1_out[0], not_45_out, multiplexer_1_out[2]);
  nand nand_23 (nand_23_out, nor_12_out, not_44_out, multiplexer_1_out[1], multiplexer_1_out[2]);
  nand nand_24 (nand_24_out, nor_12_out, multiplexer_1_out[0], multiplexer_1_out[1], multiplexer_1_out[2]);
  nand nand_25 (nand_25_out, nor_10_out, not_44_out, not_45_out, not_46_out);
  // NAND_Gate nand_26 has open pins: in0=nor_10_out, in1=multiplexer_1_out[0], in2=not_45_out, in3=not_46_out, out=open
  // NAND_Gate nand_27 has open pins: in0=nor_10_out, in1=not_44_out, in2=multiplexer_1_out[1], in3=not_46_out, out=open
  nand nand_28 (nand_28_out, nor_10_out, multiplexer_1_out[0], multiplexer_1_out[1], not_46_out);
  // NAND_Gate nand_29 has open pins: in0=nor_10_out, in1=not_44_out, in2=not_45_out, in3=multiplexer_1_out[2], out=open
  // NAND_Gate nand_30 has open pins: in0=nor_10_out, in1=multiplexer_1_out[0], in2=not_45_out, in3=multiplexer_1_out[2], out=open
  nand nand_31 (nand_31_out, nor_10_out, not_44_out, multiplexer_1_out[1], multiplexer_1_out[2]);
  // NAND_Gate nand_32 has open pins: in0=nor_10_out, in1=multiplexer_1_out[0], in2=multiplexer_1_out[1], in3=multiplexer_1_out[2], out=open
  // NAND_Gate nand_33 has open pins: in0=nor_11_out, in1=not_44_out, in2=not_45_out, in3=not_46_out, out=open
  nand nand_34 (nand_34_out, nor_11_out, multiplexer_1_out[0], not_45_out, not_46_out);
  nand nand_35 (nand_35_out, nor_11_out, not_44_out, multiplexer_1_out[1], not_46_out);
  // NAND_Gate nand_36 has open pins: in0=nor_11_out, in1=multiplexer_1_out[0], in2=multiplexer_1_out[1], in3=not_46_out, out=open
  nand nand_37 (nand_37_out, nor_11_out, not_44_out, not_45_out, multiplexer_1_out[2]);
  nand nand_38 (nand_38_out, nor_11_out, multiplexer_1_out[0], not_45_out, multiplexer_1_out[2]);
  // NAND_Gate nand_39 has open pins: in0=nor_11_out, in1=not_44_out, in2=multiplexer_1_out[1], in3=multiplexer_1_out[2], out=open
  nand nand_40 (nand_40_out, nor_11_out, multiplexer_1_out[0], multiplexer_1_out[1], multiplexer_1_out[2]);
  not not_53 (not_53_out, or_14_out);
  and and_24 (and_24_out, d_ff_53_q, d_ff_58_q[4]);
  and and_25 (and_25_out, not_52_out, d_ff_19_q);
  not not_54 (not_54_out, nor_16_out);
  nand nand_41 (nand_41_out, d_ff_60_q, d_ff_67_qn);
  nand nand_42 (nand_42_out, d_ff_67_qn, d_ff_64_q);
  nand nand_43 (nand_43_out, d_ff_64_qn, d_ff_67_q, d_ff_60_qn);
  or or_20 (or_20_out[0], not_42_out, UART_A_clk1);
  and and_26 (or_20_out[1], TEST, UART_A_clk2);
  and and_27 (or_20_out[2], TEST, UART_B_clk1);
  and and_28 (or_20_out[3], TEST, UART_B_clk2);
  and and_29 (or_20_out[4], TEST, or_13_out);
  Multiplexer multiplexer_32 (.in0(DISK), .in1(or_14_out), .out(or_20_out[5]), .sel(TEST));
  D_Flip_Flop d_ff_57 (
    .D(multiplexer_10_out[4]), .clk(or_17_out), .Q(d_ff_57_q), .preset(not_35_out));  // open: Qn, reset
  not not_55 (not_55_out, nand_38_out);
  D_Flip_Flop d_ff_58 (
    .D(nor_15_out), .clk(not_56_out), .Q(d_ff_58_q[0]), .Qn(d_ff_58_qn), .preset(not_55_out),
    .reset(not_57_out));
  not not_56 (not_56_out, not_53_out);
  not not_57 (not_57_out, d_ff_6_q);
  or or_21 (or_21_out, and_24_out, and_25_out);
  D_Flip_Flop d_ff_59 (
    .D(nand_47_out), .clk(or_14_out), .Q(d_ff_59_q), .Qn(d_ff_59_qn), .reset(not_38_out));  // open: preset
  nand nand_44 (nand_44_out, nand_6_out, nand_7_out, nand_8_out);
  nand nand_45 (nand_45_out, nand_7_out, nand_9_out, nand_15_out);
  nand nand_46 (nand_46_out, nand_7_out, nand_8_out, nand_10_out, nand_11_out);
  nand nand_47 (nand_47_out, nand_9_out, nand_15_out, nand_12_out, nand_13_out);
  nand nand_48 (nand_48_out, d_ff_59_q, d_ff_55_qn, d_ff_52_qn, d_ff_45_qn);
  D_Flip_Flop d_ff_60 (
    .D(nand_49_out), .clk(or_13_out), .Q(d_ff_60_q), .Qn(d_ff_60_qn), .preset(not_47_out));  // open: reset
  nand nand_49 (nand_49_out, not_54_out, nand_16_out, nand_43_out, nand_41_out);
  nand nand_50 (nand_50_out, nand_42_out, not_54_out, nand_51_out);
  nor nor_17 (nor_17_out, d_ff_67_q, nor_16_out);
  nand nand_51 (nand_51_out, d_ff_67_q, d_ff_64_qn);
  nand nand_52 (nand_52_out, d_ff_64_qn, d_ff_67_q, d_ff_60_qn, not_41_out);
  nand nand_53 (nand_53_out, d_ff_56_q, d_ff_60_q);
  nand nand_54 (nand_54_out, d_ff_56_q, d_ff_67_qn);
  nand nand_55 (nand_55_out, d_ff_56_q, d_ff_64_q);
  D_Flip_Flop d_ff_61 (
    .D(multiplexer_10_out[3]), .clk(or_17_out), .Q(d_ff_61_q), .preset(not_35_out));  // open: Qn, reset
  not not_58 (not_58_out, d_ff_58_qn);
  D_Flip_Flop d_ff_62 (.D(1'b0), .clk(d_ff_63_q), .Q(d_ff_62_q), .preset(not_58_out), .reset(not_57_out));  // open: Qn
  buf buffer_24 (C4o, or_21_out);
  D_Flip_Flop d_ff_63 (.D(nand_48_out), .clk(or_14_out), .Q(d_ff_63_q), .preset(not_38_out));  // open: Qn, reset
  D_Flip_Flop d_ff_64 (
    .D(nand_50_out), .clk(or_13_out), .Q(d_ff_64_q), .Qn(d_ff_64_qn), .preset(not_47_out));  // open: reset
  nand nand_56 (nand_56_out, nand_52_out, 1'b1, not_54_out, nand_53_out, nand_54_out, nand_55_out);
  D_Flip_Flop d_ff_65 (
    .D(multiplexer_10_out[2]), .clk(or_17_out), .Q(d_ff_65_q), .preset(not_35_out));  // open: Qn, reset
  D_Flip_Flop d_ff_66 (.D(d_ff_62_q), .clk(or_13_out), .Q(d_ff_66_q));  // open: Qn, preset, reset
  D_Flip_Flop d_ff_67 (
    .D(nor_17_out), .clk(or_13_out), .Q(d_ff_67_q), .Qn(d_ff_67_qn), .reset(not_47_out));  // open: preset
  assign and_30_out = bit_extender_4_out & bit_extender_5_out & bit_extender_6_out & {JAP, or_20_out};  // AND_Gate and_30, 8 bits wide
  assign and_31_out = bit_extender_4_out & bit_extender_5_out & bit_extender_3_out & {multiplexer_41_out, A3i, A2i, A1i, A0i};  // AND_Gate and_31, 8 bits wide
  assign and_32_out = bit_extender_4_out & bit_extender_2_out & bit_extender_6_out & multiplexer_45_out;  // AND_Gate and_32, 8 bits wide
  assign and_33_out = bit_extender_4_out & bit_extender_2_out & bit_extender_3_out & buffer_1_out;  // AND_Gate and_33, 8 bits wide
  assign and_34_out = bit_extender_1_out & bit_extender_5_out & bit_extender_6_out;  // AND_Gate and_34, 8 bits wide
  assign and_35_out = bit_extender_1_out & bit_extender_5_out & bit_extender_3_out;  // AND_Gate and_35, 8 bits wide
  assign and_36_out = bit_extender_1_out & bit_extender_2_out & bit_extender_6_out & d_ff_7_q;  // AND_Gate and_36, 8 bits wide
  assign and_37_out = bit_extender_1_out & bit_extender_2_out & bit_extender_3_out;  // AND_Gate and_37, 8 bits wide
  assign and_38_out = bit_extender_4_out & bit_extender_5_out & bit_extender_6_out;  // AND_Gate and_38, 8 bits wide
  assign and_39_out = bit_extender_4_out & bit_extender_5_out & bit_extender_3_out;  // AND_Gate and_39, 8 bits wide
  assign and_40_out = bit_extender_4_out & bit_extender_2_out & bit_extender_6_out;  // AND_Gate and_40, 8 bits wide
  assign and_41_out = bit_extender_4_out & bit_extender_2_out & bit_extender_3_out;  // AND_Gate and_41, 8 bits wide
  assign and_42_out = bit_extender_1_out & bit_extender_5_out & bit_extender_6_out;  // AND_Gate and_42, 8 bits wide
  assign and_43_out = bit_extender_1_out & bit_extender_5_out & bit_extender_3_out & d_ff_25_q;  // AND_Gate and_43, 8 bits wide
  assign and_44_out = bit_extender_1_out & bit_extender_2_out & bit_extender_6_out & d_ff_92_q;  // AND_Gate and_44, 8 bits wide
  assign and_45_out = bit_extender_1_out & bit_extender_2_out & bit_extender_3_out & d_ff_58_q;  // AND_Gate and_45, 8 bits wide
  D_Flip_Flop d_ff_68 (
    .D(multiplexer_10_out[1]), .clk(or_17_out), .Q(d_ff_68_q), .preset(not_35_out));  // open: Qn, reset
  not not_59 (not_59_out, d_ff_58_q[5]);
  not not_60 (not_60_out, and_49_out);
  not not_61 (not_61_out, 1'b1);
  and and_46 (and_46_out, d_ff_71_q, 1'b1);
  D_Flip_Flop d_ff_69 (.D(and_46_out), .clk(d_ff_56_qn), .Q(d_ff_69_q), .reset(not_62_out));  // open: Qn, preset
  assign nor_18_out = ~(and_30_out | and_31_out);  // NOR_Gate nor_18, 8 bits wide
  assign nor_19_out = ~(and_32_out | and_33_out);  // NOR_Gate nor_19, 8 bits wide
  assign nor_20_out = ~(and_34_out | and_35_out);  // NOR_Gate nor_20, 8 bits wide
  assign nor_21_out = ~(and_36_out | and_37_out);  // NOR_Gate nor_21, 8 bits wide
  assign nor_22_out = ~(and_38_out | and_39_out);  // NOR_Gate nor_22, 8 bits wide
  assign nor_23_out = ~(and_40_out | and_41_out);  // NOR_Gate nor_23, 8 bits wide
  assign nor_24_out = ~(and_42_out | and_43_out);  // NOR_Gate nor_24, 8 bits wide
  assign nor_25_out = ~(and_44_out | and_45_out);  // NOR_Gate nor_25, 8 bits wide
  D_Flip_Flop d_ff_70 (
    .D(multiplexer_10_out[0]), .clk(or_17_out), .Q(d_ff_70_q), .preset(not_35_out));  // open: Qn, reset
  D_Flip_Flop d_ff_71 (
    .D(buffer_1_out[5]), .clk(or_13_out), .Q(d_ff_71_q), .Qn(d_ff_71_qn), .preset(not_59_out));  // open: reset
  D_Flip_Flop d_ff_72 (.D(1'b1), .clk(or_26_out), .Q(d_ff_58_q[1]), .reset(not_60_out));  // open: Qn, preset
  D_Flip_Flop d_ff_73 (
    .D(xor_delay_6x_1_out_2), .clk(or_26_out), .Q(d_ff_92_q[7]), .reset(not_61_out));  // open: Qn, preset
  D_Flip_Flop d_ff_74 (.D(d_ff_69_q), .clk(d_ff_56_qn), .Q(d_ff_74_q), .reset(not_62_out));  // open: Qn, preset
  not not_62 (not_62_out, d_ff_58_q[5]);
  nand nand_57 (nand_57_out, d_ff_80_q, d_ff_91_q);
  D_Flip_Flop d_ff_75 (.D(d_ff_71_qn), .clk(or_26_out), .Q(d_ff_58_q[2]), .reset(not_60_out));  // open: Qn, preset
  xor_delay_6x xor_delay_6x_1 (.in_1(d_ff_69_q), .out_2(xor_delay_6x_1_out_2));
  nand nand_58 (nand_58_out, d_ff_80_qn, d_ff_91_qn, d_ff_50_qn, not_63_out);
  nand nand_59 (nand_59_out, d_ff_80_q, d_ff_83_q, d_ff_88_qn, d_ff_91_qn);
  assign nand_60_out = ~(nor_18_out & nor_19_out & nor_20_out & nor_21_out);  // NAND_Gate nand_60, 8 bits wide
  assign nand_61_out = ~(nor_22_out & nor_23_out & nor_24_out & nor_25_out);  // NAND_Gate nand_61, 8 bits wide
  not not_63 (not_63_out, d_ff_71_q);
  D_Flip_Flop d_ff_76 (
    .D(xor_delay_6x_2_out_2), .clk(or_26_out), .Q(d_ff_92_q[6]), .reset(not_61_out));  // open: Qn, preset
  xor_delay_6x xor_delay_6x_2 (.in_1(d_ff_74_q), .out_2(xor_delay_6x_2_out_2));
  D_Flip_Flop d_ff_77 (.D(d_ff_74_q), .clk(d_ff_56_qn), .Q(d_ff_77_q), .reset(not_62_out));  // open: Qn, preset
  not not_64 (not_64_out, d_ff_6_q);
  nand nand_62 (nand_62_out, nand_58_out, nand_59_out, nand_63_out, nand_57_out);
  and and_47 (and_47_out, d_ff_80_qn, d_ff_91_qn);
  nand nand_63 (nand_63_out, d_ff_88_q, d_ff_91_qn, d_ff_80_q);
  nand nand_64 (nand_64_out, d_ff_80_q, d_ff_91_qn, d_ff_83_qn, d_ff_88_qn);
  nand nand_65 (nand_65_out, d_ff_80_q, d_ff_88_q, d_ff_91_q);
  nand nand_66 (nand_66_out, d_ff_88_q, d_ff_80_q, d_ff_83_q);
  nand nand_67 (nand_67_out, d_ff_91_q, d_ff_80_q, d_ff_83_q);
  and and_48 (and_48_out, d_ff_58_q[1], d_ff_58_q[3]);
  D_Flip_Flop d_ff_78 (
    .D(xor_delay_6x_3_out_2), .clk(or_26_out), .Q(d_ff_92_q[5]), .reset(not_61_out));  // open: Qn, preset
  xor_delay_6x xor_delay_6x_3 (.in_1(d_ff_77_q), .out_2(xor_delay_6x_3_out_2));
  D_Flip_Flop d_ff_79 (.D(d_ff_77_q), .clk(d_ff_56_qn), .Q(d_ff_79_q), .reset(not_62_out));  // open: Qn, preset
  D_Flip_Flop d_ff_80 (
    .D(nand_62_out), .clk(d_ff_56_qn), .Q(d_ff_80_q), .Qn(d_ff_80_qn), .reset(not_64_out));  // open: preset
  nand nand_68 (nand_68_out, nand_59_out, nand_58_out, nand_63_out, nand_64_out);
  nand nand_69 (nand_69_out, nand_64_out, nand_58_out, nand_59_out, nand_65_out);
  nand nand_70 (nand_70_out, nand_64_out, nand_58_out, nand_66_out, nand_67_out);
  D_Flip_Flop d_ff_81 (
    .D(xor_delay_6x_4_out_2), .clk(or_26_out), .Q(d_ff_92_q[4]), .reset(not_61_out));  // open: Qn, preset
  xor_delay_6x xor_delay_6x_4 (.in_1(d_ff_79_q), .out_2(xor_delay_6x_4_out_2));
  D_Flip_Flop d_ff_82 (.D(d_ff_79_q), .clk(d_ff_56_qn), .Q(d_ff_82_q), .reset(not_65_out));  // open: Qn, preset
  D_Flip_Flop d_ff_83 (
    .D(nand_70_out), .clk(d_ff_56_qn), .Q(d_ff_83_q), .Qn(d_ff_83_qn), .reset(not_64_out));  // open: preset
  Multiplexer multiplexer_33 (.in0(d_ff_70_q), .in1(undriven_2), .out(A5d), .sel(nM3));
  Multiplexer multiplexer_34 (.in0(d_ff_68_q), .in1(undriven_3), .out(A6d), .sel(nM3));
  Multiplexer multiplexer_35 (.in0(d_ff_65_q), .in1(undriven_4), .out(B5d), .sel(nM3));
  Multiplexer multiplexer_36 (.in0(d_ff_61_q), .in1(undriven_5), .out(B6d), .sel(nM3));
  Multiplexer multiplexer_37 (.in0(d_ff_57_q), .in1(undriven_6), .out(A5o), .sel(nM3));
  Multiplexer multiplexer_38 (.in0(d_ff_54_q), .in1(undriven_7), .out(A6o), .sel(nM3));
  Multiplexer multiplexer_39 (.in0(d_ff_51_q), .in1(undriven_8), .out(B5o), .sel(nM3));
  Multiplexer multiplexer_40 (.in0(d_ff_49_q), .in1(undriven_9), .out(B6o), .sel(nM3));
  D_Flip_Flop d_ff_84 (
    .D(xor_delay_6x_5_out_2), .clk(or_26_out), .Q(d_ff_92_q[3]), .reset(not_61_out));  // open: Qn, preset
  D_Flip_Flop d_ff_85 (.D(d_ff_82_q), .clk(d_ff_56_qn), .Q(d_ff_85_q), .reset(not_65_out));  // open: Qn, preset
  not not_65 (not_65_out, d_ff_58_q[5]);
  D_Flip_Flop d_ff_86 (
    .D(xor_delay_6x_6_out_2), .clk(or_26_out), .Q(d_ff_92_q[2]), .reset(not_61_out));  // open: Qn, preset
  xor_delay_6x xor_delay_6x_5 (.in_1(d_ff_82_q), .out_2(xor_delay_6x_5_out_2));
  D_Flip_Flop d_ff_87 (.D(d_ff_85_q), .clk(d_ff_56_qn), .Q(d_ff_87_q), .reset(not_65_out));  // open: Qn, preset
  D_Flip_Flop d_ff_88 (
    .D(nand_69_out), .clk(d_ff_56_qn), .Q(d_ff_88_q), .Qn(d_ff_88_qn), .reset(not_64_out));  // open: preset
  xor_delay_6x xor_delay_6x_6 (.in_1(d_ff_85_q), .out_2(xor_delay_6x_6_out_2));
  or or_22 (or_22_out, JAP, A5d);
  or or_23 (or_23_out, JAP, A6d);
  or or_24 (or_24_out, JAP, B5d);
  or or_25 (or_25_out, JAP, B6d);
  not not_66 (not_66_out, B6d);
  not not_67 (not_67_out, A6d);
  D_Flip_Flop d_ff_89 (
    .D(xor_delay_6x_7_out_2), .clk(or_26_out), .Q(d_ff_92_q[1]), .reset(not_61_out));  // open: Qn, preset
  xor_delay_6x xor_delay_6x_7 (.in_1(d_ff_87_q), .out_2(xor_delay_6x_7_out_2));
  D_Flip_Flop d_ff_90 (.D(d_ff_87_q), .clk(d_ff_56_qn), .Q(d_ff_90_q), .reset(not_65_out));  // open: Qn, preset
  D_Flip_Flop d_ff_91 (
    .D(nand_68_out), .clk(d_ff_56_qn), .Q(d_ff_91_q), .Qn(d_ff_91_qn), .reset(not_64_out));  // open: preset
  nor nor_26 (nor_26_out, not_66_out, B6i);
  nor nor_27 (nor_27_out, not_67_out, A6i);
  D_Flip_Flop d_ff_92 (
    .D(xor_delay_6x_8_out_2), .clk(or_26_out), .Q(d_ff_92_q[0]), .reset(not_61_out));  // open: Qn, preset
  xor_delay_6x xor_delay_6x_8 (.in_1(d_ff_90_q), .out_2(xor_delay_6x_8_out_2));
  and and_49 (and_49_out, nand_31_out, d_ff_6_q);
  and and_50 (and_50_out, or_22_out, A5i);
  and and_51 (and_51_out, or_23_out, A6i);
  and and_52 (and_52_out, or_24_out, B5i);
  and and_53 (and_53_out, or_25_out, B6i);
  D_Flip_Flop d_ff_93 (.D(nand_64_out), .clk(d_ff_56_qn), .Q(d_ff_93_q), .preset(not_64_out));  // open: Qn, reset
  nor nor_28 (nor_28_out, nor_26_out, nor_27_out);
  Multiplexer multiplexer_41 (.in0(A4i), .in1(A4i), .out(multiplexer_41_out[4]), .sel(nM3));
  not not_68 (not_68_out, nM3);
  or or_26 (or_26_out, d_ff_93_q, d_ff_56_qn);
  nor nor_29 (nor_29_out, nor_28_out, nM3);
  nor nor_30 (nor_30_out, not_68_out, nor_14_out);
  Multiplexer multiplexer_42 (.in0(and_50_out), .in1(A5i), .out(multiplexer_41_out[5]), .sel(nM3));
  Multiplexer multiplexer_43 (.in0(B0i), .in1(A6i), .out(multiplexer_41_out[6]), .sel(nM3));
  Multiplexer multiplexer_44 (.in0(B1i), .in1(P3b7), .out(multiplexer_41_out[7]), .sel(nM3));
  nor nor_31 (HL, nor_29_out, nor_30_out);
  Multiplexer multiplexer_45 (.in0(B2i), .in1(B0i), .out(multiplexer_45_out[0]), .sel(nM3));
  Multiplexer multiplexer_46 (.in0(B3i), .in1(B1i), .out(multiplexer_45_out[1]), .sel(nM3));
  Multiplexer multiplexer_47 (.in0(B4i), .in1(B2i), .out(multiplexer_45_out[2]), .sel(nM3));
  Multiplexer multiplexer_48 (.in0(and_52_out), .in1(B3i), .out(multiplexer_45_out[3]), .sel(nM3));
  Multiplexer multiplexer_49 (.in0(1'b1), .in1(B4i), .out(multiplexer_45_out[4]), .sel(nM3));
  Multiplexer multiplexer_50 (.in0(1'b0), .in1(B5i), .out(multiplexer_45_out[5]), .sel(nM3));
  Multiplexer multiplexer_51 (.in0(and_51_out), .in1(B6i), .out(multiplexer_45_out[6]), .sel(nM3));
  Multiplexer multiplexer_52 (.in0(and_53_out), .in1(P5b7), .out(multiplexer_45_out[7]), .sel(nM3));
endmodule

module cnt_bit (
  input  cin,
  input  val,
  input  load,
  input  clk,
  input  res,
  output cout,
  output q,
  output nq
);

  wire multiplexer_1_out, not_1_out, xor_1_out;

  and and_1 (cout, cin, q);
  xor xor_1 (xor_1_out, cin, q);
  not not_1 (not_1_out, res);
  Multiplexer multiplexer_1 (.in0(val), .in1(xor_1_out), .out(multiplexer_1_out), .sel(load));
  D_Flip_Flop d_ff_1 (.D(multiplexer_1_out), .clk(clk), .Q(q), .Qn(nq), .reset(not_1_out));  // open: preset
endmodule

module clk_div (
  input  VCLK,
  input  Reset,
  input  PAL,
  output out_4
);

  wire and_1_out, and_2_out, and_3_out, and_4_out, cnt_bit_1_cout, cnt_bit_1_nq, cnt_bit_2_cout,
       cnt_bit_2_nq, cnt_bit_3_cout, cnt_bit_3_nq, cnt_bit_4_cout, cnt_bit_4_nq, cnt_bit_5_cout,
       cnt_bit_5_nq, cnt_bit_6_cout, cnt_bit_6_nq, cnt_bit_7_nq, cnt_bit_8_nq, nor_1_out, nor_2_out,
       nor_3_out;

  and and_1 (and_1_out, nor_3_out, 1'b1, and_4_out);
  and and_2 (and_2_out, nor_3_out, 1'b1, 1'b1);
  cnt_bit cnt_bit_1 (
    .cin(and_1_out), .val(1'b1), .load(nor_3_out), .clk(VCLK), .res(1'b1), .cout(cnt_bit_1_cout),
    .nq(cnt_bit_1_nq));  // open: q
  cnt_bit cnt_bit_2 (
    .cin(and_2_out), .val(PAL), .load(nor_3_out), .clk(VCLK), .res(1'b1), .cout(cnt_bit_2_cout),
    .nq(cnt_bit_2_nq));  // open: q
  nor nor_1 (nor_1_out, cnt_bit_1_nq, cnt_bit_3_nq, cnt_bit_5_nq, cnt_bit_7_nq);
  nor nor_2 (nor_2_out, cnt_bit_2_nq, cnt_bit_8_nq, cnt_bit_6_nq, cnt_bit_4_nq);
  cnt_bit cnt_bit_3 (
    .cin(cnt_bit_1_cout), .val(1'b0), .load(nor_3_out), .clk(VCLK), .res(1'b1), .cout(cnt_bit_3_cout),
    .nq(cnt_bit_3_nq));  // open: q
  and and_3 (and_3_out, nor_1_out, and_4_out);
  cnt_bit cnt_bit_4 (
    .cin(cnt_bit_2_cout), .val(1'b0), .load(nor_3_out), .clk(VCLK), .res(1'b1), .cout(cnt_bit_4_cout),
    .nq(cnt_bit_4_nq));  // open: q
  and and_4 (and_4_out, nor_2_out, 1'b1);
  nor nor_3 (nor_3_out, Reset, and_3_out);
  cnt_bit cnt_bit_5 (
    .cin(cnt_bit_3_cout), .val(1'b0), .load(nor_3_out), .clk(VCLK), .res(1'b1), .cout(cnt_bit_5_cout),
    .q(out_4), .nq(cnt_bit_5_nq));
  cnt_bit cnt_bit_6 (
    .cin(cnt_bit_4_cout), .val(1'b1), .load(nor_3_out), .clk(VCLK), .res(1'b1), .cout(cnt_bit_6_cout),
    .nq(cnt_bit_6_nq));  // open: q
  cnt_bit cnt_bit_7 (
    .cin(cnt_bit_5_cout), .val(1'b1), .load(nor_3_out), .clk(VCLK), .res(1'b1), .nq(cnt_bit_7_nq));  // open: cout, q
  cnt_bit cnt_bit_8 (
    .cin(cnt_bit_6_cout), .val(1'b1), .load(nor_3_out), .clk(VCLK), .res(1'b1), .nq(cnt_bit_8_nq));  // open: cout, q
endmodule

module xor_delay_6x (
  input  in_1,
  output out_2
);

  wire xor_1_out, xor_2_out, xor_3_out, xor_4_out, xor_5_out;

  xor xor_1 (xor_1_out, in_1, 1'b0);
  xor xor_2 (xor_2_out, xor_1_out, 1'b0);
  xor xor_3 (xor_3_out, xor_2_out, 1'b0);
  xor xor_4 (xor_4_out, xor_3_out, 1'b0);
  xor xor_5 (xor_5_out, xor_4_out, 1'b0);
  xor xor_6 (out_2, xor_5_out, 1'b0);
endmodule
