// Logisim project ym2610.circ as structural Verilog: 5 circuits, main circuit main
module main (
);

  write_data write_data_1 ();  // open: data_in, bank, write, oe, valout, nvalout
endmodule

module sr_bit (
  input  val,
  input  clk1,
  input  clk2,
  output valout,
  output nvalout
);

  wire d_ff_1_q;

  D_Flip_Flop #(.trigger("high")) d_ff_1 (.D(val), .clk(clk1), .Q(d_ff_1_q));  // open: Qn, preset, reset
  D_Flip_Flop #(.trigger("high")) d_ff_2 (.D(d_ff_1_q), .clk(clk2), .Q(valout), .Qn(nvalout));  // open: preset, reset
endmodule

module reg_bit_1 (
  input  oe,
  input  val,
  input  write,
  output nvalout,
  output valout
);

  wire d_ff_1_q, nor_1_out, nor_2_out;

  D_Flip_Flop #(.trigger("high")) d_ff_1 (.D(val), .clk(write), .Q(d_ff_1_q));  // open: Qn, preset, reset
  nor nor_1 (nor_1_out, oe, d_ff_1_q);
  nor nor_2 (nor_2_out, oe, nor_1_out);
  assign nvalout = nor_1_out ? 1'b1 : 1'bz;  // Controlled_Buffer controlled_buffer_1
  assign nvalout = nor_2_out ? 1'b0 : 1'bz;  // Controlled_Buffer controlled_buffer_2
  assign valout = nor_2_out ? 1'b1 : 1'bz;  // Controlled_Buffer controlled_buffer_3
  assign valout = nor_1_out ? 1'b0 : 1'bz;  // Controlled_Buffer controlled_buffer_4

  // Notes on the sheet:
  //   dynamic latch!!!
endmodule

module read_bus_1 (
  input  val,
  input  enable,
  output valout
);

  wire nor_1_out, nor_2_out;

  nor nor_1 (nor_1_out, val, enable);
  nor nor_2 (nor_2_out, nor_1_out, enable);
  assign valout = nor_2_out ? 1'b1 : 1'bz;  // Controlled_Buffer controlled_buffer_1
  assign valout = nor_1_out ? 1'b0 : 1'bz;  // Controlled_Buffer controlled_buffer_2
endmodule

module write_data (
  input  [7:0] data_in,
  input  bank,
  input  write,
  input  oe,
  output [8:0] valout,
  output [8:0] nvalout
);

  reg_bit_1 reg_bit_1_1 (.oe(oe), .val(data_in[0]), .write(write), .nvalout(nvalout[0]), .valout(valout[0]));
  reg_bit_1 reg_bit_1_2 (.oe(oe), .val(data_in[1]), .write(write), .nvalout(nvalout[1]), .valout(valout[1]));
  reg_bit_1 reg_bit_1_3 (.oe(oe), .val(data_in[2]), .write(write), .nvalout(nvalout[2]), .valout(valout[2]));
  reg_bit_1 reg_bit_1_4 (.oe(oe), .val(data_in[3]), .write(write), .nvalout(nvalout[3]), .valout(valout[3]));
  reg_bit_1 reg_bit_1_5 (.oe(oe), .val(data_in[4]), .write(write), .nvalout(nvalout[4]), .valout(valout[4]));
  reg_bit_1 reg_bit_1_6 (.oe(oe), .val(data_in[5]), .write(write), .nvalout(nvalout[5]), .valout(valout[5]));
  reg_bit_1 reg_bit_1_7 (.oe(oe), .val(data_in[6]), .write(write), .nvalout(nvalout[6]), .valout(valout[6]));
  reg_bit_1 reg_bit_1_8 (.oe(oe), .val(data_in[7]), .write(write), .nvalout(nvalout[7]), .valout(valout[7]));
  reg_bit_1 reg_bit_1_9 (.oe(oe), .val(bank), .write(write), .nvalout(nvalout[8]), .valout(valout[8]));
endmodule
