// Logisim project SEGA 315-5309.circ as structural Verilog: 8 circuits, main circuit main
module main (
  input  VCLK,
  input  nM3,
  input  nSRES,
  input  TEST,
  input  NTSC,
  input  nVTOZ,
  input  nZTOV,
  input  nLWR,
  input  nIO,
  input  nCAS0,
  input  VA1,
  input  VA2,
  input  VA3,
  input  VA4,
  input  VA5,
  input  VA6,
  input  VA7,
  input  ZA0,
  input  ZA1,
  input  ZA2,
  input  ZA3,
  input  ZA4,
  input  ZA5,
  input  ZA6,
  input  ZA7,
  input  VD0_i,
  input  VD1_i,
  input  VD2_i,
  input  VD3_i,
  input  VD4_i,
  input  VD5_i,
  input  VD6_i,
  input  VD7_i,
  input  VD8_i,
  input  VD9_i,
  input  VD10_i,
  input  VD11_i,
  input  VD12_i,
  input  VD13_i,
  input  VD14_i,
  input  VD15_i,
  input  ZD0_i,
  input  ZD1_i,
  input  ZD2_i,
  input  ZD3_i,
  input  ZD4_i,
  input  ZD5_i,
  input  ZD6_i,
  input  ZD7_i,
  input  PA0_i,
  input  PA1_i,
  input  PA2_i,
  input  PA3_i,
  input  PA4_i,
  input  PA5_i,
  input  PA6_i,
  input  PB0_i,
  input  PB1_i,
  input  PB2_i,
  input  PB3_i,
  input  PB4_i,
  input  PB5_i,
  input  PB6_i,
  input  PC0_i,
  input  PC1_i,
  input  PC2_i,
  input  PC3_i,
  input  PC4_i,
  input  PC5_i,
  input  PC6_i,
  input  nJAP,
  input  nDISK,
  input  FREQ,
  output FRES_o,
  output ZA1_o,
  output ZA2_o,
  output ZA3_o,
  output ZA4_o,
  output ZA5_o,
  output ZA6_o,
  output ZA7_o,
  output VA7_2,
  output VA6_2,
  output VA5_2,
  output VA4_2,
  output VA3_2,
  output VA2_2,
  output VA1_2,
  output ZD7_o,
  output ZD6_o,
  output ZD5_o,
  output ZD4_o,
  output ZD3_o,
  output ZD2_o,
  output ZD1_o,
  output ZD0_o,
  output VD0_o,
  output VD1_o,
  output VD2_o,
  output VD3_o,
  output VD4_o,
  output VD5_o,
  output VD6_o,
  output VD7_o,
  output VD8_o,
  output VD9_o,
  output VD10_o,
  output VD11_o,
  output VD12_o,
  output VD13_o,
  output VD14_o,
  output VD15_o,
  output nHL,
  output PA0_o,
  output PA1_o,
  output PA2_o,
  output PA3_o,
  output PA4_o,
  output PA5_o,
  output PA6_o,
  output PB0_o,
  output PB1_o,
  output PB2_o,
  output PB3_o,
  output PB4_o,
  output PB5_o,
  output PB6_o,
  output PC0_o,
  output PC1_o,
  output PC2_o,
  output PC3_o,
  output PC4_o,
  output PC5_o,
  output PC6_o
);

  wire _1_out, _2_out, _3_out, _4_out, _6_out, _7_out, _8_out, _9_out, _10_out, _11_out, _12_out, _13_out,
       _14_out, _15_out, _16_out, _17_q, _18_q, _19_out, _20_q, _21_q, _22_out, _24_out, _25_out, _26_q,
       _31_out, _33_out, _36_q, _37_out, _38_q, _39_q, _40_q, _41_out, _46_out, _54_out, _56_out, _57_out,
       _58_out, _59_out, _60_out, _61_out, _63_out, _64_out, _65_out, _66_out, _67_out, _68_out, _69_out,
       _70_out, _71_out, _72_out, _73_out, _75_out, _78_nq, _79_out, _80_co, _80_nq, _81_co, _81_nq, _81_q,
       _96_out, _101_out, _107_out, _108_out, _109_out, _110_out, _111_out, _112_out, _114_out, _115_out,
       _116_out, _117_out, _118_out, _119_out, _120_out, _121_out, _122_out, _125_out, _126_out, _128_out,
       _129_co, _129_nq, _130_co, _130_nq, _132_out, _133_co, _133_nq, _134_nq, _136_out, _137_out, _148_out,
       _149_out, _158_out, _167_out, _168_out, _169_out, _170_out, _171_out, _174_out, _187_out, _188_co,
       _188_nq, _197_q, _198_out, _203_out, _227_out, _237_out, _242_out, _244_q, _247_out, _254_out,
       _258_out, _260_out, _263_out, _264_out, _265_out, _266_out, _267_out, _268_out, _269_2_out, _269_out,
       _270_out, _288_out, _300_out, _301_out, _305_out, _306_out, _307_out, _308_out, _310_out, _311_out,
       _324_out, _325_out, _326_out, _327_out, _328_out, _330_out, _332_out, _333_out, _334_out, _336_out,
       _337_out, _338_out, _341_out, _346_q, _380_out, _382_out, _398_out, _399_out, _401_out, _402_out,
       _405_out, _406_out, _407_out, _432_out, _508_out, _527_out, _532_out, _600_q, _607_q, _608_out,
       _611_out, _620_out, _642_out, _643_out, _644_out, _645_out, _666_out, _667_out, _668_q, _669_q,
       _670_q, _671_q, _672_q, _673_q, ADR0, ADR1, ADR2, ADR3, ADR4, ADR5, ADR6, ADR7, DB0, DB1, DB2, DB3,
       DB4, DB5, DB6, DB7, DEC0_1, DEC0_2, DEC0_4, DEC0_5, DEC0_7, DEC0_SEL, DEC1_0, DEC1_3, DEC1_6,
       DEC1_SEL, DEC2_1, DEC2_2, DEC2_3, DEC2_4, DEC2_5, DEC2_6, DEC2_7, DEC2_SEL, DIV0, DIV1, DIV2, DIV3,
       DIV4, DIV5, DIV6, FRES, FRES0, FRESM3, g_5, g_47, g_48, g_93, g_95, g_98, g_113, g_151, g_152, g_155,
       g_156, g_159, g_160, g_165, g_166, g_189, g_190, g_193, g_194, g_200, g_205, g_206, g_207, g_211,
       g_215, g_241, g_261, g_272, g_273, g_277, g_280, g_312, g_314, g_321, g_340, g_354, g_371, g_379,
       g_456, g_505, g_610, multiplexer_5_out, multiplexer_10_out, multiplexer_39_out, MUX_CTRL, nM3_0,
       not_2_out, not_3_out, not_4_out, not_5_out, not_6_out, not_7_out, not_8_out, not_9_out, not_10_out,
       not_11_out, not_12_out, not_13_out, not_14_out, not_15_out, not_16_out, not_17_out, not_18_out,
       not_19_out, not_20_out, not_21_out, not_22_out, not_23_out, not_24_out, not_25_out, not_26_out,
       not_27_out, not_28_out, not_29_out, not_30_out, not_31_out, not_32_out, not_33_out, not_34_out,
       not_35_out, not_36_out, not_37_out, not_38_out, not_39_out, not_out, PA5_d, PA6_d, PB5_d, PB6_d,
       UCLKA1, UCLKA2, UCLKB1, UCLKB2, UCLKC1, UCLKC2, VD0_o_t, VD1_o_t, VD2_o_t, VD3_o_t, VD4_o_t, VD5_o_t,
       VD6_o_t, VD7_o_t;
  wire [0:0] _35_out, _87_q, _192_q, controlled_buffer_15_out;
  wire [1:0] _255_out;
  wire [2:0] _195_q, _322_out;
  wire [2:2] _32_out;
  wire [3:0] _29_q, _82_q, _86_out, _143_q, _145_q, _191_q, _602_q, multiplexer_7_out, multiplexer_8_out,
       multiplexer_9_out, multiplexer_11_out, multiplexer_12_out, multiplexer_16_out, multiplexer_20_out,
       multiplexer_24_out, multiplexer_28_out, multiplexer_29_out, multiplexer_33_out, multiplexer_34_out,
       multiplexer_35_out, multiplexer_36_out, multiplexer_37_out, multiplexer_38_out;
  wire [7:0] uart_a_1_rxa_o, uart_a_1_txa_o, uart_b_1_rxb_o, uart_b_1_txb_o, uart_c_1_rxc_o, uart_c_1_txc_o;

  buf _124 (nM3_0, nM3);
  and _645 (_645_out, _132_out, 1'b1);
  and _642 (_642_out, _645_out, _79_out);
  not _666 (_666_out, NTSC);
  nor _643 (_643_out, FRES_o, _642_out);
  and _128 (_128_out, 1'b1, _644_out, 1'b1);
  and _242 (_242_out, 1'b1, _645_out, _644_out);
  buf _644 (_644_out, _643_out);
  not _12 (_12_out, ADR6);
  not _11 (_11_out, ADR7);
  D_Flip_Flop _595 (.clk(VCLK), .D(nSRES), .Q(FRES0), .Qn(FRES_o));  // open: preset, en, reset
  _1_bit_cnt _129 (
    .C(VCLK), .CIN(_128_out), .VAL(_666_out), .nLD(_644_out), .nRES(1'b1), .nQ(_129_nq), .CO(_129_co));  // open: Q
  _1_bit_cnt _130 (
    .C(VCLK), .CIN(_129_co), .VAL(1'b0), .nLD(_644_out), .nRES(1'b1), .nQ(_130_nq), .CO(_130_co));  // open: Q
  _1_bit_cnt _133 (
    .C(VCLK), .CIN(_130_co), .VAL(1'b1), .nLD(_644_out), .nRES(1'b1), .nQ(_133_nq), .CO(_133_co));  // open: Q
  _1_bit_cnt _134 (.C(VCLK), .CIN(_133_co), .VAL(1'b1), .nLD(_644_out), .nRES(1'b1), .nQ(_134_nq));  // open: Q, CO
  _1_bit_cnt _188 (
    .C(VCLK), .CIN(_242_out), .VAL(1'b1), .nLD(_644_out), .nRES(1'b1), .nQ(_188_nq), .CO(_188_co));  // open: Q
  _1_bit_cnt _80 (
    .C(VCLK), .CIN(_188_co), .VAL(1'b0), .nLD(_644_out), .nRES(1'b1), .nQ(_80_nq), .CO(_80_co));  // open: Q
  _1_bit_cnt _81 (.C(VCLK), .CIN(_80_co), .VAL(1'b0), .nLD(_644_out), .nRES(1'b1), .Q(_81_q), .nQ(_81_nq), .CO(_81_co));
  _1_bit_cnt _78 (.C(VCLK), .CIN(_81_co), .VAL(1'b1), .nLD(_644_out), .nRES(1'b1), .nQ(_78_nq));  // open: Q, CO
  nor _46 (_46_out, ADR4, ADR5, ADR6, ADR7);
  nor _16 (_16_out, ADR4, ADR3, ADR2);
  and _14 (_14_out, ADR4, ADR2, ADR3);
  nand _10 (_10_out, ADR7, ADR6);
  or _8 (_8_out, ADR5, ADR1);
  or _620 (_620_out, nLWR, nIO);
  not _407 (_407_out, ADR0);
  not _401 (_401_out, _407_out);
  not _325 (_325_out, ADR1);
  not _398 (_398_out, _325_out);
  not _406 (_406_out, _326_out);
  not _326 (_326_out, ADR2);
  and _131 (FRESM3, nM3, FRES0);
  buf _376 (FRES, FRES0);
  Multiplexer #(.width(4), .disabled(0), .enable("false")) multiplexer_1 (
    .in0({ZA0, ZA1, ZA2, ZA3}), .in1({VA1, VA2, VA3, VA4}), .out({ADR0, ADR1, ADR2, ADR3}), .sel(nM3));
  Multiplexer #(.width(4), .disabled(0), .enable("false")) multiplexer_2 (
    .in0({ZA4, ZA5, ZA6, ZA7}), .in1({VA5, VA6, VA7, 1'b0}), .out({ADR4, ADR5, ADR6, ADR7}), .sel(nM3));
  nor _15 (_15_out, _16_out, _14_out);
  nand _13 (_13_out, 1'b1, ADR5, _12_out, _11_out, ADR1, ADR4, ADR2, ADR3);
  nor _132 (_132_out, _134_nq, _133_nq, _130_nq, _129_nq);
  nor _79 (_79_out, _78_nq, _81_nq, _80_nq, _188_nq);
  or _7 (_7_out, _15_out, _10_out, _8_out, nM3);
  or _9 (_9_out, nM3, _13_out, _620_out);
  Multiplexer #(.width(4), .disabled(0), .enable("false")) multiplexer_3 (
    .in0({VD4_i, VD5_i, VD6_i, VD7_i}), .in1({ZD4_i, ZD5_i, ZD6_i, ZD7_i}), .out({DB4, DB5, DB6, DB7}),
    .sel(_288_out));
  not _288 (_288_out, nM3_0);
  Multiplexer #(.width(4), .disabled(0), .enable("false")) multiplexer_4 (
    .in0({VD0_i, VD1_i, VD2_i, VD3_i}), .in1({ZD0_i, ZD1_i, ZD2_i, ZD3_i}), .out({DB0, DB1, DB2, DB3}),
    .sel(_288_out));
  nand _169 (_169_out, _46_out, nM3);
  and _6 (_6_out, _7_out, _9_out);
  nand _405 (_405_out, _406_out, _407_out, _398_out, DEC0_SEL);
  nand _404 (DEC0_2, _326_out, _407_out, _398_out, DEC0_SEL);
  nand _403 (DEC0_4, _406_out, _407_out, _325_out, DEC0_SEL);
  nand _402 (_402_out, _326_out, _407_out, _325_out, DEC0_SEL);
  nand _400 (DEC0_1, _326_out, _401_out, _325_out, DEC0_SEL);
  nand _399 (_399_out, _326_out, _401_out, _398_out, DEC0_SEL);
  nand _397 (DEC0_7, _406_out, _401_out, _398_out, DEC0_SEL);
  nand _396 (DEC0_5, _406_out, _401_out, _325_out, DEC0_SEL);
  Multiplexer #(.disabled(0), .enable("false")) multiplexer_5 (
    .in0(NTSC), .in1(_81_q), .out(multiplexer_5_out), .sel(TEST));
  Multiplexer #(.disabled(0), .enable("false")) multiplexer_6 (.in0(_81_q), .in1(VCLK), .out(DIV0), .sel(TEST));
  buf _237 (_237_out, FRES0);
  not _107 (_107_out, ADR3);
  T_Flip_Flop _239 (.clk(DIV0), .T(_237_out), .Q(DIV1));  // open: Qn, preset, reset, en
  T_Flip_Flop _240 (.clk(DIV1), .T(_237_out), .Q(DIV2));  // open: Qn, preset, reset, en
  T_Flip_Flop _244 (.clk(DIV2), .T(_237_out), .Q(_244_q));  // open: Qn, preset, reset, en
  T_Flip_Flop _243 (.clk(_244_q), .T(_237_out), .Q(DIV3));  // open: Qn, preset, reset, en
  T_Flip_Flop _238 (.clk(DIV3), .T(_237_out), .Q(DIV4));  // open: Qn, preset, reset, en
  T_Flip_Flop _347 (.clk(DIV4), .T(_237_out), .Q(DIV5));  // open: Qn, preset, reset, en
  T_Flip_Flop _346 (.clk(DIV5), .T(_237_out), .Q(_346_q));  // open: Qn, preset, reset, en
  T_Flip_Flop _345 (.clk(_346_q), .T(_237_out), .Q(DIV6));  // open: Qn, preset, reset, en
  and _170 (_170_out, _169_out, _6_out);
  or _341 (_341_out, _6_out, ADR0);
  not _337 (_337_out, ADR3);
  not _174 (_174_out, ADR3);
  or _108 (_108_out, nIO, nCAS0);
  not _227 (_227_out, _107_out);
  not _171 (_171_out, ADR0);
  not _56 (_56_out, ADR1);
  not _168 (_168_out, ADR2);
  nor _96 (_96_out, nIO, _170_out, nCAS0);
  D_Flip_Flop _340 (.clk(_341_out), .D(VD4_i), .Q(g_340), .reset(not_out));  // open: Qn, preset, en
  not \not  (not_out, FRESM3);
  nor _335 (DEC0_SEL, _169_out, _337_out, _620_out);
  nor _173 (DEC1_SEL, _169_out, _174_out, _108_out);
  nor _282 (DEC2_SEL, _169_out, _227_out, _620_out);
  not _60 (_60_out, _171_out);
  not _64 (_64_out, _56_out);
  not _58 (_58_out, _168_out);
  buf _432 (_432_out, FRES0);
  nand _63 (_63_out, _58_out, _171_out, _56_out, DEC1_SEL);
  nand _172 (DEC1_0, _168_out, _171_out, _56_out, DEC1_SEL);
  nand _62 (DEC1_6, _58_out, _171_out, _64_out, DEC1_SEL);
  nand _54 (_54_out, _168_out, _171_out, _64_out, DEC1_SEL);
  nand _61 (_61_out, _58_out, _60_out, _64_out, DEC1_SEL);
  nand _59 (_59_out, _58_out, _60_out, _56_out, DEC1_SEL);
  nand _57 (_57_out, _168_out, _60_out, _56_out, DEC1_SEL);
  nand _55 (DEC1_3, _168_out, _60_out, _64_out, DEC1_SEL);
  not _328 (_328_out, ADR0);
  not _330 (_330_out, ADR1);
  not _327 (_327_out, ADR2);
  UART_A uart_a_1 (
    .DIV0(DIV0), .DIV1(DIV1), .DIV2(DIV2), .DIV3(DIV3), .DIV4(DIV4), .DIV5(DIV5), .DIV6(DIV6), .PA5_i(PA5_i),
    .FRES(FRES), .FRES0(_432_out), .FRESM3(FRESM3), .DEC0_1(DEC0_1), .DEC1_0(DEC1_0), .DEC2_7(DEC2_7),
    .TXA_o(uart_a_1_txa_o), .g_505(g_505), .g_155(g_155), .g_206(g_206), .g_98(g_98), .g_93(g_93),
    .RXA_o(uart_a_1_rxa_o), .g_241(g_241), .g_152(g_152), .g_166(g_166),
    .DB({DB7, DB6, DB5, DB4, DB3, DB2, DB1, DB0}), .UCLKA1(UCLKA1), .UCLKA2(UCLKA2), .g_151(g_151),
    .g_273(g_273));
  UART_B uart_b_1 (
    .DIV0(DIV0), .DIV1(DIV1), .DIV2(DIV2), .DIV3(DIV3), .DIV4(DIV4), .DIV5(DIV5), .DIV6(DIV6), .PB5_i(PB5_i),
    .FRES(FRES), .FRES0(_432_out), .FRESM3(FRESM3), .DEC0_2(DEC0_2), .DEC0_4(DEC0_4), .DEC1_3(DEC1_3),
    .TXB_o(uart_b_1_txb_o), .g_354(g_354), .g_156(g_156), .g_207(g_207), .g_215(g_215), .g_211(g_211),
    .RXB_o(uart_b_1_rxb_o), .g_113(g_113), .g_47(g_47), .g_165(g_165),
    .DB({DB7, DB6, DB5, DB4, DB3, DB2, DB1, DB0}), .UCLKB1(UCLKB1), .UCLKB2(UCLKB2), .g_277(g_277),
    .g_321(g_321));
  UART_C uart_c_1 (
    .DIV0(DIV0), .DIV1(DIV1), .DIV2(DIV2), .DIV3(DIV3), .DIV4(DIV4), .DIV5(DIV5), .DIV6(DIV6), .PC5_i(PC5_i),
    .FRES(FRES), .FRES0(_432_out), .FRESM3(FRESM3), .DEC0_5(DEC0_5), .DEC0_7(DEC0_7), .DEC1_6(DEC1_6),
    .TXC_o(uart_c_1_txc_o), .g_456(g_456), .g_95(g_95), .g_205(g_205), .g_280(g_280), .g_272(g_272),
    .RXC_o(uart_c_1_rxc_o), .g_371(g_371), .g_48(g_48), .g_159(g_159),
    .DB({DB7, DB6, DB5, DB4, DB3, DB2, DB1, DB0}), .UCLKC1(UCLKC1), .UCLKC2(UCLKC2), .g_314(g_314),
    .g_312(g_312));
  or _31 (_31_out, PA5_d, nJAP);
  or _254 (_254_out, PB6_d, nJAP);
  or _258 (_258_out, PA6_d, nJAP);
  not not_2 (not_2_out, 1'b1);
  or _33 (_33_out, PB5_d, nJAP);
  not _336 (_336_out, _328_out);
  not _332 (_332_out, _330_out);
  not _334 (_334_out, _327_out);
  and _32 (_32_out[2], PA5_i, _31_out);
  D_Flip_Flop _87 (.clk(DEC2_1), .D(DB7), .Q(_87_q[0]), .reset(not_2_out));  // open: Qn, preset, en
  and _255 (_255_out[0], PB6_i, _254_out);
  and _259 (_255_out[1], PA6_i, _258_out);
  D_Flip_Flop _192 (.clk(DEC2_2), .D(DB7), .Q(_192_q[0]), .reset(not_2_out));  // open: Qn, preset, en
  and _35 (_35_out[0], PB5_i, _33_out);
  not not_3 (not_3_out, FRESM3);
  D_Flip_Flop _195 (.clk(DEC2_4), .D(DB7), .Q(_195_q[0]), .reset(not_3_out));  // open: Qn, preset, en
  D_Flip_Flop _186 (.clk(DEC2_5), .D(DB7), .Q(_195_q[1]), .reset(not_3_out));  // open: Qn, preset, en
  D_Flip_Flop _302 (.clk(DEC2_6), .D(DB7), .Q(_195_q[2]), .reset(not_3_out));  // open: Qn, preset, en
  nand _329 (DEC2_6, _334_out, _328_out, _332_out, DEC2_SEL);
  nand _333 (_333_out, _327_out, _328_out, _330_out, DEC2_SEL);
  nand _285 (DEC2_2, _327_out, _328_out, _332_out, DEC2_SEL);
  nand _287 (DEC2_4, _334_out, _328_out, _330_out, DEC2_SEL);
  nand _331 (DEC2_7, _334_out, _336_out, _332_out, DEC2_SEL);
  nand _283 (DEC2_3, _327_out, _336_out, _332_out, DEC2_SEL);
  nand _284 (DEC2_5, _334_out, _336_out, _330_out, DEC2_SEL);
  nand _286 (DEC2_1, _327_out, _336_out, _330_out, DEC2_SEL);
  Multiplexer #(.width(4), .disabled(0), .enable("false")) multiplexer_7 (
    .in0({PA4_i, _32_out[2], PB0_i, PB1_i}), .in1({PA4_i, PA5_i, PA6_i, _87_q[0]}), .out(multiplexer_7_out),
    .sel(nM3));
  Multiplexer #(.width(4), .disabled(0), .enable("false")) multiplexer_8 (
    .in0({2'b10, _255_out}), .in1({PB4_i, PB5_i, PB6_i, _192_q[0]}), .out(multiplexer_8_out), .sel(nM3));
  Multiplexer #(.width(4), .disabled(0), .enable("false")) multiplexer_9 (
    .in0({PB2_i, PB3_i, PB4_i, _35_out[0]}), .in1({PB0_i, PB1_i, PB2_i, PB3_i}), .out(multiplexer_9_out),
    .sel(nM3));
  not _263 (_263_out, _195_q[0]);
  not _115 (_115_out, _195_q[1]);
  not _300 (_300_out, _195_q[2]);
  nor _264 (_264_out, PA6_i, _263_out);
  nor _116 (_116_out, PB6_i, _115_out);
  nor _301 (_301_out, PC6_i, _300_out);
  not _65 (_65_out, PB6_d);
  not _66 (_66_out, PA6_d);
  nor _109 (_109_out, PB6_i, _65_out);
  nor _137 (_137_out, _66_out, PA6_i);
  nor _203 (_203_out, g_206, g_207, g_205, _264_out, _116_out, _301_out);
  nor _110 (_110_out, _109_out, _137_out);
  not _121 (_121_out, nM3);
  nor _122 (_122_out, _121_out, _203_out);
  nor _112 (_112_out, _110_out, nM3);
  nor _123 (nHL, _122_out, _112_out);
  buf _136 (_136_out, FRES0);
  Multiplexer #(.disabled(0), .enable("false")) multiplexer_10 (
    .in0(nDISK), .in1(UCLKC1), .out(multiplexer_10_out), .sel(TEST));
  and _508 (_508_out, TEST, UCLKC2);
  and _187 (_187_out, TEST, UCLKB1);
  and _266 (_266_out, TEST, UCLKB2);
  and _269 (_269_out, TEST, UCLKA1);
  and _269_2 (_269_2_out, TEST, UCLKA2);
  not not_4 (not_4_out, _136_out);
  D_Flip_Flop _29 (.clk(g_5), .D(DB7), .Q(_29_q[0]), .preset(not_4_out));  // open: Qn, en, reset
  D_Flip_Flop _27 (.clk(g_5), .D(DB6), .Q(_29_q[1]), .preset(not_4_out));  // open: Qn, en, reset
  D_Flip_Flop _30 (.clk(g_5), .D(DB5), .Q(_29_q[2]), .preset(not_4_out));  // open: Qn, en, reset
  D_Flip_Flop _674 (.clk(g_5), .D(DB4), .Q(_29_q[3]), .preset(not_4_out));  // open: Qn, en, reset
  D_Flip_Flop _191 (.clk(DEC2_2), .D(DB6), .Q(_191_q[0]), .reset(not_5_out));  // open: Qn, preset, en
  D_Flip_Flop _85 (.clk(DEC2_2), .D(DB5), .Q(_191_q[1]), .reset(not_5_out));  // open: Qn, preset, en
  D_Flip_Flop _83 (.clk(DEC2_1), .D(DB6), .Q(_191_q[2]), .reset(not_5_out));  // open: Qn, preset, en
  D_Flip_Flop _84 (.clk(DEC2_1), .D(DB5), .Q(_191_q[3]), .reset(not_5_out));  // open: Qn, preset, en
  not not_5 (not_5_out, 1'b1);
  not _4 (_4_out, ADR0);
  Multiplexer #(.width(4), .disabled(0), .enable("false")) multiplexer_11 (
    .in0(_29_q), .in1(_191_q), .out(multiplexer_11_out), .sel(nM3));
  not not_6 (not_6_out, 1'b1);
  D_Flip_Flop _600 (.clk(DEC2_3), .D(DB7), .Q(_600_q), .reset(not_6_out));  // open: Qn, preset, en
  and _1 (_1_out, nM3, ADR1);
  nor _3 (_3_out, nM3, _4_out);
  and _167 (_167_out, nM3, ADR2);
  or _5 (g_5, _4_out, _9_out);
  xnor _324 (_324_out, ADR0, nM3);
  buf _322 (_322_out[0], _324_out);
  or _2 (_2_out, _1_out, _3_out);
  buf _135 (_322_out[1], _2_out);
  buf _163 (_322_out[2], _167_out);
  D_Flip_Flop _143 (.clk(g_5), .D(DB3), .Q(_143_q[0]), .preset(not_4_out));  // open: Qn, en, reset
  D_Flip_Flop _140 (.clk(g_5), .D(DB2), .Q(_143_q[1]), .preset(not_4_out));  // open: Qn, en, reset
  D_Flip_Flop _139 (.clk(g_5), .D(DB1), .Q(_143_q[2]), .preset(not_4_out));  // open: Qn, en, reset
  D_Flip_Flop _142 (.clk(g_5), .D(DB0), .Q(_143_q[3]), .preset(not_4_out));  // open: Qn, en, reset
  D_Flip_Flop _190 (.clk(DEC2_5), .D(DB6), .Q(g_190), .reset(not_7_out));  // open: Qn, preset, en
  D_Flip_Flop _200 (.clk(DEC2_5), .D(DB5), .Q(g_200), .reset(not_7_out));  // open: Qn, preset, en
  D_Flip_Flop _193 (.clk(DEC2_4), .D(DB6), .Q(g_193), .reset(not_7_out));  // open: Qn, preset, en
  D_Flip_Flop _160 (.clk(DEC2_4), .D(DB5), .Q(g_160), .reset(not_7_out));  // open: Qn, preset, en
  not not_7 (not_7_out, FRESM3);
  Multiplexer #(.select(3), .disabled(0), .enable("false")) multiplexer_12 (
    .in0(nJAP), .in1(multiplexer_7_out[0]), .in2(multiplexer_8_out[0]), .in3(_600_q), .in4(_195_q[0]),
    .in5(_195_q[1]), .in6(_195_q[2]), .in7(uart_a_1_txa_o[7]), .out(multiplexer_12_out[0]), .sel(_322_out));
  Multiplexer #(.select(3), .disabled(0), .enable("false")) multiplexer_13 (
    .in0(multiplexer_5_out), .in1(multiplexer_7_out[1]), .in2(multiplexer_8_out[1]), .in3(PC6_i),
    .in4(g_193), .in5(g_193), .in6(g_610), .in7(uart_a_1_txa_o[6]), .out(multiplexer_12_out[1]),
    .sel(_322_out));
  Multiplexer #(.select(3), .disabled(0), .enable("false")) multiplexer_14 (
    .in0(multiplexer_10_out), .in1(multiplexer_7_out[2]), .in2(multiplexer_8_out[2]), .in3(PC5_i),
    .in4(g_160), .in5(g_200), .in6(g_379), .in7(uart_a_1_txa_o[5]), .out(multiplexer_12_out[2]),
    .sel(_322_out));
  Multiplexer #(.select(3), .disabled(0), .enable("false")) multiplexer_15 (
    .in0(_508_out), .in1(multiplexer_7_out[3]), .in2(multiplexer_8_out[3]), .in3(PC4_i), .in4(g_194),
    .in5(g_189), .in6(g_261), .in7(uart_a_1_txa_o[4]), .out(multiplexer_12_out[3]), .sel(_322_out));
  Multiplexer #(.select(3), .disabled(0), .enable("false")) multiplexer_16 (
    .in0(uart_a_1_rxa_o[7]), .in1(g_151), .in2(uart_b_1_txb_o[7]), .in3(uart_b_1_rxb_o[7]), .in4(g_321),
    .in5(uart_c_1_txc_o[7]), .in6(uart_c_1_rxc_o[7]), .in7(g_312), .out(multiplexer_16_out[0]), .sel(_322_out));
  Multiplexer #(.select(3), .disabled(0), .enable("false")) multiplexer_17 (
    .in0(uart_a_1_rxa_o[6]), .in1(g_273), .in2(uart_b_1_txb_o[6]), .in3(uart_b_1_rxb_o[6]), .in4(g_277),
    .in5(uart_c_1_txc_o[6]), .in6(uart_c_1_rxc_o[6]), .in7(g_314), .out(multiplexer_16_out[1]), .sel(_322_out));
  Multiplexer #(.select(3), .disabled(0), .enable("false")) multiplexer_18 (
    .in0(uart_a_1_rxa_o[5]), .in1(g_166), .in2(uart_b_1_txb_o[5]), .in3(uart_b_1_rxb_o[5]), .in4(g_165),
    .in5(uart_c_1_txc_o[5]), .in6(uart_c_1_rxc_o[5]), .in7(g_159), .out(multiplexer_16_out[2]), .sel(_322_out));
  Multiplexer #(.select(3), .disabled(0), .enable("false")) multiplexer_19 (
    .in0(uart_a_1_rxa_o[4]), .in1(g_152), .in2(uart_b_1_txb_o[4]), .in3(uart_b_1_rxb_o[4]), .in4(g_47),
    .in5(uart_c_1_txc_o[4]), .in6(uart_c_1_rxc_o[4]), .in7(g_48), .out(multiplexer_16_out[3]), .sel(_322_out));
  Multiplexer #(.select(3), .disabled(0), .enable("false")) multiplexer_20 (
    .in0(_187_out), .in1(PA3_i), .in2(multiplexer_9_out[0]), .in3(PC3_i), .in4(_145_q[3]), .in5(_82_q[3]),
    .in6(_602_q[3]), .in7(uart_a_1_txa_o[3]), .out(multiplexer_20_out[0]), .sel(_322_out));
  Multiplexer #(.select(3), .disabled(0), .enable("false")) multiplexer_21 (
    .in0(_266_out), .in1(PA2_i), .in2(multiplexer_9_out[1]), .in3(PC2_i), .in4(_145_q[2]), .in5(_82_q[2]),
    .in6(_602_q[2]), .in7(uart_a_1_txa_o[2]), .out(multiplexer_20_out[1]), .sel(_322_out));
  Multiplexer #(.select(3), .disabled(0), .enable("false")) multiplexer_22 (
    .in0(_269_out), .in1(PA1_i), .in2(multiplexer_9_out[2]), .in3(PC1_i), .in4(_145_q[1]), .in5(_82_q[1]),
    .in6(_602_q[1]), .in7(uart_a_1_txa_o[1]), .out(multiplexer_20_out[2]), .sel(_322_out));
  Multiplexer #(.select(3), .disabled(0), .enable("false")) multiplexer_23 (
    .in0(_269_2_out), .in1(PA0_i), .in2(multiplexer_9_out[3]), .in3(PC0_i), .in4(_145_q[0]), .in5(_82_q[0]),
    .in6(_602_q[0]), .in7(uart_a_1_txa_o[0]), .out(multiplexer_20_out[3]), .sel(_322_out));
  Multiplexer #(.select(3), .disabled(0), .enable("false")) multiplexer_24 (
    .in0(uart_a_1_rxa_o[3]), .in1(g_155), .in2(uart_b_1_txb_o[3]), .in3(uart_b_1_rxb_o[3]), .in4(g_156),
    .in5(uart_c_1_txc_o[3]), .in6(uart_c_1_rxc_o[3]), .in7(g_95), .out(multiplexer_24_out[0]), .sel(_322_out));
  Multiplexer #(.select(3), .disabled(0), .enable("false")) multiplexer_25 (
    .in0(uart_a_1_rxa_o[2]), .in1(g_93), .in2(uart_b_1_txb_o[2]), .in3(uart_b_1_rxb_o[2]), .in4(g_211),
    .in5(uart_c_1_txc_o[2]), .in6(uart_c_1_rxc_o[2]), .in7(g_272), .out(multiplexer_24_out[1]), .sel(_322_out));
  Multiplexer #(.select(3), .disabled(0), .enable("false")) multiplexer_26 (
    .in0(uart_a_1_rxa_o[1]), .in1(g_98), .in2(uart_b_1_txb_o[1]), .in3(uart_b_1_rxb_o[1]), .in4(g_215),
    .in5(uart_c_1_txc_o[1]), .in6(uart_c_1_rxc_o[1]), .in7(g_280), .out(multiplexer_24_out[2]), .sel(_322_out));
  Multiplexer #(.select(3), .disabled(0), .enable("false")) multiplexer_27 (
    .in0(uart_a_1_rxa_o[0]), .in1(g_505), .in2(uart_b_1_txb_o[0]), .in3(uart_b_1_rxb_o[0]), .in4(g_354),
    .in5(uart_c_1_txc_o[0]), .in6(uart_c_1_rxc_o[0]), .in7(g_456), .out(multiplexer_24_out[3]), .sel(_322_out));
  not _86 (_86_out[0], g_190);
  not _158 (_158_out, g_200);
  not _138 (_86_out[2], g_193);
  not _101 (_101_out, g_160);
  or _157 (_86_out[1], g_165, _158_out);
  or _161 (_86_out[3], g_166, _101_out);
  Multiplexer #(.width(4), .disabled(0), .enable("false")) multiplexer_28 (
    .in0(multiplexer_12_out), .in1(multiplexer_16_out), .out(multiplexer_28_out), .sel(_198_out));
  and _198 (_198_out, nM3, ADR3);
  Multiplexer #(.width(4), .disabled(0), .enable("false")) multiplexer_29 (
    .in0(multiplexer_20_out), .in1(multiplexer_24_out), .out(multiplexer_29_out), .sel(_198_out));
  Multiplexer #(.width(4), .disabled(0), .enable("false")) multiplexer_30 (
    .in0(_143_q), .in1(_86_out), .out({PA5_d, PA6_d, PB5_d, PB6_d}), .sel(nM3));
  Multiplexer #(.width(4), .disabled(0), .enable("false")) multiplexer_31 (
    .in0({ZD4_i, ZD5_i, ZD6_i, ZD7_i}), .in1(multiplexer_28_out), .out({VD4_o_t, VD5_o_t, VD6_o_t, VD7_o_t}),
    .sel(_96_out));
  Multiplexer #(.width(4), .disabled(0), .enable("false")) multiplexer_32 (
    .in0({ZD0_i, ZD1_i, ZD2_i, ZD3_i}), .in1(multiplexer_29_out), .out({VD0_o_t, VD1_o_t, VD2_o_t, VD3_o_t}),
    .sel(_96_out));
  not not_8 (not_8_out, 1'b1);
  not not_9 (not_9_out, FRESM3);
  not not_10 (not_10_out, 1'b1);
  not not_11 (not_11_out, FRESM3);
  not not_12 (not_12_out, FRESM3);
  not not_13 (not_13_out, 1'b1);
  not _126 (_126_out, ZA0);
  D_Flip_Flop _145 (.clk(DEC2_4), .D(DB0), .Q(_145_q[0]), .reset(not_9_out));  // open: Qn, preset, en
  D_Flip_Flop _153 (.clk(DEC2_4), .D(DB1), .Q(_145_q[1]), .reset(not_9_out));  // open: Qn, preset, en
  D_Flip_Flop _150 (.clk(DEC2_4), .D(DB2), .Q(_145_q[2]), .reset(not_9_out));  // open: Qn, preset, en
  D_Flip_Flop _146 (.clk(DEC2_4), .D(DB3), .Q(_145_q[3]), .reset(not_9_out));  // open: Qn, preset, en
  D_Flip_Flop _39 (.clk(DEC2_1), .D(DB0), .Q(_39_q), .reset(not_8_out));  // open: Qn, preset, en
  D_Flip_Flop _40 (.clk(DEC2_1), .D(DB1), .Q(_40_q), .reset(not_8_out));  // open: Qn, preset, en
  D_Flip_Flop _38 (.clk(DEC2_1), .D(DB2), .Q(_38_q), .reset(not_8_out));  // open: Qn, preset, en
  D_Flip_Flop _36 (.clk(DEC2_1), .D(DB3), .Q(_36_q), .reset(not_8_out));  // open: Qn, preset, en
  D_Flip_Flop _197 (.clk(DEC2_1), .D(DB4), .Q(_197_q), .reset(not_8_out));  // open: Qn, preset, en
  D_Flip_Flop _194 (.clk(DEC2_4), .D(DB4), .Q(g_194), .reset(not_9_out));  // open: Qn, preset, en
  D_Flip_Flop _82 (.clk(DEC2_5), .D(DB0), .Q(_82_q[0]), .reset(not_11_out));  // open: Qn, preset, en
  D_Flip_Flop _185 (.clk(DEC2_5), .D(DB1), .Q(_82_q[1]), .reset(not_11_out));  // open: Qn, preset, en
  D_Flip_Flop _184 (.clk(DEC2_5), .D(DB2), .Q(_82_q[2]), .reset(not_11_out));  // open: Qn, preset, en
  D_Flip_Flop _183 (.clk(DEC2_5), .D(DB3), .Q(_82_q[3]), .reset(not_11_out));  // open: Qn, preset, en
  D_Flip_Flop _26 (.clk(DEC2_2), .D(DB0), .Q(_26_q), .reset(not_10_out));  // open: Qn, preset, en
  D_Flip_Flop _21 (.clk(DEC2_2), .D(DB1), .Q(_21_q), .reset(not_10_out));  // open: Qn, preset, en
  D_Flip_Flop _20 (.clk(DEC2_2), .D(DB2), .Q(_20_q), .reset(not_10_out));  // open: Qn, preset, en
  D_Flip_Flop _18 (.clk(DEC2_2), .D(DB3), .Q(_18_q), .reset(not_10_out));  // open: Qn, preset, en
  D_Flip_Flop _17 (.clk(DEC2_2), .D(DB4), .Q(_17_q), .reset(not_10_out));  // open: Qn, preset, en
  D_Flip_Flop _189 (.clk(DEC2_5), .D(DB4), .Q(g_189), .reset(not_11_out));  // open: Qn, preset, en
  D_Flip_Flop _602 (.clk(DEC2_6), .D(DB0), .Q(_602_q[0]), .reset(not_12_out));  // open: Qn, preset, en
  D_Flip_Flop _609 (.clk(DEC2_6), .D(DB1), .Q(_602_q[1]), .reset(not_12_out));  // open: Qn, preset, en
  D_Flip_Flop _526 (.clk(DEC2_6), .D(DB2), .Q(_602_q[2]), .reset(not_12_out));  // open: Qn, preset, en
  D_Flip_Flop _528 (.clk(DEC2_6), .D(DB3), .Q(_602_q[3]), .reset(not_12_out));  // open: Qn, preset, en
  D_Flip_Flop _668 (.clk(DEC2_3), .D(DB0), .Q(_668_q), .reset(not_13_out));  // open: Qn, preset, en
  D_Flip_Flop _669 (.clk(DEC2_3), .D(DB1), .Q(_669_q), .reset(not_13_out));  // open: Qn, preset, en
  D_Flip_Flop _671 (.clk(DEC2_3), .D(DB2), .Q(_671_q), .reset(not_13_out));  // open: Qn, preset, en
  D_Flip_Flop _673 (.clk(DEC2_3), .D(DB3), .Q(_673_q), .reset(not_13_out));  // open: Qn, preset, en
  D_Flip_Flop _607 (.clk(DEC2_3), .D(DB4), .Q(_607_q), .reset(not_13_out));  // open: Qn, preset, en
  D_Flip_Flop _261 (.clk(DEC2_6), .D(DB4), .Q(g_261), .reset(not_12_out));  // open: Qn, preset, en
  D_Flip_Flop _610 (.clk(DEC2_6), .D(DB6), .Q(g_610), .reset(not_12_out));  // open: Qn, preset, en
  D_Flip_Flop _379 (.clk(DEC2_6), .D(DB5), .Q(g_379), .reset(not_12_out));  // open: Qn, preset, en
  D_Flip_Flop _672 (.clk(DEC2_3), .D(DB5), .Q(_672_q), .reset(not_13_out));  // open: Qn, preset, en
  D_Flip_Flop _670 (.clk(DEC2_3), .D(DB5), .Q(_670_q), .reset(not_13_out));  // open: Qn, preset, en
  and _125 (_125_out, nM3_0, _126_out);
  not _69 (_69_out, nCAS0);
  not _41 (_41_out, _145_q[0]);
  not _149 (_149_out, _145_q[1]);
  not _148 (_148_out, _145_q[2]);
  not _37 (_37_out, _145_q[3]);
  not _25 (_25_out, _82_q[0]);
  not _22 (_22_out, _82_q[1]);
  not _24 (_24_out, _82_q[2]);
  not _19 (_19_out, _82_q[3]);
  not _75 (_75_out, g_189);
  not _667 (_667_out, _602_q[0]);
  not _608 (_608_out, _602_q[1]);
  not _527 (_527_out, _602_q[2]);
  not _532 (_532_out, _602_q[3]);
  not _305 (_305_out, g_261);
  not _611 (_611_out, g_610);
  not _380 (_380_out, g_379);
  Multiplexer #(.width(4), .disabled(0), .enable("false")) multiplexer_33 (
    .in0({VD4_i, VD5_i, VD6_i, VD7_i}), .in1({VD12_i, VD13_i, VD14_i, VD15_i}), .out(multiplexer_33_out),
    .sel(_125_out));
  Multiplexer #(.width(4), .disabled(0), .enable("false")) multiplexer_34 (
    .in0({VD0_i, VD1_i, VD2_i, VD3_i}), .in1({VD8_i, VD9_i, VD10_i, VD11_i}), .out(multiplexer_34_out),
    .sel(_125_out));
  or _73 (_73_out, nZTOV, nCAS0);
  or _71 (_71_out, nVTOZ, _69_out);
  or _68 (_68_out, nZTOV, _69_out);
  or _70 (_70_out, nCAS0, nVTOZ);
  nand _111 (_111_out, MUX_CTRL, nM3_0);
  not not_14 (not_14_out, _148_out);
  not not_15 (not_15_out, _149_out);
  not not_16 (not_16_out, _37_out);
  assign PA1_o = not_15_out ? _40_q : 1'bz;  // Controlled_Buffer controlled_buffer_1
  assign PA2_o = not_14_out ? _38_q : 1'bz;  // Controlled_Buffer controlled_buffer_2
  assign PA3_o = not_16_out ? _36_q : 1'bz;  // Controlled_Buffer controlled_buffer_3
  not _267 (_267_out, g_152);
  not _260 (_260_out, g_194);
  assign PA5_o = not_18_out ? multiplexer_11_out[3] : 1'bz;  // Controlled_Buffer controlled_buffer_4
  assign PA6_o = not_17_out ? multiplexer_11_out[2] : 1'bz;  // Controlled_Buffer controlled_buffer_5
  not not_17 (not_17_out, PA6_d);
  not not_18 (not_18_out, PA5_d);
  not not_19 (not_19_out, _24_out);
  not not_20 (not_20_out, _19_out);
  not not_21 (not_21_out, _22_out);
  assign PB1_o = not_21_out ? _21_q : 1'bz;  // Controlled_Buffer controlled_buffer_6
  assign PB2_o = not_19_out ? _20_q : 1'bz;  // Controlled_Buffer controlled_buffer_7
  assign PB3_o = not_20_out ? _18_q : 1'bz;  // Controlled_Buffer controlled_buffer_8
  not _117 (_117_out, g_47);
  not not_22 (not_22_out, PB6_d);
  not not_23 (not_23_out, PB5_d);
  assign PB5_o = not_23_out ? multiplexer_11_out[1] : 1'bz;  // Controlled_Buffer controlled_buffer_9
  assign PB6_o = not_22_out ? multiplexer_11_out[0] : 1'bz;  // Controlled_Buffer controlled_buffer_10
  not not_24 (not_24_out, _608_out);
  not not_25 (not_25_out, _532_out);
  not not_26 (not_26_out, _527_out);
  assign PC1_o = not_24_out ? _669_q : 1'bz;  // Controlled_Buffer controlled_buffer_11
  assign PC2_o = not_26_out ? _671_q : 1'bz;  // Controlled_Buffer controlled_buffer_12
  assign PC3_o = not_25_out ? _673_q : 1'bz;  // Controlled_Buffer controlled_buffer_13
  not _307 (_307_out, g_48);
  or _382 (_382_out, _380_out, g_159);
  not not_27 (not_27_out, _382_out);
  assign PC5_o = not_27_out ? _672_q : 1'bz;  // Controlled_Buffer controlled_buffer_14
  Multiplexer #(.width(4), .disabled(0), .enable("false")) multiplexer_35 (
    .in0({ZA4, ZA5, ZA6, 1'b0}), .in1({ZA5, ZA6, ZA7, 1'b0}), .out(multiplexer_35_out), .sel(nM3));
  assign {VA5_2, VA6_2, VA7_2, controlled_buffer_15_out[0]} = not_34_out ? multiplexer_35_out : 4'bz;  // Controlled_Buffer controlled_buffer_15
  Multiplexer #(.width(4), .disabled(0), .enable("false")) multiplexer_36 (
    .in0({ZA0, ZA1, ZA2, ZA3}), .in1({ZA1, ZA2, ZA3, ZA4}), .out(multiplexer_36_out), .sel(nM3));
  assign {VA1_2, VA2_2, VA3_2, VA4_2} = not_34_out ? multiplexer_36_out : 4'bz;  // Controlled_Buffer controlled_buffer_16
  Multiplexer #(.width(4), .disabled(0), .enable("false")) multiplexer_37 (
    .in0(multiplexer_33_out), .in1(multiplexer_28_out), .out(multiplexer_37_out), .sel(MUX_CTRL));
  assign {ZD4_o, ZD5_o, ZD6_o, ZD7_o} = not_28_out ? multiplexer_37_out : 4'bz;  // Controlled_Buffer controlled_buffer_17
  assign {ZD0_o, ZD1_o, ZD2_o, ZD3_o} = not_28_out ? multiplexer_38_out : 4'bz;  // Controlled_Buffer controlled_buffer_18
  Multiplexer #(.width(4), .disabled(0), .enable("false")) multiplexer_38 (
    .in0(multiplexer_34_out), .in1(multiplexer_29_out), .out(multiplexer_38_out), .sel(MUX_CTRL));
  not not_28 (not_28_out, _72_out);
  and _72 (_72_out, _73_out, _71_out);
  and _338 (_338_out, nM3_0, _67_out);
  and _67 (_67_out, _68_out, _70_out, _111_out);
  not not_29 (not_29_out, _41_out);
  assign PA0_o = not_29_out ? _39_q : 1'bz;  // Controlled_Buffer controlled_buffer_19
  and _247 (_247_out, g_241, g_152);
  and _268 (_268_out, _267_out, _197_q);
  and _265 (_265_out, _267_out, _260_out);
  not not_30 (not_30_out, _25_out);
  assign PB0_o = not_30_out ? _26_q : 1'bz;  // Controlled_Buffer controlled_buffer_20
  and _114 (_114_out, g_113, g_47);
  and _120 (_120_out, _117_out, _17_q);
  and _118 (_118_out, _117_out, _75_out);
  not not_31 (not_31_out, _667_out);
  assign PC0_o = not_31_out ? _668_q : 1'bz;  // Controlled_Buffer controlled_buffer_21
  and _310 (_310_out, g_371, g_48);
  and _308 (_308_out, _307_out, _607_q);
  and _306 (_306_out, _307_out, _305_out);
  not not_32 (not_32_out, _611_out);
  assign PC6_o = not_32_out ? _670_q : 1'bz;  // Controlled_Buffer controlled_buffer_22
  assign ZA1_o = not_33_out ? VA1 : 1'bz;  // Controlled_Buffer controlled_buffer_23
  assign ZA2_o = not_33_out ? VA2 : 1'bz;  // Controlled_Buffer controlled_buffer_24
  assign ZA3_o = not_33_out ? VA3 : 1'bz;  // Controlled_Buffer controlled_buffer_25
  assign ZA4_o = not_33_out ? VA4 : 1'bz;  // Controlled_Buffer controlled_buffer_26
  assign ZA5_o = not_33_out ? VA5 : 1'bz;  // Controlled_Buffer controlled_buffer_27
  assign ZA6_o = not_33_out ? VA6 : 1'bz;  // Controlled_Buffer controlled_buffer_28
  assign ZA7_o = not_33_out ? VA7 : 1'bz;  // Controlled_Buffer controlled_buffer_29
  not not_33 (not_33_out, nVTOZ);
  not not_34 (not_34_out, nZTOV);
  not not_35 (not_35_out, _67_out);
  not not_36 (not_36_out, _338_out);
  assign VD0_o = not_35_out ? VD0_o_t : 1'bz;  // Controlled_Buffer controlled_buffer_30
  assign VD1_o = not_35_out ? VD1_o_t : 1'bz;  // Controlled_Buffer controlled_buffer_31
  assign VD2_o = not_35_out ? VD2_o_t : 1'bz;  // Controlled_Buffer controlled_buffer_32
  assign VD3_o = not_35_out ? VD3_o_t : 1'bz;  // Controlled_Buffer controlled_buffer_33
  assign VD4_o = not_35_out ? VD4_o_t : 1'bz;  // Controlled_Buffer controlled_buffer_34
  assign VD5_o = not_35_out ? VD5_o_t : 1'bz;  // Controlled_Buffer controlled_buffer_35
  assign VD6_o = not_35_out ? VD6_o_t : 1'bz;  // Controlled_Buffer controlled_buffer_36
  assign VD7_o = not_35_out ? VD7_o_t : 1'bz;  // Controlled_Buffer controlled_buffer_37
  Multiplexer #(.disabled(0), .enable("false")) multiplexer_39 (
    .in0(g_340), .in1(VD0_o_t), .out(multiplexer_39_out), .sel(nM3_0));
  assign VD8_o = not_36_out ? multiplexer_39_out : 1'bz;  // Controlled_Buffer controlled_buffer_38
  assign VD9_o = not_36_out ? VD1_o_t : 1'bz;  // Controlled_Buffer controlled_buffer_39
  assign VD10_o = not_36_out ? VD2_o_t : 1'bz;  // Controlled_Buffer controlled_buffer_40
  assign VD11_o = not_36_out ? VD3_o_t : 1'bz;  // Controlled_Buffer controlled_buffer_41
  assign VD12_o = not_36_out ? VD4_o_t : 1'bz;  // Controlled_Buffer controlled_buffer_42
  assign VD13_o = not_36_out ? VD5_o_t : 1'bz;  // Controlled_Buffer controlled_buffer_43
  assign VD14_o = not_36_out ? VD6_o_t : 1'bz;  // Controlled_Buffer controlled_buffer_44
  assign VD15_o = not_36_out ? VD7_o_t : 1'bz;  // Controlled_Buffer controlled_buffer_45
  assign PA4_o = not_37_out ? _270_out : 1'bz;  // Controlled_Buffer controlled_buffer_46
  or _270 (_270_out, _247_out, _268_out);
  not not_37 (not_37_out, _265_out);
  or _119 (_119_out, _114_out, _120_out);
  assign PB4_o = not_38_out ? _119_out : 1'bz;  // Controlled_Buffer controlled_buffer_47
  not not_38 (not_38_out, _118_out);
  assign PC4_o = not_39_out ? _311_out : 1'bz;  // Controlled_Buffer controlled_buffer_48
  or _311 (_311_out, _310_out, _308_out);
  not not_39 (not_39_out, _306_out);

  // Other names for the same wires on the sheet: VA4_i = VA4; VA3_i = VA3; VA2_i = VA2; VA1_i = VA1; VA7_i = VA7;
  //   VA6_i = VA6; VA5_i = VA5; ZA7_i = ZA7; ZA6_i = ZA6; ZA5_i = ZA5; ZA0_i = ZA0; ZA4_i = ZA4; ZA3_i = ZA3;
  //   ZA2_i = ZA2; ZA1_i = ZA1

  // Notes on the sheet:
  //   23
  //   45
  //   292
  //   76
  //   245
  //   6
  //   NC
  //   2
  //   4
  //   0
  //   NC
  //   1
  //   3
  //   NC
  //   7
  //   5
  //   248
  //   INTERNAL ADDRESS  BUS
  //   INTERNAL DATA BUS
  //   262
  //   4
  //   0
  //   6
  //   2
  //   7
  //   5
  //   1
  //   3
  //   NC
  //   NC
  //   NC
  //   NC
  //   NC
  //   88
  //   256
  //   34
  //   6
  //   0
  //   NC
  //   2
  //   4
  //   7
  //   3
  //   5
  //   1
  //   SEGA 315-5309
  //   665
  //   28
  //   323
  //   144
  //   162
  //   303
  //   298
  //   257
  //   299
  //   309
  //   271
  //   276
  //   317
  //   90
  //   91
  //   147
  //   89
  //   94
  //   204
  //   313
  //   387
  //   253
  //   201
  //   141
  //   MUX141 B3
  //   289
  //   77
  //   290
  //   74
  //   48
  //   43
  //   127
  //   293
  //   199
  //   !
  //   !
  //   !
  //   !
  //   !
  //   !
  //   !
  //   !
  //   !
  //   !
  //   !
  //   !
  //   !
  //   !
  //   !
  //   !
  //   !
  //   !
  //   !
  //   !
  //   !
  //   339
  //   !
  //   !
  //   !
  //   NC
endmodule

// COUNTER 1BIT
module _1_bit_cnt (
  input  C,
  input  CIN,
  input  VAL,
  input  nLD,
  input  nRES,
  output Q,
  output nQ,
  output CO
);

  wire d_ff_1_q, multiplexer_1_out, not_1_out, not_2_out, xor_1_out;

  not not_1 (not_1_out, nRES);
  xor xor_1 (xor_1_out, Q, CIN);
  and and_1 (CO, Q, CIN);
  Multiplexer #(.disabled(0), .enable("false")) multiplexer_1 (
    .in0(VAL), .in1(xor_1_out), .out(multiplexer_1_out), .sel(nLD));
  not not_2 (not_2_out, C);
  D_Flip_Flop #(.trigger("high")) d_ff_1 (
    .clk(C), .D(multiplexer_1_out), .Q(d_ff_1_q), .reset(not_1_out));  // open: Qn, preset, en
  D_Flip_Flop #(.trigger("high")) d_ff_2 (
    .clk(not_2_out), .D(d_ff_1_q), .Q(Q), .Qn(nQ), .reset(not_1_out));  // open: preset, en

  // Notes on the sheet:
  //   C
  //   VAL
  //   LD
  //   /RES
  //   CIN
  //   CNT BIT
  //   Q
  //   nQ
  //   CO
endmodule

module RC_DELAY (
  input  IN,
  output OUT
);

  wire xor_1_out, xor_2_out, xor_3_out, xor_4_out, xor_5_out;

  xor xor_1 (xor_1_out, IN, 1'b0);
  xor xor_2 (xor_2_out, xor_1_out, 1'b0);
  xor xor_3 (xor_3_out, xor_2_out, 1'b0);
  xor xor_4 (xor_4_out, xor_3_out, 1'b0);
  xor xor_5 (xor_5_out, xor_4_out, 1'b0);
  xor xor_6 (OUT, xor_5_out, 1'b0);
endmodule

module S_latch (
  input  EN,
  input  D,
  output Q,
  output nQ
);

  D_Flip_Flop #(.trigger("high")) d_ff_1 (.clk(EN), .D(D), .Q(Q), .Qn(nQ));  // open: preset, en, reset
endmodule

module muxer (
  output VA7,
  output VA6,
  output VA5,
  output VA4,
  output VA3,
  output VA2,
  output VA1,
  output ZD7_o,
  output ZD6_o,
  output ZD5_o,
  output ZD4_o,
  output ZD3_o,
  output ZD2_o,
  output ZD1_o,
  output ZD0_o,
  output VD0_o,
  output VD1_o,
  output VD2_o,
  output VD3_o,
  output VD4_o,
  output VD5_o,
  output VD6_o,
  output VD7_o,
  output VD8_o,
  output VD9_o,
  output VD10_o,
  output VD11_o,
  output VD12_o,
  output VD13_o,
  output VD14_o,
  output VD15_o,
  output ZA1_o,
  output ZA2_o,
  output ZA3_o,
  output ZA4_o,
  output ZA5_o,
  output ZA6_o,
  output ZA7_o
);

  wire _1_out, _2_out, _3_out, _4_out, _67_out, _68_out, _69_out, _70_out, _71_out, _72_out, _73_out,
       _111_out, _125_out, _126_out, _167_out, _198_out, _288_out, _324_out, _338_out, ADR0, ADR1, ADR2,
       ADR3, DB0, DB1, DB2, DB3, DB4, DB5, DB6, DB7, g_340, multiplexer_29_out, MUX_CTRL, nCAS0, nM3, nM3_0,
       not_2_out, not_out, nVTOZ, nZTOV, VA1_i, VA2_i, VA3_i, VA4_i, VA5_i, VA6_i, VA7_i, VD0_i, VD0_o_t,
       VD1_i, VD1_o_t, VD2_i, VD2_o_t, VD3_i, VD3_o_t, VD4_i, VD4_o_t, VD5_i, VD5_o_t, VD6_i, VD6_o_t, VD7_i,
       VD7_o_t, VD8_i, VD9_i, VD10_i, VD11_i, VD12_i, VD13_i, VD14_i, VD15_i, ZA0_i, ZA1_i, ZA2_i, ZA3_i,
       ZA4_i, ZA5_i, ZA6_i, ZA7_i, ZD0_i, ZD1_i, ZD2_i, ZD3_i, ZD4_i, ZD5_i, ZD6_i, ZD7_i;
  wire [0:0] controlled_buffer_1_out;
  wire [2:0] _322_out;
  wire [3:0] multiplexer_1_out, multiplexer_5_out, multiplexer_9_out, multiplexer_13_out, multiplexer_17_out,
       multiplexer_18_out, multiplexer_23_out, multiplexer_24_out, multiplexer_25_out, multiplexer_26_out,
       multiplexer_27_out, multiplexer_28_out;

  Multiplexer #(.select(3), .disabled(0), .enable("false")) multiplexer_1 (
    .out(multiplexer_1_out[0]), .sel(_322_out));  // open: in0, in1, in2, in3, in4, in5, in6, in7
  Multiplexer #(.select(3), .disabled(0), .enable("false")) multiplexer_2 (
    .out(multiplexer_1_out[1]), .sel(_322_out));  // open: in0, in1, in2, in3, in4, in5, in6, in7
  Multiplexer #(.select(3), .disabled(0), .enable("false")) multiplexer_3 (
    .out(multiplexer_1_out[2]), .sel(_322_out));  // open: in0, in1, in2, in3, in4, in5, in6, in7
  Multiplexer #(.select(3), .disabled(0), .enable("false")) multiplexer_4 (
    .out(multiplexer_1_out[3]), .sel(_322_out));  // open: in0, in1, in2, in3, in4, in5, in6, in7
  Multiplexer #(.select(3), .disabled(0), .enable("false")) multiplexer_5 (
    .out(multiplexer_5_out[0]), .sel(_322_out));  // open: in0, in1, in2, in3, in4, in5, in6, in7
  Multiplexer #(.select(3), .disabled(0), .enable("false")) multiplexer_6 (
    .out(multiplexer_5_out[1]), .sel(_322_out));  // open: in0, in1, in2, in3, in4, in5, in6, in7
  Multiplexer #(.select(3), .disabled(0), .enable("false")) multiplexer_7 (
    .out(multiplexer_5_out[2]), .sel(_322_out));  // open: in0, in1, in2, in3, in4, in5, in6, in7
  Multiplexer #(.select(3), .disabled(0), .enable("false")) multiplexer_8 (
    .out(multiplexer_5_out[3]), .sel(_322_out));  // open: in0, in1, in2, in3, in4, in5, in6, in7
  Multiplexer #(.select(3), .disabled(0), .enable("false")) multiplexer_9 (
    .out(multiplexer_9_out[0]), .sel(_322_out));  // open: in0, in1, in2, in3, in4, in5, in6, in7
  Multiplexer #(.select(3), .disabled(0), .enable("false")) multiplexer_10 (
    .out(multiplexer_9_out[1]), .sel(_322_out));  // open: in0, in1, in2, in3, in4, in5, in6, in7
  Multiplexer #(.select(3), .disabled(0), .enable("false")) multiplexer_11 (
    .out(multiplexer_9_out[2]), .sel(_322_out));  // open: in0, in1, in2, in3, in4, in5, in6, in7
  Multiplexer #(.select(3), .disabled(0), .enable("false")) multiplexer_12 (
    .out(multiplexer_9_out[3]), .sel(_322_out));  // open: in0, in1, in2, in3, in4, in5, in6, in7
  Multiplexer #(.select(3), .disabled(0), .enable("false")) multiplexer_13 (
    .out(multiplexer_13_out[0]), .sel(_322_out));  // open: in0, in1, in2, in3, in4, in5, in6, in7
  Multiplexer #(.select(3), .disabled(0), .enable("false")) multiplexer_14 (
    .out(multiplexer_13_out[1]), .sel(_322_out));  // open: in0, in1, in2, in3, in4, in5, in6, in7
  Multiplexer #(.select(3), .disabled(0), .enable("false")) multiplexer_15 (
    .out(multiplexer_13_out[2]), .sel(_322_out));  // open: in0, in1, in2, in3, in4, in5, in6, in7
  Multiplexer #(.select(3), .disabled(0), .enable("false")) multiplexer_16 (
    .out(multiplexer_13_out[3]), .sel(_322_out));  // open: in0, in1, in2, in3, in4, in5, in6, in7
  Multiplexer #(.width(4), .disabled(0), .enable("false")) multiplexer_17 (
    .in0(multiplexer_1_out), .in1(multiplexer_5_out), .out(multiplexer_17_out), .sel(_198_out));
  and _198 (_198_out, nM3, ADR3);
  Multiplexer #(.width(4), .disabled(0), .enable("false")) multiplexer_18 (
    .in0(multiplexer_9_out), .in1(multiplexer_13_out), .out(multiplexer_18_out), .sel(_198_out));
  buf _322 (_322_out[0], _324_out);
  xnor _324 (_324_out, ADR0, nM3);
  buf _135 (_322_out[1], _2_out);
  or _2 (_2_out, _1_out, _3_out);
  buf _163 (_322_out[2], _167_out);
  and _1 (_1_out, nM3, ADR1);
  nor _3 (_3_out, nM3, _4_out);
  and _167 (_167_out, nM3, ADR2);
  Multiplexer #(.width(4), .disabled(0), .enable("false")) multiplexer_19 (
    .in0({ZD4_i, ZD5_i, ZD6_i, ZD7_i}), .in1(multiplexer_17_out), .out({VD4_o_t, VD5_o_t, VD6_o_t, VD7_o_t}),
    .sel(MUX_CTRL));
  Multiplexer #(.width(4), .disabled(0), .enable("false")) multiplexer_20 (
    .in0({ZD0_i, ZD1_i, ZD2_i, ZD3_i}), .in1(multiplexer_18_out), .out({VD0_o_t, VD1_o_t, VD2_o_t, VD3_o_t}),
    .sel(MUX_CTRL));
  not _4 (_4_out, ADR0);
  not _288 (_288_out, nM3_0);
  and _125 (_125_out, nM3_0, _126_out);
  not _126 (_126_out, ZA0_i);
  Multiplexer #(.width(4), .disabled(0), .enable("false")) multiplexer_21 (
    .in0({VD4_i, VD5_i, VD6_i, VD7_i}), .in1({ZD4_i, ZD5_i, ZD6_i, ZD7_i}), .out({DB4, DB5, DB6, DB7}),
    .sel(_288_out));
  Multiplexer #(.width(4), .disabled(0), .enable("false")) multiplexer_22 (
    .in0({VD0_i, VD1_i, VD2_i, VD3_i}), .in1({ZD0_i, ZD1_i, ZD2_i, ZD3_i}), .out({DB0, DB1, DB2, DB3}),
    .sel(_288_out));
  Multiplexer #(.width(4), .disabled(0), .enable("false")) multiplexer_23 (
    .in0({VD4_i, VD5_i, VD6_i, VD7_i}), .in1({VD12_i, VD13_i, VD14_i, VD15_i}), .out(multiplexer_23_out),
    .sel(_125_out));
  Multiplexer #(.width(4), .disabled(0), .enable("false")) multiplexer_24 (
    .in0({VD0_i, VD1_i, VD2_i, VD3_i}), .in1({VD8_i, VD9_i, VD10_i, VD11_i}), .out(multiplexer_24_out),
    .sel(_125_out));
  not _69 (_69_out, nCAS0);
  Multiplexer #(.width(4), .disabled(0), .enable("false")) multiplexer_25 (
    .in0({ZA4_i, ZA5_i, ZA6_i, 1'b0}), .in1({ZA5_i, ZA6_i, ZA7_i, 1'b0}), .out(multiplexer_25_out), .sel(nM3));
  Multiplexer #(.width(4), .disabled(0), .enable("false")) multiplexer_26 (
    .in0({ZA0_i, ZA1_i, ZA2_i, ZA3_i}), .in1({ZA1_i, ZA2_i, ZA3_i, ZA4_i}), .out(multiplexer_26_out),
    .sel(nM3));
  Multiplexer #(.width(4), .disabled(0), .enable("false")) multiplexer_27 (
    .in0(multiplexer_23_out), .in1(multiplexer_17_out), .out(multiplexer_27_out), .sel(MUX_CTRL));
  Multiplexer #(.width(4), .disabled(0), .enable("false")) multiplexer_28 (
    .in0(multiplexer_24_out), .in1(multiplexer_18_out), .out(multiplexer_28_out), .sel(MUX_CTRL));
  or _73 (_73_out, nZTOV, nCAS0);
  or _71 (_71_out, nVTOZ, _69_out);
  or _68 (_68_out, nZTOV, _69_out);
  or _70 (_70_out, nCAS0, nVTOZ);
  nand _111 (_111_out, MUX_CTRL, nM3_0);
  assign {VA5, VA6, VA7, controlled_buffer_1_out[0]} = not_out ? multiplexer_25_out : 4'bz;  // Controlled_Buffer controlled_buffer_1
  not \not  (not_out, nZTOV);
  assign {VA1, VA2, VA3, VA4} = not_out ? multiplexer_26_out : 4'bz;  // Controlled_Buffer controlled_buffer_2
  assign {ZD4_o, ZD5_o, ZD6_o, ZD7_o} = _72_out ? multiplexer_27_out : 4'bz;  // Controlled_Buffer controlled_buffer_3
  assign {ZD0_o, ZD1_o, ZD2_o, ZD3_o} = _72_out ? multiplexer_28_out : 4'bz;  // Controlled_Buffer controlled_buffer_4
  and _72 (_72_out, _73_out, _71_out);
  and _338 (_338_out, nM3_0, _67_out);
  and _67 (_67_out, _68_out, _70_out, _111_out);
  assign VD0_o = _67_out ? VD0_o_t : 1'bz;  // Controlled_Buffer controlled_buffer_5
  assign VD1_o = _67_out ? VD1_o_t : 1'bz;  // Controlled_Buffer controlled_buffer_6
  assign VD2_o = _67_out ? VD2_o_t : 1'bz;  // Controlled_Buffer controlled_buffer_7
  assign VD3_o = _67_out ? VD3_o_t : 1'bz;  // Controlled_Buffer controlled_buffer_8
  assign VD4_o = _67_out ? VD4_o_t : 1'bz;  // Controlled_Buffer controlled_buffer_9
  assign VD5_o = _67_out ? VD5_o_t : 1'bz;  // Controlled_Buffer controlled_buffer_10
  assign VD6_o = _67_out ? VD6_o_t : 1'bz;  // Controlled_Buffer controlled_buffer_11
  assign VD7_o = _67_out ? VD7_o_t : 1'bz;  // Controlled_Buffer controlled_buffer_12
  Multiplexer #(.disabled(0), .enable("false")) multiplexer_29 (
    .in0(g_340), .in1(VD0_o_t), .out(multiplexer_29_out), .sel(nM3_0));
  not not_2 (not_2_out, nVTOZ);
  assign VD8_o = _338_out ? multiplexer_29_out : 1'bz;  // Controlled_Buffer controlled_buffer_13
  assign VD9_o = _338_out ? VD1_o_t : 1'bz;  // Controlled_Buffer controlled_buffer_14
  assign VD10_o = _338_out ? VD2_o_t : 1'bz;  // Controlled_Buffer controlled_buffer_15
  assign VD11_o = _338_out ? VD3_o_t : 1'bz;  // Controlled_Buffer controlled_buffer_16
  assign VD12_o = _338_out ? VD4_o_t : 1'bz;  // Controlled_Buffer controlled_buffer_17
  assign VD13_o = _338_out ? VD5_o_t : 1'bz;  // Controlled_Buffer controlled_buffer_18
  assign VD14_o = _338_out ? VD6_o_t : 1'bz;  // Controlled_Buffer controlled_buffer_19
  assign VD15_o = _338_out ? VD7_o_t : 1'bz;  // Controlled_Buffer controlled_buffer_20
  assign ZA1_o = not_2_out ? VA1_i : 1'bz;  // Controlled_Buffer controlled_buffer_21
  assign ZA2_o = not_2_out ? VA2_i : 1'bz;  // Controlled_Buffer controlled_buffer_22
  assign ZA3_o = not_2_out ? VA3_i : 1'bz;  // Controlled_Buffer controlled_buffer_23
  assign ZA4_o = not_2_out ? VA4_i : 1'bz;  // Controlled_Buffer controlled_buffer_24
  assign ZA5_o = not_2_out ? VA5_i : 1'bz;  // Controlled_Buffer controlled_buffer_25
  assign ZA6_o = not_2_out ? VA6_i : 1'bz;  // Controlled_Buffer controlled_buffer_26
  assign ZA7_o = not_2_out ? VA7_i : 1'bz;  // Controlled_Buffer controlled_buffer_27

  // Notes on the sheet:
  //   303
  //   298
  //   257
  //   299
  //   309
  //   271
  //   276
  //   317
  //   90
  //   91
  //   147
  //   89
  //   94
  //   204
  //   313
  //   387
  //   253
  //   201
  //   323
  //   144
  //   162
  //   289
  //   77
  //   292
  //   76
  //   290
  //   74
  //   43
  //   127
  //   293
  //   199
  //   339
  //   NC
endmodule

// UART A
module UART_A (
  input  DIV0,
  input  DIV1,
  input  DIV2,
  input  DIV3,
  input  DIV4,
  input  DIV5,
  input  DIV6,
  input  PA5_i,
  input  FRES,
  input  FRES0,
  input  FRESM3,
  input  [7:0] DB,
  input  DEC0_1,
  input  DEC1_0,
  input  DEC2_7,
  output [7:0] TXA_o,
  output g_241,
  output g_505,
  output g_155,
  output g_206,
  output g_98,
  output g_93,
  output [7:0] RXA_o,
  output g_152,
  output g_166,
  output g_273,
  output g_151,
  output UCLKA1,
  output UCLKA2
);

  wire _92_q, _92_qn, _97_out, _104_out, _351_out, _352_out, _353_q, _355_q, _358_q, _360_q, _362_nq,
       _364_nq, _365_nq, _366_nq, _367_nq, _368_nq, _369_nq, _370_nq, _433_out, _434_q, _438_q, _442_q,
       _443_q, _491_out, _498_q, _500_out, _504_q, _505_qn, _506_out, _510_out, _520_out, _521_out, _522_qn,
       _523_out, _524_out, _525_out, _529_out, _530_out, _531_out, _533_out, _534_out, _535_q, _535_qn,
       _536_out, _537_out, _538_q, _538_qn, _539_out, _540_out, _541_out, _542_out, _543_q, _543_qn,
       _544_out, _545_out, _546_out, _573_out, _574_out, _575_out, _576_q, _576_qn, _577_q, _596_out,
       _597_out, _598_q, _598_qn, _599_out, _601_out, _603_out, _604_out, _605_out, _606_q, _606_qn,
       _612_out, _613_q, _613_qn, _614_q, _615_out, _621_q, _621_qn, _622_q, _622_qn, _623_out, _624_out,
       _625_out, _626_out, _627_out, _628_out, _629_q, _629_qn, _630_out, _631_out, _632_out, _633_out,
       _634_out, _635_out, _656_out, _657_out, _658_out, _659_q, _659_qn, _660_out, _661_q, _661_qn,
       _662_out, _663_out, _664_out, _680_out, _688_out, _689_out, _690_out, _691_out, _692_out, _693_out,
       _696_out, d_ff_1_q, d_ff_2_q, d_ff_3_q, d_ff_4_q, d_ff_5_q, d_ff_6_q, d_ff_7_q, d_ff_8_q,
       multiplexer_1_out, multiplexer_2_out, multiplexer_3_out, multiplexer_4_out, multiplexer_5_out,
       multiplexer_6_out, multiplexer_7_out, multiplexer_8_out, not_1_out, not_2_out, not_3_out, not_4_out,
       not_5_out, not_6_out, not_7_out, not_8_out, not_9_out, not_10_out, not_11_out, not_12_out, not_13_out,
       not_14_out;

  S_latch _368 (.EN(not_1_out), .D(DB[0]), .Q(TXA_o[0]), .nQ(_368_nq));
  S_latch _369 (.EN(not_1_out), .D(DB[1]), .Q(TXA_o[1]), .nQ(_369_nq));
  S_latch _366 (.EN(not_1_out), .D(DB[2]), .Q(TXA_o[2]), .nQ(_366_nq));
  S_latch _367 (.EN(not_1_out), .D(DB[3]), .Q(TXA_o[3]), .nQ(_367_nq));
  S_latch _362 (.EN(not_1_out), .D(DB[4]), .Q(TXA_o[4]), .nQ(_362_nq));
  S_latch _365 (.EN(not_1_out), .D(DB[5]), .Q(TXA_o[5]), .nQ(_365_nq));
  S_latch _364 (.EN(not_1_out), .D(DB[6]), .Q(TXA_o[6]), .nQ(_364_nq));
  S_latch _370 (.EN(not_1_out), .D(DB[7]), .Q(TXA_o[7]), .nQ(_370_nq));
  not not_1 (not_1_out, DEC2_7);
  D_Flip_Flop _155 (.clk(DEC0_1), .D(DB[3]), .Q(g_155), .reset(not_2_out));  // open: Qn, preset, en
  D_Flip_Flop _152 (.clk(DEC0_1), .D(DB[4]), .Q(g_152), .reset(not_2_out));  // open: Qn, preset, en
  D_Flip_Flop _166 (.clk(DEC0_1), .D(DB[5]), .Q(g_166), .reset(not_2_out));  // open: Qn, preset, en
  D_Flip_Flop _273 (.clk(DEC0_1), .D(DB[6]), .Q(g_273), .reset(not_2_out));  // open: Qn, preset, en
  D_Flip_Flop _151 (.clk(DEC0_1), .D(DB[7]), .Q(g_151), .reset(not_2_out));  // open: Qn, preset, en
  not not_2 (not_2_out, FRESM3);
  not not_3 (not_3_out, _575_out);
  not not_4 (not_4_out, not_3_out);
  Multiplexer #(.disabled(0), .enable("false")) multiplexer_1 (
    .in0(_368_nq), .in1(_355_q), .out(multiplexer_1_out), .sel(not_4_out));
  Multiplexer #(.disabled(0), .enable("false")) multiplexer_2 (
    .in0(_369_nq), .in1(_358_q), .out(multiplexer_2_out), .sel(not_4_out));
  Multiplexer #(.disabled(0), .enable("false")) multiplexer_3 (
    .in0(_366_nq), .in1(_360_q), .out(multiplexer_3_out), .sel(not_4_out));
  Multiplexer #(.disabled(0), .enable("false")) multiplexer_4 (
    .in0(_367_nq), .in1(_434_q), .out(multiplexer_4_out), .sel(not_4_out));
  Multiplexer #(.disabled(0), .enable("false")) multiplexer_5 (
    .in0(_362_nq), .in1(_438_q), .out(multiplexer_5_out), .sel(not_4_out));
  Multiplexer #(.disabled(0), .enable("false")) multiplexer_6 (
    .in0(_365_nq), .in1(_443_q), .out(multiplexer_6_out), .sel(not_4_out));
  Multiplexer #(.disabled(0), .enable("false")) multiplexer_7 (
    .in0(_364_nq), .in1(_442_q), .out(multiplexer_7_out), .sel(not_4_out));
  Multiplexer #(.disabled(0), .enable("false")) multiplexer_8 (
    .in0(_370_nq), .in1(1'b0), .out(multiplexer_8_out), .sel(not_4_out));
  or _433 (_433_out, UCLKA1, 1'b0);
  Multiplexer #(.select(2), .disabled(0), .enable("false")) multiplexer_9 (
    .in0(DIV0), .in1(DIV1), .in2(DIV2), .in3(DIV3), .out(UCLKA2), .sel({g_273, g_151}));
  Multiplexer #(.select(2), .disabled(0), .enable("false")) multiplexer_10 (
    .in0(DIV3), .in1(DIV4), .in2(DIV5), .in3(DIV6), .out(UCLKA1), .sel({g_273, g_151}));
  D_Flip_Flop _353 (.clk(_433_out), .D(multiplexer_1_out), .Q(_353_q), .reset(not_5_out));  // open: Qn, preset, en
  D_Flip_Flop _355 (.clk(_433_out), .D(multiplexer_2_out), .Q(_355_q), .reset(not_5_out));  // open: Qn, preset, en
  D_Flip_Flop _358 (.clk(_433_out), .D(multiplexer_3_out), .Q(_358_q), .reset(not_5_out));  // open: Qn, preset, en
  D_Flip_Flop _360 (.clk(_433_out), .D(multiplexer_4_out), .Q(_360_q), .reset(not_5_out));  // open: Qn, preset, en
  D_Flip_Flop _434 (.clk(_433_out), .D(multiplexer_5_out), .Q(_434_q), .reset(not_5_out));  // open: Qn, preset, en
  D_Flip_Flop _438 (.clk(_433_out), .D(multiplexer_6_out), .Q(_438_q), .reset(not_5_out));  // open: Qn, preset, en
  D_Flip_Flop _443 (.clk(_433_out), .D(multiplexer_7_out), .Q(_443_q), .reset(not_5_out));  // open: Qn, preset, en
  D_Flip_Flop _442 (.clk(_433_out), .D(multiplexer_8_out), .Q(_442_q), .reset(not_5_out));  // open: Qn, preset, en
  and _351 (_351_out, _575_out, _352_out);
  not _352 (_352_out, _353_q);
  not not_5 (not_5_out, g_152);
  not _596 (_596_out, _521_out);
  D_Flip_Flop _241 (.clk(UCLKA1), .D(_351_out), .Q(g_241), .preset(not_5_out));  // open: Qn, en, reset
  not not_6 (not_6_out, _510_out);
  buf _510 (_510_out, FRES);
  nand _605 (_605_out, _606_q, _659_q);
  nand _603 (_603_out, _606_q, _661_q);
  nand _601 (_601_out, _606_q, _598_qn);
  nand _599 (_599_out, _659_qn, _606_qn, _661_qn, _598_q);
  nand _662 (_662_out, _598_q, _661_qn);
  nand _664 (_664_out, _661_q, _598_qn);
  nand _656 (_656_out, _661_q, _659_q);
  nand _660 (_660_out, _598_q, _661_qn, _659_qn);
  nand _657 (_657_out, _598_qn, _659_q);
  nor _597 (_597_out, _598_q, _521_out);
  or _523 (_523_out, _606_q, _521_out);
  or _525 (_525_out, _521_out, _522_qn);
  D_Flip_Flop _606 (.clk(UCLKA2), .D(_604_out), .Q(_606_q), .Qn(_606_qn), .preset(not_6_out));  // open: en, reset
  nand _604 (_604_out, _605_out, _603_out, _601_out, _599_out, _596_out, 1'b1);
  nand _663 (_663_out, _596_out, _662_out, _664_out);
  nand _658 (_658_out, _596_out, _656_out, _660_out, _657_out);
  nand _524 (_524_out, _523_out, _525_out);
  D_Flip_Flop _661 (.clk(UCLKA2), .D(_663_out), .Q(_661_q), .Qn(_661_qn), .preset(not_6_out));  // open: en, reset
  buf _491 (_491_out, FRES);
  nand _628 (_628_out, _621_qn, _622_q, _629_qn, _576_q);
  nand _623 (_623_out, _621_q, _622_q);
  nand _627 (_627_out, _629_q, _622_q);
  nand _626 (_626_out, _629_q, _621_q);
  nand _573 (_573_out, _577_q, _629_qn, _622_qn);
  nand _635 (_635_out, _622_q, _576_q, _621_q);
  nand _630 (_630_out, _629_q, _621_q, _622_qn);
  nand _633 (_633_out, _576_q, _629_q, _622_q);
  nand _631 (_631_out, _629_qn, _622_q);
  nand _574 (_574_out, _576_qn, _621_qn, _622_q, _629_qn);
  nand _575 (_575_out, 1'b1, _621_qn, _576_qn, _577_q, _629_qn, _622_qn);
  D_Flip_Flop _659 (.clk(UCLKA2), .D(_658_out), .Q(_659_q), .Qn(_659_qn), .preset(not_6_out));  // open: en, reset
  not not_7 (not_7_out, _491_out);
  not _500 (_500_out, _575_out);
  not _506 (_506_out, UCLKA1);
  not not_8 (not_8_out, FRES0);
  not not_9 (not_9_out, DEC2_7);
  D_Flip_Flop _622 (.clk(UCLKA1), .D(_624_out), .Q(_622_q), .Qn(_622_qn), .preset(not_7_out));  // open: en, reset
  nand _624 (_624_out, _628_out, _623_out, _627_out, _626_out);
  nand _625 (_625_out, _626_out, _628_out, _573_out);
  nand _634 (_634_out, _635_out, _573_out, _630_out, _633_out);
  nand _632 (_632_out, _573_out, _630_out, _631_out);
  D_Flip_Flop _598 (.clk(UCLKA2), .D(_597_out), .Q(_598_q), .Qn(_598_qn), .reset(not_6_out));  // open: preset, en
  D_Flip_Flop _522 (.clk(UCLKA2), .D(_524_out), .Qn(_522_qn), .reset(not_6_out));  // open: Q, preset, en
  nor _521 (_521_out, _522_qn, _92_q, _520_out);
  J_K_Flip_Flop #(.trigger("falling")) _505 (
    .J(_500_out), .clk(_506_out), .K(1'b0), .Q(g_505), .Qn(_505_qn), .preset(not_9_out), .reset(not_8_out));  // open: en
  not not_10 (not_10_out, _505_qn);
  D_Flip_Flop _621 (.clk(UCLKA1), .D(_625_out), .Q(_621_q), .Qn(_621_qn), .preset(not_7_out));  // open: en, reset
  D_Flip_Flop _504 (.clk(_498_q), .D(1'b0), .Q(_504_q), .preset(not_10_out), .reset(not_8_out));  // open: Qn, en
  D_Flip_Flop _576 (.clk(UCLKA1), .D(_634_out), .Q(_576_q), .Qn(_576_qn), .preset(not_7_out));  // open: en, reset
  not _529 (_529_out, _92_q);
  D_Flip_Flop _629 (.clk(UCLKA1), .D(_632_out), .Q(_629_q), .Qn(_629_qn), .reset(not_7_out));  // open: preset, en
  D_Flip_Flop _577 (.clk(UCLKA2), .D(_504_q), .Q(_577_q));  // open: Qn, preset, en, reset
  D_Flip_Flop _498 (.clk(UCLKA1), .D(_574_out), .Q(_498_q), .reset(not_7_out));  // open: Qn, preset, en
  not not_11 (not_11_out, _612_out);
  buf _612 (_612_out, FRES);
  nand _545 (_545_out, _613_q, _538_q, _543_q);
  nand _546 (_546_out, _535_q, _543_q, _613_q);
  nand _531 (_531_out, _529_out, _522_qn, _535_qn, _613_qn);
  nand _541 (_541_out, _613_q, _535_qn, _543_q, _538_qn);
  nand _537 (_537_out, _613_q, _538_q, _535_qn);
  nand _540 (_540_out, _613_q, _535_q, _538_q);
  nand _534 (_534_out, _535_q, _613_q);
  nand _542 (_542_out, _613_q, _535_qn, _543_qn, _538_qn);
  not _520 (_520_out, _530_out);
  and _530 (_530_out, _535_qn, _613_qn);
  D_Flip_Flop _543 (.clk(_606_qn), .D(_544_out), .Q(_543_q), .Qn(_543_qn), .reset(not_11_out));  // open: preset, en
  nand _544 (_544_out, _545_out, _546_out, _531_out, _542_out);
  nand _536 (_536_out, _542_out, _541_out, _531_out, _537_out);
  nand _539 (_539_out, _542_out, _541_out, _540_out, _531_out);
  nand _533 (_533_out, _541_out, _531_out, _534_out, _537_out);
  D_Flip_Flop _92 (.clk(UCLKA2), .D(PA5_i), .Q(_92_q), .Qn(_92_qn), .preset(not_12_out));  // open: en, reset
  D_Flip_Flop _535 (.clk(_606_qn), .D(_536_out), .Q(_535_q), .Qn(_535_qn), .reset(not_11_out));  // open: preset, en
  and _97 (_97_out, 1'b1, _92_q);
  not not_12 (not_12_out, g_166);
  D_Flip_Flop _538 (.clk(_606_qn), .D(_539_out), .Q(_538_q), .Qn(_538_qn), .reset(not_11_out));  // open: preset, en
  D_Flip_Flop d_ff_1 (.clk(_606_qn), .D(_97_out), .Q(d_ff_1_q), .reset(not_12_out));  // open: Qn, preset, en
  D_Flip_Flop d_ff_2 (.clk(_606_qn), .D(d_ff_1_q), .Q(d_ff_2_q), .reset(not_12_out));  // open: Qn, preset, en
  D_Flip_Flop d_ff_3 (.clk(_606_qn), .D(d_ff_2_q), .Q(d_ff_3_q), .reset(not_12_out));  // open: Qn, preset, en
  D_Flip_Flop d_ff_4 (.clk(_606_qn), .D(d_ff_3_q), .Q(d_ff_4_q), .reset(not_12_out));  // open: Qn, preset, en
  D_Flip_Flop d_ff_5 (.clk(_606_qn), .D(d_ff_4_q), .Q(d_ff_5_q), .reset(not_12_out));  // open: Qn, preset, en
  D_Flip_Flop d_ff_6 (.clk(_606_qn), .D(d_ff_5_q), .Q(d_ff_6_q), .reset(not_12_out));  // open: Qn, preset, en
  D_Flip_Flop d_ff_7 (.clk(_606_qn), .D(d_ff_6_q), .Q(d_ff_7_q), .reset(not_12_out));  // open: Qn, preset, en
  D_Flip_Flop d_ff_8 (.clk(_606_qn), .D(d_ff_7_q), .Q(d_ff_8_q), .reset(not_12_out));  // open: Qn, preset, en
  D_Flip_Flop _613 (.clk(_606_qn), .D(_533_out), .Q(_613_q), .Qn(_613_qn), .reset(not_11_out));  // open: preset, en
  RC_DELAY _693 (.IN(d_ff_1_q), .OUT(_693_out));
  RC_DELAY _690 (.IN(d_ff_2_q), .OUT(_690_out));
  RC_DELAY _688 (.IN(d_ff_3_q), .OUT(_688_out));
  RC_DELAY _696 (.IN(d_ff_4_q), .OUT(_696_out));
  RC_DELAY _692 (.IN(d_ff_5_q), .OUT(_692_out));
  RC_DELAY _691 (.IN(d_ff_6_q), .OUT(_691_out));
  RC_DELAY _689 (.IN(d_ff_7_q), .OUT(_689_out));
  RC_DELAY _680 (.IN(d_ff_8_q), .OUT(_680_out));
  and _104 (_104_out, DEC1_0, FRES0);
  D_Flip_Flop _614 (.clk(_606_qn), .D(_542_out), .Q(_614_q), .preset(not_11_out));  // open: Qn, en, reset
  not not_13 (not_13_out, _104_out);
  or _615 (_615_out, _606_qn, _614_q);
  D_Flip_Flop _98 (.clk(_615_out), .D(1'b1), .Q(g_98), .reset(not_13_out));  // open: Qn, preset, en
  D_Flip_Flop _93 (.clk(_615_out), .D(_92_qn), .Q(g_93), .reset(not_13_out));  // open: Qn, preset, en
  D_Flip_Flop _100 (.clk(_615_out), .D(_693_out), .Q(RXA_o[7]), .reset(not_14_out));  // open: Qn, preset, en
  D_Flip_Flop _106 (.clk(_615_out), .D(_690_out), .Q(RXA_o[6]), .reset(not_14_out));  // open: Qn, preset, en
  D_Flip_Flop _214 (.clk(_615_out), .D(_688_out), .Q(RXA_o[5]), .reset(not_14_out));  // open: Qn, preset, en
  D_Flip_Flop _213 (.clk(_615_out), .D(_696_out), .Q(RXA_o[4]), .reset(not_14_out));  // open: Qn, preset, en
  D_Flip_Flop _99 (.clk(_615_out), .D(_692_out), .Q(RXA_o[3]), .reset(not_14_out));  // open: Qn, preset, en
  D_Flip_Flop _105 (.clk(_615_out), .D(_691_out), .Q(RXA_o[2]), .reset(not_14_out));  // open: Qn, preset, en
  D_Flip_Flop _281 (.clk(_615_out), .D(_689_out), .Q(RXA_o[1]), .reset(not_14_out));  // open: Qn, preset, en
  D_Flip_Flop _389 (.clk(_615_out), .D(_680_out), .Q(RXA_o[0]), .reset(not_14_out));  // open: Qn, preset, en
  not not_14 (not_14_out, 1'b1);
  and _206 (g_206, g_155, g_98);

  // Other names for the same wires on the sheet: DIV1_t = DIV2; DIV2_t = DIV1; DIV4_t = DIV5; DIV5_t = DIV4

  // Notes on the sheet:
  //   363
  //   294
  //   294
  //   499
  //   430
  //   356
  //   357
  //   361
  //   359
  //   435
  //   439
  //   441
  //   440
  //   B
  //   A
  //   !
  //   NEGEDGE
  //   !
  //   SIPO SR 4bit
  //   SIPO SR 4bit
  //   102
  //   103
  //   387 B
  //   313 B
  //   204 B
endmodule

// UART B
module UART_B (
  input  DIV0,
  input  DIV1,
  input  DIV2,
  input  DIV3,
  input  DIV4,
  input  DIV5,
  input  DIV6,
  input  PB5_i,
  input  FRES,
  input  FRES0,
  input  FRESM3,
  input  [7:0] DB,
  input  DEC0_2,
  input  DEC0_4,
  input  DEC1_3,
  output [7:0] TXB_o,
  output g_113,
  output g_354,
  output g_156,
  output g_207,
  output g_215,
  output g_211,
  output [7:0] RXB_o,
  output g_47,
  output g_165,
  output g_277,
  output g_321,
  output UCLKB1,
  output UCLKB2
);

  wire _175_out, _176_out, _177_q, _179_q, _182_q, _212_q, _212_qn, _217_out, _218_out, _219_out, _220_qn,
       _221_out, _222_out, _223_out, _224_out, _225_out, _226_out, _229_q, _231_q, _234_q, _236_q, _246_nq,
       _249_nq, _250_nq, _251_nq, _252_nq, _297_nq, _304_nq, _319_nq, _342_out, _344_q, _348_out, _349_out,
       _354_qn, _393_out, _394_out, _395_out, _408_q, _409_out, _410_q, _410_qn, _411_q, _411_qn, _412_out,
       _413_out, _414_q, _414_qn, _415_out, _416_q, _416_qn, _417_out, _418_q, _418_qn, _419_q, _420_out,
       _426_q, _429_q, _463_q, _463_qn, _464_q, _464_qn, _465_out, _466_q, _466_qn, _468_q, _468_qn,
       _469_out, _470_out, _471_out, _472_out, _473_out, _474_out, _475_out, _476_out, _477_out, _478_out,
       _479_out, _480_out, _481_out, _482_out, _483_out, _484_out, _485_out, _547_out, _548_out, _549_out,
       _550_out, _551_out, _552_out, _553_out, _554_out, _555_out, _556_out, _557_q, _557_qn, _558_out,
       _559_q, _559_qn, _560_out, _561_out, _562_out, _563_out, _616_q, _616_qn, _617_out, _618_out,
       _619_out, _676_out, _677_out, _681_out, _682_out, _684_out, _694_out, _695_out, _697_out, d_ff_1_q,
       d_ff_2_q, d_ff_3_q, d_ff_4_q, d_ff_5_q, d_ff_6_q, d_ff_7_q, d_ff_8_q, multiplexer_1_out,
       multiplexer_2_out, multiplexer_3_out, multiplexer_4_out, multiplexer_5_out, multiplexer_6_out,
       multiplexer_7_out, multiplexer_8_out, not_1_out, not_2_out, not_3_out, not_4_out, not_5_out,
       not_6_out, not_7_out, not_8_out, not_9_out, not_10_out, not_11_out, not_12_out, not_13_out, not_14_out;

  S_latch _249 (.EN(not_1_out), .D(DB[0]), .Q(TXB_o[0]), .nQ(_249_nq));
  S_latch _304 (.EN(not_1_out), .D(DB[1]), .Q(TXB_o[1]), .nQ(_304_nq));
  S_latch _250 (.EN(not_1_out), .D(DB[2]), .Q(TXB_o[2]), .nQ(_250_nq));
  S_latch _246 (.EN(not_1_out), .D(DB[3]), .Q(TXB_o[3]), .nQ(_246_nq));
  S_latch _252 (.EN(not_1_out), .D(DB[4]), .Q(TXB_o[4]), .nQ(_252_nq));
  S_latch _319 (.EN(not_1_out), .D(DB[5]), .Q(TXB_o[5]), .nQ(_319_nq));
  S_latch _251 (.EN(not_1_out), .D(DB[6]), .Q(TXB_o[6]), .nQ(_251_nq));
  S_latch _297 (.EN(not_1_out), .D(DB[7]), .Q(TXB_o[7]), .nQ(_297_nq));
  not not_1 (not_1_out, DEC0_2);
  D_Flip_Flop _156 (.clk(DEC0_4), .D(DB[3]), .Q(g_156), .reset(not_2_out));  // open: Qn, preset, en
  D_Flip_Flop _47 (.clk(DEC0_4), .D(DB[4]), .Q(g_47), .reset(not_2_out));  // open: Qn, preset, en
  D_Flip_Flop _165 (.clk(DEC0_4), .D(DB[5]), .Q(g_165), .reset(not_2_out));  // open: Qn, preset, en
  D_Flip_Flop _277 (.clk(DEC0_4), .D(DB[6]), .Q(g_277), .reset(not_2_out));  // open: Qn, preset, en
  D_Flip_Flop _321 (.clk(DEC0_4), .D(DB[7]), .Q(g_321), .reset(not_2_out));  // open: Qn, preset, en
  not not_2 (not_2_out, FRESM3);
  not not_3 (not_3_out, _412_out);
  not not_4 (not_4_out, not_3_out);
  Multiplexer #(.disabled(0), .enable("false")) multiplexer_1 (
    .in0(_249_nq), .in1(_179_q), .out(multiplexer_1_out), .sel(not_4_out));
  Multiplexer #(.disabled(0), .enable("false")) multiplexer_2 (
    .in0(_304_nq), .in1(_182_q), .out(multiplexer_2_out), .sel(not_4_out));
  Multiplexer #(.disabled(0), .enable("false")) multiplexer_3 (
    .in0(_250_nq), .in1(_229_q), .out(multiplexer_3_out), .sel(not_4_out));
  Multiplexer #(.disabled(0), .enable("false")) multiplexer_4 (
    .in0(_246_nq), .in1(_231_q), .out(multiplexer_4_out), .sel(not_4_out));
  Multiplexer #(.disabled(0), .enable("false")) multiplexer_5 (
    .in0(_252_nq), .in1(_234_q), .out(multiplexer_5_out), .sel(not_4_out));
  Multiplexer #(.disabled(0), .enable("false")) multiplexer_6 (
    .in0(_319_nq), .in1(_236_q), .out(multiplexer_6_out), .sel(not_4_out));
  Multiplexer #(.disabled(0), .enable("false")) multiplexer_7 (
    .in0(_251_nq), .in1(_344_q), .out(multiplexer_7_out), .sel(not_4_out));
  Multiplexer #(.disabled(0), .enable("false")) multiplexer_8 (
    .in0(_297_nq), .in1(1'b0), .out(multiplexer_8_out), .sel(not_4_out));
  or _342 (_342_out, UCLKB1, 1'b0);
  Multiplexer #(.select(2), .disabled(0), .enable("false")) multiplexer_9 (
    .in0(DIV0), .in1(DIV1), .in2(DIV2), .in3(DIV3), .out(UCLKB2), .sel({g_277, g_321}));
  Multiplexer #(.select(2), .disabled(0), .enable("false")) multiplexer_10 (
    .in0(DIV3), .in1(DIV4), .in2(DIV5), .in3(DIV6), .out(UCLKB1), .sel({g_277, g_321}));
  D_Flip_Flop _177 (.clk(_342_out), .D(multiplexer_1_out), .Q(_177_q), .reset(not_5_out));  // open: Qn, preset, en
  D_Flip_Flop _179 (.clk(_342_out), .D(multiplexer_2_out), .Q(_179_q), .reset(not_5_out));  // open: Qn, preset, en
  D_Flip_Flop _182 (.clk(_342_out), .D(multiplexer_3_out), .Q(_182_q), .reset(not_5_out));  // open: Qn, preset, en
  D_Flip_Flop _229 (.clk(_342_out), .D(multiplexer_4_out), .Q(_229_q), .reset(not_5_out));  // open: Qn, preset, en
  D_Flip_Flop _231 (.clk(_342_out), .D(multiplexer_5_out), .Q(_231_q), .reset(not_5_out));  // open: Qn, preset, en
  D_Flip_Flop _234 (.clk(_342_out), .D(multiplexer_6_out), .Q(_234_q), .reset(not_5_out));  // open: Qn, preset, en
  D_Flip_Flop _236 (.clk(_342_out), .D(multiplexer_7_out), .Q(_236_q), .reset(not_5_out));  // open: Qn, preset, en
  D_Flip_Flop _344 (.clk(_342_out), .D(multiplexer_8_out), .Q(_344_q), .reset(not_5_out));  // open: Qn, preset, en
  and _175 (_175_out, _412_out, _176_out);
  not _176 (_176_out, _177_q);
  not not_5 (not_5_out, g_47);
  not _470 (_470_out, _224_out);
  D_Flip_Flop _113 (.clk(UCLKB1), .D(_175_out), .Q(g_113), .preset(not_5_out));  // open: Qn, en, reset
  not not_6 (not_6_out, _395_out);
  buf _395 (_395_out, FRES);
  nand _472 (_472_out, _410_q, _464_q);
  nand _473 (_473_out, _410_q, _463_q);
  nand _474 (_474_out, _410_q, _468_qn);
  nand _465 (_465_out, _464_qn, _410_qn, _463_qn, _468_q);
  nand _551 (_551_out, _468_q, _463_qn);
  nand _552 (_552_out, _463_q, _468_qn);
  nand _548 (_548_out, _463_q, _464_q);
  nand _550 (_550_out, _468_q, _463_qn, _464_qn);
  nand _549 (_549_out, _468_qn, _464_q);
  nor _469 (_469_out, _468_q, _224_out);
  or _223 (_223_out, _410_q, _224_out);
  or _222 (_222_out, _224_out, _220_qn);
  D_Flip_Flop _410 (.clk(UCLKB2), .D(_471_out), .Q(_410_q), .Qn(_410_qn), .preset(not_6_out));  // open: en, reset
  nand _471 (_471_out, _472_out, _473_out, _474_out, _465_out, _470_out, 1'b1);
  nand _553 (_553_out, _470_out, _551_out, _552_out);
  nand _547 (_547_out, _470_out, _548_out, _550_out, _549_out);
  nand _221 (_221_out, _223_out, _222_out);
  D_Flip_Flop _463 (.clk(UCLKB2), .D(_553_out), .Q(_463_q), .Qn(_463_qn), .preset(not_6_out));  // open: en, reset
  buf _420 (_420_out, FRES);
  nand _415 (_415_out, _414_qn, _411_q, _418_qn, _416_q);
  nand _478 (_478_out, _414_q, _411_q);
  nand _477 (_477_out, _418_q, _411_q);
  nand _479 (_479_out, _418_q, _414_q);
  nand _413 (_413_out, _429_q, _418_qn, _411_qn);
  nand _485 (_485_out, _411_q, _416_q, _414_q);
  nand _480 (_480_out, _418_q, _414_q, _411_qn);
  nand _484 (_484_out, _416_q, _418_q, _411_q);
  nand _481 (_481_out, _418_qn, _411_q);
  nand _417 (_417_out, _416_qn, _414_qn, _411_q, _418_qn);
  nand _412 (_412_out, 1'b1, _414_qn, _416_qn, _429_q, _418_qn, _411_qn);
  D_Flip_Flop _464 (.clk(UCLKB2), .D(_547_out), .Q(_464_q), .Qn(_464_qn), .preset(not_6_out));  // open: en, reset
  not not_7 (not_7_out, _420_out);
  not _348 (_348_out, _412_out);
  not _349 (_349_out, UCLKB1);
  not not_8 (not_8_out, FRES0);
  not not_9 (not_9_out, DEC0_2);
  D_Flip_Flop _411 (.clk(UCLKB1), .D(_476_out), .Q(_411_q), .Qn(_411_qn), .preset(not_7_out));  // open: en, reset
  nand _476 (_476_out, _415_out, _478_out, _477_out, _479_out);
  nand _475 (_475_out, _479_out, _415_out, _413_out);
  nand _483 (_483_out, _485_out, _413_out, _480_out, _484_out);
  nand _482 (_482_out, _413_out, _480_out, _481_out);
  D_Flip_Flop _468 (.clk(UCLKB2), .D(_469_out), .Q(_468_q), .Qn(_468_qn), .reset(not_6_out));  // open: preset, en
  D_Flip_Flop _220 (.clk(UCLKB2), .D(_221_out), .Qn(_220_qn), .reset(not_6_out));  // open: Q, preset, en
  nor _224 (_224_out, _220_qn, _212_q, _225_out);
  J_K_Flip_Flop #(.trigger("falling")) _354 (
    .J(_348_out), .clk(_349_out), .K(1'b0), .Q(g_354), .Qn(_354_qn), .preset(not_9_out), .reset(not_8_out));  // open: en
  not not_10 (not_10_out, _354_qn);
  D_Flip_Flop _414 (.clk(UCLKB1), .D(_475_out), .Q(_414_q), .Qn(_414_qn), .preset(not_7_out));  // open: en, reset
  D_Flip_Flop _426 (.clk(_419_q), .D(1'b0), .Q(_426_q), .preset(not_10_out), .reset(not_8_out));  // open: Qn, en
  D_Flip_Flop _416 (.clk(UCLKB1), .D(_483_out), .Q(_416_q), .Qn(_416_qn), .preset(not_7_out));  // open: en, reset
  not _226 (_226_out, _212_q);
  D_Flip_Flop _418 (.clk(UCLKB1), .D(_482_out), .Q(_418_q), .Qn(_418_qn), .reset(not_7_out));  // open: preset, en
  D_Flip_Flop _429 (.clk(UCLKB2), .D(_426_q), .Q(_429_q));  // open: Qn, preset, en, reset
  D_Flip_Flop _419 (.clk(UCLKB1), .D(_417_out), .Q(_419_q), .reset(not_7_out));  // open: Qn, preset, en
  buf _393 (_393_out, FRES);
  not not_11 (not_11_out, _393_out);
  nand _618 (_618_out, _466_q, _559_q, _616_q);
  nand _619 (_619_out, _557_q, _616_q, _466_q);
  nand _218 (_218_out, _226_out, _220_qn, _557_qn, _466_qn);
  nand _555 (_555_out, _466_q, _557_qn, _616_q, _559_qn);
  nand _556 (_556_out, _466_q, _559_q, _557_qn);
  nand _562 (_562_out, _466_q, _557_q, _559_q);
  nand _563 (_563_out, _557_q, _466_q);
  nand _554 (_554_out, _466_q, _557_qn, _616_qn, _559_qn);
  not _225 (_225_out, _219_out);
  and _219 (_219_out, _557_qn, _466_qn);
  D_Flip_Flop _616 (.clk(_410_qn), .D(_617_out), .Q(_616_q), .Qn(_616_qn), .reset(not_11_out));  // open: preset, en
  nand _617 (_617_out, _618_out, _619_out, _218_out, _554_out);
  nand _558 (_558_out, _554_out, _555_out, _218_out, _556_out);
  nand _560 (_560_out, _554_out, _555_out, _562_out, _218_out);
  nand _561 (_561_out, _555_out, _218_out, _563_out, _556_out);
  D_Flip_Flop _212 (.clk(UCLKB2), .D(PB5_i), .Q(_212_q), .Qn(_212_qn), .preset(not_12_out));  // open: en, reset
  D_Flip_Flop _557 (.clk(_410_qn), .D(_558_out), .Q(_557_q), .Qn(_557_qn), .reset(not_11_out));  // open: preset, en
  and _394 (_394_out, 1'b1, _212_q);
  not not_12 (not_12_out, g_165);
  D_Flip_Flop _559 (.clk(_410_qn), .D(_560_out), .Q(_559_q), .Qn(_559_qn), .reset(not_11_out));  // open: preset, en
  D_Flip_Flop d_ff_1 (.clk(_410_qn), .D(_394_out), .Q(d_ff_1_q), .reset(not_12_out));  // open: Qn, preset, en
  D_Flip_Flop d_ff_2 (.clk(_410_qn), .D(d_ff_1_q), .Q(d_ff_2_q), .reset(not_12_out));  // open: Qn, preset, en
  D_Flip_Flop d_ff_3 (.clk(_410_qn), .D(d_ff_2_q), .Q(d_ff_3_q), .reset(not_12_out));  // open: Qn, preset, en
  D_Flip_Flop d_ff_4 (.clk(_410_qn), .D(d_ff_3_q), .Q(d_ff_4_q), .reset(not_12_out));  // open: Qn, preset, en
  D_Flip_Flop d_ff_5 (.clk(_410_qn), .D(d_ff_4_q), .Q(d_ff_5_q), .reset(not_12_out));  // open: Qn, preset, en
  D_Flip_Flop d_ff_6 (.clk(_410_qn), .D(d_ff_5_q), .Q(d_ff_6_q), .reset(not_12_out));  // open: Qn, preset, en
  D_Flip_Flop d_ff_7 (.clk(_410_qn), .D(d_ff_6_q), .Q(d_ff_7_q), .reset(not_12_out));  // open: Qn, preset, en
  D_Flip_Flop d_ff_8 (.clk(_410_qn), .D(d_ff_7_q), .Q(d_ff_8_q), .reset(not_12_out));  // open: Qn, preset, en
  D_Flip_Flop _466 (.clk(_410_qn), .D(_561_out), .Q(_466_q), .Qn(_466_qn), .reset(not_11_out));  // open: preset, en
  RC_DELAY _677 (.IN(d_ff_1_q), .OUT(_677_out));
  RC_DELAY _684 (.IN(d_ff_2_q), .OUT(_684_out));
  RC_DELAY _676 (.IN(d_ff_3_q), .OUT(_676_out));
  RC_DELAY _681 (.IN(d_ff_4_q), .OUT(_681_out));
  RC_DELAY _694 (.IN(d_ff_5_q), .OUT(_694_out));
  RC_DELAY _697 (.IN(d_ff_6_q), .OUT(_697_out));
  RC_DELAY _682 (.IN(d_ff_7_q), .OUT(_682_out));
  RC_DELAY _695 (.IN(d_ff_8_q), .OUT(_695_out));
  and _217 (_217_out, DEC1_3, FRES0);
  D_Flip_Flop _408 (.clk(_410_qn), .D(_554_out), .Q(_408_q), .preset(not_11_out));  // open: Qn, en, reset
  not not_13 (not_13_out, _217_out);
  or _409 (_409_out, _410_qn, _408_q);
  D_Flip_Flop _215 (.clk(_409_out), .D(1'b1), .Q(g_215), .reset(not_13_out));  // open: Qn, preset, en
  D_Flip_Flop _211 (.clk(_409_out), .D(_212_qn), .Q(g_211), .reset(not_13_out));  // open: Qn, preset, en
  D_Flip_Flop _390 (.clk(_409_out), .D(_677_out), .Q(RXB_o[7]), .reset(not_14_out));  // open: Qn, preset, en
  D_Flip_Flop _274 (.clk(_409_out), .D(_684_out), .Q(RXB_o[6]), .reset(not_14_out));  // open: Qn, preset, en
  D_Flip_Flop _391 (.clk(_409_out), .D(_676_out), .Q(RXB_o[5]), .reset(not_14_out));  // open: Qn, preset, en
  D_Flip_Flop _318 (.clk(_409_out), .D(_681_out), .Q(RXB_o[4]), .reset(not_14_out));  // open: Qn, preset, en
  D_Flip_Flop _216 (.clk(_409_out), .D(_694_out), .Q(RXB_o[3]), .reset(not_14_out));  // open: Qn, preset, en
  D_Flip_Flop _202 (.clk(_409_out), .D(_697_out), .Q(RXB_o[2]), .reset(not_14_out));  // open: Qn, preset, en
  D_Flip_Flop _315 (.clk(_409_out), .D(_682_out), .Q(RXB_o[1]), .reset(not_14_out));  // open: Qn, preset, en
  D_Flip_Flop _208 (.clk(_409_out), .D(_695_out), .Q(RXB_o[0]), .reset(not_14_out));  // open: Qn, preset, en
  not not_14 (not_14_out, 1'b1);
  and _207 (g_207, g_156, g_215);

  // Other names for the same wires on the sheet: DIV1_t = DIV2; DIV2_t = DIV1; DIV4_t = DIV5; DIV5_t = DIV4

  // Notes on the sheet:
  //   388
  //   295
  //   295
  //   228
  //   180
  //   178
  //   181
  //   232
  //   230
  //   233
  //   235
  //   291
  //   343
  //   B
  //   A
  //   !
  //   NEGEDGE
  //   !
  //   SIPO SR 4bit
  //   SIPO SR 4bit
  //   392
  //   209
endmodule

// UART C
module UART_C (
  input  DIV0,
  input  DIV1,
  input  DIV2,
  input  DIV3,
  input  DIV4,
  input  DIV5,
  input  DIV6,
  input  PC5_i,
  input  FRES,
  input  FRES0,
  input  FRESM3,
  input  [7:0] DB,
  input  DEC0_5,
  input  DEC0_7,
  input  DEC1_6,
  output [7:0] TXC_o,
  output g_371,
  output g_456,
  output g_95,
  output g_205,
  output g_280,
  output g_272,
  output [7:0] RXC_o,
  output g_48,
  output g_159,
  output g_314,
  output g_312,
  output UCLKC1,
  output UCLKC2
);

  wire _279_out, _350_out, _372_out, _373_nq, _374_out, _375_nq, _377_q, _378_nq, _381_q, _381_qn, _383_nq,
       _384_nq, _385_nq, _421_out, _422_out, _423_out, _424_out, _425_qn, _427_out, _428_out, _431_out,
       _436_q, _437_out, _445_out, _446_q, _448_q, _451_q, _452_q, _455_out, _456_qn, _457_q, _458_out,
       _486_out, _487_out, _488_out, _489_q, _489_qn, _490_out, _492_q, _492_qn, _493_out, _494_out,
       _495_out, _496_out, _497_out, _501_out, _502_q, _503_out, _507_q, _509_q, _513_q, _515_out, _517_q,
       _518_nq, _519_nq, _564_out, _565_out, _566_out, _567_out, _568_out, _569_out, _570_out, _571_q,
       _571_qn, _572_q, _572_qn, _578_out, _579_out, _580_out, _581_q, _581_qn, _582_out, _583_out, _584_out,
       _585_out, _586_out, _587_q, _587_qn, _588_out, _589_out, _590_q, _590_qn, _591_out, _592_out,
       _593_out, _594_q, _594_qn, _636_q, _636_qn, _637_out, _638_out, _639_q, _639_qn, _640_out, _641_out,
       _646_q, _646_qn, _647_q, _647_qn, _648_out, _649_out, _650_out, _651_out, _652_out, _653_out,
       _654_out, _655_out, _675_out, _678_out, _679_out, _683_out, _685_out, _686_out, _687_out, _698_out,
       d_ff_1_q, d_ff_2_q, d_ff_3_q, d_ff_4_q, d_ff_5_q, d_ff_6_q, d_ff_7_q, d_ff_8_q, multiplexer_1_out,
       multiplexer_2_out, multiplexer_3_out, multiplexer_4_out, multiplexer_5_out, multiplexer_6_out,
       multiplexer_7_out, multiplexer_8_out, not_1_out, not_2_out, not_3_out, not_4_out, not_5_out,
       not_6_out, not_7_out, not_8_out, not_9_out, not_10_out, not_11_out, not_12_out, not_13_out, not_14_out;

  S_latch _385 (.EN(not_1_out), .D(DB[0]), .Q(TXC_o[0]), .nQ(_385_nq));
  S_latch _383 (.EN(not_1_out), .D(DB[1]), .Q(TXC_o[1]), .nQ(_383_nq));
  S_latch _375 (.EN(not_1_out), .D(DB[2]), .Q(TXC_o[2]), .nQ(_375_nq));
  S_latch _384 (.EN(not_1_out), .D(DB[3]), .Q(TXC_o[3]), .nQ(_384_nq));
  S_latch _378 (.EN(not_1_out), .D(DB[4]), .Q(TXC_o[4]), .nQ(_378_nq));
  S_latch _519 (.EN(not_1_out), .D(DB[5]), .Q(TXC_o[5]), .nQ(_519_nq));
  S_latch _373 (.EN(not_1_out), .D(DB[6]), .Q(TXC_o[6]), .nQ(_373_nq));
  S_latch _518 (.EN(not_1_out), .D(DB[7]), .Q(TXC_o[7]), .nQ(_518_nq));
  not not_1 (not_1_out, DEC0_5);
  D_Flip_Flop _95 (.clk(DEC0_7), .D(DB[3]), .Q(g_95), .reset(not_2_out));  // open: Qn, preset, en
  D_Flip_Flop _48 (.clk(DEC0_7), .D(DB[4]), .Q(g_48), .reset(not_2_out));  // open: Qn, preset, en
  D_Flip_Flop _159 (.clk(DEC0_7), .D(DB[5]), .Q(g_159), .reset(not_2_out));  // open: Qn, preset, en
  D_Flip_Flop _314 (.clk(DEC0_7), .D(DB[6]), .Q(g_314), .reset(not_2_out));  // open: Qn, preset, en
  D_Flip_Flop _312 (.clk(DEC0_7), .D(DB[7]), .Q(g_312), .reset(not_2_out));  // open: Qn, preset, en
  not not_2 (not_2_out, FRESM3);
  not not_3 (not_3_out, _589_out);
  not not_4 (not_4_out, not_3_out);
  Multiplexer #(.disabled(0), .enable("false")) multiplexer_1 (
    .in0(_385_nq), .in1(_452_q), .out(multiplexer_1_out), .sel(not_4_out));
  Multiplexer #(.disabled(0), .enable("false")) multiplexer_2 (
    .in0(_383_nq), .in1(_446_q), .out(multiplexer_2_out), .sel(not_4_out));
  Multiplexer #(.disabled(0), .enable("false")) multiplexer_3 (
    .in0(_375_nq), .in1(_448_q), .out(multiplexer_3_out), .sel(not_4_out));
  Multiplexer #(.disabled(0), .enable("false")) multiplexer_4 (
    .in0(_384_nq), .in1(_451_q), .out(multiplexer_4_out), .sel(not_4_out));
  Multiplexer #(.disabled(0), .enable("false")) multiplexer_5 (
    .in0(_378_nq), .in1(_517_q), .out(multiplexer_5_out), .sel(not_4_out));
  Multiplexer #(.disabled(0), .enable("false")) multiplexer_6 (
    .in0(_519_nq), .in1(_509_q), .out(multiplexer_6_out), .sel(not_4_out));
  Multiplexer #(.disabled(0), .enable("false")) multiplexer_7 (
    .in0(_373_nq), .in1(_513_q), .out(multiplexer_7_out), .sel(not_4_out));
  Multiplexer #(.disabled(0), .enable("false")) multiplexer_8 (
    .in0(_518_nq), .in1(1'b0), .out(multiplexer_8_out), .sel(not_4_out));
  or _515 (_515_out, UCLKC1, 1'b0);
  Multiplexer #(.select(2), .disabled(0), .enable("false")) multiplexer_9 (
    .in0(DIV0), .in1(DIV1), .in2(DIV2), .in3(DIV3), .out(UCLKC2), .sel({g_314, g_312}));
  Multiplexer #(.select(2), .disabled(0), .enable("false")) multiplexer_10 (
    .in0(DIV3), .in1(DIV4), .in2(DIV5), .in3(DIV6), .out(UCLKC1), .sel({g_314, g_312}));
  D_Flip_Flop _377 (.clk(_515_out), .D(multiplexer_1_out), .Q(_377_q), .reset(not_5_out));  // open: Qn, preset, en
  D_Flip_Flop _452 (.clk(_515_out), .D(multiplexer_2_out), .Q(_452_q), .reset(not_5_out));  // open: Qn, preset, en
  D_Flip_Flop _446 (.clk(_515_out), .D(multiplexer_3_out), .Q(_446_q), .reset(not_5_out));  // open: Qn, preset, en
  D_Flip_Flop _448 (.clk(_515_out), .D(multiplexer_4_out), .Q(_448_q), .reset(not_5_out));  // open: Qn, preset, en
  D_Flip_Flop _451 (.clk(_515_out), .D(multiplexer_5_out), .Q(_451_q), .reset(not_5_out));  // open: Qn, preset, en
  D_Flip_Flop _517 (.clk(_515_out), .D(multiplexer_6_out), .Q(_517_q), .reset(not_5_out));  // open: Qn, preset, en
  D_Flip_Flop _509 (.clk(_515_out), .D(multiplexer_7_out), .Q(_509_q), .reset(not_5_out));  // open: Qn, preset, en
  D_Flip_Flop _513 (.clk(_515_out), .D(multiplexer_8_out), .Q(_513_q), .reset(not_5_out));  // open: Qn, preset, en
  and _372 (_372_out, _589_out, _374_out);
  not _374 (_374_out, _377_q);
  not not_5 (not_5_out, g_48);
  not _487 (_487_out, _422_out);
  D_Flip_Flop _371 (.clk(UCLKC1), .D(_372_out), .Q(g_371), .preset(not_5_out));  // open: Qn, en, reset
  not not_6 (not_6_out, _490_out);
  buf _490 (_490_out, FRES);
  nand _495 (_495_out, _492_q, _572_q);
  nand _496 (_496_out, _492_q, _571_q);
  nand _493 (_493_out, _492_q, _489_qn);
  nand _486 (_486_out, _572_qn, _492_qn, _571_qn, _489_q);
  nand _569 (_569_out, _489_q, _571_qn);
  nand _565 (_565_out, _571_q, _489_qn);
  nand _566 (_566_out, _571_q, _572_q);
  nand _570 (_570_out, _489_q, _571_qn, _572_qn);
  nand _564 (_564_out, _489_qn, _572_q);
  nor _488 (_488_out, _489_q, _422_out);
  or _497 (_497_out, _492_q, _422_out);
  or _423 (_423_out, _422_out, _425_qn);
  D_Flip_Flop _492 (.clk(UCLKC2), .D(_494_out), .Q(_492_q), .Qn(_492_qn), .preset(not_6_out));  // open: en, reset
  nand _494 (_494_out, _495_out, _496_out, _493_out, _486_out, _487_out, 1'b1);
  nand _568 (_568_out, _487_out, _569_out, _565_out);
  nand _567 (_567_out, _487_out, _566_out, _570_out, _564_out);
  nand _424 (_424_out, _497_out, _423_out);
  D_Flip_Flop _571 (.clk(UCLKC2), .D(_568_out), .Q(_571_q), .Qn(_571_qn), .preset(not_6_out));  // open: en, reset
  buf _501 (_501_out, FRES);
  nand _582 (_582_out, _636_qn, _581_q, _639_qn, _587_q);
  nand _578 (_578_out, _636_q, _581_q);
  nand _579 (_579_out, _639_q, _581_q);
  nand _637 (_637_out, _639_q, _636_q);
  nand _588 (_588_out, _507_q, _639_qn, _581_qn);
  nand _585 (_585_out, _581_q, _587_q, _636_q);
  nand _583 (_583_out, _639_q, _636_q, _581_qn);
  nand _584 (_584_out, _587_q, _639_q, _581_q);
  nand _641 (_641_out, _639_qn, _581_q);
  nand _503 (_503_out, _587_qn, _636_qn, _581_q, _639_qn);
  nand _589 (_589_out, 1'b1, _636_qn, _587_qn, _507_q, _639_qn, _581_qn);
  D_Flip_Flop _572 (.clk(UCLKC2), .D(_567_out), .Q(_572_q), .Qn(_572_qn), .preset(not_6_out));  // open: en, reset
  not not_7 (not_7_out, _501_out);
  not _445 (_445_out, _589_out);
  not _455 (_455_out, UCLKC1);
  not not_8 (not_8_out, FRES0);
  not not_9 (not_9_out, DEC0_5);
  D_Flip_Flop _581 (.clk(UCLKC1), .D(_580_out), .Q(_581_q), .Qn(_581_qn), .preset(not_7_out));  // open: en, reset
  nand _580 (_580_out, _582_out, _578_out, _579_out, _637_out);
  nand _638 (_638_out, _637_out, _582_out, _588_out);
  nand _586 (_586_out, _585_out, _588_out, _583_out, _584_out);
  nand _640 (_640_out, _588_out, _583_out, _641_out);
  D_Flip_Flop _489 (.clk(UCLKC2), .D(_488_out), .Q(_489_q), .Qn(_489_qn), .reset(not_6_out));  // open: preset, en
  D_Flip_Flop _425 (.clk(UCLKC2), .D(_424_out), .Qn(_425_qn), .reset(not_6_out));  // open: Q, preset, en
  nor _422 (_422_out, _425_qn, _381_q, _421_out);
  J_K_Flip_Flop #(.trigger("falling")) _456 (
    .J(_445_out), .clk(_455_out), .K(1'b0), .Q(g_456), .Qn(_456_qn), .preset(not_9_out), .reset(not_8_out));  // open: en
  not not_10 (not_10_out, _456_qn);
  D_Flip_Flop _636 (.clk(UCLKC1), .D(_638_out), .Q(_636_q), .Qn(_636_qn), .preset(not_7_out));  // open: en, reset
  D_Flip_Flop _457 (.clk(_502_q), .D(1'b0), .Q(_457_q), .preset(not_10_out), .reset(not_8_out));  // open: Qn, en
  D_Flip_Flop _587 (.clk(UCLKC1), .D(_586_out), .Q(_587_q), .Qn(_587_qn), .preset(not_7_out));  // open: en, reset
  not _350 (_350_out, _381_q);
  D_Flip_Flop _639 (.clk(UCLKC1), .D(_640_out), .Q(_639_q), .Qn(_639_qn), .reset(not_7_out));  // open: preset, en
  D_Flip_Flop _507 (.clk(UCLKC2), .D(_457_q), .Q(_507_q));  // open: Qn, preset, en, reset
  D_Flip_Flop _502 (.clk(UCLKC1), .D(_503_out), .Q(_502_q), .reset(not_7_out));  // open: Qn, preset, en
  buf _431 (_431_out, FRES);
  not not_11 (not_11_out, _431_out);
  nand _654 (_654_out, _590_q, _646_q, _647_q);
  nand _655 (_655_out, _594_q, _647_q, _590_q);
  nand _428 (_428_out, _350_out, _425_qn, _594_qn, _590_qn);
  nand _650 (_650_out, _590_q, _594_qn, _647_q, _646_qn);
  nand _653 (_653_out, _590_q, _646_q, _594_qn);
  nand _648 (_648_out, _590_q, _594_q, _646_q);
  nand _591 (_591_out, _594_q, _590_q);
  nand _652 (_652_out, _590_q, _594_qn, _647_qn, _646_qn);
  not _421 (_421_out, _427_out);
  and _427 (_427_out, _594_qn, _590_qn);
  D_Flip_Flop _647 (.clk(_492_qn), .D(_651_out), .Q(_647_q), .Qn(_647_qn), .reset(not_11_out));  // open: preset, en
  nand _651 (_651_out, _654_out, _655_out, _428_out, _652_out);
  nand _593 (_593_out, _652_out, _650_out, _428_out, _653_out);
  nand _649 (_649_out, _652_out, _650_out, _648_out, _428_out);
  nand _592 (_592_out, _650_out, _428_out, _591_out, _653_out);
  D_Flip_Flop _381 (.clk(UCLKC2), .D(PC5_i), .Q(_381_q), .Qn(_381_qn), .preset(not_12_out));  // open: en, reset
  D_Flip_Flop _594 (.clk(_492_qn), .D(_593_out), .Q(_594_q), .Qn(_594_qn), .reset(not_11_out));  // open: preset, en
  and _458 (_458_out, 1'b1, _381_q);
  not not_12 (not_12_out, g_159);
  D_Flip_Flop _646 (.clk(_492_qn), .D(_649_out), .Q(_646_q), .Qn(_646_qn), .reset(not_11_out));  // open: preset, en
  D_Flip_Flop d_ff_1 (.clk(_492_qn), .D(_458_out), .Q(d_ff_1_q), .reset(not_12_out));  // open: Qn, preset, en
  D_Flip_Flop d_ff_2 (.clk(_492_qn), .D(d_ff_1_q), .Q(d_ff_2_q), .reset(not_12_out));  // open: Qn, preset, en
  D_Flip_Flop d_ff_3 (.clk(_492_qn), .D(d_ff_2_q), .Q(d_ff_3_q), .reset(not_12_out));  // open: Qn, preset, en
  D_Flip_Flop d_ff_4 (.clk(_492_qn), .D(d_ff_3_q), .Q(d_ff_4_q), .reset(not_12_out));  // open: Qn, preset, en
  D_Flip_Flop d_ff_5 (.clk(_492_qn), .D(d_ff_4_q), .Q(d_ff_5_q), .reset(not_12_out));  // open: Qn, preset, en
  D_Flip_Flop d_ff_6 (.clk(_492_qn), .D(d_ff_5_q), .Q(d_ff_6_q), .reset(not_12_out));  // open: Qn, preset, en
  D_Flip_Flop d_ff_7 (.clk(_492_qn), .D(d_ff_6_q), .Q(d_ff_7_q), .reset(not_12_out));  // open: Qn, preset, en
  D_Flip_Flop d_ff_8 (.clk(_492_qn), .D(d_ff_7_q), .Q(d_ff_8_q), .reset(not_12_out));  // open: Qn, preset, en
  D_Flip_Flop _590 (.clk(_492_qn), .D(_592_out), .Q(_590_q), .Qn(_590_qn), .reset(not_11_out));  // open: preset, en
  RC_DELAY _678 (.IN(d_ff_1_q), .OUT(_678_out));
  RC_DELAY _675 (.IN(d_ff_2_q), .OUT(_675_out));
  RC_DELAY _679 (.IN(d_ff_3_q), .OUT(_679_out));
  RC_DELAY _685 (.IN(d_ff_4_q), .OUT(_685_out));
  RC_DELAY _687 (.IN(d_ff_5_q), .OUT(_687_out));
  RC_DELAY _686 (.IN(d_ff_6_q), .OUT(_686_out));
  RC_DELAY _683 (.IN(d_ff_7_q), .OUT(_683_out));
  RC_DELAY _698 (.IN(d_ff_8_q), .OUT(_698_out));
  and _279 (_279_out, DEC1_6, FRES0);
  D_Flip_Flop _436 (.clk(_492_qn), .D(_652_out), .Q(_436_q), .preset(not_11_out));  // open: Qn, en, reset
  not not_13 (not_13_out, _279_out);
  or _437 (_437_out, _492_qn, _436_q);
  D_Flip_Flop _280 (.clk(_437_out), .D(1'b1), .Q(g_280), .reset(not_13_out));  // open: Qn, preset, en
  D_Flip_Flop _272 (.clk(_437_out), .D(_381_qn), .Q(g_272), .reset(not_13_out));  // open: Qn, preset, en
  D_Flip_Flop _462 (.clk(_437_out), .D(_678_out), .Q(RXC_o[7]), .reset(not_14_out));  // open: Qn, preset, en
  D_Flip_Flop _461 (.clk(_437_out), .D(_675_out), .Q(RXC_o[6]), .reset(not_14_out));  // open: Qn, preset, en
  D_Flip_Flop _467 (.clk(_437_out), .D(_679_out), .Q(RXC_o[5]), .reset(not_14_out));  // open: Qn, preset, en
  D_Flip_Flop _320 (.clk(_437_out), .D(_685_out), .Q(RXC_o[4]), .reset(not_14_out));  // open: Qn, preset, en
  D_Flip_Flop _210 (.clk(_437_out), .D(_687_out), .Q(RXC_o[3]), .reset(not_14_out));  // open: Qn, preset, en
  D_Flip_Flop _278 (.clk(_437_out), .D(_686_out), .Q(RXC_o[2]), .reset(not_14_out));  // open: Qn, preset, en
  D_Flip_Flop _316 (.clk(_437_out), .D(_683_out), .Q(RXC_o[1]), .reset(not_14_out));  // open: Qn, preset, en
  D_Flip_Flop _459 (.clk(_437_out), .D(_698_out), .Q(RXC_o[0]), .reset(not_14_out));  // open: Qn, preset, en
  not not_14 (not_14_out, 1'b1);
  and _205 (g_205, g_95, g_280);

  // Other names for the same wires on the sheet: DIV1_t = DIV2; DIV2_t = DIV1; DIV4_t = DIV5; DIV5_t = DIV4

  // Notes on the sheet:
  //   386
  //   296
  //   296
  //   444
  //   512
  //   454
  //   453
  //   447
  //   449
  //   450
  //   516
  //   511
  //   514
  //   B
  //   A
  //   !
  //   NEGEDGE
  //   !
  //   SIPO SR 4bit
  //   SIPO SR 4bit
  //   460
  //   275
  //   313 H
  //   94 H
endmodule
