// Logisim project ym2602.circ as structural Verilog
module PSG (
  input  clk,
  input  reset,
  input  WR,
  input  IORQ,
  input  A7,
  input  A6,
  input  [7:0] data,
  output [3:0] out_8,
  output [3:0] out_9,
  output [3:0] out_10,
  output [3:0] out_11
);

  wire and_1_out, and_6_out, and_7_out, and_8_out, cmp_bit_1_cout, cmp_bit_2_cout, cmp_bit_3_cout,
       cmp_bit_4_cout, cmp_bit_5_cout, cmp_bit_6_cout, cmp_bit_7_cout, cmp_bit_8_cout, cmp_bit_9_cout,
       cmp_bit_10_cout, d_ff_9_q, d_ff_9_qn, d_ff_10_q, d_ff_10_qn, d_ff_11_q, d_ff_11_qn, d_ff_12_q,
       d_ff_13_q, d_ff_14_q, d_ff_15_q, d_ff_16_q, d_ff_17_q, d_ff_18_q, d_ff_19_q, d_ff_20_q, d_ff_21_q,
       d_ff_21_qn, d_ff_22_q, d_ff_23_q, d_ff_24_q, d_ff_25_q, d_ff_26_q, d_ff_27_qn, d_ff_28_q, d_ff_29_q,
       d_ff_30_q, nor_1_out, nor_2_out, nor_3_out, nor_7_out, nor_9_out, nor_10_out, nor_11_out, nor_12_out,
       nor_13_out, nor_14_out, not_1_out, not_2_out, not_3_out, not_4_out, not_5_out, not_6_out, not_7_out,
       not_8_out, not_9_out, not_10_out, not_11_out, not_12_out, not_13_out, not_14_out, not_15_out,
       not_16_out, not_17_out, not_18_out, not_19_out, not_20_out, not_21_out, not_22_out, not_23_out,
       not_24_out, not_25_out, not_26_out, not_27_out, not_28_out, not_29_out, or_1_out, or_2_out, or_3_out,
       or_4_out, or_5_out, or_6_out, or_7_out, or_8_out, or_9_out, or_10_out, or_11_out, or_12_out,
       or_13_out, or_14_out, psg_clk_1_clk1, psg_clk_1_clk2, psg_clk_1_hclk1, psg_clk_1_hclk2,
       psg_clk_1_reset_sync, psg_noise_bit_1_valout, psg_noise_bit_2_valout, psg_noise_bit_3_valout,
       psg_noise_bit_4_valout, psg_noise_bit_5_valout, psg_noise_bit_6_valout, psg_noise_bit_7_valout,
       psg_noise_bit_8_valout, psg_noise_bit_9_valout, psg_noise_bit_10_valout, psg_noise_bit_11_valout,
       psg_noise_bit_12_valout, psg_noise_bit_13_valout, psg_noise_bit_14_valout, psg_noise_bit_15_valout,
       psg_noise_bit_16_valout, psg_reg_bit2_1_out_5, psg_reg_bit2_2_out_5, psg_reg_bit2_3_out_5,
       psg_sign_bit_1_sign, psg_sign_bit_1_valout, psg_sign_bit_2_sign, psg_sign_bit_2_valout,
       psg_sign_bit_3_sign, psg_sign_bit_3_valout, psg_sign_bit_4_sign, xor_1_out;
  wire [3:0] bit_extender_6_out, bit_extender_7_out, bit_extender_8_out, bit_extender_9_out,
       psg_reg_bit3_1_out_5, psg_reg_bit3_5_out_5, psg_reg_bit3_9_out_5, psg_reg_bit3_13_out_5;
  wire [6:4] nor_4_out;
  wire [7:0] d_ff_1_q;
  wire [9:0] adder_1_out, and_2_out, and_3_out, and_4_out, and_5_out, and_9_out, bit_extender_1_out,
       bit_extender_2_out, bit_extender_3_out, bit_extender_4_out, bit_extender_5_out, latch_10bit_1_val_out,
       latch_10bit_2_val_out, latch_10bit_3_val_out, latch_10bit_4_val_out, latch_10bit_5_val_out,
       latch_10bit_6_val_out, latch_10bit_7_val_out, latch_10bit_8_val_out, latch_10bit_9_val_out, nor_8_out,
       psg_reg_bit_1_out_5, psg_reg_bit_11_out_5, psg_reg_bit_21_out_5;

  not not_1 (not_1_out, A6);
  or or_1 (or_1_out, WR, IORQ, A7, not_1_out);
  not not_2 (not_2_out, or_1_out);
  not not_3 (not_3_out, or_2_out);
  not not_4 (not_4_out, or_7_out);
  D_Flip_Flop #(.trigger("high")) d_ff_1 (.D(data[0]), .clk(not_2_out), .Q(d_ff_1_q[0]));  // open: Qn, preset, reset
  D_Flip_Flop #(.trigger("high")) d_ff_2 (.D(data[1]), .clk(not_2_out), .Q(d_ff_1_q[1]));  // open: Qn, preset, reset
  D_Flip_Flop #(.trigger("high")) d_ff_3 (.D(data[2]), .clk(not_2_out), .Q(d_ff_1_q[2]));  // open: Qn, preset, reset
  D_Flip_Flop #(.trigger("high")) d_ff_4 (.D(data[3]), .clk(not_2_out), .Q(d_ff_1_q[3]));  // open: Qn, preset, reset
  D_Flip_Flop #(.trigger("high")) d_ff_5 (.D(data[4]), .clk(not_2_out), .Q(d_ff_1_q[4]));  // open: Qn, preset, reset
  D_Flip_Flop #(.trigger("high")) d_ff_6 (.D(data[5]), .clk(not_2_out), .Q(d_ff_1_q[5]));  // open: Qn, preset, reset
  D_Flip_Flop #(.trigger("high")) d_ff_7 (.D(data[6]), .clk(not_2_out), .Q(d_ff_1_q[6]));  // open: Qn, preset, reset
  D_Flip_Flop #(.trigger("high")) d_ff_8 (.D(data[7]), .clk(not_2_out), .Q(d_ff_1_q[7]));  // open: Qn, preset, reset
  psg_clk psg_clk_1 (
    .clk(clk), .reset(reset), .clk1(psg_clk_1_clk1), .clk2(psg_clk_1_clk2), .hclk1(psg_clk_1_hclk1),
    .hclk2(psg_clk_1_hclk2), .reset_sync(psg_clk_1_reset_sync));
  psg_reg_bit psg_reg_bit_1 (
    .val(d_ff_1_q[0]), .wr(not_3_out), .nwr(or_2_out), .reset(psg_clk_1_reset_sync),
    .out_5(psg_reg_bit_1_out_5[0]));
  psg_reg_bit psg_reg_bit_2 (
    .val(d_ff_1_q[1]), .wr(not_3_out), .nwr(or_2_out), .reset(psg_clk_1_reset_sync),
    .out_5(psg_reg_bit_1_out_5[1]));
  psg_reg_bit psg_reg_bit_3 (
    .val(d_ff_1_q[2]), .wr(not_3_out), .nwr(or_2_out), .reset(psg_clk_1_reset_sync),
    .out_5(psg_reg_bit_1_out_5[2]));
  psg_reg_bit psg_reg_bit_4 (
    .val(d_ff_1_q[3]), .wr(not_3_out), .nwr(or_2_out), .reset(psg_clk_1_reset_sync),
    .out_5(psg_reg_bit_1_out_5[3]));
  psg_reg_bit psg_reg_bit_5 (
    .val(d_ff_1_q[0]), .wr(not_4_out), .nwr(or_7_out), .reset(psg_clk_1_reset_sync),
    .out_5(psg_reg_bit_1_out_5[4]));
  psg_reg_bit psg_reg_bit_6 (
    .val(d_ff_1_q[1]), .wr(not_4_out), .nwr(or_7_out), .reset(psg_clk_1_reset_sync),
    .out_5(psg_reg_bit_1_out_5[5]));
  psg_reg_bit psg_reg_bit_7 (
    .val(d_ff_1_q[2]), .wr(not_4_out), .nwr(or_7_out), .reset(psg_clk_1_reset_sync),
    .out_5(psg_reg_bit_1_out_5[6]));
  psg_reg_bit psg_reg_bit_8 (
    .val(d_ff_1_q[3]), .wr(not_4_out), .nwr(or_7_out), .reset(psg_clk_1_reset_sync),
    .out_5(psg_reg_bit_1_out_5[7]));
  psg_reg_bit psg_reg_bit_9 (
    .val(d_ff_1_q[4]), .wr(not_4_out), .nwr(or_7_out), .reset(psg_clk_1_reset_sync),
    .out_5(psg_reg_bit_1_out_5[8]));
  psg_reg_bit psg_reg_bit_10 (
    .val(d_ff_1_q[5]), .wr(not_4_out), .nwr(or_7_out), .reset(psg_clk_1_reset_sync),
    .out_5(psg_reg_bit_1_out_5[9]));
  nor nor_1 (nor_1_out, not_2_out, nor_2_out);
  nor nor_2 (nor_2_out, nor_1_out, d_ff_13_q);
  and and_1 (and_1_out, d_ff_13_q, d_ff_1_q[7]);
  nor nor_3 (nor_3_out, not_2_out, nor_1_out);
  D_Flip_Flop #(.trigger("high")) d_ff_9 (
    .D(d_ff_1_q[4]), .clk(and_1_out), .Q(d_ff_9_q), .Qn(d_ff_9_qn));  // open: preset, reset
  D_Flip_Flop #(.trigger("high")) d_ff_10 (
    .D(d_ff_1_q[5]), .clk(and_1_out), .Q(d_ff_10_q), .Qn(d_ff_10_qn));  // open: preset, reset
  D_Flip_Flop #(.trigger("high")) d_ff_11 (
    .D(d_ff_1_q[6]), .clk(and_1_out), .Q(d_ff_11_q), .Qn(d_ff_11_qn));  // open: preset, reset
  not not_5 (not_5_out, d_ff_1_q[7]);
  not not_6 (not_6_out, or_3_out);
  not not_7 (not_7_out, or_6_out);
  D_Flip_Flop #(.trigger("high")) d_ff_12 (
    .D(nor_3_out), .clk(psg_clk_1_clk1), .Q(d_ff_12_q));  // open: Qn, preset, reset
  psg_reg_bit psg_reg_bit_11 (
    .val(d_ff_1_q[0]), .wr(not_6_out), .nwr(or_3_out), .reset(psg_clk_1_reset_sync),
    .out_5(psg_reg_bit_11_out_5[0]));
  psg_reg_bit psg_reg_bit_12 (
    .val(d_ff_1_q[1]), .wr(not_6_out), .nwr(or_3_out), .reset(psg_clk_1_reset_sync),
    .out_5(psg_reg_bit_11_out_5[1]));
  psg_reg_bit psg_reg_bit_13 (
    .val(d_ff_1_q[2]), .wr(not_6_out), .nwr(or_3_out), .reset(psg_clk_1_reset_sync),
    .out_5(psg_reg_bit_11_out_5[2]));
  psg_reg_bit psg_reg_bit_14 (
    .val(d_ff_1_q[3]), .wr(not_6_out), .nwr(or_3_out), .reset(psg_clk_1_reset_sync),
    .out_5(psg_reg_bit_11_out_5[3]));
  psg_reg_bit psg_reg_bit_15 (
    .val(d_ff_1_q[0]), .wr(not_7_out), .nwr(or_6_out), .reset(psg_clk_1_reset_sync),
    .out_5(psg_reg_bit_11_out_5[4]));
  psg_reg_bit psg_reg_bit_16 (
    .val(d_ff_1_q[1]), .wr(not_7_out), .nwr(or_6_out), .reset(psg_clk_1_reset_sync),
    .out_5(psg_reg_bit_11_out_5[5]));
  psg_reg_bit psg_reg_bit_17 (
    .val(d_ff_1_q[2]), .wr(not_7_out), .nwr(or_6_out), .reset(psg_clk_1_reset_sync),
    .out_5(psg_reg_bit_11_out_5[6]));
  psg_reg_bit psg_reg_bit_18 (
    .val(d_ff_1_q[3]), .wr(not_7_out), .nwr(or_6_out), .reset(psg_clk_1_reset_sync),
    .out_5(psg_reg_bit_11_out_5[7]));
  psg_reg_bit psg_reg_bit_19 (
    .val(d_ff_1_q[4]), .wr(not_7_out), .nwr(or_6_out), .reset(psg_clk_1_reset_sync),
    .out_5(psg_reg_bit_11_out_5[8]));
  psg_reg_bit psg_reg_bit_20 (
    .val(d_ff_1_q[5]), .wr(not_7_out), .nwr(or_6_out), .reset(psg_clk_1_reset_sync),
    .out_5(psg_reg_bit_11_out_5[9]));
  D_Flip_Flop #(.trigger("high")) d_ff_13 (
    .D(d_ff_12_q), .clk(psg_clk_1_clk2), .Q(d_ff_13_q));  // open: Qn, preset, reset
  or or_2 (or_2_out, d_ff_9_q, d_ff_10_q, d_ff_11_q, not_5_out, d_ff_15_q);
  or or_3 (or_3_out, d_ff_9_q, d_ff_10_qn, d_ff_11_q, not_5_out, d_ff_15_q);
  or or_4 (or_4_out, d_ff_9_q, d_ff_10_q, d_ff_11_qn, d_ff_15_q, not_5_out);
  or or_5 (or_5_out, d_ff_9_q, d_ff_10_q, d_ff_11_qn, d_ff_1_q[7], d_ff_15_q);
  or or_6 (or_6_out, d_ff_9_q, d_ff_10_qn, d_ff_11_q, d_ff_1_q[7], d_ff_15_q);
  or or_7 (or_7_out, d_ff_9_q, d_ff_10_q, d_ff_11_q, d_ff_1_q[7], d_ff_15_q);
  or or_8 (or_8_out, d_ff_9_qn, d_ff_10_q, d_ff_11_q, d_ff_15_q);
  or or_9 (or_9_out, d_ff_9_qn, d_ff_10_qn, d_ff_11_q, d_ff_15_q);
  or or_10 (or_10_out, d_ff_9_qn, d_ff_10_q, d_ff_11_qn, d_ff_15_q);
  or or_11 (or_11_out, d_ff_9_qn, d_ff_10_qn, d_ff_11_qn, d_ff_15_q);
  or or_12 (or_12_out, d_ff_9_q, d_ff_10_qn, d_ff_11_qn, d_ff_15_q);
  D_Flip_Flop #(.trigger("high")) d_ff_14 (
    .D(d_ff_13_q), .clk(psg_clk_1_clk1), .Q(d_ff_14_q));  // open: Qn, preset, reset
  D_Flip_Flop #(.trigger("high")) d_ff_15 (
    .D(d_ff_14_q), .clk(psg_clk_1_clk2), .Q(d_ff_15_q));  // open: Qn, preset, reset
  not not_8 (not_8_out, or_4_out);
  not not_9 (not_9_out, or_5_out);
  not not_10 (not_10_out, or_12_out);
  psg_reg_bit psg_reg_bit_21 (
    .val(d_ff_1_q[0]), .wr(not_8_out), .nwr(or_4_out), .reset(psg_clk_1_reset_sync),
    .out_5(psg_reg_bit_21_out_5[0]));
  psg_reg_bit psg_reg_bit_22 (
    .val(d_ff_1_q[1]), .wr(not_8_out), .nwr(or_4_out), .reset(psg_clk_1_reset_sync),
    .out_5(psg_reg_bit_21_out_5[1]));
  psg_reg_bit psg_reg_bit_23 (
    .val(d_ff_1_q[2]), .wr(not_8_out), .nwr(or_4_out), .reset(psg_clk_1_reset_sync),
    .out_5(psg_reg_bit_21_out_5[2]));
  psg_reg_bit psg_reg_bit_24 (
    .val(d_ff_1_q[3]), .wr(not_8_out), .nwr(or_4_out), .reset(psg_clk_1_reset_sync),
    .out_5(psg_reg_bit_21_out_5[3]));
  psg_reg_bit psg_reg_bit_25 (
    .val(d_ff_1_q[0]), .wr(not_9_out), .nwr(or_5_out), .reset(psg_clk_1_reset_sync),
    .out_5(psg_reg_bit_21_out_5[4]));
  psg_reg_bit psg_reg_bit_26 (
    .val(d_ff_1_q[1]), .wr(not_9_out), .nwr(or_5_out), .reset(psg_clk_1_reset_sync),
    .out_5(psg_reg_bit_21_out_5[5]));
  psg_reg_bit psg_reg_bit_27 (
    .val(d_ff_1_q[2]), .wr(not_9_out), .nwr(or_5_out), .reset(psg_clk_1_reset_sync),
    .out_5(psg_reg_bit_21_out_5[6]));
  psg_reg_bit psg_reg_bit_28 (
    .val(d_ff_1_q[3]), .wr(not_9_out), .nwr(or_5_out), .reset(psg_clk_1_reset_sync),
    .out_5(psg_reg_bit_21_out_5[7]));
  psg_reg_bit psg_reg_bit_29 (
    .val(d_ff_1_q[4]), .wr(not_9_out), .nwr(or_5_out), .reset(psg_clk_1_reset_sync),
    .out_5(psg_reg_bit_21_out_5[8]));
  psg_reg_bit psg_reg_bit_30 (
    .val(d_ff_1_q[5]), .wr(not_9_out), .nwr(or_5_out), .reset(psg_clk_1_reset_sync),
    .out_5(psg_reg_bit_21_out_5[9]));
  not not_11 (not_11_out, psg_reg_bit2_2_out_5);
  not not_12 (not_12_out, psg_reg_bit2_1_out_5);
  nor nor_4 (nor_4_out[4], psg_reg_bit2_2_out_5, psg_reg_bit2_1_out_5);
  nor nor_5 (nor_4_out[5], not_11_out, psg_reg_bit2_1_out_5);
  nor nor_6 (nor_4_out[6], psg_reg_bit2_2_out_5, not_12_out);
  nor nor_7 (nor_7_out, not_11_out, not_12_out);
  assign bit_extender_1_out = {{9{d_ff_24_q}}, d_ff_24_q};  // Bit_Extender bit_extender_1
  assign bit_extender_2_out = {{9{d_ff_23_q}}, d_ff_23_q};  // Bit_Extender bit_extender_2
  assign bit_extender_3_out = {{9{d_ff_22_q}}, d_ff_22_q};  // Bit_Extender bit_extender_3
  assign bit_extender_4_out = {{9{d_ff_25_q}}, d_ff_25_q};  // Bit_Extender bit_extender_4
  psg_reg_bit2 psg_reg_bit2_1 (
    .val(d_ff_1_q[0]), .wr(not_10_out), .nwr(or_12_out), .reset(psg_clk_1_reset_sync),
    .out_5(psg_reg_bit2_1_out_5));
  psg_reg_bit2 psg_reg_bit2_2 (
    .val(d_ff_1_q[1]), .wr(not_10_out), .nwr(or_12_out), .reset(psg_clk_1_reset_sync),
    .out_5(psg_reg_bit2_2_out_5));
  psg_reg_bit2 psg_reg_bit2_3 (
    .val(d_ff_1_q[2]), .wr(not_10_out), .nwr(or_12_out), .reset(psg_clk_1_reset_sync),
    .out_5(psg_reg_bit2_3_out_5));
  assign and_2_out = psg_reg_bit_21_out_5 & bit_extender_1_out;  // AND_Gate and_2, 10 bits wide
  assign and_3_out = psg_reg_bit_11_out_5 & bit_extender_2_out;  // AND_Gate and_3, 10 bits wide
  assign and_4_out = psg_reg_bit_1_out_5 & bit_extender_3_out;  // AND_Gate and_4, 10 bits wide
  assign and_5_out = bit_extender_4_out & {3'b000, nor_4_out, 4'b0000};  // AND_Gate and_5, 10 bits wide
  assign nor_8_out = ~(and_2_out | and_3_out | and_4_out | and_5_out);  // NOR_Gate nor_8, 10 bits wide
  nor nor_9 (nor_9_out, d_ff_22_q, d_ff_23_q, d_ff_24_q, psg_clk_1_reset_sync);
  D_Flip_Flop #(.trigger("high")) d_ff_16 (
    .D(nor_9_out), .clk(psg_clk_1_hclk1), .Q(d_ff_16_q));  // open: Qn, preset, reset
  D_Flip_Flop #(.trigger("high")) d_ff_17 (
    .D(d_ff_22_q), .clk(psg_clk_1_hclk1), .Q(d_ff_17_q));  // open: Qn, preset, reset
  D_Flip_Flop #(.trigger("high")) d_ff_18 (
    .D(d_ff_23_q), .clk(psg_clk_1_hclk1), .Q(d_ff_18_q));  // open: Qn, preset, reset
  D_Flip_Flop #(.trigger("high")) d_ff_19 (
    .D(d_ff_24_q), .clk(psg_clk_1_hclk1), .Q(d_ff_19_q));  // open: Qn, preset, reset
  D_Flip_Flop #(.trigger("high")) d_ff_20 (
    .D(psg_clk_1_reset_sync), .clk(psg_clk_1_hclk1), .Q(d_ff_20_q));  // open: Qn, preset, reset
  D_Flip_Flop #(.trigger("high")) d_ff_21 (
    .D(d_ff_26_q), .clk(psg_clk_1_hclk1), .Q(d_ff_21_q), .Qn(d_ff_21_qn));  // open: preset, reset
  latch_10bit latch_10bit_1 (.val(nor_8_out), .clk(psg_clk_1_hclk1), .val_out(latch_10bit_1_val_out));
  D_Flip_Flop #(.trigger("high")) d_ff_22 (
    .D(d_ff_16_q), .clk(psg_clk_1_hclk2), .Q(d_ff_22_q));  // open: Qn, preset, reset
  D_Flip_Flop #(.trigger("high")) d_ff_23 (
    .D(d_ff_17_q), .clk(psg_clk_1_hclk2), .Q(d_ff_23_q));  // open: Qn, preset, reset
  D_Flip_Flop #(.trigger("high")) d_ff_24 (
    .D(d_ff_18_q), .clk(psg_clk_1_hclk2), .Q(d_ff_24_q));  // open: Qn, preset, reset
  D_Flip_Flop #(.trigger("high")) d_ff_25 (
    .D(d_ff_19_q), .clk(psg_clk_1_hclk2), .Q(d_ff_25_q));  // open: Qn, preset, reset
  D_Flip_Flop #(.trigger("high")) d_ff_26 (
    .D(d_ff_20_q), .clk(psg_clk_1_hclk2), .Q(d_ff_26_q));  // open: Qn, preset, reset
  not not_13 (not_13_out, d_ff_21_qn);
  D_Flip_Flop #(.trigger("high")) d_ff_27 (
    .D(nor_10_out), .clk(psg_clk_1_hclk2), .Qn(d_ff_27_qn));  // open: Q, preset, reset
  nor nor_10 (nor_10_out, d_ff_21_q, cmp_bit_10_cout);
  not not_14 (not_14_out, not_13_out);
  D_Flip_Flop #(.trigger("high")) d_ff_28 (
    .D(d_ff_22_q), .clk(psg_clk_1_hclk1), .Q(d_ff_28_q));  // open: Qn, preset, reset
  not not_15 (not_15_out, psg_sign_bit_1_sign);
  not not_16 (not_16_out, nor_7_out);
  not not_17 (not_17_out, psg_sign_bit_3_sign);
  and and_6 (and_6_out, not_15_out, not_16_out);
  and and_7 (and_7_out, not_17_out, nor_7_out);
  psg_sign_bit psg_sign_bit_1 (
    .step(d_ff_28_q), .reset(not_14_out), .val(cmp_bit_10_cout), .clk1(psg_clk_1_hclk1),
    .clk2(psg_clk_1_hclk2), .sign(psg_sign_bit_1_sign), .valout(psg_sign_bit_1_valout));
  psg_sign_bit psg_sign_bit_2 (
    .step(d_ff_28_q), .reset(not_14_out), .val(psg_sign_bit_3_valout), .clk1(psg_clk_1_hclk1),
    .clk2(psg_clk_1_hclk2), .sign(psg_sign_bit_2_sign), .valout(psg_sign_bit_2_valout));
  nor nor_11 (nor_11_out, and_6_out, and_7_out);
  not not_18 (not_18_out, or_12_out);
  D_Flip_Flop #(.trigger("high")) d_ff_29 (
    .D(nor_11_out), .clk(psg_clk_1_hclk1), .Q(d_ff_29_q));  // open: Qn, preset, reset
  Adder #(.width(10)) adder_1 (.a(latch_10bit_9_val_out), .b({10{1'b0}}), .out(adder_1_out), .cin(1'b1));  // open: cout
  cmp_bit cmp_bit_1 (.cin(1'b1), .a(latch_10bit_1_val_out[0]), .b(latch_10bit_2_val_out[0]), .cout(cmp_bit_1_cout));
  cmp_bit cmp_bit_2 (
    .cin(cmp_bit_1_cout), .a(latch_10bit_1_val_out[1]), .b(latch_10bit_2_val_out[1]), .cout(cmp_bit_2_cout));
  cmp_bit cmp_bit_3 (
    .cin(cmp_bit_2_cout), .a(latch_10bit_1_val_out[2]), .b(latch_10bit_2_val_out[2]), .cout(cmp_bit_3_cout));
  cmp_bit cmp_bit_4 (
    .cin(cmp_bit_3_cout), .a(latch_10bit_1_val_out[3]), .b(latch_10bit_2_val_out[3]), .cout(cmp_bit_4_cout));
  cmp_bit cmp_bit_5 (
    .cin(cmp_bit_4_cout), .a(latch_10bit_1_val_out[4]), .b(latch_10bit_2_val_out[4]), .cout(cmp_bit_5_cout));
  cmp_bit cmp_bit_6 (
    .cin(cmp_bit_5_cout), .a(latch_10bit_1_val_out[5]), .b(latch_10bit_2_val_out[5]), .cout(cmp_bit_6_cout));
  cmp_bit cmp_bit_7 (
    .cin(cmp_bit_6_cout), .a(latch_10bit_1_val_out[6]), .b(latch_10bit_2_val_out[6]), .cout(cmp_bit_7_cout));
  cmp_bit cmp_bit_8 (
    .cin(cmp_bit_7_cout), .a(latch_10bit_1_val_out[7]), .b(latch_10bit_2_val_out[7]), .cout(cmp_bit_8_cout));
  cmp_bit cmp_bit_9 (
    .cin(cmp_bit_8_cout), .a(latch_10bit_1_val_out[8]), .b(latch_10bit_2_val_out[8]), .cout(cmp_bit_9_cout));
  cmp_bit cmp_bit_10 (
    .cin(cmp_bit_9_cout), .a(latch_10bit_1_val_out[9]), .b(latch_10bit_2_val_out[9]), .cout(cmp_bit_10_cout));
  D_Flip_Flop #(.trigger("high")) d_ff_30 (
    .D(d_ff_29_q), .clk(psg_clk_1_hclk2), .Q(d_ff_30_q));  // open: Qn, preset, reset
  and and_8 (and_8_out, xor_1_out, psg_reg_bit2_3_out_5);
  not not_19 (not_19_out, d_ff_27_qn);
  or or_13 (or_13_out, not_18_out, psg_clk_1_reset_sync);
  not not_20 (not_20_out, d_ff_30_q);
  or or_14 (or_14_out, and_8_out, nor_14_out);
  psg_sign_bit psg_sign_bit_3 (
    .step(d_ff_28_q), .reset(not_14_out), .val(psg_sign_bit_1_valout), .clk1(psg_clk_1_hclk1),
    .clk2(psg_clk_1_hclk2), .sign(psg_sign_bit_3_sign), .valout(psg_sign_bit_3_valout));
  psg_sign_bit psg_sign_bit_4 (
    .step(d_ff_28_q), .reset(not_14_out), .val(psg_sign_bit_2_valout), .clk1(psg_clk_1_hclk1),
    .clk2(psg_clk_1_hclk2), .sign(psg_sign_bit_4_sign));  // open: valout
  assign bit_extender_5_out = {{9{not_19_out}}, not_19_out};  // Bit_Extender bit_extender_5
  not not_21 (not_21_out, or_8_out);
  nor nor_12 (nor_12_out, d_ff_30_q, not_25_out);
  nor nor_13 (nor_13_out, not_20_out, not_24_out);
  latch_10bit latch_10bit_2 (.val(adder_1_out), .clk(psg_clk_1_hclk1), .val_out(latch_10bit_2_val_out));
  latch_10bit latch_10bit_3 (.val(and_9_out), .clk(psg_clk_1_hclk1), .val_out(latch_10bit_3_val_out));
  latch_10bit latch_10bit_4 (.val(latch_10bit_7_val_out), .clk(psg_clk_1_hclk1), .val_out(latch_10bit_4_val_out));
  latch_10bit latch_10bit_5 (.val(latch_10bit_8_val_out), .clk(psg_clk_1_hclk1), .val_out(latch_10bit_5_val_out));
  not not_22 (not_22_out, nor_12_out);
  not not_23 (not_23_out, nor_13_out);
  assign bit_extender_6_out = {{3{psg_sign_bit_4_sign}}, psg_sign_bit_4_sign};  // Bit_Extender bit_extender_6
  not not_24 (not_24_out, not_22_out);
  not not_25 (not_25_out, not_23_out);
  assign out_8 = psg_reg_bit3_1_out_5 | bit_extender_6_out;  // OR_Gate or_15, 4 bits wide
  assign and_9_out = latch_10bit_6_val_out & bit_extender_5_out;  // AND_Gate and_9, 10 bits wide
  psg_reg_bit3 psg_reg_bit3_1 (
    .val(d_ff_1_q[0]), .wr(not_21_out), .nwr(or_8_out), .reset(psg_clk_1_reset_sync),
    .out_5(psg_reg_bit3_1_out_5[0]));
  psg_reg_bit3 psg_reg_bit3_2 (
    .val(d_ff_1_q[1]), .wr(not_21_out), .nwr(or_8_out), .reset(psg_clk_1_reset_sync),
    .out_5(psg_reg_bit3_1_out_5[1]));
  psg_reg_bit3 psg_reg_bit3_3 (
    .val(d_ff_1_q[2]), .wr(not_21_out), .nwr(or_8_out), .reset(psg_clk_1_reset_sync),
    .out_5(psg_reg_bit3_1_out_5[2]));
  psg_reg_bit3 psg_reg_bit3_4 (
    .val(d_ff_1_q[3]), .wr(not_21_out), .nwr(or_8_out), .reset(psg_clk_1_reset_sync),
    .out_5(psg_reg_bit3_1_out_5[3]));
  not not_26 (not_26_out, or_9_out);
  latch_10bit latch_10bit_6 (.val(latch_10bit_2_val_out), .clk(psg_clk_1_hclk2), .val_out(latch_10bit_6_val_out));
  latch_10bit latch_10bit_7 (.val(latch_10bit_3_val_out), .clk(psg_clk_1_hclk2), .val_out(latch_10bit_7_val_out));
  latch_10bit latch_10bit_8 (.val(latch_10bit_4_val_out), .clk(psg_clk_1_hclk2), .val_out(latch_10bit_8_val_out));
  latch_10bit latch_10bit_9 (.val(latch_10bit_5_val_out), .clk(psg_clk_1_hclk2), .val_out(latch_10bit_9_val_out));
  assign bit_extender_7_out = {{3{psg_sign_bit_2_sign}}, psg_sign_bit_2_sign};  // Bit_Extender bit_extender_7
  psg_noise_bit psg_noise_bit_1 (
    .val(or_14_out), .clk1(not_25_out), .clk2(not_24_out), .reset(or_13_out), .valout(psg_noise_bit_1_valout));
  psg_noise_bit psg_noise_bit_2 (
    .val(psg_noise_bit_1_valout), .clk1(not_25_out), .clk2(not_24_out), .reset(or_13_out),
    .valout(psg_noise_bit_2_valout));
  psg_noise_bit psg_noise_bit_3 (
    .val(psg_noise_bit_2_valout), .clk1(not_25_out), .clk2(not_24_out), .reset(or_13_out),
    .valout(psg_noise_bit_3_valout));
  psg_noise_bit psg_noise_bit_4 (
    .val(psg_noise_bit_3_valout), .clk1(not_25_out), .clk2(not_24_out), .reset(or_13_out),
    .valout(psg_noise_bit_4_valout));
  psg_noise_bit psg_noise_bit_5 (
    .val(psg_noise_bit_4_valout), .clk1(not_25_out), .clk2(not_24_out), .reset(or_13_out),
    .valout(psg_noise_bit_5_valout));
  psg_noise_bit psg_noise_bit_6 (
    .val(psg_noise_bit_5_valout), .clk1(not_25_out), .clk2(not_24_out), .reset(or_13_out),
    .valout(psg_noise_bit_6_valout));
  psg_noise_bit psg_noise_bit_7 (
    .val(psg_noise_bit_6_valout), .clk1(not_25_out), .clk2(not_24_out), .reset(or_13_out),
    .valout(psg_noise_bit_7_valout));
  assign out_9 = psg_reg_bit3_5_out_5 | bit_extender_7_out;  // OR_Gate or_16, 4 bits wide
  psg_reg_bit3 psg_reg_bit3_5 (
    .val(d_ff_1_q[0]), .wr(not_26_out), .nwr(or_9_out), .reset(psg_clk_1_reset_sync),
    .out_5(psg_reg_bit3_5_out_5[0]));
  psg_reg_bit3 psg_reg_bit3_6 (
    .val(d_ff_1_q[1]), .wr(not_26_out), .nwr(or_9_out), .reset(psg_clk_1_reset_sync),
    .out_5(psg_reg_bit3_5_out_5[1]));
  psg_reg_bit3 psg_reg_bit3_7 (
    .val(d_ff_1_q[2]), .wr(not_26_out), .nwr(or_9_out), .reset(psg_clk_1_reset_sync),
    .out_5(psg_reg_bit3_5_out_5[2]));
  psg_reg_bit3 psg_reg_bit3_8 (
    .val(d_ff_1_q[3]), .wr(not_26_out), .nwr(or_9_out), .reset(psg_clk_1_reset_sync),
    .out_5(psg_reg_bit3_5_out_5[3]));
  not not_27 (not_27_out, or_10_out);
  assign bit_extender_8_out = {{3{psg_sign_bit_3_sign}}, psg_sign_bit_3_sign};  // Bit_Extender bit_extender_8
  psg_noise_bit psg_noise_bit_8 (
    .val(psg_noise_bit_7_valout), .clk1(not_25_out), .clk2(not_24_out), .reset(or_13_out),
    .valout(psg_noise_bit_8_valout));
  psg_noise_bit psg_noise_bit_9 (
    .val(psg_noise_bit_8_valout), .clk1(not_25_out), .clk2(not_24_out), .reset(or_13_out),
    .valout(psg_noise_bit_9_valout));
  psg_noise_bit psg_noise_bit_10 (
    .val(psg_noise_bit_9_valout), .clk1(not_25_out), .clk2(not_24_out), .reset(or_13_out),
    .valout(psg_noise_bit_10_valout));
  psg_noise_bit psg_noise_bit_11 (
    .val(psg_noise_bit_10_valout), .clk1(not_25_out), .clk2(not_24_out), .reset(or_13_out),
    .valout(psg_noise_bit_11_valout));
  psg_noise_bit psg_noise_bit_12 (
    .val(psg_noise_bit_11_valout), .clk1(not_25_out), .clk2(not_24_out), .reset(or_13_out),
    .valout(psg_noise_bit_12_valout));
  psg_noise_bit psg_noise_bit_13 (
    .val(psg_noise_bit_12_valout), .clk1(not_25_out), .clk2(not_24_out), .reset(or_13_out),
    .valout(psg_noise_bit_13_valout));
  psg_noise_bit psg_noise_bit_14 (
    .val(psg_noise_bit_13_valout), .clk1(not_25_out), .clk2(not_24_out), .reset(or_13_out),
    .valout(psg_noise_bit_14_valout));
  psg_noise_bit psg_noise_bit_15 (
    .val(psg_noise_bit_14_valout), .clk1(not_25_out), .clk2(not_24_out), .reset(or_13_out),
    .valout(psg_noise_bit_15_valout));
  psg_noise_bit psg_noise_bit_16 (
    .val(psg_noise_bit_15_valout), .clk1(not_25_out), .clk2(not_24_out), .reset(or_13_out),
    .valout(psg_noise_bit_16_valout));
  psg_reg_bit3 psg_reg_bit3_9 (
    .val(d_ff_1_q[0]), .wr(not_27_out), .nwr(or_10_out), .reset(psg_clk_1_reset_sync),
    .out_5(psg_reg_bit3_9_out_5[0]));
  psg_reg_bit3 psg_reg_bit3_10 (
    .val(d_ff_1_q[1]), .wr(not_27_out), .nwr(or_10_out), .reset(psg_clk_1_reset_sync),
    .out_5(psg_reg_bit3_9_out_5[1]));
  psg_reg_bit3 psg_reg_bit3_11 (
    .val(d_ff_1_q[2]), .wr(not_27_out), .nwr(or_10_out), .reset(psg_clk_1_reset_sync),
    .out_5(psg_reg_bit3_9_out_5[2]));
  psg_reg_bit3 psg_reg_bit3_12 (
    .val(d_ff_1_q[3]), .wr(not_27_out), .nwr(or_10_out), .reset(psg_clk_1_reset_sync),
    .out_5(psg_reg_bit3_9_out_5[3]));
  assign out_10 = psg_reg_bit3_9_out_5 | bit_extender_8_out;  // OR_Gate or_17, 4 bits wide
  not not_28 (not_28_out, or_11_out);
  xor xor_1 (xor_1_out, psg_noise_bit_13_valout, psg_noise_bit_16_valout);
  not not_29 (not_29_out, psg_noise_bit_15_valout);
  nor nor_14 (nor_14_out, psg_noise_bit_1_valout, psg_noise_bit_2_valout, psg_noise_bit_3_valout, psg_noise_bit_4_valout, psg_noise_bit_5_valout, psg_noise_bit_6_valout, psg_noise_bit_7_valout, psg_noise_bit_8_valout, psg_noise_bit_9_valout, psg_noise_bit_10_valout, psg_noise_bit_11_valout, psg_noise_bit_12_valout, psg_noise_bit_13_valout, psg_noise_bit_14_valout, psg_noise_bit_15_valout);
  assign bit_extender_9_out = {{3{not_29_out}}, not_29_out};  // Bit_Extender bit_extender_9
  psg_reg_bit3 psg_reg_bit3_13 (
    .val(d_ff_1_q[0]), .wr(not_28_out), .nwr(or_11_out), .reset(psg_clk_1_reset_sync),
    .out_5(psg_reg_bit3_13_out_5[0]));
  psg_reg_bit3 psg_reg_bit3_14 (
    .val(d_ff_1_q[1]), .wr(not_28_out), .nwr(or_11_out), .reset(psg_clk_1_reset_sync),
    .out_5(psg_reg_bit3_13_out_5[1]));
  psg_reg_bit3 psg_reg_bit3_15 (
    .val(d_ff_1_q[2]), .wr(not_28_out), .nwr(or_11_out), .reset(psg_clk_1_reset_sync),
    .out_5(psg_reg_bit3_13_out_5[2]));
  psg_reg_bit3 psg_reg_bit3_16 (
    .val(d_ff_1_q[3]), .wr(not_28_out), .nwr(or_11_out), .reset(psg_clk_1_reset_sync),
    .out_5(psg_reg_bit3_13_out_5[3]));
  assign out_11 = psg_reg_bit3_13_out_5 | bit_extender_9_out;  // OR_Gate or_18, 4 bits wide
endmodule

module sr_bit (
  input  val,
  input  clk1,
  input  clk2,
  output valout,
  output nvalout
);

  wire d_ff_1_q;

  D_Flip_Flop #(.trigger("high")) d_ff_1 (.D(val), .clk(clk1), .Q(d_ff_1_q));  // open: Qn, preset, reset
  D_Flip_Flop #(.trigger("high")) d_ff_2 (.D(d_ff_1_q), .clk(clk2), .Q(valout), .Qn(nvalout));  // open: preset, reset
endmodule

module psg_clk (
  input  clk,
  input  reset,
  output clk1,
  output clk2,
  output hclk1,
  output hclk2,
  output reset_sync
);

  wire d_ff_1_q, d_ff_3_q, d_ff_4_qn, d_ff_5_q, d_ff_6_q, d_ff_7_qn, d_ff_8_qn, d_ff_9_q, nor_1_out,
       nor_2_out, nor_3_out, not_1_out, not_4_out, not_5_out, not_6_out, not_7_out, or_1_out, or_2_out,
       or_3_out, or_4_out, xnor_1_out;

  not not_1 (not_1_out, clk);
  or or_1 (or_1_out, clk, clk2);
  or or_2 (or_2_out, not_1_out, clk1);
  not not_2 (clk1, or_1_out);
  not not_3 (clk2, or_2_out);
  D_Flip_Flop #(.trigger("high")) d_ff_1 (.D(reset), .clk(clk1), .Q(d_ff_1_q));  // open: Qn, preset, reset
  D_Flip_Flop #(.trigger("high")) d_ff_2 (.D(d_ff_1_q), .clk(clk2), .Qn(reset_sync));  // open: Q, preset, reset
  not not_4 (not_4_out, reset_sync);
  D_Flip_Flop #(.trigger("high")) d_ff_3 (.D(not_4_out), .clk(clk1), .Q(d_ff_3_q));  // open: Qn, preset, reset
  D_Flip_Flop #(.trigger("high")) d_ff_4 (.D(d_ff_3_q), .clk(clk2), .Qn(d_ff_4_qn));  // open: Q, preset, reset
  nor nor_1 (nor_1_out, d_ff_4_qn, not_4_out);
  nor nor_2 (nor_2_out, d_ff_6_q, nor_1_out);
  D_Flip_Flop #(.trigger("high")) d_ff_5 (.D(nor_2_out), .clk(clk1), .Q(d_ff_5_q));  // open: Qn, preset, reset
  D_Flip_Flop #(.trigger("high")) d_ff_6 (.D(d_ff_5_q), .clk(clk2), .Q(d_ff_6_q));  // open: Qn, preset, reset
  not not_5 (not_5_out, d_ff_6_q);
  xnor xnor_1 (xnor_1_out, not_5_out, d_ff_9_q);
  nor nor_3 (nor_3_out, xnor_1_out, nor_1_out);
  D_Flip_Flop #(.trigger("high")) d_ff_7 (.D(nor_3_out), .clk(clk1), .Qn(d_ff_7_qn));  // open: Q, preset, reset
  D_Flip_Flop #(.trigger("high")) d_ff_8 (.D(d_ff_7_qn), .clk(clk2), .Qn(d_ff_8_qn));  // open: Q, preset, reset
  D_Flip_Flop #(.trigger("high")) d_ff_9 (.D(d_ff_7_qn), .clk(clk2), .Q(d_ff_9_q));  // open: Qn, preset, reset
  not not_6 (not_6_out, d_ff_7_qn);
  or or_3 (or_3_out, d_ff_8_qn, not_6_out);
  not not_7 (not_7_out, d_ff_8_qn);
  or or_4 (or_4_out, not_7_out, d_ff_7_qn);
  not not_8 (hclk1, or_3_out);
  not not_9 (hclk2, or_4_out);
endmodule

module nmi_logic (
  input  reset,
  input  nmi_in,
  input  in_3,
  output nmi
);

  wire nand_1_out, nand_2_out, nand_3_out, nand_4_out, nand_6_out, not_1_out;

  not not_1 (not_1_out, nmi_in);
  nand nand_1 (nand_1_out, nand_2_out, reset, not_1_out);
  nand nand_2 (nand_2_out, nand_1_out, in_3, nand_3_out);
  nand nand_3 (nand_3_out, nand_4_out, reset, in_3);
  nand nand_4 (nand_4_out, nand_1_out, nand_3_out);
  nand nand_5 (nmi, nand_3_out, nand_6_out);
  nand nand_6 (nand_6_out, nmi, reset, nand_2_out);
endmodule

module psg_reg_bit (
  input  val,
  input  wr,
  input  nwr,
  input  reset,
  output out_5
);

  wire controlled_buffer_1_out, d_ff_1_qn;

  assign controlled_buffer_1_out = wr ? val : 1'bz;  // Controlled_Buffer controlled_buffer_1
  assign controlled_buffer_1_out = nwr ? out_5 : 1'bz;  // Controlled_Buffer controlled_buffer_2
  D_Flip_Flop #(.trigger("high")) d_ff_1 (
    .D(controlled_buffer_1_out), .clk(1'b1), .Qn(d_ff_1_qn));  // open: Q, preset, reset
  nor nor_1 (out_5, d_ff_1_qn, reset);
endmodule

module latch_10bit (
  input  [9:0] val,
  input  clk,
  output [9:0] val_out
);

  D_Flip_Flop #(.trigger("high")) d_ff_1 (.D(val[0]), .clk(clk), .Qn(val_out[0]));  // open: Q, preset, reset
  D_Flip_Flop #(.trigger("high")) d_ff_2 (.D(val[1]), .clk(clk), .Qn(val_out[1]));  // open: Q, preset, reset
  D_Flip_Flop #(.trigger("high")) d_ff_3 (.D(val[2]), .clk(clk), .Qn(val_out[2]));  // open: Q, preset, reset
  D_Flip_Flop #(.trigger("high")) d_ff_4 (.D(val[3]), .clk(clk), .Qn(val_out[3]));  // open: Q, preset, reset
  D_Flip_Flop #(.trigger("high")) d_ff_5 (.D(val[4]), .clk(clk), .Qn(val_out[4]));  // open: Q, preset, reset
  D_Flip_Flop #(.trigger("high")) d_ff_6 (.D(val[5]), .clk(clk), .Qn(val_out[5]));  // open: Q, preset, reset
  D_Flip_Flop #(.trigger("high")) d_ff_7 (.D(val[6]), .clk(clk), .Qn(val_out[6]));  // open: Q, preset, reset
  D_Flip_Flop #(.trigger("high")) d_ff_8 (.D(val[7]), .clk(clk), .Qn(val_out[7]));  // open: Q, preset, reset
  D_Flip_Flop #(.trigger("high")) d_ff_9 (.D(val[8]), .clk(clk), .Qn(val_out[8]));  // open: Q, preset, reset
  D_Flip_Flop #(.trigger("high")) d_ff_10 (.D(val[9]), .clk(clk), .Qn(val_out[9]));  // open: Q, preset, reset
endmodule

module cmp_bit (
  input  cin,
  input  a,
  input  b,
  output cout
);

  wire and_1_out, nor_1_out, nor_2_out;

  nor nor_1 (nor_1_out, b, a);
  nor nor_2 (nor_2_out, cin, nor_1_out);
  and and_1 (and_1_out, a, b);
  nor nor_3 (cout, nor_2_out, and_1_out);
endmodule

module psg_reg_bit2 (
  input  val,
  input  wr,
  input  nwr,
  input  reset,
  output out_5
);

  wire controlled_buffer_1_out, d_ff_1_qn, nor_1_out;

  assign controlled_buffer_1_out = wr ? val : 1'bz;  // Controlled_Buffer controlled_buffer_1
  assign controlled_buffer_1_out = nwr ? nor_1_out : 1'bz;  // Controlled_Buffer controlled_buffer_2
  D_Flip_Flop #(.trigger("high")) d_ff_1 (
    .D(controlled_buffer_1_out), .clk(1'b1), .Q(out_5), .Qn(d_ff_1_qn));  // open: preset, reset
  nor nor_1 (nor_1_out, d_ff_1_qn, reset);
endmodule

module psg_sign_bit (
  input  step,
  input  reset,
  input  val,
  input  clk1,
  input  clk2,
  output sign,
  output valout
);

  wire d_ff_1_q, d_ff_4_q, nand_1_out, nor_1_out, xnor_1_out;

  D_Flip_Flop #(.trigger("high")) d_ff_1 (.D(val), .clk(clk1), .Q(d_ff_1_q));  // open: Qn, preset, reset
  nand nand_1 (nand_1_out, valout, step);
  D_Flip_Flop #(.trigger("high")) d_ff_2 (.D(d_ff_1_q), .clk(clk2), .Q(valout));  // open: Qn, preset, reset
  xnor xnor_1 (xnor_1_out, d_ff_4_q, nand_1_out);
  D_Flip_Flop #(.trigger("high")) d_ff_3 (.D(nor_1_out), .clk(clk1), .Qn(sign));  // open: Q, preset, reset
  nor nor_1 (nor_1_out, xnor_1_out, reset);
  D_Flip_Flop #(.trigger("high")) d_ff_4 (.D(sign), .clk(clk2), .Q(d_ff_4_q));  // open: Qn, preset, reset
endmodule

module psg_noise_bit (
  input  val,
  input  clk1,
  input  clk2,
  input  reset,
  output valout
);

  wire controlled_buffer_1_out, controlled_buffer_3_out, d_ff_1_qn, d_ff_2_qn, nor_1_out;

  assign controlled_buffer_1_out = clk1 ? val : 1'bz;  // Controlled_Buffer controlled_buffer_1
  assign controlled_buffer_1_out = clk2 ? nor_1_out : 1'bz;  // Controlled_Buffer controlled_buffer_2
  D_Flip_Flop #(.trigger("high")) d_ff_1 (
    .D(controlled_buffer_1_out), .clk(1'b1), .Qn(d_ff_1_qn));  // open: Q, preset, reset
  nor nor_1 (nor_1_out, d_ff_1_qn, reset);
  assign controlled_buffer_3_out = clk1 ? valout : 1'bz;  // Controlled_Buffer controlled_buffer_3
  assign controlled_buffer_3_out = clk2 ? nor_1_out : 1'bz;  // Controlled_Buffer controlled_buffer_4
  D_Flip_Flop #(.trigger("high")) d_ff_2 (
    .D(controlled_buffer_3_out), .clk(1'b1), .Qn(d_ff_2_qn));  // open: Q, preset, reset
  nor nor_2 (valout, d_ff_2_qn, reset);
endmodule

module psg_reg_bit3 (
  input  val,
  input  wr,
  input  nwr,
  input  reset,
  output out_5
);

  wire controlled_buffer_1_out, d_ff_1_q;

  assign controlled_buffer_1_out = wr ? val : 1'bz;  // Controlled_Buffer controlled_buffer_1
  assign controlled_buffer_1_out = nwr ? out_5 : 1'bz;  // Controlled_Buffer controlled_buffer_2
  D_Flip_Flop #(.trigger("high")) d_ff_1 (
    .D(controlled_buffer_1_out), .clk(1'b1), .Q(d_ff_1_q));  // open: Qn, preset, reset
  or or_1 (out_5, d_ff_1_q, reset);
endmodule

module io_ctrl (
  input  RD,
  input  WR,
  input  IORQ,
  input  A0,
  input  A6,
  input  A7,
  output hv_read
);

  wire d_ff_1_q, d_ff_2_qn, nor_1_out, nor_2_out, nor_3_out, nor_5_out, nor_6_out, nor_7_out, not_1_out,
       not_2_out, not_3_out, not_4_out, not_5_out, not_6_out;

  not not_1 (not_1_out, A7);
  not not_2 (not_2_out, A6);
  not not_3 (not_3_out, d_ff_2_qn);
  or or_1 (hv_read, RD, IORQ, not_2_out, A7);
  nor nor_1 (nor_1_out, RD, IORQ, A6, not_1_out);
  nor nor_2 (nor_2_out, WR, IORQ, A6, not_1_out);
  not not_4 (not_4_out, A0);
  nor nor_3 (nor_3_out, not_3_out, not_6_out);
  // NOR_Gate nor_4 has open pins: in0=d_ff_2_qn, in1=not_6_out, out=open
  nor nor_5 (nor_5_out, d_ff_2_qn, not_6_out);
  // OR_Gate or_2 has open pins: in0=nor_3_out, in1=nor_5_out, in2=nor_7_out, in3=nor_6_out, out=open
  nor nor_6 (nor_6_out, not_5_out, not_4_out);
  nor nor_7 (nor_7_out, not_5_out, A0);
  not not_5 (not_5_out, nor_1_out);
  not not_6 (not_6_out, nor_2_out);
  // OR_Gate or_3 has open pins: in0=nor_1_out, in1=nor_2_out, out=open
  D_Flip_Flop #(.trigger("high")) d_ff_1 (.D(A0), .clk(not_5_out), .Q(d_ff_1_q));  // open: Qn, preset, reset
  D_Flip_Flop #(.trigger("high")) d_ff_2 (.D(A0), .clk(not_6_out), .Qn(d_ff_2_qn));  // open: Q, preset, reset
  // NOR_Gate nor_8 has open pins: in0=d_ff_1_q, in1=not_5_out, out=open
endmodule

module clocks (
  input  xin,
  input  reset,
  output clk1,
  output clk2,
  output hclk1,
  output hclk2,
  output zclk,
  output reset_sync
);

  wire controlled_buffer_1_out, d_ff_1_qn, d_ff_2_q, d_ff_3_qn, d_ff_4_qn, d_ff_5_qn, d_ff_6_qn, d_ff_7_q,
       d_ff_8_qn, d_ff_9_q, d_ff_10_q, d_ff_11_q, d_ff_12_q, multiplexer_1_out, nor_1_out, nor_2_out,
       nor_5_out, nor_6_out, nor_7_out, nor_8_out, not_1_out, not_2_out, not_3_out, not_4_out, not_5_out,
       not_6_out, not_7_out, not_8_out, not_9_out, not_11_out, not_12_out, sr_bit_1_valout, sr_bit_2_nvalout,
       sr_bit_3_valout, sr_bit_4_valout, sr_bit_5_valout, sr_bit_6_valout, sr_bit_7_valout;

  not not_1 (not_1_out, xin);
  D_Flip_Flop #(.trigger("high")) d_ff_1 (.D(d_ff_4_qn), .clk(clk1), .Qn(d_ff_1_qn));  // open: Q, preset, reset
  D_Flip_Flop #(.trigger("high")) d_ff_2 (.D(not_6_out), .clk(clk1), .Q(d_ff_2_q));  // open: Qn, preset, reset
  not not_2 (not_2_out, xin);
  not not_3 (not_3_out, not_1_out);
  sr_bit sr_bit_1 (.clk2(clk1), .val(reset), .clk1(clk2), .valout(sr_bit_1_valout));  // open: nvalout
  sr_bit sr_bit_2 (.clk2(clk1), .val(sr_bit_1_valout), .clk1(clk2), .nvalout(sr_bit_2_nvalout));  // open: valout
  not not_4 (not_4_out, not_2_out);
  not not_5 (not_5_out, not_3_out);
  D_Flip_Flop #(.trigger("high")) d_ff_3 (.D(nor_1_out), .clk(clk2), .Qn(d_ff_3_qn));  // open: Q, preset, reset
  nor nor_1 (nor_1_out, d_ff_1_qn, d_ff_2_q);
  nor nor_2 (nor_2_out, sr_bit_2_nvalout, reset);
  nor nor_3 (clk1, not_4_out, clk2);
  nor nor_4 (clk2, not_5_out, clk1);
  D_Flip_Flop #(.trigger("high")) d_ff_4 (.D(nor_2_out), .clk(clk2), .Qn(d_ff_4_qn));  // open: Q, preset, reset
  assign controlled_buffer_1_out = hclk2 ? reset : 1'bz;  // Controlled_Buffer controlled_buffer_1
  assign controlled_buffer_1_out = hclk1 ? d_ff_7_q : 1'bz;  // Controlled_Buffer controlled_buffer_2
  D_Flip_Flop #(.trigger("high")) d_ff_5 (.D(d_ff_3_qn), .clk(clk1), .Qn(d_ff_5_qn));  // open: Q, preset, reset
  D_Flip_Flop #(.trigger("high")) d_ff_6 (.D(not_6_out), .clk(clk1), .Qn(d_ff_6_qn));  // open: Q, preset, reset
  not not_6 (not_6_out, d_ff_3_qn);
  D_Flip_Flop #(.trigger("high")) d_ff_7 (
    .D(controlled_buffer_1_out), .clk(1'b1), .Q(d_ff_7_q));  // open: Qn, preset, reset
  D_Flip_Flop #(.trigger("high")) d_ff_8 (.D(d_ff_4_qn), .clk(clk1), .Qn(d_ff_8_qn));  // open: Q, preset, reset
  D_Flip_Flop #(.trigger("high")) d_ff_9 (
    .D(controlled_buffer_1_out), .clk(hclk1), .Q(d_ff_9_q));  // open: Qn, preset, reset
  D_Flip_Flop #(.trigger("high")) d_ff_10 (.D(d_ff_5_qn), .clk(clk2), .Q(d_ff_10_q));  // open: Qn, preset, reset
  D_Flip_Flop #(.trigger("high")) d_ff_11 (.D(d_ff_6_qn), .clk(clk2), .Q(d_ff_11_q));  // open: Qn, preset, reset
  nor nor_5 (nor_5_out, d_ff_8_qn, sr_bit_3_valout, sr_bit_5_valout);
  not not_7 (not_7_out, sr_bit_3_valout);
  sr_bit sr_bit_3 (.clk2(clk1), .val(nor_5_out), .clk1(clk2), .valout(sr_bit_3_valout));  // open: nvalout
  sr_bit sr_bit_4 (.clk2(hclk1), .val(not_7_out), .clk1(hclk2), .valout(sr_bit_4_valout));  // open: nvalout
  nor nor_6 (nor_6_out, d_ff_10_q, not_12_out);
  nor nor_7 (nor_7_out, d_ff_11_q, not_11_out);
  sr_bit sr_bit_5 (.clk2(clk1), .val(sr_bit_3_valout), .clk1(clk2), .valout(sr_bit_5_valout));  // open: nvalout
  sr_bit sr_bit_6 (.clk2(hclk1), .val(sr_bit_4_valout), .clk1(hclk2), .valout(sr_bit_6_valout));  // open: nvalout
  not not_8 (not_8_out, nor_6_out);
  not not_9 (not_9_out, nor_7_out);
  sr_bit sr_bit_7 (.clk2(clk1), .val(sr_bit_5_valout), .clk1(clk2), .valout(sr_bit_7_valout));  // open: nvalout
  not not_10 (hclk2, not_8_out);
  not not_11 (not_11_out, not_8_out);
  not not_12 (not_12_out, not_9_out);
  not not_13 (hclk1, not_9_out);
  D_Flip_Flop #(.trigger("high")) d_ff_12 (.D(sr_bit_3_valout), .clk(clk2), .Q(d_ff_12_q));  // open: Qn, preset, reset
  Multiplexer multiplexer_1 (.in0(hclk2), .in1(1'b0), .out(multiplexer_1_out), .sel(sr_bit_6_valout));
  D_Flip_Flop #(.trigger("high")) d_ff_13 (
    .D(d_ff_9_q), .clk(multiplexer_1_out), .Qn(reset_sync));  // open: Q, preset, reset
  nor nor_8 (nor_8_out, d_ff_12_q, zclk);
  nor nor_9 (zclk, nor_8_out, sr_bit_7_valout);
endmodule

module vcounter_bit (
  input  cin,
  input  reset,
  input  loadval,
  input  clk1,
  input  clk2,
  output cout,
  output outval
);

  wire and_1_out, d_ff_1_q, d_ff_2_q, d_ff_3_q, nor_2_out, nor_3_out, not_1_out, xnor_1_out;

  not not_1 (not_1_out, cin);
  D_Flip_Flop #(.trigger("high")) d_ff_1 (.D(reset), .clk(clk1), .Q(d_ff_1_q));  // open: Qn, preset, reset
  nor nor_1 (cout, not_1_out, d_ff_3_q);
  xnor xnor_1 (xnor_1_out, not_1_out, d_ff_3_q);
  nor nor_2 (nor_2_out, xnor_1_out, reset);
  D_Flip_Flop #(.trigger("high")) d_ff_2 (.D(nor_2_out), .clk(clk1), .Q(d_ff_2_q));  // open: Qn, preset, reset
  and and_1 (and_1_out, d_ff_1_q, loadval);
  nor nor_3 (nor_3_out, d_ff_2_q, and_1_out);
  D_Flip_Flop #(.trigger("high")) d_ff_3 (.D(nor_3_out), .clk(clk2), .Q(d_ff_3_q));  // open: Qn, preset, reset
  not not_2 (outval, nor_3_out);
endmodule

module vcounter (
  input  pal,
  input  vcinc,
  input  tr_reset,
  input  vc_reset,
  input  clk1,
  input  clk2,
  output [8:0] vc,
  output v1,
  output v2,
  output v3,
  output v4,
  output v5,
  output v6
);

  wire and_1_out, d_ff_1_q, d_ff_2_q, d_ff_4_q, d_ff_5_q, d_ff_6_q, d_ff_7_q, d_ff_8_q, d_ff_9_q, d_ff_10_q,
       d_ff_11_q, d_ff_13_q, d_ff_15_q, nor_1_out, nor_2_out, nor_3_out, nor_4_out, nor_5_out, nor_6_out,
       not_1_out, or_1_out, or_2_out, vcounter_bit_1_cout, vcounter_bit_2_cout, vcounter_bit_3_cout,
       vcounter_bit_4_cout, vcounter_bit_5_cout, vcounter_bit_6_cout, vcounter_bit_7_cout,
       vcounter_bit_8_cout, vpla_1_out_4, vpla_1_out_5, vpla_1_out_6, vpla_1_out_7, vpla_1_out_8,
       vpla_1_out_9, vpla_1_out_10, vpla_1_out_11, vpla_1_out_12, vpla_1_out_13, vpla_1_out_14,
       vpla_1_out_15, vpla_1_out_16, vpla_1_out_17;

  not not_1 (not_1_out, pal);
  D_Flip_Flop #(.trigger("high")) d_ff_1 (.D(vcinc), .clk(clk1), .Q(d_ff_1_q));  // open: Qn, preset, reset
  vcounter_bit vcounter_bit_1 (
    .cin(d_ff_1_q), .reset(d_ff_2_q), .loadval(not_1_out), .clk1(clk2), .clk2(clk1),
    .cout(vcounter_bit_1_cout), .outval(vc[0]));
  vcounter_bit vcounter_bit_2 (
    .cin(vcounter_bit_1_cout), .reset(d_ff_2_q), .loadval(pal), .clk1(clk2), .clk2(clk1),
    .cout(vcounter_bit_2_cout), .outval(vc[1]));
  vcounter_bit vcounter_bit_3 (
    .cin(vcounter_bit_2_cout), .reset(d_ff_2_q), .loadval(not_1_out), .clk1(clk2), .clk2(clk1),
    .cout(vcounter_bit_3_cout), .outval(vc[2]));
  vcounter_bit vcounter_bit_4 (
    .cin(vcounter_bit_3_cout), .reset(d_ff_2_q), .loadval(pal), .clk1(clk2), .clk2(clk1),
    .cout(vcounter_bit_4_cout), .outval(vc[3]));
  vcounter_bit vcounter_bit_5 (
    .cin(vcounter_bit_4_cout), .reset(d_ff_2_q), .loadval(1'b1), .clk1(clk2), .clk2(clk1),
    .cout(vcounter_bit_5_cout), .outval(vc[4]));
  vcounter_bit vcounter_bit_6 (
    .cin(vcounter_bit_5_cout), .reset(d_ff_2_q), .loadval(pal), .clk1(clk2), .clk2(clk1),
    .cout(vcounter_bit_6_cout), .outval(vc[5]));
  vcounter_bit vcounter_bit_7 (
    .cin(vcounter_bit_6_cout), .reset(d_ff_2_q), .loadval(not_1_out), .clk1(clk2), .clk2(clk1),
    .cout(vcounter_bit_7_cout), .outval(vc[6]));
  vcounter_bit vcounter_bit_8 (
    .cin(vcounter_bit_7_cout), .reset(d_ff_2_q), .loadval(1'b1), .clk1(clk2), .clk2(clk1),
    .cout(vcounter_bit_8_cout), .outval(vc[7]));
  vcounter_bit vcounter_bit_9 (
    .cin(vcounter_bit_8_cout), .reset(d_ff_2_q), .loadval(1'b1), .clk1(clk2), .clk2(clk1), .outval(vc[8]));  // open: cout
  and and_1 (and_1_out, vcinc, d_ff_15_q);
  D_Flip_Flop #(.trigger("high")) d_ff_2 (.D(or_1_out), .clk(clk1), .Q(d_ff_2_q));  // open: Qn, preset, reset
  or or_1 (or_1_out, and_1_out, vc_reset);
  vpla vpla_1 (
    .vc(vc), .pal(pal), .clk(clk1), .out_4(vpla_1_out_4), .out_5(vpla_1_out_5), .out_6(vpla_1_out_6),
    .out_7(vpla_1_out_7), .out_8(vpla_1_out_8), .out_9(vpla_1_out_9), .out_10(vpla_1_out_10),
    .out_11(vpla_1_out_11), .out_12(vpla_1_out_12), .out_13(vpla_1_out_13), .out_14(vpla_1_out_14),
    .out_15(vpla_1_out_15), .out_16(vpla_1_out_16), .out_17(vpla_1_out_17));
  or or_2 (or_2_out, vpla_1_out_16, vpla_1_out_17);
  D_Flip_Flop #(.trigger("high")) d_ff_3 (.D(vpla_1_out_4), .clk(clk2), .Q(v1));  // open: Qn, preset, reset
  D_Flip_Flop #(.trigger("high")) d_ff_4 (.D(vpla_1_out_5), .clk(clk2), .Q(d_ff_4_q));  // open: Qn, preset, reset
  D_Flip_Flop #(.trigger("high")) d_ff_5 (.D(vpla_1_out_6), .clk(clk2), .Q(d_ff_5_q));  // open: Qn, preset, reset
  D_Flip_Flop #(.trigger("high")) d_ff_6 (.D(vpla_1_out_7), .clk(clk2), .Q(d_ff_6_q));  // open: Qn, preset, reset
  D_Flip_Flop #(.trigger("high")) d_ff_7 (.D(vpla_1_out_8), .clk(clk2), .Q(d_ff_7_q));  // open: Qn, preset, reset
  D_Flip_Flop #(.trigger("high")) d_ff_8 (.D(vpla_1_out_9), .clk(clk2), .Q(d_ff_8_q));  // open: Qn, preset, reset
  D_Flip_Flop #(.trigger("high")) d_ff_9 (.D(vpla_1_out_10), .clk(clk2), .Q(d_ff_9_q));  // open: Qn, preset, reset
  D_Flip_Flop #(.trigger("high")) d_ff_10 (.D(vpla_1_out_11), .clk(clk2), .Q(d_ff_10_q));  // open: Qn, preset, reset
  D_Flip_Flop #(.trigger("high")) d_ff_11 (.D(vpla_1_out_12), .clk(clk2), .Q(d_ff_11_q));  // open: Qn, preset, reset
  D_Flip_Flop #(.trigger("high")) d_ff_12 (.D(vpla_1_out_13), .clk(clk2), .Q(v4));  // open: Qn, preset, reset
  D_Flip_Flop #(.trigger("high")) d_ff_13 (.D(vpla_1_out_14), .clk(clk2), .Q(d_ff_13_q));  // open: Qn, preset, reset
  D_Flip_Flop #(.trigger("high")) d_ff_14 (.D(vpla_1_out_15), .clk(clk2), .Q(v6));  // open: Qn, preset, reset
  D_Flip_Flop #(.trigger("high")) d_ff_15 (.D(or_2_out), .clk(clk2), .Q(d_ff_15_q));  // open: Qn, preset, reset
  nor nor_1 (nor_1_out, d_ff_4_q, d_ff_5_q, nor_2_out);
  nor nor_2 (nor_2_out, nor_1_out, tr_reset, d_ff_6_q, d_ff_7_q);
  nor nor_3 (nor_3_out, d_ff_8_q, d_ff_9_q, nor_4_out);
  nor nor_4 (nor_4_out, nor_3_out, tr_reset, d_ff_10_q, d_ff_11_q);
  nor nor_5 (nor_5_out, d_ff_13_q, nor_6_out);
  nor nor_6 (nor_6_out, nor_5_out, v4, tr_reset);
  not not_2 (v2, nor_2_out);
  not not_3 (v3, nor_4_out);
  not not_4 (v5, nor_5_out);
endmodule

module vpla (
  input  [8:0] vc,
  input  pal,
  input  clk,
  output out_4,
  output out_5,
  output out_6,
  output out_7,
  output out_8,
  output out_9,
  output out_10,
  output out_11,
  output out_12,
  output out_13,
  output out_14,
  output out_15,
  output out_16,
  output out_17
);

  wire not_1_out, not_2_out, not_3_out, not_4_out, not_5_out, not_6_out, not_7_out, not_8_out, not_9_out,
       not_10_out, pull_resistor_1_node, pull_resistor_2_node, pull_resistor_3_node, pull_resistor_4_node,
       pull_resistor_5_node, pull_resistor_6_node, pull_resistor_7_node, pull_resistor_8_node,
       pull_resistor_9_node, pull_resistor_10_node, pull_resistor_11_node, pull_resistor_12_node,
       pull_resistor_13_node, pull_resistor_14_node;

  Pull_Resistor #(.pull(1)) pull_resistor_1 (.node(pull_resistor_1_node));
  Pull_Resistor #(.pull(1)) pull_resistor_2 (.node(pull_resistor_2_node));
  Pull_Resistor #(.pull(1)) pull_resistor_3 (.node(pull_resistor_3_node));
  Pull_Resistor #(.pull(1)) pull_resistor_4 (.node(pull_resistor_4_node));
  Pull_Resistor #(.pull(1)) pull_resistor_5 (.node(pull_resistor_5_node));
  Pull_Resistor #(.pull(1)) pull_resistor_6 (.node(pull_resistor_6_node));
  Pull_Resistor #(.pull(1)) pull_resistor_7 (.node(pull_resistor_7_node));
  Pull_Resistor #(.pull(1)) pull_resistor_8 (.node(pull_resistor_8_node));
  Pull_Resistor #(.pull(1)) pull_resistor_9 (.node(pull_resistor_9_node));
  Pull_Resistor #(.pull(1)) pull_resistor_10 (.node(pull_resistor_10_node));
  Pull_Resistor #(.pull(1)) pull_resistor_11 (.node(pull_resistor_11_node));
  Pull_Resistor #(.pull(1)) pull_resistor_12 (.node(pull_resistor_12_node));
  Pull_Resistor #(.pull(1)) pull_resistor_13 (.node(pull_resistor_13_node));
  Pull_Resistor #(.pull(1)) pull_resistor_14 (.node(pull_resistor_14_node));
  Transistor #(.\type ("n")) transistor_1 (.in(1'b0), .out(pull_resistor_3_node), .gate(pal));
  Transistor #(.\type ("n")) transistor_2 (.in(1'b0), .out(pull_resistor_5_node), .gate(pal));
  Transistor #(.\type ("n")) transistor_3 (.in(1'b0), .out(pull_resistor_7_node), .gate(pal));
  Transistor #(.\type ("n")) transistor_4 (.in(1'b0), .out(pull_resistor_9_node), .gate(pal));
  Transistor #(.\type ("n")) transistor_5 (.in(1'b0), .out(pull_resistor_14_node), .gate(pal));
  Transistor #(.\type ("n")) transistor_6 (.in(1'b0), .out(pull_resistor_2_node), .gate(not_1_out));
  Transistor #(.\type ("n")) transistor_7 (.in(1'b0), .out(pull_resistor_4_node), .gate(not_1_out));
  Transistor #(.\type ("n")) transistor_8 (.in(1'b0), .out(pull_resistor_6_node), .gate(not_1_out));
  Transistor #(.\type ("n")) transistor_9 (.in(1'b0), .out(pull_resistor_8_node), .gate(not_1_out));
  Transistor #(.\type ("n")) transistor_10 (.in(1'b0), .out(pull_resistor_13_node), .gate(not_1_out));
  not not_1 (not_1_out, pal);
  Transistor #(.\type ("n")) transistor_11 (.in(1'b0), .out(pull_resistor_2_node), .gate(not_2_out));
  Transistor #(.\type ("n")) transistor_12 (.in(1'b0), .out(pull_resistor_3_node), .gate(not_2_out));
  Transistor #(.\type ("n")) transistor_13 (.in(1'b0), .out(pull_resistor_4_node), .gate(not_2_out));
  Transistor #(.\type ("n")) transistor_14 (.in(1'b0), .out(pull_resistor_5_node), .gate(not_2_out));
  Transistor #(.\type ("n")) transistor_15 (.in(1'b0), .out(pull_resistor_6_node), .gate(not_2_out));
  Transistor #(.\type ("n")) transistor_16 (.in(1'b0), .out(pull_resistor_7_node), .gate(not_2_out));
  Transistor #(.\type ("n")) transistor_17 (.in(1'b0), .out(pull_resistor_12_node), .gate(not_2_out));
  not not_2 (not_2_out, vc[8]);
  Transistor #(.\type ("n")) transistor_18 (.in(1'b0), .out(pull_resistor_1_node), .gate(vc[8]));
  Transistor #(.\type ("n")) transistor_19 (.in(1'b0), .out(pull_resistor_8_node), .gate(vc[8]));
  Transistor #(.\type ("n")) transistor_20 (.in(1'b0), .out(pull_resistor_9_node), .gate(vc[8]));
  Transistor #(.\type ("n")) transistor_21 (.in(1'b0), .out(pull_resistor_10_node), .gate(vc[8]));
  Transistor #(.\type ("n")) transistor_22 (.in(1'b0), .out(pull_resistor_11_node), .gate(vc[8]));
  Transistor #(.\type ("n")) transistor_23 (.in(1'b0), .out(pull_resistor_13_node), .gate(vc[8]));
  Transistor #(.\type ("n")) transistor_24 (.in(1'b0), .out(pull_resistor_14_node), .gate(vc[8]));
  Transistor #(.\type ("n")) transistor_25 (.in(1'b0), .out(pull_resistor_2_node), .gate(not_3_out));
  Transistor #(.\type ("n")) transistor_26 (.in(1'b0), .out(pull_resistor_3_node), .gate(not_3_out));
  Transistor #(.\type ("n")) transistor_27 (.in(1'b0), .out(pull_resistor_4_node), .gate(not_3_out));
  Transistor #(.\type ("n")) transistor_28 (.in(1'b0), .out(pull_resistor_5_node), .gate(not_3_out));
  Transistor #(.\type ("n")) transistor_29 (.in(1'b0), .out(pull_resistor_6_node), .gate(not_3_out));
  Transistor #(.\type ("n")) transistor_30 (.in(1'b0), .out(pull_resistor_7_node), .gate(not_3_out));
  Transistor #(.\type ("n")) transistor_31 (.in(1'b0), .out(pull_resistor_8_node), .gate(not_3_out));
  Transistor #(.\type ("n")) transistor_32 (.in(1'b0), .out(pull_resistor_9_node), .gate(not_3_out));
  Transistor #(.\type ("n")) transistor_33 (.in(1'b0), .out(pull_resistor_10_node), .gate(not_3_out));
  Transistor #(.\type ("n")) transistor_34 (.in(1'b0), .out(pull_resistor_12_node), .gate(not_3_out));
  Transistor #(.\type ("n")) transistor_35 (.in(1'b0), .out(pull_resistor_13_node), .gate(not_3_out));
  Transistor #(.\type ("n")) transistor_36 (.in(1'b0), .out(pull_resistor_14_node), .gate(not_3_out));
  not not_3 (not_3_out, vc[7]);
  Transistor #(.\type ("n")) transistor_37 (.in(1'b0), .out(pull_resistor_11_node), .gate(vc[7]));
  Transistor #(.\type ("n")) transistor_38 (.in(1'b0), .out(pull_resistor_3_node), .gate(not_4_out));
  Transistor #(.\type ("n")) transistor_39 (.in(1'b0), .out(pull_resistor_5_node), .gate(not_4_out));
  Transistor #(.\type ("n")) transistor_40 (.in(1'b0), .out(pull_resistor_6_node), .gate(not_4_out));
  Transistor #(.\type ("n")) transistor_41 (.in(1'b0), .out(pull_resistor_7_node), .gate(not_4_out));
  Transistor #(.\type ("n")) transistor_42 (.in(1'b0), .out(pull_resistor_8_node), .gate(not_4_out));
  Transistor #(.\type ("n")) transistor_43 (.in(1'b0), .out(pull_resistor_9_node), .gate(not_4_out));
  Transistor #(.\type ("n")) transistor_44 (.in(1'b0), .out(pull_resistor_10_node), .gate(not_4_out));
  Transistor #(.\type ("n")) transistor_45 (.in(1'b0), .out(pull_resistor_12_node), .gate(not_4_out));
  Transistor #(.\type ("n")) transistor_46 (.in(1'b0), .out(pull_resistor_13_node), .gate(not_4_out));
  Transistor #(.\type ("n")) transistor_47 (.in(1'b0), .out(pull_resistor_14_node), .gate(not_4_out));
  not not_4 (not_4_out, vc[6]);
  Transistor #(.\type ("n")) transistor_48 (.in(1'b0), .out(pull_resistor_2_node), .gate(vc[6]));
  Transistor #(.\type ("n")) transistor_49 (.in(1'b0), .out(pull_resistor_4_node), .gate(vc[6]));
  Transistor #(.\type ("n")) transistor_50 (.in(1'b0), .out(pull_resistor_11_node), .gate(vc[6]));
  Transistor #(.\type ("n")) transistor_51 (.in(1'b0), .out(pull_resistor_2_node), .gate(not_5_out));
  Transistor #(.\type ("n")) transistor_52 (.in(1'b0), .out(pull_resistor_4_node), .gate(not_5_out));
  Transistor #(.\type ("n")) transistor_53 (.in(1'b0), .out(pull_resistor_7_node), .gate(not_5_out));
  Transistor #(.\type ("n")) transistor_54 (.in(1'b0), .out(pull_resistor_8_node), .gate(not_5_out));
  Transistor #(.\type ("n")) transistor_55 (.in(1'b0), .out(pull_resistor_12_node), .gate(not_5_out));
  Transistor #(.\type ("n")) transistor_56 (.in(1'b0), .out(pull_resistor_13_node), .gate(not_5_out));
  not not_5 (not_5_out, vc[5]);
  Transistor #(.\type ("n")) transistor_57 (.in(1'b0), .out(pull_resistor_3_node), .gate(vc[5]));
  Transistor #(.\type ("n")) transistor_58 (.in(1'b0), .out(pull_resistor_5_node), .gate(vc[5]));
  Transistor #(.\type ("n")) transistor_59 (.in(1'b0), .out(pull_resistor_6_node), .gate(vc[5]));
  Transistor #(.\type ("n")) transistor_60 (.in(1'b0), .out(pull_resistor_9_node), .gate(vc[5]));
  Transistor #(.\type ("n")) transistor_61 (.in(1'b0), .out(pull_resistor_10_node), .gate(vc[5]));
  Transistor #(.\type ("n")) transistor_62 (.in(1'b0), .out(pull_resistor_11_node), .gate(vc[5]));
  Transistor #(.\type ("n")) transistor_63 (.in(1'b0), .out(pull_resistor_14_node), .gate(vc[5]));
  Transistor #(.\type ("n")) transistor_64 (.in(1'b0), .out(pull_resistor_2_node), .gate(not_6_out));
  Transistor #(.\type ("n")) transistor_65 (.in(1'b0), .out(pull_resistor_3_node), .gate(not_6_out));
  Transistor #(.\type ("n")) transistor_66 (.in(1'b0), .out(pull_resistor_4_node), .gate(not_6_out));
  Transistor #(.\type ("n")) transistor_67 (.in(1'b0), .out(pull_resistor_5_node), .gate(not_6_out));
  Transistor #(.\type ("n")) transistor_68 (.in(1'b0), .out(pull_resistor_8_node), .gate(not_6_out));
  Transistor #(.\type ("n")) transistor_69 (.in(1'b0), .out(pull_resistor_9_node), .gate(not_6_out));
  Transistor #(.\type ("n")) transistor_70 (.in(1'b0), .out(pull_resistor_12_node), .gate(not_6_out));
  Transistor #(.\type ("n")) transistor_71 (.in(1'b0), .out(pull_resistor_13_node), .gate(not_6_out));
  Transistor #(.\type ("n")) transistor_72 (.in(1'b0), .out(pull_resistor_14_node), .gate(not_6_out));
  not not_6 (not_6_out, vc[4]);
  Transistor #(.\type ("n")) transistor_73 (.in(1'b0), .out(pull_resistor_6_node), .gate(vc[4]));
  Transistor #(.\type ("n")) transistor_74 (.in(1'b0), .out(pull_resistor_7_node), .gate(vc[4]));
  Transistor #(.\type ("n")) transistor_75 (.in(1'b0), .out(pull_resistor_10_node), .gate(vc[4]));
  Transistor #(.\type ("n")) transistor_76 (.in(1'b0), .out(pull_resistor_11_node), .gate(vc[4]));
  Transistor #(.\type ("n")) transistor_77 (.in(1'b0), .out(pull_resistor_2_node), .gate(not_7_out));
  Transistor #(.\type ("n")) transistor_78 (.in(1'b0), .out(pull_resistor_3_node), .gate(not_7_out));
  Transistor #(.\type ("n")) transistor_79 (.in(1'b0), .out(pull_resistor_4_node), .gate(not_7_out));
  Transistor #(.\type ("n")) transistor_80 (.in(1'b0), .out(pull_resistor_6_node), .gate(not_7_out));
  Transistor #(.\type ("n")) transistor_81 (.in(1'b0), .out(pull_resistor_9_node), .gate(not_7_out));
  Transistor #(.\type ("n")) transistor_82 (.in(1'b0), .out(pull_resistor_12_node), .gate(not_7_out));
  Transistor #(.\type ("n")) transistor_83 (.in(1'b0), .out(pull_resistor_14_node), .gate(not_7_out));
  not not_7 (not_7_out, vc[3]);
  Transistor #(.\type ("n")) transistor_84 (.in(1'b0), .out(pull_resistor_5_node), .gate(vc[3]));
  Transistor #(.\type ("n")) transistor_85 (.in(1'b0), .out(pull_resistor_7_node), .gate(vc[3]));
  Transistor #(.\type ("n")) transistor_86 (.in(1'b0), .out(pull_resistor_8_node), .gate(vc[3]));
  Transistor #(.\type ("n")) transistor_87 (.in(1'b0), .out(pull_resistor_10_node), .gate(vc[3]));
  Transistor #(.\type ("n")) transistor_88 (.in(1'b0), .out(pull_resistor_11_node), .gate(vc[3]));
  Transistor #(.\type ("n")) transistor_89 (.in(1'b0), .out(pull_resistor_13_node), .gate(vc[3]));
  Transistor #(.\type ("n")) transistor_90 (.in(1'b0), .out(pull_resistor_1_node), .gate(not_8_out));
  Transistor #(.\type ("n")) transistor_91 (.in(1'b0), .out(pull_resistor_2_node), .gate(not_8_out));
  Transistor #(.\type ("n")) transistor_92 (.in(1'b0), .out(pull_resistor_5_node), .gate(not_8_out));
  Transistor #(.\type ("n")) transistor_93 (.in(1'b0), .out(pull_resistor_7_node), .gate(not_8_out));
  Transistor #(.\type ("n")) transistor_94 (.in(1'b0), .out(pull_resistor_12_node), .gate(not_8_out));
  not not_8 (not_8_out, vc[2]);
  Transistor #(.\type ("n")) transistor_95 (.in(1'b0), .out(pull_resistor_3_node), .gate(vc[2]));
  Transistor #(.\type ("n")) transistor_96 (.in(1'b0), .out(pull_resistor_4_node), .gate(vc[2]));
  Transistor #(.\type ("n")) transistor_97 (.in(1'b0), .out(pull_resistor_6_node), .gate(vc[2]));
  Transistor #(.\type ("n")) transistor_98 (.in(1'b0), .out(pull_resistor_8_node), .gate(vc[2]));
  Transistor #(.\type ("n")) transistor_99 (.in(1'b0), .out(pull_resistor_9_node), .gate(vc[2]));
  Transistor #(.\type ("n")) transistor_100 (.in(1'b0), .out(pull_resistor_10_node), .gate(vc[2]));
  Transistor #(.\type ("n")) transistor_101 (.in(1'b0), .out(pull_resistor_11_node), .gate(vc[2]));
  Transistor #(.\type ("n")) transistor_102 (.in(1'b0), .out(pull_resistor_13_node), .gate(vc[2]));
  Transistor #(.\type ("n")) transistor_103 (.in(1'b0), .out(pull_resistor_14_node), .gate(vc[2]));
  Transistor #(.\type ("n")) transistor_104 (.in(1'b0), .out(pull_resistor_1_node), .gate(not_9_out));
  Transistor #(.\type ("n")) transistor_105 (.in(1'b0), .out(pull_resistor_4_node), .gate(not_9_out));
  Transistor #(.\type ("n")) transistor_106 (.in(1'b0), .out(pull_resistor_6_node), .gate(not_9_out));
  Transistor #(.\type ("n")) transistor_107 (.in(1'b0), .out(pull_resistor_12_node), .gate(not_9_out));
  Transistor #(.\type ("n")) transistor_108 (.in(1'b0), .out(pull_resistor_13_node), .gate(not_9_out));
  Transistor #(.\type ("n")) transistor_109 (.in(1'b0), .out(pull_resistor_14_node), .gate(not_9_out));
  not not_9 (not_9_out, vc[1]);
  Transistor #(.\type ("n")) transistor_110 (.in(1'b0), .out(pull_resistor_2_node), .gate(vc[1]));
  Transistor #(.\type ("n")) transistor_111 (.in(1'b0), .out(pull_resistor_3_node), .gate(vc[1]));
  Transistor #(.\type ("n")) transistor_112 (.in(1'b0), .out(pull_resistor_5_node), .gate(vc[1]));
  Transistor #(.\type ("n")) transistor_113 (.in(1'b0), .out(pull_resistor_7_node), .gate(vc[1]));
  Transistor #(.\type ("n")) transistor_114 (.in(1'b0), .out(pull_resistor_8_node), .gate(vc[1]));
  Transistor #(.\type ("n")) transistor_115 (.in(1'b0), .out(pull_resistor_9_node), .gate(vc[1]));
  Transistor #(.\type ("n")) transistor_116 (.in(1'b0), .out(pull_resistor_10_node), .gate(vc[1]));
  Transistor #(.\type ("n")) transistor_117 (.in(1'b0), .out(pull_resistor_11_node), .gate(vc[1]));
  Transistor #(.\type ("n")) transistor_118 (.in(1'b0), .out(pull_resistor_1_node), .gate(not_10_out));
  Transistor #(.\type ("n")) transistor_119 (.in(1'b0), .out(pull_resistor_2_node), .gate(not_10_out));
  Transistor #(.\type ("n")) transistor_120 (.in(1'b0), .out(pull_resistor_5_node), .gate(not_10_out));
  Transistor #(.\type ("n")) transistor_121 (.in(1'b0), .out(pull_resistor_7_node), .gate(not_10_out));
  Transistor #(.\type ("n")) transistor_122 (.in(1'b0), .out(pull_resistor_12_node), .gate(not_10_out));
  not not_10 (not_10_out, vc[0]);
  Transistor #(.\type ("n")) transistor_123 (.in(1'b0), .out(pull_resistor_3_node), .gate(vc[0]));
  Transistor #(.\type ("n")) transistor_124 (.in(1'b0), .out(pull_resistor_4_node), .gate(vc[0]));
  Transistor #(.\type ("n")) transistor_125 (.in(1'b0), .out(pull_resistor_6_node), .gate(vc[0]));
  Transistor #(.\type ("n")) transistor_126 (.in(1'b0), .out(pull_resistor_8_node), .gate(vc[0]));
  Transistor #(.\type ("n")) transistor_127 (.in(1'b0), .out(pull_resistor_9_node), .gate(vc[0]));
  Transistor #(.\type ("n")) transistor_128 (.in(1'b0), .out(pull_resistor_10_node), .gate(vc[0]));
  Transistor #(.\type ("n")) transistor_129 (.in(1'b0), .out(pull_resistor_11_node), .gate(vc[0]));
  Transistor #(.\type ("n")) transistor_130 (.in(1'b0), .out(pull_resistor_13_node), .gate(vc[0]));
  Transistor #(.\type ("n")) transistor_131 (.in(1'b0), .out(pull_resistor_14_node), .gate(vc[0]));
  D_Flip_Flop #(.trigger("high")) d_ff_1 (.D(pull_resistor_1_node), .clk(clk), .Q(out_4));  // open: Qn, preset, reset
  D_Flip_Flop #(.trigger("high")) d_ff_2 (.D(pull_resistor_2_node), .clk(clk), .Q(out_5));  // open: Qn, preset, reset
  D_Flip_Flop #(.trigger("high")) d_ff_3 (.D(pull_resistor_3_node), .clk(clk), .Q(out_6));  // open: Qn, preset, reset
  D_Flip_Flop #(.trigger("high")) d_ff_4 (.D(pull_resistor_4_node), .clk(clk), .Q(out_7));  // open: Qn, preset, reset
  D_Flip_Flop #(.trigger("high")) d_ff_5 (.D(pull_resistor_5_node), .clk(clk), .Q(out_8));  // open: Qn, preset, reset
  D_Flip_Flop #(.trigger("high")) d_ff_6 (.D(pull_resistor_6_node), .clk(clk), .Q(out_9));  // open: Qn, preset, reset
  D_Flip_Flop #(.trigger("high")) d_ff_7 (.D(pull_resistor_7_node), .clk(clk), .Q(out_10));  // open: Qn, preset, reset
  D_Flip_Flop #(.trigger("high")) d_ff_8 (.D(pull_resistor_8_node), .clk(clk), .Q(out_11));  // open: Qn, preset, reset
  D_Flip_Flop #(.trigger("high")) d_ff_9 (.D(pull_resistor_9_node), .clk(clk), .Q(out_12));  // open: Qn, preset, reset
  D_Flip_Flop #(.trigger("high")) d_ff_10 (
    .D(pull_resistor_10_node), .clk(clk), .Q(out_13));  // open: Qn, preset, reset
  D_Flip_Flop #(.trigger("high")) d_ff_11 (
    .D(pull_resistor_11_node), .clk(clk), .Q(out_14));  // open: Qn, preset, reset
  D_Flip_Flop #(.trigger("high")) d_ff_12 (
    .D(pull_resistor_12_node), .clk(clk), .Q(out_15));  // open: Qn, preset, reset
  D_Flip_Flop #(.trigger("high")) d_ff_13 (
    .D(pull_resistor_13_node), .clk(clk), .Q(out_16));  // open: Qn, preset, reset
  D_Flip_Flop #(.trigger("high")) d_ff_14 (
    .D(pull_resistor_14_node), .clk(clk), .Q(out_17));  // open: Qn, preset, reset
endmodule

module hcounter (
  input  clk1,
  input  clk2,
  input  r80b0,
  input  reset,
  output out_5
);

  wire and_1_out, and_2_out, and_3_out, d_ff_1_q, d_ff_2_qn, d_ff_3_qn, d_ff_4_qn, d_ff_5_q, nand_1_out,
       nor_1_out, nor_2_out, nor_3_out, nor_4_out, nor_5_out, nor_6_out, nor_7_out, nor_8_out, not_1_out,
       or_1_out, or_2_out, sr_bit_1_valout, sr_bit_2_valout, sr_bit_3_nvalout, sr_bit_4_valout,
       sr_bit_5_nvalout, sr_bit_6_valout, sr_bit_7_valout, sr_bit_8_valout, undriven, undriven_2, undriven_3,
       undriven_4, vcounter_bit_1_cout, vcounter_bit_2_cout, vcounter_bit_4_cout, vcounter_bit_5_cout,
       vcounter_bit_6_cout, vcounter_bit_7_cout, vcounter_bit_8_cout;
  wire [8:0] vcounter_bit_1_outval;

  not not_1 (not_1_out, r80b0);
  nand nand_1 (nand_1_out, r80b0, undriven);
  sr_bit sr_bit_1 (.clk2(clk2), .val(reset), .clk1(clk1), .valout(sr_bit_1_valout));  // open: nvalout
  nor nor_1 (nor_1_out, undriven_3, sr_bit_7_valout);
  nor nor_2 (nor_2_out, sr_bit_7_valout, sr_bit_3_nvalout);
  sr_bit sr_bit_2 (.clk2(clk2), .clk1(clk1), .valout(sr_bit_2_valout));  // open: val, nvalout
  sr_bit sr_bit_3 (.clk2(clk2), .val(nor_1_out), .clk1(clk1), .nvalout(sr_bit_3_nvalout));  // open: valout
  sr_bit sr_bit_4 (.clk2(clk2), .val(nor_2_out), .clk1(clk1), .valout(sr_bit_4_valout));  // open: nvalout
  sr_bit sr_bit_5 (.clk2(clk2), .val(sr_bit_6_valout), .clk1(clk1), .nvalout(sr_bit_5_nvalout));  // open: valout
  sr_bit sr_bit_6 (.clk2(clk2), .val(nand_1_out), .clk1(clk1), .valout(sr_bit_6_valout));  // open: nvalout
  and and_1 (and_1_out, sr_bit_2_valout, nor_1_out);
  nor nor_3 (nor_3_out, sr_bit_5_nvalout, sr_bit_6_valout, not_1_out);
  and and_2 (and_2_out, nand_1_out, undriven_2);
  or or_1 (or_1_out, nor_3_out, sr_bit_1_valout);
  sr_bit sr_bit_7 (.clk2(clk2), .val(or_2_out), .clk1(clk1), .valout(sr_bit_7_valout));  // open: nvalout
  nor nor_4 (nor_4_out, sr_bit_2_valout, or_2_out, sr_bit_7_valout);
  or or_2 (or_2_out, and_2_out, or_1_out);
  nor nor_5 (nor_5_out, not_1_out, sr_bit_6_valout);
  or or_3 (out_5, nor_5_out, sr_bit_1_valout);
  and and_3 (and_3_out, nor_4_out, sr_bit_4_valout);
  D_Flip_Flop #(.trigger("high")) d_ff_1 (.D(or_2_out), .clk(clk1), .Q(d_ff_1_q));  // open: Qn, preset, reset
  nor nor_6 (nor_6_out, and_3_out, and_1_out);
  nor nor_7 (nor_7_out, and_1_out, undriven_4, or_2_out);
  nor nor_8 (nor_8_out, or_2_out, undriven_4);
  D_Flip_Flop #(.trigger("high")) d_ff_2 (.D(nor_7_out), .clk(clk1), .Qn(d_ff_2_qn));  // open: Q, preset, reset
  D_Flip_Flop #(.trigger("high")) d_ff_3 (.D(nor_8_out), .clk(clk1), .Qn(d_ff_3_qn));  // open: Q, preset, reset
  D_Flip_Flop #(.trigger("high")) d_ff_4 (.D(nor_6_out), .clk(clk1), .Qn(d_ff_4_qn));  // open: Q, preset, reset
  sr_bit sr_bit_8 (.clk2(clk2), .val(undriven_4), .clk1(clk1), .valout(sr_bit_8_valout));  // open: nvalout
  D_Flip_Flop #(.trigger("high")) d_ff_5 (.D(d_ff_1_q), .clk(clk2), .Q(d_ff_5_q));  // open: Qn, preset, reset
  vcounter_bit vcounter_bit_1 (
    .cin(1'b1), .reset(d_ff_2_qn), .loadval(1'b0), .clk1(clk2), .clk2(clk1), .cout(vcounter_bit_1_cout),
    .outval(vcounter_bit_1_outval[0]));
  vcounter_bit vcounter_bit_2 (
    .cin(vcounter_bit_1_cout), .reset(d_ff_2_qn), .loadval(d_ff_5_q), .clk1(clk2), .clk2(clk1),
    .cout(vcounter_bit_2_cout), .outval(vcounter_bit_1_outval[1]));
  vcounter_bit vcounter_bit_3 (
    .cin(vcounter_bit_2_cout), .reset(d_ff_2_qn), .loadval(1'b0), .clk1(clk2), .clk2(clk1),
    .outval(vcounter_bit_1_outval[2]));  // open: cout
  vcounter_bit vcounter_bit_4 (
    .cin(d_ff_4_qn), .reset(d_ff_3_qn), .loadval(sr_bit_8_valout), .clk1(clk2), .clk2(clk1),
    .cout(vcounter_bit_4_cout), .outval(vcounter_bit_1_outval[3]));
  vcounter_bit vcounter_bit_5 (
    .cin(vcounter_bit_4_cout), .reset(d_ff_3_qn), .loadval(d_ff_5_q), .clk1(clk2), .clk2(clk1),
    .cout(vcounter_bit_5_cout), .outval(vcounter_bit_1_outval[4]));
  vcounter_bit vcounter_bit_6 (
    .cin(vcounter_bit_5_cout), .reset(d_ff_3_qn), .loadval(1'b0), .clk1(clk2), .clk2(clk1),
    .cout(vcounter_bit_6_cout), .outval(vcounter_bit_1_outval[5]));
  vcounter_bit vcounter_bit_7 (
    .cin(vcounter_bit_6_cout), .reset(d_ff_3_qn), .loadval(d_ff_5_q), .clk1(clk2), .clk2(clk1),
    .cout(vcounter_bit_7_cout), .outval(vcounter_bit_1_outval[6]));
  vcounter_bit vcounter_bit_8 (
    .cin(vcounter_bit_7_cout), .reset(d_ff_3_qn), .loadval(d_ff_5_q), .clk1(clk2), .clk2(clk1),
    .cout(vcounter_bit_8_cout), .outval(vcounter_bit_1_outval[7]));
  vcounter_bit vcounter_bit_9 (
    .cin(vcounter_bit_8_cout), .reset(d_ff_3_qn), .loadval(1'b1), .clk1(clk2), .clk2(clk1),
    .outval(vcounter_bit_1_outval[8]));  // open: cout
  hpla hpla_1 (.hc(vcounter_bit_1_outval));  // open: out_2, out_3, out_4, out_5, out_6, out_7, out_8, out_9, out_10, out_11, out_12, out_13, out_14, out_15, out_16, out_17, out_18, out_19, out_20, out_21, out_22, out_23, out_24, out_25, out_26, out_27, out_28, out_29, out_30, out_31, out_32, out_33, out_34, out_35, out_36, out_37, out_38, out_39, out_40, out_41, out_42, out_43, out_44, out_45, out_46, out_47, out_48, out_49, out_50, out_51, out_52, out_53, out_54, out_55, out_56, out_57, out_58
endmodule
module hpla (
  input  [8:0] hc,
  output out_2,
  output out_3,
  output out_4,
  output out_5,
  output out_6,
  output out_7,
  output out_8,
  output out_9,
  output out_10,
  output out_11,
  output out_12,
  output out_13,
  output out_14,
  output out_15,
  output out_16,
  output out_17,
  output out_18,
  output out_19,
  output out_20,
  output out_21,
  output out_22,
  output out_23,
  output out_24,
  output out_25,
  output out_26,
  output out_27,
  output out_28,
  output out_29,
  output out_30,
  output out_31,
  output out_32,
  output out_33,
  output out_34,
  output out_35,
  output out_36,
  output out_37,
  output out_38,
  output out_39,
  output out_40,
  output out_41,
  output out_42,
  output out_43,
  output out_44,
  output out_45,
  output out_46,
  output out_47,
  output out_48,
  output out_49,
  output out_50,
  output out_51,
  output out_52,
  output out_53,
  output out_54,
  output out_55,
  output out_56,
  output out_57,
  output out_58
);

  wire not_1_out, not_2_out, not_3_out, not_4_out, not_5_out, not_6_out, not_7_out, not_8_out, not_9_out,
       undriven;

  Pull_Resistor #(.pull(1)) pull_resistor_1 (.node(out_2));
  Pull_Resistor #(.pull(1)) pull_resistor_2 (.node(out_3));
  Pull_Resistor #(.pull(1)) pull_resistor_3 (.node(out_4));
  Pull_Resistor #(.pull(1)) pull_resistor_4 (.node(out_5));
  Pull_Resistor #(.pull(1)) pull_resistor_5 (.node(out_6));
  Pull_Resistor #(.pull(1)) pull_resistor_6 (.node(out_7));
  Pull_Resistor #(.pull(1)) pull_resistor_7 (.node(out_8));
  Pull_Resistor #(.pull(1)) pull_resistor_8 (.node(out_9));
  Pull_Resistor #(.pull(1)) pull_resistor_9 (.node(out_10));
  Pull_Resistor #(.pull(1)) pull_resistor_10 (.node(out_11));
  Pull_Resistor #(.pull(1)) pull_resistor_11 (.node(out_12));
  Pull_Resistor #(.pull(1)) pull_resistor_12 (.node(out_13));
  Pull_Resistor #(.pull(1)) pull_resistor_13 (.node(out_14));
  Pull_Resistor #(.pull(1)) pull_resistor_14 (.node(out_15));
  Pull_Resistor #(.pull(1)) pull_resistor_15 (.node(out_16));
  Pull_Resistor #(.pull(1)) pull_resistor_16 (.node(out_17));
  Pull_Resistor #(.pull(1)) pull_resistor_17 (.node(out_18));
  Pull_Resistor #(.pull(1)) pull_resistor_18 (.node(out_19));
  Pull_Resistor #(.pull(1)) pull_resistor_19 (.node(out_20));
  Pull_Resistor #(.pull(1)) pull_resistor_20 (.node(out_21));
  Pull_Resistor #(.pull(1)) pull_resistor_21 (.node(out_22));
  Pull_Resistor #(.pull(1)) pull_resistor_22 (.node(out_23));
  Pull_Resistor #(.pull(1)) pull_resistor_23 (.node(out_24));
  Pull_Resistor #(.pull(1)) pull_resistor_24 (.node(out_25));
  Pull_Resistor #(.pull(1)) pull_resistor_25 (.node(out_26));
  Pull_Resistor #(.pull(1)) pull_resistor_26 (.node(out_27));
  Pull_Resistor #(.pull(1)) pull_resistor_27 (.node(out_28));
  Pull_Resistor #(.pull(1)) pull_resistor_28 (.node(out_29));
  Pull_Resistor #(.pull(1)) pull_resistor_29 (.node(out_30));
  Pull_Resistor #(.pull(1)) pull_resistor_30 (.node(out_31));
  Pull_Resistor #(.pull(1)) pull_resistor_31 (.node(out_32));
  Pull_Resistor #(.pull(1)) pull_resistor_32 (.node(out_33));
  Pull_Resistor #(.pull(1)) pull_resistor_33 (.node(out_34));
  Pull_Resistor #(.pull(1)) pull_resistor_34 (.node(out_35));
  Pull_Resistor #(.pull(1)) pull_resistor_35 (.node(out_36));
  Pull_Resistor #(.pull(1)) pull_resistor_36 (.node(out_37));
  Pull_Resistor #(.pull(1)) pull_resistor_37 (.node(out_38));
  Pull_Resistor #(.pull(1)) pull_resistor_38 (.node(out_39));
  Pull_Resistor #(.pull(1)) pull_resistor_39 (.node(out_40));
  Pull_Resistor #(.pull(1)) pull_resistor_40 (.node(out_41));
  Pull_Resistor #(.pull(1)) pull_resistor_41 (.node(out_42));
  Pull_Resistor #(.pull(1)) pull_resistor_42 (.node(out_43));
  Pull_Resistor #(.pull(1)) pull_resistor_43 (.node(out_44));
  Pull_Resistor #(.pull(1)) pull_resistor_44 (.node(out_45));
  Pull_Resistor #(.pull(1)) pull_resistor_45 (.node(out_46));
  Pull_Resistor #(.pull(1)) pull_resistor_46 (.node(out_47));
  Pull_Resistor #(.pull(1)) pull_resistor_47 (.node(out_48));
  Pull_Resistor #(.pull(1)) pull_resistor_48 (.node(out_49));
  Pull_Resistor #(.pull(1)) pull_resistor_49 (.node(out_50));
  Pull_Resistor #(.pull(1)) pull_resistor_50 (.node(out_51));
  Pull_Resistor #(.pull(1)) pull_resistor_51 (.node(out_52));
  Pull_Resistor #(.pull(1)) pull_resistor_52 (.node(out_53));
  Pull_Resistor #(.pull(1)) pull_resistor_53 (.node(out_54));
  Pull_Resistor #(.pull(1)) pull_resistor_54 (.node(out_55));
  Pull_Resistor #(.pull(1)) pull_resistor_55 (.node(out_56));
  Pull_Resistor #(.pull(1)) pull_resistor_56 (.node(out_57));
  Pull_Resistor #(.pull(1)) pull_resistor_57 (.node(out_58));
  Transistor #(.\type ("n")) transistor_1 (.in(1'b0), .out(out_2), .gate(not_1_out));
  Transistor #(.\type ("n")) transistor_2 (.in(1'b0), .out(out_6), .gate(not_1_out));
  Transistor #(.\type ("n")) transistor_3 (.in(1'b0), .out(out_7), .gate(not_1_out));
  Transistor #(.\type ("n")) transistor_4 (.in(1'b0), .out(out_8), .gate(not_1_out));
  Transistor #(.\type ("n")) transistor_5 (.in(1'b0), .out(out_9), .gate(not_1_out));
  Transistor #(.\type ("n")) transistor_6 (.in(1'b0), .out(out_10), .gate(not_1_out));
  Transistor #(.\type ("n")) transistor_7 (.in(1'b0), .out(out_11), .gate(not_1_out));
  Transistor #(.\type ("n")) transistor_8 (.in(1'b0), .out(out_12), .gate(not_1_out));
  Transistor #(.\type ("n")) transistor_9 (.in(undriven), .out(out_13), .gate(not_1_out));
  Transistor #(.\type ("n")) transistor_10 (.in(1'b0), .out(out_16), .gate(not_1_out));
  Transistor #(.\type ("n")) transistor_11 (.in(1'b0), .out(out_18), .gate(not_1_out));
  Transistor #(.\type ("n")) transistor_12 (.in(1'b0), .out(out_22), .gate(not_1_out));
  Transistor #(.\type ("n")) transistor_13 (.in(1'b0), .out(out_23), .gate(not_1_out));
  Transistor #(.\type ("n")) transistor_14 (.in(1'b0), .out(out_24), .gate(not_1_out));
  Transistor #(.\type ("n")) transistor_15 (.in(1'b0), .out(out_25), .gate(not_1_out));
  Transistor #(.\type ("n")) transistor_16 (.in(1'b0), .out(out_26), .gate(not_1_out));
  Transistor #(.\type ("n")) transistor_17 (.in(1'b0), .out(out_27), .gate(not_1_out));
  Transistor #(.\type ("n")) transistor_18 (.in(1'b0), .out(out_28), .gate(not_1_out));
  Transistor #(.\type ("n")) transistor_19 (.in(1'b0), .out(out_29), .gate(not_1_out));
  Transistor #(.\type ("n")) transistor_20 (.in(1'b0), .out(out_30), .gate(not_1_out));
  Transistor #(.\type ("n")) transistor_21 (.in(1'b0), .out(out_31), .gate(not_1_out));
  Transistor #(.\type ("n")) transistor_22 (.in(1'b0), .out(out_32), .gate(not_1_out));
  Transistor #(.\type ("n")) transistor_23 (.in(1'b0), .out(out_33), .gate(not_1_out));
  Transistor #(.\type ("n")) transistor_24 (.in(1'b0), .out(out_34), .gate(not_1_out));
  Transistor #(.\type ("n")) transistor_25 (.in(1'b0), .out(out_35), .gate(not_1_out));
  Transistor #(.\type ("n")) transistor_26 (.in(1'b0), .out(out_37), .gate(not_1_out));
  Transistor #(.\type ("n")) transistor_27 (.in(1'b0), .out(out_40), .gate(not_1_out));
  Transistor #(.\type ("n")) transistor_28 (.in(1'b0), .out(out_41), .gate(not_1_out));
  Transistor #(.\type ("n")) transistor_29 (.in(1'b0), .out(out_43), .gate(not_1_out));
  Transistor #(.\type ("n")) transistor_30 (.in(1'b0), .out(out_44), .gate(not_1_out));
  Transistor #(.\type ("n")) transistor_31 (.in(1'b0), .out(out_45), .gate(not_1_out));
  Transistor #(.\type ("n")) transistor_32 (.in(1'b0), .out(out_46), .gate(not_1_out));
  Transistor #(.\type ("n")) transistor_33 (.in(1'b0), .out(out_47), .gate(not_1_out));
  Transistor #(.\type ("n")) transistor_34 (.in(1'b0), .out(out_49), .gate(not_1_out));
  Transistor #(.\type ("n")) transistor_35 (.in(1'b0), .out(out_50), .gate(not_1_out));
  Transistor #(.\type ("n")) transistor_36 (.in(1'b0), .out(out_51), .gate(not_1_out));
  Transistor #(.\type ("n")) transistor_37 (.in(1'b0), .out(out_54), .gate(not_1_out));
  Transistor #(.\type ("n")) transistor_38 (.in(1'b0), .out(out_57), .gate(not_1_out));
  Transistor #(.\type ("n")) transistor_39 (.in(1'b0), .out(out_58), .gate(not_1_out));
  not not_1 (not_1_out, hc[8]);
  Transistor #(.\type ("n")) transistor_40 (.in(1'b0), .out(out_3), .gate(hc[8]));
  Transistor #(.\type ("n")) transistor_41 (.in(1'b0), .out(out_4), .gate(hc[8]));
  Transistor #(.\type ("n")) transistor_42 (.in(1'b0), .out(out_14), .gate(hc[8]));
  Transistor #(.\type ("n")) transistor_43 (.in(1'b0), .out(out_17), .gate(hc[8]));
  Transistor #(.\type ("n")) transistor_44 (.in(1'b0), .out(out_19), .gate(hc[8]));
  Transistor #(.\type ("n")) transistor_45 (.in(1'b0), .out(out_20), .gate(hc[8]));
  Transistor #(.\type ("n")) transistor_46 (.in(1'b0), .out(out_36), .gate(hc[8]));
  Transistor #(.\type ("n")) transistor_47 (.in(1'b0), .out(out_48), .gate(hc[8]));
  Transistor #(.\type ("n")) transistor_48 (.in(1'b0), .out(out_52), .gate(hc[8]));
  Transistor #(.\type ("n")) transistor_49 (.in(1'b0), .out(out_53), .gate(hc[8]));
  Transistor #(.\type ("n")) transistor_50 (.in(1'b0), .out(out_55), .gate(hc[8]));
  Transistor #(.\type ("n")) transistor_51 (.in(1'b0), .out(out_2), .gate(not_2_out));
  Transistor #(.\type ("n")) transistor_52 (.in(1'b0), .out(out_6), .gate(not_2_out));
  Transistor #(.\type ("n")) transistor_53 (.in(1'b0), .out(out_11), .gate(not_2_out));
  Transistor #(.\type ("n")) transistor_54 (.in(1'b0), .out(out_12), .gate(not_2_out));
  Transistor #(.\type ("n")) transistor_55 (.in(1'b0), .out(out_13), .gate(not_2_out));
  Transistor #(.\type ("n")) transistor_56 (.in(1'b0), .out(out_22), .gate(not_2_out));
  Transistor #(.\type ("n")) transistor_57 (.in(1'b0), .out(out_23), .gate(not_2_out));
  Transistor #(.\type ("n")) transistor_58 (.in(1'b0), .out(out_24), .gate(not_2_out));
  Transistor #(.\type ("n")) transistor_59 (.in(1'b0), .out(out_25), .gate(not_2_out));
  Transistor #(.\type ("n")) transistor_60 (.in(1'b0), .out(out_26), .gate(not_2_out));
  Transistor #(.\type ("n")) transistor_61 (.in(1'b0), .out(out_27), .gate(not_2_out));
  Transistor #(.\type ("n")) transistor_62 (.in(1'b0), .out(out_28), .gate(not_2_out));
  Transistor #(.\type ("n")) transistor_63 (.in(1'b0), .out(out_37), .gate(not_2_out));
  Transistor #(.\type ("n")) transistor_64 (.in(1'b0), .out(out_40), .gate(not_2_out));
  Transistor #(.\type ("n")) transistor_65 (.in(1'b0), .out(out_44), .gate(not_2_out));
  Transistor #(.\type ("n")) transistor_66 (.in(1'b0), .out(out_45), .gate(not_2_out));
  Transistor #(.\type ("n")) transistor_67 (.in(1'b0), .out(out_46), .gate(not_2_out));
  not not_2 (not_2_out, hc[7]);
  Transistor #(.\type ("n")) transistor_68 (.in(1'b0), .out(out_7), .gate(hc[7]));
  Transistor #(.\type ("n")) transistor_69 (.in(1'b0), .out(out_8), .gate(hc[7]));
  Transistor #(.\type ("n")) transistor_70 (.in(1'b0), .out(out_9), .gate(hc[7]));
  Transistor #(.\type ("n")) transistor_71 (.in(1'b0), .out(out_10), .gate(hc[7]));
  Transistor #(.\type ("n")) transistor_72 (.in(1'b0), .out(out_16), .gate(hc[7]));
  Transistor #(.\type ("n")) transistor_73 (.in(1'b0), .out(out_18), .gate(hc[7]));
  Transistor #(.\type ("n")) transistor_74 (.in(1'b0), .out(out_29), .gate(hc[7]));
  Transistor #(.\type ("n")) transistor_75 (.in(1'b0), .out(out_30), .gate(hc[7]));
  Transistor #(.\type ("n")) transistor_76 (.in(1'b0), .out(out_31), .gate(hc[7]));
  Transistor #(.\type ("n")) transistor_77 (.in(1'b0), .out(out_32), .gate(hc[7]));
  Transistor #(.\type ("n")) transistor_78 (.in(1'b0), .out(out_33), .gate(hc[7]));
  Transistor #(.\type ("n")) transistor_79 (.in(1'b0), .out(out_34), .gate(hc[7]));
  Transistor #(.\type ("n")) transistor_80 (.in(1'b0), .out(out_35), .gate(hc[7]));
  Transistor #(.\type ("n")) transistor_81 (.in(1'b0), .out(out_36), .gate(hc[7]));
  Transistor #(.\type ("n")) transistor_82 (.in(1'b0), .out(out_41), .gate(hc[7]));
  Transistor #(.\type ("n")) transistor_83 (.in(1'b0), .out(out_47), .gate(hc[7]));
  Transistor #(.\type ("n")) transistor_84 (.in(1'b0), .out(out_48), .gate(hc[7]));
  Transistor #(.\type ("n")) transistor_85 (.in(1'b0), .out(out_49), .gate(hc[7]));
  Transistor #(.\type ("n")) transistor_86 (.in(1'b0), .out(out_50), .gate(hc[7]));
  Transistor #(.\type ("n")) transistor_87 (.in(1'b0), .out(out_51), .gate(hc[7]));
  Transistor #(.\type ("n")) transistor_88 (.in(1'b0), .out(out_52), .gate(hc[7]));
  Transistor #(.\type ("n")) transistor_89 (.in(1'b0), .out(out_53), .gate(hc[7]));
  Transistor #(.\type ("n")) transistor_90 (.in(1'b0), .out(out_54), .gate(hc[7]));
  Transistor #(.\type ("n")) transistor_91 (.in(1'b0), .out(out_55), .gate(hc[7]));
  Transistor #(.\type ("n")) transistor_92 (.in(1'b0), .out(out_57), .gate(hc[7]));
  Transistor #(.\type ("n")) transistor_93 (.in(1'b0), .out(out_58), .gate(hc[7]));
  Transistor #(.\type ("n")) transistor_94 (.in(1'b0), .out(out_2), .gate(not_3_out));
  Transistor #(.\type ("n")) transistor_95 (.in(1'b0), .out(out_6), .gate(not_3_out));
  Transistor #(.\type ("n")) transistor_96 (.in(1'b0), .out(out_11), .gate(not_3_out));
  Transistor #(.\type ("n")) transistor_97 (.in(1'b0), .out(out_12), .gate(not_3_out));
  Transistor #(.\type ("n")) transistor_98 (.in(1'b0), .out(out_13), .gate(not_3_out));
  Transistor #(.\type ("n")) transistor_99 (.in(1'b0), .out(out_22), .gate(not_3_out));
  Transistor #(.\type ("n")) transistor_100 (.in(1'b0), .out(out_23), .gate(not_3_out));
  Transistor #(.\type ("n")) transistor_101 (.in(1'b0), .out(out_24), .gate(not_3_out));
  Transistor #(.\type ("n")) transistor_102 (.in(1'b0), .out(out_25), .gate(not_3_out));
  Transistor #(.\type ("n")) transistor_103 (.in(1'b0), .out(out_26), .gate(not_3_out));
  Transistor #(.\type ("n")) transistor_104 (.in(1'b0), .out(out_27), .gate(not_3_out));
  Transistor #(.\type ("n")) transistor_105 (.in(1'b0), .out(out_28), .gate(not_3_out));
  Transistor #(.\type ("n")) transistor_106 (.in(1'b0), .out(out_37), .gate(not_3_out));
  Transistor #(.\type ("n")) transistor_107 (.in(1'b0), .out(out_40), .gate(not_3_out));
  Transistor #(.\type ("n")) transistor_108 (.in(1'b0), .out(out_44), .gate(not_3_out));
  Transistor #(.\type ("n")) transistor_109 (.in(1'b0), .out(out_45), .gate(not_3_out));
  Transistor #(.\type ("n")) transistor_110 (.in(1'b0), .out(out_46), .gate(not_3_out));
  Transistor #(.\type ("n")) transistor_111 (.in(1'b0), .out(out_51), .gate(not_3_out));
  Transistor #(.\type ("n")) transistor_112 (.in(1'b0), .out(out_54), .gate(not_3_out));
  Transistor #(.\type ("n")) transistor_113 (.in(1'b0), .out(out_57), .gate(not_3_out));
  not not_3 (not_3_out, hc[6]);
  Transistor #(.\type ("n")) transistor_114 (.in(1'b0), .out(out_7), .gate(hc[6]));
  Transistor #(.\type ("n")) transistor_115 (.in(1'b0), .out(out_8), .gate(hc[6]));
  Transistor #(.\type ("n")) transistor_116 (.in(1'b0), .out(out_9), .gate(hc[6]));
  Transistor #(.\type ("n")) transistor_117 (.in(1'b0), .out(out_10), .gate(hc[6]));
  Transistor #(.\type ("n")) transistor_118 (.in(1'b0), .out(out_16), .gate(hc[6]));
  Transistor #(.\type ("n")) transistor_119 (.in(1'b0), .out(out_18), .gate(hc[6]));
  Transistor #(.\type ("n")) transistor_120 (.in(1'b0), .out(out_29), .gate(hc[6]));
  Transistor #(.\type ("n")) transistor_121 (.in(1'b0), .out(out_30), .gate(hc[6]));
  Transistor #(.\type ("n")) transistor_122 (.in(1'b0), .out(out_31), .gate(hc[6]));
  Transistor #(.\type ("n")) transistor_123 (.in(1'b0), .out(out_32), .gate(hc[6]));
  Transistor #(.\type ("n")) transistor_124 (.in(1'b0), .out(out_33), .gate(hc[6]));
  Transistor #(.\type ("n")) transistor_125 (.in(1'b0), .out(out_34), .gate(hc[6]));
  Transistor #(.\type ("n")) transistor_126 (.in(1'b0), .out(out_35), .gate(hc[6]));
  Transistor #(.\type ("n")) transistor_127 (.in(1'b0), .out(out_36), .gate(hc[6]));
  Transistor #(.\type ("n")) transistor_128 (.in(1'b0), .out(out_41), .gate(hc[6]));
  Transistor #(.\type ("n")) transistor_129 (.in(1'b0), .out(out_47), .gate(hc[6]));
  Transistor #(.\type ("n")) transistor_130 (.in(1'b0), .out(out_48), .gate(hc[6]));
  Transistor #(.\type ("n")) transistor_131 (.in(1'b0), .out(out_49), .gate(hc[6]));
  Transistor #(.\type ("n")) transistor_132 (.in(1'b0), .out(out_50), .gate(hc[6]));
  Transistor #(.\type ("n")) transistor_133 (.in(1'b0), .out(out_52), .gate(hc[6]));
  Transistor #(.\type ("n")) transistor_134 (.in(1'b0), .out(out_53), .gate(hc[6]));
  Transistor #(.\type ("n")) transistor_135 (.in(1'b0), .out(out_55), .gate(hc[6]));
  Transistor #(.\type ("n")) transistor_136 (.in(1'b0), .out(out_58), .gate(hc[6]));
  Transistor #(.\type ("n")) transistor_137 (.in(1'b0), .out(out_2), .gate(not_4_out));
  Transistor #(.\type ("n")) transistor_138 (.in(1'b0), .out(out_6), .gate(not_4_out));
  Transistor #(.\type ("n")) transistor_139 (.in(1'b0), .out(out_13), .gate(not_4_out));
  Transistor #(.\type ("n")) transistor_140 (.in(1'b0), .out(out_23), .gate(not_4_out));
  Transistor #(.\type ("n")) transistor_141 (.in(1'b0), .out(out_24), .gate(not_4_out));
  Transistor #(.\type ("n")) transistor_142 (.in(1'b0), .out(out_25), .gate(not_4_out));
  Transistor #(.\type ("n")) transistor_143 (.in(1'b0), .out(out_26), .gate(not_4_out));
  Transistor #(.\type ("n")) transistor_144 (.in(1'b0), .out(out_29), .gate(not_4_out));
  Transistor #(.\type ("n")) transistor_145 (.in(1'b0), .out(out_37), .gate(not_4_out));
  Transistor #(.\type ("n")) transistor_146 (.in(1'b0), .out(out_44), .gate(not_4_out));
  Transistor #(.\type ("n")) transistor_147 (.in(1'b0), .out(out_45), .gate(not_4_out));
  Transistor #(.\type ("n")) transistor_148 (.in(1'b0), .out(out_46), .gate(not_4_out));
  Transistor #(.\type ("n")) transistor_149 (.in(1'b0), .out(out_47), .gate(not_4_out));
  Transistor #(.\type ("n")) transistor_150 (.in(1'b0), .out(out_58), .gate(not_4_out));
  not not_4 (not_4_out, hc[5]);
  Transistor #(.\type ("n")) transistor_151 (.in(1'b0), .out(out_7), .gate(hc[5]));
  Transistor #(.\type ("n")) transistor_152 (.in(1'b0), .out(out_8), .gate(hc[5]));
  Transistor #(.\type ("n")) transistor_153 (.in(1'b0), .out(out_9), .gate(hc[5]));
  Transistor #(.\type ("n")) transistor_154 (.in(1'b0), .out(out_10), .gate(hc[5]));
  Transistor #(.\type ("n")) transistor_155 (.in(1'b0), .out(out_11), .gate(hc[5]));
  Transistor #(.\type ("n")) transistor_156 (.in(1'b0), .out(out_12), .gate(hc[5]));
  Transistor #(.\type ("n")) transistor_157 (.in(1'b0), .out(out_16), .gate(hc[5]));
  Transistor #(.\type ("n")) transistor_158 (.in(1'b0), .out(out_18), .gate(hc[5]));
  Transistor #(.\type ("n")) transistor_159 (.in(1'b0), .out(out_22), .gate(hc[5]));
  Transistor #(.\type ("n")) transistor_160 (.in(1'b0), .out(out_27), .gate(hc[5]));
  Transistor #(.\type ("n")) transistor_161 (.in(1'b0), .out(out_28), .gate(hc[5]));
  Transistor #(.\type ("n")) transistor_162 (.in(1'b0), .out(out_30), .gate(hc[5]));
  Transistor #(.\type ("n")) transistor_163 (.in(1'b0), .out(out_31), .gate(hc[5]));
  Transistor #(.\type ("n")) transistor_164 (.in(1'b0), .out(out_32), .gate(hc[5]));
  Transistor #(.\type ("n")) transistor_165 (.in(1'b0), .out(out_33), .gate(hc[5]));
  Transistor #(.\type ("n")) transistor_166 (.in(1'b0), .out(out_34), .gate(hc[5]));
  Transistor #(.\type ("n")) transistor_167 (.in(1'b0), .out(out_35), .gate(hc[5]));
  Transistor #(.\type ("n")) transistor_168 (.in(1'b0), .out(out_36), .gate(hc[5]));
  Transistor #(.\type ("n")) transistor_169 (.in(1'b0), .out(out_40), .gate(hc[5]));
  Transistor #(.\type ("n")) transistor_170 (.in(1'b0), .out(out_41), .gate(hc[5]));
  Transistor #(.\type ("n")) transistor_171 (.in(1'b0), .out(out_48), .gate(hc[5]));
  Transistor #(.\type ("n")) transistor_172 (.in(1'b0), .out(out_49), .gate(hc[5]));
  Transistor #(.\type ("n")) transistor_173 (.in(1'b0), .out(out_50), .gate(hc[5]));
  Transistor #(.\type ("n")) transistor_174 (.in(1'b0), .out(out_51), .gate(hc[5]));
  Transistor #(.\type ("n")) transistor_175 (.in(1'b0), .out(out_52), .gate(hc[5]));
  Transistor #(.\type ("n")) transistor_176 (.in(1'b0), .out(out_53), .gate(hc[5]));
  Transistor #(.\type ("n")) transistor_177 (.in(1'b0), .out(out_54), .gate(hc[5]));
  Transistor #(.\type ("n")) transistor_178 (.in(1'b0), .out(out_55), .gate(hc[5]));
  Transistor #(.\type ("n")) transistor_179 (.in(1'b0), .out(out_57), .gate(hc[5]));
  Transistor #(.\type ("n")) transistor_180 (.in(1'b0), .out(out_3), .gate(not_5_out));
  Transistor #(.\type ("n")) transistor_181 (.in(1'b0), .out(out_6), .gate(not_5_out));
  Transistor #(.\type ("n")) transistor_182 (.in(1'b0), .out(out_9), .gate(not_5_out));
  Transistor #(.\type ("n")) transistor_183 (.in(1'b0), .out(out_10), .gate(not_5_out));
  Transistor #(.\type ("n")) transistor_184 (.in(1'b0), .out(out_11), .gate(not_5_out));
  Transistor #(.\type ("n")) transistor_185 (.in(1'b0), .out(out_12), .gate(not_5_out));
  Transistor #(.\type ("n")) transistor_186 (.in(1'b0), .out(out_18), .gate(not_5_out));
  Transistor #(.\type ("n")) transistor_187 (.in(1'b0), .out(out_22), .gate(not_5_out));
  Transistor #(.\type ("n")) transistor_188 (.in(1'b0), .out(out_27), .gate(not_5_out));
  Transistor #(.\type ("n")) transistor_189 (.in(1'b0), .out(out_28), .gate(not_5_out));
  Transistor #(.\type ("n")) transistor_190 (.in(1'b0), .out(out_30), .gate(not_5_out));
  Transistor #(.\type ("n")) transistor_191 (.in(1'b0), .out(out_31), .gate(not_5_out));
  Transistor #(.\type ("n")) transistor_192 (.in(1'b0), .out(out_32), .gate(not_5_out));
  Transistor #(.\type ("n")) transistor_193 (.in(1'b0), .out(out_40), .gate(not_5_out));
  Transistor #(.\type ("n")) transistor_194 (.in(1'b0), .out(out_41), .gate(not_5_out));
  Transistor #(.\type ("n")) transistor_195 (.in(1'b0), .out(out_43), .gate(not_5_out));
  Transistor #(.\type ("n")) transistor_196 (.in(1'b0), .out(out_44), .gate(not_5_out));
  Transistor #(.\type ("n")) transistor_197 (.in(1'b0), .out(out_49), .gate(not_5_out));
  Transistor #(.\type ("n")) transistor_198 (.in(1'b0), .out(out_51), .gate(not_5_out));
  Transistor #(.\type ("n")) transistor_199 (.in(1'b0), .out(out_52), .gate(not_5_out));
  Transistor #(.\type ("n")) transistor_200 (.in(1'b0), .out(out_57), .gate(not_5_out));
  not not_5 (not_5_out, hc[4]);
  Transistor #(.\type ("n")) transistor_201 (.in(1'b0), .out(out_2), .gate(hc[4]));
  Transistor #(.\type ("n")) transistor_202 (.in(1'b0), .out(out_4), .gate(hc[4]));
  Transistor #(.\type ("n")) transistor_203 (.in(1'b0), .out(out_7), .gate(hc[4]));
  Transistor #(.\type ("n")) transistor_204 (.in(1'b0), .out(out_8), .gate(hc[4]));
  Transistor #(.\type ("n")) transistor_205 (.in(1'b0), .out(out_13), .gate(hc[4]));
  Transistor #(.\type ("n")) transistor_206 (.in(1'b0), .out(out_16), .gate(hc[4]));
  Transistor #(.\type ("n")) transistor_207 (.in(1'b0), .out(out_23), .gate(hc[4]));
  Transistor #(.\type ("n")) transistor_208 (.in(1'b0), .out(out_24), .gate(hc[4]));
  Transistor #(.\type ("n")) transistor_209 (.in(1'b0), .out(out_25), .gate(hc[4]));
  Transistor #(.\type ("n")) transistor_210 (.in(1'b0), .out(out_26), .gate(hc[4]));
  Transistor #(.\type ("n")) transistor_211 (.in(1'b0), .out(out_29), .gate(hc[4]));
  Transistor #(.\type ("n")) transistor_212 (.in(1'b0), .out(out_33), .gate(hc[4]));
  Transistor #(.\type ("n")) transistor_213 (.in(1'b0), .out(out_34), .gate(hc[4]));
  Transistor #(.\type ("n")) transistor_214 (.in(1'b0), .out(out_35), .gate(hc[4]));
  Transistor #(.\type ("n")) transistor_215 (.in(1'b0), .out(out_36), .gate(hc[4]));
  Transistor #(.\type ("n")) transistor_216 (.in(1'b0), .out(out_37), .gate(hc[4]));
  Transistor #(.\type ("n")) transistor_217 (.in(1'b0), .out(out_45), .gate(hc[4]));
  Transistor #(.\type ("n")) transistor_218 (.in(1'b0), .out(out_46), .gate(hc[4]));
  Transistor #(.\type ("n")) transistor_219 (.in(1'b0), .out(out_47), .gate(hc[4]));
  Transistor #(.\type ("n")) transistor_220 (.in(1'b0), .out(out_48), .gate(hc[4]));
  Transistor #(.\type ("n")) transistor_221 (.in(1'b0), .out(out_50), .gate(hc[4]));
  Transistor #(.\type ("n")) transistor_222 (.in(1'b0), .out(out_53), .gate(hc[4]));
  Transistor #(.\type ("n")) transistor_223 (.in(1'b0), .out(out_54), .gate(hc[4]));
  Transistor #(.\type ("n")) transistor_224 (.in(1'b0), .out(out_55), .gate(hc[4]));
  Transistor #(.\type ("n")) transistor_225 (.in(1'b0), .out(out_58), .gate(hc[4]));
  Transistor #(.\type ("n")) transistor_226 (.in(1'b0), .out(out_2), .gate(not_6_out));
  Transistor #(.\type ("n")) transistor_227 (.in(1'b0), .out(out_4), .gate(not_6_out));
  Transistor #(.\type ("n")) transistor_228 (.in(1'b0), .out(out_8), .gate(not_6_out));
  Transistor #(.\type ("n")) transistor_229 (.in(1'b0), .out(out_10), .gate(not_6_out));
  Transistor #(.\type ("n")) transistor_230 (.in(1'b0), .out(out_12), .gate(not_6_out));
  Transistor #(.\type ("n")) transistor_231 (.in(1'b0), .out(out_16), .gate(not_6_out));
  Transistor #(.\type ("n")) transistor_232 (.in(1'b0), .out(out_18), .gate(not_6_out));
  Transistor #(.\type ("n")) transistor_233 (.in(1'b0), .out(out_22), .gate(not_6_out));
  Transistor #(.\type ("n")) transistor_234 (.in(1'b0), .out(out_27), .gate(not_6_out));
  Transistor #(.\type ("n")) transistor_235 (.in(1'b0), .out(out_28), .gate(not_6_out));
  Transistor #(.\type ("n")) transistor_236 (.in(1'b0), .out(out_30), .gate(not_6_out));
  Transistor #(.\type ("n")) transistor_237 (.in(1'b0), .out(out_31), .gate(not_6_out));
  Transistor #(.\type ("n")) transistor_238 (.in(1'b0), .out(out_33), .gate(not_6_out));
  Transistor #(.\type ("n")) transistor_239 (.in(1'b0), .out(out_34), .gate(not_6_out));
  Transistor #(.\type ("n")) transistor_240 (.in(1'b0), .out(out_35), .gate(not_6_out));
  Transistor #(.\type ("n")) transistor_241 (.in(1'b0), .out(out_36), .gate(not_6_out));
  Transistor #(.\type ("n")) transistor_242 (.in(1'b0), .out(out_37), .gate(not_6_out));
  Transistor #(.\type ("n")) transistor_243 (.in(1'b0), .out(out_44), .gate(not_6_out));
  Transistor #(.\type ("n")) transistor_244 (.in(1'b0), .out(out_45), .gate(not_6_out));
  Transistor #(.\type ("n")) transistor_245 (.in(1'b0), .out(out_46), .gate(not_6_out));
  Transistor #(.\type ("n")) transistor_246 (.in(1'b0), .out(out_49), .gate(not_6_out));
  Transistor #(.\type ("n")) transistor_247 (.in(1'b0), .out(out_50), .gate(not_6_out));
  Transistor #(.\type ("n")) transistor_248 (.in(1'b0), .out(out_51), .gate(not_6_out));
  Transistor #(.\type ("n")) transistor_249 (.in(1'b0), .out(out_53), .gate(not_6_out));
  Transistor #(.\type ("n")) transistor_250 (.in(1'b0), .out(out_57), .gate(not_6_out));
  not not_6 (not_6_out, hc[3]);
  Transistor #(.\type ("n")) transistor_251 (.in(1'b0), .out(out_7), .gate(hc[3]));
  Transistor #(.\type ("n")) transistor_252 (.in(1'b0), .out(out_9), .gate(hc[3]));
  Transistor #(.\type ("n")) transistor_253 (.in(1'b0), .out(out_11), .gate(hc[3]));
  Transistor #(.\type ("n")) transistor_254 (.in(1'b0), .out(out_13), .gate(hc[3]));
  Transistor #(.\type ("n")) transistor_255 (.in(1'b0), .out(out_23), .gate(hc[3]));
  Transistor #(.\type ("n")) transistor_256 (.in(1'b0), .out(out_24), .gate(hc[3]));
  Transistor #(.\type ("n")) transistor_257 (.in(1'b0), .out(out_25), .gate(hc[3]));
  Transistor #(.\type ("n")) transistor_258 (.in(1'b0), .out(out_26), .gate(hc[3]));
  Transistor #(.\type ("n")) transistor_259 (.in(1'b0), .out(out_29), .gate(hc[3]));
  Transistor #(.\type ("n")) transistor_260 (.in(1'b0), .out(out_32), .gate(hc[3]));
  Transistor #(.\type ("n")) transistor_261 (.in(1'b0), .out(out_40), .gate(hc[3]));
  Transistor #(.\type ("n")) transistor_262 (.in(1'b0), .out(out_41), .gate(hc[3]));
  Transistor #(.\type ("n")) transistor_263 (.in(1'b0), .out(out_47), .gate(hc[3]));
  Transistor #(.\type ("n")) transistor_264 (.in(1'b0), .out(out_48), .gate(hc[3]));
  Transistor #(.\type ("n")) transistor_265 (.in(1'b0), .out(out_52), .gate(hc[3]));
  Transistor #(.\type ("n")) transistor_266 (.in(1'b0), .out(out_54), .gate(hc[3]));
  Transistor #(.\type ("n")) transistor_267 (.in(1'b0), .out(out_55), .gate(hc[3]));
  Transistor #(.\type ("n")) transistor_268 (.in(1'b0), .out(out_58), .gate(hc[3]));
  Transistor #(.\type ("n")) transistor_269 (.in(1'b0), .out(out_7), .gate(not_7_out));
  Transistor #(.\type ("n")) transistor_270 (.in(1'b0), .out(out_10), .gate(not_7_out));
  Transistor #(.\type ("n")) transistor_271 (.in(1'b0), .out(out_11), .gate(not_7_out));
  Transistor #(.\type ("n")) transistor_272 (.in(1'b0), .out(out_12), .gate(not_7_out));
  Transistor #(.\type ("n")) transistor_273 (.in(1'b0), .out(out_16), .gate(not_7_out));
  Transistor #(.\type ("n")) transistor_274 (.in(1'b0), .out(out_19), .gate(not_7_out));
  Transistor #(.\type ("n")) transistor_275 (.in(1'b0), .out(out_20), .gate(not_7_out));
  Transistor #(.\type ("n")) transistor_276 (.in(1'b0), .out(out_21), .gate(not_7_out));
  Transistor #(.\type ("n")) transistor_277 (.in(1'b0), .out(out_23), .gate(not_7_out));
  Transistor #(.\type ("n")) transistor_278 (.in(1'b0), .out(out_24), .gate(not_7_out));
  Transistor #(.\type ("n")) transistor_279 (.in(1'b0), .out(out_25), .gate(not_7_out));
  Transistor #(.\type ("n")) transistor_280 (.in(1'b0), .out(out_32), .gate(not_7_out));
  Transistor #(.\type ("n")) transistor_281 (.in(1'b0), .out(out_33), .gate(not_7_out));
  Transistor #(.\type ("n")) transistor_282 (.in(1'b0), .out(out_34), .gate(not_7_out));
  Transistor #(.\type ("n")) transistor_283 (.in(1'b0), .out(out_38), .gate(not_7_out));
  Transistor #(.\type ("n")) transistor_284 (.in(1'b0), .out(out_40), .gate(not_7_out));
  Transistor #(.\type ("n")) transistor_285 (.in(1'b0), .out(out_41), .gate(not_7_out));
  Transistor #(.\type ("n")) transistor_286 (.in(1'b0), .out(out_47), .gate(not_7_out));
  Transistor #(.\type ("n")) transistor_287 (.in(1'b0), .out(out_49), .gate(not_7_out));
  Transistor #(.\type ("n")) transistor_288 (.in(1'b0), .out(out_54), .gate(not_7_out));
  Transistor #(.\type ("n")) transistor_289 (.in(1'b0), .out(out_55), .gate(not_7_out));
  Transistor #(.\type ("n")) transistor_290 (.in(1'b0), .out(out_56), .gate(not_7_out));
  Transistor #(.\type ("n")) transistor_291 (.in(1'b0), .out(out_57), .gate(not_7_out));
  Transistor #(.\type ("n")) transistor_292 (.in(1'b0), .out(out_58), .gate(not_7_out));
  not not_7 (not_7_out, hc[2]);
  Transistor #(.\type ("n")) transistor_293 (.in(1'b0), .out(out_2), .gate(hc[2]));
  Transistor #(.\type ("n")) transistor_294 (.in(1'b0), .out(out_3), .gate(hc[2]));
  Transistor #(.\type ("n")) transistor_295 (.in(1'b0), .out(out_4), .gate(hc[2]));
  Transistor #(.\type ("n")) transistor_296 (.in(1'b0), .out(out_8), .gate(hc[2]));
  Transistor #(.\type ("n")) transistor_297 (.in(1'b0), .out(out_13), .gate(hc[2]));
  Transistor #(.\type ("n")) transistor_298 (.in(1'b0), .out(out_15), .gate(hc[2]));
  Transistor #(.\type ("n")) transistor_299 (.in(1'b0), .out(out_17), .gate(hc[2]));
  Transistor #(.\type ("n")) transistor_300 (.in(1'b0), .out(out_18), .gate(hc[2]));
  Transistor #(.\type ("n")) transistor_301 (.in(1'b0), .out(out_22), .gate(hc[2]));
  Transistor #(.\type ("n")) transistor_302 (.in(1'b0), .out(out_26), .gate(hc[2]));
  Transistor #(.\type ("n")) transistor_303 (.in(1'b0), .out(out_27), .gate(hc[2]));
  Transistor #(.\type ("n")) transistor_304 (.in(1'b0), .out(out_28), .gate(hc[2]));
  Transistor #(.\type ("n")) transistor_305 (.in(1'b0), .out(out_29), .gate(hc[2]));
  Transistor #(.\type ("n")) transistor_306 (.in(1'b0), .out(out_30), .gate(hc[2]));
  Transistor #(.\type ("n")) transistor_307 (.in(1'b0), .out(out_31), .gate(hc[2]));
  Transistor #(.\type ("n")) transistor_308 (.in(1'b0), .out(out_35), .gate(hc[2]));
  Transistor #(.\type ("n")) transistor_309 (.in(1'b0), .out(out_36), .gate(hc[2]));
  Transistor #(.\type ("n")) transistor_310 (.in(1'b0), .out(out_37), .gate(hc[2]));
  Transistor #(.\type ("n")) transistor_311 (.in(1'b0), .out(out_39), .gate(hc[2]));
  Transistor #(.\type ("n")) transistor_312 (.in(1'b0), .out(out_42), .gate(hc[2]));
  Transistor #(.\type ("n")) transistor_313 (.in(1'b0), .out(out_44), .gate(hc[2]));
  Transistor #(.\type ("n")) transistor_314 (.in(1'b0), .out(out_45), .gate(hc[2]));
  Transistor #(.\type ("n")) transistor_315 (.in(1'b0), .out(out_46), .gate(hc[2]));
  Transistor #(.\type ("n")) transistor_316 (.in(1'b0), .out(out_48), .gate(hc[2]));
  Transistor #(.\type ("n")) transistor_317 (.in(1'b0), .out(out_50), .gate(hc[2]));
  Transistor #(.\type ("n")) transistor_318 (.in(1'b0), .out(out_51), .gate(hc[2]));
  Transistor #(.\type ("n")) transistor_319 (.in(1'b0), .out(out_52), .gate(hc[2]));
  Transistor #(.\type ("n")) transistor_320 (.in(1'b0), .out(out_53), .gate(hc[2]));
  Transistor #(.\type ("n")) transistor_321 (.in(1'b0), .out(out_3), .gate(not_8_out));
  Transistor #(.\type ("n")) transistor_322 (.in(1'b0), .out(out_4), .gate(not_8_out));
  Transistor #(.\type ("n")) transistor_323 (.in(1'b0), .out(out_20), .gate(not_8_out));
  Transistor #(.\type ("n")) transistor_324 (.in(1'b0), .out(out_24), .gate(not_8_out));
  Transistor #(.\type ("n")) transistor_325 (.in(1'b0), .out(out_27), .gate(not_8_out));
  Transistor #(.\type ("n")) transistor_326 (.in(1'b0), .out(out_30), .gate(not_8_out));
  Transistor #(.\type ("n")) transistor_327 (.in(1'b0), .out(out_33), .gate(not_8_out));
  Transistor #(.\type ("n")) transistor_328 (.in(1'b0), .out(out_38), .gate(not_8_out));
  Transistor #(.\type ("n")) transistor_329 (.in(1'b0), .out(out_40), .gate(not_8_out));
  Transistor #(.\type ("n")) transistor_330 (.in(1'b0), .out(out_41), .gate(not_8_out));
  Transistor #(.\type ("n")) transistor_331 (.in(1'b0), .out(out_42), .gate(not_8_out));
  Transistor #(.\type ("n")) transistor_332 (.in(1'b0), .out(out_45), .gate(not_8_out));
  Transistor #(.\type ("n")) transistor_333 (.in(1'b0), .out(out_50), .gate(not_8_out));
  Transistor #(.\type ("n")) transistor_334 (.in(1'b0), .out(out_52), .gate(not_8_out));
  Transistor #(.\type ("n")) transistor_335 (.in(1'b0), .out(out_53), .gate(not_8_out));
  Transistor #(.\type ("n")) transistor_336 (.in(1'b0), .out(out_55), .gate(not_8_out));
  Transistor #(.\type ("n")) transistor_337 (.in(1'b0), .out(out_57), .gate(not_8_out));
  Transistor #(.\type ("n")) transistor_338 (.in(1'b0), .out(out_58), .gate(not_8_out));
  not not_8 (not_8_out, hc[1]);
  Transistor #(.\type ("n")) transistor_339 (.in(1'b0), .out(out_14), .gate(hc[1]));
  Transistor #(.\type ("n")) transistor_340 (.in(1'b0), .out(out_15), .gate(hc[1]));
  Transistor #(.\type ("n")) transistor_341 (.in(1'b0), .out(out_17), .gate(hc[1]));
  Transistor #(.\type ("n")) transistor_342 (.in(1'b0), .out(out_19), .gate(hc[1]));
  Transistor #(.\type ("n")) transistor_343 (.in(1'b0), .out(out_21), .gate(hc[1]));
  Transistor #(.\type ("n")) transistor_344 (.in(1'b0), .out(out_25), .gate(hc[1]));
  Transistor #(.\type ("n")) transistor_345 (.in(1'b0), .out(out_26), .gate(hc[1]));
  Transistor #(.\type ("n")) transistor_346 (.in(1'b0), .out(out_28), .gate(hc[1]));
  Transistor #(.\type ("n")) transistor_347 (.in(1'b0), .out(out_29), .gate(hc[1]));
  Transistor #(.\type ("n")) transistor_348 (.in(1'b0), .out(out_31), .gate(hc[1]));
  Transistor #(.\type ("n")) transistor_349 (.in(1'b0), .out(out_32), .gate(hc[1]));
  Transistor #(.\type ("n")) transistor_350 (.in(1'b0), .out(out_34), .gate(hc[1]));
  Transistor #(.\type ("n")) transistor_351 (.in(1'b0), .out(out_35), .gate(hc[1]));
  Transistor #(.\type ("n")) transistor_352 (.in(1'b0), .out(out_36), .gate(hc[1]));
  Transistor #(.\type ("n")) transistor_353 (.in(1'b0), .out(out_37), .gate(hc[1]));
  Transistor #(.\type ("n")) transistor_354 (.in(1'b0), .out(out_39), .gate(hc[1]));
  Transistor #(.\type ("n")) transistor_355 (.in(1'b0), .out(out_44), .gate(hc[1]));
  Transistor #(.\type ("n")) transistor_356 (.in(1'b0), .out(out_46), .gate(hc[1]));
  Transistor #(.\type ("n")) transistor_357 (.in(1'b0), .out(out_47), .gate(hc[1]));
  Transistor #(.\type ("n")) transistor_358 (.in(1'b0), .out(out_48), .gate(hc[1]));
  Transistor #(.\type ("n")) transistor_359 (.in(1'b0), .out(out_49), .gate(hc[1]));
  Transistor #(.\type ("n")) transistor_360 (.in(1'b0), .out(out_51), .gate(hc[1]));
  Transistor #(.\type ("n")) transistor_361 (.in(1'b0), .out(out_54), .gate(hc[1]));
  Transistor #(.\type ("n")) transistor_362 (.in(1'b0), .out(out_56), .gate(hc[1]));
  Transistor #(.\type ("n")) transistor_363 (.in(1'b0), .out(out_5), .gate(not_9_out));
  Transistor #(.\type ("n")) transistor_364 (.in(1'b0), .out(out_24), .gate(not_9_out));
  Transistor #(.\type ("n")) transistor_365 (.in(1'b0), .out(out_25), .gate(not_9_out));
  Transistor #(.\type ("n")) transistor_366 (.in(1'b0), .out(out_26), .gate(not_9_out));
  Transistor #(.\type ("n")) transistor_367 (.in(1'b0), .out(out_27), .gate(not_9_out));
  Transistor #(.\type ("n")) transistor_368 (.in(1'b0), .out(out_28), .gate(not_9_out));
  Transistor #(.\type ("n")) transistor_369 (.in(1'b0), .out(out_29), .gate(not_9_out));
  Transistor #(.\type ("n")) transistor_370 (.in(1'b0), .out(out_30), .gate(not_9_out));
  Transistor #(.\type ("n")) transistor_371 (.in(1'b0), .out(out_31), .gate(not_9_out));
  Transistor #(.\type ("n")) transistor_372 (.in(1'b0), .out(out_32), .gate(not_9_out));
  Transistor #(.\type ("n")) transistor_373 (.in(1'b0), .out(out_33), .gate(not_9_out));
  Transistor #(.\type ("n")) transistor_374 (.in(1'b0), .out(out_34), .gate(not_9_out));
  Transistor #(.\type ("n")) transistor_375 (.in(1'b0), .out(out_35), .gate(not_9_out));
  Transistor #(.\type ("n")) transistor_376 (.in(1'b0), .out(out_36), .gate(not_9_out));
  Transistor #(.\type ("n")) transistor_377 (.in(1'b0), .out(out_37), .gate(not_9_out));
  Transistor #(.\type ("n")) transistor_378 (.in(1'b0), .out(out_38), .gate(not_9_out));
  Transistor #(.\type ("n")) transistor_379 (.in(1'b0), .out(out_39), .gate(not_9_out));
  Transistor #(.\type ("n")) transistor_380 (.in(1'b0), .out(out_40), .gate(not_9_out));
  Transistor #(.\type ("n")) transistor_381 (.in(1'b0), .out(out_41), .gate(not_9_out));
  Transistor #(.\type ("n")) transistor_382 (.in(1'b0), .out(out_42), .gate(not_9_out));
  not not_9 (not_9_out, hc[0]);
  Transistor #(.\type ("n")) transistor_383 (.in(1'b0), .out(out_2), .gate(hc[0]));
  Transistor #(.\type ("n")) transistor_384 (.in(1'b0), .out(out_3), .gate(hc[0]));
  Transistor #(.\type ("n")) transistor_385 (.in(1'b0), .out(out_4), .gate(hc[0]));
  Transistor #(.\type ("n")) transistor_386 (.in(1'b0), .out(out_6), .gate(hc[0]));
  Transistor #(.\type ("n")) transistor_387 (.in(1'b0), .out(out_7), .gate(hc[0]));
  Transistor #(.\type ("n")) transistor_388 (.in(1'b0), .out(out_8), .gate(hc[0]));
  Transistor #(.\type ("n")) transistor_389 (.in(1'b0), .out(out_9), .gate(hc[0]));
  Transistor #(.\type ("n")) transistor_390 (.in(1'b0), .out(out_10), .gate(hc[0]));
  Transistor #(.\type ("n")) transistor_391 (.in(1'b0), .out(out_11), .gate(hc[0]));
  Transistor #(.\type ("n")) transistor_392 (.in(1'b0), .out(out_12), .gate(hc[0]));
  Transistor #(.\type ("n")) transistor_393 (.in(1'b0), .out(out_13), .gate(hc[0]));
  Transistor #(.\type ("n")) transistor_394 (.in(1'b0), .out(out_14), .gate(hc[0]));
  Transistor #(.\type ("n")) transistor_395 (.in(1'b0), .out(out_15), .gate(hc[0]));
  Transistor #(.\type ("n")) transistor_396 (.in(1'b0), .out(out_16), .gate(hc[0]));
  Transistor #(.\type ("n")) transistor_397 (.in(1'b0), .out(out_17), .gate(hc[0]));
  Transistor #(.\type ("n")) transistor_398 (.in(1'b0), .out(out_18), .gate(hc[0]));
  Transistor #(.\type ("n")) transistor_399 (.in(1'b0), .out(out_19), .gate(hc[0]));
  Transistor #(.\type ("n")) transistor_400 (.in(1'b0), .out(out_20), .gate(hc[0]));
  Transistor #(.\type ("n")) transistor_401 (.in(1'b0), .out(out_21), .gate(hc[0]));
  Transistor #(.\type ("n")) transistor_402 (.in(1'b0), .out(out_22), .gate(hc[0]));
  Transistor #(.\type ("n")) transistor_403 (.in(1'b0), .out(out_23), .gate(hc[0]));
  Transistor #(.\type ("n")) transistor_404 (.in(1'b0), .out(out_44), .gate(hc[0]));
  Transistor #(.\type ("n")) transistor_405 (.in(1'b0), .out(out_45), .gate(hc[0]));
  Transistor #(.\type ("n")) transistor_406 (.in(1'b0), .out(out_46), .gate(hc[0]));
  Transistor #(.\type ("n")) transistor_407 (.in(1'b0), .out(out_47), .gate(hc[0]));
  Transistor #(.\type ("n")) transistor_408 (.in(1'b0), .out(out_48), .gate(hc[0]));
  Transistor #(.\type ("n")) transistor_409 (.in(1'b0), .out(out_49), .gate(hc[0]));
  Transistor #(.\type ("n")) transistor_410 (.in(1'b0), .out(out_50), .gate(hc[0]));
  Transistor #(.\type ("n")) transistor_411 (.in(1'b0), .out(out_51), .gate(hc[0]));
  Transistor #(.\type ("n")) transistor_412 (.in(1'b0), .out(out_52), .gate(hc[0]));
  Transistor #(.\type ("n")) transistor_413 (.in(1'b0), .out(out_53), .gate(hc[0]));
  Transistor #(.\type ("n")) transistor_414 (.in(1'b0), .out(out_54), .gate(hc[0]));
  Transistor #(.\type ("n")) transistor_415 (.in(1'b0), .out(out_55), .gate(hc[0]));
  Transistor #(.\type ("n")) transistor_416 (.in(1'b0), .out(out_56), .gate(hc[0]));
  Transistor #(.\type ("n")) transistor_417 (.in(1'b0), .out(out_57), .gate(hc[0]));
  Transistor #(.\type ("n")) transistor_418 (.in(1'b0), .out(out_58), .gate(hc[0]));
endmodule
