// Logisim project alu_modules.circ as structural Verilog: 3 circuits, main circuit oai32
module oai32 (
  input  a0,
  input  a1,
  input  a2,
  input  b0,
  input  b1,
  output x2,
  output x
);

  wire or_1_out, or_2_out, transistor_1_out, transistor_2_out, transistor_3_out, transistor_8_out;

  Transistor transistor_1 (.in(1'b1), .out(transistor_1_out), .gate(a0));
  Transistor #(.\type ("n")) transistor_2 (.in(1'b0), .out(transistor_2_out), .gate(a0));
  Transistor transistor_3 (.in(transistor_1_out), .out(transistor_3_out), .gate(a1));
  Transistor #(.\type ("n")) transistor_4 (.in(1'b0), .out(transistor_2_out), .gate(a1));
  Transistor transistor_5 (.in(transistor_3_out), .out(x), .gate(a2));
  Transistor #(.\type ("n")) transistor_6 (.in(1'b0), .out(transistor_2_out), .gate(a2));
  Transistor transistor_7 (.in(transistor_8_out), .out(x), .gate(b0));
  Transistor transistor_8 (.in(1'b1), .out(transistor_8_out), .gate(b1));
  Transistor #(.\type ("n")) transistor_9 (.in(transistor_2_out), .out(x), .gate(b0));
  Transistor #(.\type ("n")) transistor_10 (.in(transistor_2_out), .out(x), .gate(b1));
  or or_1 (or_1_out, a0, a1, a2);
  or or_2 (or_2_out, b0, b1);
  nand nand_1 (x2, or_1_out, or_2_out);
endmodule

module aoi (
  input  b,
  input  a1,
  input  a0,
  output x2,
  output x
);

  wire and_1_out, transistor_2_out, transistor_3_out;

  Transistor #(.\type ("n")) transistor_1 (.in(1'b0), .out(x), .gate(b));
  Transistor transistor_2 (.in(1'b1), .out(transistor_2_out), .gate(b));
  Transistor #(.\type ("n")) transistor_3 (.in(1'b0), .out(transistor_3_out), .gate(a1));
  Transistor transistor_4 (.in(transistor_2_out), .out(x), .gate(a1));
  Transistor #(.\type ("n")) transistor_5 (.in(transistor_3_out), .out(x), .gate(a0));
  Transistor transistor_6 (.in(transistor_2_out), .out(x), .gate(a0));
  and and_1 (and_1_out, a1, a0);
  nor nor_1 (x2, and_1_out, b);
endmodule

module inv_tris_comp (
  input  a,
  input  n_ena,
  input  ena,
  output x
);

  wire transistor_1_out, transistor_3_out;

  Transistor transistor_1 (.in(1'b1), .out(transistor_1_out), .gate(a));
  Transistor transistor_2 (.in(transistor_1_out), .out(x), .gate(n_ena));
  Transistor #(.\type ("n")) transistor_3 (.in(1'b0), .out(transistor_3_out), .gate(a));
  Transistor #(.\type ("n")) transistor_4 (.in(transistor_3_out), .out(x), .gate(ena));

  // Notes on the sheet:
  //   disabled gate
  //   disabled gate
endmodule
