// Logisim project clkgen.circ as structural Verilog: 1 circuit, main circuit main
module main (
  input  clk_frompad,
  output clk,
  output cclk
);

  wire buffer_1_out, nand_1_out, nand_2_out, not_1_out, not_2_out, not_3_out, not_4_out, not_5_out;

  buf buffer_1 (buffer_1_out, clk_frompad);
  not not_1 (not_1_out, buffer_1_out);
  not not_2 (not_2_out, not_1_out);
  not not_3 (not_3_out, not_2_out);
  not not_4 (not_4_out, not_3_out);
  not not_5 (not_5_out, not_4_out);
  nand nand_1 (nand_1_out, not_2_out, not_4_out);
  nand nand_2 (nand_2_out, not_1_out, not_5_out);
  not not_6 (clk, nand_1_out);
  not not_7 (cclk, nand_2_out);
endmodule
