// Logisim project dbif.circ as structural Verilog: 3 circuits, main circuit main
module main (
  input  n_out_enable,
  input  latch_to_db,
  input  pad_to_latch,
  input  n_db_to_latch,
  input  n_val_in,
  input  db_in,
  output oe,
  output n_oe,
  output db_out,
  output set_in,
  output val_out
);

  wire buffer_1_out, dl_nq, dl_q, feedback_tris_x, nor_1_out, not_1_out, not_4_out, not_5_out;

  buf buffer_1 (buffer_1_out, n_val_in);
  nor nor_1 (nor_1_out, pad_to_latch, n_db_to_latch);
  not not_1 (not_1_out, nor_1_out);
  not not_2 (set_in, pad_to_latch);
  not not_3 (oe, n_out_enable);
  not not_4 (not_4_out, n_out_enable);
  inv_tris_comp feedback_tris (.a(dl_nq), .ena(nor_1_out), .n_ena(not_1_out), .x(feedback_tris_x));
  inv_tris_comp from_pad_tris (.a(buffer_1_out), .ena(pad_to_latch), .n_ena(set_in), .x(feedback_tris_x));
  not not_5 (not_5_out, n_db_to_latch);
  assign feedback_tris_x = not_5_out ? ~db_in : 1'bz;  // Controlled_Inverter controlled_inverter_1
  not not_6 (n_oe, not_4_out);
  transp_latch_nq dl (.d(feedback_tris_x), .q(dl_q), .nq(dl_nq));
  assign db_out = latch_to_db ? ~dl_q : 1'bz;  // Controlled_Inverter controlled_inverter_2
  buf buffer_2 (val_out, feedback_tris_x);

  // Notes on the sheet:
  //   from pad (active-low)
  //   from databus
  //   databus is active-low (inverse hold)
  //   notif0
  //   from_databus_tris
  //   notif1
  //   D pad drive enable
  //   to databus
  //   1: force n_val_in = 0
  //   to pad
endmodule

module transp_latch_nq (
  input  d,
  output q,
  output nq
);

  D_Flip_Flop #(.trigger("high")) d_ff_1 (.D(d), .clk(1'b1), .Q(q), .Qn(nq));  // open: preset, reset
endmodule

module inv_tris_comp (
  input  a,
  input  ena,
  input  n_ena,
  output x
);

  assign x = ena ? ~a : 1'bz;  // Controlled_Inverter controlled_inverter_1
endmodule
