// Logisim project pad_d.circ as structural Verilog: 2 circuits, main circuit main
module main (
  input  val_out,
  input  n_oe,
  input  oe,
  input  from_pad,
  input  set_in,
  output to_pad,
  output n_val_in
);

  wire transistor_1_out, transistor_3_out, transistor_8_out, transp_latch_1_out_2;

  transp_latch transp_latch_1 (.tri_state(from_pad), .out_2(transp_latch_1_out_2));
  Transistor transistor_1 (.in(transistor_8_out), .out(transistor_1_out), .gate(n_oe));
  Transistor transistor_2 (.in(transistor_3_out), .out(n_val_in), .gate(transp_latch_1_out_2));
  Transistor transistor_3 (.in(1'b1), .out(transistor_3_out), .gate(set_in));
  Transistor transistor_4 (.in(1'b1), .out(to_pad), .gate(transistor_1_out));
  Transistor transistor_5 (.in(1'b1), .out(transistor_1_out), .gate(val_out));
  Transistor transistor_6 (.in(1'b1), .out(transistor_1_out), .gate(oe));
  Transistor #(.\type ("n")) transistor_7 (.in(1'b0), .out(to_pad), .gate(transistor_8_out));
  Transistor #(.\type ("n")) transistor_8 (.in(1'b0), .out(transistor_8_out), .gate(val_out));
  Transistor #(.\type ("n")) transistor_9 (.in(1'b0), .out(transistor_8_out), .gate(n_oe));
  Transistor #(.\type ("n")) transistor_10 (.in(transistor_8_out), .out(transistor_1_out), .gate(oe));
  Transistor #(.\type ("n")) transistor_11 (.in(1'b0), .out(n_val_in), .gate(transp_latch_1_out_2));
  Transistor #(.\type ("n")) transistor_12 (.in(1'b0), .out(n_val_in), .gate(set_in));

  // Notes on the sheet:
  //   tri-state
  //   bidir FET
  //   CPU -> Bus
  //   Bus -> CPU
  //   bidir FET
  //   tri-state
endmodule

module transp_latch (
  input  tri_state,
  output out_2
);

  D_Flip_Flop #(.trigger("high")) d_ff_1 (.D(tri_state), .clk(1'b1), .Q(out_2));  // open: Qn, preset, reset
endmodule
