// Logisim project regblock_bufif1.circ as structural Verilog: 1 circuit, main circuit main
module main (
  input  ena,
  input  d,
  output q
);

  wire transistor_3_out, transistor_5_out, transistor_8_out;

  Transistor #(.\type ("n")) transistor_1 (.in(1'b0), .out(q), .gate(transistor_3_out));
  Transistor transistor_2 (.in(1'b1), .out(q), .gate(transistor_5_out));
  Transistor #(.\type ("n")) transistor_3 (.in(1'b0), .out(transistor_3_out), .gate(d));
  Transistor transistor_4 (.in(1'b1), .out(transistor_3_out), .gate(d));
  Transistor #(.\type ("n")) transistor_5 (.in(transistor_8_out), .out(transistor_5_out), .gate(d));
  Transistor transistor_6 (.in(1'b1), .out(transistor_3_out), .gate(d));
  Transistor transistor_7 (.in(1'b1), .out(transistor_5_out), .gate(d));
  Transistor #(.\type ("n")) transistor_8 (.in(1'b0), .out(transistor_8_out), .gate(ena));
  Transistor transistor_9 (.in(1'b1), .out(transistor_5_out), .gate(ena));
endmodule
