// Logisim project regblock_duty_extend.circ as structural Verilog: 1 circuit, main circuit main
module main (
  input  a,
  output x
);

  wire not_1_out, not_2_out, not_3_out, not_4_out, not_5_out;

  not not_1 (not_1_out, a);
  not not_2 (not_2_out, not_1_out);
  not not_3 (not_3_out, not_2_out);
  not not_4 (not_4_out, not_3_out);
  not not_5 (not_5_out, not_4_out);
  or or_1 (x, not_1_out, not_5_out);

  // Notes on the sheet:
  //   delay
endmodule
