// Logisim project regblock_idu_xor.circ as structural Verilog: 1 circuit, main circuit main
module main (
  input  xi,
  input  in2,
  output ab,
  output xo
);

  wire nand_1_out, nand_2_out, or_1_out;

  nand nand_1 (nand_1_out, xi, in2);
  or or_1 (or_1_out, xi, in2);
  nand nand_2 (nand_2_out, or_1_out, nand_1_out);
  not not_1 (ab, xi);
  not not_2 (xo, nand_2_out);

  // Notes on the sheet:
  //   xor
endmodule
