// Logisim project regblock_oai.circ as structural Verilog: 1 circuit, main circuit main
module main (
  input  b,
  input  a1,
  input  a0,
  output out_4
);

  wire transistor_4_out, transistor_5_out;

  Transistor #(.\type ("n")) transistor_1 (.in(transistor_5_out), .out(out_4), .gate(a0));
  Transistor transistor_2 (.in(transistor_4_out), .out(out_4), .gate(a0));
  Transistor #(.\type ("n")) transistor_3 (.in(transistor_5_out), .out(out_4), .gate(a1));
  Transistor transistor_4 (.in(1'b1), .out(transistor_4_out), .gate(a1));
  Transistor #(.\type ("n")) transistor_5 (.in(1'b0), .out(transistor_5_out), .gate(b));
  Transistor transistor_6 (.in(1'b1), .out(out_4), .gate(b));
endmodule
