// Logisim project CMOS_CELLS.circ as structural Verilog
module D_LATCH (
  input  EN,
  input  D,
  output Q,
  output nQ
);

  D_Flip_Flop #(.trigger("high")) d_ff_1 (.clk(EN), .D(D), .Q(Q), .Qn(nQ));  // open: preset, en, reset
endmodule

module COMPL_INV (
  input  B,
  input  A,
  input  A_2,
  input  B_2,
  output out_5,
  output out_6
);

  wire not_1_out, transistor_1_out, transistor_3_out, transistor_6_out;

  Transistor transistor_1 (.in(1'b1), .out(transistor_1_out), .gate(A));
  Transistor #(.\type ("n")) transistor_2 (.in(1'b0), .out(transistor_1_out), .gate(A));
  Transistor transistor_3 (.in(1'b1), .out(transistor_3_out), .gate(B_2));
  Transistor transistor_4 (.in(transistor_3_out), .out(out_5), .gate(A));
  Transistor #(.\type ("n")) transistor_5 (.in(transistor_6_out), .out(out_5), .gate(transistor_1_out));
  Transistor #(.\type ("n")) transistor_6 (.in(1'b0), .out(transistor_6_out), .gate(B_2));
  not not_1 (not_1_out, B);
  assign out_6 = not_1_out ? ~A_2 : 1'bz;  // Controlled_Inverter controlled_inverter_1

  // Notes on the sheet:
  //   A
  //   B
  //   A
  //   ~
endmodule

module OR (
  input  B,
  input  B_2,
  input  A,
  input  A_2,
  output out_5,
  output out_6
);

  wire transistor_1_out, transistor_2_out;

  Transistor #(.\type ("n")) transistor_1 (.in(1'b0), .out(transistor_1_out), .gate(A_2));
  Transistor transistor_2 (.in(1'b1), .out(transistor_2_out), .gate(A_2));
  Transistor transistor_3 (.in(transistor_2_out), .out(transistor_1_out), .gate(B_2));
  Transistor #(.\type ("n")) transistor_4 (.in(1'b0), .out(transistor_1_out), .gate(B_2));
  Transistor transistor_5 (.in(1'b1), .out(out_5), .gate(transistor_1_out));
  Transistor #(.\type ("n")) transistor_6 (.in(1'b0), .out(out_5), .gate(transistor_1_out));
  or or_1 (out_6, B, A);

  // Notes on the sheet:
  //   A
  //   B
  //   B
  //   A
endmodule

module SR_BIT (
  input  IN,
  input  nSTEP,
  input  STEP,
  input  LOAD,
  input  nLOAD,
  input  IN_2,
  input  LOAD_2,
  input  STEP_2,
  output OUT,
  output OUT_2
);

  wire d_latch_1_nq, transistor_1_out, transistor_3_out, transistor_4_out, transistor_6_out;

  Transistor transistor_1 (.in(IN), .out(transistor_1_out), .gate(nLOAD));
  Transistor #(.\type ("n")) transistor_2 (.in(IN), .out(transistor_1_out), .gate(LOAD_2));
  Transistor transistor_3 (.in(1'b1), .out(transistor_3_out), .gate(transistor_1_out));
  Transistor transistor_4 (.in(transistor_3_out), .out(transistor_4_out), .gate(nSTEP));
  Transistor #(.\type ("n")) transistor_5 (.in(transistor_6_out), .out(transistor_4_out), .gate(STEP_2));
  Transistor #(.\type ("n")) transistor_6 (.in(1'b0), .out(transistor_6_out), .gate(transistor_1_out));
  Transistor transistor_7 (.in(1'b1), .out(OUT), .gate(transistor_4_out));
  Transistor #(.\type ("n")) transistor_8 (.in(1'b0), .out(OUT), .gate(transistor_4_out));
  D_LATCH d_latch_1 (.EN(LOAD), .D(IN_2), .nQ(d_latch_1_nq));  // open: Q
  D_LATCH d_latch_2 (.EN(STEP), .D(d_latch_1_nq), .nQ(OUT_2));  // open: Q

  // Notes on the sheet:
  //   ~
endmodule

module _3_NAND (
  input  C,
  input  B,
  input  C_2,
  input  A,
  input  B_2,
  input  A_2,
  output out_7,
  output out_8
);

  wire transistor_5_out, transistor_6_out;

  Transistor transistor_1 (.in(1'b1), .out(out_7), .gate(A_2));
  Transistor transistor_2 (.in(1'b1), .out(out_7), .gate(B_2));
  Transistor transistor_3 (.in(1'b1), .out(out_7), .gate(C_2));
  Transistor #(.\type ("n")) transistor_4 (.in(transistor_5_out), .out(out_7), .gate(C_2));
  Transistor #(.\type ("n")) transistor_5 (.in(transistor_6_out), .out(transistor_5_out), .gate(B_2));
  Transistor #(.\type ("n")) transistor_6 (.in(1'b0), .out(transistor_6_out), .gate(A_2));
  nand nand_1 (out_8, C, B, A);

  // Notes on the sheet:
  //   A
  //   B
  //   C
  //   C
  //   B
  //   A
  //   ~
endmodule

module DLATCH_CMOS (
  input  B,
  input  C,
  input  B_2,
  input  A,
  input  A_2,
  input  C_2,
  output Q,
  output Q_2
);

  wire transistor_1_out, transistor_2_out, transistor_4_out, transistor_5_out, transistor_8_out,
       transistor_9_out, transistor_11_out;

  Transistor transistor_1 (.in(1'b1), .out(transistor_1_out), .gate(A));
  Transistor transistor_2 (.in(transistor_1_out), .out(transistor_2_out), .gate(C_2));
  Transistor #(.\type ("n")) transistor_3 (.in(transistor_4_out), .out(transistor_2_out), .gate(B));
  Transistor #(.\type ("n")) transistor_4 (.in(1'b0), .out(transistor_4_out), .gate(A));
  Transistor transistor_5 (.in(1'b1), .out(transistor_5_out), .gate(transistor_9_out));
  Transistor transistor_6 (.in(transistor_5_out), .out(transistor_2_out), .gate(B));
  Transistor #(.\type ("n")) transistor_7 (.in(transistor_8_out), .out(transistor_2_out), .gate(C_2));
  Transistor #(.\type ("n")) transistor_8 (.in(1'b0), .out(transistor_8_out), .gate(transistor_9_out));
  Transistor transistor_9 (.in(1'b1), .out(transistor_9_out), .gate(transistor_2_out));
  Transistor #(.\type ("n")) transistor_10 (.in(1'b0), .out(transistor_9_out), .gate(transistor_2_out));
  Transistor transistor_11 (.in(1'b1), .out(transistor_11_out), .gate(transistor_9_out));
  Transistor #(.\type ("n")) transistor_12 (.in(1'b0), .out(transistor_11_out), .gate(transistor_9_out));
  Transistor transistor_13 (.in(1'b1), .out(Q), .gate(transistor_11_out));
  Transistor #(.\type ("n")) transistor_14 (.in(1'b0), .out(Q), .gate(transistor_11_out));
  D_LATCH d_latch_1 (.EN(B_2), .D(A_2), .Q(Q_2));  // open: nQ

  // Notes on the sheet:
  //   1
  //   3
  //   4
  //   2
  //   7
  //   5
  //   6
  //   8
  //   9
  //   10
  //   11
  //   12
  //   13
  //   14
  //   COMPL
  //   ~
endmodule

module _2NOT_CMOS (
  input  A,
  input  A_2,
  output Q2,
  output Q1,
  output Q2_2,
  output Q1_2
);

  wire transistor_2_out, transistor_3_out, transistor_6_out, transistor_7_out;

  Transistor transistor_1 (.in(1'b1), .out(Q1_2), .gate(A));
  Transistor transistor_2 (.in(Q1_2), .out(transistor_2_out), .gate(A));
  Transistor #(.\type ("n")) transistor_3 (.in(Q1_2), .out(transistor_3_out), .gate(A));
  Transistor #(.\type ("n")) transistor_4 (.in(1'b0), .out(Q1_2), .gate(A));
  Transistor transistor_5 (.in(1'b1), .out(Q2), .gate(Q1_2));
  Transistor transistor_6 (.in(Q2), .out(transistor_6_out), .gate(Q1_2));
  Transistor #(.\type ("n")) transistor_7 (.in(Q2), .out(transistor_7_out), .gate(Q1_2));
  Transistor #(.\type ("n")) transistor_8 (.in(1'b0), .out(Q2), .gate(Q1_2));
  not not_1 (Q1, A_2);
  not not_2 (Q2_2, Q1);
  // also tied to GND on the sheet: {transistor_3_out, transistor_7_out}
  // also tied to VCC on the sheet: {transistor_2_out, transistor_6_out}

  // Notes on the sheet:
  //   3
  //   4
  //   7
  //   8
  //   1
  //   2
  //   5
  //   6
  //   ~
endmodule

module SUPER_INV_BUF (
  input  IN,
  input  IN_2,
  output Q,
  output Q_2
);

  wire transistor_2_out, transistor_3_out, transistor_6_out, transistor_7_out;

  Transistor transistor_1 (.in(1'b1), .out(Q), .gate(IN));
  Transistor transistor_2 (.in(Q), .out(transistor_2_out), .gate(IN));
  Transistor #(.\type ("n")) transistor_3 (.in(Q), .out(transistor_3_out), .gate(IN));
  Transistor #(.\type ("n")) transistor_4 (.in(1'b0), .out(Q), .gate(IN));
  Transistor transistor_5 (.in(1'b1), .out(Q), .gate(IN));
  Transistor transistor_6 (.in(Q), .out(transistor_6_out), .gate(IN));
  Transistor #(.\type ("n")) transistor_7 (.in(Q), .out(transistor_7_out), .gate(IN));
  Transistor #(.\type ("n")) transistor_8 (.in(1'b0), .out(Q), .gate(IN));
  not not_1 (Q_2, IN_2);
  // also tied to GND on the sheet: {transistor_3_out, transistor_7_out}
  // also tied to VCC on the sheet: {transistor_2_out, transistor_6_out}

  // Notes on the sheet:
  //   A
  //   C
  //   B
  //   D
  //   ~
endmodule

module NAND (
  input  B,
  input  B_2,
  input  A,
  input  A_2,
  output out_5,
  output out_6
);

  wire transistor_4_out;

  Transistor transistor_1 (.in(1'b1), .out(out_5), .gate(A_2));
  Transistor transistor_2 (.in(1'b1), .out(out_5), .gate(B_2));
  Transistor #(.\type ("n")) transistor_3 (.in(transistor_4_out), .out(out_5), .gate(B_2));
  Transistor #(.\type ("n")) transistor_4 (.in(1'b0), .out(transistor_4_out), .gate(A_2));
  nand nand_1 (out_6, B, A);

  // Notes on the sheet:
  //   A
  //   B
  //   B
  //   A
  //   ~
endmodule

module NOT (
  input  A,
  input  A_2,
  output Q,
  output Q_2
);

  Transistor transistor_1 (.in(1'b1), .out(Q), .gate(A));
  Transistor #(.\type ("n")) transistor_2 (.in(1'b0), .out(Q), .gate(A));
  not not_1 (Q_2, A_2);

  // Notes on the sheet:
  //   ~
endmodule

module AOI21 (
  input  A,
  input  A_2,
  input  B,
  input  C,
  input  B_2,
  input  C_2,
  output Q,
  output Q_2
);

  wire and_1_out, transistor_1_out, transistor_3_out;

  Transistor transistor_1 (.in(1'b1), .out(transistor_1_out), .gate(A));
  Transistor #(.\type ("n")) transistor_2 (.in(transistor_3_out), .out(Q), .gate(A));
  Transistor #(.\type ("n")) transistor_3 (.in(1'b0), .out(transistor_3_out), .gate(B_2));
  Transistor transistor_4 (.in(1'b1), .out(transistor_1_out), .gate(B_2));
  Transistor transistor_5 (.in(transistor_1_out), .out(Q), .gate(C_2));
  Transistor #(.\type ("n")) transistor_6 (.in(1'b0), .out(Q), .gate(C_2));
  and and_1 (and_1_out, A_2, B);
  nor nor_1 (Q_2, and_1_out, C);

  // Notes on the sheet:
  //   1
  //   4
  //   5
  //   2
  //   3
  //   6
  //   AOI21
  //   ~
endmodule

module _3AND (
  input  B,
  input  A,
  input  C,
  input  B_2,
  input  A_2,
  input  C_2,
  output Q,
  output Q_2
);

  wire transistor_1_out, transistor_5_out, transistor_6_out;

  Transistor transistor_1 (.in(1'b1), .out(transistor_1_out), .gate(B_2));
  Transistor transistor_2 (.in(1'b1), .out(transistor_1_out), .gate(A_2));
  Transistor transistor_3 (.in(1'b1), .out(transistor_1_out), .gate(C_2));
  Transistor #(.\type ("n")) transistor_4 (.in(transistor_5_out), .out(transistor_1_out), .gate(B_2));
  Transistor #(.\type ("n")) transistor_5 (.in(transistor_6_out), .out(transistor_5_out), .gate(A_2));
  Transistor #(.\type ("n")) transistor_6 (.in(1'b0), .out(transistor_6_out), .gate(C_2));
  Transistor transistor_7 (.in(1'b1), .out(Q), .gate(transistor_1_out));
  Transistor #(.\type ("n")) transistor_8 (.in(1'b0), .out(Q), .gate(transistor_1_out));
  and and_1 (Q_2, B, A, C);

  // Notes on the sheet:
  //   1
  //   2
  //   3
  //   5
  //   8
  //   6
  //   4
  //   7
  //   ~
endmodule

module XOR (
  input  A,
  input  B,
  input  A_2,
  input  B_2,
  output Q,
  output Q_2
);

  wire transistor_1_out, transistor_2_out, transistor_5_out, transistor_8_out, transistor_9_out;

  Transistor transistor_1 (.in(1'b1), .out(transistor_1_out), .gate(B_2));
  Transistor transistor_2 (.in(transistor_1_out), .out(transistor_2_out), .gate(A_2));
  Transistor #(.\type ("n")) transistor_3 (.in(1'b0), .out(transistor_2_out), .gate(A_2));
  Transistor #(.\type ("n")) transistor_4 (.in(1'b0), .out(transistor_2_out), .gate(B_2));
  Transistor transistor_5 (.in(1'b1), .out(transistor_5_out), .gate(B_2));
  Transistor transistor_6 (.in(transistor_5_out), .out(Q), .gate(transistor_2_out));
  Transistor #(.\type ("n")) transistor_7 (.in(transistor_8_out), .out(Q), .gate(A_2));
  Transistor #(.\type ("n")) transistor_8 (.in(1'b0), .out(transistor_8_out), .gate(B_2));
  Transistor transistor_9 (.in(1'b1), .out(transistor_9_out), .gate(A_2));
  Transistor transistor_10 (.in(transistor_9_out), .out(Q), .gate(transistor_2_out));
  Transistor #(.\type ("n")) transistor_11 (.in(1'b0), .out(Q), .gate(transistor_2_out));
  xor xor_1 (Q_2, A, B);

  // Notes on the sheet:
  //   2
  //   1
  //   7
  //   8
  //   3
  //   4
  //   10
  //   9
  //   6
  //   5
  //   11
  //   ~
endmodule

module LFSR_BIT (
  input  D,
  input  C,
  input  G,
  input  C_2,
  input  D_2,
  input  B,
  input  E,
  input  F,
  input  A,
  input  G_2,
  input  A_2,
  input  B_2,
  input  E_2,
  input  F_2,
  output Q,
  output Q_2
);

  wire and_1_out, and_2_out, d_latch_1_nq, nor_1_out, not_1_out, transistor_1_out, transistor_2_out,
       transistor_4_out, transistor_8_out, transistor_9_out, transistor_10_out, transistor_12_out,
       transistor_13_out, transistor_14_out, transistor_16_out, transistor_17_out;

  Transistor transistor_1 (.in(1'b1), .out(transistor_1_out), .gate(G));
  Transistor transistor_2 (.in(transistor_1_out), .out(transistor_2_out), .gate(transistor_17_out));
  Transistor #(.\type ("n")) transistor_3 (.in(transistor_4_out), .out(transistor_2_out), .gate(B_2));
  Transistor #(.\type ("n")) transistor_4 (.in(1'b0), .out(transistor_4_out), .gate(G));
  Transistor transistor_5 (.in(1'b1), .out(transistor_1_out), .gate(B_2));
  Transistor transistor_6 (.in(transistor_1_out), .out(transistor_2_out), .gate(A));
  Transistor #(.\type ("n")) transistor_7 (.in(transistor_8_out), .out(transistor_2_out), .gate(A));
  Transistor #(.\type ("n")) transistor_8 (.in(1'b0), .out(transistor_8_out), .gate(transistor_17_out));
  Transistor transistor_9 (.in(1'b1), .out(transistor_9_out), .gate(transistor_2_out));
  Transistor transistor_10 (.in(transistor_9_out), .out(transistor_10_out), .gate(C));
  Transistor #(.\type ("n")) transistor_11 (.in(transistor_12_out), .out(transistor_10_out), .gate(E_2));
  Transistor #(.\type ("n")) transistor_12 (.in(1'b0), .out(transistor_12_out), .gate(transistor_2_out));
  Transistor transistor_13 (.in(1'b1), .out(transistor_13_out), .gate(transistor_10_out));
  Transistor transistor_14 (.in(transistor_13_out), .out(transistor_14_out), .gate(D));
  Transistor #(.\type ("n")) transistor_15 (.in(transistor_16_out), .out(transistor_14_out), .gate(F_2));
  Transistor #(.\type ("n")) transistor_16 (.in(1'b0), .out(transistor_16_out), .gate(transistor_10_out));
  Transistor transistor_17 (.in(1'b1), .out(transistor_17_out), .gate(transistor_14_out));
  Transistor #(.\type ("n")) transistor_18 (.in(1'b0), .out(transistor_17_out), .gate(transistor_14_out));
  Transistor transistor_19 (.in(1'b1), .out(Q), .gate(transistor_14_out));
  Transistor #(.\type ("n")) transistor_20 (.in(1'b0), .out(Q), .gate(transistor_14_out));
  and and_1 (and_1_out, B, G_2);
  and and_2 (and_2_out, A_2, Q_2);
  not not_1 (not_1_out, nor_1_out);
  nor nor_1 (nor_1_out, and_1_out, and_2_out);
  D_LATCH d_latch_1 (.EN(E), .D(not_1_out), .nQ(d_latch_1_nq));  // open: Q
  D_LATCH d_latch_2 (.EN(F), .D(d_latch_1_nq), .nQ(Q_2));  // open: Q

  // Notes on the sheet:
  //   1
  //   2
  //   12
  //   11
  //   4
  //   3
  //   13
  //   14
  //   5
  //   6
  //   16
  //   15
  //   7
  //   8
  //   18
  //   17
  //   9
  //   19
  //   10
  //   20
  //   ~
  //   COMPL
  //   COMPL
endmodule

module AON2222 (
  input  _7,
  input  _7_2,
  input  _6,
  input  _6_2,
  input  _5,
  input  _5_2,
  input  _4,
  input  _4_2,
  input  _3,
  input  _3_2,
  input  _2,
  input  _2_2,
  input  _1,
  input  _1_2,
  input  _0,
  input  _0_2,
  output Q,
  output Q_2
);

  wire and_1_out, and_2_out, and_3_out, and_4_out, transistor_1_out, transistor_2_out, transistor_4_out,
       transistor_6_out, transistor_7_out, transistor_8_out, transistor_9_out, transistor_12_out;

  Transistor #(.\type ("n")) transistor_1 (.in(transistor_2_out), .out(transistor_1_out), .gate(_1_2));
  Transistor #(.\type ("n")) transistor_2 (.in(1'b0), .out(transistor_2_out), .gate(_0_2));
  Transistor #(.\type ("n")) transistor_3 (.in(transistor_4_out), .out(transistor_1_out), .gate(_7));
  Transistor #(.\type ("n")) transistor_4 (.in(1'b0), .out(transistor_4_out), .gate(_6));
  Transistor #(.\type ("n")) transistor_5 (.in(transistor_6_out), .out(transistor_1_out), .gate(_5));
  Transistor #(.\type ("n")) transistor_6 (.in(1'b0), .out(transistor_6_out), .gate(_4));
  Transistor transistor_7 (.in(1'b1), .out(transistor_7_out), .gate(_1_2));
  Transistor transistor_8 (.in(transistor_7_out), .out(transistor_8_out), .gate(_7));
  Transistor transistor_9 (.in(transistor_8_out), .out(transistor_9_out), .gate(_5));
  Transistor transistor_10 (.in(transistor_9_out), .out(transistor_1_out), .gate(_3));
  Transistor #(.\type ("n")) transistor_11 (.in(transistor_12_out), .out(transistor_1_out), .gate(_3));
  Transistor #(.\type ("n")) transistor_12 (.in(1'b0), .out(transistor_12_out), .gate(_2));
  Transistor transistor_13 (.in(1'b1), .out(transistor_7_out), .gate(_0_2));
  Transistor transistor_14 (.in(transistor_7_out), .out(transistor_8_out), .gate(_6));
  Transistor transistor_15 (.in(transistor_8_out), .out(transistor_9_out), .gate(_4));
  Transistor transistor_16 (.in(transistor_9_out), .out(transistor_1_out), .gate(_2));
  Transistor transistor_17 (.in(1'b1), .out(Q_2), .gate(transistor_1_out));
  Transistor #(.\type ("n")) transistor_18 (.in(1'b0), .out(Q_2), .gate(transistor_1_out));
  and and_1 (and_1_out, _7_2, _6_2);
  and and_2 (and_2_out, _5_2, _4_2);
  and and_3 (and_3_out, _3_2, _2_2);
  and and_4 (and_4_out, _1, _0);
  or or_1 (Q, and_1_out, and_2_out, and_3_out, and_4_out);

  // Notes on the sheet:
  //   ~
  //   AON2222
endmodule

module SR_FF (
  input  A_SET,
  input  A,
  input  B_RESET,
  input  B,
  output nQ,
  output Q,
  output Q_2,
  output nQ_2
);

  wire transistor_1_out, transistor_2_out, transistor_5_out, transistor_6_out;

  Transistor #(.\type ("n")) transistor_1 (.in(1'b0), .out(transistor_1_out), .gate(A));
  Transistor transistor_2 (.in(1'b1), .out(transistor_2_out), .gate(transistor_5_out));
  Transistor transistor_3 (.in(transistor_2_out), .out(transistor_1_out), .gate(A));
  Transistor #(.\type ("n")) transistor_4 (.in(1'b0), .out(transistor_1_out), .gate(transistor_5_out));
  Transistor #(.\type ("n")) transistor_5 (.in(1'b0), .out(transistor_5_out), .gate(B));
  Transistor transistor_6 (.in(1'b1), .out(transistor_6_out), .gate(transistor_1_out));
  Transistor transistor_7 (.in(transistor_6_out), .out(transistor_5_out), .gate(B));
  Transistor #(.\type ("n")) transistor_8 (.in(1'b0), .out(transistor_5_out), .gate(transistor_1_out));
  Transistor transistor_9 (.in(1'b1), .out(nQ_2), .gate(transistor_5_out));
  Transistor #(.\type ("n")) transistor_10 (.in(1'b0), .out(nQ_2), .gate(transistor_5_out));
  Transistor transistor_11 (.in(1'b1), .out(Q), .gate(transistor_1_out));
  Transistor #(.\type ("n")) transistor_12 (.in(1'b0), .out(Q), .gate(transistor_1_out));
  nor nor_1 (nQ, A_SET, Q_2);
  nor nor_2 (Q_2, nQ, B_RESET);

  // Notes on the sheet:
  //   4
  //   1
  //   2
  //   3
  //   8
  //   5
  //   6
  //   7
  //   9
  //   10
  //   11
  //   12
  //   ~
endmodule

module HALF_SUM (
  input  A,
  input  B,
  input  B_2,
  input  A_2,
  output nS,
  output nS_2,
  output S,
  output S_2,
  output C,
  output C_2
);

  wire and_1_out, and_2_out, not_1_out, not_2_out, transistor_1_out, transistor_2_out, transistor_4_out,
       transistor_9_out, transistor_12_out;

  Transistor transistor_1 (.in(1'b1), .out(transistor_1_out), .gate(A_2));
  Transistor transistor_2 (.in(transistor_1_out), .out(transistor_2_out), .gate(B_2));
  Transistor #(.\type ("n")) transistor_3 (.in(transistor_4_out), .out(transistor_2_out), .gate(transistor_9_out));
  Transistor #(.\type ("n")) transistor_4 (.in(1'b0), .out(transistor_4_out), .gate(A_2));
  Transistor transistor_5 (.in(1'b1), .out(transistor_2_out), .gate(transistor_9_out));
  Transistor transistor_6 (.in(1'b1), .out(S_2), .gate(transistor_2_out));
  Transistor #(.\type ("n")) transistor_7 (.in(1'b0), .out(S_2), .gate(transistor_2_out));
  Transistor #(.\type ("n")) transistor_8 (.in(1'b0), .out(transistor_4_out), .gate(B_2));
  Transistor transistor_9 (.in(1'b1), .out(transistor_9_out), .gate(A_2));
  Transistor transistor_10 (.in(1'b1), .out(transistor_9_out), .gate(B_2));
  Transistor #(.\type ("n")) transistor_11 (.in(transistor_12_out), .out(transistor_9_out), .gate(B_2));
  Transistor #(.\type ("n")) transistor_12 (.in(1'b0), .out(transistor_12_out), .gate(A_2));
  Transistor transistor_13 (.in(1'b1), .out(nS), .gate(S_2));
  Transistor #(.\type ("n")) transistor_14 (.in(1'b0), .out(nS), .gate(S_2));
  Transistor transistor_15 (.in(1'b1), .out(C_2), .gate(transistor_9_out));
  Transistor #(.\type ("n")) transistor_16 (.in(1'b0), .out(C_2), .gate(transistor_9_out));
  not not_1 (not_1_out, B);
  and and_1 (and_1_out, not_1_out, A);
  and and_2 (and_2_out, B, not_2_out);
  not not_2 (not_2_out, A);
  and and_3 (C, B, A);
  or or_1 (S, and_1_out, and_2_out);
  not not_3 (nS_2, S);

  // Notes on the sheet:
  //   ~
  //   HA
endmodule

module CARRY_GEN (
  input  A,
  input  A_2,
  input  B,
  input  C,
  input  A_3,
  input  B_2,
  input  B_3,
  input  C_2,
  input  C_3,
  output X,
  output X_2,
  output X_3
);

  wire and_1_out, and_2_out, nor_1_out, nor_2_out, or_1_out, transistor_1_out, transistor_3_out,
       transistor_4_out, transistor_6_out, transistor_7_out, transistor_10_out;

  Transistor transistor_1 (.in(1'b1), .out(transistor_1_out), .gate(A_2));
  Transistor #(.\type ("n")) transistor_2 (.in(1'b0), .out(transistor_1_out), .gate(A_2));
  Transistor transistor_3 (.in(1'b1), .out(transistor_3_out), .gate(transistor_1_out));
  Transistor transistor_4 (.in(transistor_3_out), .out(transistor_4_out), .gate(B_3));
  Transistor #(.\type ("n")) transistor_5 (.in(transistor_6_out), .out(transistor_4_out), .gate(B_3));
  Transistor #(.\type ("n")) transistor_6 (.in(1'b0), .out(transistor_6_out), .gate(transistor_1_out));
  Transistor transistor_7 (.in(1'b1), .out(transistor_7_out), .gate(transistor_1_out));
  Transistor transistor_8 (.in(transistor_7_out), .out(transistor_4_out), .gate(C_3));
  Transistor #(.\type ("n")) transistor_9 (.in(transistor_10_out), .out(transistor_4_out), .gate(C_3));
  Transistor #(.\type ("n")) transistor_10 (.in(1'b0), .out(transistor_10_out), .gate(transistor_1_out));
  Transistor transistor_11 (.in(1'b1), .out(transistor_7_out), .gate(B_3));
  Transistor #(.\type ("n")) transistor_12 (.in(1'b0), .out(transistor_10_out), .gate(B_3));
  Transistor transistor_13 (.in(1'b1), .out(X), .gate(transistor_4_out));
  Transistor #(.\type ("n")) transistor_14 (.in(1'b0), .out(X), .gate(transistor_4_out));
  or or_1 (or_1_out, B, C);
  and and_1 (and_1_out, C, B);
  nor nor_1 (nor_1_out, B_2, C_2);
  and and_2 (and_2_out, B_2, C_2);
  Multiplexer #(.disabled(0), .enable("false")) multiplexer_1 (.in0(or_1_out), .in1(and_1_out), .out(X_2), .sel(A));
  nor nor_2 (nor_2_out, A_3, nor_1_out);
  or or_2 (X_3, nor_2_out, and_2_out);

  // Notes on the sheet:
  //   ~
endmodule

module DFF (
  input  nC2,
  input  nC1,
  input  nC1_2,
  input  C1,
  input  D,
  input  D_2,
  input  C1_2,
  input  C2,
  output Q,
  output Q_2,
  output nQ,
  output nQ_2
);

  wire transistor_1_out, transistor_2_out, transistor_4_out, transistor_5_out, transistor_7_out,
       transistor_10_out, transistor_11_out, transistor_14_out, transistor_15_out, transistor_18_out;

  Transistor transistor_1 (.in(1'b1), .out(transistor_1_out), .gate(D));
  Transistor #(.gate("br")) transistor_2 (.in(transistor_1_out), .out(transistor_2_out), .gate(nC1));
  Transistor #(.\type ("n"), .gate("br")) transistor_3 (.in(transistor_4_out), .out(transistor_2_out), .gate(C1_2));
  Transistor #(.\type ("n")) transistor_4 (.in(1'b0), .out(transistor_4_out), .gate(D));
  Transistor #(.gate("br")) transistor_5 (.in(1'b1), .out(transistor_5_out), .gate(transistor_7_out));
  Transistor transistor_6 (.in(transistor_5_out), .out(transistor_2_out), .gate(C1_2));
  Transistor transistor_7 (.in(1'b1), .out(transistor_7_out), .gate(transistor_2_out));
  Transistor #(.\type ("n")) transistor_8 (.in(1'b0), .out(transistor_7_out), .gate(transistor_2_out));
  Transistor #(.\type ("n")) transistor_9 (.in(transistor_10_out), .out(transistor_2_out), .gate(nC1));
  Transistor #(.\type ("n"), .gate("br")) transistor_10 (.in(1'b0), .out(transistor_10_out), .gate(transistor_7_out));
  Transistor transistor_11 (.in(1'b1), .out(transistor_11_out), .gate(transistor_7_out));
  Transistor #(.gate("br")) transistor_12 (.in(transistor_11_out), .out(nQ_2), .gate(nC2));
  Transistor #(.\type ("n"), .gate("br")) transistor_13 (.in(transistor_14_out), .out(nQ_2), .gate(C2));
  Transistor #(.\type ("n")) transistor_14 (.in(1'b0), .out(transistor_14_out), .gate(transistor_7_out));
  Transistor #(.gate("br")) transistor_15 (.in(1'b1), .out(transistor_15_out), .gate(Q_2));
  Transistor transistor_16 (.in(transistor_15_out), .out(nQ_2), .gate(C2));
  Transistor #(.\type ("n")) transistor_17 (.in(transistor_18_out), .out(nQ_2), .gate(nC2));
  Transistor #(.\type ("n"), .gate("br")) transistor_18 (.in(1'b0), .out(transistor_18_out), .gate(Q_2));
  Transistor transistor_19 (.in(1'b1), .out(Q_2), .gate(nQ_2));
  Transistor #(.\type ("n")) transistor_20 (.in(1'b0), .out(Q_2), .gate(nQ_2));
  D_Flip_Flop d_ff_1 (.clk(C1), .D(D_2), .Q(Q), .Qn(nQ));  // open: preset, en, reset

  // Notes on the sheet:
  //   ~
  //   COMPL
endmodule

module COUNTER_BIT (
  input  nC2,
  input  nC1,
  input  C2,
  input  C1,
  input  CARRY_IN,
  input  CARRY_IN_2,
  input  nEN,
  input  nEN_2,
  input  C1_2,
  input  C2_2,
  output Q,
  output Q_2,
  output nQ1,
  output CARRY_OUT,
  output nQ,
  output CARRY_OUT_2
);

  wire d_ff_1_qn, not_1_out, not_2_out, transistor_1_out, transistor_4_out, transistor_7_out,
       transistor_8_out, transistor_9_out, transistor_12_out, transistor_15_out, transistor_16_out,
       transistor_18_out, transistor_19_out, transistor_20_out, transistor_22_out, transistor_23_out,
       xor_1_out;

  Transistor transistor_1 (.in(1'b1), .out(transistor_1_out), .gate(CARRY_IN));
  Transistor #(.\type ("n")) transistor_2 (.in(1'b0), .out(transistor_1_out), .gate(CARRY_IN));
  Transistor #(.\type ("n")) transistor_3 (.in(1'b0), .out(CARRY_OUT_2), .gate(transistor_23_out));
  Transistor transistor_4 (.in(1'b1), .out(transistor_4_out), .gate(transistor_23_out));
  Transistor transistor_5 (.in(transistor_4_out), .out(CARRY_OUT_2), .gate(transistor_1_out));
  Transistor #(.\type ("n")) transistor_6 (.in(1'b0), .out(CARRY_OUT_2), .gate(transistor_1_out));
  Transistor #(.\type ("n")) transistor_7 (.in(transistor_8_out), .out(transistor_7_out), .gate(transistor_23_out));
  Transistor #(.\type ("n")) transistor_8 (.in(1'b0), .out(transistor_8_out), .gate(transistor_1_out));
  Transistor transistor_9 (.in(1'b1), .out(transistor_9_out), .gate(transistor_1_out));
  Transistor #(.\type ("n")) transistor_10 (.in(1'b0), .out(transistor_7_out), .gate(nEN_2));
  Transistor transistor_11 (.in(1'b1), .out(transistor_9_out), .gate(transistor_23_out));
  Transistor transistor_12 (.in(transistor_9_out), .out(transistor_12_out), .gate(nEN_2));
  Transistor transistor_13 (.in(transistor_12_out), .out(transistor_7_out), .gate(CARRY_OUT_2));
  Transistor #(.\type ("n")) transistor_14 (.in(1'b0), .out(transistor_7_out), .gate(CARRY_OUT_2));
  Transistor transistor_15 (.in(1'b1), .out(transistor_15_out), .gate(transistor_7_out));
  Transistor transistor_16 (.in(transistor_15_out), .out(transistor_16_out), .gate(nC1));
  Transistor #(.\type ("n")) transistor_17 (.in(transistor_18_out), .out(transistor_16_out), .gate(C1_2));
  Transistor #(.\type ("n")) transistor_18 (.in(1'b0), .out(transistor_18_out), .gate(transistor_7_out));
  Transistor transistor_19 (.in(1'b1), .out(transistor_19_out), .gate(transistor_16_out));
  Transistor transistor_20 (.in(transistor_19_out), .out(transistor_20_out), .gate(nC2));
  Transistor #(.\type ("n")) transistor_21 (.in(transistor_22_out), .out(transistor_20_out), .gate(C2_2));
  Transistor #(.\type ("n")) transistor_22 (.in(1'b0), .out(transistor_22_out), .gate(transistor_16_out));
  Transistor transistor_23 (.in(1'b1), .out(transistor_23_out), .gate(transistor_20_out));
  Transistor #(.\type ("n")) transistor_24 (.in(1'b0), .out(transistor_23_out), .gate(transistor_20_out));
  Transistor transistor_25 (.in(1'b1), .out(nQ), .gate(transistor_20_out));
  Transistor #(.\type ("n")) transistor_26 (.in(1'b0), .out(nQ), .gate(transistor_20_out));
  Transistor transistor_27 (.in(1'b1), .out(Q_2), .gate(nQ));
  Transistor #(.\type ("n")) transistor_28 (.in(1'b0), .out(Q_2), .gate(nQ));
  xor xor_1 (xor_1_out, CARRY_IN_2, nQ1);
  not not_1 (not_1_out, nEN);
  D_Flip_Flop #(.trigger("high")) d_ff_1 (
    .clk(C1), .D(xor_1_out), .Qn(d_ff_1_qn), .en(not_1_out));  // open: Q, preset, reset
  not not_2 (not_2_out, CARRY_IN_2);
  D_LATCH d_latch_1 (.EN(C2), .D(d_ff_1_qn), .Q(Q), .nQ(nQ1));
  nor nor_1 (CARRY_OUT, nQ1, not_2_out);

  // Notes on the sheet:
  //   1
  //   2
  //   5
  //   3
  //   4
  //   6
  //   10
  //   8
  //   7
  //   13
  //   9
  //   11
  //   12
  //   14
  //   16
  //   15
  //   17
  //   18
  //   20
  //   19
  //   21
  //   22
  //   23
  //   24
  //   25
  //   26
  //   27
  //   28
  //   ~
endmodule

module FULL_ADDER (
  input  A,
  input  B,
  input  C,
  input  C_2,
  input  A_2,
  input  B_2,
  output S,
  output S_2,
  output C_3,
  output C_4
);

  wire and_1_out, and_2_out, transistor_1_out, transistor_3_out, transistor_5_out, transistor_7_out,
       transistor_10_out, transistor_11_out, transistor_13_out, transistor_15_out, transistor_19_out,
       transistor_20_out, transistor_23_out, transistor_24_out, xor_1_out;

  Transistor #(.gate("br")) transistor_1 (.in(1'b1), .out(transistor_1_out), .gate(B_2));
  Transistor transistor_2 (.in(1'b1), .out(transistor_1_out), .gate(A_2));
  Transistor transistor_3 (.in(transistor_1_out), .out(transistor_3_out), .gate(C));
  Transistor #(.\type ("n")) transistor_4 (.in(transistor_5_out), .out(transistor_3_out), .gate(C));
  Transistor #(.\type ("n")) transistor_5 (.in(1'b0), .out(transistor_5_out), .gate(A_2));
  Transistor #(.\type ("n"), .gate("br")) transistor_6 (.in(1'b0), .out(transistor_5_out), .gate(B_2));
  Transistor transistor_7 (.in(1'b1), .out(transistor_7_out), .gate(B_2));
  Transistor transistor_8 (.in(transistor_7_out), .out(transistor_3_out), .gate(A_2));
  Transistor #(.\type ("n")) transistor_9 (.in(transistor_10_out), .out(transistor_3_out), .gate(A_2));
  Transistor #(.\type ("n")) transistor_10 (.in(1'b0), .out(transistor_10_out), .gate(B_2));
  Transistor transistor_11 (.in(1'b1), .out(transistor_11_out), .gate(C));
  Transistor #(.gate("br")) transistor_12 (.in(1'b1), .out(transistor_11_out), .gate(A_2));
  Transistor transistor_13 (.in(transistor_11_out), .out(transistor_13_out), .gate(transistor_3_out));
  Transistor #(.\type ("n")) transistor_14 (.in(transistor_15_out), .out(transistor_13_out), .gate(transistor_3_out));
  Transistor #(.\type ("n"), .gate("br")) transistor_15 (.in(1'b0), .out(transistor_15_out), .gate(A_2));
  Transistor #(.\type ("n")) transistor_16 (.in(1'b0), .out(transistor_15_out), .gate(C));
  Transistor #(.gate("br")) transistor_17 (.in(1'b1), .out(transistor_11_out), .gate(B_2));
  Transistor #(.\type ("n"), .gate("br")) transistor_18 (.in(1'b0), .out(transistor_15_out), .gate(B_2));
  Transistor transistor_19 (.in(1'b1), .out(transistor_19_out), .gate(B_2));
  Transistor transistor_20 (.in(transistor_19_out), .out(transistor_20_out), .gate(A_2));
  Transistor transistor_21 (.in(transistor_20_out), .out(transistor_13_out), .gate(C));
  Transistor #(.\type ("n")) transistor_22 (.in(transistor_23_out), .out(transistor_13_out), .gate(C));
  Transistor #(.\type ("n")) transistor_23 (.in(transistor_24_out), .out(transistor_23_out), .gate(A_2));
  Transistor #(.\type ("n")) transistor_24 (.in(1'b0), .out(transistor_24_out), .gate(B_2));
  Transistor transistor_25 (.in(1'b1), .out(S), .gate(transistor_13_out));
  Transistor #(.\type ("n")) transistor_26 (.in(1'b0), .out(S), .gate(transistor_13_out));
  Transistor transistor_27 (.in(1'b1), .out(C_4), .gate(transistor_3_out));
  Transistor #(.\type ("n")) transistor_28 (.in(1'b0), .out(C_4), .gate(transistor_3_out));
  xor xor_1 (xor_1_out, A, B);
  xor xor_2 (S_2, xor_1_out, C_2);
  and and_1 (and_1_out, xor_1_out, C_2);
  and and_2 (and_2_out, B, A);
  or or_1 (C_3, and_1_out, and_2_out);

  // Notes on the sheet:
  //   1
  //   2
  //   1
  //   2
  //   ~
endmodule

module AON22 (
  input  A,
  input  A_2,
  input  B,
  input  B_2,
  input  C,
  input  D,
  input  C_2,
  input  D_2,
  output Q,
  output Q_2
);

  wire and_1_out, and_2_out, transistor_1_out, transistor_2_out, transistor_4_out, transistor_8_out;

  Transistor transistor_1 (.in(1'b1), .out(transistor_1_out), .gate(A));
  Transistor transistor_2 (.in(transistor_1_out), .out(transistor_2_out), .gate(C_2));
  Transistor #(.\type ("n")) transistor_3 (.in(transistor_4_out), .out(transistor_2_out), .gate(B_2));
  Transistor #(.\type ("n")) transistor_4 (.in(1'b0), .out(transistor_4_out), .gate(A));
  Transistor transistor_5 (.in(1'b1), .out(transistor_1_out), .gate(B_2));
  Transistor transistor_6 (.in(transistor_1_out), .out(transistor_2_out), .gate(D_2));
  Transistor #(.\type ("n")) transistor_7 (.in(transistor_8_out), .out(transistor_2_out), .gate(C_2));
  Transistor #(.\type ("n")) transistor_8 (.in(1'b0), .out(transistor_8_out), .gate(D_2));
  Transistor transistor_9 (.in(1'b1), .out(Q), .gate(transistor_2_out));
  Transistor #(.\type ("n")) transistor_10 (.in(1'b0), .out(Q), .gate(transistor_2_out));
  and and_1 (and_1_out, A_2, B);
  and and_2 (and_2_out, C, D);
  or or_1 (Q_2, and_1_out, and_2_out);

  // Notes on the sheet:
  //   ~
endmodule

module CNT_SET_BIT (
  input  nC2,
  input  nC1,
  input  CLK,
  input  LOAD,
  input  IN1,
  input  STEP,
  input  CARRY_IN,
  input  CARRY_IN_2,
  input  RES,
  input  R,
  input  C1,
  input  C2,
  input  nLOAD,
  input  LOAD_2,
  input  VAL,
  output CARRY_OUT,
  output Q1,
  output nQ1,
  output CARRY_OUT_2,
  output Q,
  output nQ
);

  wire controlled_buffer_1_out, d_latch_1_nq, multiplexer_1_out, nor_1_out, not_1_out, transistor_1_out,
       transistor_4_out, transistor_7_out, transistor_8_out, transistor_9_out, transistor_11_out,
       transistor_12_out, transistor_13_out, transistor_16_out, transistor_17_out, transistor_19_out,
       transistor_22_out, transistor_25_out, transistor_26_out, transistor_28_out, transistor_29_out,
       transistor_32_out;

  Transistor transistor_1 (.in(1'b1), .out(transistor_1_out), .gate(CARRY_IN_2));
  Transistor #(.\type ("n")) transistor_2 (.in(1'b0), .out(transistor_1_out), .gate(CARRY_IN_2));
  Transistor #(.\type ("n")) transistor_3 (.in(1'b0), .out(CARRY_OUT), .gate(transistor_1_out));
  Transistor transistor_4 (.in(1'b1), .out(transistor_4_out), .gate(transistor_1_out));
  Transistor transistor_5 (.in(transistor_4_out), .out(CARRY_OUT), .gate(transistor_26_out));
  Transistor #(.\type ("n")) transistor_6 (.in(1'b0), .out(CARRY_OUT), .gate(transistor_26_out));
  Transistor transistor_7 (.in(1'b1), .out(transistor_7_out), .gate(transistor_1_out));
  Transistor transistor_8 (.in(transistor_7_out), .out(transistor_8_out), .gate(CARRY_OUT));
  Transistor transistor_9 (.in(transistor_8_out), .out(transistor_9_out), .gate(R));
  Transistor #(.\type ("n")) transistor_10 (.in(1'b0), .out(transistor_9_out), .gate(R));
  Transistor transistor_11 (.in(1'b1), .out(transistor_11_out), .gate(CARRY_OUT));
  Transistor #(.gate("br")) transistor_12 (.in(transistor_11_out), .out(transistor_12_out), .gate(transistor_26_out));
  Transistor transistor_13 (.in(transistor_12_out), .out(transistor_13_out), .gate(R));
  Transistor #(.\type ("n")) transistor_14 (.in(1'b0), .out(transistor_13_out), .gate(CARRY_OUT));
  Transistor #(.\type ("n")) transistor_15 (.in(transistor_16_out), .out(transistor_9_out), .gate(transistor_26_out));
  Transistor #(.\type ("n")) transistor_16 (.in(1'b0), .out(transistor_16_out), .gate(transistor_1_out));
  Transistor transistor_17 (.in(transistor_9_out), .out(transistor_17_out), .gate(nC1));
  Transistor #(.\type ("n"), .gate("br")) transistor_18 (.in(transistor_9_out), .out(transistor_17_out), .gate(C1));
  Transistor transistor_19 (.in(1'b1), .out(transistor_19_out), .gate(transistor_17_out));
  Transistor transistor_20 (.in(transistor_19_out), .out(nQ), .gate(nC2));
  Transistor #(.\type ("n")) transistor_21 (.in(transistor_22_out), .out(nQ), .gate(C2));
  Transistor #(.\type ("n")) transistor_22 (.in(1'b0), .out(transistor_22_out), .gate(transistor_17_out));
  Transistor transistor_23 (.in(1'b1), .out(Q), .gate(nQ));
  Transistor #(.\type ("n")) transistor_24 (.in(1'b0), .out(Q), .gate(nQ));
  Transistor transistor_25 (.in(1'b1), .out(transistor_25_out), .gate(Q));
  Transistor #(.gate("br")) transistor_26 (.in(transistor_25_out), .out(transistor_26_out), .gate(LOAD_2));
  Transistor #(.\type ("n"), .gate("br")) transistor_27 (.in(transistor_28_out), .out(transistor_26_out), .gate(nLOAD));
  Transistor #(.\type ("n")) transistor_28 (.in(1'b0), .out(transistor_28_out), .gate(Q));
  Transistor transistor_29 (.in(1'b1), .out(transistor_29_out), .gate(VAL));
  Transistor transistor_30 (.in(transistor_29_out), .out(transistor_26_out), .gate(nLOAD));
  Transistor #(.\type ("n")) transistor_31 (.in(transistor_32_out), .out(transistor_26_out), .gate(LOAD_2));
  Transistor #(.\type ("n")) transistor_32 (.in(1'b0), .out(transistor_32_out), .gate(VAL));
  Multiplexer #(.enable("false")) multiplexer_1 (.in0(nQ1), .in1(nor_1_out), .out(multiplexer_1_out), .sel(CARRY_IN));
  nor nor_1 (nor_1_out, nQ1, RES);
  D_LATCH d_latch_1 (.EN(CLK), .D(multiplexer_1_out), .nQ(d_latch_1_nq));  // open: Q
  assign controlled_buffer_1_out = CLK ? nor_1_out : 1'bz;  // Controlled_Buffer controlled_buffer_1
  assign controlled_buffer_1_out = LOAD ? IN1 : 1'bz;  // Controlled_Buffer controlled_buffer_2
  assign controlled_buffer_1_out = STEP ? d_latch_1_nq : 1'bz;  // Controlled_Buffer controlled_buffer_3
  not not_1 (not_1_out, CARRY_IN);
  D_LATCH d_latch_2 (.EN(1'b1), .D(controlled_buffer_1_out), .Q(Q1), .nQ(nQ1));
  nor nor_2 (CARRY_OUT_2, nQ1, not_1_out);

  // Notes on the sheet:
  //   ~
endmodule

module CLKGEN (
  input  IN,
  input  IN_2,
  input  IN_3,
  output CLK1,
  output nCLK1,
  output CLK2,
  output nCLK2,
  output nCLK1_2,
  output nCLK2_2,
  output CLK1_2,
  output CLK2_2,
  output nCLK1_3,
  output CLK1_3,
  output nCLK2_3,
  output CLK2_3
);

  wire nand_3_out, nand_4_out, not_1_out, not_2_out, not_3_out, not_4_out, not_8_out, not_10_out, not_11_out,
       not_12_out, not_13_out, not_15_out, not_16_out, not_18_out, not_19_out, transistor_1_out,
       transistor_3_out, transistor_5_out, transistor_8_out, transistor_9_out, transistor_11_out,
       transistor_30_out, transistor_32_out, transistor_34_out, transistor_36_out, transistor_39_out,
       transistor_40_out, transistor_42_out, transistor_61_out, transistor_63_out, transistor_65_out;

  Transistor transistor_1 (.in(1'b1), .out(transistor_1_out), .gate(IN));
  Transistor #(.\type ("n")) transistor_2 (.in(1'b0), .out(transistor_1_out), .gate(IN));
  Transistor transistor_3 (.in(1'b1), .out(transistor_3_out), .gate(transistor_1_out));
  Transistor #(.\type ("n")) transistor_4 (.in(1'b0), .out(transistor_3_out), .gate(transistor_1_out));
  not not_1 (not_1_out, IN_2);
  not not_2 (not_2_out, IN_3);
  Transistor transistor_5 (.in(1'b1), .out(transistor_5_out), .gate(transistor_65_out));
  not not_3 (not_3_out, not_1_out);
  nand nand_1 (nCLK1_3, IN_3, CLK2_3);
  nand nand_2 (CLK2_3, nCLK1_3, not_2_out);
  Transistor transistor_6 (.in(1'b1), .out(transistor_5_out), .gate(transistor_1_out));
  Transistor #(.\type ("n")) transistor_7 (.in(transistor_8_out), .out(transistor_5_out), .gate(transistor_1_out));
  Transistor #(.\type ("n")) transistor_8 (.in(1'b0), .out(transistor_8_out), .gate(transistor_65_out));
  not not_4 (not_4_out, nand_3_out);
  nand nand_3 (nand_3_out, not_1_out, not_18_out);
  not not_5 (CLK1_3, nCLK1_3);
  not not_6 (nCLK2_3, CLK2_3);
  Transistor transistor_9 (.in(1'b1), .out(transistor_9_out), .gate(transistor_5_out));
  Transistor #(.\type ("n")) transistor_10 (.in(1'b0), .out(transistor_9_out), .gate(transistor_5_out));
  Transistor transistor_11 (.in(1'b1), .out(transistor_11_out), .gate(transistor_9_out));
  Transistor #(.\type ("n")) transistor_12 (.in(1'b0), .out(transistor_11_out), .gate(transistor_9_out));
  not not_7 (nCLK1_2, not_4_out);
  not not_8 (not_8_out, not_4_out);
  not not_9 (CLK1_2, not_8_out);
  not not_10 (not_10_out, not_11_out);
  not not_11 (not_11_out, not_4_out);
  Transistor transistor_13 (.in(1'b1), .out(CLK1), .gate(transistor_11_out));
  Transistor #(.\type ("n")) transistor_14 (.in(1'b0), .out(CLK1), .gate(transistor_11_out));
  not not_12 (not_12_out, not_10_out);
  Transistor transistor_15 (.in(1'b1), .out(CLK1), .gate(transistor_11_out));
  Transistor #(.\type ("n")) transistor_16 (.in(1'b0), .out(CLK1), .gate(transistor_11_out));
  Transistor transistor_17 (.in(1'b1), .out(CLK1), .gate(transistor_11_out));
  Transistor #(.\type ("n")) transistor_18 (.in(1'b0), .out(CLK1), .gate(transistor_11_out));
  nand nand_4 (nand_4_out, not_3_out, not_12_out);
  Transistor transistor_19 (.in(1'b1), .out(CLK1), .gate(transistor_11_out));
  Transistor #(.\type ("n")) transistor_20 (.in(1'b0), .out(CLK1), .gate(transistor_11_out));
  not not_13 (not_13_out, nand_4_out);
  not not_14 (nCLK2_2, not_13_out);
  not not_15 (not_15_out, not_13_out);
  not not_16 (not_16_out, not_13_out);
  Transistor transistor_21 (.in(1'b1), .out(nCLK1), .gate(transistor_9_out));
  Transistor #(.\type ("n")) transistor_22 (.in(1'b0), .out(nCLK1), .gate(transistor_9_out));
  not not_17 (CLK2_2, not_15_out);
  not not_18 (not_18_out, not_19_out);
  not not_19 (not_19_out, not_16_out);
  Transistor transistor_23 (.in(1'b1), .out(nCLK1), .gate(transistor_9_out));
  Transistor transistor_24 (.in(1'b1), .out(nCLK1), .gate(transistor_9_out));
  Transistor #(.\type ("n")) transistor_25 (.in(1'b0), .out(nCLK1), .gate(transistor_9_out));
  Transistor transistor_26 (.in(1'b1), .out(nCLK1), .gate(transistor_9_out));
  Transistor transistor_27 (.in(1'b1), .out(nCLK1), .gate(transistor_9_out));
  Transistor transistor_28 (.in(1'b1), .out(nCLK1), .gate(transistor_9_out));
  Transistor #(.\type ("n")) transistor_29 (.in(1'b0), .out(nCLK1), .gate(transistor_9_out));
  Transistor transistor_30 (.in(1'b1), .out(transistor_30_out), .gate(transistor_9_out));
  Transistor #(.\type ("n")) transistor_31 (.in(1'b0), .out(transistor_30_out), .gate(transistor_9_out));
  Transistor transistor_32 (.in(1'b1), .out(transistor_32_out), .gate(transistor_30_out));
  Transistor #(.\type ("n")) transistor_33 (.in(1'b0), .out(transistor_32_out), .gate(transistor_30_out));
  Transistor transistor_34 (.in(1'b1), .out(transistor_34_out), .gate(transistor_32_out));
  Transistor #(.\type ("n")) transistor_35 (.in(1'b0), .out(transistor_34_out), .gate(transistor_32_out));
  Transistor transistor_36 (.in(1'b1), .out(transistor_36_out), .gate(transistor_34_out));
  Transistor transistor_37 (.in(1'b1), .out(transistor_36_out), .gate(transistor_3_out));
  Transistor #(.\type ("n")) transistor_38 (.in(transistor_39_out), .out(transistor_36_out), .gate(transistor_3_out));
  Transistor #(.\type ("n")) transistor_39 (.in(1'b0), .out(transistor_39_out), .gate(transistor_34_out));
  Transistor transistor_40 (.in(1'b1), .out(transistor_40_out), .gate(transistor_36_out));
  Transistor #(.\type ("n")) transistor_41 (.in(1'b0), .out(transistor_40_out), .gate(transistor_36_out));
  Transistor transistor_42 (.in(1'b1), .out(transistor_42_out), .gate(transistor_40_out));
  Transistor #(.\type ("n")) transistor_43 (.in(1'b0), .out(transistor_42_out), .gate(transistor_40_out));
  Transistor transistor_44 (.in(1'b1), .out(CLK2), .gate(transistor_42_out));
  Transistor #(.\type ("n")) transistor_45 (.in(1'b0), .out(CLK2), .gate(transistor_42_out));
  Transistor transistor_46 (.in(1'b1), .out(CLK2), .gate(transistor_42_out));
  Transistor #(.\type ("n")) transistor_47 (.in(1'b0), .out(CLK2), .gate(transistor_42_out));
  Transistor transistor_48 (.in(1'b1), .out(CLK2), .gate(transistor_42_out));
  Transistor #(.\type ("n")) transistor_49 (.in(1'b0), .out(CLK2), .gate(transistor_42_out));
  Transistor transistor_50 (.in(1'b1), .out(CLK2), .gate(transistor_42_out));
  Transistor #(.\type ("n")) transistor_51 (.in(1'b0), .out(CLK2), .gate(transistor_42_out));
  Transistor transistor_52 (.in(1'b1), .out(nCLK2), .gate(transistor_40_out));
  Transistor #(.\type ("n")) transistor_53 (.in(1'b0), .out(nCLK2), .gate(transistor_40_out));
  Transistor transistor_54 (.in(1'b1), .out(nCLK2), .gate(transistor_40_out));
  Transistor transistor_55 (.in(1'b1), .out(nCLK2), .gate(transistor_40_out));
  Transistor #(.\type ("n")) transistor_56 (.in(1'b0), .out(nCLK2), .gate(transistor_40_out));
  Transistor transistor_57 (.in(1'b1), .out(nCLK2), .gate(transistor_40_out));
  Transistor transistor_58 (.in(1'b1), .out(nCLK2), .gate(transistor_40_out));
  Transistor transistor_59 (.in(1'b1), .out(nCLK2), .gate(transistor_40_out));
  Transistor #(.\type ("n")) transistor_60 (.in(1'b0), .out(nCLK2), .gate(transistor_40_out));
  Transistor transistor_61 (.in(1'b1), .out(transistor_61_out), .gate(transistor_40_out));
  Transistor #(.\type ("n")) transistor_62 (.in(1'b0), .out(transistor_61_out), .gate(transistor_40_out));
  Transistor transistor_63 (.in(1'b1), .out(transistor_63_out), .gate(transistor_61_out));
  Transistor #(.\type ("n")) transistor_64 (.in(1'b0), .out(transistor_63_out), .gate(transistor_61_out));
  Transistor transistor_65 (.in(1'b1), .out(transistor_65_out), .gate(transistor_63_out));
  Transistor #(.\type ("n")) transistor_66 (.in(1'b0), .out(transistor_65_out), .gate(transistor_63_out));

  // Notes on the sheet:
  //   x4
  //   x4
endmodule
