// Logisim project PSG.circ as structural Verilog: 7 circuits, main circuit main
module main (
  input  PSG_CLK,
  input  PSG_TEST_OE,
  input  nPSG_WRITE,
  input  SYSRES,
  input  [15:0] DB,
  input  TEST9,
  input  TEST10,
  input  TEST11,
  output D0,
  output D1,
  output D2,
  output D3,
  output D4,
  output D5,
  output D6,
  output D7,
  output D8,
  output D9,
  output D10,
  output D11,
  output D12,
  output D13,
  output D14,
  output D15,
  output DAC0_ATT1,
  output DAC0_ATT2,
  output MUTE_DAC0,
  output [7:0] DAC0,
  output DAC1_ATT1,
  output DAC1_ATT2,
  output MUTE_DAC1,
  output [7:0] DAC1,
  output DAC2_ATT1,
  output DAC2_ATT2,
  output MUTE_DAC2,
  output [7:0] DAC2,
  output DAC3_ATT1,
  output DAC3_ATT2,
  output MUTE_DAC3,
  output [7:0] DAC3
);

  wire _2015_out, _2016_out, _2017_out, _2018_out, _2039_out, _2040_out, _2042_out, _2043_2_out, _2043_out,
       _2044_out, _2045_out, _2046_out, _2047_out, _2048_out, _2049_out, _2050_out, _2051_q, _2052_q,
       _2053_q, _2054_q, _2055_q, _2056_q, _2057_q, _2058_q, _2059_q, _2060_q, _2061_q, _2062_q, _2063_q,
       _2064_q, _2065_q, _2066_q, _2067_q, _2068_q, _2069_q, _2070_q, _2071_q, _2072_q, _2073_q, _2074_q,
       _2075_q, _2076_q, _2077_q, _2078_q, _2079_q, _2080_q, _2081_q, _2088_q, _2091_q, _2094_q, _2097_q,
       _2098_out, _2100_q, _2103_q, _2106_q, _2109_q, _2110_out, _2112_q, _2115_q, _2118_q, _2121_q,
       _2122_out, _2124_q, _2127_q, _2130_q, _2133_q, _2134_out, _2136_out, _2137_out, _2138_out, _2139_q,
       _2140_q, _2141_2_out, _2141_q, _2142_out, _2143_out, _2144_out, _2146_nq, _2147_out, _2148_out,
       _2149_out, _2150_out, _2155_out, _2156_q, _2157_q, _2158_q, _2159_q, _2160_q, _2161_q, _2162_q,
       _2163_q, _2164_q, _2165_q, _2166_q, _2167_q, _2168_q, _2169_q, _2170_q, _2171_q, _2172_q, _2173_q,
       _2174_q, _2175_q, _2176_q, _2177_q, _2178_q, _2179_q, _2180_q, _2181_q, _2182_q, _2183_q, _2184_q,
       _2185_q, _2186_q, _2187_q, _2188_q, _2189_q, _2190_q, _2191_q, _2192_q, _2193_q, _2194_q, _2195_q,
       _2196_2_out, _2196_3_out, _2196_4_out, _2196_5_out, _2196_out, _2197_out_4, _2198_2_out, _2198_3_out,
       _2198_4_out, _2198_5_out, _2198_out, _2199_out_4, _2200_2_out, _2200_3_out, _2200_4_out, _2200_5_out,
       _2200_out, _2201_out_4, _2202_2_out, _2202_3_out, _2202_4_out, _2202_5_out, _2202_out, _2203_out_4,
       _2204_2_out, _2204_3_out, _2204_4_out, _2204_5_out, _2204_out, _2205_out_4, _2206_2_out, _2206_3_out,
       _2206_4_out, _2206_5_out, _2206_out, _2207_out_4, _2208_2_out, _2208_3_out, _2208_4_out, _2208_5_out,
       _2208_out, _2209_out_4, _2210_2_out, _2210_3_out, _2210_4_out, _2210_5_out, _2210_out, _2211_out_4,
       _2212_2_out, _2212_3_out, _2212_4_out, _2212_5_out, _2212_out, _2213_out_4, _2214_2_out, _2214_3_out,
       _2214_4_out, _2214_5_out, _2214_out, _2215_out_4, _2217_q, _2218_out, _2220_q, _2221_out, _2223_q,
       _2224_out, _2226_q, _2227_out, _2228_q, _2229_q, _2230_q, _2231_q, _2232_q, _2233_out, _2234_out,
       _2235_out, _2236_out, _2237_out, _2238_out, _2239_out, _2240_out, _2241_out, _2242_q, _2243_q,
       _2244_q, _2245_q, _2246_q, _2247_q, _2248_q, _2249_q, _2250_q, _2251_q, _2252_q, _2253_q, _2254_q,
       _2255_q, _2256_q, _2257_q, _2258_out, _2259_out, _2261_out, _2263_out, _2265_out, _2267_out,
       _2269_out, _2271_out, _2273_out, _2275_out, _2277_out, _2279_out, _2281_out, _2283_out, _2285_out,
       _2286_q, _2287_out, _2288_q, _2291_out, _2292_out, _2293_q, _2295_out, _2296_q, _2298_out, _2299_q,
       _2301_out, _2302_q, _2304_out, _2306_q, _2307_out, _2308_out, _2310_q, _2311_out, _2313_q, _2314_out,
       _2315_2_out, _2315_3_out, _2315_4_out, _2315_out, _2317_out, _2320_out, _2321_2_out, _2321_out,
       _2323_out, _2324_out, _2325_out, _2326_out, _2327_out, _2328_out, _2329_out, _2330_2_out, _2330_out,
       _2332_out, _2333_2_out, _2333_out, _2335_out, _2336_out, _2337_out, _2338_2_out, _2338_out, _2341_out,
       _2342_2_out, _2342_out, _2345_2_out, _2345_out, _2351_out, _2352_out, _2353_out, _2354_out, _2356_q,
       _2358_out, _2361_out, _2362_q, _2367_out, _2372_out, _2373_out, _2374_out, _2375_out, _2376_out,
       _2377_out, _2378_out, _2379_out, _2380_q, _2381_q, _2382_out, _2383_q, _2384_q, _2385_q, adder_1_cout,
       adder_1_out, adder_2_cout, adder_2_out, adder_3_cout, adder_3_out, adder_4_cout, adder_4_out,
       adder_5_cout, adder_5_out, adder_6_cout, adder_6_out, adder_7_cout, adder_7_out, adder_8_cout,
       adder_8_out, adder_9_cout, adder_9_out, adder_10_cout, adder_10_out, CLK1, CLK2, CLK3, CLK4,
       cnt_bit_1_q, decoder_1_out0, decoder_1_out1, decoder_1_out2, decoder_1_out3, decoder_2_out0,
       decoder_2_out1, decoder_2_out2, decoder_2_out3, decoder_2_out4, decoder_2_out5, decoder_2_out6,
       decoder_2_out7, decoder_3_out0, decoder_3_out1, decoder_3_out2, decoder_3_out3, G_2290, LATCH0,
       LATCH1, LATCH2, LATCH3, LATCH4, LATCH4_star, LATCH5, LATCH6, LATCH7, LATCH8, LATCH9, LATCH10,
       multiplexer_1_out, nCLK1, nCLK2, nCLK3, nCLK4, not_5_out, undriven, undriven_2, undriven_3,
       undriven_4, undriven_5, undriven_6, undriven_7, undriven_8, undriven_9, undriven_10, undriven_11,
       undriven_12;
  wire [1:0] _2083_q;
  wire [2:0] _2089_out, _2101_out, _2113_out, _2125_out, _2280_q, _2294_q;
  wire [3:0] _2216_out, _2303_out;

  Clock clock_1 ();  // open: out
  S_LATCH _2288 (.EN(nPSG_WRITE), .D(DB[7]), .Q(_2288_q));  // open: nQ
  S_LATCH _2293 (.EN(nPSG_WRITE), .D(DB[6]), .Q(_2293_q));  // open: nQ
  or _125 (_2303_out[3], _2307_out, _2311_out);
  S_LATCH _2313 (.EN(nPSG_WRITE), .D(DB[0]), .Q(_2313_q));  // open: nQ
  or _2309 (_2303_out[2], _2307_out, _2308_out);
  S_LATCH _2310 (.EN(nPSG_WRITE), .D(DB[1]), .Q(_2310_q));  // open: nQ
  or _2305 (_2303_out[1], _2307_out, _2304_out);
  S_LATCH _2306 (.EN(nPSG_WRITE), .D(DB[2]), .Q(_2306_q));  // open: nQ
  or _2303 (_2303_out[0], _2307_out, _2301_out);
  S_LATCH _2302 (.EN(nPSG_WRITE), .D(DB[3]), .Q(_2302_q));  // open: nQ
  S_LATCH _2299 (.EN(nPSG_WRITE), .D(DB[4]), .Q(_2299_q));  // open: nQ
  S_LATCH _2296 (.EN(nPSG_WRITE), .D(DB[5]), .Q(_2296_q));  // open: nQ
  not _2307 (_2307_out, _2238_out);
  and _2290 (G_2290, _2288_q, _2238_out);
  and _2292 (_2292_out, _2293_q, _2238_out);
  and _2311 (_2311_out, _2313_q, _2238_out);
  and _2308 (_2308_out, _2310_q, _2238_out);
  and _2304 (_2304_out, _2306_q, _2238_out);
  and _2301 (_2301_out, _2302_q, _2238_out);
  and _2298 (_2298_out, _2299_q, _2238_out);
  and _2295 (_2295_out, _2296_q, _2238_out);
  not _2238 (_2238_out, _2228_q);
  and _2291 (_2291_out, _2383_q, G_2290);
  not _2043 (_2043_out, _2291_out);
  not _2043_2 (_2043_2_out, _2043_out);
  S_LATCH _2294 (.EN(_2043_2_out), .D(_2292_out), .Q(_2294_q[0]));  // open: nQ
  S_LATCH _2297 (.EN(_2043_2_out), .D(_2295_out), .Q(_2294_q[1]));  // open: nQ
  S_LATCH _2300 (.EN(_2043_2_out), .D(_2298_out), .Q(_2294_q[2]));  // open: nQ
  S_LATCH _2081 (.EN(LATCH4), .D(_2304_out), .Q(_2081_q));  // open: nQ
  S_LATCH _2082 (.EN(LATCH4), .D(_2308_out), .Q(_2083_q[1]));  // open: nQ
  S_LATCH _2083 (.EN(LATCH4), .D(_2311_out), .Q(_2083_q[0]));  // open: nQ
  S_LATCH _2072 (.EN(LATCH10), .D(_2311_out), .Q(_2072_q));  // open: nQ
  S_LATCH _2070 (.EN(LATCH9), .D(_2311_out), .Q(_2070_q));  // open: nQ
  S_LATCH _2069 (.EN(LATCH8), .D(_2311_out), .Q(_2069_q));  // open: nQ
  S_LATCH _2074 (.EN(LATCH10), .D(_2308_out), .Q(_2074_q));  // open: nQ
  S_LATCH _2075 (.EN(LATCH9), .D(_2308_out), .Q(_2075_q));  // open: nQ
  S_LATCH _2071 (.EN(LATCH8), .D(_2308_out), .Q(_2071_q));  // open: nQ
  S_LATCH _2077 (.EN(LATCH10), .D(_2304_out), .Q(_2077_q));  // open: nQ
  S_LATCH _2078 (.EN(LATCH9), .D(_2304_out), .Q(_2078_q));  // open: nQ
  S_LATCH _2073 (.EN(LATCH8), .D(_2304_out), .Q(_2073_q));  // open: nQ
  S_LATCH _2079 (.EN(LATCH10), .D(_2301_out), .Q(_2079_q));  // open: nQ
  S_LATCH _2080 (.EN(LATCH9), .D(_2301_out), .Q(_2080_q));  // open: nQ
  S_LATCH _2076 (.EN(LATCH8), .D(_2301_out), .Q(_2076_q));  // open: nQ
  S_LATCH _2054 (.EN(LATCH7), .D(_2311_out), .Q(_2054_q));  // open: nQ
  S_LATCH _2052 (.EN(LATCH6), .D(_2311_out), .Q(_2052_q));  // open: nQ
  S_LATCH _2051 (.EN(LATCH5), .D(_2311_out), .Q(_2051_q));  // open: nQ
  S_LATCH _2056 (.EN(LATCH7), .D(_2308_out), .Q(_2056_q));  // open: nQ
  S_LATCH _2057 (.EN(LATCH6), .D(_2308_out), .Q(_2057_q));  // open: nQ
  S_LATCH _2053 (.EN(LATCH5), .D(_2308_out), .Q(_2053_q));  // open: nQ
  S_LATCH _2059 (.EN(LATCH7), .D(_2304_out), .Q(_2059_q));  // open: nQ
  S_LATCH _2060 (.EN(LATCH6), .D(_2304_out), .Q(_2060_q));  // open: nQ
  S_LATCH _2055 (.EN(LATCH5), .D(_2304_out), .Q(_2055_q));  // open: nQ
  S_LATCH _2062 (.EN(LATCH7), .D(_2301_out), .Q(_2062_q));  // open: nQ
  S_LATCH _2063 (.EN(LATCH6), .D(_2301_out), .Q(_2063_q));  // open: nQ
  S_LATCH _2058 (.EN(LATCH5), .D(_2301_out), .Q(_2058_q));  // open: nQ
  S_LATCH _2064 (.EN(LATCH7), .D(_2298_out), .Q(_2064_q));  // open: nQ
  S_LATCH _2065 (.EN(LATCH6), .D(_2298_out), .Q(_2065_q));  // open: nQ
  S_LATCH _2061 (.EN(LATCH5), .D(_2298_out), .Q(_2061_q));  // open: nQ
  S_LATCH _2067 (.EN(LATCH7), .D(_2295_out), .Q(_2067_q));  // open: nQ
  S_LATCH _2068 (.EN(LATCH6), .D(_2295_out), .Q(_2068_q));  // open: nQ
  S_LATCH _2066 (.EN(LATCH5), .D(_2295_out), .Q(_2066_q));  // open: nQ
  Decoder #(.select(2), .disabled(0), .enable("false")) decoder_1 (
    .out0(decoder_1_out0), .out1(decoder_1_out1), .out2(decoder_1_out2), .out3(decoder_1_out3), .sel(_2083_q));
  and _2214 (_2214_out, 1'b0, _2216_out[0]);
  and _2214_2 (_2214_2_out, _2072_q, _2216_out[1]);
  and _2214_3 (_2214_3_out, _2070_q, _2216_out[2]);
  and _2214_4 (_2214_4_out, _2069_q, _2216_out[3]);
  and _2212 (_2212_out, 1'b0, _2216_out[0]);
  and _2212_2 (_2212_2_out, _2074_q, _2216_out[1]);
  and _2212_3 (_2212_3_out, _2075_q, _2216_out[2]);
  and _2212_4 (_2212_4_out, _2071_q, _2216_out[3]);
  and _2210 (_2210_out, 1'b0, _2216_out[0]);
  and _2210_2 (_2210_2_out, _2077_q, _2216_out[1]);
  and _2210_3 (_2210_3_out, _2078_q, _2216_out[2]);
  and _2210_4 (_2210_4_out, _2073_q, _2216_out[3]);
  and _2208 (_2208_out, 1'b0, _2216_out[0]);
  and _2208_2 (_2208_2_out, _2079_q, _2216_out[1]);
  and _2208_3 (_2208_3_out, _2080_q, _2216_out[2]);
  and _2208_4 (_2208_4_out, _2076_q, _2216_out[3]);
  and _2206 (_2206_out, decoder_1_out0, _2216_out[0]);
  and _2206_2 (_2206_2_out, _2054_q, _2216_out[1]);
  and _2206_3 (_2206_3_out, _2052_q, _2216_out[2]);
  and _2206_4 (_2206_4_out, _2051_q, _2216_out[3]);
  and _2204 (_2204_out, decoder_1_out1, _2216_out[0]);
  and _2204_2 (_2204_2_out, _2056_q, _2216_out[1]);
  and _2204_3 (_2204_3_out, _2057_q, _2216_out[2]);
  and _2204_4 (_2204_4_out, _2053_q, _2216_out[3]);
  and _2202 (_2202_out, decoder_1_out2, _2216_out[0]);
  and _2202_2 (_2202_2_out, _2059_q, _2216_out[1]);
  and _2202_3 (_2202_3_out, _2060_q, _2216_out[2]);
  and _2202_4 (_2202_4_out, _2055_q, _2216_out[3]);
  and _2200 (_2200_out, 1'b0, _2216_out[0]);
  and _2200_2 (_2200_2_out, _2062_q, _2216_out[1]);
  and _2200_3 (_2200_3_out, _2063_q, _2216_out[2]);
  and _2200_4 (_2200_4_out, _2058_q, _2216_out[3]);
  and _2198 (_2198_out, 1'b0, _2216_out[0]);
  and _2198_2 (_2198_2_out, _2064_q, _2216_out[1]);
  and _2198_3 (_2198_3_out, _2065_q, _2216_out[2]);
  and _2198_4 (_2198_4_out, _2061_q, _2216_out[3]);
  and _2196 (_2196_out, 1'b0, _2216_out[0]);
  and _2196_2 (_2196_2_out, _2067_q, _2216_out[1]);
  and _2196_3 (_2196_3_out, _2068_q, _2216_out[2]);
  and _2196_4 (_2196_4_out, _2066_q, _2216_out[3]);
  or _2214_5 (_2214_5_out, _2214_out, _2214_2_out, _2214_3_out, _2214_4_out);
  or _2212_5 (_2212_5_out, _2212_out, _2212_2_out, _2212_3_out, _2212_4_out);
  or _2210_5 (_2210_5_out, _2210_out, _2210_2_out, _2210_3_out, _2210_4_out);
  or _2208_5 (_2208_5_out, _2208_out, _2208_2_out, _2208_3_out, _2208_4_out);
  or _2206_5 (_2206_5_out, _2206_out, _2206_2_out, _2206_3_out, _2206_4_out);
  or _2204_5 (_2204_5_out, _2204_out, _2204_2_out, _2204_3_out, _2204_4_out);
  or _2202_5 (_2202_5_out, _2202_out, _2202_2_out, _2202_3_out, _2202_4_out);
  or _2200_5 (_2200_5_out, _2200_out, _2200_2_out, _2200_3_out, _2200_4_out);
  or _2198_5 (_2198_5_out, _2198_out, _2198_2_out, _2198_3_out, _2198_4_out);
  or _2196_5 (_2196_5_out, _2196_out, _2196_2_out, _2196_3_out, _2196_4_out);
  CGI2A _2215 (.A(_2214_5_out), .B(1'b1), .C(_2192_q), .out_4(_2215_out_4));
  CGI2A _2213 (.A(_2212_5_out), .B(_2215_out_4), .C(_2188_q), .out_4(_2213_out_4));
  CGI2A _2211 (.A(_2210_5_out), .B(_2213_out_4), .C(_2184_q), .out_4(_2211_out_4));
  CGI2A _2209 (.A(_2208_5_out), .B(_2211_out_4), .C(_2180_q), .out_4(_2209_out_4));
  CGI2A _2207 (.A(_2206_5_out), .B(_2209_out_4), .C(_2176_q), .out_4(_2207_out_4));
  CGI2A _2205 (.A(_2204_5_out), .B(_2207_out_4), .C(_2172_q), .out_4(_2205_out_4));
  CGI2A _2203 (.A(_2202_5_out), .B(_2205_out_4), .C(_2168_q), .out_4(_2203_out_4));
  CGI2A _2201 (.A(_2200_5_out), .B(_2203_out_4), .C(_2164_q), .out_4(_2201_out_4));
  CGI2A _2199 (.A(_2198_5_out), .B(_2201_out_4), .C(_2160_q), .out_4(_2199_out_4));
  CGI2A _2197 (.A(_2196_5_out), .B(_2199_out_4), .C(_2156_q), .out_4(_2197_out_4));
  not _2137 (_2137_out, PSG_CLK);
  not _2138 (_2138_out, _2137_out);
  nor _2287 (_2287_out, _2228_q, _2197_out_4);
  nand _2138_2 (CLK1, _2137_out, CLK2);
  nand _2138_3 (CLK2, CLK1, _2138_out);
  and _2259 (_2259_out, _2287_out, _2192_q);
  and _2261 (_2261_out, _2287_out, _2188_q);
  and _2263 (_2263_out, _2287_out, _2184_q);
  and _2265 (_2265_out, _2287_out, _2180_q);
  and _2267 (_2267_out, _2287_out, _2176_q);
  and _2269 (_2269_out, _2287_out, _2172_q);
  and _2271 (_2271_out, _2287_out, _2168_q);
  and _2273 (_2273_out, _2287_out, _2164_q);
  and _2275 (_2275_out, _2287_out, _2160_q);
  and _2277 (_2277_out, _2287_out, _2156_q);
  Adder #(.width(1)) adder_1 (.a(1'b1), .b(_2259_out), .out(adder_1_out), .cin(1'b0), .cout(adder_1_cout));
  Adder #(.width(1)) adder_2 (.a(adder_1_cout), .b(_2261_out), .out(adder_2_out), .cin(1'b0), .cout(adder_2_cout));
  Adder #(.width(1)) adder_3 (.a(adder_2_cout), .b(_2263_out), .out(adder_3_out), .cin(1'b0), .cout(adder_3_cout));
  Adder #(.width(1)) adder_4 (.a(adder_3_cout), .b(_2265_out), .out(adder_4_out), .cin(1'b0), .cout(adder_4_cout));
  Adder #(.width(1)) adder_5 (.a(adder_4_cout), .b(_2267_out), .out(adder_5_out), .cin(1'b0), .cout(adder_5_cout));
  Adder #(.width(1)) adder_6 (.a(adder_5_cout), .b(_2269_out), .out(adder_6_out), .cin(1'b0), .cout(adder_6_cout));
  Adder #(.width(1)) adder_7 (.a(adder_6_cout), .b(_2271_out), .out(adder_7_out), .cin(1'b0), .cout(adder_7_cout));
  Adder #(.width(1)) adder_8 (.a(adder_7_cout), .b(_2273_out), .out(adder_8_out), .cin(1'b0), .cout(adder_8_cout));
  Adder #(.width(1)) adder_9 (.a(adder_8_cout), .b(_2275_out), .out(adder_9_out), .cin(1'b0), .cout(adder_9_cout));
  Adder #(.width(1)) adder_10 (.a(adder_9_cout), .b(_2277_out), .out(adder_10_out), .cin(1'b0), .cout(adder_10_cout));
  not _2138_4 (nCLK1, CLK1);
  not _2138_5 (nCLK2, CLK2);
  SR_BIT _2226 (.C2(CLK4), .C1(CLK3), .D(_2234_out), .Q(_2226_q));  // open: nQ
  SR_BIT _2223 (.C2(CLK4), .C1(CLK3), .D(_2226_q), .Q(_2223_q));  // open: nQ
  SR_BIT _2220 (.C2(CLK4), .C1(CLK3), .D(_2223_q), .Q(_2220_q));  // open: nQ
  SR_BIT _2217 (.C2(CLK4), .C1(CLK3), .D(_2220_q), .Q(_2217_q));  // open: nQ
  SR_BIT _2228 (.C2(CLK4), .C1(CLK3), .D(_2376_out), .Q(_2228_q));  // open: nQ
  SR_BIT _2195 (.C2(CLK3), .C1(CLK4), .D(adder_1_out), .Q(_2195_q));  // open: nQ
  SR_BIT _2191 (.C2(CLK3), .C1(CLK4), .D(adder_2_out), .Q(_2191_q));  // open: nQ
  SR_BIT _2187 (.C2(CLK3), .C1(CLK4), .D(adder_3_out), .Q(_2187_q));  // open: nQ
  SR_BIT _2183 (.C2(CLK3), .C1(CLK4), .D(adder_4_out), .Q(_2183_q));  // open: nQ
  SR_BIT _2179 (.C2(CLK3), .C1(CLK4), .D(adder_5_out), .Q(_2179_q));  // open: nQ
  SR_BIT _2175 (.C2(CLK3), .C1(CLK4), .D(adder_6_out), .Q(_2175_q));  // open: nQ
  SR_BIT _2171 (.C2(CLK3), .C1(CLK4), .D(adder_7_out), .Q(_2171_q));  // open: nQ
  SR_BIT _2167 (.C2(CLK3), .C1(CLK4), .D(adder_8_out), .Q(_2167_q));  // open: nQ
  SR_BIT _2163 (.C2(CLK3), .C1(CLK4), .D(adder_9_out), .Q(_2163_q));  // open: nQ
  SR_BIT _2159 (.C2(CLK3), .C1(CLK4), .D(adder_10_out), .Q(_2159_q));  // open: nQ
  S_R_Flip_Flop _2381 (.S(_2383_q), .R(nPSG_WRITE), .Q(_2381_q), .preset(_2383_q));  // open: clk, Qn, reset, en
  D_Flip_Flop _2384 (.clk(CLK4), .D(SYSRES), .Q(_2384_q));  // open: Qn, preset, en, reset
  not _2361 (_2361_out, _2384_q);
  nor _2234 (_2234_out, _2376_out, _2220_q, _2223_q, _2226_q);
  S_R_Flip_Flop _2380 (.S(LATCH4_star), .clk(1'b1), .R(_2385_q), .Q(_2380_q));  // open: Qn, preset, reset, en
  nor _2382 (_2382_out, _2381_q, nPSG_WRITE);
  not _2376 (_2376_out, _2361_out);
  not _2233 (_2233_out, _2228_q);
  SR_BIT _2356 (.C2(CLK4), .C1(CLK3), .D(multiplexer_1_out), .Q(_2356_q));  // open: nQ
  SR_BIT _2194 (.C2(CLK3), .C1(CLK4), .D(_2195_q), .Q(_2194_q));  // open: nQ
  SR_BIT _2190 (.C2(CLK3), .C1(CLK4), .D(_2191_q), .Q(_2190_q));  // open: nQ
  SR_BIT _2186 (.C2(CLK3), .C1(CLK4), .D(_2187_q), .Q(_2186_q));  // open: nQ
  SR_BIT _2182 (.C2(CLK3), .C1(CLK4), .D(_2183_q), .Q(_2182_q));  // open: nQ
  SR_BIT _2178 (.C2(CLK3), .C1(CLK4), .D(_2179_q), .Q(_2178_q));  // open: nQ
  SR_BIT _2174 (.C2(CLK3), .C1(CLK4), .D(_2175_q), .Q(_2174_q));  // open: nQ
  SR_BIT _2170 (.C2(CLK3), .C1(CLK4), .D(_2171_q), .Q(_2170_q));  // open: nQ
  SR_BIT _2166 (.C2(CLK3), .C1(CLK4), .D(_2167_q), .Q(_2166_q));  // open: nQ
  SR_BIT _2162 (.C2(CLK3), .C1(CLK4), .D(_2163_q), .Q(_2162_q));  // open: nQ
  SR_BIT _2158 (.C2(CLK3), .C1(CLK4), .D(_2159_q), .Q(_2158_q));  // open: nQ
  D_Flip_Flop _2139 (.clk(CLK2), .D(SYSRES), .Q(_2139_q));  // open: Qn, preset, en, reset
  D_Flip_Flop _2383 (.clk(CLK2), .D(_2382_out), .Q(_2383_q));  // open: Qn, preset, en, reset
  not _2225 (_2216_out[3], _2227_out);
  nand _2227 (_2227_out, _2226_q, _2233_out);
  nand _2224 (_2224_out, _2223_q, _2233_out);
  not _2222 (_2216_out[2], _2224_out);
  not _2219 (_2216_out[1], _2221_out);
  nand _2221 (_2221_out, _2220_q, _2233_out);
  not _2216 (_2216_out[0], _2218_out);
  nand _2218 (_2218_out, _2217_q, _2233_out);
  D_Flip_Flop _2385 (.clk(CLK4), .D(_2380_q), .Q(_2385_q));  // open: Qn, preset, en, reset
  not _2358 (_2358_out, _2356_q);
  SR_BIT _2140 (.C2(CLK2), .C1(CLK1), .D(_2139_q), .Q(_2140_q));  // open: nQ
  and _2367 (_2367_out, multiplexer_1_out, _2358_out);
  SR_BIT _2193 (.C2(CLK3), .C1(CLK4), .D(_2194_q), .Q(_2193_q));  // open: nQ
  SR_BIT _2189 (.C2(CLK3), .C1(CLK4), .D(_2190_q), .Q(_2189_q));  // open: nQ
  SR_BIT _2185 (.C2(CLK3), .C1(CLK4), .D(_2186_q), .Q(_2185_q));  // open: nQ
  SR_BIT _2181 (.C2(CLK3), .C1(CLK4), .D(_2182_q), .Q(_2181_q));  // open: nQ
  SR_BIT _2177 (.C2(CLK3), .C1(CLK4), .D(_2178_q), .Q(_2177_q));  // open: nQ
  SR_BIT _2173 (.C2(CLK3), .C1(CLK4), .D(_2174_q), .Q(_2173_q));  // open: nQ
  SR_BIT _2169 (.C2(CLK3), .C1(CLK4), .D(_2170_q), .Q(_2169_q));  // open: nQ
  SR_BIT _2165 (.C2(CLK3), .C1(CLK4), .D(_2166_q), .Q(_2165_q));  // open: nQ
  SR_BIT _2161 (.C2(CLK3), .C1(CLK4), .D(_2162_q), .Q(_2161_q));  // open: nQ
  SR_BIT _2157 (.C2(CLK3), .C1(CLK4), .D(_2158_q), .Q(_2157_q));  // open: nQ
  not _2142 (_2142_out, _2140_q);
  nor _2379 (_2379_out, _2376_out, _2385_q);
  not _2373 (_2373_out, _2367_out);
  SR_BIT _2141 (.C2(CLK2), .C1(CLK1), .D(_2144_out), .Q(_2141_q));  // open: nQ
  nor _2144 (_2144_out, _2141_q, _2143_out);
  and _2143 (_2143_out, _2142_out, _2139_q);
  SR_BIT _2362 (.C2(CLK2), .C1(CLK1), .D(_2383_q), .Q(_2362_q));  // open: nQ
  SR_BIT _2229 (.C2(CLK4), .C1(CLK3), .D(_2230_q), .Q(_2229_q));  // open: nQ
  SR_BIT _2230 (.C2(CLK4), .C1(CLK3), .D(_2231_q), .Q(_2230_q));  // open: nQ
  SR_BIT _2231 (.C2(CLK4), .C1(CLK3), .D(_2232_q), .Q(_2231_q));  // open: nQ
  SR_BIT _2232 (.C2(CLK4), .C1(CLK3), .D(_2197_out_4), .Q(_2232_q));  // open: nQ
  nand _2378 (_2378_out, _2367_out, _2379_out);
  nand _2377 (_2377_out, _2379_out, _2373_out);
  SR_BIT _2192 (.C2(CLK3), .C1(CLK4), .D(_2193_q), .Q(_2192_q));  // open: nQ
  SR_BIT _2188 (.C2(CLK3), .C1(CLK4), .D(_2189_q), .Q(_2188_q));  // open: nQ
  SR_BIT _2184 (.C2(CLK3), .C1(CLK4), .D(_2185_q), .Q(_2184_q));  // open: nQ
  SR_BIT _2180 (.C2(CLK3), .C1(CLK4), .D(_2181_q), .Q(_2180_q));  // open: nQ
  SR_BIT _2176 (.C2(CLK3), .C1(CLK4), .D(_2177_q), .Q(_2176_q));  // open: nQ
  SR_BIT _2172 (.C2(CLK3), .C1(CLK4), .D(_2173_q), .Q(_2172_q));  // open: nQ
  SR_BIT _2168 (.C2(CLK3), .C1(CLK4), .D(_2169_q), .Q(_2168_q));  // open: nQ
  SR_BIT _2164 (.C2(CLK3), .C1(CLK4), .D(_2165_q), .Q(_2164_q));  // open: nQ
  SR_BIT _2160 (.C2(CLK3), .C1(CLK4), .D(_2161_q), .Q(_2160_q));  // open: nQ
  SR_BIT _2156 (.C2(CLK3), .C1(CLK4), .D(_2157_q), .Q(_2156_q));  // open: nQ
  not _2375 (_2375_out, _2378_out);
  not _2374 (_2374_out, _2377_out);
  and _2279 (_2279_out, _2226_q, _2229_q);
  and _2281 (_2281_out, _2226_q, _2230_q);
  and _2283 (_2283_out, _2226_q, _2231_q);
  and _2285 (_2285_out, _2226_q, _2232_q);
  CNT_BIT cnt_bit_1 (.C1(CLK1), .C2(CLK2), .R(_2143_out), .CI(_2141_q), .Q(cnt_bit_1_q));  // open: CO
  CNT_BIT _2280 (.C1(CLK3), .C2(CLK4), .R(_2228_q), .CI(_2279_out), .Q(_2280_q[0]));  // open: CO
  CNT_BIT _2282 (.C1(CLK3), .C2(CLK4), .R(_2228_q), .CI(_2281_out), .Q(_2280_q[1]));  // open: CO
  CNT_BIT _2284 (.C1(CLK3), .C2(CLK4), .R(_2228_q), .CI(_2283_out), .Q(_2280_q[2]));  // open: CO
  CNT_BIT _2286 (.C1(CLK3), .C2(CLK4), .R(_2228_q), .CI(_2285_out), .Q(_2286_q));  // open: CO
  LFSR_BIT _2242 (.C1(CLK3), .C2(CLK4), .A(_2241_out), .B(_2374_out), .C(_2375_out), .Q(_2242_q));
  LFSR_BIT _2243 (.C1(CLK3), .C2(CLK4), .A(_2242_q), .B(_2374_out), .C(_2375_out), .Q(_2243_q));
  LFSR_BIT _2244 (.C1(CLK3), .C2(CLK4), .A(_2243_q), .B(_2374_out), .C(_2375_out), .Q(_2244_q));
  LFSR_BIT _2245 (.C1(CLK3), .C2(CLK4), .A(_2244_q), .B(_2374_out), .C(_2375_out), .Q(_2245_q));
  LFSR_BIT _2246 (.C1(CLK3), .C2(CLK4), .A(_2245_q), .B(_2374_out), .C(_2375_out), .Q(_2246_q));
  LFSR_BIT _2247 (.C1(CLK3), .C2(CLK4), .A(_2246_q), .B(_2374_out), .C(_2375_out), .Q(_2247_q));
  LFSR_BIT _2248 (.C1(CLK3), .C2(CLK4), .A(_2247_q), .B(_2374_out), .C(_2375_out), .Q(_2248_q));
  LFSR_BIT _2249 (.C1(CLK3), .C2(CLK4), .A(_2248_q), .B(_2374_out), .C(_2375_out), .Q(_2249_q));
  LFSR_BIT _2250 (.C1(CLK3), .C2(CLK4), .A(_2249_q), .B(_2374_out), .C(_2375_out), .Q(_2250_q));
  LFSR_BIT _2251 (.C1(CLK3), .C2(CLK4), .A(_2250_q), .B(_2374_out), .C(_2375_out), .Q(_2251_q));
  LFSR_BIT _2252 (.C1(CLK3), .C2(CLK4), .A(_2251_q), .B(_2374_out), .C(_2375_out), .Q(_2252_q));
  LFSR_BIT _2253 (.C1(CLK3), .C2(CLK4), .A(_2252_q), .B(_2374_out), .C(_2375_out), .Q(_2253_q));
  LFSR_BIT _2254 (.C1(CLK3), .C2(CLK4), .A(_2253_q), .B(_2374_out), .C(_2375_out), .Q(_2254_q));
  LFSR_BIT _2255 (.C1(CLK3), .C2(CLK4), .A(_2254_q), .B(_2374_out), .C(_2375_out), .Q(_2255_q));
  LFSR_BIT _2256 (.C1(CLK3), .C2(CLK4), .A(_2255_q), .B(_2374_out), .C(_2375_out), .Q(_2256_q));
  LFSR_BIT _2257 (.C1(CLK3), .C2(CLK4), .A(_2256_q), .B(_2374_out), .C(_2375_out), .Q(_2257_q));
  Multiplexer #(.disabled(0), .enable("false")) multiplexer_1 (
    .in0(_2286_q), .in1(_2280_q[2]), .out(multiplexer_1_out), .sel(decoder_1_out3));
  D_LATCH _2146 (.EN(CLK1), .D(cnt_bit_1_q), .nQ(_2146_nq));  // open: Q
  not _2147 (_2147_out, _2146_nq);
  nand _2241 (_2241_out, _2240_out, _2239_out);
  nor _2236 (_2236_out, _2242_q, _2243_q, _2244_q, _2245_q);
  nor _2237 (_2237_out, _2246_q, _2247_q, _2248_q);
  nor _2235 (_2235_out, _2249_q, _2250_q, _2251_q, _2252_q);
  nor _2372 (_2372_out, _2253_q, _2254_q, _2255_q, _2256_q);
  nand _2155 (_2155_out, _2141_q, _2147_out);
  not _2150 (_2150_out, _2155_out);
  nand _2148 (_2148_out, _2146_nq, _2141_q);
  not _2149 (_2149_out, _2148_out);
  nand _2240 (_2240_out, _2081_q, _2258_out);
  nand _2239 (_2239_out, _2236_out, _2237_out, _2235_out, _2372_out);
  xor _2258 (_2258_out, _2254_q, _2257_q);
  not _2154 (CLK4, _2155_out);
  not _2153 (nCLK4, _2150_out);
  not _2151 (CLK3, _2148_out);
  not _2152 (nCLK3, _2149_out);
  Decoder #(.select(3), .disabled(0), .enable("false")) decoder_2 (
    .out0(decoder_2_out0), .out1(decoder_2_out1), .out2(decoder_2_out2), .out3(decoder_2_out3),
    .out4(decoder_2_out4), .out5(decoder_2_out5), .out6(decoder_2_out6), .out7(decoder_2_out7), .sel(_2294_q));
  S_LATCH _2088 (.EN(LATCH0), .D(_2303_out[0]), .Q(_2088_q));  // open: nQ
  S_LATCH _2091 (.EN(LATCH0), .D(_2303_out[1]), .Q(_2091_q));  // open: nQ
  S_LATCH _2094 (.EN(LATCH0), .D(_2303_out[2]), .Q(_2094_q));  // open: nQ
  S_LATCH _2097 (.EN(LATCH0), .D(_2303_out[3]), .Q(_2097_q));  // open: nQ
  S_LATCH _2100 (.EN(LATCH1), .D(_2303_out[0]), .Q(_2100_q));  // open: nQ
  S_LATCH _2103 (.EN(LATCH1), .D(_2303_out[1]), .Q(_2103_q));  // open: nQ
  S_LATCH _2106 (.EN(LATCH1), .D(_2303_out[2]), .Q(_2106_q));  // open: nQ
  S_LATCH _2109 (.EN(LATCH1), .D(_2303_out[3]), .Q(_2109_q));  // open: nQ
  S_LATCH _2112 (.EN(LATCH2), .D(_2303_out[0]), .Q(_2112_q));  // open: nQ
  S_LATCH _2115 (.EN(LATCH2), .D(_2303_out[1]), .Q(_2115_q));  // open: nQ
  S_LATCH _2118 (.EN(LATCH2), .D(_2303_out[2]), .Q(_2118_q));  // open: nQ
  S_LATCH _2121 (.EN(LATCH2), .D(_2303_out[3]), .Q(_2121_q));  // open: nQ
  S_LATCH _2124 (.EN(LATCH3), .D(_2303_out[0]), .Q(_2124_q));  // open: nQ
  S_LATCH _2127 (.EN(LATCH3), .D(_2303_out[1]), .Q(_2127_q));  // open: nQ
  S_LATCH _2130 (.EN(LATCH3), .D(_2303_out[2]), .Q(_2130_q));  // open: nQ
  S_LATCH _2133 (.EN(LATCH3), .D(_2303_out[3]), .Q(_2133_q));  // open: nQ
  and _2321 (_2321_out, decoder_2_out0, _2362_q);
  and _2330 (_2330_out, decoder_2_out1, _2362_q);
  and _2338 (_2338_out, decoder_2_out2, _2362_q);
  and _2345 (_2345_out, decoder_2_out3, _2362_q);
  and _2342 (_2342_out, decoder_2_out4, _2362_q);
  and _2333 (_2333_out, decoder_2_out5, _2362_q);
  and _2315 (_2315_out, decoder_2_out6, _2362_q);
  and _2315_2 (_2315_2_out, decoder_2_out7, _2362_q);
  nor _2354 (_2354_out, _2280_q[0], TEST9);
  nor _2353 (_2353_out, _2280_q[1], TEST9);
  nor _2352 (_2352_out, _2280_q[2], TEST9);
  nor _2351 (_2351_out, _2256_q, TEST9);
  Decoder #(.select(2), .disabled(0)) decoder_3 (
    .out0(decoder_3_out0), .out1(decoder_3_out1), .out2(decoder_3_out2), .out3(decoder_3_out3),
    .sel({TEST11, TEST10}), .en(TEST9));
  not _2323 (_2323_out, G_2290);
  or _2324 (_2324_out, G_2290, _2376_out);
  not _2320 (_2320_out, _2321_2_out);
  nor _2321_2 (_2321_2_out, _2321_out, _2376_out);
  nor _2330_2 (_2330_2_out, _2330_out, _2376_out);
  not _2329 (_2329_out, _2330_2_out);
  not _2337 (_2337_out, _2338_2_out);
  nor _2338_2 (_2338_2_out, _2338_out, _2376_out);
  not _2344 (LATCH4_star, _2345_2_out);
  nor _2345_2 (_2345_2_out, _2345_out, _2376_out);
  nor _2342_2 (_2342_2_out, _2342_out, _2376_out);
  not _2341 (_2341_out, _2342_2_out);
  nor _2333_2 (_2333_2_out, _2333_out, _2376_out);
  not _2332 (_2332_out, _2333_2_out);
  not _2317 (_2317_out, _2315_3_out);
  nor _2315_3 (_2315_3_out, _2315_out, _2376_out);
  nor _2315_4 (_2315_4_out, _2315_2_out, _2376_out);
  not _2314 (_2314_out, _2315_4_out);
  or _2089 (_2089_out[0], _2088_q, _2354_out);
  or _2092 (_2089_out[1], _2091_q, _2354_out);
  or _2095 (_2089_out[2], _2094_q, _2354_out);
  or _2098 (_2098_out, _2097_q, _2354_out);
  or _2101 (_2101_out[0], _2100_q, _2353_out);
  or _2104 (_2101_out[1], _2103_q, _2353_out);
  or _2107 (_2101_out[2], _2106_q, _2353_out);
  or _2110 (_2110_out, _2109_q, _2353_out);
  or _2113 (_2113_out[0], _2112_q, _2352_out);
  or _2116 (_2113_out[1], _2115_q, _2352_out);
  or _2119 (_2113_out[2], _2118_q, _2352_out);
  or _2122 (_2122_out, _2121_q, _2352_out);
  or _2125 (_2125_out[0], _2124_q, _2351_out);
  or _2128 (_2125_out[1], _2127_q, _2351_out);
  or _2131 (_2125_out[2], _2130_q, _2351_out);
  or _2134 (_2134_out, _2133_q, _2351_out);
  not \not  (MUTE_DAC0, decoder_3_out0);
  not not_2 (MUTE_DAC1, decoder_3_out1);
  not not_3 (MUTE_DAC2, decoder_3_out2);
  not not_4 (MUTE_DAC3, decoder_3_out3);
  and _2326 (_2326_out, _2323_out, _2320_out);
  and _2325 (_2325_out, _2324_out, _2320_out);
  and _2328 (_2328_out, _2323_out, _2329_out);
  and _2327 (_2327_out, _2324_out, _2329_out);
  and _2336 (_2336_out, _2323_out, _2337_out);
  and _2335 (_2335_out, _2324_out, _2337_out);
  not _2048 (_2048_out, _2326_out);
  not _2045 (_2045_out, _2325_out);
  not _2049 (_2049_out, _2328_out);
  not _2046 (_2046_out, _2327_out);
  not _2050 (_2050_out, _2336_out);
  not _2047 (_2047_out, _2335_out);
  not _2044 (_2044_out, LATCH4_star);
  not _2039 (_2039_out, _2341_out);
  not _2040 (_2040_out, _2332_out);
  not _2141_2 (_2141_2_out, _2317_out);
  not _2042 (_2042_out, _2314_out);
  not _2048_2 (LATCH7, _2048_out);
  not _2045_2 (LATCH10, _2045_out);
  not _2049_2 (LATCH6, _2049_out);
  not _2046_2 (LATCH9, _2046_out);
  not _2050_2 (LATCH5, _2050_out);
  not _2047_2 (LATCH8, _2047_out);
  not _2044_2 (LATCH4, _2044_out);
  not _2039_2 (LATCH0, _2039_out);
  not _2040_2 (LATCH1, _2040_out);
  not _2141_3 (LATCH2, _2141_2_out);
  not _2042_2 (LATCH3, _2042_out);
  not _2136 (_2136_out, PSG_TEST_OE);
  not _2015 (_2015_out, MUTE_DAC0);
  not _2016 (_2016_out, MUTE_DAC1);
  not _2017 (_2017_out, MUTE_DAC2);
  not _2018 (_2018_out, MUTE_DAC3);
  not not_5 (not_5_out, _2136_out);
  assign D0 = not_5_out ? ~_2089_out[0] : 1'bz;  // Controlled_Inverter controlled_inverter_1
  assign D1 = undriven ? ~_2089_out[1] : 1'bz;  // Controlled_Inverter controlled_inverter_2
  assign D2 = undriven_2 ? ~_2089_out[2] : 1'bz;  // Controlled_Inverter controlled_inverter_3
  assign D3 = undriven_3 ? ~_2098_out : 1'bz;  // Controlled_Inverter controlled_inverter_4
  assign D4 = undriven_4 ? ~_2101_out[0] : 1'bz;  // Controlled_Inverter controlled_inverter_5
  assign D5 = undriven_5 ? ~_2101_out[1] : 1'bz;  // Controlled_Inverter controlled_inverter_6
  assign D6 = undriven_6 ? ~_2101_out[2] : 1'bz;  // Controlled_Inverter controlled_inverter_7
  assign D7 = undriven_7 ? ~_2110_out : 1'bz;  // Controlled_Inverter controlled_inverter_8
  assign D8 = undriven_8 ? ~_2113_out[0] : 1'bz;  // Controlled_Inverter controlled_inverter_9
  assign D9 = undriven_9 ? ~_2113_out[1] : 1'bz;  // Controlled_Inverter controlled_inverter_10
  assign D10 = undriven_10 ? ~_2113_out[2] : 1'bz;  // Controlled_Inverter controlled_inverter_11
  assign D11 = undriven_11 ? ~_2122_out : 1'bz;  // Controlled_Inverter controlled_inverter_12
  assign D12 = undriven_12 ? ~_2125_out[0] : 1'bz;  // Controlled_Inverter controlled_inverter_13
  assign D13 = undriven_12 ? ~_2125_out[1] : 1'bz;  // Controlled_Inverter controlled_inverter_14
  assign D14 = undriven_12 ? ~_2125_out[2] : 1'bz;  // Controlled_Inverter controlled_inverter_15
  assign D15 = undriven_12 ? ~_2134_out : 1'bz;  // Controlled_Inverter controlled_inverter_16
  nand _2020 (DAC0_ATT1, _2134_out, _2015_out);
  nand _2021 (DAC0_ATT2, DAC0_ATT1, _2015_out);
  Decoder #(.select(3), .disabled(0), .enable("false")) decoder_4 (
    .out0(DAC0[0]), .out1(DAC0[1]), .out2(DAC0[2]), .out3(DAC0[3]), .out4(DAC0[4]), .out5(DAC0[5]),
    .out6(DAC0[6]), .out7(DAC0[7]), .sel(_2125_out));
  nand _2022 (DAC1_ATT1, _2122_out, _2016_out);
  nand _2021_2 (DAC1_ATT2, DAC1_ATT1, _2016_out);
  Decoder #(.select(3), .disabled(0), .enable("false")) decoder_5 (
    .out0(DAC1[0]), .out1(DAC1[1]), .out2(DAC1[2]), .out3(DAC1[3]), .out4(DAC1[4]), .out5(DAC1[5]),
    .out6(DAC1[6]), .out7(DAC1[7]), .sel(_2113_out));
  nand _2029 (DAC2_ATT1, _2110_out, _2017_out);
  nand _2033 (DAC2_ATT2, DAC2_ATT1, _2017_out);
  Decoder #(.select(3), .disabled(0), .enable("false")) decoder_6 (
    .out0(DAC2[0]), .out1(DAC2[1]), .out2(DAC2[2]), .out3(DAC2[3]), .out4(DAC2[4]), .out5(DAC2[5]),
    .out6(DAC2[6]), .out7(DAC2[7]), .sel(_2101_out));
  nand _2034 (DAC3_ATT1, _2098_out, _2018_out);
  nand _2038 (DAC3_ATT2, DAC3_ATT1, _2018_out);
  Decoder #(.select(3), .disabled(0), .enable("false")) decoder_7 (
    .out0(DAC3[0]), .out1(DAC3[1]), .out2(DAC3[2]), .out3(DAC3[3]), .out4(DAC3[4]), .out5(DAC3[5]),
    .out6(DAC3[6]), .out7(DAC3[7]), .sel(_2089_out));

  // Other names for the same wires on the sheet: nPSG_WR = nPSG_WRITE

  // Notes on the sheet:
  //   Not used
  //   LATCH11
  //   2084 - 2087,2346 - 2347
  //   CLKGEN
  //   2260
  //   2262
  //   2264
  //   2266
  //   2268
  //   2270
  //   2272
  //   2274
  //   2276
  //   2278
  //   not used
  //   DFF
  //   complementary clock
  //   complementary clock
  //   DFF
  //   DFF
  //   DFF
  //   CLOCK DIVIDER
  //   2355,2357
  //   RNDOUT
  //   C2
  //   C1
  //   2316,2319
  //   2322,2331
  //   2334,2339
  //   2340,2343
  //   2348 - 2350
  //   complementary clock
  //   complementary clock
  //   CLK1
  //   CLK2
  //   CLK3
  //   CLK4
  //   TEST9
  //   2359,2360
  //   2364 - 2366
  //   2368 - 2371
  //   AOI21
  //   AOI21
  //   AOI21
  //   AOI21
  //   AOI21
  //   AOI21
  //   AOI21
  //   AOI21
  //   2007 - 2014,2026 - 2028
  //   1999 - 2006,2023 - 2025
  //   1991 - 1998,2030 - 2032
  //   1983 - 1990,2035 - 2037
  //   2090
  //   2093
  //   2096
  //   2099
  //   2102
  //   2105
  //   2108
  //   2111
  //   2114
  //   2117
  //   2120
  //   2123
  //   2126
  //   2129
  //   2132
  //   2135
endmodule

module D_LATCH (
  input  EN,
  input  D,
  output Q,
  output nQ
);

  D_Flip_Flop #(.trigger("high")) d_ff_1 (.clk(EN), .D(D), .Q(Q), .Qn(nQ));  // open: preset, en, reset
endmodule

module CGI2A (
  input  A,
  input  B,
  input  C,
  output out_4
);

  wire and_1_out, nor_1_out, nor_2_out;

  nor nor_1 (nor_1_out, B, C);
  and and_1 (and_1_out, B, C);
  nor nor_2 (nor_2_out, A, nor_1_out);
  or or_1 (out_4, nor_2_out, and_1_out);

  // Notes on the sheet:
  //   CGI2A
endmodule

// SR BIT
module SR_BIT (
  input  C2,
  input  C1,
  input  D,
  output Q,
  output nQ
);

  wire d_latch_1_q;

  D_LATCH d_latch_1 (.EN(C1), .D(D), .Q(d_latch_1_q));  // open: nQ
  D_LATCH d_latch_2 (.EN(C2), .D(d_latch_1_q), .Q(Q), .nQ(nQ));
endmodule

module S_LATCH (
  input  EN,
  input  D,
  output Q,
  output nQ
);

  D_Flip_Flop #(.trigger("high")) d_ff_1 (.clk(EN), .D(D), .Q(Q), .Qn(nQ));  // open: preset, en, reset
endmodule

// LFSR BIT
module LFSR_BIT (
  input  C1,
  input  C2,
  input  A,
  input  B,
  input  C,
  output Q
);

  wire and_1_out, and_2_out, d_latch_1_nq, or_1_out;

  and and_1 (and_1_out, A, B);
  and and_2 (and_2_out, C, Q);
  or or_1 (or_1_out, and_1_out, and_2_out);
  D_LATCH d_latch_1 (.EN(C1), .D(or_1_out), .nQ(d_latch_1_nq));  // open: Q
  D_LATCH d_latch_2 (.EN(C2), .D(d_latch_1_nq), .nQ(Q));  // open: Q
endmodule

// COUNTER 1 BIT
module CNT_BIT (
  input  C1,
  input  C2,
  input  R,
  input  CI,
  output Q,
  output CO
);

  wire and_1_out, not_1_out, not_2_out, sr_bit_1_nq, xor_1_out;

  not not_1 (not_1_out, R);
  not not_2 (not_2_out, CI);
  xor xor_1 (xor_1_out, not_2_out, sr_bit_1_nq);
  and and_1 (and_1_out, not_1_out, xor_1_out);
  SR_BIT sr_bit_1 (.C2(C2), .C1(C1), .D(and_1_out), .Q(Q), .nQ(sr_bit_1_nq));
  nor nor_1 (CO, sr_bit_1_nq, not_2_out);
endmodule
