// Logisim project TestDACEnable.circ as structural Verilog: 1 circuit, main circuit main
module main (
  input  Test9,
  input  Test10,
  input  Test11,
  output n_Chan3_Enable,
  output n_Chan2_Enable,
  output n_Chan0_Enable,
  output n_Chan1_Enable
);

  wire nand_1_out, nand_2_out, nand_3_out, nand_4_out, not_1_out, not_2_out;

  not not_1 (not_1_out, Test10);
  not not_2 (not_2_out, Test11);
  nand nand_1 (nand_1_out, Test10, Test11);
  nand nand_2 (nand_2_out, not_1_out, Test11);
  nand nand_3 (nand_3_out, not_1_out, not_2_out);
  nand nand_4 (nand_4_out, not_2_out, Test10);
  and and_1 (n_Chan3_Enable, Test9, nand_1_out);
  and and_2 (n_Chan2_Enable, Test9, nand_2_out);
  and and_3 (n_Chan0_Enable, Test9, nand_3_out);
  and and_4 (n_Chan1_Enable, Test9, nand_4_out);
endmodule
