// Logisim project cell11.circ as structural Verilog: 1 circuit, main circuit main
module main (
  input  nc1,
  input  nc2,
  input  a,
  input  c1,
  input  c2,
  output out_6
);

  wire transistor_1_out, transistor_2_out, transistor_4_out, transistor_5_out, transistor_8_out,
       transistor_9_out, transistor_11_out, transistor_12_out, transistor_13_out, transistor_17_out,
       transistor_18_out, transistor_19_out;

  Transistor transistor_1 (.in(1'b1), .out(transistor_1_out), .gate(a));
  Transistor transistor_2 (.in(transistor_1_out), .out(transistor_2_out), .gate(nc1));
  Transistor #(.\type ("n")) transistor_3 (.in(transistor_4_out), .out(transistor_2_out), .gate(c1));
  Transistor #(.\type ("n")) transistor_4 (.in(1'b0), .out(transistor_4_out), .gate(a));
  Transistor transistor_5 (.in(1'b1), .out(transistor_5_out), .gate(transistor_9_out));
  Transistor transistor_6 (.in(transistor_5_out), .out(transistor_2_out), .gate(c1));
  Transistor #(.\type ("n")) transistor_7 (.in(transistor_8_out), .out(transistor_2_out), .gate(nc1));
  Transistor #(.\type ("n")) transistor_8 (.in(1'b0), .out(transistor_8_out), .gate(transistor_9_out));
  Transistor transistor_9 (.in(1'b1), .out(transistor_9_out), .gate(transistor_2_out));
  Transistor #(.\type ("n")) transistor_10 (.in(1'b0), .out(transistor_9_out), .gate(transistor_2_out));
  Transistor transistor_11 (.in(1'b1), .out(transistor_11_out), .gate(transistor_19_out));
  Transistor transistor_12 (.in(1'b1), .out(transistor_12_out), .gate(transistor_9_out));
  Transistor transistor_13 (.in(transistor_12_out), .out(transistor_13_out), .gate(nc2));
  Transistor transistor_14 (.in(transistor_11_out), .out(transistor_13_out), .gate(c2));
  Transistor #(.\type ("n")) transistor_15 (.in(transistor_18_out), .out(transistor_13_out), .gate(nc2));
  Transistor #(.\type ("n")) transistor_16 (.in(transistor_17_out), .out(transistor_13_out), .gate(c2));
  Transistor #(.\type ("n")) transistor_17 (.in(1'b0), .out(transistor_17_out), .gate(transistor_9_out));
  Transistor #(.\type ("n")) transistor_18 (.in(1'b0), .out(transistor_18_out), .gate(transistor_19_out));
  Transistor transistor_19 (.in(1'b1), .out(transistor_19_out), .gate(transistor_13_out));
  Transistor #(.\type ("n")) transistor_20 (.in(1'b0), .out(transistor_19_out), .gate(transistor_13_out));
  Transistor transistor_21 (.in(1'b1), .out(out_6), .gate(transistor_13_out));
  Transistor #(.\type ("n")) transistor_22 (.in(1'b0), .out(out_6), .gate(transistor_13_out));
endmodule
