// Logisim project cell19.circ as structural Verilog: 2 circuits, main circuit main
module main (
  input  b,
  input  a,
  input  c,
  input  d,
  output out_5
);

  wire transistor_1_out, transistor_2_out, transistor_4_out, transistor_8_out;

  Transistor transistor_1 (.in(1'b1), .out(transistor_1_out), .gate(a));
  Transistor transistor_2 (.in(transistor_1_out), .out(transistor_2_out), .gate(c));
  Transistor #(.\type ("n")) transistor_3 (.in(transistor_4_out), .out(transistor_2_out), .gate(b));
  Transistor #(.\type ("n")) transistor_4 (.in(1'b0), .out(transistor_4_out), .gate(a));
  Transistor transistor_5 (.in(1'b1), .out(transistor_1_out), .gate(b));
  Transistor transistor_6 (.in(transistor_1_out), .out(transistor_2_out), .gate(d));
  Transistor #(.\type ("n")) transistor_7 (.in(transistor_8_out), .out(transistor_2_out), .gate(c));
  Transistor #(.\type ("n")) transistor_8 (.in(1'b0), .out(transistor_8_out), .gate(d));
  Transistor transistor_9 (.in(1'b1), .out(out_5), .gate(transistor_2_out));
  Transistor #(.\type ("n")) transistor_10 (.in(1'b0), .out(out_5), .gate(transistor_2_out));
endmodule

module mainb (
  input  b,
  input  a,
  input  c,
  input  d,
  output x
);

  wire and_1_out, and_2_out;

  and and_1 (and_1_out, c, d);
  and and_2 (and_2_out, b, a);
  or or_1 (x, and_1_out, and_2_out);
endmodule
