// Logisim project cell21.circ as structural Verilog: 2 circuits, main circuit main
module main (
  input  b,
  input  a,
  output ns,
  output c,
  output s
);

  wire transistor_1_out, transistor_3_out, transistor_7_out, transistor_8_out, transistor_11_out;

  Transistor transistor_1 (.in(1'b1), .out(transistor_1_out), .gate(b));
  Transistor #(.\type ("n")) transistor_2 (.in(transistor_3_out), .out(transistor_1_out), .gate(b));
  Transistor #(.\type ("n")) transistor_3 (.in(1'b0), .out(transistor_3_out), .gate(a));
  Transistor transistor_4 (.in(1'b1), .out(transistor_1_out), .gate(a));
  Transistor transistor_5 (.in(1'b1), .out(c), .gate(transistor_1_out));
  Transistor #(.\type ("n")) transistor_6 (.in(1'b0), .out(c), .gate(transistor_1_out));
  Transistor transistor_7 (.in(1'b1), .out(transistor_7_out), .gate(a));
  Transistor transistor_8 (.in(1'b1), .out(transistor_8_out), .gate(transistor_1_out));
  Transistor transistor_9 (.in(transistor_7_out), .out(transistor_8_out), .gate(b));
  Transistor #(.\type ("n")) transistor_10 (.in(transistor_11_out), .out(transistor_8_out), .gate(transistor_1_out));
  Transistor #(.\type ("n")) transistor_11 (.in(1'b0), .out(transistor_11_out), .gate(a));
  Transistor transistor_12 (.in(1'b1), .out(s), .gate(transistor_8_out));
  Transistor #(.\type ("n")) transistor_13 (.in(1'b0), .out(s), .gate(transistor_8_out));
  Transistor #(.\type ("n")) transistor_14 (.in(1'b0), .out(transistor_11_out), .gate(b));
  Transistor transistor_15 (.in(1'b1), .out(ns), .gate(s));
  Transistor #(.\type ("n")) transistor_16 (.in(1'b0), .out(ns), .gate(s));
endmodule

module mainb (
  input  a,
  input  b,
  output s,
  output c,
  output s2
);

  wire and_2_out, and_3_out, and_4_out, and_5_out, not_1_out, not_2_out, not_3_out, not_4_out;

  not not_1 (not_1_out, a);
  not not_2 (not_2_out, b);
  and and_1 (c, a, b);
  not not_3 (not_3_out, a);
  not not_4 (not_4_out, b);
  and and_2 (and_2_out, not_1_out, b);
  and and_3 (and_3_out, a, not_2_out);
  and and_4 (and_4_out, not_3_out, not_4_out);
  and and_5 (and_5_out, a, b);
  or or_1 (s, and_2_out, and_3_out);
  or or_2 (s2, and_4_out, and_5_out);
endmodule
