// Logisim project cell_18_Evo.circ as structural Verilog: 2 circuits, main circuit main
module main (
  input  c1,
  input  c2,
  input  r,
  input  cin,
  output val_out,
  output cout
);

  wire latch1_qn, latch2_q, latch2_qn, not_1_out, not_2_out, not_3_out, transistor_1_out, transistor_3_out,
       transistor_4_out, transistor_5_out;

  not not_1 (not_1_out, cin);
  Transistor transistor_1 (.in(1'b1), .out(transistor_1_out), .gate(not_1_out));
  Transistor transistor_2 (.in(1'b1), .out(transistor_1_out), .gate(latch2_qn));
  Transistor #(.\type ("n")) transistor_3 (.in(1'b0), .out(transistor_3_out), .gate(not_1_out));
  Transistor #(.\type ("n")) transistor_4 (.in(transistor_3_out), .out(transistor_4_out), .gate(latch2_qn));
  nor nor_1 (cout, latch2_qn, not_1_out);
  Transistor transistor_5 (.in(transistor_1_out), .out(transistor_5_out), .gate(r));
  Transistor #(.\type ("n")) transistor_6 (.in(1'b0), .out(transistor_4_out), .gate(r));
  Transistor transistor_7 (.in(transistor_5_out), .out(transistor_4_out), .gate(cout));
  Transistor #(.\type ("n")) transistor_8 (.in(1'b0), .out(transistor_4_out), .gate(cout));
  not not_2 (not_2_out, transistor_4_out);
  D_Flip_Flop #(.trigger("high")) latch1 (.D(not_2_out), .clk(c1), .Qn(latch1_qn));  // open: Q, preset, reset
  D_Flip_Flop #(.trigger("high")) latch2 (
    .D(latch1_qn), .clk(c2), .Q(latch2_q), .Qn(latch2_qn));  // open: preset, reset
  not not_3 (not_3_out, latch2_q);
  not not_4 (val_out, not_3_out);
endmodule

module cnt_xor (
  input  r,
  input  n_val,
  input  cin,
  input  r_2,
  input  n_val_2,
  input  cin_2,
  output out_7,
  output out_8
);

  wire nor_1_out, not_1_out, transistor_1_out, transistor_3_out, transistor_5_out, xor_1_out;

  not not_1 (not_1_out, cin);
  Transistor transistor_1 (.in(1'b1), .out(transistor_1_out), .gate(not_1_out));
  Transistor transistor_2 (.in(1'b1), .out(transistor_1_out), .gate(n_val));
  Transistor #(.\type ("n")) transistor_3 (.in(1'b0), .out(transistor_3_out), .gate(not_1_out));
  Transistor #(.\type ("n")) transistor_4 (.in(transistor_3_out), .out(out_7), .gate(n_val));
  nor nor_1 (nor_1_out, n_val, not_1_out);
  xor xor_1 (xor_1_out, n_val_2, ~cin_2);  // XOR_Gate
  Transistor transistor_5 (.in(transistor_1_out), .out(transistor_5_out), .gate(r));
  Transistor #(.\type ("n")) transistor_6 (.in(1'b0), .out(out_7), .gate(r));
  and and_1 (out_8, ~r_2, xor_1_out);  // AND_Gate
  Transistor transistor_7 (.in(transistor_5_out), .out(out_7), .gate(nor_1_out));
  Transistor #(.\type ("n")) transistor_8 (.in(1'b0), .out(out_7), .gate(nor_1_out));
endmodule
