// Logisim project cgi2a.circ as structural Verilog: 1 circuit, main circuit main
module main (
  input  a,
  input  b,
  input  c,
  output out
);

  wire not_1_out, transistor_1_out, transistor_3_out, transistor_4_out, transistor_7_out, transistor_9_out;

  not not_1 (not_1_out, a);
  Transistor #(.\type ("n")) transistor_1 (.in(transistor_4_out), .out(transistor_1_out), .gate(c));
  Transistor #(.\type ("n")) transistor_2 (.in(transistor_3_out), .out(transistor_1_out), .gate(b));
  Transistor #(.\type ("n")) transistor_3 (.in(1'b0), .out(transistor_3_out), .gate(not_1_out));
  Transistor #(.\type ("n")) transistor_4 (.in(1'b0), .out(transistor_4_out), .gate(b));
  Transistor #(.\type ("n")) transistor_5 (.in(1'b0), .out(transistor_4_out), .gate(not_1_out));
  Transistor transistor_6 (.in(transistor_9_out), .out(transistor_1_out), .gate(c));
  Transistor transistor_7 (.in(1'b1), .out(transistor_7_out), .gate(not_1_out));
  Transistor transistor_8 (.in(transistor_7_out), .out(transistor_1_out), .gate(b));
  Transistor transistor_9 (.in(1'b1), .out(transistor_9_out), .gate(not_1_out));
  Transistor transistor_10 (.in(1'b1), .out(transistor_9_out), .gate(b));
  not not_2 (out, transistor_1_out);
endmodule
