// Logisim project SEGA 315-5309 TA-05.circ as structural Verilog: 1 circuit, main circuit main
module main (
  input  ZA0,
  input  ZA1,
  input  ZA2,
  input  ZA3,
  input  ZA4,
  input  ZA5,
  input  ZA6,
  input  ZA7,
  input  A0,
  input  A1,
  input  A2,
  input  A3,
  input  A4,
  input  A5,
  input  A6,
  input  A7,
  input  D0,
  input  D1,
  input  D2,
  input  D3,
  input  D4,
  input  D5,
  input  D6,
  input  D7,
  input  D8,
  input  D9,
  input  D10,
  input  D11,
  input  D12,
  input  D13,
  input  D14,
  input  D15,
  input  ZD0,
  input  ZD1,
  input  ZD2,
  input  ZD3,
  input  ZD4,
  input  ZD5,
  input  ZD6,
  input  ZD7,
  input  EM31,
  input  EM32,
  input  EM33,
  input  EM34,
  input  EM36,
  input  EM38,
  input  EM37,
  input  EM11,
  input  EM12,
  input  EM13,
  input  EM14,
  input  EM16,
  input  EM18,
  input  EM17,
  input  EM21,
  input  EM22,
  input  EM23,
  input  EM24,
  input  EM26,
  input  EM28,
  input  EM27,
  input  nVTOZ,
  input  nZTOV,
  input  nSRES,
  input  nIO,
  input  nM3,
  input  FREQ,
  input  LANG,
  input  nCAS0,
  input  nLWR,
  input  nDISK,
  input  nFRES,
  output D0_2,
  output D1_2,
  output D2_2,
  output D3_2,
  output D4_2,
  output D5_2,
  output D6_2,
  output D7_2,
  output D8_2,
  output D9_2,
  output D10_2,
  output D11_2,
  output D12_2,
  output D13_2,
  output D14_2,
  output D15_2,
  output ZD0_2,
  output ZD1_2,
  output ZD2_2,
  output ZD3_2,
  output ZD4_2,
  output ZD5_2,
  output ZD6_2,
  output ZD7_2,
  output EM31_2,
  output EM32_2,
  output EM33_2,
  output EM34_2,
  output EM36_2,
  output EM38_2,
  output EM37_2,
  output EM11_2,
  output EM12_2,
  output EM13_2,
  output EM14_2,
  output EM16_2,
  output EM18_2,
  output EM17_2,
  output EM21_2,
  output EM22_2,
  output EM23_2,
  output EM24_2,
  output EM26_2,
  output EM28_2,
  output EM27_2,
  output nHL
);


  // Notes on the sheet:
  //   SEGA 315-5309   TA-05
endmodule
