// Logisim project SEGA_VDP_315-5313.circ as structural Verilog
module D_Latch (
  input  in_1,
  input  in_2,
  output out_3,
  output out_4
);

  D_Flip_Flop #(.trigger("high")) d_ff_1 (.clk(in_1), .D(in_2), .Q(out_3), .Qn(out_4));  // open: preset, en, reset
endmodule

// RGB DECODER
module RGB_DECODER (
  input  RCLK1,
  input  RCLK2,
  input  _1__36,
  input  _93,
  input  _94,
  input  R0,
  input  R1,
  input  R2,
  input  G0,
  input  G1,
  input  G2,
  input  B0,
  input  B1,
  input  B2,
  output [16:0] B_DAC,
  output [16:0] G_DAC,
  output [16:0] R_DAC
);

  wire _68_2_out, _68_3_out, _68_4_out, _68_5_out, _68_out, _69_2_out, _69_out, _70_2_out, _70_out,
       _119_2_out, _119_out, _120_2_out, _120_out, _121_2_out, _121_out, _125_2_out, _125_out, _126_2_out,
       _126_out, _127_2_out, _127_3_out, _127_4_out, _127_5_out, _127_out, _128_2_out, _128_out, _129_2_out,
       _129_out, _133_2_out, _133_out, _134_2_out, _134_out, _135_2_out, _135_3_out, _135_4_out, _135_out,
       _137_2_out, _137_out, _138_2_out, _138_out, _139_2_out, _139_out, _143_2_out, _143_out, _144_2_out,
       _144_out, _148_2_out, _148_out, _149_2_out, _149_out, _150_2_out, _150_3_out, _150_4_out, _150_out,
       _151_2_out, _151_out, _152_2_out, _152_out, _153_2_out, _153_out, _157_2_out, _157_out, _158_2_out,
       _158_out, _159_2_out, _159_3_out, _159_4_out, _159_5_out, _159_out, _160_2_out, _160_out, _161_2_out,
       _161_out, _162_2_out, _162_out, _166_2_out, _166_out, _167_2_out, _167_3_out, _167_4_out, _167_out,
       _168_out, _169_out, d_latch_1_out_4, d_latch_2_out_4, d_latch_3_out_4, d_latch_4_out_4,
       d_latch_5_out_4, d_latch_6_out_4, d_latch_7_out_4, d_latch_8_out_4, d_latch_9_out_4, d_latch_10_out_4,
       d_latch_11_out_4, d_latch_12_out_4, d_latch_13_out_4, decoder_1_out0, decoder_1_out1, decoder_1_out2,
       decoder_1_out3, decoder_1_out4, decoder_1_out5, decoder_1_out6, decoder_1_out7, decoder_2_out0,
       decoder_2_out1, decoder_2_out2, decoder_2_out3, decoder_2_out4, decoder_2_out5, decoder_2_out6,
       decoder_2_out7, decoder_3_out0, decoder_3_out1, decoder_3_out2, decoder_3_out3, decoder_3_out4,
       decoder_3_out5, decoder_3_out6, decoder_3_out7, not_1_out, not_2_out, not_3_out;
  wire [2:0] d_latch_14_out_4, d_latch_17_out_4, d_latch_20_out_4;

  D_Latch d_latch_1 (.in_1(RCLK1), .in_2(_93), .out_4(d_latch_1_out_4));  // open: out_3
  D_Latch d_latch_2 (.in_1(RCLK1), .in_2(_94), .out_4(d_latch_2_out_4));  // open: out_3
  D_Latch d_latch_3 (.in_1(RCLK1), .in_2(R0), .out_4(d_latch_3_out_4));  // open: out_3
  D_Latch d_latch_4 (.in_1(RCLK1), .in_2(R1), .out_4(d_latch_4_out_4));  // open: out_3
  D_Latch d_latch_5 (.in_1(RCLK1), .in_2(R2), .out_4(d_latch_5_out_4));  // open: out_3
  D_Latch d_latch_6 (.in_1(RCLK1), .in_2(G0), .out_4(d_latch_6_out_4));  // open: out_3
  D_Latch d_latch_7 (.in_1(RCLK1), .in_2(G1), .out_4(d_latch_7_out_4));  // open: out_3
  D_Latch d_latch_8 (.in_1(RCLK1), .in_2(G2), .out_4(d_latch_8_out_4));  // open: out_3
  D_Latch d_latch_9 (.in_1(RCLK1), .in_2(B0), .out_4(d_latch_9_out_4));  // open: out_3
  D_Latch d_latch_10 (.in_1(RCLK1), .in_2(B1), .out_4(d_latch_10_out_4));  // open: out_3
  D_Latch d_latch_11 (.in_1(RCLK1), .in_2(B2), .out_4(d_latch_11_out_4));  // open: out_3
  D_Latch d_latch_12 (.in_1(RCLK2), .in_2(d_latch_1_out_4), .out_4(d_latch_12_out_4));  // open: out_3
  D_Latch d_latch_13 (.in_1(RCLK2), .in_2(d_latch_2_out_4), .out_4(d_latch_13_out_4));  // open: out_3
  D_Latch d_latch_14 (.in_1(RCLK2), .in_2(d_latch_3_out_4), .out_4(d_latch_14_out_4[0]));  // open: out_3
  D_Latch d_latch_15 (.in_1(RCLK2), .in_2(d_latch_4_out_4), .out_4(d_latch_14_out_4[1]));  // open: out_3
  D_Latch d_latch_16 (.in_1(RCLK2), .in_2(d_latch_5_out_4), .out_4(d_latch_14_out_4[2]));  // open: out_3
  D_Latch d_latch_17 (.in_1(RCLK2), .in_2(d_latch_6_out_4), .out_4(d_latch_17_out_4[0]));  // open: out_3
  D_Latch d_latch_18 (.in_1(RCLK2), .in_2(d_latch_7_out_4), .out_4(d_latch_17_out_4[1]));  // open: out_3
  D_Latch d_latch_19 (.in_1(RCLK2), .in_2(d_latch_8_out_4), .out_4(d_latch_17_out_4[2]));  // open: out_3
  D_Latch d_latch_20 (.in_1(RCLK2), .in_2(d_latch_9_out_4), .out_4(d_latch_20_out_4[0]));  // open: out_3
  D_Latch d_latch_21 (.in_1(RCLK2), .in_2(d_latch_10_out_4), .out_4(d_latch_20_out_4[1]));  // open: out_3
  D_Latch d_latch_22 (.in_1(RCLK2), .in_2(d_latch_11_out_4), .out_4(d_latch_20_out_4[2]));  // open: out_3
  not not_1 (not_1_out, _1__36);
  not not_2 (not_2_out, not_1_out);
  not not_3 (not_3_out, d_latch_13_out_4);
  Decoder #(.select(3), .disabled(0), .enable("false")) decoder_1 (
    .out0(decoder_1_out0), .out1(decoder_1_out1), .out2(decoder_1_out2), .out3(decoder_1_out3),
    .out4(decoder_1_out4), .out5(decoder_1_out5), .out6(decoder_1_out6), .out7(decoder_1_out7),
    .sel(d_latch_20_out_4));
  and _169 (_169_out, d_latch_12_out_4, not_3_out);
  nor _168 (_168_out, not_2_out, d_latch_12_out_4, d_latch_13_out_4);
  and _151 (_151_out, d_latch_13_out_4, decoder_1_out5);
  and _151_2 (_151_2_out, decoder_1_out6, _168_out);
  and _152 (_152_out, d_latch_13_out_4, decoder_1_out1);
  and _152_2 (_152_2_out, decoder_1_out4, _168_out);
  and _153 (_153_out, _169_out, decoder_1_out7);
  and _153_2 (_153_2_out, decoder_1_out0, d_latch_13_out_4);
  nand _154 (B_DAC[3], d_latch_13_out_4, decoder_1_out4);
  nand _155 (B_DAC[4], d_latch_13_out_4, decoder_1_out6);
  nand _156 (B_DAC[5], d_latch_13_out_4, decoder_1_out2);
  and _157 (_157_out, not_2_out, decoder_1_out4);
  and _157_2 (_157_2_out, decoder_1_out5, not_2_out);
  and _158 (_158_out, d_latch_13_out_4, decoder_1_out3);
  and _158_2 (_158_2_out, decoder_1_out5, _168_out);
  and _160 (_160_out, _169_out, decoder_1_out2);
  and _160_2 (_160_2_out, decoder_1_out1, _168_out);
  and _161 (_161_out, not_2_out, decoder_1_out2);
  and _161_2 (_161_2_out, decoder_1_out3, not_2_out);
  and _163 (B_DAC[12], _169_out, decoder_1_out3);
  and _164 (B_DAC[13], _169_out, decoder_1_out1);
  and _165 (B_DAC[14], _169_out, decoder_1_out5);
  and _162 (_162_out, _169_out, decoder_1_out6);
  and _162_2 (_162_2_out, decoder_1_out3, _168_out);
  and _166 (_166_out, _169_out, decoder_1_out4);
  and _166_2 (_166_2_out, decoder_1_out2, _168_out);
  and _167 (_167_out, not_2_out, decoder_1_out0);
  and _167_2 (_167_2_out, decoder_1_out1, not_2_out);
  and _167_3 (_167_3_out, _169_out, decoder_1_out0);
  and _167_4 (_167_4_out, decoder_1_out0, _168_out);
  and _159 (_159_out, not_2_out, decoder_1_out6);
  and _159_2 (_159_2_out, decoder_1_out7, not_2_out);
  and _159_3 (_159_3_out, d_latch_13_out_4, decoder_1_out7);
  and _159_4 (_159_4_out, decoder_1_out7, _168_out);
  nor _151_3 (B_DAC[0], _151_out, _151_2_out);
  nor _152_3 (B_DAC[1], _152_out, _152_2_out);
  nor _153_3 (B_DAC[2], _153_out, _153_2_out);
  nor _157_3 (B_DAC[6], _157_out, _157_2_out);
  nor _158_3 (B_DAC[7], _158_out, _158_2_out);
  or _160_3 (B_DAC[9], _160_out, _160_2_out);
  or _161_3 (B_DAC[10], _161_out, _161_2_out);
  or _162_3 (B_DAC[11], _162_out, _162_2_out);
  or _166_3 (B_DAC[15], _166_out, _166_2_out);
  or _167_5 (B_DAC[16], _167_out, _167_2_out, _167_3_out, _167_4_out);
  not not_4 (B_DAC[8], _159_5_out);
  or _159_5 (_159_5_out, _159_out, _159_2_out, _159_3_out, _159_4_out);
  Decoder #(.select(3), .disabled(0), .enable("false")) decoder_2 (
    .out0(decoder_2_out0), .out1(decoder_2_out1), .out2(decoder_2_out2), .out3(decoder_2_out3),
    .out4(decoder_2_out4), .out5(decoder_2_out5), .out6(decoder_2_out6), .out7(decoder_2_out7),
    .sel(d_latch_17_out_4));
  and _137 (_137_out, d_latch_13_out_4, decoder_2_out5);
  and _137_2 (_137_2_out, decoder_2_out6, _168_out);
  and _138 (_138_out, d_latch_13_out_4, decoder_2_out1);
  and _138_2 (_138_2_out, decoder_2_out4, _168_out);
  and _139 (_139_out, _169_out, decoder_2_out7);
  and _139_2 (_139_2_out, decoder_2_out0, d_latch_13_out_4);
  nand _140 (G_DAC[3], d_latch_13_out_4, decoder_2_out4);
  nand _141 (G_DAC[4], d_latch_13_out_4, decoder_2_out6);
  nand _142 (G_DAC[5], d_latch_13_out_4, decoder_2_out2);
  and _143 (_143_out, not_2_out, decoder_2_out4);
  and _143_2 (_143_2_out, decoder_2_out5, not_2_out);
  and _144 (_144_out, d_latch_13_out_4, decoder_2_out3);
  and _144_2 (_144_2_out, decoder_2_out5, _168_out);
  and _69 (_69_out, _169_out, decoder_2_out2);
  and _69_2 (_69_2_out, decoder_2_out1, _168_out);
  and _70 (_70_out, _169_out, decoder_2_out6);
  and _70_2 (_70_2_out, decoder_2_out3, _168_out);
  and _145 (G_DAC[11], _169_out, decoder_2_out5);
  and _146 (G_DAC[12], _169_out, decoder_2_out3);
  and _147 (G_DAC[13], _169_out, decoder_2_out1);
  and _148 (_148_out, not_2_out, decoder_2_out2);
  and _148_2 (_148_2_out, decoder_2_out3, not_2_out);
  and _149 (_149_out, _169_out, decoder_2_out4);
  and _149_2 (_149_2_out, decoder_2_out2, _168_out);
  and _150 (_150_out, not_2_out, decoder_2_out0);
  and _150_2 (_150_2_out, decoder_2_out1, not_2_out);
  and _150_3 (_150_3_out, _169_out, decoder_2_out0);
  and _150_4 (_150_4_out, decoder_2_out0, _168_out);
  and _68 (_68_out, not_2_out, decoder_2_out6);
  and _68_2 (_68_2_out, decoder_2_out7, not_2_out);
  and _68_3 (_68_3_out, d_latch_13_out_4, decoder_2_out7);
  and _68_4 (_68_4_out, decoder_2_out7, _168_out);
  nor _137_3 (G_DAC[0], _137_out, _137_2_out);
  nor _138_3 (G_DAC[1], _138_out, _138_2_out);
  nor _139_3 (G_DAC[2], _139_out, _139_2_out);
  nor _143_3 (G_DAC[6], _143_out, _143_2_out);
  nor _144_3 (G_DAC[7], _144_out, _144_2_out);
  or _69_3 (G_DAC[9], _69_out, _69_2_out);
  or _70_3 (G_DAC[10], _70_out, _70_2_out);
  or _148_3 (G_DAC[14], _148_out, _148_2_out);
  or _149_3 (G_DAC[15], _149_out, _149_2_out);
  or _150_5 (G_DAC[16], _150_out, _150_2_out, _150_3_out, _150_4_out);
  or _68_5 (_68_5_out, _68_out, _68_2_out, _68_3_out, _68_4_out);
  not not_5 (G_DAC[8], _68_5_out);
  Decoder #(.select(3), .disabled(0), .enable("false")) decoder_3 (
    .out0(decoder_3_out0), .out1(decoder_3_out1), .out2(decoder_3_out2), .out3(decoder_3_out3),
    .out4(decoder_3_out4), .out5(decoder_3_out5), .out6(decoder_3_out6), .out7(decoder_3_out7),
    .sel(d_latch_14_out_4));
  and _119 (_119_out, d_latch_13_out_4, decoder_3_out5);
  and _119_2 (_119_2_out, decoder_3_out6, _168_out);
  and _120 (_120_out, d_latch_13_out_4, decoder_3_out1);
  and _120_2 (_120_2_out, decoder_3_out4, _168_out);
  and _121 (_121_out, _169_out, decoder_3_out7);
  and _121_2 (_121_2_out, decoder_3_out0, d_latch_13_out_4);
  nand _122 (R_DAC[3], d_latch_13_out_4, decoder_3_out4);
  nand _123 (R_DAC[4], d_latch_13_out_4, decoder_3_out6);
  nand _124 (R_DAC[5], d_latch_13_out_4, decoder_3_out2);
  and _125 (_125_out, not_2_out, decoder_3_out4);
  and _125_2 (_125_2_out, decoder_3_out5, not_2_out);
  and _126 (_126_out, d_latch_13_out_4, decoder_3_out3);
  and _126_2 (_126_2_out, decoder_3_out5, _168_out);
  and _128 (_128_out, _169_out, decoder_3_out2);
  and _128_2 (_128_2_out, decoder_3_out1, _168_out);
  and _129 (_129_out, _169_out, decoder_3_out6);
  and _129_2 (_129_2_out, decoder_3_out3, _168_out);
  and _130 (R_DAC[11], _169_out, decoder_3_out5);
  and _131 (R_DAC[12], _169_out, decoder_3_out3);
  and _132 (R_DAC[13], _169_out, decoder_3_out1);
  and _133 (_133_out, not_2_out, decoder_3_out2);
  and _133_2 (_133_2_out, decoder_3_out3, not_2_out);
  and _134 (_134_out, _169_out, decoder_3_out4);
  and _134_2 (_134_2_out, decoder_3_out2, _168_out);
  and _135 (_135_out, not_2_out, decoder_3_out0);
  and _135_2 (_135_2_out, decoder_3_out1, not_2_out);
  and _135_3 (_135_3_out, _169_out, decoder_3_out0);
  and _135_4 (_135_4_out, decoder_3_out0, _168_out);
  and _127 (_127_out, not_2_out, decoder_3_out6);
  and _127_2 (_127_2_out, decoder_3_out7, not_2_out);
  and _127_3 (_127_3_out, d_latch_13_out_4, decoder_3_out7);
  and _127_4 (_127_4_out, decoder_3_out7, _168_out);
  nor _119_3 (R_DAC[0], _119_out, _119_2_out);
  nor _120_3 (R_DAC[1], _120_out, _120_2_out);
  nor _121_3 (R_DAC[2], _121_out, _121_2_out);
  nor _125_3 (R_DAC[6], _125_out, _125_2_out);
  nor _126_3 (R_DAC[7], _126_out, _126_2_out);
  or _128_3 (R_DAC[9], _128_out, _128_2_out);
  or _129_3 (R_DAC[10], _129_out, _129_2_out);
  or _133_3 (R_DAC[14], _133_out, _133_2_out);
  or _134_3 (R_DAC[15], _134_out, _134_2_out);
  or _135_5 (R_DAC[16], _135_out, _135_2_out, _135_3_out, _135_4_out);
  not not_6 (R_DAC[8], _127_5_out);
  or _127_5 (_127_5_out, _127_out, _127_2_out, _127_3_out, _127_4_out);

  // Notes on the sheet:
  //   81
  //   83
  //   108
  //   110
  //   109
  //   94
  //   95
  //   96
  //   82
  //   81
  //   83
  //   76
  //   80
  //   168
  //   169
  //   83
  //   76
  //   75
  //   169
  //   83
  //   168
  //   76
  //   74
  //   168
  //   76
  //   169
  //   83
  //   136
endmodule

module CLK_DIVIDER (
  input  TO_RES,
  input  nRES,
  input  MCLK,
  input  in_4,
  input  in_5,
  input  EDCLK_INP,
  input  H40,
  input  in_8,
  input  in_9,
  output _1,
  output RES,
  output _2,
  output SYSRES,
  output _68k_CPU_CLOCK,
  output SUB_CARRIER_OUTPUT,
  output PSG_CLK,
  output Z80_CLK
);

  wire _1_out, _8_out, _13_out, _14_q, _16_out, _17_q, _18_q, _21_2_out, _21_3_out, _21_4_out, _21_out,
       _22_out, _23_out, _24_out, _29_out, _30_q, _32_out, _33_q, _34_q, _36_out, _39_q, _45_q, _46_q,
       _47_out, _48_q, _49_q, _51_q, _52_out, _53_q, _54_q, _56_q, _58_q, _60_out, _62_q, _63_q, _64_out,
       and_1_out, and_2_out, clock_1_out, d_ff_1_q, d_ff_2_q, d_latch_1_out_4, d_latch_2_out_4,
       d_latch_3_out_4, d_latch_4_out_4, d_latch_5_out_4, d_latch_6_out_4, DCLK1, DCLK2, nand_1_out,
       nand_2_out, nor_1_out, not_1_out, not_2_out, not_3_out, not_4_out, not_5_out, not_6_out, not_7_out,
       not_8_out, not_9_out, not_10_out, not_11_out, not_12_out, not_13_out, not_14_out, not_15_out,
       not_16_out, not_17_out, not_18_out, not_19_out, not_20_out, not_21_out, not_22_out, not_23_out,
       not_24_out, not_28_out, not_29_out, not_30_out, not_31_out, not_34_out, not_35_out, not_36_out,
       not_37_out, not_38_out, not_39_out, not_40_out, not_41_out, not_42_out, not_43_out, not_44_out,
       not_45_out, not_46_out, not_47_out, not_48_out, not_49_out, not_50_out, not_51_out, not_54_out,
       not_55_out, not_56_out, not_57_out, not_58_out, not_59_out, undriven;

  Clock clock_1 (.out(clock_1_out));
  nand _64 (_64_out, TO_RES, nRES);
  D_Flip_Flop _49 (.clk(clock_1_out), .D(_45_q), .Q(_49_q), .reset(not_3_out));  // open: Qn, preset, en
  D_Flip_Flop _63 (.clk(clock_1_out), .D(_64_out), .Q(_63_q));  // open: Qn, preset, en, reset
  D_Flip_Flop _54 (.clk(clock_1_out), .D(_51_q), .Q(_54_q), .reset(not_3_out));  // open: Qn, preset, en
  D_Flip_Flop _39 (.clk(DCLK1), .D(_64_out), .Q(_39_q));  // open: Qn, preset, en, reset
  D_Flip_Flop _48 (.clk(clock_1_out), .D(_49_q), .Q(_48_q), .reset(not_3_out));  // open: Qn, preset, en
  or _24 (_24_out, in_4, in_5);
  D_Flip_Flop _62 (.clk(clock_1_out), .D(_63_q), .Q(_62_q));  // open: Qn, preset, en, reset
  D_Flip_Flop _58 (.clk(clock_1_out), .D(_56_q), .Q(_58_q), .reset(not_3_out));  // open: Qn, preset, en
  D_Flip_Flop _53 (.clk(clock_1_out), .D(_54_q), .Q(_53_q), .reset(not_3_out));  // open: Qn, preset, en
  nand _47 (_47_out, _48_q, _49_q);
  not not_1 (not_1_out, _62_q);
  not not_2 (not_2_out, _58_q);
  nand _52 (_52_out, _53_q, _54_q);
  D_Latch d_latch_1 (.in_1(DCLK1), .in_2(_39_q), .out_4(d_latch_1_out_4));  // open: out_3
  D_Flip_Flop _46 (.clk(clock_1_out), .D(_47_out), .Q(_46_q), .reset(not_3_out));  // open: Qn, preset, en
  nand _60 (_60_out, not_1_out, _63_q);
  D_Flip_Flop _56 (.clk(clock_1_out), .D(not_2_out), .Q(_56_q), .reset(not_3_out));  // open: Qn, preset, en
  D_Flip_Flop _51 (.clk(clock_1_out), .D(_52_out), .Q(_51_q), .reset(not_3_out));  // open: Qn, preset, en
  not not_3 (not_3_out, _60_out);
  not not_4 (not_4_out, _56_q);
  not not_5 (not_5_out, _51_q);
  D_Latch d_latch_2 (.in_1(DCLK2), .in_2(d_latch_1_out_4), .out_4(d_latch_2_out_4));  // open: out_3
  not not_6 (not_6_out, d_latch_2_out_4);
  D_Flip_Flop _45 (.clk(clock_1_out), .D(_46_q), .Q(_45_q), .reset(not_3_out));  // open: Qn, preset, en
  not not_7 (not_7_out, _45_q);
  nand _36 (_36_out, not_6_out, _39_q);
  not not_8 (not_8_out, not_4_out);
  not not_9 (not_9_out, not_4_out);
  nor _32 (_32_out, _34_q, _33_q);
  not not_10 (not_10_out, not_5_out);
  not not_11 (not_11_out, not_5_out);
  nor _16 (_16_out, _18_q, _17_q);
  D_Flip_Flop _34 (.clk(not_9_out), .D(_32_out), .Q(_34_q), .reset(not_3_out));  // open: Qn, preset, en
  D_Flip_Flop _18 (.clk(not_11_out), .D(_16_out), .Q(_18_q), .reset(not_3_out));  // open: Qn, preset, en
  not not_12 (not_12_out, not_9_out);
  D_Flip_Flop _33 (.clk(not_9_out), .D(_34_q), .Q(_33_q), .reset(not_3_out));  // open: Qn, preset, en
  not not_13 (not_13_out, not_11_out);
  D_Flip_Flop _17 (.clk(not_11_out), .D(_18_q), .Q(_17_q), .reset(not_3_out));  // open: Qn, preset, en
  not not_14 (not_14_out, H40);
  D_Flip_Flop _30 (.clk(not_12_out), .D(_33_q), .Q(_30_q), .reset(not_3_out));  // open: Qn, preset, en
  D_Flip_Flop _14 (.clk(not_13_out), .D(_17_q), .Q(_14_q), .reset(not_3_out));  // open: Qn, preset, en
  nor _22 (_22_out, _24_out, not_14_out);
  nor _23 (_23_out, _24_out, H40);
  or _29 (_29_out, _30_q, _33_q);
  or _13 (_13_out, _14_q, _17_q);
  not not_15 (not_15_out, not_7_out);
  not not_16 (not_16_out, not_15_out);
  and _21 (_21_out, _24_out, EDCLK_INP);
  and _21_2 (_21_2_out, _22_out, not_8_out);
  and _21_3 (_21_3_out, _23_out, not_10_out);
  not not_17 (not_17_out, not_18_out);
  not not_18 (not_18_out, _13_out);
  not not_19 (not_19_out, not_16_out);
  not not_20 (not_20_out, not_19_out);
  nor _21_4 (_21_4_out, _21_out, _21_2_out, _21_3_out);
  not not_21 (not_21_out, not_22_out);
  not not_22 (not_22_out, not_17_out);
  not not_23 (not_23_out, _64_out);
  or u__1 (_1_out, not_20_out, not_7_out);
  and _8 (_8_out, not_21_out, _13_out);
  not not_24 (not_24_out, _36_out);
  not not_25 (RES, nRES);
  not not_26 (SYSRES, not_23_out);
  not not_27 (_68k_CPU_CLOCK, _1_out);
  not not_28 (not_28_out, _21_4_out);
  Multiplexer #(.disabled(0), .enable("false")) multiplexer_1 (
    .in0(_8_out), .in1(_29_out), .out(SUB_CARRIER_OUTPUT), .sel(in_8));
  Multiplexer #(.disabled(0), .enable("false")) multiplexer_2 (.in0(_8_out), .in1(in_9), .out(PSG_CLK), .sel(in_5));
  nor nor_1 (nor_1_out, not_24_out, d_latch_4_out_4);
  not not_29 (not_29_out, not_28_out);
  not not_30 (not_30_out, not_28_out);
  D_Latch d_latch_3 (.in_1(DCLK1), .in_2(nor_1_out), .out_4(d_latch_3_out_4));  // open: out_3
  not not_31 (not_31_out, not_29_out);
  not not_32 (DCLK1, not_31_out);
  not not_33 (DCLK2, not_30_out);
  not not_34 (not_34_out, undriven);
  D_Latch d_latch_4 (.in_1(DCLK2), .in_2(d_latch_3_out_4), .out_4(d_latch_4_out_4));  // open: out_3
  not not_35 (not_35_out, not_36_out);
  not not_36 (not_36_out, undriven);
  not not_37 (not_37_out, not_38_out);
  not not_38 (not_38_out, not_34_out);
  not not_39 (not_39_out, d_latch_4_out_4);
  not not_40 (not_40_out, not_41_out);
  not not_41 (not_41_out, not_35_out);
  not not_42 (not_42_out, not_37_out);
  not not_43 (not_43_out, not_42_out);
  D_Latch d_latch_5 (.in_1(DCLK1), .in_2(not_39_out), .out_4(d_latch_5_out_4));  // open: out_3
  D_Latch d_latch_6 (.in_1(DCLK1), .in_2(d_latch_4_out_4), .out_4(d_latch_6_out_4));  // open: out_3
  not not_44 (not_44_out, not_45_out);
  not not_45 (not_45_out, not_40_out);
  not not_46 (not_46_out, not_47_out);
  not not_47 (not_47_out, not_43_out);
  and and_1 (and_1_out, d_latch_5_out_4, DCLK2);
  and and_2 (and_2_out, d_latch_6_out_4, DCLK2);
  not not_48 (not_48_out, not_44_out);
  not not_49 (not_49_out, not_48_out);
  not not_50 (not_50_out, not_51_out);
  not not_51 (not_51_out, not_46_out);
  D_Flip_Flop d_ff_1 (.clk(DCLK1), .D(1'b1), .Q(d_ff_1_q), .reset(and_1_out));  // open: Qn, preset, en
  D_Flip_Flop d_ff_2 (.clk(DCLK1), .D(1'b1), .Q(d_ff_2_q), .reset(and_2_out));  // open: Qn, preset, en
  nand nand_1 (nand_1_out, not_49_out, not_36_out);
  nand nand_2 (nand_2_out, not_50_out, not_38_out);
  not not_52 (_1, d_ff_1_q);
  not not_53 (_2, d_ff_2_q);
  not not_54 (not_54_out, nand_1_out);
  not not_55 (not_55_out, not_56_out);
  not not_56 (not_56_out, nand_1_out);
  not not_57 (not_57_out, nand_2_out);
  not not_58 (not_58_out, not_59_out);
  not not_59 (not_59_out, nand_2_out);
  // NOT_Gate not_60 is placed but not wired

  assign Z80_CLK = PSG_CLK;

  // Notes on the sheet:
  //   61
  //   57
  //   59
  //   55
  //   50
  //   37
  //   38
  //   44
  //   26
  //   35
  //   20
  //   19
  //   VDP CLOCK DIVIDER
  //   25
  //   31
  //   15
  //   5
  //   3
  //   4
  //   11
  //   12
  //   2
  //   9
  //   10
  //   41
  //   66
  //   42
  //   40
  //   43
  //   65
  //   27,28
  //   6,7
  //   RES
  //   EDCLK OUTPUT
  //   RES
  //   EDCLK
  //   EDCLK
  //   VDP CLOCK PUSH PULL
  //   1
  //   2
  //   DCLK1
  //   DCLK2
endmodule

module VRAM_CTR (
  input  DCLK1,
  input  DCLK2,
  input  RCLK1,
  input  RCLK2,
  input  _18,
  input  _7,
  input  _15,
  input  _21,
  input  _14,
  input  _24,
  input  _53,
  input  _27,
  input  _128k,
  input  _31,
  input  _26,
  input  _34,
  input  _13,
  input  M5,
  input  [7:0] in_19,
  input  [7:0] AD_IN,
  input  [7:0] RD_IN,
  input  _39,
  input  [7:0] in_23,
  input  _36,
  input  _73,
  input  _80,
  input  _75,
  input  _28,
  input  _30,
  output nOE1,
  output nCE0,
  output nSC,
  output AD_RD_DIR_PAD,
  output nRAS,
  output nCAS,
  output nWE0,
  output nWE1,
  output [7:0] AD_OUT,
  output [7:0] RD_OUT,
  output nYS,
  output [7:0] RD_BUS_READ,
  output [7:0] AD_BUS_READ
);

  wire _8_out, _12_out, _25_2_out, _25_out, _26_out, _27_out, _38_2_out, _38_out, _41_2_out, _41_3_out,
       _41_4_out, _41_out, _42_2_out, _42_3_out, _42_out, _43_out, _49_out, _50_out, _51_out, _52_2_out,
       _52_3_out, _52_out, _53_out, _63_out, _66_out, _67_out, _76_out, _77_out, _78_out, _79_out, _80_2_out,
       _80_out, _109_out_4, _177_out, _181_2_out, _181_out, _208_out, _218_2_out, _218_3_out, _218_4_out,
       _218_out, _219_2_out, _219_3_out, _219_4_out, _219_out, _220_2_out, _220_3_out, _220_4_out, _220_out,
       _221_2_out, _221_3_out, _221_4_out, _221_out, _222_2_out, _222_3_out, _222_out, _223_2_out,
       _223_3_out, _223_4_out, _223_out, _224_2_out, _224_3_out, _224_4_out, _224_out, _225_2_out,
       _225_3_out, _225_4_out, _225_out, _228_2_out, _228_out, d_latch_1_out_4, d_latch_2_out_4,
       d_latch_3_out_4, d_latch_4_out_4, d_latch_5_out_4, d_latch_6_out_4, d_latch_7_out_4, d_latch_8_out_4,
       d_latch_9_out_4, d_latch_10_out_4, d_latch_11_out_4, d_latch_12_out_4, d_latch_13_out_4,
       d_latch_14_out_4, d_latch_15_out_4, d_latch_16_out_4, d_latch_17_out_4, d_latch_18_out_4,
       d_latch_19_out_4, d_latch_20_out_4, d_latch_21_out_4, d_latch_22_out_4, d_latch_23_out_4,
       d_latch_24_out_4, d_latch_25_out_4, d_latch_26_out_4, d_latch_27_out_4, d_latch_28_out_4,
       d_latch_29_out_4, d_latch_30_out_4, d_latch_31_out_4, d_latch_32_out_4, d_latch_33_out_4,
       d_latch_34_out_4, d_latch_35_out_4, d_latch_36_out_4, d_latch_37_out_4, d_latch_38_out_4,
       d_latch_40_out_4, d_latch_41_out_4, d_latch_42_out_4, d_latch_43_out_4, d_latch_44_out_4,
       d_latch_45_out_4, d_latch_46_out_4, d_latch_47_out_4, d_latch_48_out_4, d_latch_49_out_4,
       d_latch_50_out_4, d_latch_51_out_4, d_latch_52_out_4, d_latch_53_out_4, d_latch_54_out_4,
       d_latch_55_out_4, d_latch_56_out_4, d_latch_57_out_4, d_latch_58_out_4, d_latch_59_out_4,
       d_latch_60_out_4, d_latch_61_out_4, d_latch_62_out_4, d_latch_63_out_4, d_latch_64_out_4,
       d_latch_65_out_4, d_latch_66_out_4, d_latch_67_out_4, d_latch_68_out_4, d_latch_69_out_4,
       d_latch_70_out_4, d_latch_71_out_4, d_latch_72_out_4, d_latch_73_out_4, d_latch_74_out_4,
       d_latch_75_out_4, d_latch_76_out_3, d_latch_77_out_3, d_latch_78_out_3, d_latch_79_out_3,
       d_latch_80_out_3, d_latch_81_out_3, d_latch_82_out_3, d_latch_83_out_3, d_latch_84_out_3,
       d_latch_85_out_3, d_latch_86_out_3, d_latch_87_out_3, d_latch_88_out_3, d_latch_89_out_3,
       d_latch_90_out_3, d_latch_91_out_3, d_latch_92_out_3, d_latch_93_out_3, d_latch_94_out_3,
       d_latch_95_out_3, d_latch_96_out_3, d_latch_97_out_3, d_latch_98_out_3, d_latch_99_out_3,
       d_latch_100_out_3, d_latch_101_out_3, d_latch_102_out_3, d_latch_103_out_3, d_latch_104_out_3,
       d_latch_105_out_3, d_latch_106_out_3, d_latch_107_out_3, multiplexer_1_out, multiplexer_2_out,
       multiplexer_3_out, multiplexer_4_out, multiplexer_5_out, multiplexer_6_out, multiplexer_7_out,
       multiplexer_8_out, multiplexer_9_out, multiplexer_10_out, multiplexer_11_out, multiplexer_12_out,
       multiplexer_13_out, multiplexer_14_out, multiplexer_15_out, multiplexer_16_out, multiplexer_17_out,
       multiplexer_18_out, multiplexer_19_out, multiplexer_20_out, multiplexer_21_out, multiplexer_22_out,
       multiplexer_23_out, multiplexer_24_out, multiplexer_25_out, multiplexer_26_out, multiplexer_27_out,
       multiplexer_28_out, multiplexer_29_out, multiplexer_30_out, multiplexer_31_out, multiplexer_32_out,
       multiplexer_33_out, not_1_out, not_2_out, not_3_out, not_4_out, not_5_out, not_6_out, not_7_out,
       not_8_out, not_9_out, not_10_out, not_11_out, not_12_out, not_13_out, not_14_out, not_15_out,
       not_16_out, not_17_out, not_18_out, not_19_out, not_20_out, not_21_out, not_22_out, not_23_out,
       not_24_out, not_25_out, not_26_out, not_27_out, not_28_out, not_29_out, not_30_out, not_31_out,
       not_32_out, not_33_out, not_34_out, not_35_out, not_36_out, not_37_out, not_38_out, not_39_out,
       not_40_out, not_41_out, not_42_out, not_46_out, not_47_out, not_48_out, not_49_out, not_50_out,
       not_51_out, not_52_out, or_1_out;
  wire [2:0] not_43_out;

  not not_1 (not_1_out, M5);
  not _63 (_63_out, _34);
  not not_2 (not_2_out, _26);
  and _208 (_208_out, _39, M5);
  and _181 (_181_out, not_1_out, in_19[1]);
  Multiplexer #(.disabled(0), .enable("false")) multiplexer_1 (
    .in0(_80), .in1(_75), .out(multiplexer_1_out), .sel(_73));
  and _52 (_52_out, d_latch_72_out_4, _26, _26);
  and _52_2 (_52_2_out, _63_out, not_2_out, _18);
  nor _181_2 (_181_2_out, _208_out, _181_out);
  nor _52_3 (_52_3_out, _52_out, _52_2_out);
  D_Latch d_latch_1 (.in_1(RCLK1), .in_2(_18), .out_4(d_latch_1_out_4));  // open: out_3
  and _67 (_67_out, RCLK1, _128k);
  not not_3 (not_3_out, _128k);
  D_Latch d_latch_2 (.in_1(RCLK1), .in_2(_15), .out_4(d_latch_2_out_4));  // open: out_3
  D_Latch d_latch_3 (.in_1(RCLK1), .in_2(d_latch_11_out_4), .out_4(d_latch_3_out_4));  // open: out_3
  D_Latch d_latch_4 (.in_1(RCLK1), .in_2(_21), .out_4(d_latch_4_out_4));  // open: out_3
  D_Latch d_latch_5 (.in_1(RCLK1), .in_2(d_latch_13_out_4), .out_4(d_latch_5_out_4));  // open: out_3
  D_Latch d_latch_6 (.in_1(RCLK1), .in_2(_14), .out_4(d_latch_6_out_4));  // open: out_3
  D_Latch d_latch_7 (.in_1(RCLK1), .in_2(_24), .out_4(d_latch_7_out_4));  // open: out_3
  D_Latch d_latch_8 (.in_1(RCLK1), .in_2(_53), .out_4(d_latch_8_out_4));  // open: out_3
  D_Latch d_latch_9 (.in_1(RCLK1), .in_2(_27), .out_4(d_latch_9_out_4));  // open: out_3
  D_Latch d_latch_10 (.in_1(RCLK1), .in_2(_52_3_out), .out_4(d_latch_10_out_4));  // open: out_3
  not not_4 (not_4_out, _53_out);
  not not_5 (not_5_out, not_4_out);
  D_Latch d_latch_11 (.in_1(RCLK2), .in_2(d_latch_2_out_4), .out_4(d_latch_11_out_4));  // open: out_3
  D_Latch d_latch_12 (.in_1(RCLK2), .in_2(d_latch_3_out_4), .out_4(d_latch_12_out_4));  // open: out_3
  D_Latch d_latch_13 (.in_1(RCLK2), .in_2(d_latch_4_out_4), .out_4(d_latch_13_out_4));  // open: out_3
  D_Latch d_latch_14 (.in_1(RCLK2), .in_2(d_latch_5_out_4), .out_4(d_latch_14_out_4));  // open: out_3
  D_Latch d_latch_15 (.in_1(RCLK2), .in_2(d_latch_6_out_4), .out_4(d_latch_15_out_4));  // open: out_3
  D_Latch d_latch_16 (.in_1(RCLK2), .in_2(d_latch_7_out_4), .out_4(d_latch_16_out_4));  // open: out_3
  D_Latch d_latch_17 (.in_1(RCLK2), .in_2(d_latch_8_out_4), .out_4(d_latch_17_out_4));  // open: out_3
  D_Latch d_latch_18 (.in_1(RCLK2), .in_2(d_latch_9_out_4), .out_4(d_latch_18_out_4));  // open: out_3
  D_Latch d_latch_19 (.in_1(not_5_out), .in_2(AD_IN[0]), .out_4(d_latch_19_out_4));  // open: out_3
  D_Latch d_latch_20 (.in_1(not_5_out), .in_2(RD_IN[0]), .out_4(d_latch_20_out_4));  // open: out_3
  D_Latch d_latch_21 (.in_1(not_5_out), .in_2(AD_IN[1]), .out_4(d_latch_21_out_4));  // open: out_3
  D_Latch d_latch_22 (.in_1(not_5_out), .in_2(RD_IN[1]), .out_4(d_latch_22_out_4));  // open: out_3
  D_Latch d_latch_23 (.in_1(not_5_out), .in_2(AD_IN[2]), .out_4(d_latch_23_out_4));  // open: out_3
  D_Latch d_latch_24 (.in_1(not_5_out), .in_2(RD_IN[2]), .out_4(d_latch_24_out_4));  // open: out_3
  D_Latch _109 (.in_1(not_5_out), .in_2(AD_IN[3]), .out_4(_109_out_4));  // open: out_3
  D_Latch d_latch_25 (.in_1(not_5_out), .in_2(RD_IN[3]), .out_4(d_latch_25_out_4));  // open: out_3
  D_Latch d_latch_26 (.in_1(not_5_out), .in_2(AD_IN[4]), .out_4(d_latch_26_out_4));  // open: out_3
  D_Latch d_latch_27 (.in_1(not_5_out), .in_2(RD_IN[4]), .out_4(d_latch_27_out_4));  // open: out_3
  D_Latch d_latch_28 (.in_1(not_5_out), .in_2(AD_IN[5]), .out_4(d_latch_28_out_4));  // open: out_3
  D_Latch d_latch_29 (.in_1(not_5_out), .in_2(RD_IN[5]), .out_4(d_latch_29_out_4));  // open: out_3
  D_Latch d_latch_30 (.in_1(not_5_out), .in_2(AD_IN[6]), .out_4(d_latch_30_out_4));  // open: out_3
  D_Latch d_latch_31 (.in_1(not_5_out), .in_2(RD_IN[6]), .out_4(d_latch_31_out_4));  // open: out_3
  D_Latch d_latch_32 (.in_1(not_5_out), .in_2(AD_IN[7]), .out_4(d_latch_32_out_4));  // open: out_3
  D_Latch d_latch_33 (.in_1(not_5_out), .in_2(RD_IN[7]), .out_4(d_latch_33_out_4));  // open: out_3
  not not_6 (not_6_out, d_latch_1_out_4);
  or u__80 (_80_out, not_3_out, RCLK2);
  or _66 (_66_out, d_latch_13_out_4, d_latch_14_out_4);
  not not_7 (not_7_out, d_latch_73_out_4);
  assign AD_BUS_READ[0] = not_7_out ? ~d_latch_19_out_4 : 1'bz;  // Controlled_Inverter controlled_inverter_1
  assign RD_BUS_READ[0] = not_7_out ? ~d_latch_20_out_4 : 1'bz;  // Controlled_Inverter controlled_inverter_2
  assign AD_BUS_READ[1] = not_7_out ? ~d_latch_21_out_4 : 1'bz;  // Controlled_Inverter controlled_inverter_3
  assign RD_BUS_READ[1] = not_7_out ? ~d_latch_22_out_4 : 1'bz;  // Controlled_Inverter controlled_inverter_4
  assign AD_BUS_READ[2] = not_7_out ? ~d_latch_23_out_4 : 1'bz;  // Controlled_Inverter controlled_inverter_5
  assign RD_BUS_READ[2] = not_7_out ? ~d_latch_24_out_4 : 1'bz;  // Controlled_Inverter controlled_inverter_6
  assign AD_BUS_READ[3] = not_7_out ? ~_109_out_4 : 1'bz;  // Controlled_Inverter controlled_inverter_7
  assign RD_BUS_READ[3] = not_7_out ? ~d_latch_25_out_4 : 1'bz;  // Controlled_Inverter controlled_inverter_8
  assign AD_BUS_READ[4] = not_7_out ? ~d_latch_26_out_4 : 1'bz;  // Controlled_Inverter controlled_inverter_9
  assign RD_BUS_READ[4] = not_7_out ? ~d_latch_27_out_4 : 1'bz;  // Controlled_Inverter controlled_inverter_10
  assign AD_BUS_READ[5] = not_7_out ? ~d_latch_28_out_4 : 1'bz;  // Controlled_Inverter controlled_inverter_11
  assign RD_BUS_READ[5] = not_7_out ? ~d_latch_29_out_4 : 1'bz;  // Controlled_Inverter controlled_inverter_12
  assign AD_BUS_READ[6] = not_7_out ? ~d_latch_30_out_4 : 1'bz;  // Controlled_Inverter controlled_inverter_13
  assign RD_BUS_READ[6] = not_7_out ? ~d_latch_31_out_4 : 1'bz;  // Controlled_Inverter controlled_inverter_14
  assign AD_BUS_READ[7] = not_7_out ? ~d_latch_32_out_4 : 1'bz;  // Controlled_Inverter controlled_inverter_15
  assign RD_BUS_READ[7] = not_7_out ? ~d_latch_33_out_4 : 1'bz;  // Controlled_Inverter controlled_inverter_16
  D_Latch d_latch_34 (.in_1(DCLK1), .in_2(not_6_out), .out_4(d_latch_34_out_4));  // open: out_3
  D_Latch d_latch_35 (.in_1(DCLK1), .in_2(d_latch_1_out_4), .out_4(d_latch_35_out_4));  // open: out_3
  D_Latch d_latch_36 (.in_1(DCLK1), .in_2(_67_out), .out_4(d_latch_36_out_4));  // open: out_3
  nand _80_2 (_80_2_out, DCLK1, _80_out);
  or _43 (_43_out, d_latch_11_out_4, d_latch_12_out_4, _66_out);
  or _12 (_12_out, d_latch_16_out_4, d_latch_15_out_4);
  or u__27 (_27_out, d_latch_15_out_4, _14);
  or _8 (_8_out, d_latch_16_out_4, _24);
  and _76 (_76_out, _31, _18);
  and _78 (_78_out, RCLK2, d_latch_10_out_4);
  and _79 (_79_out, RCLK2, _18);
  and _77 (_77_out, _18, RCLK1);
  not not_8 (not_8_out, _79_out);
  not not_9 (not_9_out, not_8_out);
  D_Latch d_latch_37 (.in_1(DCLK2), .in_2(d_latch_34_out_4), .out_4(d_latch_37_out_4));  // open: out_3
  D_Latch d_latch_38 (.in_1(DCLK2), .in_2(d_latch_35_out_4), .out_4(d_latch_38_out_4));  // open: out_3
  D_Latch d_latch_39 (.in_1(DCLK2), .in_2(d_latch_36_out_4), .out_4(nCE0));  // open: out_3
  D_Latch d_latch_40 (.in_1(RCLK1), .in_2(_43_out), .out_4(d_latch_40_out_4));  // open: out_3
  D_Latch d_latch_41 (.in_1(RCLK1), .in_2(d_latch_12_out_4), .out_4(d_latch_41_out_4));  // open: out_3
  D_Latch d_latch_42 (.in_1(RCLK1), .in_2(_66_out), .out_4(d_latch_42_out_4));  // open: out_3
  D_Latch d_latch_43 (.in_1(RCLK1), .in_2(_12_out), .out_4(d_latch_43_out_4));  // open: out_3
  D_Latch d_latch_44 (.in_1(RCLK1), .in_2(_27_out), .out_4(d_latch_44_out_4));  // open: out_3
  D_Latch d_latch_45 (.in_1(RCLK1), .in_2(_8_out), .out_4(d_latch_45_out_4));  // open: out_3
  D_Latch d_latch_46 (.in_1(RCLK1), .in_2(d_latch_18_out_4), .out_4(d_latch_46_out_4));  // open: out_3
  D_Latch d_latch_47 (.in_1(RCLK1), .in_2(_76_out), .out_4(d_latch_47_out_4));  // open: out_3
  D_Latch d_latch_48 (.in_1(not_9_out), .in_2(AD_BUS_READ[0]), .out_4(d_latch_48_out_4));  // open: out_3
  D_Latch d_latch_49 (.in_1(not_9_out), .in_2(RD_BUS_READ[0]), .out_4(d_latch_49_out_4));  // open: out_3
  D_Latch d_latch_50 (.in_1(not_9_out), .in_2(AD_BUS_READ[1]), .out_4(d_latch_50_out_4));  // open: out_3
  D_Latch d_latch_51 (.in_1(not_9_out), .in_2(RD_BUS_READ[1]), .out_4(d_latch_51_out_4));  // open: out_3
  D_Latch d_latch_52 (.in_1(not_9_out), .in_2(AD_BUS_READ[2]), .out_4(d_latch_52_out_4));  // open: out_3
  D_Latch d_latch_53 (.in_1(not_9_out), .in_2(RD_BUS_READ[2]), .out_4(d_latch_53_out_4));  // open: out_3
  D_Latch d_latch_54 (.in_1(not_9_out), .in_2(AD_BUS_READ[3]), .out_4(d_latch_54_out_4));  // open: out_3
  D_Latch d_latch_55 (.in_1(not_9_out), .in_2(RD_BUS_READ[3]), .out_4(d_latch_55_out_4));  // open: out_3
  D_Latch d_latch_56 (.in_1(not_9_out), .in_2(AD_BUS_READ[4]), .out_4(d_latch_56_out_4));  // open: out_3
  D_Latch d_latch_57 (.in_1(not_9_out), .in_2(RD_BUS_READ[4]), .out_4(d_latch_57_out_4));  // open: out_3
  D_Latch d_latch_58 (.in_1(not_9_out), .in_2(AD_BUS_READ[5]), .out_4(d_latch_58_out_4));  // open: out_3
  D_Latch d_latch_59 (.in_1(not_9_out), .in_2(RD_BUS_READ[5]), .out_4(d_latch_59_out_4));  // open: out_3
  D_Latch d_latch_60 (.in_1(not_9_out), .in_2(AD_BUS_READ[6]), .out_4(d_latch_60_out_4));  // open: out_3
  D_Latch d_latch_61 (.in_1(not_9_out), .in_2(RD_BUS_READ[6]), .out_4(d_latch_61_out_4));  // open: out_3
  D_Latch d_latch_62 (.in_1(not_9_out), .in_2(AD_BUS_READ[7]), .out_4(d_latch_62_out_4));  // open: out_3
  D_Latch d_latch_63 (.in_1(not_9_out), .in_2(RD_BUS_READ[7]), .out_4(d_latch_63_out_4));  // open: out_3
  D_Latch d_latch_64 (.in_1(DCLK1), .in_2(not_10_out), .out_4(d_latch_64_out_4));  // open: out_3
  not not_10 (not_10_out, d_latch_74_out_4);
  D_Latch d_latch_65 (.in_1(DCLK1), .in_2(d_latch_37_out_4), .out_4(d_latch_65_out_4));  // open: out_3
  D_Latch d_latch_66 (.in_1(DCLK1), .in_2(d_latch_38_out_4), .out_4(d_latch_66_out_4));  // open: out_3
  D_Latch d_latch_67 (.in_1(RCLK2), .in_2(d_latch_41_out_4), .out_4(d_latch_67_out_4));  // open: out_3
  D_Latch d_latch_68 (.in_1(RCLK2), .in_2(d_latch_42_out_4), .out_4(d_latch_68_out_4));  // open: out_3
  D_Latch d_latch_69 (.in_1(RCLK2), .in_2(d_latch_43_out_4), .out_4(d_latch_69_out_4));  // open: out_3
  D_Latch d_latch_70 (.in_1(RCLK2), .in_2(d_latch_44_out_4), .out_4(d_latch_70_out_4));  // open: out_3
  D_Latch d_latch_71 (.in_1(RCLK2), .in_2(d_latch_45_out_4), .out_4(d_latch_71_out_4));  // open: out_3
  D_Latch d_latch_72 (.in_1(RCLK2), .in_2(d_latch_46_out_4), .out_4(d_latch_72_out_4));  // open: out_3
  D_Latch d_latch_73 (.in_1(RCLK2), .in_2(d_latch_47_out_4), .out_4(d_latch_73_out_4));  // open: out_3
  not not_11 (not_11_out, d_latch_17_out_4);
  not not_12 (not_12_out, not_11_out);
  Multiplexer #(.disabled(0), .enable("false")) multiplexer_2 (
    .in0(d_latch_48_out_4), .in1(d_latch_19_out_4), .out(multiplexer_2_out), .sel(not_12_out));
  Multiplexer #(.disabled(0), .enable("false")) multiplexer_3 (
    .in0(d_latch_49_out_4), .in1(d_latch_20_out_4), .out(multiplexer_3_out), .sel(not_12_out));
  Multiplexer #(.disabled(0), .enable("false")) multiplexer_4 (
    .in0(d_latch_50_out_4), .in1(d_latch_21_out_4), .out(multiplexer_4_out), .sel(not_12_out));
  Multiplexer #(.disabled(0), .enable("false")) multiplexer_5 (
    .in0(d_latch_51_out_4), .in1(d_latch_22_out_4), .out(multiplexer_5_out), .sel(not_12_out));
  Multiplexer #(.disabled(0), .enable("false")) multiplexer_6 (
    .in0(d_latch_52_out_4), .in1(d_latch_23_out_4), .out(multiplexer_6_out), .sel(not_12_out));
  Multiplexer #(.disabled(0), .enable("false")) multiplexer_7 (
    .in0(d_latch_53_out_4), .in1(d_latch_24_out_4), .out(multiplexer_7_out), .sel(not_12_out));
  Multiplexer #(.disabled(0), .enable("false")) multiplexer_8 (
    .in0(d_latch_54_out_4), .in1(_109_out_4), .out(multiplexer_8_out), .sel(not_12_out));
  Multiplexer #(.disabled(0), .enable("false")) multiplexer_9 (
    .in0(d_latch_55_out_4), .in1(d_latch_25_out_4), .out(multiplexer_9_out), .sel(not_12_out));
  Multiplexer #(.disabled(0), .enable("false")) multiplexer_10 (
    .in0(d_latch_56_out_4), .in1(d_latch_26_out_4), .out(multiplexer_10_out), .sel(not_12_out));
  Multiplexer #(.disabled(0), .enable("false")) multiplexer_11 (
    .in0(d_latch_57_out_4), .in1(d_latch_27_out_4), .out(multiplexer_11_out), .sel(not_12_out));
  Multiplexer #(.disabled(0), .enable("false")) multiplexer_12 (
    .in0(d_latch_58_out_4), .in1(d_latch_28_out_4), .out(multiplexer_12_out), .sel(not_12_out));
  Multiplexer #(.disabled(0), .enable("false")) multiplexer_13 (
    .in0(d_latch_59_out_4), .in1(d_latch_29_out_4), .out(multiplexer_13_out), .sel(not_12_out));
  Multiplexer #(.disabled(0), .enable("false")) multiplexer_14 (
    .in0(d_latch_60_out_4), .in1(d_latch_30_out_4), .out(multiplexer_14_out), .sel(not_12_out));
  Multiplexer #(.disabled(0), .enable("false")) multiplexer_15 (
    .in0(d_latch_61_out_4), .in1(d_latch_31_out_4), .out(multiplexer_15_out), .sel(not_12_out));
  Multiplexer #(.disabled(0), .enable("false")) multiplexer_16 (
    .in0(d_latch_62_out_4), .in1(d_latch_32_out_4), .out(multiplexer_16_out), .sel(not_12_out));
  Multiplexer #(.disabled(0), .enable("false")) multiplexer_17 (
    .in0(d_latch_63_out_4), .in1(d_latch_33_out_4), .out(multiplexer_17_out), .sel(not_12_out));
  not not_13 (not_13_out, d_latch_41_out_4);
  not not_14 (not_14_out, d_latch_43_out_4);
  not not_15 (not_15_out, _78_out);
  not not_16 (not_16_out, not_15_out);
  not not_17 (not_17_out, multiplexer_2_out);
  not not_18 (not_18_out, multiplexer_3_out);
  not not_19 (not_19_out, multiplexer_4_out);
  not _177 (_177_out, _181_2_out);
  not not_20 (not_20_out, multiplexer_5_out);
  not not_21 (not_21_out, multiplexer_6_out);
  not not_22 (not_22_out, multiplexer_7_out);
  not not_23 (not_23_out, multiplexer_8_out);
  not not_24 (not_24_out, multiplexer_9_out);
  not not_25 (not_25_out, multiplexer_10_out);
  not not_26 (not_26_out, multiplexer_11_out);
  not not_27 (not_27_out, multiplexer_12_out);
  not not_28 (not_28_out, multiplexer_13_out);
  not not_29 (not_29_out, multiplexer_14_out);
  not not_30 (not_30_out, multiplexer_15_out);
  not not_31 (not_31_out, multiplexer_16_out);
  not not_32 (not_32_out, multiplexer_17_out);
  D_Latch d_latch_74 (.in_1(DCLK2), .in_2(d_latch_65_out_4), .out_4(d_latch_74_out_4));  // open: out_3
  D_Latch d_latch_75 (.in_1(DCLK2), .in_2(d_latch_66_out_4), .out_4(d_latch_75_out_4));  // open: out_3
  or _25 (_25_out, not_13_out, d_latch_67_out_4);
  not not_33 (not_33_out, _26_out);
  or u__26 (_26_out, not_14_out, d_latch_69_out_4);
  D_Latch d_latch_76 (.in_1(not_16_out), .in_2(not_17_out), .out_3(d_latch_76_out_3));  // open: out_4
  D_Latch d_latch_77 (.in_1(not_16_out), .in_2(not_18_out), .out_3(d_latch_77_out_3));  // open: out_4
  D_Latch d_latch_78 (.in_1(not_16_out), .in_2(not_19_out), .out_3(d_latch_78_out_3));  // open: out_4
  D_Latch d_latch_79 (.in_1(not_16_out), .in_2(not_20_out), .out_3(d_latch_79_out_3));  // open: out_4
  D_Latch d_latch_80 (.in_1(not_16_out), .in_2(not_21_out), .out_3(d_latch_80_out_3));  // open: out_4
  D_Latch d_latch_81 (.in_1(not_16_out), .in_2(not_22_out), .out_3(d_latch_81_out_3));  // open: out_4
  D_Latch d_latch_82 (.in_1(not_16_out), .in_2(not_23_out), .out_3(d_latch_82_out_3));  // open: out_4
  D_Latch d_latch_83 (.in_1(not_16_out), .in_2(not_24_out), .out_3(d_latch_83_out_3));  // open: out_4
  D_Latch d_latch_84 (.in_1(not_16_out), .in_2(not_25_out), .out_3(d_latch_84_out_3));  // open: out_4
  D_Latch d_latch_85 (.in_1(not_16_out), .in_2(not_26_out), .out_3(d_latch_85_out_3));  // open: out_4
  D_Latch d_latch_86 (.in_1(not_16_out), .in_2(not_27_out), .out_3(d_latch_86_out_3));  // open: out_4
  D_Latch d_latch_87 (.in_1(not_16_out), .in_2(not_28_out), .out_3(d_latch_87_out_3));  // open: out_4
  D_Latch d_latch_88 (.in_1(not_16_out), .in_2(not_29_out), .out_3(d_latch_88_out_3));  // open: out_4
  D_Latch d_latch_89 (.in_1(not_16_out), .in_2(not_30_out), .out_3(d_latch_89_out_3));  // open: out_4
  D_Latch d_latch_90 (.in_1(not_16_out), .in_2(not_31_out), .out_3(d_latch_90_out_3));  // open: out_4
  D_Latch d_latch_91 (.in_1(not_16_out), .in_2(not_32_out), .out_3(d_latch_91_out_3));  // open: out_4
  not not_34 (not_34_out, _25_2_out);
  nand _25_2 (_25_2_out, _25_out, not_33_out);
  and u__53 (_53_out, d_latch_65_out_4, d_latch_64_out_4);
  not not_35 (not_35_out, M5);
  not not_36 (not_36_out, not_35_out);
  Multiplexer #(.disabled(0), .enable("false")) multiplexer_18 (
    .in0(_39), .in1(in_23[0]), .out(multiplexer_18_out), .sel(not_36_out));
  Multiplexer #(.disabled(0), .enable("false")) multiplexer_19 (
    .in0(_177_out), .in1(in_23[1]), .out(multiplexer_19_out), .sel(not_36_out));
  Multiplexer #(.disabled(0), .enable("false")) multiplexer_20 (
    .in0(in_23[1]), .in1(in_23[2]), .out(multiplexer_20_out), .sel(not_36_out));
  Multiplexer #(.disabled(0), .enable("false")) multiplexer_21 (
    .in0(in_23[2]), .in1(in_23[3]), .out(multiplexer_21_out), .sel(not_36_out));
  Multiplexer #(.disabled(0), .enable("false")) multiplexer_22 (
    .in0(in_23[3]), .in1(in_23[4]), .out(multiplexer_22_out), .sel(not_36_out));
  Multiplexer #(.disabled(0), .enable("false")) multiplexer_23 (
    .in0(in_23[4]), .in1(in_23[5]), .out(multiplexer_23_out), .sel(not_36_out));
  Multiplexer #(.disabled(0), .enable("false")) multiplexer_24 (
    .in0(in_23[5]), .in1(in_23[6]), .out(multiplexer_24_out), .sel(not_36_out));
  Multiplexer #(.disabled(0), .enable("false")) multiplexer_25 (
    .in0(in_23[6]), .in1(in_23[7]), .out(multiplexer_25_out), .sel(not_36_out));
  and _40 (nWE0, d_latch_64_out_4, d_latch_65_out_4, d_latch_70_out_4);
  and u__39 (nWE1, d_latch_65_out_4, d_latch_71_out_4, d_latch_64_out_4);
  not not_37 (not_37_out, _128k);
  not not_38 (not_38_out, not_37_out);
  nand _49 (_49_out, d_latch_74_out_4, d_latch_37_out_4);
  nand _50 (_50_out, d_latch_37_out_4, d_latch_75_out_4);
  nand _51 (_51_out, d_latch_38_out_4, 1'b1);
  not not_39 (not_39_out, _77_out);
  not not_40 (not_40_out, not_39_out);
  Multiplexer #(.disabled(0), .enable("false")) multiplexer_26 (
    .in0(in_19[0]), .in1(_208_out), .out(multiplexer_26_out), .sel(not_38_out));
  Multiplexer #(.disabled(0), .enable("false")) multiplexer_27 (
    .in0(_177_out), .in1(in_19[2]), .out(multiplexer_27_out), .sel(not_38_out));
  Multiplexer #(.disabled(0), .enable("false")) multiplexer_28 (
    .in0(in_19[2]), .in1(in_19[3]), .out(multiplexer_28_out), .sel(not_38_out));
  Multiplexer #(.disabled(0), .enable("false")) multiplexer_29 (
    .in0(in_19[3]), .in1(in_19[4]), .out(multiplexer_29_out), .sel(not_38_out));
  Multiplexer #(.disabled(0), .enable("false")) multiplexer_30 (
    .in0(in_19[4]), .in1(in_19[5]), .out(multiplexer_30_out), .sel(not_38_out));
  Multiplexer #(.disabled(0), .enable("false")) multiplexer_31 (
    .in0(in_19[5]), .in1(in_19[6]), .out(multiplexer_31_out), .sel(not_38_out));
  Multiplexer #(.disabled(0), .enable("false")) multiplexer_32 (
    .in0(in_19[6]), .in1(in_19[7]), .out(multiplexer_32_out), .sel(not_38_out));
  Multiplexer #(.disabled(0), .enable("false")) multiplexer_33 (
    .in0(in_19[7]), .in1(multiplexer_1_out), .out(multiplexer_33_out), .sel(not_38_out));
  not not_41 (not_41_out, not_42_out);
  not not_42 (not_42_out, d_latch_37_out_4);
  not not_43 (not_43_out[0], _49_out);
  not not_44 (not_43_out[1], _50_out);
  not not_45 (not_43_out[2], _51_out);
  D_Latch d_latch_92 (.in_1(not_40_out), .in_2(multiplexer_18_out), .out_3(d_latch_92_out_3));  // open: out_4
  D_Latch d_latch_93 (.in_1(not_40_out), .in_2(multiplexer_26_out), .out_3(d_latch_93_out_3));  // open: out_4
  D_Latch d_latch_94 (.in_1(not_40_out), .in_2(multiplexer_19_out), .out_3(d_latch_94_out_3));  // open: out_4
  D_Latch d_latch_95 (.in_1(not_40_out), .in_2(multiplexer_27_out), .out_3(d_latch_95_out_3));  // open: out_4
  D_Latch d_latch_96 (.in_1(not_40_out), .in_2(multiplexer_20_out), .out_3(d_latch_96_out_3));  // open: out_4
  D_Latch d_latch_97 (.in_1(not_40_out), .in_2(multiplexer_28_out), .out_3(d_latch_97_out_3));  // open: out_4
  D_Latch d_latch_98 (.in_1(not_40_out), .in_2(multiplexer_21_out), .out_3(d_latch_98_out_3));  // open: out_4
  D_Latch d_latch_99 (.in_1(not_40_out), .in_2(multiplexer_29_out), .out_3(d_latch_99_out_3));  // open: out_4
  D_Latch d_latch_100 (.in_1(not_40_out), .in_2(multiplexer_22_out), .out_3(d_latch_100_out_3));  // open: out_4
  D_Latch d_latch_101 (.in_1(not_40_out), .in_2(multiplexer_30_out), .out_3(d_latch_101_out_3));  // open: out_4
  D_Latch d_latch_102 (.in_1(not_40_out), .in_2(multiplexer_23_out), .out_3(d_latch_102_out_3));  // open: out_4
  D_Latch d_latch_103 (.in_1(not_40_out), .in_2(multiplexer_31_out), .out_3(d_latch_103_out_3));  // open: out_4
  D_Latch d_latch_104 (.in_1(not_40_out), .in_2(multiplexer_24_out), .out_3(d_latch_104_out_3));  // open: out_4
  D_Latch d_latch_105 (.in_1(not_40_out), .in_2(multiplexer_32_out), .out_3(d_latch_105_out_3));  // open: out_4
  D_Latch d_latch_106 (.in_1(not_40_out), .in_2(multiplexer_25_out), .out_3(d_latch_106_out_3));  // open: out_4
  D_Latch d_latch_107 (.in_1(not_40_out), .in_2(multiplexer_33_out), .out_3(d_latch_107_out_3));  // open: out_4
  not not_46 (not_46_out, not_41_out);
  not not_47 (not_47_out, not_46_out);
  not not_48 (not_48_out, d_latch_74_out_4);
  not not_49 (not_49_out, not_48_out);
  not not_50 (not_50_out, d_latch_68_out_4);
  and _218 (_218_out, d_latch_76_out_3, not_43_out[0]);
  or _218_2 (_218_2_out, _218_out, _218_3_out, _218_4_out);
  and _218_3 (_218_3_out, d_latch_92_out_3, not_43_out[1]);
  and _218_4 (_218_4_out, d_latch_93_out_3, not_43_out[2]);
  and _219 (_219_out, d_latch_78_out_3, not_43_out[0]);
  and _219_2 (_219_2_out, d_latch_94_out_3, not_43_out[1]);
  or _219_3 (_219_3_out, _219_out, _219_2_out, _219_4_out);
  and _219_4 (_219_4_out, d_latch_95_out_3, not_43_out[2]);
  and _220 (_220_out, d_latch_80_out_3, not_43_out[0]);
  or _220_2 (_220_2_out, _220_out, _220_3_out, _220_4_out);
  and _220_3 (_220_3_out, d_latch_96_out_3, not_43_out[1]);
  and _220_4 (_220_4_out, d_latch_97_out_3, not_43_out[2]);
  and _221 (_221_out, d_latch_82_out_3, not_43_out[0]);
  or _221_2 (_221_2_out, _221_out, _221_3_out, _221_4_out);
  and _221_3 (_221_3_out, d_latch_98_out_3, not_43_out[1]);
  and _221_4 (_221_4_out, d_latch_99_out_3, not_43_out[2]);
  and _222 (_222_out, d_latch_84_out_3, not_43_out[0]);
  or or_1 (or_1_out, _222_out, _222_2_out, _222_3_out);
  and _222_2 (_222_2_out, d_latch_100_out_3, not_43_out[1]);
  and _222_3 (_222_3_out, d_latch_101_out_3, not_43_out[2]);
  and _223 (_223_out, d_latch_86_out_3, not_43_out[0]);
  or _223_2 (_223_2_out, _223_out, _223_3_out, _223_4_out);
  and _223_3 (_223_3_out, d_latch_102_out_3, not_43_out[1]);
  and _223_4 (_223_4_out, d_latch_103_out_3, not_43_out[2]);
  and _224 (_224_out, d_latch_88_out_3, not_43_out[0]);
  and _224_2 (_224_2_out, d_latch_104_out_3, not_43_out[1]);
  or _224_3 (_224_3_out, _224_out, _224_2_out, _224_4_out);
  and _224_4 (_224_4_out, d_latch_105_out_3, not_43_out[2]);
  and _225 (_225_out, d_latch_90_out_3, not_43_out[0]);
  and _225_2 (_225_2_out, d_latch_106_out_3, not_43_out[1]);
  or _225_3 (_225_3_out, _225_out, _225_2_out, _225_4_out);
  and _225_4 (_225_4_out, d_latch_107_out_3, not_43_out[2]);
  and _42 (_42_out, not_34_out, d_latch_38_out_4, d_latch_64_out_4);
  and _42_2 (_42_2_out, d_latch_40_out_4, d_latch_40_out_4, not_47_out);
  and _42_3 (_42_3_out, d_latch_40_out_4, d_latch_40_out_4, d_latch_37_out_4);
  and _41 (_41_out, 1'b1, _7);
  and _41_2 (_41_2_out, d_latch_37_out_4, 1'b1);
  and _41_3 (_41_3_out, _26_out, d_latch_64_out_4);
  and _228 (_228_out, 1'b1, not_49_out);
  and _228_2 (_228_2_out, not_50_out, d_latch_66_out_4);
  and _38 (_38_out, d_latch_66_out_4, d_latch_68_out_4);
  and _38_2 (_38_2_out, d_latch_64_out_4, 1'b1);
  not not_51 (not_51_out, _13);
  not not_52 (not_52_out, not_51_out);
  or _42_4 (nOE1, _42_out, _42_2_out, _42_3_out);
  nor _41_4 (_41_4_out, _41_out, _41_2_out, _41_3_out);
  or _228_3 (nRAS, _228_out, _228_2_out);
  or _38_3 (nCAS, _38_out, _38_2_out);
  Multiplexer #(.disabled(0), .enable("false")) multiplexer_34 (
    .in0(d_latch_77_out_3), .in1(in_19[0]), .out(AD_OUT[0]), .sel(not_52_out));
  Multiplexer #(.disabled(0), .enable("false")) multiplexer_35 (
    .in0(_218_2_out), .in1(_36), .out(RD_OUT[0]), .sel(not_52_out));
  Multiplexer #(.disabled(0), .enable("false")) multiplexer_36 (
    .in0(d_latch_79_out_3), .in1(in_19[1]), .out(AD_OUT[1]), .sel(not_52_out));
  Multiplexer #(.disabled(0), .enable("false")) multiplexer_37 (
    .in0(_219_3_out), .in1(_39), .out(RD_OUT[1]), .sel(not_52_out));
  Multiplexer #(.disabled(0), .enable("false")) multiplexer_38 (
    .in0(d_latch_81_out_3), .in1(in_19[2]), .out(AD_OUT[2]), .sel(not_52_out));
  Multiplexer #(.disabled(0), .enable("false")) multiplexer_39 (
    .in0(_220_2_out), .in1(in_23[0]), .out(RD_OUT[2]), .sel(not_52_out));
  Multiplexer #(.disabled(0), .enable("false")) multiplexer_40 (
    .in0(d_latch_83_out_3), .in1(in_19[3]), .out(AD_OUT[3]), .sel(not_52_out));
  Multiplexer #(.disabled(0), .enable("false")) multiplexer_41 (
    .in0(_221_2_out), .in1(in_23[1]), .out(RD_OUT[3]), .sel(not_52_out));
  Multiplexer #(.disabled(0), .enable("false")) multiplexer_42 (
    .in0(d_latch_85_out_3), .in1(in_19[4]), .out(AD_OUT[4]), .sel(not_52_out));
  Multiplexer #(.disabled(0), .enable("false")) multiplexer_43 (
    .in0(or_1_out), .in1(in_23[2]), .out(RD_OUT[4]), .sel(not_52_out));
  Multiplexer #(.disabled(0), .enable("false")) multiplexer_44 (
    .in0(d_latch_87_out_3), .in1(in_19[5]), .out(AD_OUT[5]), .sel(not_52_out));
  Multiplexer #(.disabled(0), .enable("false")) multiplexer_45 (
    .in0(_223_2_out), .in1(in_23[3]), .out(RD_OUT[5]), .sel(not_52_out));
  Multiplexer #(.disabled(0), .enable("false")) multiplexer_46 (
    .in0(d_latch_89_out_3), .in1(in_19[6]), .out(AD_OUT[6]), .sel(not_52_out));
  Multiplexer #(.disabled(0), .enable("false")) multiplexer_47 (
    .in0(_224_3_out), .in1(in_23[4]), .out(RD_OUT[6]), .sel(not_52_out));
  Multiplexer #(.disabled(0), .enable("false")) multiplexer_48 (
    .in0(d_latch_91_out_3), .in1(in_19[7]), .out(AD_OUT[7]), .sel(not_52_out));
  Multiplexer #(.disabled(0), .enable("false")) multiplexer_49 (
    .in0(_225_3_out), .in1(in_23[5]), .out(RD_OUT[7]), .sel(not_52_out));
  Multiplexer #(.disabled(0), .enable("false")) multiplexer_50 (.in0(_28), .in1(_30), .out(nYS), .sel(not_52_out));
  not not_53 (nSC, _80_2_out);
  not not_54 (AD_RD_DIR_PAD, _41_4_out);

  // Notes on the sheet:
  //   33
  //   178
  //   62
  //   50
  //   52
  //   56
  //   57
  //   63
  //   65
  //   68
  //   69
  //   74
  //   77
  //   81
  //   176
  //   217
  //   37
  //   40
  //   42
  //   AOI21
  //   44
  //   45
  //   AD
  //   30
  //   20
  //   14
  //   15
  //   21
  //   16
  //   13
  //   6
  //   175
  //   5
  //   226
  //   64
  //   65
  //   RD
  //   106
  //   121
  //   107
  //   120
  //   108
  //   119
  //   47
  //   118
  //   55
  //   110
  //   117
  //   59
  //   111
  //   116
  //   67
  //   112
  //   115
  //   113
  //   114
  //   78
  //   29
  //   OAI21
  //   54
  //   70
  //   81
  //   145
  //   99
  //   144
  //   100
  //   143
  //   101
  //   142
  //   103
  //   141
  //   102
  //   140
  //   104
  //   139
  //   105
  //   138
  //   44
  //   18
  //   9
  //   56
  //   57
  //   35
  //   36
  //   10
  //   33
  //   1
  //   3
  //   17
  //   4
  //   152
  //   136
  //   151
  //   137
  //   150
  //   135
  //   149
  //   134
  //   190
  //   133
  //   148
  //   132
  //   147
  //   131
  //   146
  //   130
  //   47
  //   48
  //   45
  //   32
  //   37
  //   7
  //   34
  //   69
  //   192
  //   229
  //   193
  //   182
  //   194
  //   184
  //   195
  //   183
  //   196
  //   186
  //   197
  //   185
  //   199
  //   188
  //   198
  //   187
  //   46
  //   31
  //   23
  //   55
  //   58
  //   189
  //   122
  //   158
  //   123
  //   156
  //   125
  //   157
  //   124
  //   191
  //   127
  //   155
  //   126
  //   154
  //   129
  //   153
  //   128
  //   OAI21
  //   24
  //   74
  //   22
  //   200
  //   201
  //   202
  //   203
  //   204
  //   205
  //   206
  //   207
  //   75
  //   216
  //   215
  //   214
  //   212
  //   213
  //   211
  //   209
  //   59
  //   60
  //   210
  //   179
  //   61
  //   71
  //   72
  //   73
  //   166
  //   167
  //   164
  //   168
  //   165
  //   169
  //   163
  //   170
  //   162
  //   172
  //   161
  //   171
  //   160
  //   173
  //   159
  //   174
  //   28
  //   180
  //   227
  //   1
  //   68
  //   96
  //   95
  //   98
  //   97
  //   94
  //   93
  //   92
  //   91
  //   90
  //   89
  //   88
  //   87
  //   85
  //   84
  //   86
  //   83
  //   82
  //   19
  //   2
  //   TRANSPARENT OUTPUT
endmodule

module FSM (
  input  CLK1,
  input  CLK2,
  input  nCSYNC_IN,
  input  _41,
  input  _42,
  input  SYSRES,
  input  _25,
  input  H40,
  input  M5,
  input  _3,
  input  _54,
  input  _26,
  input  _48,
  input  _86,
  input  _90,
  input  _93,
  input  _98,
  input  _103,
  input  _111,
  input  _112,
  input  _114,
  input  _128,
  input  nHSYNC_IN,
  input  _60,
  input  _24__480i,
  input  _145,
  input  _134,
  input  _129,
  input  _136,
  input  _130,
  input  PAL,
  input  [15:0] DATA_IN,
  input  _126,
  output _52,
  output [8:0] H_POS,
  output nCSYNC_OUT,
  output nHSYNC_OUT,
  output VSYNC_OUT,
  output [15:0] DATA_OUT,
  output _32,
  output _37,
  output _39,
  output _40,
  output _45,
  output _46,
  output _55,
  output _58,
  output _51,
  output _63,
  output _66,
  output _67,
  output _70,
  output _75,
  output _81,
  output _82,
  output _85,
  output _90_2,
  output _94,
  output _100,
  output _104,
  output _105,
  output _113,
  output _116,
  output _49__131,
  output _44,
  output [9:0] VPOS_0,
  output _132,
  output _148,
  output _139,
  output _137,
  output _140,
  output _141
);

  wire _249_out, _251_out, _258_out, _259_out, _260_out, _271_out, _273_out, _280_2_out, _280_3_out,
       _280_out, _283_2_out, _283_out, _284_2_out, _284_out, _289_out, _297_out, _298_out, _299_out,
       _301_out, _307_out, _314_out, _315_out, _316_out, _317_out, _318_out, _433_out, d_ff_1_q,
       d_latch_1_out_4, d_latch_2_out_4, d_latch_3_out_4, d_latch_4_out_4, fsm_hlogic_1__43,
       fsm_hlogic_1__68, fsm_hlogic_1__96, fsm_hlogic_1_n307, fsm_vlogic_1__143, fsm_vlogic_1__149,
       fsm_vlogic_1__150, fsm_vlogic_1__151, fsm_vlogic_1__153, fsm_vlogic_1__160, fsm_vlogic_1_nvsync_1,
       fsm_vlogic_1_odd_even, hpla_1_hpla_0, hpla_1_hpla_1, hpla_1_hpla_2, hpla_1_hpla_3, hpla_1_hpla_4,
       hpla_1_hpla_5, hpla_1_hpla_6, hpla_1_hpla_7, hpla_1_hpla_8, hpla_1_hpla_9, hpla_1_hpla_10,
       hpla_1_hpla_11, hpla_1_hpla_12, hpla_1_hpla_13, hpla_1_hpla_14, hpla_1_hpla_15, hpla_1_hpla_16,
       hpla_1_hpla_17, hpla_1_hpla_18, hpla_1_hpla_19, hpla_1_hpla_20, hpla_1_hpla_21, hpla_1_hpla_22,
       hpla_1_hpla_23, hpla_1_hpla_24, hpla_1_hpla_25, hpla_1_hpla_26, hpla_1_hpla_27, hpla_1_hpla_28,
       hpla_1_hpla_29, hpla_1_hpla_30, hpla_1_hpla_31, hpla_1_hpla_32, hpla_1_hpla_33, hpla_1_hpla_34,
       hpla_1_hpla_35, hpla_1_hpla_36, not_1_out, not_2_out, not_3_out, not_4_out, not_5_out, not_6_out,
       not_7_out, not_8_out, not_9_out, not_10_out, not_11_out, not_12_out, not_13_out, not_14_out,
       not_15_out, not_16_out, not_17_out, not_18_out, not_19_out, not_20_out, vpla_1_vpla_0, vpla_1_vpla_1,
       vpla_1_vpla_2, vpla_1_vpla_3, vpla_1_vpla_4, vpla_1_vpla_5, vpla_1_vpla_6, vpla_1_vpla_7,
       vpla_1_vpla_8;
  wire [2:0] fsm_hlogic_1__1_hpla_in;
  wire [8:0] hv_counter_1_cnt_out, hv_counter_2_cnt_out, multiplexer_1_out, multiplexer_10_out, not_22_out;

  not not_1 (not_1_out, _130);
  nor _318 (_318_out, _52, SYSRES);
  not not_2 (not_2_out, _126);
  D_Flip_Flop d_ff_1 (.clk(CLK2), .D(nCSYNC_IN), .Q(d_ff_1_q));  // open: Qn, preset, en, reset
  and _284 (_284_out, d_latch_4_out_4, _273_out);
  nor _284_2 (_284_2_out, _284_out, _318_out);
  not not_3 (not_3_out, _284_2_out);
  D_Latch d_latch_1 (.in_1(CLK1), .in_2(d_latch_4_out_4), .out_4(d_latch_1_out_4));  // open: out_3
  D_Latch d_latch_2 (.in_1(CLK1), .in_2(not_3_out), .out_4(d_latch_2_out_4));  // open: out_3
  and _258 (_258_out, _49__131, _132);
  D_Latch d_latch_3 (.in_1(CLK2), .in_2(d_latch_1_out_4), .out_4(d_latch_3_out_4));  // open: out_3
  D_Latch d_latch_4 (.in_1(CLK2), .in_2(d_latch_2_out_4), .out_4(d_latch_4_out_4));  // open: out_3
  not not_4 (not_4_out, _134);
  nor _301 (_301_out, fsm_vlogic_1__160, _258_out, SYSRES, _136);
  not not_5 (not_5_out, d_latch_3_out_4);
  not not_6 (not_6_out, _54);
  not not_7 (not_7_out, H40);
  and _280 (_280_out, _49__131, not_4_out, _301_out);
  and _280_2 (_280_2_out, _134, _129, 1'b1);
  not not_8 (not_8_out, _301_out);
  not not_9 (not_9_out, PAL);
  and _298 (_298_out, not_5_out, d_latch_4_out_4, _54);
  and _299 (_299_out, H40, M5, not_6_out);
  and _251 (_251_out, not_6_out, not_7_out);
  and _249 (_249_out, not_7_out, _54);
  and _297 (_297_out, not_7_out, _54, M5);
  or _280_3 (_280_3_out, _280_out, _280_2_out);
  nor _317 (_317_out, not_9_out, not_1_out);
  nor _316 (_316_out, not_1_out, PAL);
  nor _314 (_314_out, not_9_out, M5);
  or _273 (_273_out, d_ff_1_q, fsm_hlogic_1__96);
  or _271 (_271_out, _299_out, _297_out);
  xor _289 (_289_out, fsm_vlogic_1_odd_even, not_9_out);
  nor _315 (_315_out, fsm_vlogic_1_odd_even, not_9_out);
  or _260 (_260_out, _317_out, _314_out);
  or _259 (_259_out, _316_out, _314_out);
  or _307 (_307_out, fsm_hlogic_1_n307, _298_out, SYSRES, _25);
  not not_10 (not_10_out, not_11_out);
  not not_11 (not_11_out, _25);
  not not_12 (not_12_out, _299_out);
  not not_13 (not_13_out, not_8_out);
  not not_14 (not_14_out, not_13_out);
  not not_15 (not_15_out, _136);
  not not_16 (not_16_out, not_15_out);
  not not_17 (not_17_out, _314_out);
  and _283 (_283_out, _41, _42);
  nor _433 (_433_out, _42, _307_out);
  Multiplexer #(.disabled(0), .enable("false")) multiplexer_1 (
    .in0(_299_out), .in1(DATA_IN[0]), .out(multiplexer_1_out[0]), .sel(not_10_out));
  Multiplexer #(.disabled(0), .enable("false")) multiplexer_2 (
    .in0(_251_out), .in1(DATA_IN[1]), .out(multiplexer_1_out[1]), .sel(not_10_out));
  Multiplexer #(.disabled(0), .enable("false")) multiplexer_3 (
    .in0(_249_out), .in1(DATA_IN[2]), .out(multiplexer_1_out[2]), .sel(not_10_out));
  Multiplexer #(.disabled(0), .enable("false")) multiplexer_4 (
    .in0(_271_out), .in1(DATA_IN[3]), .out(multiplexer_1_out[3]), .sel(not_10_out));
  Multiplexer #(.disabled(0), .enable("false")) multiplexer_5 (
    .in0(not_12_out), .in1(DATA_IN[4]), .out(multiplexer_1_out[4]), .sel(not_10_out));
  Multiplexer #(.disabled(0), .enable("false")) multiplexer_6 (
    .in0(1'b0), .in1(DATA_IN[5]), .out(multiplexer_1_out[5]), .sel(not_10_out));
  Multiplexer #(.disabled(0), .enable("false")) multiplexer_7 (
    .in0(1'b1), .in1(DATA_IN[6]), .out(multiplexer_1_out[6]), .sel(not_10_out));
  Multiplexer #(.disabled(0), .enable("false")) multiplexer_8 (
    .in0(1'b1), .in1(DATA_IN[7]), .out(multiplexer_1_out[7]), .sel(not_10_out));
  Multiplexer #(.disabled(0), .enable("false")) multiplexer_9 (
    .in0(1'b1), .in1(DATA_IN[8]), .out(multiplexer_1_out[8]), .sel(not_10_out));
  Multiplexer #(.disabled(0), .enable("false")) multiplexer_10 (
    .in0(_289_out), .in1(DATA_IN[0]), .out(multiplexer_10_out[0]), .sel(not_16_out));
  Multiplexer #(.disabled(0), .enable("false")) multiplexer_11 (
    .in0(_315_out), .in1(DATA_IN[1]), .out(multiplexer_10_out[1]), .sel(not_16_out));
  Multiplexer #(.disabled(0), .enable("false")) multiplexer_12 (
    .in0(not_9_out), .in1(DATA_IN[2]), .out(multiplexer_10_out[2]), .sel(not_16_out));
  Multiplexer #(.disabled(0), .enable("false")) multiplexer_13 (
    .in0(_260_out), .in1(DATA_IN[3]), .out(multiplexer_10_out[3]), .sel(not_16_out));
  Multiplexer #(.disabled(0), .enable("false")) multiplexer_14 (
    .in0(not_1_out), .in1(DATA_IN[4]), .out(multiplexer_10_out[4]), .sel(not_16_out));
  Multiplexer #(.disabled(0), .enable("false")) multiplexer_15 (
    .in0(_259_out), .in1(DATA_IN[5]), .out(multiplexer_10_out[5]), .sel(not_16_out));
  Multiplexer #(.disabled(0), .enable("false")) multiplexer_16 (
    .in0(not_17_out), .in1(DATA_IN[6]), .out(multiplexer_10_out[6]), .sel(not_16_out));
  Multiplexer #(.disabled(0), .enable("false")) multiplexer_17 (
    .in0(1'b1), .in1(DATA_IN[7]), .out(multiplexer_10_out[7]), .sel(not_16_out));
  Multiplexer #(.disabled(0), .enable("false")) multiplexer_18 (
    .in0(1'b1), .in1(DATA_IN[8]), .out(multiplexer_10_out[8]), .sel(not_16_out));
  nor _283_2 (_283_2_out, _283_out, _433_out);
  not not_18 (not_18_out, _307_out);
  not not_19 (not_19_out, _283_2_out);
  not not_20 (not_20_out, not_18_out);
  HV_COUNTER hv_counter_1 (
    .CLK1(CLK1), .CLK2(CLK2), .CIN(not_19_out), .RES(1'b0), .LOAD(not_20_out), .VAL(multiplexer_1_out),
    .CNT_OUT(hv_counter_1_cnt_out));
  HV_COUNTER hv_counter_2 (
    .CLK1(CLK1), .CLK2(CLK2), .CIN(_280_3_out), .RES(1'b0), .LOAD(not_14_out), .VAL(multiplexer_10_out),
    .CNT_OUT(hv_counter_2_cnt_out));
  assign H_POS = ~not_22_out;  // NOT_Gate not_21, 9 bits wide
  assign not_22_out = ~hv_counter_1_cnt_out;  // NOT_Gate not_22, 9 bits wide
  VPLA vpla_1 (
    .ODD_EVEN(fsm_vlogic_1_odd_even), .B(_145), .nPAL(not_9_out), .PAL(PAL), ._2(not_2_out), ._3(not_1_out),
    .M5(M5), .V8(hv_counter_2_cnt_out[8]), .V7(hv_counter_2_cnt_out[7]), .V6(hv_counter_2_cnt_out[6]),
    .V5(hv_counter_2_cnt_out[5]), .V4(hv_counter_2_cnt_out[4]), .V3(hv_counter_2_cnt_out[3]),
    .V2(hv_counter_2_cnt_out[2]), .V1(hv_counter_2_cnt_out[1]), .V0(hv_counter_2_cnt_out[0]),
    .VPLA_0(vpla_1_vpla_0), .VPLA_1(vpla_1_vpla_1), .VPLA_2(vpla_1_vpla_2), .VPLA_3(vpla_1_vpla_3),
    .VPLA_4(vpla_1_vpla_4), .VPLA_5(vpla_1_vpla_5), .VPLA_6(vpla_1_vpla_6), .VPLA_7(vpla_1_vpla_7),
    .VPLA_8(vpla_1_vpla_8));
  HPLA hpla_1 (
    ._0(_3), .M5(M5), .H40(H40), .H8(hv_counter_1_cnt_out[8]), .H7(hv_counter_1_cnt_out[7]),
    .H6(hv_counter_1_cnt_out[6]), .H5(hv_counter_1_cnt_out[5]), .H4(hv_counter_1_cnt_out[4]),
    .H3(hv_counter_1_cnt_out[3]), .H2(hv_counter_1_cnt_out[2]), .H1(hv_counter_1_cnt_out[1]),
    .H0(hv_counter_1_cnt_out[0]), .HPLA_0(hpla_1_hpla_0), .HPLA_1(hpla_1_hpla_1), .HPLA_2(hpla_1_hpla_2),
    .HPLA_3(hpla_1_hpla_3), .HPLA_4(hpla_1_hpla_4), .HPLA_5(hpla_1_hpla_5), .HPLA_6(hpla_1_hpla_6),
    .HPLA_7(hpla_1_hpla_7), .HPLA_8(hpla_1_hpla_8), .HPLA_9(hpla_1_hpla_9), .HPLA_10(hpla_1_hpla_10),
    .HPLA_11(hpla_1_hpla_11), .HPLA_12(hpla_1_hpla_12), .HPLA_13(hpla_1_hpla_13), .HPLA_14(hpla_1_hpla_14),
    .HPLA_15(hpla_1_hpla_15), .HPLA_16(hpla_1_hpla_16), .HPLA_17(hpla_1_hpla_17), .HPLA_18(hpla_1_hpla_18),
    .HPLA_19(hpla_1_hpla_19), .HPLA_20(hpla_1_hpla_20), .HPLA_21(hpla_1_hpla_21), .HPLA_22(hpla_1_hpla_22),
    ._2(fsm_hlogic_1__1_hpla_in[1]), ._1(fsm_hlogic_1__1_hpla_in[0]), .C(fsm_vlogic_1__143),
    ._3(fsm_hlogic_1__1_hpla_in[2]), .HPLA_23(hpla_1_hpla_23), .HPLA_24(hpla_1_hpla_24),
    .HPLA_25(hpla_1_hpla_25), .HPLA_26(hpla_1_hpla_26), .HPLA_27(hpla_1_hpla_27), .HPLA_28(hpla_1_hpla_28),
    .HPLA_29(hpla_1_hpla_29), .HPLA_30(hpla_1_hpla_30), .HPLA_31(hpla_1_hpla_31), .HPLA_32(hpla_1_hpla_32),
    .HPLA_34(hpla_1_hpla_34), .HPLA_35(hpla_1_hpla_35), .HPLA_36(hpla_1_hpla_36), .HPLA_33(hpla_1_hpla_33));
  FSM_VLOGIC fsm_vlogic_1 (
    .CLK2(CLK2), .CLK1(CLK1), .VPLA_0(vpla_1_vpla_0), ._138(_60), .VPLA_8(vpla_1_vpla_8),
    .VPLA_1(vpla_1_vpla_1), .VPLA_2(vpla_1_vpla_2), ._156(_44), .SYSRES(SYSRES), .VPLA_3(vpla_1_vpla_3),
    .VPLA_4(vpla_1_vpla_4), .VPLA_5(vpla_1_vpla_5), .VPLA_6(vpla_1_vpla_6), .VPLA_7(vpla_1_vpla_7), .M5(M5),
    ._154(fsm_hlogic_1__43), ._158(fsm_hlogic_1__68), ._161(d_ff_1_q), ._157(_52), ._155(_54), ._145(_145),
    ._132(_132), ._143(fsm_vlogic_1__143), ._137(_137), ._150(fsm_vlogic_1__150), ._139(_139), ._148(_148),
    ._140(_140), ._141(_141), ._153(fsm_vlogic_1__153), ._151(fsm_vlogic_1__151), ._149(fsm_vlogic_1__149),
    ._160(fsm_vlogic_1__160), .ODD_EVEN(fsm_vlogic_1_odd_even), .nVSYNC_1(fsm_vlogic_1_nvsync_1));
  FSM_HLOGIC fsm_hlogic_1 (
    .CLK2(CLK2), .CLK1(CLK1), .HPLA_2(hpla_1_hpla_2), .HPLA_3(hpla_1_hpla_3), .HPLA_4(hpla_1_hpla_4),
    .HPLA_5(hpla_1_hpla_5), .HPLA_6(hpla_1_hpla_6), .HPLA_7(hpla_1_hpla_7), .HPLA_8(hpla_1_hpla_8),
    .HPLA_9(hpla_1_hpla_9), .HPLA_10(hpla_1_hpla_10), .HPLA_11(hpla_1_hpla_11), .HPLA_12(hpla_1_hpla_12),
    .HPLA_13(hpla_1_hpla_13), .HPLA_14(hpla_1_hpla_14), .HPLA_15(hpla_1_hpla_15), .HPLA_16(hpla_1_hpla_16),
    .HPLA_17(hpla_1_hpla_17), .HPLA_18(hpla_1_hpla_18), .HPLA_19(hpla_1_hpla_19), .HPLA_20(hpla_1_hpla_20),
    .HPLA_21(hpla_1_hpla_21), .HPLA_22(hpla_1_hpla_22), .HPLA_23(hpla_1_hpla_23), .HPLA_24(hpla_1_hpla_24),
    .HPLA_25(hpla_1_hpla_25), .HPLA_26(hpla_1_hpla_26), .HPLA_27(hpla_1_hpla_27), .HPLA_28(hpla_1_hpla_28),
    .HPLA_29(hpla_1_hpla_29), .HPLA_30(hpla_1_hpla_30), .HPLA_31(hpla_1_hpla_31), .HPLA_32(hpla_1_hpla_32),
    .HPLA_33(hpla_1_hpla_33), .HPLA_34(hpla_1_hpla_34), .HPLA_35(hpla_1_hpla_35), .HPLA_36(hpla_1_hpla_36),
    ._111(_111), ._68(fsm_hlogic_1__68), .nCSYNC_OUT(nCSYNC_OUT), ._61(_51), ._63(_63), ._46(_46),
    ._113(_113), .SYSRES(SYSRES), .M5(M5), .nHSYNC_OUT(nHSYNC_OUT), ._96(fsm_hlogic_1__96), ._112(_112),
    .VSYNC_OUT(VSYNC_OUT), ._48(_48), .nVSYNC_1(fsm_vlogic_1_nvsync_1), ._90(_90), .nHSYNC_IN(nHSYNC_IN),
    ._49(_49__131), ._43(fsm_hlogic_1__43), ._44(_44), ._40(_40), ._26(_26), ._58(_58), ._66(_66), ._75(_75),
    ._90_2(_90_2), ._100(_100), ._104(_104), ._116(_116), ._37(_37), ._67(_67), ._55(_55), ._45(_45),
    ._39(_39), ._94(_94), ._86(_86), ._93(_93), ._98(_98), ._70(_70), ._81(_81), ._105(_105), ._85(_85),
    ._82(_82), ._128(_128), ._32(_32), ._3_HPLA_IN(fsm_hlogic_1__1_hpla_in[2]), ._87(_307_out),
    ._2_HPLA_IN(fsm_hlogic_1__1_hpla_in[1]), ._114(_114), ._103(_103), ._107__54(_54), .D_OUT(DATA_OUT),
    ._69(fsm_vlogic_1__150), ._62(_148), ._60(_60), ._72(fsm_vlogic_1__151), ._73(fsm_vlogic_1__149),
    ._74(fsm_vlogic_1__153), ._52(_52), .HPLA_1(hpla_1_hpla_1), .HPLA_0(hpla_1_hpla_0),
    .N307(fsm_hlogic_1_n307), ._1_HPLA_IN(fsm_hlogic_1__1_hpla_in[0]));
  Multiplexer #(.disabled(0), .enable("false")) multiplexer_19 (
    .in0(hv_counter_2_cnt_out[0]), .in1(fsm_vlogic_1_odd_even), .out(VPOS_0[0]), .sel(_24__480i));
  Multiplexer #(.disabled(0), .enable("false")) multiplexer_20 (
    .in0(hv_counter_2_cnt_out[1]), .in1(hv_counter_2_cnt_out[0]), .out(VPOS_0[1]), .sel(_24__480i));
  Multiplexer #(.disabled(0), .enable("false")) multiplexer_21 (
    .in0(hv_counter_2_cnt_out[2]), .in1(hv_counter_2_cnt_out[1]), .out(VPOS_0[2]), .sel(_24__480i));
  Multiplexer #(.disabled(0), .enable("false")) multiplexer_22 (
    .in0(hv_counter_2_cnt_out[3]), .in1(hv_counter_2_cnt_out[2]), .out(VPOS_0[3]), .sel(_24__480i));
  Multiplexer #(.disabled(0), .enable("false")) multiplexer_23 (
    .in0(hv_counter_2_cnt_out[4]), .in1(hv_counter_2_cnt_out[3]), .out(VPOS_0[4]), .sel(_24__480i));
  Multiplexer #(.disabled(0), .enable("false")) multiplexer_24 (
    .in0(hv_counter_2_cnt_out[5]), .in1(hv_counter_2_cnt_out[4]), .out(VPOS_0[5]), .sel(_24__480i));
  Multiplexer #(.disabled(0), .enable("false")) multiplexer_25 (
    .in0(hv_counter_2_cnt_out[6]), .in1(hv_counter_2_cnt_out[5]), .out(VPOS_0[6]), .sel(_24__480i));
  Multiplexer #(.disabled(0), .enable("false")) multiplexer_26 (
    .in0(hv_counter_2_cnt_out[7]), .in1(hv_counter_2_cnt_out[6]), .out(VPOS_0[7]), .sel(_24__480i));
  Multiplexer #(.disabled(0), .enable("false")) multiplexer_27 (
    .in0(hv_counter_2_cnt_out[8]), .in1(hv_counter_2_cnt_out[7]), .out(VPOS_0[8]), .sel(_24__480i));
  Multiplexer #(.disabled(0), .enable("false")) multiplexer_28 (
    .in0(1'b0), .in1(hv_counter_2_cnt_out[8]), .out(VPOS_0[9]), .sel(_24__480i));

  // Notes on the sheet:
  //   2, 71
  //   150
  //   152
  //   29,38,127,144,152
  //   239
  //   POSEDGE DFF
  //   AOI21
  //   129
  //   27,79115,147
  //   73
  //   78
  //   133
  //   117
  //   132
  //   242
  //   153
  //   121
  //   151
  //   304
  //   177
  //   176
  //   173
  //   171
  //   134
  //   170
  //   168
  //   165
  //   163
  //   159
  //   302
  //   303
  //   149
  //   185
  //   162
  //   161
  //   160
  //   154
  //   155
  //   156
  //   157
  //   158
  //   AOI21
  //   305
  //   116
  //   225
  //   118
  //   223
  //   120
  //   221
  //   130
  //   219
  //   131
  //   217
  //   135
  //   216
  //   136
  //   213
  //   138
  //   211
  //   147
  //   212
  //   148
  //   229
  //   230
  //   231
  //   232
  //   233
  //   234
  //   235
  //   236
  //   237
  //   238
endmodule
module VPLA (
  input  ODD_EVEN,
  input  B,
  input  nPAL,
  input  PAL,
  input  _2,
  input  _3,
  input  M5,
  input  V8,
  input  V7,
  input  V6,
  input  V5,
  input  V4,
  input  V3,
  input  V2,
  input  V1,
  input  V0,
  output VPLA_1,
  output VPLA_2,
  output VPLA_0,
  output VPLA_3,
  output VPLA_4,
  output VPLA_5,
  output VPLA_6,
  output VPLA_7,
  output VPLA_8
);

  wire not_1_out, not_2_out, not_3_out, not_4_out, not_5_out, not_6_out, not_7_out, not_8_out, not_9_out,
       not_10_out, not_11_out, transistor_1_out, transistor_12_out, transistor_23_out, transistor_35_out,
       transistor_47_out, transistor_59_out, transistor_71_out, transistor_74_out, transistor_92_out,
       transistor_102_out, transistor_112_out, transistor_122_out, transistor_133_out, transistor_144_out,
       transistor_156_out, transistor_157_out, transistor_180_out, transistor_192_out, transistor_204_out,
       transistor_215_out, transistor_226_out, transistor_237_out, transistor_248_out, transistor_249_out,
       transistor_271_out, transistor_283_out, transistor_295_out, transistor_307_out, transistor_319_out,
       transistor_331_out, transistor_343_out, transistor_344_out, transistor_367_out, transistor_379_out,
       transistor_391_out, transistor_403_out, transistor_415_out, transistor_426_out, transistor_438_out,
       transistor_439_out, transistor_462_out, transistor_474_out, transistor_486_out, transistor_498_out,
       transistor_510_out, transistor_522_out, transistor_534_out;

  not not_1 (not_1_out, ODD_EVEN);
  not not_2 (not_2_out, B);
  not not_3 (not_3_out, V8);
  not not_4 (not_4_out, V7);
  not not_5 (not_5_out, V6);
  not not_6 (not_6_out, V5);
  not not_7 (not_7_out, V4);
  not not_8 (not_8_out, V3);
  not not_9 (not_9_out, V2);
  not not_10 (not_10_out, V1);
  not not_11 (not_11_out, V0);
  Transistor #(.\type ("n")) transistor_1 (.in(1'b0), .out(transistor_1_out), .gate(PAL));
  Transistor #(.\type ("n")) transistor_2 (.in(1'b0), .out(transistor_1_out), .gate(M5));
  Transistor #(.\type ("n")) transistor_3 (.in(1'b0), .out(transistor_1_out), .gate(V8));
  Transistor #(.\type ("n")) transistor_4 (.in(1'b0), .out(transistor_1_out), .gate(not_4_out));
  Transistor #(.\type ("n")) transistor_5 (.in(1'b0), .out(transistor_1_out), .gate(not_5_out));
  Transistor #(.\type ("n")) transistor_6 (.in(1'b0), .out(transistor_1_out), .gate(V5));
  Transistor #(.\type ("n")) transistor_7 (.in(1'b0), .out(transistor_1_out), .gate(not_7_out));
  Transistor #(.\type ("n")) transistor_8 (.in(1'b0), .out(transistor_1_out), .gate(not_8_out));
  Transistor #(.\type ("n")) transistor_9 (.in(1'b0), .out(transistor_1_out), .gate(V2));
  Transistor #(.\type ("n")) transistor_10 (.in(1'b0), .out(transistor_1_out), .gate(not_10_out));
  Transistor #(.\type ("n")) transistor_11 (.in(1'b0), .out(transistor_1_out), .gate(V0));
  Pull_Resistor #(.pull(1)) pull_resistor_1 (.node(transistor_1_out));
  Transistor #(.\type ("n")) transistor_12 (.in(1'b0), .out(transistor_12_out), .gate(PAL));
  Transistor #(.\type ("n")) transistor_13 (.in(1'b0), .out(transistor_12_out), .gate(_3));
  Transistor #(.\type ("n")) transistor_14 (.in(1'b0), .out(transistor_12_out), .gate(V8));
  Transistor #(.\type ("n")) transistor_15 (.in(1'b0), .out(transistor_12_out), .gate(not_4_out));
  Transistor #(.\type ("n")) transistor_16 (.in(1'b0), .out(transistor_12_out), .gate(not_5_out));
  Transistor #(.\type ("n")) transistor_17 (.in(1'b0), .out(transistor_12_out), .gate(not_6_out));
  Transistor #(.\type ("n")) transistor_18 (.in(1'b0), .out(transistor_12_out), .gate(V4));
  Transistor #(.\type ("n")) transistor_19 (.in(1'b0), .out(transistor_12_out), .gate(not_8_out));
  Transistor #(.\type ("n")) transistor_20 (.in(1'b0), .out(transistor_12_out), .gate(V2));
  Transistor #(.\type ("n")) transistor_21 (.in(1'b0), .out(transistor_12_out), .gate(not_10_out));
  Transistor #(.\type ("n")) transistor_22 (.in(1'b0), .out(transistor_12_out), .gate(V0));
  Pull_Resistor #(.pull(1)) pull_resistor_2 (.node(transistor_12_out));
  Transistor #(.\type ("n")) transistor_23 (.in(1'b0), .out(transistor_23_out), .gate(B));
  Transistor #(.\type ("n")) transistor_24 (.in(1'b0), .out(transistor_23_out), .gate(nPAL));
  Transistor #(.\type ("n")) transistor_25 (.in(1'b0), .out(transistor_23_out), .gate(M5));
  Transistor #(.\type ("n")) transistor_26 (.in(1'b0), .out(transistor_23_out), .gate(V8));
  Transistor #(.\type ("n")) transistor_27 (.in(1'b0), .out(transistor_23_out), .gate(not_4_out));
  Transistor #(.\type ("n")) transistor_28 (.in(1'b0), .out(transistor_23_out), .gate(not_5_out));
  Transistor #(.\type ("n")) transistor_29 (.in(1'b0), .out(transistor_23_out), .gate(not_6_out));
  Transistor #(.\type ("n")) transistor_30 (.in(1'b0), .out(transistor_23_out), .gate(not_7_out));
  Transistor #(.\type ("n")) transistor_31 (.in(1'b0), .out(transistor_23_out), .gate(V3));
  Transistor #(.\type ("n")) transistor_32 (.in(1'b0), .out(transistor_23_out), .gate(V2));
  Transistor #(.\type ("n")) transistor_33 (.in(1'b0), .out(transistor_23_out), .gate(not_10_out));
  Transistor #(.\type ("n")) transistor_34 (.in(1'b0), .out(transistor_23_out), .gate(V0));
  Pull_Resistor #(.pull(1)) pull_resistor_3 (.node(transistor_23_out));
  or or_1 (VPLA_0, transistor_1_out, transistor_12_out, transistor_23_out, transistor_35_out, transistor_47_out, transistor_59_out, transistor_71_out);
  Transistor #(.\type ("n")) transistor_35 (.in(1'b0), .out(transistor_35_out), .gate(B));
  Transistor #(.\type ("n")) transistor_36 (.in(1'b0), .out(transistor_35_out), .gate(nPAL));
  Transistor #(.\type ("n")) transistor_37 (.in(1'b0), .out(transistor_35_out), .gate(_3));
  Transistor #(.\type ("n")) transistor_38 (.in(1'b0), .out(transistor_35_out), .gate(not_3_out));
  Transistor #(.\type ("n")) transistor_39 (.in(1'b0), .out(transistor_35_out), .gate(V7));
  Transistor #(.\type ("n")) transistor_40 (.in(1'b0), .out(transistor_35_out), .gate(V6));
  Transistor #(.\type ("n")) transistor_41 (.in(1'b0), .out(transistor_35_out), .gate(V5));
  Transistor #(.\type ("n")) transistor_42 (.in(1'b0), .out(transistor_35_out), .gate(V4));
  Transistor #(.\type ("n")) transistor_43 (.in(1'b0), .out(transistor_35_out), .gate(V3));
  Transistor #(.\type ("n")) transistor_44 (.in(1'b0), .out(transistor_35_out), .gate(V2));
  Transistor #(.\type ("n")) transistor_45 (.in(1'b0), .out(transistor_35_out), .gate(not_10_out));
  Transistor #(.\type ("n")) transistor_46 (.in(1'b0), .out(transistor_35_out), .gate(V0));
  Pull_Resistor #(.pull(1)) pull_resistor_4 (.node(transistor_35_out));
  Transistor #(.\type ("n")) transistor_47 (.in(1'b0), .out(transistor_47_out), .gate(B));
  Transistor #(.\type ("n")) transistor_48 (.in(1'b0), .out(transistor_47_out), .gate(nPAL));
  Transistor #(.\type ("n")) transistor_49 (.in(1'b0), .out(transistor_47_out), .gate(_2));
  Transistor #(.\type ("n")) transistor_50 (.in(1'b0), .out(transistor_47_out), .gate(not_3_out));
  Transistor #(.\type ("n")) transistor_51 (.in(1'b0), .out(transistor_47_out), .gate(V7));
  Transistor #(.\type ("n")) transistor_52 (.in(1'b0), .out(transistor_47_out), .gate(V6));
  Transistor #(.\type ("n")) transistor_53 (.in(1'b0), .out(transistor_47_out), .gate(V5));
  Transistor #(.\type ("n")) transistor_54 (.in(1'b0), .out(transistor_47_out), .gate(V4));
  Transistor #(.\type ("n")) transistor_55 (.in(1'b0), .out(transistor_47_out), .gate(not_8_out));
  Transistor #(.\type ("n")) transistor_56 (.in(1'b0), .out(transistor_47_out), .gate(V2));
  Transistor #(.\type ("n")) transistor_57 (.in(1'b0), .out(transistor_47_out), .gate(not_10_out));
  Transistor #(.\type ("n")) transistor_58 (.in(1'b0), .out(transistor_47_out), .gate(V0));
  Pull_Resistor #(.pull(1)) pull_resistor_5 (.node(transistor_47_out));
  Transistor #(.\type ("n")) transistor_59 (.in(1'b0), .out(transistor_59_out), .gate(not_2_out));
  Transistor #(.\type ("n")) transistor_60 (.in(1'b0), .out(transistor_59_out), .gate(nPAL));
  Transistor #(.\type ("n")) transistor_61 (.in(1'b0), .out(transistor_59_out), .gate(_3));
  Transistor #(.\type ("n")) transistor_62 (.in(1'b0), .out(transistor_59_out), .gate(not_3_out));
  Transistor #(.\type ("n")) transistor_63 (.in(1'b0), .out(transistor_59_out), .gate(V7));
  Transistor #(.\type ("n")) transistor_64 (.in(1'b0), .out(transistor_59_out), .gate(V6));
  Transistor #(.\type ("n")) transistor_65 (.in(1'b0), .out(transistor_59_out), .gate(V5));
  Transistor #(.\type ("n")) transistor_66 (.in(1'b0), .out(transistor_59_out), .gate(V4));
  Transistor #(.\type ("n")) transistor_67 (.in(1'b0), .out(transistor_59_out), .gate(V3));
  Transistor #(.\type ("n")) transistor_68 (.in(1'b0), .out(transistor_59_out), .gate(V2));
  Transistor #(.\type ("n")) transistor_69 (.in(1'b0), .out(transistor_59_out), .gate(V1));
  Transistor #(.\type ("n")) transistor_70 (.in(1'b0), .out(transistor_59_out), .gate(not_11_out));
  Pull_Resistor #(.pull(1)) pull_resistor_6 (.node(transistor_59_out));
  not not_12 (VPLA_1, transistor_74_out);
  Transistor #(.\type ("n")) transistor_71 (.in(1'b0), .out(transistor_71_out), .gate(not_2_out));
  Transistor #(.\type ("n")) transistor_72 (.in(1'b0), .out(transistor_71_out), .gate(nPAL));
  Transistor #(.\type ("n")) transistor_73 (.in(1'b0), .out(transistor_71_out), .gate(_2));
  Transistor #(.\type ("n")) transistor_74 (.in(1'b0), .out(transistor_74_out), .gate(V8));
  Transistor #(.\type ("n")) transistor_75 (.in(1'b0), .out(transistor_71_out), .gate(not_3_out));
  Transistor #(.\type ("n")) transistor_76 (.in(1'b0), .out(transistor_74_out), .gate(V7));
  Transistor #(.\type ("n")) transistor_77 (.in(1'b0), .out(transistor_71_out), .gate(V7));
  Transistor #(.\type ("n")) transistor_78 (.in(1'b0), .out(transistor_74_out), .gate(V6));
  Transistor #(.\type ("n")) transistor_79 (.in(1'b0), .out(transistor_71_out), .gate(V6));
  Transistor #(.\type ("n")) transistor_80 (.in(1'b0), .out(transistor_71_out), .gate(V5));
  Transistor #(.\type ("n")) transistor_81 (.in(1'b0), .out(transistor_74_out), .gate(V5));
  Transistor #(.\type ("n")) transistor_82 (.in(1'b0), .out(transistor_74_out), .gate(V4));
  Transistor #(.\type ("n")) transistor_83 (.in(1'b0), .out(transistor_71_out), .gate(V4));
  Transistor #(.\type ("n")) transistor_84 (.in(1'b0), .out(transistor_74_out), .gate(V3));
  Transistor #(.\type ("n")) transistor_85 (.in(1'b0), .out(transistor_71_out), .gate(not_8_out));
  Transistor #(.\type ("n")) transistor_86 (.in(1'b0), .out(transistor_74_out), .gate(V2));
  Transistor #(.\type ("n")) transistor_87 (.in(1'b0), .out(transistor_71_out), .gate(V2));
  Transistor #(.\type ("n")) transistor_88 (.in(1'b0), .out(transistor_74_out), .gate(V1));
  Transistor #(.\type ("n")) transistor_89 (.in(1'b0), .out(transistor_71_out), .gate(V1));
  Transistor #(.\type ("n")) transistor_90 (.in(1'b0), .out(transistor_74_out), .gate(V0));
  Transistor #(.\type ("n")) transistor_91 (.in(1'b0), .out(transistor_71_out), .gate(not_11_out));
  Pull_Resistor #(.pull(1)) pull_resistor_7 (.node(transistor_74_out));
  Pull_Resistor #(.pull(1)) pull_resistor_8 (.node(transistor_71_out));
  Transistor #(.\type ("n")) transistor_92 (.in(1'b0), .out(transistor_92_out), .gate(M5));
  Transistor #(.\type ("n")) transistor_93 (.in(1'b0), .out(transistor_92_out), .gate(V8));
  Transistor #(.\type ("n")) transistor_94 (.in(1'b0), .out(transistor_92_out), .gate(not_4_out));
  Transistor #(.\type ("n")) transistor_95 (.in(1'b0), .out(transistor_92_out), .gate(not_5_out));
  Transistor #(.\type ("n")) transistor_96 (.in(1'b0), .out(transistor_92_out), .gate(V5));
  Transistor #(.\type ("n")) transistor_97 (.in(1'b0), .out(transistor_92_out), .gate(V4));
  Transistor #(.\type ("n")) transistor_98 (.in(1'b0), .out(transistor_92_out), .gate(V3));
  Transistor #(.\type ("n")) transistor_99 (.in(1'b0), .out(transistor_92_out), .gate(V2));
  Transistor #(.\type ("n")) transistor_100 (.in(1'b0), .out(transistor_92_out), .gate(V1));
  Transistor #(.\type ("n")) transistor_101 (.in(1'b0), .out(transistor_92_out), .gate(V0));
  Pull_Resistor #(.pull(1)) pull_resistor_9 (.node(transistor_92_out));
  nor nor_1 (VPLA_2, transistor_92_out, transistor_102_out, transistor_112_out);
  Transistor #(.\type ("n")) transistor_102 (.in(1'b0), .out(transistor_102_out), .gate(_3));
  Transistor #(.\type ("n")) transistor_103 (.in(1'b0), .out(transistor_102_out), .gate(V8));
  Transistor #(.\type ("n")) transistor_104 (.in(1'b0), .out(transistor_102_out), .gate(not_4_out));
  Transistor #(.\type ("n")) transistor_105 (.in(1'b0), .out(transistor_102_out), .gate(not_5_out));
  Transistor #(.\type ("n")) transistor_106 (.in(1'b0), .out(transistor_102_out), .gate(not_6_out));
  Transistor #(.\type ("n")) transistor_107 (.in(1'b0), .out(transistor_102_out), .gate(V4));
  Transistor #(.\type ("n")) transistor_108 (.in(1'b0), .out(transistor_102_out), .gate(V3));
  Transistor #(.\type ("n")) transistor_109 (.in(1'b0), .out(transistor_102_out), .gate(V2));
  Transistor #(.\type ("n")) transistor_110 (.in(1'b0), .out(transistor_102_out), .gate(V1));
  Transistor #(.\type ("n")) transistor_111 (.in(1'b0), .out(transistor_102_out), .gate(V0));
  Pull_Resistor #(.pull(1)) pull_resistor_10 (.node(transistor_102_out));
  Transistor #(.\type ("n")) transistor_112 (.in(1'b0), .out(transistor_112_out), .gate(_2));
  Transistor #(.\type ("n")) transistor_113 (.in(1'b0), .out(transistor_112_out), .gate(V8));
  Transistor #(.\type ("n")) transistor_114 (.in(1'b0), .out(transistor_112_out), .gate(not_4_out));
  Transistor #(.\type ("n")) transistor_115 (.in(1'b0), .out(transistor_112_out), .gate(not_5_out));
  Transistor #(.\type ("n")) transistor_116 (.in(1'b0), .out(transistor_112_out), .gate(not_6_out));
  Transistor #(.\type ("n")) transistor_117 (.in(1'b0), .out(transistor_112_out), .gate(not_7_out));
  Transistor #(.\type ("n")) transistor_118 (.in(1'b0), .out(transistor_112_out), .gate(V3));
  Transistor #(.\type ("n")) transistor_119 (.in(1'b0), .out(transistor_112_out), .gate(V2));
  Transistor #(.\type ("n")) transistor_120 (.in(1'b0), .out(transistor_112_out), .gate(V1));
  Transistor #(.\type ("n")) transistor_121 (.in(1'b0), .out(transistor_112_out), .gate(V0));
  Pull_Resistor #(.pull(1)) pull_resistor_11 (.node(transistor_112_out));
  Transistor #(.\type ("n")) transistor_122 (.in(1'b0), .out(transistor_122_out), .gate(PAL));
  Transistor #(.\type ("n")) transistor_123 (.in(1'b0), .out(transistor_122_out), .gate(M5));
  Transistor #(.\type ("n")) transistor_124 (.in(1'b0), .out(transistor_122_out), .gate(V8));
  Transistor #(.\type ("n")) transistor_125 (.in(1'b0), .out(transistor_122_out), .gate(not_4_out));
  Transistor #(.\type ("n")) transistor_126 (.in(1'b0), .out(transistor_122_out), .gate(not_5_out));
  Transistor #(.\type ("n")) transistor_127 (.in(1'b0), .out(transistor_122_out), .gate(V5));
  Transistor #(.\type ("n")) transistor_128 (.in(1'b0), .out(transistor_122_out), .gate(not_7_out));
  Transistor #(.\type ("n")) transistor_129 (.in(1'b0), .out(transistor_122_out), .gate(not_8_out));
  Transistor #(.\type ("n")) transistor_130 (.in(1'b0), .out(transistor_122_out), .gate(V2));
  Transistor #(.\type ("n")) transistor_131 (.in(1'b0), .out(transistor_122_out), .gate(V1));
  Transistor #(.\type ("n")) transistor_132 (.in(1'b0), .out(transistor_122_out), .gate(V0));
  Pull_Resistor #(.pull(1)) pull_resistor_12 (.node(transistor_122_out));
  Transistor #(.\type ("n")) transistor_133 (.in(1'b0), .out(transistor_133_out), .gate(PAL));
  Transistor #(.\type ("n")) transistor_134 (.in(1'b0), .out(transistor_133_out), .gate(_3));
  Transistor #(.\type ("n")) transistor_135 (.in(1'b0), .out(transistor_133_out), .gate(V8));
  Transistor #(.\type ("n")) transistor_136 (.in(1'b0), .out(transistor_133_out), .gate(not_4_out));
  Transistor #(.\type ("n")) transistor_137 (.in(1'b0), .out(transistor_133_out), .gate(not_5_out));
  Transistor #(.\type ("n")) transistor_138 (.in(1'b0), .out(transistor_133_out), .gate(not_6_out));
  Transistor #(.\type ("n")) transistor_139 (.in(1'b0), .out(transistor_133_out), .gate(V4));
  Transistor #(.\type ("n")) transistor_140 (.in(1'b0), .out(transistor_133_out), .gate(not_8_out));
  Transistor #(.\type ("n")) transistor_141 (.in(1'b0), .out(transistor_133_out), .gate(V2));
  Transistor #(.\type ("n")) transistor_142 (.in(1'b0), .out(transistor_133_out), .gate(V1));
  Transistor #(.\type ("n")) transistor_143 (.in(1'b0), .out(transistor_133_out), .gate(V0));
  Pull_Resistor #(.pull(1)) pull_resistor_13 (.node(transistor_133_out));
  Transistor #(.\type ("n")) transistor_144 (.in(1'b0), .out(transistor_144_out), .gate(B));
  Transistor #(.\type ("n")) transistor_145 (.in(1'b0), .out(transistor_144_out), .gate(nPAL));
  Transistor #(.\type ("n")) transistor_146 (.in(1'b0), .out(transistor_144_out), .gate(M5));
  Transistor #(.\type ("n")) transistor_147 (.in(1'b0), .out(transistor_144_out), .gate(V8));
  Transistor #(.\type ("n")) transistor_148 (.in(1'b0), .out(transistor_144_out), .gate(not_4_out));
  Transistor #(.\type ("n")) transistor_149 (.in(1'b0), .out(transistor_144_out), .gate(not_5_out));
  Transistor #(.\type ("n")) transistor_150 (.in(1'b0), .out(transistor_144_out), .gate(not_6_out));
  Transistor #(.\type ("n")) transistor_151 (.in(1'b0), .out(transistor_144_out), .gate(not_7_out));
  Transistor #(.\type ("n")) transistor_152 (.in(1'b0), .out(transistor_144_out), .gate(V3));
  Transistor #(.\type ("n")) transistor_153 (.in(1'b0), .out(transistor_144_out), .gate(V2));
  Transistor #(.\type ("n")) transistor_154 (.in(1'b0), .out(transistor_144_out), .gate(V1));
  Transistor #(.\type ("n")) transistor_155 (.in(1'b0), .out(transistor_144_out), .gate(V0));
  Pull_Resistor #(.pull(1)) pull_resistor_14 (.node(transistor_144_out));
  or or_2 (VPLA_3, transistor_122_out, transistor_133_out, transistor_144_out, transistor_156_out, transistor_157_out, transistor_180_out, transistor_192_out);
  Transistor #(.\type ("n")) transistor_156 (.in(1'b0), .out(transistor_156_out), .gate(B));
  Transistor #(.\type ("n")) transistor_157 (.in(1'b0), .out(transistor_157_out), .gate(B));
  Transistor #(.\type ("n")) transistor_158 (.in(1'b0), .out(transistor_157_out), .gate(nPAL));
  Transistor #(.\type ("n")) transistor_159 (.in(1'b0), .out(transistor_156_out), .gate(nPAL));
  Transistor #(.\type ("n")) transistor_160 (.in(1'b0), .out(transistor_157_out), .gate(_2));
  Transistor #(.\type ("n")) transistor_161 (.in(1'b0), .out(transistor_156_out), .gate(_3));
  Transistor #(.\type ("n")) transistor_162 (.in(1'b0), .out(transistor_157_out), .gate(not_3_out));
  Transistor #(.\type ("n")) transistor_163 (.in(1'b0), .out(transistor_156_out), .gate(not_3_out));
  Transistor #(.\type ("n")) transistor_164 (.in(1'b0), .out(transistor_156_out), .gate(V7));
  Transistor #(.\type ("n")) transistor_165 (.in(1'b0), .out(transistor_157_out), .gate(V7));
  Transistor #(.\type ("n")) transistor_166 (.in(1'b0), .out(transistor_156_out), .gate(V6));
  Transistor #(.\type ("n")) transistor_167 (.in(1'b0), .out(transistor_157_out), .gate(V6));
  Transistor #(.\type ("n")) transistor_168 (.in(1'b0), .out(transistor_157_out), .gate(V5));
  Transistor #(.\type ("n")) transistor_169 (.in(1'b0), .out(transistor_156_out), .gate(V5));
  Transistor #(.\type ("n")) transistor_170 (.in(1'b0), .out(transistor_156_out), .gate(V4));
  Transistor #(.\type ("n")) transistor_171 (.in(1'b0), .out(transistor_157_out), .gate(V4));
  Transistor #(.\type ("n")) transistor_172 (.in(1'b0), .out(transistor_156_out), .gate(V3));
  Transistor #(.\type ("n")) transistor_173 (.in(1'b0), .out(transistor_157_out), .gate(not_8_out));
  Transistor #(.\type ("n")) transistor_174 (.in(1'b0), .out(transistor_156_out), .gate(V2));
  Transistor #(.\type ("n")) transistor_175 (.in(1'b0), .out(transistor_157_out), .gate(V2));
  Transistor #(.\type ("n")) transistor_176 (.in(1'b0), .out(transistor_156_out), .gate(V1));
  Transistor #(.\type ("n")) transistor_177 (.in(1'b0), .out(transistor_157_out), .gate(V1));
  Transistor #(.\type ("n")) transistor_178 (.in(1'b0), .out(transistor_156_out), .gate(V0));
  Transistor #(.\type ("n")) transistor_179 (.in(1'b0), .out(transistor_157_out), .gate(V0));
  Pull_Resistor #(.pull(1)) pull_resistor_15 (.node(transistor_157_out));
  Pull_Resistor #(.pull(1)) pull_resistor_16 (.node(transistor_156_out));
  Transistor #(.\type ("n")) transistor_180 (.in(1'b0), .out(transistor_180_out), .gate(not_2_out));
  Transistor #(.\type ("n")) transistor_181 (.in(1'b0), .out(transistor_180_out), .gate(nPAL));
  Transistor #(.\type ("n")) transistor_182 (.in(1'b0), .out(transistor_180_out), .gate(_3));
  Transistor #(.\type ("n")) transistor_183 (.in(1'b0), .out(transistor_180_out), .gate(V8));
  Transistor #(.\type ("n")) transistor_184 (.in(1'b0), .out(transistor_180_out), .gate(not_4_out));
  Transistor #(.\type ("n")) transistor_185 (.in(1'b0), .out(transistor_180_out), .gate(not_5_out));
  Transistor #(.\type ("n")) transistor_186 (.in(1'b0), .out(transistor_180_out), .gate(not_6_out));
  Transistor #(.\type ("n")) transistor_187 (.in(1'b0), .out(transistor_180_out), .gate(not_7_out));
  Transistor #(.\type ("n")) transistor_188 (.in(1'b0), .out(transistor_180_out), .gate(not_8_out));
  Transistor #(.\type ("n")) transistor_189 (.in(1'b0), .out(transistor_180_out), .gate(not_9_out));
  Transistor #(.\type ("n")) transistor_190 (.in(1'b0), .out(transistor_180_out), .gate(not_10_out));
  Transistor #(.\type ("n")) transistor_191 (.in(1'b0), .out(transistor_180_out), .gate(not_11_out));
  Pull_Resistor #(.pull(1)) pull_resistor_17 (.node(transistor_180_out));
  Transistor #(.\type ("n")) transistor_192 (.in(1'b0), .out(transistor_192_out), .gate(not_2_out));
  Transistor #(.\type ("n")) transistor_193 (.in(1'b0), .out(transistor_192_out), .gate(nPAL));
  Transistor #(.\type ("n")) transistor_194 (.in(1'b0), .out(transistor_192_out), .gate(_2));
  Transistor #(.\type ("n")) transistor_195 (.in(1'b0), .out(transistor_192_out), .gate(not_3_out));
  Transistor #(.\type ("n")) transistor_196 (.in(1'b0), .out(transistor_192_out), .gate(V7));
  Transistor #(.\type ("n")) transistor_197 (.in(1'b0), .out(transistor_192_out), .gate(V6));
  Transistor #(.\type ("n")) transistor_198 (.in(1'b0), .out(transistor_192_out), .gate(V5));
  Transistor #(.\type ("n")) transistor_199 (.in(1'b0), .out(transistor_192_out), .gate(V4));
  Transistor #(.\type ("n")) transistor_200 (.in(1'b0), .out(transistor_192_out), .gate(V3));
  Transistor #(.\type ("n")) transistor_201 (.in(1'b0), .out(transistor_192_out), .gate(not_9_out));
  Transistor #(.\type ("n")) transistor_202 (.in(1'b0), .out(transistor_192_out), .gate(not_10_out));
  Transistor #(.\type ("n")) transistor_203 (.in(1'b0), .out(transistor_192_out), .gate(not_11_out));
  Pull_Resistor #(.pull(1)) pull_resistor_18 (.node(transistor_192_out));
  Transistor #(.\type ("n")) transistor_204 (.in(1'b0), .out(transistor_204_out), .gate(PAL));
  Transistor #(.\type ("n")) transistor_205 (.in(1'b0), .out(transistor_204_out), .gate(M5));
  Transistor #(.\type ("n")) transistor_206 (.in(1'b0), .out(transistor_204_out), .gate(not_3_out));
  Transistor #(.\type ("n")) transistor_207 (.in(1'b0), .out(transistor_204_out), .gate(not_4_out));
  Transistor #(.\type ("n")) transistor_208 (.in(1'b0), .out(transistor_204_out), .gate(not_5_out));
  Transistor #(.\type ("n")) transistor_209 (.in(1'b0), .out(transistor_204_out), .gate(not_6_out));
  Transistor #(.\type ("n")) transistor_210 (.in(1'b0), .out(transistor_204_out), .gate(V4));
  Transistor #(.\type ("n")) transistor_211 (.in(1'b0), .out(transistor_204_out), .gate(V3));
  Transistor #(.\type ("n")) transistor_212 (.in(1'b0), .out(transistor_204_out), .gate(not_9_out));
  Transistor #(.\type ("n")) transistor_213 (.in(1'b0), .out(transistor_204_out), .gate(V1));
  Transistor #(.\type ("n")) transistor_214 (.in(1'b0), .out(transistor_204_out), .gate(not_11_out));
  Pull_Resistor #(.pull(1)) pull_resistor_19 (.node(transistor_204_out));
  Transistor #(.\type ("n")) transistor_215 (.in(1'b0), .out(transistor_215_out), .gate(PAL));
  Transistor #(.\type ("n")) transistor_216 (.in(1'b0), .out(transistor_215_out), .gate(_3));
  Transistor #(.\type ("n")) transistor_217 (.in(1'b0), .out(transistor_215_out), .gate(not_3_out));
  Transistor #(.\type ("n")) transistor_218 (.in(1'b0), .out(transistor_215_out), .gate(not_4_out));
  Transistor #(.\type ("n")) transistor_219 (.in(1'b0), .out(transistor_215_out), .gate(not_5_out));
  Transistor #(.\type ("n")) transistor_220 (.in(1'b0), .out(transistor_215_out), .gate(not_6_out));
  Transistor #(.\type ("n")) transistor_221 (.in(1'b0), .out(transistor_215_out), .gate(not_7_out));
  Transistor #(.\type ("n")) transistor_222 (.in(1'b0), .out(transistor_215_out), .gate(V3));
  Transistor #(.\type ("n")) transistor_223 (.in(1'b0), .out(transistor_215_out), .gate(not_9_out));
  Transistor #(.\type ("n")) transistor_224 (.in(1'b0), .out(transistor_215_out), .gate(V1));
  Transistor #(.\type ("n")) transistor_225 (.in(1'b0), .out(transistor_215_out), .gate(not_11_out));
  Pull_Resistor #(.pull(1)) pull_resistor_20 (.node(transistor_215_out));
  or or_3 (VPLA_4, transistor_204_out, transistor_215_out, transistor_226_out, transistor_237_out, transistor_249_out);
  Transistor #(.\type ("n")) transistor_226 (.in(1'b0), .out(transistor_226_out), .gate(nPAL));
  Transistor #(.\type ("n")) transistor_227 (.in(1'b0), .out(transistor_226_out), .gate(M5));
  Transistor #(.\type ("n")) transistor_228 (.in(1'b0), .out(transistor_226_out), .gate(not_3_out));
  Transistor #(.\type ("n")) transistor_229 (.in(1'b0), .out(transistor_226_out), .gate(not_4_out));
  Transistor #(.\type ("n")) transistor_230 (.in(1'b0), .out(transistor_226_out), .gate(not_5_out));
  Transistor #(.\type ("n")) transistor_231 (.in(1'b0), .out(transistor_226_out), .gate(V5));
  Transistor #(.\type ("n")) transistor_232 (.in(1'b0), .out(transistor_226_out), .gate(V4));
  Transistor #(.\type ("n")) transistor_233 (.in(1'b0), .out(transistor_226_out), .gate(not_8_out));
  Transistor #(.\type ("n")) transistor_234 (.in(1'b0), .out(transistor_226_out), .gate(V2));
  Transistor #(.\type ("n")) transistor_235 (.in(1'b0), .out(transistor_226_out), .gate(not_10_out));
  Transistor #(.\type ("n")) transistor_236 (.in(1'b0), .out(transistor_226_out), .gate(V0));
  Pull_Resistor #(.pull(1)) pull_resistor_21 (.node(transistor_226_out));
  Transistor #(.\type ("n")) transistor_237 (.in(1'b0), .out(transistor_237_out), .gate(nPAL));
  Transistor #(.\type ("n")) transistor_238 (.in(1'b0), .out(transistor_237_out), .gate(_3));
  Transistor #(.\type ("n")) transistor_239 (.in(1'b0), .out(transistor_237_out), .gate(not_3_out));
  Transistor #(.\type ("n")) transistor_240 (.in(1'b0), .out(transistor_237_out), .gate(not_4_out));
  Transistor #(.\type ("n")) transistor_241 (.in(1'b0), .out(transistor_237_out), .gate(not_5_out));
  Transistor #(.\type ("n")) transistor_242 (.in(1'b0), .out(transistor_237_out), .gate(V5));
  Transistor #(.\type ("n")) transistor_243 (.in(1'b0), .out(transistor_237_out), .gate(not_7_out));
  Transistor #(.\type ("n")) transistor_244 (.in(1'b0), .out(transistor_237_out), .gate(not_8_out));
  Transistor #(.\type ("n")) transistor_245 (.in(1'b0), .out(transistor_237_out), .gate(V2));
  Transistor #(.\type ("n")) transistor_246 (.in(1'b0), .out(transistor_237_out), .gate(not_10_out));
  Transistor #(.\type ("n")) transistor_247 (.in(1'b0), .out(transistor_237_out), .gate(V0));
  Pull_Resistor #(.pull(1)) pull_resistor_22 (.node(transistor_237_out));
  Transistor #(.\type ("n")) transistor_248 (.in(1'b0), .out(transistor_248_out), .gate(ODD_EVEN));
  Transistor #(.\type ("n")) transistor_249 (.in(1'b0), .out(transistor_249_out), .gate(nPAL));
  Transistor #(.\type ("n")) transistor_250 (.in(1'b0), .out(transistor_248_out), .gate(PAL));
  Transistor #(.\type ("n")) transistor_251 (.in(1'b0), .out(transistor_249_out), .gate(_2));
  Transistor #(.\type ("n")) transistor_252 (.in(1'b0), .out(transistor_248_out), .gate(M5));
  Transistor #(.\type ("n")) transistor_253 (.in(1'b0), .out(transistor_248_out), .gate(not_3_out));
  Transistor #(.\type ("n")) transistor_254 (.in(1'b0), .out(transistor_249_out), .gate(not_3_out));
  Transistor #(.\type ("n")) transistor_255 (.in(1'b0), .out(transistor_248_out), .gate(not_4_out));
  Transistor #(.\type ("n")) transistor_256 (.in(1'b0), .out(transistor_249_out), .gate(not_4_out));
  Transistor #(.\type ("n")) transistor_257 (.in(1'b0), .out(transistor_248_out), .gate(not_5_out));
  Transistor #(.\type ("n")) transistor_258 (.in(1'b0), .out(transistor_249_out), .gate(not_5_out));
  Transistor #(.\type ("n")) transistor_259 (.in(1'b0), .out(transistor_248_out), .gate(V5));
  Transistor #(.\type ("n")) transistor_260 (.in(1'b0), .out(transistor_249_out), .gate(not_6_out));
  Transistor #(.\type ("n")) transistor_261 (.in(1'b0), .out(transistor_249_out), .gate(V4));
  Transistor #(.\type ("n")) transistor_262 (.in(1'b0), .out(transistor_248_out), .gate(not_7_out));
  Transistor #(.\type ("n")) transistor_263 (.in(1'b0), .out(transistor_248_out), .gate(V3));
  Transistor #(.\type ("n")) transistor_264 (.in(1'b0), .out(transistor_249_out), .gate(V3));
  Transistor #(.\type ("n")) transistor_265 (.in(1'b0), .out(transistor_249_out), .gate(V2));
  Transistor #(.\type ("n")) transistor_266 (.in(1'b0), .out(transistor_248_out), .gate(not_9_out));
  Transistor #(.\type ("n")) transistor_267 (.in(1'b0), .out(transistor_248_out), .gate(V1));
  Transistor #(.\type ("n")) transistor_268 (.in(1'b0), .out(transistor_249_out), .gate(not_10_out));
  Transistor #(.\type ("n")) transistor_269 (.in(1'b0), .out(transistor_249_out), .gate(V0));
  Transistor #(.\type ("n")) transistor_270 (.in(1'b0), .out(transistor_248_out), .gate(not_11_out));
  Pull_Resistor #(.pull(1)) pull_resistor_23 (.node(transistor_249_out));
  Pull_Resistor #(.pull(1)) pull_resistor_24 (.node(transistor_248_out));
  Transistor #(.\type ("n")) transistor_271 (.in(1'b0), .out(transistor_271_out), .gate(ODD_EVEN));
  Transistor #(.\type ("n")) transistor_272 (.in(1'b0), .out(transistor_271_out), .gate(PAL));
  Transistor #(.\type ("n")) transistor_273 (.in(1'b0), .out(transistor_271_out), .gate(_3));
  Transistor #(.\type ("n")) transistor_274 (.in(1'b0), .out(transistor_271_out), .gate(not_3_out));
  Transistor #(.\type ("n")) transistor_275 (.in(1'b0), .out(transistor_271_out), .gate(not_4_out));
  Transistor #(.\type ("n")) transistor_276 (.in(1'b0), .out(transistor_271_out), .gate(not_5_out));
  Transistor #(.\type ("n")) transistor_277 (.in(1'b0), .out(transistor_271_out), .gate(not_6_out));
  Transistor #(.\type ("n")) transistor_278 (.in(1'b0), .out(transistor_271_out), .gate(V4));
  Transistor #(.\type ("n")) transistor_279 (.in(1'b0), .out(transistor_271_out), .gate(V3));
  Transistor #(.\type ("n")) transistor_280 (.in(1'b0), .out(transistor_271_out), .gate(not_9_out));
  Transistor #(.\type ("n")) transistor_281 (.in(1'b0), .out(transistor_271_out), .gate(V1));
  Transistor #(.\type ("n")) transistor_282 (.in(1'b0), .out(transistor_271_out), .gate(not_11_out));
  Pull_Resistor #(.pull(1)) pull_resistor_25 (.node(transistor_271_out));
  Transistor #(.\type ("n")) transistor_283 (.in(1'b0), .out(transistor_283_out), .gate(ODD_EVEN));
  Transistor #(.\type ("n")) transistor_284 (.in(1'b0), .out(transistor_283_out), .gate(nPAL));
  Transistor #(.\type ("n")) transistor_285 (.in(1'b0), .out(transistor_283_out), .gate(M5));
  Transistor #(.\type ("n")) transistor_286 (.in(1'b0), .out(transistor_283_out), .gate(not_3_out));
  Transistor #(.\type ("n")) transistor_287 (.in(1'b0), .out(transistor_283_out), .gate(not_4_out));
  Transistor #(.\type ("n")) transistor_288 (.in(1'b0), .out(transistor_283_out), .gate(V6));
  Transistor #(.\type ("n")) transistor_289 (.in(1'b0), .out(transistor_283_out), .gate(not_6_out));
  Transistor #(.\type ("n")) transistor_290 (.in(1'b0), .out(transistor_283_out), .gate(not_7_out));
  Transistor #(.\type ("n")) transistor_291 (.in(1'b0), .out(transistor_283_out), .gate(not_8_out));
  Transistor #(.\type ("n")) transistor_292 (.in(1'b0), .out(transistor_283_out), .gate(V2));
  Transistor #(.\type ("n")) transistor_293 (.in(1'b0), .out(transistor_283_out), .gate(not_10_out));
  Transistor #(.\type ("n")) transistor_294 (.in(1'b0), .out(transistor_283_out), .gate(V0));
  Pull_Resistor #(.pull(1)) pull_resistor_26 (.node(transistor_283_out));
  or or_4 (VPLA_5, transistor_248_out, transistor_271_out, transistor_283_out, transistor_295_out, transistor_307_out, transistor_319_out, transistor_331_out, transistor_344_out);
  Transistor #(.\type ("n")) transistor_295 (.in(1'b0), .out(transistor_295_out), .gate(ODD_EVEN));
  Transistor #(.\type ("n")) transistor_296 (.in(1'b0), .out(transistor_295_out), .gate(nPAL));
  Transistor #(.\type ("n")) transistor_297 (.in(1'b0), .out(transistor_295_out), .gate(_3));
  Transistor #(.\type ("n")) transistor_298 (.in(1'b0), .out(transistor_295_out), .gate(not_3_out));
  Transistor #(.\type ("n")) transistor_299 (.in(1'b0), .out(transistor_295_out), .gate(not_4_out));
  Transistor #(.\type ("n")) transistor_300 (.in(1'b0), .out(transistor_295_out), .gate(not_5_out));
  Transistor #(.\type ("n")) transistor_301 (.in(1'b0), .out(transistor_295_out), .gate(V5));
  Transistor #(.\type ("n")) transistor_302 (.in(1'b0), .out(transistor_295_out), .gate(V4));
  Transistor #(.\type ("n")) transistor_303 (.in(1'b0), .out(transistor_295_out), .gate(not_8_out));
  Transistor #(.\type ("n")) transistor_304 (.in(1'b0), .out(transistor_295_out), .gate(V2));
  Transistor #(.\type ("n")) transistor_305 (.in(1'b0), .out(transistor_295_out), .gate(not_10_out));
  Transistor #(.\type ("n")) transistor_306 (.in(1'b0), .out(transistor_295_out), .gate(V0));
  Pull_Resistor #(.pull(1)) pull_resistor_27 (.node(transistor_295_out));
  Transistor #(.\type ("n")) transistor_307 (.in(1'b0), .out(transistor_307_out), .gate(ODD_EVEN));
  Transistor #(.\type ("n")) transistor_308 (.in(1'b0), .out(transistor_307_out), .gate(nPAL));
  Transistor #(.\type ("n")) transistor_309 (.in(1'b0), .out(transistor_307_out), .gate(_2));
  Transistor #(.\type ("n")) transistor_310 (.in(1'b0), .out(transistor_307_out), .gate(not_3_out));
  Transistor #(.\type ("n")) transistor_311 (.in(1'b0), .out(transistor_307_out), .gate(not_4_out));
  Transistor #(.\type ("n")) transistor_312 (.in(1'b0), .out(transistor_307_out), .gate(not_5_out));
  Transistor #(.\type ("n")) transistor_313 (.in(1'b0), .out(transistor_307_out), .gate(V5));
  Transistor #(.\type ("n")) transistor_314 (.in(1'b0), .out(transistor_307_out), .gate(not_7_out));
  Transistor #(.\type ("n")) transistor_315 (.in(1'b0), .out(transistor_307_out), .gate(V3));
  Transistor #(.\type ("n")) transistor_316 (.in(1'b0), .out(transistor_307_out), .gate(V2));
  Transistor #(.\type ("n")) transistor_317 (.in(1'b0), .out(transistor_307_out), .gate(not_10_out));
  Transistor #(.\type ("n")) transistor_318 (.in(1'b0), .out(transistor_307_out), .gate(V0));
  Pull_Resistor #(.pull(1)) pull_resistor_28 (.node(transistor_307_out));
  Transistor #(.\type ("n")) transistor_319 (.in(1'b0), .out(transistor_319_out), .gate(not_1_out));
  Transistor #(.\type ("n")) transistor_320 (.in(1'b0), .out(transistor_319_out), .gate(PAL));
  Transistor #(.\type ("n")) transistor_321 (.in(1'b0), .out(transistor_319_out), .gate(_3));
  Transistor #(.\type ("n")) transistor_322 (.in(1'b0), .out(transistor_319_out), .gate(not_3_out));
  Transistor #(.\type ("n")) transistor_323 (.in(1'b0), .out(transistor_319_out), .gate(not_4_out));
  Transistor #(.\type ("n")) transistor_324 (.in(1'b0), .out(transistor_319_out), .gate(not_5_out));
  Transistor #(.\type ("n")) transistor_325 (.in(1'b0), .out(transistor_319_out), .gate(not_6_out));
  Transistor #(.\type ("n")) transistor_326 (.in(1'b0), .out(transistor_319_out), .gate(V4));
  Transistor #(.\type ("n")) transistor_327 (.in(1'b0), .out(transistor_319_out), .gate(V3));
  Transistor #(.\type ("n")) transistor_328 (.in(1'b0), .out(transistor_319_out), .gate(not_9_out));
  Transistor #(.\type ("n")) transistor_329 (.in(1'b0), .out(transistor_319_out), .gate(V1));
  Transistor #(.\type ("n")) transistor_330 (.in(1'b0), .out(transistor_319_out), .gate(V0));
  Pull_Resistor #(.pull(1)) pull_resistor_29 (.node(transistor_319_out));
  Transistor #(.\type ("n")) transistor_331 (.in(1'b0), .out(transistor_331_out), .gate(not_1_out));
  Transistor #(.\type ("n")) transistor_332 (.in(1'b0), .out(transistor_331_out), .gate(nPAL));
  Transistor #(.\type ("n")) transistor_333 (.in(1'b0), .out(transistor_331_out), .gate(_3));
  Transistor #(.\type ("n")) transistor_334 (.in(1'b0), .out(transistor_331_out), .gate(not_3_out));
  Transistor #(.\type ("n")) transistor_335 (.in(1'b0), .out(transistor_331_out), .gate(not_4_out));
  Transistor #(.\type ("n")) transistor_336 (.in(1'b0), .out(transistor_331_out), .gate(not_5_out));
  Transistor #(.\type ("n")) transistor_337 (.in(1'b0), .out(transistor_331_out), .gate(V5));
  Transistor #(.\type ("n")) transistor_338 (.in(1'b0), .out(transistor_331_out), .gate(V4));
  Transistor #(.\type ("n")) transistor_339 (.in(1'b0), .out(transistor_331_out), .gate(not_8_out));
  Transistor #(.\type ("n")) transistor_340 (.in(1'b0), .out(transistor_331_out), .gate(V2));
  Transistor #(.\type ("n")) transistor_341 (.in(1'b0), .out(transistor_331_out), .gate(V1));
  Transistor #(.\type ("n")) transistor_342 (.in(1'b0), .out(transistor_331_out), .gate(not_11_out));
  Pull_Resistor #(.pull(1)) pull_resistor_30 (.node(transistor_331_out));
  Transistor #(.\type ("n")) transistor_343 (.in(1'b0), .out(transistor_343_out), .gate(ODD_EVEN));
  Transistor #(.\type ("n")) transistor_344 (.in(1'b0), .out(transistor_344_out), .gate(not_1_out));
  Transistor #(.\type ("n")) transistor_345 (.in(1'b0), .out(transistor_344_out), .gate(nPAL));
  Transistor #(.\type ("n")) transistor_346 (.in(1'b0), .out(transistor_343_out), .gate(PAL));
  Transistor #(.\type ("n")) transistor_347 (.in(1'b0), .out(transistor_344_out), .gate(_2));
  Transistor #(.\type ("n")) transistor_348 (.in(1'b0), .out(transistor_343_out), .gate(M5));
  Transistor #(.\type ("n")) transistor_349 (.in(1'b0), .out(transistor_344_out), .gate(not_3_out));
  Transistor #(.\type ("n")) transistor_350 (.in(1'b0), .out(transistor_343_out), .gate(not_3_out));
  Transistor #(.\type ("n")) transistor_351 (.in(1'b0), .out(transistor_344_out), .gate(not_4_out));
  Transistor #(.\type ("n")) transistor_352 (.in(1'b0), .out(transistor_343_out), .gate(not_4_out));
  Transistor #(.\type ("n")) transistor_353 (.in(1'b0), .out(transistor_343_out), .gate(not_5_out));
  Transistor #(.\type ("n")) transistor_354 (.in(1'b0), .out(transistor_344_out), .gate(not_5_out));
  Transistor #(.\type ("n")) transistor_355 (.in(1'b0), .out(transistor_343_out), .gate(V5));
  Transistor #(.\type ("n")) transistor_356 (.in(1'b0), .out(transistor_344_out), .gate(V5));
  Transistor #(.\type ("n")) transistor_357 (.in(1'b0), .out(transistor_343_out), .gate(not_7_out));
  Transistor #(.\type ("n")) transistor_358 (.in(1'b0), .out(transistor_344_out), .gate(not_7_out));
  Transistor #(.\type ("n")) transistor_359 (.in(1'b0), .out(transistor_344_out), .gate(V3));
  Transistor #(.\type ("n")) transistor_360 (.in(1'b0), .out(transistor_343_out), .gate(not_8_out));
  Transistor #(.\type ("n")) transistor_361 (.in(1'b0), .out(transistor_344_out), .gate(V2));
  Transistor #(.\type ("n")) transistor_362 (.in(1'b0), .out(transistor_343_out), .gate(V2));
  Transistor #(.\type ("n")) transistor_363 (.in(1'b0), .out(transistor_343_out), .gate(V1));
  Transistor #(.\type ("n")) transistor_364 (.in(1'b0), .out(transistor_344_out), .gate(V1));
  Transistor #(.\type ("n")) transistor_365 (.in(1'b0), .out(transistor_343_out), .gate(V0));
  Transistor #(.\type ("n")) transistor_366 (.in(1'b0), .out(transistor_344_out), .gate(not_11_out));
  Pull_Resistor #(.pull(1)) pull_resistor_31 (.node(transistor_344_out));
  Pull_Resistor #(.pull(1)) pull_resistor_32 (.node(transistor_343_out));
  Transistor #(.\type ("n")) transistor_367 (.in(1'b0), .out(transistor_367_out), .gate(ODD_EVEN));
  Transistor #(.\type ("n")) transistor_368 (.in(1'b0), .out(transistor_367_out), .gate(PAL));
  Transistor #(.\type ("n")) transistor_369 (.in(1'b0), .out(transistor_367_out), .gate(_3));
  Transistor #(.\type ("n")) transistor_370 (.in(1'b0), .out(transistor_367_out), .gate(not_3_out));
  Transistor #(.\type ("n")) transistor_371 (.in(1'b0), .out(transistor_367_out), .gate(not_4_out));
  Transistor #(.\type ("n")) transistor_372 (.in(1'b0), .out(transistor_367_out), .gate(not_5_out));
  Transistor #(.\type ("n")) transistor_373 (.in(1'b0), .out(transistor_367_out), .gate(not_6_out));
  Transistor #(.\type ("n")) transistor_374 (.in(1'b0), .out(transistor_367_out), .gate(V4));
  Transistor #(.\type ("n")) transistor_375 (.in(1'b0), .out(transistor_367_out), .gate(not_8_out));
  Transistor #(.\type ("n")) transistor_376 (.in(1'b0), .out(transistor_367_out), .gate(V2));
  Transistor #(.\type ("n")) transistor_377 (.in(1'b0), .out(transistor_367_out), .gate(V1));
  Transistor #(.\type ("n")) transistor_378 (.in(1'b0), .out(transistor_367_out), .gate(V0));
  Pull_Resistor #(.pull(1)) pull_resistor_33 (.node(transistor_367_out));
  Transistor #(.\type ("n")) transistor_379 (.in(1'b0), .out(transistor_379_out), .gate(ODD_EVEN));
  Transistor #(.\type ("n")) transistor_380 (.in(1'b0), .out(transistor_379_out), .gate(nPAL));
  Transistor #(.\type ("n")) transistor_381 (.in(1'b0), .out(transistor_379_out), .gate(M5));
  Transistor #(.\type ("n")) transistor_382 (.in(1'b0), .out(transistor_379_out), .gate(not_3_out));
  Transistor #(.\type ("n")) transistor_383 (.in(1'b0), .out(transistor_379_out), .gate(not_4_out));
  Transistor #(.\type ("n")) transistor_384 (.in(1'b0), .out(transistor_379_out), .gate(V6));
  Transistor #(.\type ("n")) transistor_385 (.in(1'b0), .out(transistor_379_out), .gate(not_6_out));
  Transistor #(.\type ("n")) transistor_386 (.in(1'b0), .out(transistor_379_out), .gate(not_7_out));
  Transistor #(.\type ("n")) transistor_387 (.in(1'b0), .out(transistor_379_out), .gate(not_8_out));
  Transistor #(.\type ("n")) transistor_388 (.in(1'b0), .out(transistor_379_out), .gate(not_9_out));
  Transistor #(.\type ("n")) transistor_389 (.in(1'b0), .out(transistor_379_out), .gate(V1));
  Transistor #(.\type ("n")) transistor_390 (.in(1'b0), .out(transistor_379_out), .gate(not_11_out));
  Pull_Resistor #(.pull(1)) pull_resistor_34 (.node(transistor_379_out));
  or or_5 (VPLA_6, transistor_343_out, transistor_367_out, transistor_379_out, transistor_391_out, transistor_403_out, transistor_415_out, transistor_426_out, transistor_439_out);
  Transistor #(.\type ("n")) transistor_391 (.in(1'b0), .out(transistor_391_out), .gate(ODD_EVEN));
  Transistor #(.\type ("n")) transistor_392 (.in(1'b0), .out(transistor_391_out), .gate(nPAL));
  Transistor #(.\type ("n")) transistor_393 (.in(1'b0), .out(transistor_391_out), .gate(_3));
  Transistor #(.\type ("n")) transistor_394 (.in(1'b0), .out(transistor_391_out), .gate(not_3_out));
  Transistor #(.\type ("n")) transistor_395 (.in(1'b0), .out(transistor_391_out), .gate(not_4_out));
  Transistor #(.\type ("n")) transistor_396 (.in(1'b0), .out(transistor_391_out), .gate(not_5_out));
  Transistor #(.\type ("n")) transistor_397 (.in(1'b0), .out(transistor_391_out), .gate(V5));
  Transistor #(.\type ("n")) transistor_398 (.in(1'b0), .out(transistor_391_out), .gate(V4));
  Transistor #(.\type ("n")) transistor_399 (.in(1'b0), .out(transistor_391_out), .gate(not_8_out));
  Transistor #(.\type ("n")) transistor_400 (.in(1'b0), .out(transistor_391_out), .gate(not_9_out));
  Transistor #(.\type ("n")) transistor_401 (.in(1'b0), .out(transistor_391_out), .gate(V1));
  Transistor #(.\type ("n")) transistor_402 (.in(1'b0), .out(transistor_391_out), .gate(not_11_out));
  Pull_Resistor #(.pull(1)) pull_resistor_35 (.node(transistor_391_out));
  Transistor #(.\type ("n")) transistor_403 (.in(1'b0), .out(transistor_403_out), .gate(ODD_EVEN));
  Transistor #(.\type ("n")) transistor_404 (.in(1'b0), .out(transistor_403_out), .gate(nPAL));
  Transistor #(.\type ("n")) transistor_405 (.in(1'b0), .out(transistor_403_out), .gate(_2));
  Transistor #(.\type ("n")) transistor_406 (.in(1'b0), .out(transistor_403_out), .gate(not_3_out));
  Transistor #(.\type ("n")) transistor_407 (.in(1'b0), .out(transistor_403_out), .gate(not_4_out));
  Transistor #(.\type ("n")) transistor_408 (.in(1'b0), .out(transistor_403_out), .gate(not_5_out));
  Transistor #(.\type ("n")) transistor_409 (.in(1'b0), .out(transistor_403_out), .gate(V5));
  Transistor #(.\type ("n")) transistor_410 (.in(1'b0), .out(transistor_403_out), .gate(not_7_out));
  Transistor #(.\type ("n")) transistor_411 (.in(1'b0), .out(transistor_403_out), .gate(V3));
  Transistor #(.\type ("n")) transistor_412 (.in(1'b0), .out(transistor_403_out), .gate(not_9_out));
  Transistor #(.\type ("n")) transistor_413 (.in(1'b0), .out(transistor_403_out), .gate(V1));
  Transistor #(.\type ("n")) transistor_414 (.in(1'b0), .out(transistor_403_out), .gate(not_11_out));
  Pull_Resistor #(.pull(1)) pull_resistor_36 (.node(transistor_403_out));
  Transistor #(.\type ("n")) transistor_415 (.in(1'b0), .out(transistor_415_out), .gate(PAL));
  Transistor #(.\type ("n")) transistor_416 (.in(1'b0), .out(transistor_415_out), .gate(_3));
  Transistor #(.\type ("n")) transistor_417 (.in(1'b0), .out(transistor_415_out), .gate(not_3_out));
  Transistor #(.\type ("n")) transistor_418 (.in(1'b0), .out(transistor_415_out), .gate(not_4_out));
  Transistor #(.\type ("n")) transistor_419 (.in(1'b0), .out(transistor_415_out), .gate(not_5_out));
  Transistor #(.\type ("n")) transistor_420 (.in(1'b0), .out(transistor_415_out), .gate(not_6_out));
  Transistor #(.\type ("n")) transistor_421 (.in(1'b0), .out(transistor_415_out), .gate(V4));
  Transistor #(.\type ("n")) transistor_422 (.in(1'b0), .out(transistor_415_out), .gate(V3));
  Transistor #(.\type ("n")) transistor_423 (.in(1'b0), .out(transistor_415_out), .gate(not_9_out));
  Transistor #(.\type ("n")) transistor_424 (.in(1'b0), .out(transistor_415_out), .gate(not_10_out));
  Transistor #(.\type ("n")) transistor_425 (.in(1'b0), .out(transistor_415_out), .gate(not_11_out));
  Pull_Resistor #(.pull(1)) pull_resistor_37 (.node(transistor_415_out));
  Transistor #(.\type ("n")) transistor_426 (.in(1'b0), .out(transistor_426_out), .gate(not_1_out));
  Transistor #(.\type ("n")) transistor_427 (.in(1'b0), .out(transistor_426_out), .gate(nPAL));
  Transistor #(.\type ("n")) transistor_428 (.in(1'b0), .out(transistor_426_out), .gate(_3));
  Transistor #(.\type ("n")) transistor_429 (.in(1'b0), .out(transistor_426_out), .gate(not_3_out));
  Transistor #(.\type ("n")) transistor_430 (.in(1'b0), .out(transistor_426_out), .gate(not_4_out));
  Transistor #(.\type ("n")) transistor_431 (.in(1'b0), .out(transistor_426_out), .gate(not_5_out));
  Transistor #(.\type ("n")) transistor_432 (.in(1'b0), .out(transistor_426_out), .gate(V5));
  Transistor #(.\type ("n")) transistor_433 (.in(1'b0), .out(transistor_426_out), .gate(V4));
  Transistor #(.\type ("n")) transistor_434 (.in(1'b0), .out(transistor_426_out), .gate(not_8_out));
  Transistor #(.\type ("n")) transistor_435 (.in(1'b0), .out(transistor_426_out), .gate(not_9_out));
  Transistor #(.\type ("n")) transistor_436 (.in(1'b0), .out(transistor_426_out), .gate(V1));
  Transistor #(.\type ("n")) transistor_437 (.in(1'b0), .out(transistor_426_out), .gate(V0));
  Pull_Resistor #(.pull(1)) pull_resistor_38 (.node(transistor_426_out));
  Transistor #(.\type ("n")) transistor_438 (.in(1'b0), .out(transistor_438_out), .gate(ODD_EVEN));
  Transistor #(.\type ("n")) transistor_439 (.in(1'b0), .out(transistor_439_out), .gate(not_1_out));
  Transistor #(.\type ("n")) transistor_440 (.in(1'b0), .out(transistor_439_out), .gate(nPAL));
  Transistor #(.\type ("n")) transistor_441 (.in(1'b0), .out(transistor_438_out), .gate(PAL));
  Transistor #(.\type ("n")) transistor_442 (.in(1'b0), .out(transistor_439_out), .gate(_2));
  Transistor #(.\type ("n")) transistor_443 (.in(1'b0), .out(transistor_438_out), .gate(M5));
  Transistor #(.\type ("n")) transistor_444 (.in(1'b0), .out(transistor_438_out), .gate(not_3_out));
  Transistor #(.\type ("n")) transistor_445 (.in(1'b0), .out(transistor_439_out), .gate(not_3_out));
  Transistor #(.\type ("n")) transistor_446 (.in(1'b0), .out(transistor_438_out), .gate(not_4_out));
  Transistor #(.\type ("n")) transistor_447 (.in(1'b0), .out(transistor_439_out), .gate(not_4_out));
  Transistor #(.\type ("n")) transistor_448 (.in(1'b0), .out(transistor_439_out), .gate(not_5_out));
  Transistor #(.\type ("n")) transistor_449 (.in(1'b0), .out(transistor_438_out), .gate(not_5_out));
  Transistor #(.\type ("n")) transistor_450 (.in(1'b0), .out(transistor_438_out), .gate(V5));
  Transistor #(.\type ("n")) transistor_451 (.in(1'b0), .out(transistor_439_out), .gate(V5));
  Transistor #(.\type ("n")) transistor_452 (.in(1'b0), .out(transistor_438_out), .gate(not_7_out));
  Transistor #(.\type ("n")) transistor_453 (.in(1'b0), .out(transistor_439_out), .gate(not_7_out));
  Transistor #(.\type ("n")) transistor_454 (.in(1'b0), .out(transistor_439_out), .gate(V3));
  Transistor #(.\type ("n")) transistor_455 (.in(1'b0), .out(transistor_438_out), .gate(not_8_out));
  Transistor #(.\type ("n")) transistor_456 (.in(1'b0), .out(transistor_438_out), .gate(V2));
  Transistor #(.\type ("n")) transistor_457 (.in(1'b0), .out(transistor_439_out), .gate(not_9_out));
  Transistor #(.\type ("n")) transistor_458 (.in(1'b0), .out(transistor_439_out), .gate(V1));
  Transistor #(.\type ("n")) transistor_459 (.in(1'b0), .out(transistor_438_out), .gate(not_10_out));
  Transistor #(.\type ("n")) transistor_460 (.in(1'b0), .out(transistor_439_out), .gate(V0));
  Transistor #(.\type ("n")) transistor_461 (.in(1'b0), .out(transistor_438_out), .gate(not_11_out));
  Pull_Resistor #(.pull(1)) pull_resistor_39 (.node(transistor_439_out));
  Pull_Resistor #(.pull(1)) pull_resistor_40 (.node(transistor_438_out));
  Transistor #(.\type ("n")) transistor_462 (.in(1'b0), .out(transistor_462_out), .gate(ODD_EVEN));
  Transistor #(.\type ("n")) transistor_463 (.in(1'b0), .out(transistor_462_out), .gate(PAL));
  Transistor #(.\type ("n")) transistor_464 (.in(1'b0), .out(transistor_462_out), .gate(_3));
  Transistor #(.\type ("n")) transistor_465 (.in(1'b0), .out(transistor_462_out), .gate(not_3_out));
  Transistor #(.\type ("n")) transistor_466 (.in(1'b0), .out(transistor_462_out), .gate(not_4_out));
  Transistor #(.\type ("n")) transistor_467 (.in(1'b0), .out(transistor_462_out), .gate(not_5_out));
  Transistor #(.\type ("n")) transistor_468 (.in(1'b0), .out(transistor_462_out), .gate(not_6_out));
  Transistor #(.\type ("n")) transistor_469 (.in(1'b0), .out(transistor_462_out), .gate(V4));
  Transistor #(.\type ("n")) transistor_470 (.in(1'b0), .out(transistor_462_out), .gate(not_8_out));
  Transistor #(.\type ("n")) transistor_471 (.in(1'b0), .out(transistor_462_out), .gate(V2));
  Transistor #(.\type ("n")) transistor_472 (.in(1'b0), .out(transistor_462_out), .gate(not_10_out));
  Transistor #(.\type ("n")) transistor_473 (.in(1'b0), .out(transistor_462_out), .gate(not_11_out));
  Pull_Resistor #(.pull(1)) pull_resistor_41 (.node(transistor_462_out));
  Transistor #(.\type ("n")) transistor_474 (.in(1'b0), .out(transistor_474_out), .gate(ODD_EVEN));
  Transistor #(.\type ("n")) transistor_475 (.in(1'b0), .out(transistor_474_out), .gate(nPAL));
  Transistor #(.\type ("n")) transistor_476 (.in(1'b0), .out(transistor_474_out), .gate(M5));
  Transistor #(.\type ("n")) transistor_477 (.in(1'b0), .out(transistor_474_out), .gate(not_3_out));
  Transistor #(.\type ("n")) transistor_478 (.in(1'b0), .out(transistor_474_out), .gate(not_4_out));
  Transistor #(.\type ("n")) transistor_479 (.in(1'b0), .out(transistor_474_out), .gate(not_5_out));
  Transistor #(.\type ("n")) transistor_480 (.in(1'b0), .out(transistor_474_out), .gate(V5));
  Transistor #(.\type ("n")) transistor_481 (.in(1'b0), .out(transistor_474_out), .gate(V4));
  Transistor #(.\type ("n")) transistor_482 (.in(1'b0), .out(transistor_474_out), .gate(V3));
  Transistor #(.\type ("n")) transistor_483 (.in(1'b0), .out(transistor_474_out), .gate(V2));
  Transistor #(.\type ("n")) transistor_484 (.in(1'b0), .out(transistor_474_out), .gate(V1));
  Transistor #(.\type ("n")) transistor_485 (.in(1'b0), .out(transistor_474_out), .gate(V0));
  Pull_Resistor #(.pull(1)) pull_resistor_42 (.node(transistor_474_out));
  or or_6 (VPLA_7, transistor_438_out, transistor_462_out, transistor_474_out, transistor_486_out, transistor_498_out, transistor_510_out, transistor_522_out, transistor_534_out);
  Transistor #(.\type ("n")) transistor_486 (.in(1'b0), .out(transistor_486_out), .gate(ODD_EVEN));
  Transistor #(.\type ("n")) transistor_487 (.in(1'b0), .out(transistor_486_out), .gate(nPAL));
  Transistor #(.\type ("n")) transistor_488 (.in(1'b0), .out(transistor_486_out), .gate(_3));
  Transistor #(.\type ("n")) transistor_489 (.in(1'b0), .out(transistor_486_out), .gate(not_3_out));
  Transistor #(.\type ("n")) transistor_490 (.in(1'b0), .out(transistor_486_out), .gate(not_4_out));
  Transistor #(.\type ("n")) transistor_491 (.in(1'b0), .out(transistor_486_out), .gate(not_5_out));
  Transistor #(.\type ("n")) transistor_492 (.in(1'b0), .out(transistor_486_out), .gate(V5));
  Transistor #(.\type ("n")) transistor_493 (.in(1'b0), .out(transistor_486_out), .gate(V4));
  Transistor #(.\type ("n")) transistor_494 (.in(1'b0), .out(transistor_486_out), .gate(V3));
  Transistor #(.\type ("n")) transistor_495 (.in(1'b0), .out(transistor_486_out), .gate(V2));
  Transistor #(.\type ("n")) transistor_496 (.in(1'b0), .out(transistor_486_out), .gate(V1));
  Transistor #(.\type ("n")) transistor_497 (.in(1'b0), .out(transistor_486_out), .gate(V0));
  Pull_Resistor #(.pull(1)) pull_resistor_43 (.node(transistor_486_out));
  Transistor #(.\type ("n")) transistor_498 (.in(1'b0), .out(transistor_498_out), .gate(ODD_EVEN));
  Transistor #(.\type ("n")) transistor_499 (.in(1'b0), .out(transistor_498_out), .gate(nPAL));
  Transistor #(.\type ("n")) transistor_500 (.in(1'b0), .out(transistor_498_out), .gate(_2));
  Transistor #(.\type ("n")) transistor_501 (.in(1'b0), .out(transistor_498_out), .gate(not_3_out));
  Transistor #(.\type ("n")) transistor_502 (.in(1'b0), .out(transistor_498_out), .gate(not_4_out));
  Transistor #(.\type ("n")) transistor_503 (.in(1'b0), .out(transistor_498_out), .gate(not_5_out));
  Transistor #(.\type ("n")) transistor_504 (.in(1'b0), .out(transistor_498_out), .gate(V5));
  Transistor #(.\type ("n")) transistor_505 (.in(1'b0), .out(transistor_498_out), .gate(V4));
  Transistor #(.\type ("n")) transistor_506 (.in(1'b0), .out(transistor_498_out), .gate(not_8_out));
  Transistor #(.\type ("n")) transistor_507 (.in(1'b0), .out(transistor_498_out), .gate(V2));
  Transistor #(.\type ("n")) transistor_508 (.in(1'b0), .out(transistor_498_out), .gate(V1));
  Transistor #(.\type ("n")) transistor_509 (.in(1'b0), .out(transistor_498_out), .gate(V0));
  Pull_Resistor #(.pull(1)) pull_resistor_44 (.node(transistor_498_out));
  Transistor #(.\type ("n")) transistor_510 (.in(1'b0), .out(transistor_510_out), .gate(not_1_out));
  Transistor #(.\type ("n")) transistor_511 (.in(1'b0), .out(transistor_510_out), .gate(PAL));
  Transistor #(.\type ("n")) transistor_512 (.in(1'b0), .out(transistor_510_out), .gate(_3));
  Transistor #(.\type ("n")) transistor_513 (.in(1'b0), .out(transistor_510_out), .gate(not_3_out));
  Transistor #(.\type ("n")) transistor_514 (.in(1'b0), .out(transistor_510_out), .gate(not_4_out));
  Transistor #(.\type ("n")) transistor_515 (.in(1'b0), .out(transistor_510_out), .gate(not_5_out));
  Transistor #(.\type ("n")) transistor_516 (.in(1'b0), .out(transistor_510_out), .gate(not_6_out));
  Transistor #(.\type ("n")) transistor_517 (.in(1'b0), .out(transistor_510_out), .gate(not_7_out));
  Transistor #(.\type ("n")) transistor_518 (.in(1'b0), .out(transistor_510_out), .gate(not_8_out));
  Transistor #(.\type ("n")) transistor_519 (.in(1'b0), .out(transistor_510_out), .gate(V2));
  Transistor #(.\type ("n")) transistor_520 (.in(1'b0), .out(transistor_510_out), .gate(not_10_out));
  Transistor #(.\type ("n")) transistor_521 (.in(1'b0), .out(transistor_510_out), .gate(V0));
  Pull_Resistor #(.pull(1)) pull_resistor_45 (.node(transistor_510_out));
  Transistor #(.\type ("n")) transistor_522 (.in(1'b0), .out(transistor_522_out), .gate(not_1_out));
  Transistor #(.\type ("n")) transistor_523 (.in(1'b0), .out(transistor_522_out), .gate(nPAL));
  Transistor #(.\type ("n")) transistor_524 (.in(1'b0), .out(transistor_522_out), .gate(_3));
  Transistor #(.\type ("n")) transistor_525 (.in(1'b0), .out(transistor_522_out), .gate(not_3_out));
  Transistor #(.\type ("n")) transistor_526 (.in(1'b0), .out(transistor_522_out), .gate(not_4_out));
  Transistor #(.\type ("n")) transistor_527 (.in(1'b0), .out(transistor_522_out), .gate(not_5_out));
  Transistor #(.\type ("n")) transistor_528 (.in(1'b0), .out(transistor_522_out), .gate(V5));
  Transistor #(.\type ("n")) transistor_529 (.in(1'b0), .out(transistor_522_out), .gate(not_7_out));
  Transistor #(.\type ("n")) transistor_530 (.in(1'b0), .out(transistor_522_out), .gate(not_8_out));
  Transistor #(.\type ("n")) transistor_531 (.in(1'b0), .out(transistor_522_out), .gate(not_9_out));
  Transistor #(.\type ("n")) transistor_532 (.in(1'b0), .out(transistor_522_out), .gate(not_10_out));
  Transistor #(.\type ("n")) transistor_533 (.in(1'b0), .out(transistor_522_out), .gate(not_11_out));
  Pull_Resistor #(.pull(1)) pull_resistor_46 (.node(transistor_522_out));
  Transistor #(.\type ("n")) transistor_534 (.in(1'b0), .out(transistor_534_out), .gate(not_1_out));
  Transistor #(.\type ("n")) transistor_535 (.in(1'b0), .out(transistor_534_out), .gate(nPAL));
  Transistor #(.\type ("n")) transistor_536 (.in(1'b0), .out(transistor_534_out), .gate(_2));
  Transistor #(.\type ("n")) transistor_537 (.in(1'b0), .out(VPLA_8), .gate(not_3_out));
  Transistor #(.\type ("n")) transistor_538 (.in(1'b0), .out(transistor_534_out), .gate(not_3_out));
  Transistor #(.\type ("n")) transistor_539 (.in(1'b0), .out(VPLA_8), .gate(not_4_out));
  Transistor #(.\type ("n")) transistor_540 (.in(1'b0), .out(transistor_534_out), .gate(not_4_out));
  Transistor #(.\type ("n")) transistor_541 (.in(1'b0), .out(VPLA_8), .gate(not_5_out));
  Transistor #(.\type ("n")) transistor_542 (.in(1'b0), .out(transistor_534_out), .gate(not_5_out));
  Transistor #(.\type ("n")) transistor_543 (.in(1'b0), .out(transistor_534_out), .gate(V5));
  Transistor #(.\type ("n")) transistor_544 (.in(1'b0), .out(VPLA_8), .gate(not_6_out));
  Transistor #(.\type ("n")) transistor_545 (.in(1'b0), .out(VPLA_8), .gate(V4));
  Transistor #(.\type ("n")) transistor_546 (.in(1'b0), .out(transistor_534_out), .gate(V4));
  Transistor #(.\type ("n")) transistor_547 (.in(1'b0), .out(transistor_534_out), .gate(V3));
  Transistor #(.\type ("n")) transistor_548 (.in(1'b0), .out(VPLA_8), .gate(not_8_out));
  Transistor #(.\type ("n")) transistor_549 (.in(1'b0), .out(transistor_534_out), .gate(not_9_out));
  Transistor #(.\type ("n")) transistor_550 (.in(1'b0), .out(VPLA_8), .gate(not_9_out));
  Transistor #(.\type ("n")) transistor_551 (.in(1'b0), .out(VPLA_8), .gate(not_10_out));
  Transistor #(.\type ("n")) transistor_552 (.in(1'b0), .out(transistor_534_out), .gate(not_10_out));
  Transistor #(.\type ("n")) transistor_553 (.in(1'b0), .out(transistor_534_out), .gate(not_11_out));
  Transistor #(.\type ("n")) transistor_554 (.in(1'b0), .out(VPLA_8), .gate(not_11_out));
  Pull_Resistor #(.pull(1)) pull_resistor_47 (.node(VPLA_8));
  Pull_Resistor #(.pull(1)) pull_resistor_48 (.node(transistor_534_out));
endmodule
module HPLA (
  input  _2,
  input  _1,
  input  C,
  input  _3,
  input  _0,
  input  M5,
  input  H40,
  input  H8,
  input  H7,
  input  H6,
  input  H5,
  input  H4,
  input  H3,
  input  H2,
  input  H1,
  input  H0,
  output HPLA_0,
  output HPLA_1,
  output HPLA_2,
  output HPLA_3,
  output HPLA_4,
  output HPLA_5,
  output HPLA_6,
  output HPLA_7,
  output HPLA_8,
  output HPLA_9,
  output HPLA_10,
  output HPLA_11,
  output HPLA_12,
  output HPLA_13,
  output HPLA_14,
  output HPLA_15,
  output HPLA_16,
  output HPLA_17,
  output HPLA_18,
  output HPLA_19,
  output HPLA_20,
  output HPLA_21,
  output HPLA_22,
  output HPLA_23,
  output HPLA_24,
  output HPLA_25,
  output HPLA_26,
  output HPLA_27,
  output HPLA_28,
  output HPLA_29,
  output HPLA_30,
  output HPLA_31,
  output HPLA_32,
  output HPLA_33,
  output HPLA_34,
  output HPLA_35,
  output HPLA_36
);

  wire not_1_out, not_2_out, not_3_out, not_4_out, not_5_out, not_6_out, not_7_out, not_8_out, not_9_out,
       not_10_out, not_11_out, not_13_out, not_15_out, not_17_out, not_19_out, not_21_out, not_22_out,
       not_23_out, not_24_out, not_33_out, not_39_out, pull_resistor_47_node, pull_resistor_48_node,
       pull_resistor_49_node, pull_resistor_50_node, pull_resistor_51_node, pull_resistor_52_node,
       pull_resistor_53_node, pull_resistor_54_node, pull_resistor_55_node, pull_resistor_56_node,
       pull_resistor_57_node, pull_resistor_58_node, transistor_1_out, transistor_11_out, transistor_12_out,
       transistor_31_out, transistor_41_out, transistor_51_out, transistor_61_out, transistor_71_out,
       transistor_80_out, transistor_90_out, transistor_91_out, transistor_110_out, transistor_120_out,
       transistor_130_out, transistor_140_out, transistor_150_out, transistor_160_out, transistor_170_out,
       transistor_171_out, transistor_190_out, transistor_200_out, transistor_210_out, transistor_220_out,
       transistor_230_out, transistor_240_out, transistor_250_out, transistor_251_out, transistor_270_out,
       transistor_281_out, transistor_292_out, transistor_302_out, transistor_312_out, transistor_321_out,
       transistor_331_out, transistor_339_out, transistor_344_out, transistor_348_out, transistor_353_out,
       transistor_357_out, transistor_367_out, transistor_377_out, transistor_387_out, transistor_388_out,
       transistor_403_out, transistor_412_out, transistor_421_out, transistor_427_out, transistor_428_out,
       transistor_449_out, transistor_458_out, transistor_465_out, transistor_476_out, transistor_484_out,
       transistor_491_out, transistor_502_out, transistor_503_out, transistor_517_out, transistor_524_out,
       transistor_535_out, transistor_548_out, transistor_561_out, transistor_574_out, transistor_587_out,
       transistor_588_out, transistor_610_out, transistor_612_out, transistor_618_out, transistor_628_out,
       transistor_638_out, transistor_647_out, transistor_659_out, transistor_660_out, transistor_681_out,
       transistor_694_out, transistor_705_out, transistor_716_out, transistor_727_out, transistor_738_out,
       transistor_748_out, transistor_760_out, transistor_771_out, transistor_783_out, transistor_793_out,
       transistor_805_out, transistor_816_out, transistor_817_out, transistor_838_out, transistor_851_out,
       transistor_863_out, transistor_875_out, transistor_888_out, transistor_902_out, transistor_916_out,
       transistor_917_out, transistor_938_out, transistor_952_out, transistor_965_out, transistor_979_out,
       transistor_994_out, transistor_1007_out, transistor_1021_out, transistor_1022_out,
       transistor_1047_out, transistor_1056_out, transistor_1067_out, transistor_1078_out,
       transistor_1089_out, transistor_1100_out, transistor_1112_out;

  not not_1 (not_1_out, M5);
  not not_2 (not_2_out, H40);
  not not_3 (not_3_out, H8);
  not not_4 (not_4_out, H7);
  not not_5 (not_5_out, H6);
  not not_6 (not_6_out, H5);
  not not_7 (not_7_out, H4);
  not not_8 (not_8_out, H3);
  not not_9 (not_9_out, H2);
  not not_10 (not_10_out, H1);
  not not_11 (not_11_out, H0);
  or or_1 (HPLA_0, transistor_1_out, transistor_12_out);
  Transistor #(.\type ("n")) transistor_1 (.in(1'b0), .out(transistor_1_out), .gate(H40));
  Transistor #(.\type ("n")) transistor_2 (.in(1'b0), .out(transistor_1_out), .gate(not_3_out));
  Transistor #(.\type ("n")) transistor_3 (.in(1'b0), .out(transistor_1_out), .gate(H7));
  Transistor #(.\type ("n")) transistor_4 (.in(1'b0), .out(transistor_1_out), .gate(H6));
  Transistor #(.\type ("n")) transistor_5 (.in(1'b0), .out(transistor_1_out), .gate(not_6_out));
  Transistor #(.\type ("n")) transistor_6 (.in(1'b0), .out(transistor_1_out), .gate(H4));
  Transistor #(.\type ("n")) transistor_7 (.in(1'b0), .out(transistor_1_out), .gate(H3));
  Transistor #(.\type ("n")) transistor_8 (.in(1'b0), .out(transistor_1_out), .gate(not_9_out));
  Transistor #(.\type ("n")) transistor_9 (.in(1'b0), .out(transistor_1_out), .gate(not_10_out));
  Transistor #(.\type ("n")) transistor_10 (.in(1'b0), .out(transistor_1_out), .gate(H0));
  Pull_Resistor #(.pull(1)) pull_resistor_1 (.node(transistor_1_out));
  Transistor #(.\type ("n")) transistor_11 (.in(1'b0), .out(transistor_11_out), .gate(H40));
  Transistor #(.\type ("n")) transistor_12 (.in(1'b0), .out(transistor_12_out), .gate(not_2_out));
  Transistor #(.\type ("n")) transistor_13 (.in(1'b0), .out(transistor_11_out), .gate(H8));
  Transistor #(.\type ("n")) transistor_14 (.in(1'b0), .out(transistor_12_out), .gate(not_3_out));
  Transistor #(.\type ("n")) transistor_15 (.in(1'b0), .out(transistor_12_out), .gate(H7));
  Transistor #(.\type ("n")) transistor_16 (.in(1'b0), .out(transistor_11_out), .gate(not_4_out));
  Transistor #(.\type ("n")) transistor_17 (.in(1'b0), .out(transistor_11_out), .gate(not_5_out));
  Transistor #(.\type ("n")) transistor_18 (.in(1'b0), .out(transistor_12_out), .gate(not_5_out));
  Transistor #(.\type ("n")) transistor_19 (.in(1'b0), .out(transistor_11_out), .gate(H5));
  Transistor #(.\type ("n")) transistor_20 (.in(1'b0), .out(transistor_12_out), .gate(not_6_out));
  Transistor #(.\type ("n")) transistor_21 (.in(1'b0), .out(transistor_12_out), .gate(H4));
  Transistor #(.\type ("n")) transistor_22 (.in(1'b0), .out(transistor_11_out), .gate(H4));
  Transistor #(.\type ("n")) transistor_23 (.in(1'b0), .out(transistor_12_out), .gate(not_8_out));
  Transistor #(.\type ("n")) transistor_24 (.in(1'b0), .out(transistor_11_out), .gate(not_8_out));
  Transistor #(.\type ("n")) transistor_25 (.in(1'b0), .out(transistor_12_out), .gate(H2));
  Transistor #(.\type ("n")) transistor_26 (.in(1'b0), .out(transistor_11_out), .gate(not_9_out));
  Transistor #(.\type ("n")) transistor_27 (.in(1'b0), .out(transistor_12_out), .gate(not_10_out));
  Transistor #(.\type ("n")) transistor_28 (.in(1'b0), .out(transistor_11_out), .gate(not_10_out));
  Transistor #(.\type ("n")) transistor_29 (.in(1'b0), .out(transistor_11_out), .gate(H0));
  Transistor #(.\type ("n")) transistor_30 (.in(1'b0), .out(transistor_12_out), .gate(not_11_out));
  Pull_Resistor #(.pull(1)) pull_resistor_2 (.node(transistor_11_out));
  Pull_Resistor #(.pull(1)) pull_resistor_3 (.node(transistor_12_out));
  or or_2 (HPLA_1, transistor_11_out, transistor_31_out);
  Transistor #(.\type ("n")) transistor_31 (.in(1'b0), .out(transistor_31_out), .gate(not_2_out));
  Transistor #(.\type ("n")) transistor_32 (.in(1'b0), .out(transistor_31_out), .gate(H8));
  Transistor #(.\type ("n")) transistor_33 (.in(1'b0), .out(transistor_31_out), .gate(not_4_out));
  Transistor #(.\type ("n")) transistor_34 (.in(1'b0), .out(transistor_31_out), .gate(not_5_out));
  Transistor #(.\type ("n")) transistor_35 (.in(1'b0), .out(transistor_31_out), .gate(not_6_out));
  Transistor #(.\type ("n")) transistor_36 (.in(1'b0), .out(transistor_31_out), .gate(not_7_out));
  Transistor #(.\type ("n")) transistor_37 (.in(1'b0), .out(transistor_31_out), .gate(not_8_out));
  Transistor #(.\type ("n")) transistor_38 (.in(1'b0), .out(transistor_31_out), .gate(not_9_out));
  Transistor #(.\type ("n")) transistor_39 (.in(1'b0), .out(transistor_31_out), .gate(H1));
  Transistor #(.\type ("n")) transistor_40 (.in(1'b0), .out(transistor_31_out), .gate(not_11_out));
  Pull_Resistor #(.pull(1)) pull_resistor_4 (.node(transistor_31_out));
  or or_3 (HPLA_2, transistor_41_out, transistor_51_out);
  Transistor #(.\type ("n")) transistor_41 (.in(1'b0), .out(transistor_41_out), .gate(H40));
  Transistor #(.\type ("n")) transistor_42 (.in(1'b0), .out(transistor_41_out), .gate(H8));
  Transistor #(.\type ("n")) transistor_43 (.in(1'b0), .out(transistor_41_out), .gate(H7));
  Transistor #(.\type ("n")) transistor_44 (.in(1'b0), .out(transistor_41_out), .gate(H6));
  Transistor #(.\type ("n")) transistor_45 (.in(1'b0), .out(transistor_41_out), .gate(not_6_out));
  Transistor #(.\type ("n")) transistor_46 (.in(1'b0), .out(transistor_41_out), .gate(H4));
  Transistor #(.\type ("n")) transistor_47 (.in(1'b0), .out(transistor_41_out), .gate(H3));
  Transistor #(.\type ("n")) transistor_48 (.in(1'b0), .out(transistor_41_out), .gate(not_9_out));
  Transistor #(.\type ("n")) transistor_49 (.in(1'b0), .out(transistor_41_out), .gate(H1));
  Transistor #(.\type ("n")) transistor_50 (.in(1'b0), .out(transistor_41_out), .gate(H0));
  Pull_Resistor #(.pull(1)) pull_resistor_5 (.node(transistor_41_out));
  Transistor #(.\type ("n")) transistor_51 (.in(1'b0), .out(transistor_51_out), .gate(not_2_out));
  Transistor #(.\type ("n")) transistor_52 (.in(1'b0), .out(transistor_51_out), .gate(H8));
  Transistor #(.\type ("n")) transistor_53 (.in(1'b0), .out(transistor_51_out), .gate(H7));
  Transistor #(.\type ("n")) transistor_54 (.in(1'b0), .out(transistor_51_out), .gate(H6));
  Transistor #(.\type ("n")) transistor_55 (.in(1'b0), .out(transistor_51_out), .gate(not_6_out));
  Transistor #(.\type ("n")) transistor_56 (.in(1'b0), .out(transistor_51_out), .gate(H4));
  Transistor #(.\type ("n")) transistor_57 (.in(1'b0), .out(transistor_51_out), .gate(not_8_out));
  Transistor #(.\type ("n")) transistor_58 (.in(1'b0), .out(transistor_51_out), .gate(H2));
  Transistor #(.\type ("n")) transistor_59 (.in(1'b0), .out(transistor_51_out), .gate(not_10_out));
  Transistor #(.\type ("n")) transistor_60 (.in(1'b0), .out(transistor_51_out), .gate(not_11_out));
  Pull_Resistor #(.pull(1)) pull_resistor_6 (.node(transistor_51_out));
  or or_4 (HPLA_3, transistor_61_out, transistor_71_out);
  Transistor #(.\type ("n")) transistor_61 (.in(1'b0), .out(transistor_61_out), .gate(_0));
  Transistor #(.\type ("n")) transistor_62 (.in(1'b0), .out(transistor_61_out), .gate(H8));
  Transistor #(.\type ("n")) transistor_63 (.in(1'b0), .out(transistor_61_out), .gate(H7));
  Transistor #(.\type ("n")) transistor_64 (.in(1'b0), .out(transistor_61_out), .gate(H6));
  Transistor #(.\type ("n")) transistor_65 (.in(1'b0), .out(transistor_61_out), .gate(H5));
  Transistor #(.\type ("n")) transistor_66 (.in(1'b0), .out(transistor_61_out), .gate(H4));
  Transistor #(.\type ("n")) transistor_67 (.in(1'b0), .out(transistor_61_out), .gate(not_8_out));
  Transistor #(.\type ("n")) transistor_68 (.in(1'b0), .out(transistor_61_out), .gate(H2));
  Transistor #(.\type ("n")) transistor_69 (.in(1'b0), .out(transistor_61_out), .gate(not_10_out));
  Transistor #(.\type ("n")) transistor_70 (.in(1'b0), .out(transistor_61_out), .gate(H0));
  Pull_Resistor #(.pull(1)) pull_resistor_7 (.node(transistor_61_out));
  Transistor #(.\type ("n")) transistor_71 (.in(1'b0), .out(transistor_71_out), .gate(H8));
  Transistor #(.\type ("n")) transistor_72 (.in(1'b0), .out(transistor_71_out), .gate(H7));
  Transistor #(.\type ("n")) transistor_73 (.in(1'b0), .out(transistor_71_out), .gate(H6));
  Transistor #(.\type ("n")) transistor_74 (.in(1'b0), .out(transistor_71_out), .gate(H5));
  Transistor #(.\type ("n")) transistor_75 (.in(1'b0), .out(transistor_71_out), .gate(not_7_out));
  Transistor #(.\type ("n")) transistor_76 (.in(1'b0), .out(transistor_71_out), .gate(H3));
  Transistor #(.\type ("n")) transistor_77 (.in(1'b0), .out(transistor_71_out), .gate(H2));
  Transistor #(.\type ("n")) transistor_78 (.in(1'b0), .out(transistor_71_out), .gate(not_10_out));
  Transistor #(.\type ("n")) transistor_79 (.in(1'b0), .out(transistor_71_out), .gate(H0));
  Pull_Resistor #(.pull(1)) pull_resistor_8 (.node(transistor_71_out));
  or or_5 (HPLA_4, transistor_80_out, transistor_91_out);
  Transistor #(.\type ("n")) transistor_80 (.in(1'b0), .out(transistor_80_out), .gate(H40));
  Transistor #(.\type ("n")) transistor_81 (.in(1'b0), .out(transistor_80_out), .gate(not_3_out));
  Transistor #(.\type ("n")) transistor_82 (.in(1'b0), .out(transistor_80_out), .gate(H7));
  Transistor #(.\type ("n")) transistor_83 (.in(1'b0), .out(transistor_80_out), .gate(H6));
  Transistor #(.\type ("n")) transistor_84 (.in(1'b0), .out(transistor_80_out), .gate(H5));
  Transistor #(.\type ("n")) transistor_85 (.in(1'b0), .out(transistor_80_out), .gate(H4));
  Transistor #(.\type ("n")) transistor_86 (.in(1'b0), .out(transistor_80_out), .gate(not_8_out));
  Transistor #(.\type ("n")) transistor_87 (.in(1'b0), .out(transistor_80_out), .gate(H2));
  Transistor #(.\type ("n")) transistor_88 (.in(1'b0), .out(transistor_80_out), .gate(not_10_out));
  Transistor #(.\type ("n")) transistor_89 (.in(1'b0), .out(transistor_80_out), .gate(H0));
  Pull_Resistor #(.pull(1)) pull_resistor_9 (.node(transistor_80_out));
  Transistor #(.\type ("n")) transistor_90 (.in(1'b0), .out(transistor_90_out), .gate(H40));
  Transistor #(.\type ("n")) transistor_91 (.in(1'b0), .out(transistor_91_out), .gate(not_2_out));
  Transistor #(.\type ("n")) transistor_92 (.in(1'b0), .out(transistor_90_out), .gate(not_3_out));
  Transistor #(.\type ("n")) transistor_93 (.in(1'b0), .out(transistor_91_out), .gate(not_3_out));
  Transistor #(.\type ("n")) transistor_94 (.in(1'b0), .out(transistor_90_out), .gate(H7));
  Transistor #(.\type ("n")) transistor_95 (.in(1'b0), .out(transistor_91_out), .gate(H7));
  Transistor #(.\type ("n")) transistor_96 (.in(1'b0), .out(transistor_90_out), .gate(H6));
  Transistor #(.\type ("n")) transistor_97 (.in(1'b0), .out(transistor_91_out), .gate(not_5_out));
  Transistor #(.\type ("n")) transistor_98 (.in(1'b0), .out(transistor_91_out), .gate(H5));
  Transistor #(.\type ("n")) transistor_99 (.in(1'b0), .out(transistor_90_out), .gate(H5));
  Transistor #(.\type ("n")) transistor_100 (.in(1'b0), .out(transistor_91_out), .gate(H4));
  Transistor #(.\type ("n")) transistor_101 (.in(1'b0), .out(transistor_90_out), .gate(not_7_out));
  Transistor #(.\type ("n")) transistor_102 (.in(1'b0), .out(transistor_91_out), .gate(not_8_out));
  Transistor #(.\type ("n")) transistor_103 (.in(1'b0), .out(transistor_90_out), .gate(not_8_out));
  Transistor #(.\type ("n")) transistor_104 (.in(1'b0), .out(transistor_91_out), .gate(H2));
  Transistor #(.\type ("n")) transistor_105 (.in(1'b0), .out(transistor_90_out), .gate(not_9_out));
  Transistor #(.\type ("n")) transistor_106 (.in(1'b0), .out(transistor_90_out), .gate(H1));
  Transistor #(.\type ("n")) transistor_107 (.in(1'b0), .out(transistor_91_out), .gate(not_10_out));
  Transistor #(.\type ("n")) transistor_108 (.in(1'b0), .out(transistor_90_out), .gate(H0));
  Transistor #(.\type ("n")) transistor_109 (.in(1'b0), .out(transistor_91_out), .gate(H0));
  Pull_Resistor #(.pull(1)) pull_resistor_10 (.node(transistor_90_out));
  Pull_Resistor #(.pull(1)) pull_resistor_11 (.node(transistor_91_out));
  or or_6 (HPLA_5, transistor_90_out, transistor_110_out);
  Transistor #(.\type ("n")) transistor_110 (.in(1'b0), .out(transistor_110_out), .gate(not_2_out));
  Transistor #(.\type ("n")) transistor_111 (.in(1'b0), .out(transistor_110_out), .gate(not_3_out));
  Transistor #(.\type ("n")) transistor_112 (.in(1'b0), .out(transistor_110_out), .gate(H7));
  Transistor #(.\type ("n")) transistor_113 (.in(1'b0), .out(transistor_110_out), .gate(not_5_out));
  Transistor #(.\type ("n")) transistor_114 (.in(1'b0), .out(transistor_110_out), .gate(H5));
  Transistor #(.\type ("n")) transistor_115 (.in(1'b0), .out(transistor_110_out), .gate(not_7_out));
  Transistor #(.\type ("n")) transistor_116 (.in(1'b0), .out(transistor_110_out), .gate(not_8_out));
  Transistor #(.\type ("n")) transistor_117 (.in(1'b0), .out(transistor_110_out), .gate(not_9_out));
  Transistor #(.\type ("n")) transistor_118 (.in(1'b0), .out(transistor_110_out), .gate(H1));
  Transistor #(.\type ("n")) transistor_119 (.in(1'b0), .out(transistor_110_out), .gate(H0));
  Pull_Resistor #(.pull(1)) pull_resistor_12 (.node(transistor_110_out));
  or or_7 (HPLA_6, transistor_120_out, transistor_130_out);
  Transistor #(.\type ("n")) transistor_120 (.in(1'b0), .out(transistor_120_out), .gate(H40));
  Transistor #(.\type ("n")) transistor_121 (.in(1'b0), .out(transistor_120_out), .gate(H8));
  Transistor #(.\type ("n")) transistor_122 (.in(1'b0), .out(transistor_120_out), .gate(H7));
  Transistor #(.\type ("n")) transistor_123 (.in(1'b0), .out(transistor_120_out), .gate(H6));
  Transistor #(.\type ("n")) transistor_124 (.in(1'b0), .out(transistor_120_out), .gate(H5));
  Transistor #(.\type ("n")) transistor_125 (.in(1'b0), .out(transistor_120_out), .gate(H4));
  Transistor #(.\type ("n")) transistor_126 (.in(1'b0), .out(transistor_120_out), .gate(H3));
  Transistor #(.\type ("n")) transistor_127 (.in(1'b0), .out(transistor_120_out), .gate(H2));
  Transistor #(.\type ("n")) transistor_128 (.in(1'b0), .out(transistor_120_out), .gate(H1));
  Transistor #(.\type ("n")) transistor_129 (.in(1'b0), .out(transistor_120_out), .gate(H0));
  Pull_Resistor #(.pull(1)) pull_resistor_13 (.node(transistor_120_out));
  Transistor #(.\type ("n")) transistor_130 (.in(1'b0), .out(transistor_130_out), .gate(not_2_out));
  Transistor #(.\type ("n")) transistor_131 (.in(1'b0), .out(transistor_130_out), .gate(H8));
  Transistor #(.\type ("n")) transistor_132 (.in(1'b0), .out(transistor_130_out), .gate(H7));
  Transistor #(.\type ("n")) transistor_133 (.in(1'b0), .out(transistor_130_out), .gate(H6));
  Transistor #(.\type ("n")) transistor_134 (.in(1'b0), .out(transistor_130_out), .gate(H5));
  Transistor #(.\type ("n")) transistor_135 (.in(1'b0), .out(transistor_130_out), .gate(H4));
  Transistor #(.\type ("n")) transistor_136 (.in(1'b0), .out(transistor_130_out), .gate(H3));
  Transistor #(.\type ("n")) transistor_137 (.in(1'b0), .out(transistor_130_out), .gate(H2));
  Transistor #(.\type ("n")) transistor_138 (.in(1'b0), .out(transistor_130_out), .gate(H1));
  Transistor #(.\type ("n")) transistor_139 (.in(1'b0), .out(transistor_130_out), .gate(not_11_out));
  Pull_Resistor #(.pull(1)) pull_resistor_14 (.node(transistor_130_out));
  or or_8 (HPLA_7, transistor_140_out, transistor_150_out);
  Transistor #(.\type ("n")) transistor_140 (.in(1'b0), .out(transistor_140_out), .gate(H40));
  Transistor #(.\type ("n")) transistor_141 (.in(1'b0), .out(transistor_140_out), .gate(H8));
  Transistor #(.\type ("n")) transistor_142 (.in(1'b0), .out(transistor_140_out), .gate(H7));
  Transistor #(.\type ("n")) transistor_143 (.in(1'b0), .out(transistor_140_out), .gate(not_5_out));
  Transistor #(.\type ("n")) transistor_144 (.in(1'b0), .out(transistor_140_out), .gate(H5));
  Transistor #(.\type ("n")) transistor_145 (.in(1'b0), .out(transistor_140_out), .gate(not_7_out));
  Transistor #(.\type ("n")) transistor_146 (.in(1'b0), .out(transistor_140_out), .gate(not_8_out));
  Transistor #(.\type ("n")) transistor_147 (.in(1'b0), .out(transistor_140_out), .gate(not_9_out));
  Transistor #(.\type ("n")) transistor_148 (.in(1'b0), .out(transistor_140_out), .gate(not_10_out));
  Transistor #(.\type ("n")) transistor_149 (.in(1'b0), .out(transistor_140_out), .gate(not_11_out));
  Pull_Resistor #(.pull(1)) pull_resistor_15 (.node(transistor_140_out));
  Transistor #(.\type ("n")) transistor_150 (.in(1'b0), .out(transistor_150_out), .gate(not_2_out));
  Transistor #(.\type ("n")) transistor_151 (.in(1'b0), .out(transistor_150_out), .gate(H8));
  Transistor #(.\type ("n")) transistor_152 (.in(1'b0), .out(transistor_150_out), .gate(H7));
  Transistor #(.\type ("n")) transistor_153 (.in(1'b0), .out(transistor_150_out), .gate(not_5_out));
  Transistor #(.\type ("n")) transistor_154 (.in(1'b0), .out(transistor_150_out), .gate(not_6_out));
  Transistor #(.\type ("n")) transistor_155 (.in(1'b0), .out(transistor_150_out), .gate(not_7_out));
  Transistor #(.\type ("n")) transistor_156 (.in(1'b0), .out(transistor_150_out), .gate(not_8_out));
  Transistor #(.\type ("n")) transistor_157 (.in(1'b0), .out(transistor_150_out), .gate(H2));
  Transistor #(.\type ("n")) transistor_158 (.in(1'b0), .out(transistor_150_out), .gate(H1));
  Transistor #(.\type ("n")) transistor_159 (.in(1'b0), .out(transistor_150_out), .gate(H0));
  Pull_Resistor #(.pull(1)) pull_resistor_16 (.node(transistor_150_out));
  or or_9 (HPLA_8, transistor_160_out, transistor_171_out);
  Transistor #(.\type ("n")) transistor_160 (.in(1'b0), .out(transistor_160_out), .gate(H40));
  Transistor #(.\type ("n")) transistor_161 (.in(1'b0), .out(transistor_160_out), .gate(H8));
  Transistor #(.\type ("n")) transistor_162 (.in(1'b0), .out(transistor_160_out), .gate(H7));
  Transistor #(.\type ("n")) transistor_163 (.in(1'b0), .out(transistor_160_out), .gate(not_5_out));
  Transistor #(.\type ("n")) transistor_164 (.in(1'b0), .out(transistor_160_out), .gate(not_6_out));
  Transistor #(.\type ("n")) transistor_165 (.in(1'b0), .out(transistor_160_out), .gate(not_7_out));
  Transistor #(.\type ("n")) transistor_166 (.in(1'b0), .out(transistor_160_out), .gate(not_8_out));
  Transistor #(.\type ("n")) transistor_167 (.in(1'b0), .out(transistor_160_out), .gate(H2));
  Transistor #(.\type ("n")) transistor_168 (.in(1'b0), .out(transistor_160_out), .gate(H1));
  Transistor #(.\type ("n")) transistor_169 (.in(1'b0), .out(transistor_160_out), .gate(not_11_out));
  Pull_Resistor #(.pull(1)) pull_resistor_17 (.node(transistor_160_out));
  Transistor #(.\type ("n")) transistor_170 (.in(1'b0), .out(transistor_170_out), .gate(H40));
  Transistor #(.\type ("n")) transistor_171 (.in(1'b0), .out(transistor_171_out), .gate(not_2_out));
  Transistor #(.\type ("n")) transistor_172 (.in(1'b0), .out(transistor_171_out), .gate(H8));
  Transistor #(.\type ("n")) transistor_173 (.in(1'b0), .out(transistor_170_out), .gate(not_3_out));
  Transistor #(.\type ("n")) transistor_174 (.in(1'b0), .out(transistor_171_out), .gate(not_4_out));
  Transistor #(.\type ("n")) transistor_175 (.in(1'b0), .out(transistor_170_out), .gate(not_4_out));
  Transistor #(.\type ("n")) transistor_176 (.in(1'b0), .out(transistor_171_out), .gate(H6));
  Transistor #(.\type ("n")) transistor_177 (.in(1'b0), .out(transistor_170_out), .gate(not_5_out));
  Transistor #(.\type ("n")) transistor_178 (.in(1'b0), .out(transistor_171_out), .gate(H5));
  Transistor #(.\type ("n")) transistor_179 (.in(1'b0), .out(transistor_170_out), .gate(H5));
  Transistor #(.\type ("n")) transistor_180 (.in(1'b0), .out(transistor_170_out), .gate(not_7_out));
  Transistor #(.\type ("n")) transistor_181 (.in(1'b0), .out(transistor_171_out), .gate(not_7_out));
  Transistor #(.\type ("n")) transistor_182 (.in(1'b0), .out(transistor_171_out), .gate(H3));
  Transistor #(.\type ("n")) transistor_183 (.in(1'b0), .out(transistor_170_out), .gate(not_8_out));
  Transistor #(.\type ("n")) transistor_184 (.in(1'b0), .out(transistor_170_out), .gate(H2));
  Transistor #(.\type ("n")) transistor_185 (.in(1'b0), .out(transistor_171_out), .gate(not_9_out));
  Transistor #(.\type ("n")) transistor_186 (.in(1'b0), .out(transistor_171_out), .gate(H1));
  Transistor #(.\type ("n")) transistor_187 (.in(1'b0), .out(transistor_170_out), .gate(not_10_out));
  Transistor #(.\type ("n")) transistor_188 (.in(1'b0), .out(transistor_171_out), .gate(H0));
  Transistor #(.\type ("n")) transistor_189 (.in(1'b0), .out(transistor_170_out), .gate(not_11_out));
  Pull_Resistor #(.pull(1)) pull_resistor_18 (.node(transistor_170_out));
  Pull_Resistor #(.pull(1)) pull_resistor_19 (.node(transistor_171_out));
  or or_10 (HPLA_9, transistor_170_out, transistor_190_out, transistor_200_out, transistor_210_out);
  Transistor #(.\type ("n")) transistor_190 (.in(1'b0), .out(transistor_190_out), .gate(H40));
  Transistor #(.\type ("n")) transistor_191 (.in(1'b0), .out(transistor_190_out), .gate(H8));
  Transistor #(.\type ("n")) transistor_192 (.in(1'b0), .out(transistor_190_out), .gate(not_4_out));
  Transistor #(.\type ("n")) transistor_193 (.in(1'b0), .out(transistor_190_out), .gate(H6));
  Transistor #(.\type ("n")) transistor_194 (.in(1'b0), .out(transistor_190_out), .gate(H5));
  Transistor #(.\type ("n")) transistor_195 (.in(1'b0), .out(transistor_190_out), .gate(H4));
  Transistor #(.\type ("n")) transistor_196 (.in(1'b0), .out(transistor_190_out), .gate(H3));
  Transistor #(.\type ("n")) transistor_197 (.in(1'b0), .out(transistor_190_out), .gate(not_9_out));
  Transistor #(.\type ("n")) transistor_198 (.in(1'b0), .out(transistor_190_out), .gate(not_10_out));
  Transistor #(.\type ("n")) transistor_199 (.in(1'b0), .out(transistor_190_out), .gate(H0));
  Pull_Resistor #(.pull(1)) pull_resistor_20 (.node(transistor_190_out));
  Transistor #(.\type ("n")) transistor_200 (.in(1'b0), .out(transistor_200_out), .gate(not_2_out));
  Transistor #(.\type ("n")) transistor_201 (.in(1'b0), .out(transistor_200_out), .gate(not_3_out));
  Transistor #(.\type ("n")) transistor_202 (.in(1'b0), .out(transistor_200_out), .gate(not_4_out));
  Transistor #(.\type ("n")) transistor_203 (.in(1'b0), .out(transistor_200_out), .gate(not_5_out));
  Transistor #(.\type ("n")) transistor_204 (.in(1'b0), .out(transistor_200_out), .gate(H5));
  Transistor #(.\type ("n")) transistor_205 (.in(1'b0), .out(transistor_200_out), .gate(not_7_out));
  Transistor #(.\type ("n")) transistor_206 (.in(1'b0), .out(transistor_200_out), .gate(H3));
  Transistor #(.\type ("n")) transistor_207 (.in(1'b0), .out(transistor_200_out), .gate(H2));
  Transistor #(.\type ("n")) transistor_208 (.in(1'b0), .out(transistor_200_out), .gate(not_10_out));
  Transistor #(.\type ("n")) transistor_209 (.in(1'b0), .out(transistor_200_out), .gate(H0));
  Pull_Resistor #(.pull(1)) pull_resistor_21 (.node(transistor_200_out));
  Transistor #(.\type ("n")) transistor_210 (.in(1'b0), .out(transistor_210_out), .gate(not_2_out));
  Transistor #(.\type ("n")) transistor_211 (.in(1'b0), .out(transistor_210_out), .gate(H8));
  Transistor #(.\type ("n")) transistor_212 (.in(1'b0), .out(transistor_210_out), .gate(not_4_out));
  Transistor #(.\type ("n")) transistor_213 (.in(1'b0), .out(transistor_210_out), .gate(H6));
  Transistor #(.\type ("n")) transistor_214 (.in(1'b0), .out(transistor_210_out), .gate(not_6_out));
  Transistor #(.\type ("n")) transistor_215 (.in(1'b0), .out(transistor_210_out), .gate(H4));
  Transistor #(.\type ("n")) transistor_216 (.in(1'b0), .out(transistor_210_out), .gate(H3));
  Transistor #(.\type ("n")) transistor_217 (.in(1'b0), .out(transistor_210_out), .gate(not_9_out));
  Transistor #(.\type ("n")) transistor_218 (.in(1'b0), .out(transistor_210_out), .gate(H1));
  Transistor #(.\type ("n")) transistor_219 (.in(1'b0), .out(transistor_210_out), .gate(H0));
  Pull_Resistor #(.pull(1)) pull_resistor_22 (.node(transistor_210_out));
  or or_11 (HPLA_10, transistor_220_out, transistor_230_out);
  Transistor #(.\type ("n")) transistor_220 (.in(1'b0), .out(transistor_220_out), .gate(H40));
  Transistor #(.\type ("n")) transistor_221 (.in(1'b0), .out(transistor_220_out), .gate(not_3_out));
  Transistor #(.\type ("n")) transistor_222 (.in(1'b0), .out(transistor_220_out), .gate(H7));
  Transistor #(.\type ("n")) transistor_223 (.in(1'b0), .out(transistor_220_out), .gate(H6));
  Transistor #(.\type ("n")) transistor_224 (.in(1'b0), .out(transistor_220_out), .gate(not_6_out));
  Transistor #(.\type ("n")) transistor_225 (.in(1'b0), .out(transistor_220_out), .gate(H4));
  Transistor #(.\type ("n")) transistor_226 (.in(1'b0), .out(transistor_220_out), .gate(H3));
  Transistor #(.\type ("n")) transistor_227 (.in(1'b0), .out(transistor_220_out), .gate(not_9_out));
  Transistor #(.\type ("n")) transistor_228 (.in(1'b0), .out(transistor_220_out), .gate(H1));
  Transistor #(.\type ("n")) transistor_229 (.in(1'b0), .out(transistor_220_out), .gate(H0));
  Pull_Resistor #(.pull(1)) pull_resistor_23 (.node(transistor_220_out));
  Transistor #(.\type ("n")) transistor_230 (.in(1'b0), .out(transistor_230_out), .gate(not_2_out));
  Transistor #(.\type ("n")) transistor_231 (.in(1'b0), .out(transistor_230_out), .gate(not_3_out));
  Transistor #(.\type ("n")) transistor_232 (.in(1'b0), .out(transistor_230_out), .gate(H7));
  Transistor #(.\type ("n")) transistor_233 (.in(1'b0), .out(transistor_230_out), .gate(not_5_out));
  Transistor #(.\type ("n")) transistor_234 (.in(1'b0), .out(transistor_230_out), .gate(not_6_out));
  Transistor #(.\type ("n")) transistor_235 (.in(1'b0), .out(transistor_230_out), .gate(H4));
  Transistor #(.\type ("n")) transistor_236 (.in(1'b0), .out(transistor_230_out), .gate(H3));
  Transistor #(.\type ("n")) transistor_237 (.in(1'b0), .out(transistor_230_out), .gate(not_9_out));
  Transistor #(.\type ("n")) transistor_238 (.in(1'b0), .out(transistor_230_out), .gate(not_10_out));
  Transistor #(.\type ("n")) transistor_239 (.in(1'b0), .out(transistor_230_out), .gate(H0));
  Pull_Resistor #(.pull(1)) pull_resistor_24 (.node(transistor_230_out));
  or or_12 (HPLA_11, transistor_240_out, transistor_251_out);
  Transistor #(.\type ("n")) transistor_240 (.in(1'b0), .out(transistor_240_out), .gate(H40));
  Transistor #(.\type ("n")) transistor_241 (.in(1'b0), .out(transistor_240_out), .gate(not_3_out));
  Transistor #(.\type ("n")) transistor_242 (.in(1'b0), .out(transistor_240_out), .gate(not_4_out));
  Transistor #(.\type ("n")) transistor_243 (.in(1'b0), .out(transistor_240_out), .gate(not_5_out));
  Transistor #(.\type ("n")) transistor_244 (.in(1'b0), .out(transistor_240_out), .gate(not_6_out));
  Transistor #(.\type ("n")) transistor_245 (.in(1'b0), .out(transistor_240_out), .gate(H4));
  Transistor #(.\type ("n")) transistor_246 (.in(1'b0), .out(transistor_240_out), .gate(not_8_out));
  Transistor #(.\type ("n")) transistor_247 (.in(1'b0), .out(transistor_240_out), .gate(H2));
  Transistor #(.\type ("n")) transistor_248 (.in(1'b0), .out(transistor_240_out), .gate(H1));
  Transistor #(.\type ("n")) transistor_249 (.in(1'b0), .out(transistor_240_out), .gate(H0));
  Pull_Resistor #(.pull(1)) pull_resistor_25 (.node(transistor_240_out));
  Transistor #(.\type ("n")) transistor_250 (.in(1'b0), .out(transistor_250_out), .gate(M5));
  Transistor #(.\type ("n")) transistor_251 (.in(1'b0), .out(transistor_251_out), .gate(not_2_out));
  Transistor #(.\type ("n")) transistor_252 (.in(1'b0), .out(transistor_251_out), .gate(not_3_out));
  Transistor #(.\type ("n")) transistor_253 (.in(1'b0), .out(transistor_250_out), .gate(not_3_out));
  Transistor #(.\type ("n")) transistor_254 (.in(1'b0), .out(transistor_250_out), .gate(not_4_out));
  Transistor #(.\type ("n")) transistor_255 (.in(1'b0), .out(transistor_251_out), .gate(not_4_out));
  Transistor #(.\type ("n")) transistor_256 (.in(1'b0), .out(transistor_250_out), .gate(not_5_out));
  Transistor #(.\type ("n")) transistor_257 (.in(1'b0), .out(transistor_251_out), .gate(not_5_out));
  Transistor #(.\type ("n")) transistor_258 (.in(1'b0), .out(transistor_251_out), .gate(not_6_out));
  Transistor #(.\type ("n")) transistor_259 (.in(1'b0), .out(transistor_250_out), .gate(not_6_out));
  Transistor #(.\type ("n")) transistor_260 (.in(1'b0), .out(transistor_251_out), .gate(H4));
  Transistor #(.\type ("n")) transistor_261 (.in(1'b0), .out(transistor_250_out), .gate(H4));
  Transistor #(.\type ("n")) transistor_262 (.in(1'b0), .out(transistor_251_out), .gate(H3));
  Transistor #(.\type ("n")) transistor_263 (.in(1'b0), .out(transistor_250_out), .gate(not_8_out));
  Transistor #(.\type ("n")) transistor_264 (.in(1'b0), .out(transistor_250_out), .gate(H2));
  Transistor #(.\type ("n")) transistor_265 (.in(1'b0), .out(transistor_251_out), .gate(H2));
  Transistor #(.\type ("n")) transistor_266 (.in(1'b0), .out(transistor_250_out), .gate(H1));
  Transistor #(.\type ("n")) transistor_267 (.in(1'b0), .out(transistor_251_out), .gate(not_10_out));
  Transistor #(.\type ("n")) transistor_268 (.in(1'b0), .out(transistor_250_out), .gate(H0));
  Transistor #(.\type ("n")) transistor_269 (.in(1'b0), .out(transistor_251_out), .gate(H0));
  Pull_Resistor #(.pull(1)) pull_resistor_26 (.node(transistor_250_out));
  Pull_Resistor #(.pull(1)) pull_resistor_27 (.node(transistor_251_out));
  nor nor_1 (HPLA_12, transistor_250_out, transistor_270_out, transistor_281_out);
  Transistor #(.\type ("n")) transistor_270 (.in(1'b0), .out(transistor_270_out), .gate(not_1_out));
  Transistor #(.\type ("n")) transistor_271 (.in(1'b0), .out(transistor_270_out), .gate(H40));
  Transistor #(.\type ("n")) transistor_272 (.in(1'b0), .out(transistor_270_out), .gate(not_3_out));
  Transistor #(.\type ("n")) transistor_273 (.in(1'b0), .out(transistor_270_out), .gate(H7));
  Transistor #(.\type ("n")) transistor_274 (.in(1'b0), .out(transistor_270_out), .gate(H6));
  Transistor #(.\type ("n")) transistor_275 (.in(1'b0), .out(transistor_270_out), .gate(H5));
  Transistor #(.\type ("n")) transistor_276 (.in(1'b0), .out(transistor_270_out), .gate(H4));
  Transistor #(.\type ("n")) transistor_277 (.in(1'b0), .out(transistor_270_out), .gate(not_8_out));
  Transistor #(.\type ("n")) transistor_278 (.in(1'b0), .out(transistor_270_out), .gate(H2));
  Transistor #(.\type ("n")) transistor_279 (.in(1'b0), .out(transistor_270_out), .gate(H1));
  Transistor #(.\type ("n")) transistor_280 (.in(1'b0), .out(transistor_270_out), .gate(H0));
  Pull_Resistor #(.pull(1)) pull_resistor_28 (.node(transistor_270_out));
  Transistor #(.\type ("n")) transistor_281 (.in(1'b0), .out(transistor_281_out), .gate(not_1_out));
  Transistor #(.\type ("n")) transistor_282 (.in(1'b0), .out(transistor_281_out), .gate(not_2_out));
  Transistor #(.\type ("n")) transistor_283 (.in(1'b0), .out(transistor_281_out), .gate(not_3_out));
  Transistor #(.\type ("n")) transistor_284 (.in(1'b0), .out(transistor_281_out), .gate(H7));
  Transistor #(.\type ("n")) transistor_285 (.in(1'b0), .out(transistor_281_out), .gate(not_5_out));
  Transistor #(.\type ("n")) transistor_286 (.in(1'b0), .out(transistor_281_out), .gate(H5));
  Transistor #(.\type ("n")) transistor_287 (.in(1'b0), .out(transistor_281_out), .gate(H4));
  Transistor #(.\type ("n")) transistor_288 (.in(1'b0), .out(transistor_281_out), .gate(not_8_out));
  Transistor #(.\type ("n")) transistor_289 (.in(1'b0), .out(transistor_281_out), .gate(H2));
  Transistor #(.\type ("n")) transistor_290 (.in(1'b0), .out(transistor_281_out), .gate(H1));
  Transistor #(.\type ("n")) transistor_291 (.in(1'b0), .out(transistor_281_out), .gate(H0));
  Pull_Resistor #(.pull(1)) pull_resistor_29 (.node(transistor_281_out));
  or or_13 (HPLA_13, transistor_292_out, transistor_302_out);
  Transistor #(.\type ("n")) transistor_292 (.in(1'b0), .out(transistor_292_out), .gate(H40));
  Transistor #(.\type ("n")) transistor_293 (.in(1'b0), .out(transistor_292_out), .gate(H8));
  Transistor #(.\type ("n")) transistor_294 (.in(1'b0), .out(transistor_292_out), .gate(H7));
  Transistor #(.\type ("n")) transistor_295 (.in(1'b0), .out(transistor_292_out), .gate(not_5_out));
  Transistor #(.\type ("n")) transistor_296 (.in(1'b0), .out(transistor_292_out), .gate(H5));
  Transistor #(.\type ("n")) transistor_297 (.in(1'b0), .out(transistor_292_out), .gate(not_7_out));
  Transistor #(.\type ("n")) transistor_298 (.in(1'b0), .out(transistor_292_out), .gate(not_8_out));
  Transistor #(.\type ("n")) transistor_299 (.in(1'b0), .out(transistor_292_out), .gate(not_9_out));
  Transistor #(.\type ("n")) transistor_300 (.in(1'b0), .out(transistor_292_out), .gate(not_10_out));
  Transistor #(.\type ("n")) transistor_301 (.in(1'b0), .out(transistor_292_out), .gate(not_11_out));
  Pull_Resistor #(.pull(1)) pull_resistor_30 (.node(transistor_292_out));
  Transistor #(.\type ("n")) transistor_302 (.in(1'b0), .out(transistor_302_out), .gate(not_2_out));
  Transistor #(.\type ("n")) transistor_303 (.in(1'b0), .out(transistor_302_out), .gate(H8));
  Transistor #(.\type ("n")) transistor_304 (.in(1'b0), .out(transistor_302_out), .gate(H7));
  Transistor #(.\type ("n")) transistor_305 (.in(1'b0), .out(transistor_302_out), .gate(not_5_out));
  Transistor #(.\type ("n")) transistor_306 (.in(1'b0), .out(transistor_302_out), .gate(not_6_out));
  Transistor #(.\type ("n")) transistor_307 (.in(1'b0), .out(transistor_302_out), .gate(not_7_out));
  Transistor #(.\type ("n")) transistor_308 (.in(1'b0), .out(transistor_302_out), .gate(not_8_out));
  Transistor #(.\type ("n")) transistor_309 (.in(1'b0), .out(transistor_302_out), .gate(H2));
  Transistor #(.\type ("n")) transistor_310 (.in(1'b0), .out(transistor_302_out), .gate(H1));
  Transistor #(.\type ("n")) transistor_311 (.in(1'b0), .out(transistor_302_out), .gate(H0));
  Pull_Resistor #(.pull(1)) pull_resistor_31 (.node(transistor_302_out));
  not not_12 (HPLA_14, not_13_out);
  not not_13 (not_13_out, transistor_312_out);
  Transistor #(.\type ("n")) transistor_312 (.in(1'b0), .out(transistor_312_out), .gate(H8));
  Transistor #(.\type ("n")) transistor_313 (.in(1'b0), .out(transistor_312_out), .gate(H7));
  Transistor #(.\type ("n")) transistor_314 (.in(1'b0), .out(transistor_312_out), .gate(H6));
  Transistor #(.\type ("n")) transistor_315 (.in(1'b0), .out(transistor_312_out), .gate(H5));
  Transistor #(.\type ("n")) transistor_316 (.in(1'b0), .out(transistor_312_out), .gate(H4));
  Transistor #(.\type ("n")) transistor_317 (.in(1'b0), .out(transistor_312_out), .gate(H3));
  Transistor #(.\type ("n")) transistor_318 (.in(1'b0), .out(transistor_312_out), .gate(H2));
  Transistor #(.\type ("n")) transistor_319 (.in(1'b0), .out(transistor_312_out), .gate(H1));
  Transistor #(.\type ("n")) transistor_320 (.in(1'b0), .out(transistor_312_out), .gate(H0));
  Pull_Resistor #(.pull(1)) pull_resistor_32 (.node(transistor_312_out));
  nor nor_2 (HPLA_15, transistor_321_out, transistor_331_out);
  Transistor #(.\type ("n")) transistor_321 (.in(1'b0), .out(transistor_321_out), .gate(H40));
  Transistor #(.\type ("n")) transistor_322 (.in(1'b0), .out(transistor_321_out), .gate(not_3_out));
  Transistor #(.\type ("n")) transistor_323 (.in(1'b0), .out(transistor_321_out), .gate(H7));
  Transistor #(.\type ("n")) transistor_324 (.in(1'b0), .out(transistor_321_out), .gate(H6));
  Transistor #(.\type ("n")) transistor_325 (.in(1'b0), .out(transistor_321_out), .gate(H5));
  Transistor #(.\type ("n")) transistor_326 (.in(1'b0), .out(transistor_321_out), .gate(H4));
  Transistor #(.\type ("n")) transistor_327 (.in(1'b0), .out(transistor_321_out), .gate(H3));
  Transistor #(.\type ("n")) transistor_328 (.in(1'b0), .out(transistor_321_out), .gate(H2));
  Transistor #(.\type ("n")) transistor_329 (.in(1'b0), .out(transistor_321_out), .gate(not_10_out));
  Transistor #(.\type ("n")) transistor_330 (.in(1'b0), .out(transistor_321_out), .gate(H0));
  Pull_Resistor #(.pull(1)) pull_resistor_33 (.node(transistor_321_out));
  not not_14 (HPLA_16, not_15_out);
  not not_15 (not_15_out, transistor_339_out);
  Transistor #(.\type ("n")) transistor_331 (.in(1'b0), .out(transistor_331_out), .gate(not_2_out));
  Transistor #(.\type ("n")) transistor_332 (.in(1'b0), .out(transistor_331_out), .gate(not_3_out));
  Transistor #(.\type ("n")) transistor_333 (.in(1'b0), .out(transistor_331_out), .gate(H7));
  Transistor #(.\type ("n")) transistor_334 (.in(1'b0), .out(transistor_331_out), .gate(not_5_out));
  Transistor #(.\type ("n")) transistor_335 (.in(1'b0), .out(transistor_331_out), .gate(H5));
  Transistor #(.\type ("n")) transistor_336 (.in(1'b0), .out(transistor_331_out), .gate(H4));
  Transistor #(.\type ("n")) transistor_337 (.in(1'b0), .out(transistor_331_out), .gate(H3));
  Transistor #(.\type ("n")) transistor_338 (.in(1'b0), .out(transistor_331_out), .gate(H2));
  Transistor #(.\type ("n")) transistor_339 (.in(1'b0), .out(transistor_339_out), .gate(H2));
  Transistor #(.\type ("n")) transistor_340 (.in(1'b0), .out(transistor_339_out), .gate(H1));
  Transistor #(.\type ("n")) transistor_341 (.in(1'b0), .out(transistor_331_out), .gate(not_10_out));
  Transistor #(.\type ("n")) transistor_342 (.in(1'b0), .out(transistor_339_out), .gate(H0));
  Transistor #(.\type ("n")) transistor_343 (.in(1'b0), .out(transistor_331_out), .gate(H0));
  Pull_Resistor #(.pull(1)) pull_resistor_34 (.node(transistor_331_out));
  Pull_Resistor #(.pull(1)) pull_resistor_35 (.node(transistor_339_out));
  Transistor #(.\type ("n")) transistor_344 (.in(1'b0), .out(transistor_344_out), .gate(H3));
  Transistor #(.\type ("n")) transistor_345 (.in(1'b0), .out(transistor_344_out), .gate(not_9_out));
  Transistor #(.\type ("n")) transistor_346 (.in(1'b0), .out(transistor_344_out), .gate(not_10_out));
  Transistor #(.\type ("n")) transistor_347 (.in(1'b0), .out(transistor_344_out), .gate(not_11_out));
  Pull_Resistor #(.pull(1)) pull_resistor_36 (.node(transistor_344_out));
  or or_14 (HPLA_17, transistor_344_out, transistor_348_out);
  Transistor #(.\type ("n")) transistor_348 (.in(1'b0), .out(transistor_348_out), .gate(M5));
  Transistor #(.\type ("n")) transistor_349 (.in(1'b0), .out(transistor_348_out), .gate(not_8_out));
  Transistor #(.\type ("n")) transistor_350 (.in(1'b0), .out(transistor_348_out), .gate(not_9_out));
  Transistor #(.\type ("n")) transistor_351 (.in(1'b0), .out(transistor_348_out), .gate(not_10_out));
  Transistor #(.\type ("n")) transistor_352 (.in(1'b0), .out(transistor_348_out), .gate(not_11_out));
  Pull_Resistor #(.pull(1)) pull_resistor_37 (.node(transistor_348_out));
  not not_16 (HPLA_18, not_17_out);
  not not_17 (not_17_out, transistor_353_out);
  Transistor #(.\type ("n")) transistor_353 (.in(1'b0), .out(transistor_353_out), .gate(not_8_out));
  Transistor #(.\type ("n")) transistor_354 (.in(1'b0), .out(transistor_353_out), .gate(not_9_out));
  Transistor #(.\type ("n")) transistor_355 (.in(1'b0), .out(transistor_353_out), .gate(not_10_out));
  Transistor #(.\type ("n")) transistor_356 (.in(1'b0), .out(transistor_353_out), .gate(not_11_out));
  Pull_Resistor #(.pull(1)) pull_resistor_38 (.node(transistor_353_out));
  Transistor #(.\type ("n")) transistor_357 (.in(1'b0), .out(transistor_357_out), .gate(M5));
  Transistor #(.\type ("n")) transistor_358 (.in(1'b0), .out(transistor_357_out), .gate(not_3_out));
  Transistor #(.\type ("n")) transistor_359 (.in(1'b0), .out(transistor_357_out), .gate(H7));
  Transistor #(.\type ("n")) transistor_360 (.in(1'b0), .out(transistor_357_out), .gate(H6));
  Transistor #(.\type ("n")) transistor_361 (.in(1'b0), .out(transistor_357_out), .gate(H5));
  Transistor #(.\type ("n")) transistor_362 (.in(1'b0), .out(transistor_357_out), .gate(H4));
  Transistor #(.\type ("n")) transistor_363 (.in(1'b0), .out(transistor_357_out), .gate(not_8_out));
  Transistor #(.\type ("n")) transistor_364 (.in(1'b0), .out(transistor_357_out), .gate(H2));
  Transistor #(.\type ("n")) transistor_365 (.in(1'b0), .out(transistor_357_out), .gate(not_10_out));
  Transistor #(.\type ("n")) transistor_366 (.in(1'b0), .out(transistor_357_out), .gate(not_11_out));
  Pull_Resistor #(.pull(1)) pull_resistor_39 (.node(transistor_357_out));
  or or_15 (HPLA_19, transistor_357_out, transistor_367_out, transistor_377_out, transistor_387_out);
  Transistor #(.\type ("n")) transistor_367 (.in(1'b0), .out(transistor_367_out), .gate(M5));
  Transistor #(.\type ("n")) transistor_368 (.in(1'b0), .out(transistor_367_out), .gate(not_3_out));
  Transistor #(.\type ("n")) transistor_369 (.in(1'b0), .out(transistor_367_out), .gate(H7));
  Transistor #(.\type ("n")) transistor_370 (.in(1'b0), .out(transistor_367_out), .gate(H6));
  Transistor #(.\type ("n")) transistor_371 (.in(1'b0), .out(transistor_367_out), .gate(H5));
  Transistor #(.\type ("n")) transistor_372 (.in(1'b0), .out(transistor_367_out), .gate(not_7_out));
  Transistor #(.\type ("n")) transistor_373 (.in(1'b0), .out(transistor_367_out), .gate(H3));
  Transistor #(.\type ("n")) transistor_374 (.in(1'b0), .out(transistor_367_out), .gate(not_9_out));
  Transistor #(.\type ("n")) transistor_375 (.in(1'b0), .out(transistor_367_out), .gate(not_10_out));
  Transistor #(.\type ("n")) transistor_376 (.in(1'b0), .out(transistor_367_out), .gate(not_11_out));
  Pull_Resistor #(.pull(1)) pull_resistor_40 (.node(transistor_367_out));
  Transistor #(.\type ("n")) transistor_377 (.in(1'b0), .out(transistor_377_out), .gate(M5));
  Transistor #(.\type ("n")) transistor_378 (.in(1'b0), .out(transistor_377_out), .gate(not_3_out));
  Transistor #(.\type ("n")) transistor_379 (.in(1'b0), .out(transistor_377_out), .gate(not_4_out));
  Transistor #(.\type ("n")) transistor_380 (.in(1'b0), .out(transistor_377_out), .gate(not_5_out));
  Transistor #(.\type ("n")) transistor_381 (.in(1'b0), .out(transistor_377_out), .gate(H5));
  Transistor #(.\type ("n")) transistor_382 (.in(1'b0), .out(transistor_377_out), .gate(not_7_out));
  Transistor #(.\type ("n")) transistor_383 (.in(1'b0), .out(transistor_377_out), .gate(H3));
  Transistor #(.\type ("n")) transistor_384 (.in(1'b0), .out(transistor_377_out), .gate(not_9_out));
  Transistor #(.\type ("n")) transistor_385 (.in(1'b0), .out(transistor_377_out), .gate(not_10_out));
  Transistor #(.\type ("n")) transistor_386 (.in(1'b0), .out(transistor_377_out), .gate(not_11_out));
  Pull_Resistor #(.pull(1)) pull_resistor_41 (.node(transistor_377_out));
  Transistor #(.\type ("n")) transistor_387 (.in(1'b0), .out(transistor_387_out), .gate(M5));
  Transistor #(.\type ("n")) transistor_388 (.in(1'b0), .out(transistor_388_out), .gate(not_1_out));
  Transistor #(.\type ("n")) transistor_389 (.in(1'b0), .out(transistor_388_out), .gate(H8));
  Transistor #(.\type ("n")) transistor_390 (.in(1'b0), .out(transistor_387_out), .gate(not_3_out));
  Transistor #(.\type ("n")) transistor_391 (.in(1'b0), .out(transistor_387_out), .gate(not_4_out));
  Transistor #(.\type ("n")) transistor_392 (.in(1'b0), .out(transistor_387_out), .gate(not_5_out));
  Transistor #(.\type ("n")) transistor_393 (.in(1'b0), .out(transistor_387_out), .gate(not_6_out));
  Transistor #(.\type ("n")) transistor_394 (.in(1'b0), .out(transistor_387_out), .gate(H4));
  Transistor #(.\type ("n")) transistor_395 (.in(1'b0), .out(transistor_387_out), .gate(H3));
  Transistor #(.\type ("n")) transistor_396 (.in(1'b0), .out(transistor_388_out), .gate(not_8_out));
  Transistor #(.\type ("n")) transistor_397 (.in(1'b0), .out(transistor_387_out), .gate(H2));
  Transistor #(.\type ("n")) transistor_398 (.in(1'b0), .out(transistor_388_out), .gate(not_9_out));
  Transistor #(.\type ("n")) transistor_399 (.in(1'b0), .out(transistor_388_out), .gate(H1));
  Transistor #(.\type ("n")) transistor_400 (.in(1'b0), .out(transistor_387_out), .gate(not_10_out));
  Transistor #(.\type ("n")) transistor_401 (.in(1'b0), .out(transistor_387_out), .gate(not_11_out));
  Transistor #(.\type ("n")) transistor_402 (.in(1'b0), .out(transistor_388_out), .gate(not_11_out));
  Pull_Resistor #(.pull(1)) pull_resistor_42 (.node(transistor_387_out));
  Pull_Resistor #(.pull(1)) pull_resistor_43 (.node(transistor_388_out));
  or or_16 (HPLA_20, transistor_388_out, transistor_403_out);
  Transistor #(.\type ("n")) transistor_403 (.in(1'b0), .out(transistor_403_out), .gate(not_1_out));
  Transistor #(.\type ("n")) transistor_404 (.in(1'b0), .out(transistor_403_out), .gate(not_2_out));
  Transistor #(.\type ("n")) transistor_405 (.in(1'b0), .out(transistor_403_out), .gate(not_3_out));
  Transistor #(.\type ("n")) transistor_406 (.in(1'b0), .out(transistor_403_out), .gate(H7));
  Transistor #(.\type ("n")) transistor_407 (.in(1'b0), .out(transistor_403_out), .gate(H6));
  Transistor #(.\type ("n")) transistor_408 (.in(1'b0), .out(transistor_403_out), .gate(not_8_out));
  Transistor #(.\type ("n")) transistor_409 (.in(1'b0), .out(transistor_403_out), .gate(not_9_out));
  Transistor #(.\type ("n")) transistor_410 (.in(1'b0), .out(transistor_403_out), .gate(H1));
  Transistor #(.\type ("n")) transistor_411 (.in(1'b0), .out(transistor_403_out), .gate(not_11_out));
  Pull_Resistor #(.pull(1)) pull_resistor_44 (.node(transistor_403_out));
  not not_18 (HPLA_21, not_19_out);
  not not_19 (not_19_out, transistor_412_out);
  Transistor #(.\type ("n")) transistor_412 (.in(1'b0), .out(transistor_412_out), .gate(not_3_out));
  Transistor #(.\type ("n")) transistor_413 (.in(1'b0), .out(transistor_412_out), .gate(not_4_out));
  Transistor #(.\type ("n")) transistor_414 (.in(1'b0), .out(transistor_412_out), .gate(not_5_out));
  Transistor #(.\type ("n")) transistor_415 (.in(1'b0), .out(transistor_412_out), .gate(not_6_out));
  Transistor #(.\type ("n")) transistor_416 (.in(1'b0), .out(transistor_412_out), .gate(not_7_out));
  Transistor #(.\type ("n")) transistor_417 (.in(1'b0), .out(transistor_412_out), .gate(not_8_out));
  Transistor #(.\type ("n")) transistor_418 (.in(1'b0), .out(transistor_412_out), .gate(H2));
  Transistor #(.\type ("n")) transistor_419 (.in(1'b0), .out(transistor_412_out), .gate(not_10_out));
  Transistor #(.\type ("n")) transistor_420 (.in(1'b0), .out(transistor_412_out), .gate(not_11_out));
  Pull_Resistor #(.pull(1)) pull_resistor_45 (.node(transistor_412_out));
  not not_20 (HPLA_22, not_21_out);
  not not_21 (not_21_out, transistor_421_out);
  Transistor #(.\type ("n")) transistor_421 (.in(1'b0), .out(transistor_421_out), .gate(H3));
  Transistor #(.\type ("n")) transistor_422 (.in(1'b0), .out(transistor_421_out), .gate(H2));
  Transistor #(.\type ("n")) transistor_423 (.in(1'b0), .out(transistor_421_out), .gate(not_10_out));
  Transistor #(.\type ("n")) transistor_424 (.in(1'b0), .out(transistor_421_out), .gate(not_11_out));
  Pull_Resistor #(.pull(1)) pull_resistor_46 (.node(transistor_421_out));
  not not_22 (not_22_out, C);
  Pull_Resistor #(.pull(1)) pull_resistor_47 (.node(pull_resistor_47_node));
  Pull_Resistor #(.pull(1)) pull_resistor_48 (.node(pull_resistor_48_node));
  Pull_Resistor #(.pull(1)) pull_resistor_49 (.node(pull_resistor_49_node));
  Pull_Resistor #(.pull(1)) pull_resistor_50 (.node(pull_resistor_50_node));
  Pull_Resistor #(.pull(1)) pull_resistor_51 (.node(pull_resistor_51_node));
  Pull_Resistor #(.pull(1)) pull_resistor_52 (.node(pull_resistor_52_node));
  Pull_Resistor #(.pull(1)) pull_resistor_53 (.node(pull_resistor_53_node));
  Pull_Resistor #(.pull(1)) pull_resistor_54 (.node(pull_resistor_54_node));
  Pull_Resistor #(.pull(1)) pull_resistor_55 (.node(pull_resistor_55_node));
  Pull_Resistor #(.pull(1)) pull_resistor_56 (.node(pull_resistor_56_node));
  Pull_Resistor #(.pull(1)) pull_resistor_57 (.node(pull_resistor_57_node));
  Pull_Resistor #(.pull(1)) pull_resistor_58 (.node(pull_resistor_58_node));
  not not_23 (not_23_out, C);
  not not_24 (not_24_out, not_22_out);
  Transistor #(.\type ("n"), .gate("br")) transistor_425 (.in(1'b0), .out(pull_resistor_50_node), .gate(_3));
  Transistor #(.\type ("n"), .gate("br")) transistor_426 (
    .in(1'b0), .out(pull_resistor_58_node), .gate(transistor_427_out));
  Transistor #(.\type ("n")) transistor_427 (.in(1'b0), .out(transistor_427_out), .gate(not_23_out));
  Transistor #(.\type ("n")) transistor_428 (.in(1'b0), .out(transistor_428_out), .gate(not_23_out));
  Transistor #(.\type ("n")) transistor_429 (.in(1'b0), .out(transistor_428_out), .gate(not_1_out));
  Transistor #(.\type ("n")) transistor_430 (.in(1'b0), .out(transistor_427_out), .gate(not_1_out));
  Transistor #(.\type ("n")) transistor_431 (.in(1'b0), .out(transistor_428_out), .gate(not_2_out));
  Transistor #(.\type ("n")) transistor_432 (.in(1'b0), .out(transistor_427_out), .gate(H8));
  Transistor #(.\type ("n")) transistor_433 (.in(1'b0), .out(transistor_428_out), .gate(not_3_out));
  Transistor #(.\type ("n")) transistor_434 (.in(1'b0), .out(transistor_428_out), .gate(H7));
  Transistor #(.\type ("n")) transistor_435 (.in(1'b0), .out(transistor_428_out), .gate(H6));
  Transistor #(.\type ("n")) transistor_436 (.in(1'b0), .out(transistor_428_out), .gate(not_6_out));
  Transistor #(.\type ("n")) transistor_437 (.in(1'b0), .out(transistor_427_out), .gate(not_6_out));
  Transistor #(.\type ("n")) transistor_438 (.in(1'b0), .out(transistor_427_out), .gate(not_7_out));
  Transistor #(.\type ("n")) transistor_439 (.in(1'b0), .out(transistor_428_out), .gate(not_7_out));
  Transistor #(.\type ("n")) transistor_440 (.in(1'b0), .out(transistor_428_out), .gate(H3));
  Transistor #(.\type ("n")) transistor_441 (.in(1'b0), .out(transistor_427_out), .gate(H3));
  Transistor #(.\type ("n")) transistor_442 (.in(1'b0), .out(transistor_427_out), .gate(H2));
  Transistor #(.\type ("n")) transistor_443 (.in(1'b0), .out(transistor_428_out), .gate(H2));
  Transistor #(.\type ("n")) transistor_444 (.in(1'b0), .out(transistor_427_out), .gate(not_10_out));
  Transistor #(.\type ("n")) transistor_445 (.in(1'b0), .out(transistor_428_out), .gate(not_10_out));
  Transistor #(.\type ("n")) transistor_446 (.in(1'b0), .out(transistor_428_out), .gate(H0));
  Transistor #(.\type ("n")) transistor_447 (.in(1'b0), .out(transistor_427_out), .gate(H0));
  Pull_Resistor #(.pull(1)) pull_resistor_59 (.node(transistor_427_out));
  Pull_Resistor #(.pull(1)) pull_resistor_60 (.node(transistor_428_out));
  Transistor #(.\type ("n"), .gate("br")) transistor_448 (
    .in(1'b0), .out(pull_resistor_58_node), .gate(transistor_428_out));
  Transistor #(.\type ("n")) transistor_449 (.in(1'b0), .out(transistor_449_out), .gate(not_24_out));
  Transistor #(.\type ("n")) transistor_450 (.in(1'b0), .out(transistor_449_out), .gate(not_6_out));
  Transistor #(.\type ("n")) transistor_451 (.in(1'b0), .out(transistor_449_out), .gate(not_7_out));
  Transistor #(.\type ("n")) transistor_452 (.in(1'b0), .out(transistor_449_out), .gate(H3));
  Transistor #(.\type ("n")) transistor_453 (.in(1'b0), .out(transistor_449_out), .gate(H2));
  Transistor #(.\type ("n")) transistor_454 (.in(1'b0), .out(transistor_449_out), .gate(not_10_out));
  Transistor #(.\type ("n")) transistor_455 (.in(1'b0), .out(transistor_449_out), .gate(H0));
  Pull_Resistor #(.pull(1)) pull_resistor_61 (.node(transistor_449_out));
  not not_25 (HPLA_23, pull_resistor_58_node);
  Transistor #(.\type ("n"), .gate("br")) transistor_456 (
    .in(1'b0), .out(pull_resistor_57_node), .gate(transistor_458_out));
  Transistor #(.\type ("n"), .gate("br")) transistor_457 (
    .in(1'b0), .out(pull_resistor_58_node), .gate(transistor_449_out));
  Transistor #(.\type ("n")) transistor_458 (.in(1'b0), .out(transistor_458_out), .gate(not_23_out));
  Transistor #(.\type ("n")) transistor_459 (.in(1'b0), .out(transistor_458_out), .gate(H8));
  Transistor #(.\type ("n")) transistor_460 (.in(1'b0), .out(transistor_458_out), .gate(H3));
  Transistor #(.\type ("n")) transistor_461 (.in(1'b0), .out(transistor_458_out), .gate(H2));
  Transistor #(.\type ("n")) transistor_462 (.in(1'b0), .out(transistor_458_out), .gate(H1));
  Transistor #(.\type ("n")) transistor_463 (.in(1'b0), .out(transistor_458_out), .gate(H0));
  Pull_Resistor #(.pull(1)) pull_resistor_62 (.node(transistor_458_out));
  Transistor #(.\type ("n"), .gate("br")) transistor_464 (
    .in(1'b0), .out(pull_resistor_57_node), .gate(transistor_465_out));
  Transistor #(.\type ("n")) transistor_465 (.in(1'b0), .out(transistor_465_out), .gate(not_23_out));
  Transistor #(.\type ("n")) transistor_466 (.in(1'b0), .out(transistor_465_out), .gate(not_1_out));
  Transistor #(.\type ("n")) transistor_467 (.in(1'b0), .out(transistor_465_out), .gate(not_2_out));
  Transistor #(.\type ("n")) transistor_468 (.in(1'b0), .out(transistor_465_out), .gate(not_3_out));
  Transistor #(.\type ("n")) transistor_469 (.in(1'b0), .out(transistor_465_out), .gate(H7));
  Transistor #(.\type ("n")) transistor_470 (.in(1'b0), .out(transistor_465_out), .gate(H6));
  Transistor #(.\type ("n")) transistor_471 (.in(1'b0), .out(transistor_465_out), .gate(H3));
  Transistor #(.\type ("n")) transistor_472 (.in(1'b0), .out(transistor_465_out), .gate(H2));
  Transistor #(.\type ("n")) transistor_473 (.in(1'b0), .out(transistor_465_out), .gate(H1));
  Transistor #(.\type ("n")) transistor_474 (.in(1'b0), .out(transistor_465_out), .gate(H0));
  Pull_Resistor #(.pull(1)) pull_resistor_63 (.node(transistor_465_out));
  not not_26 (HPLA_24, pull_resistor_57_node);
  Transistor #(.\type ("n"), .gate("br")) transistor_475 (
    .in(1'b0), .out(pull_resistor_57_node), .gate(transistor_476_out));
  Transistor #(.\type ("n")) transistor_476 (.in(1'b0), .out(transistor_476_out), .gate(not_23_out));
  Transistor #(.\type ("n")) transistor_477 (.in(1'b0), .out(transistor_476_out), .gate(M5));
  Transistor #(.\type ("n")) transistor_478 (.in(1'b0), .out(transistor_476_out), .gate(H8));
  Transistor #(.\type ("n")) transistor_479 (.in(1'b0), .out(transistor_476_out), .gate(not_8_out));
  Transistor #(.\type ("n")) transistor_480 (.in(1'b0), .out(transistor_476_out), .gate(H2));
  Transistor #(.\type ("n")) transistor_481 (.in(1'b0), .out(transistor_476_out), .gate(H1));
  Transistor #(.\type ("n")) transistor_482 (.in(1'b0), .out(transistor_476_out), .gate(H0));
  Pull_Resistor #(.pull(1)) pull_resistor_64 (.node(transistor_476_out));
  Transistor #(.\type ("n"), .gate("br")) transistor_483 (
    .in(1'b0), .out(pull_resistor_56_node), .gate(transistor_484_out));
  Transistor #(.\type ("n")) transistor_484 (.in(1'b0), .out(transistor_484_out), .gate(not_23_out));
  Transistor #(.\type ("n")) transistor_485 (.in(1'b0), .out(transistor_484_out), .gate(H8));
  Transistor #(.\type ("n")) transistor_486 (.in(1'b0), .out(transistor_484_out), .gate(not_8_out));
  Transistor #(.\type ("n")) transistor_487 (.in(1'b0), .out(transistor_484_out), .gate(H2));
  Transistor #(.\type ("n")) transistor_488 (.in(1'b0), .out(transistor_484_out), .gate(H1));
  Transistor #(.\type ("n")) transistor_489 (.in(1'b0), .out(transistor_484_out), .gate(H0));
  Pull_Resistor #(.pull(1)) pull_resistor_65 (.node(transistor_484_out));
  not not_27 (HPLA_25, pull_resistor_56_node);
  Transistor #(.\type ("n"), .gate("br")) transistor_490 (
    .in(1'b0), .out(pull_resistor_56_node), .gate(transistor_491_out));
  Transistor #(.\type ("n")) transistor_491 (.in(1'b0), .out(transistor_491_out), .gate(not_23_out));
  Transistor #(.\type ("n")) transistor_492 (.in(1'b0), .out(transistor_491_out), .gate(not_1_out));
  Transistor #(.\type ("n")) transistor_493 (.in(1'b0), .out(transistor_491_out), .gate(not_2_out));
  Transistor #(.\type ("n")) transistor_494 (.in(1'b0), .out(transistor_491_out), .gate(not_3_out));
  Transistor #(.\type ("n")) transistor_495 (.in(1'b0), .out(transistor_491_out), .gate(H7));
  Transistor #(.\type ("n")) transistor_496 (.in(1'b0), .out(transistor_491_out), .gate(H6));
  Transistor #(.\type ("n")) transistor_497 (.in(1'b0), .out(transistor_491_out), .gate(not_8_out));
  Transistor #(.\type ("n")) transistor_498 (.in(1'b0), .out(transistor_491_out), .gate(H2));
  Transistor #(.\type ("n")) transistor_499 (.in(1'b0), .out(transistor_491_out), .gate(H1));
  Transistor #(.\type ("n")) transistor_500 (.in(1'b0), .out(transistor_491_out), .gate(H0));
  Pull_Resistor #(.pull(1)) pull_resistor_66 (.node(transistor_491_out));
  Transistor #(.\type ("n"), .gate("br")) transistor_501 (
    .in(1'b0), .out(pull_resistor_55_node), .gate(transistor_502_out));
  Transistor #(.\type ("n")) transistor_502 (.in(1'b0), .out(transistor_502_out), .gate(not_23_out));
  Transistor #(.\type ("n")) transistor_503 (.in(1'b0), .out(transistor_503_out), .gate(not_23_out));
  Transistor #(.\type ("n")) transistor_504 (.in(1'b0), .out(transistor_503_out), .gate(not_1_out));
  Transistor #(.\type ("n")) transistor_505 (.in(1'b0), .out(transistor_503_out), .gate(not_2_out));
  Transistor #(.\type ("n")) transistor_506 (.in(1'b0), .out(transistor_502_out), .gate(H8));
  Transistor #(.\type ("n")) transistor_507 (.in(1'b0), .out(transistor_503_out), .gate(not_3_out));
  Transistor #(.\type ("n")) transistor_508 (.in(1'b0), .out(transistor_503_out), .gate(H7));
  Transistor #(.\type ("n")) transistor_509 (.in(1'b0), .out(transistor_503_out), .gate(H6));
  Transistor #(.\type ("n")) transistor_510 (.in(1'b0), .out(transistor_503_out), .gate(not_9_out));
  Transistor #(.\type ("n")) transistor_511 (.in(1'b0), .out(transistor_502_out), .gate(not_9_out));
  Transistor #(.\type ("n")) transistor_512 (.in(1'b0), .out(transistor_502_out), .gate(H1));
  Transistor #(.\type ("n")) transistor_513 (.in(1'b0), .out(transistor_503_out), .gate(H1));
  Transistor #(.\type ("n")) transistor_514 (.in(1'b0), .out(transistor_503_out), .gate(H0));
  Transistor #(.\type ("n")) transistor_515 (.in(1'b0), .out(transistor_502_out), .gate(H0));
  Pull_Resistor #(.pull(1)) pull_resistor_67 (.node(transistor_503_out));
  Pull_Resistor #(.pull(1)) pull_resistor_68 (.node(transistor_502_out));
  not not_28 (HPLA_26, pull_resistor_55_node);
  Transistor #(.\type ("n"), .gate("br")) transistor_516 (
    .in(1'b0), .out(pull_resistor_55_node), .gate(transistor_503_out));
  Transistor #(.\type ("n")) transistor_517 (.in(1'b0), .out(transistor_517_out), .gate(not_23_out));
  Transistor #(.\type ("n")) transistor_518 (.in(1'b0), .out(transistor_517_out), .gate(H8));
  Transistor #(.\type ("n")) transistor_519 (.in(1'b0), .out(transistor_517_out), .gate(not_9_out));
  Transistor #(.\type ("n")) transistor_520 (.in(1'b0), .out(transistor_517_out), .gate(not_10_out));
  Transistor #(.\type ("n")) transistor_521 (.in(1'b0), .out(transistor_517_out), .gate(H0));
  Pull_Resistor #(.pull(1)) pull_resistor_69 (.node(transistor_517_out));
  not not_29 (HPLA_28, pull_resistor_53_node);
  not not_30 (HPLA_27, pull_resistor_54_node);
  Transistor #(.\type ("n"), .gate("br")) transistor_522 (
    .in(1'b0), .out(pull_resistor_54_node), .gate(transistor_517_out));
  Transistor #(.\type ("n"), .gate("br")) transistor_523 (
    .in(1'b0), .out(pull_resistor_54_node), .gate(transistor_524_out));
  Transistor #(.\type ("n")) transistor_524 (.in(1'b0), .out(transistor_524_out), .gate(not_23_out));
  Transistor #(.\type ("n")) transistor_525 (.in(1'b0), .out(transistor_524_out), .gate(not_1_out));
  Transistor #(.\type ("n")) transistor_526 (.in(1'b0), .out(transistor_524_out), .gate(not_2_out));
  Transistor #(.\type ("n")) transistor_527 (.in(1'b0), .out(transistor_524_out), .gate(not_3_out));
  Transistor #(.\type ("n")) transistor_528 (.in(1'b0), .out(transistor_524_out), .gate(H7));
  Transistor #(.\type ("n")) transistor_529 (.in(1'b0), .out(transistor_524_out), .gate(H6));
  Transistor #(.\type ("n")) transistor_530 (.in(1'b0), .out(transistor_524_out), .gate(not_9_out));
  Transistor #(.\type ("n")) transistor_531 (.in(1'b0), .out(transistor_524_out), .gate(not_10_out));
  Transistor #(.\type ("n")) transistor_532 (.in(1'b0), .out(transistor_524_out), .gate(H0));
  Pull_Resistor #(.pull(1)) pull_resistor_70 (.node(transistor_524_out));
  Transistor #(.\type ("n"), .gate("br")) transistor_533 (
    .in(1'b0), .out(pull_resistor_49_node), .gate(transistor_535_out));
  Transistor #(.\type ("n"), .gate("br")) transistor_534 (
    .in(1'b0), .out(pull_resistor_57_node), .gate(transistor_535_out));
  Transistor #(.\type ("n")) transistor_535 (.in(1'b0), .out(transistor_535_out), .gate(not_23_out));
  Transistor #(.\type ("n")) transistor_536 (.in(1'b0), .out(transistor_535_out), .gate(not_1_out));
  Transistor #(.\type ("n")) transistor_537 (.in(1'b0), .out(transistor_535_out), .gate(not_3_out));
  Transistor #(.\type ("n")) transistor_538 (.in(1'b0), .out(transistor_535_out), .gate(not_4_out));
  Transistor #(.\type ("n")) transistor_539 (.in(1'b0), .out(transistor_535_out), .gate(not_5_out));
  Transistor #(.\type ("n")) transistor_540 (.in(1'b0), .out(transistor_535_out), .gate(not_6_out));
  Transistor #(.\type ("n")) transistor_541 (.in(1'b0), .out(transistor_535_out), .gate(not_7_out));
  Transistor #(.\type ("n")) transistor_542 (.in(1'b0), .out(transistor_535_out), .gate(H3));
  Transistor #(.\type ("n")) transistor_543 (.in(1'b0), .out(transistor_535_out), .gate(H2));
  Transistor #(.\type ("n")) transistor_544 (.in(1'b0), .out(transistor_535_out), .gate(H1));
  Transistor #(.\type ("n")) transistor_545 (.in(1'b0), .out(transistor_535_out), .gate(H0));
  Pull_Resistor #(.pull(1)) pull_resistor_71 (.node(transistor_535_out));
  Transistor #(.\type ("n"), .gate("br")) transistor_546 (
    .in(1'b0), .out(pull_resistor_49_node), .gate(transistor_548_out));
  Transistor #(.\type ("n"), .gate("br")) transistor_547 (
    .in(1'b0), .out(pull_resistor_56_node), .gate(transistor_548_out));
  Transistor #(.\type ("n")) transistor_548 (.in(1'b0), .out(transistor_548_out), .gate(not_23_out));
  Transistor #(.\type ("n")) transistor_549 (.in(1'b0), .out(transistor_548_out), .gate(not_1_out));
  Transistor #(.\type ("n")) transistor_550 (.in(1'b0), .out(transistor_548_out), .gate(not_3_out));
  Transistor #(.\type ("n")) transistor_551 (.in(1'b0), .out(transistor_548_out), .gate(not_4_out));
  Transistor #(.\type ("n")) transistor_552 (.in(1'b0), .out(transistor_548_out), .gate(not_5_out));
  Transistor #(.\type ("n")) transistor_553 (.in(1'b0), .out(transistor_548_out), .gate(not_6_out));
  Transistor #(.\type ("n")) transistor_554 (.in(1'b0), .out(transistor_548_out), .gate(not_7_out));
  Transistor #(.\type ("n")) transistor_555 (.in(1'b0), .out(transistor_548_out), .gate(not_8_out));
  Transistor #(.\type ("n")) transistor_556 (.in(1'b0), .out(transistor_548_out), .gate(H2));
  Transistor #(.\type ("n")) transistor_557 (.in(1'b0), .out(transistor_548_out), .gate(H1));
  Transistor #(.\type ("n")) transistor_558 (.in(1'b0), .out(transistor_548_out), .gate(H0));
  Pull_Resistor #(.pull(1)) pull_resistor_72 (.node(transistor_548_out));
  Transistor #(.\type ("n"), .gate("br")) transistor_559 (
    .in(1'b0), .out(pull_resistor_49_node), .gate(transistor_561_out));
  Transistor #(.\type ("n"), .gate("br")) transistor_560 (
    .in(1'b0), .out(pull_resistor_55_node), .gate(transistor_561_out));
  Transistor #(.\type ("n")) transistor_561 (.in(1'b0), .out(transistor_561_out), .gate(not_23_out));
  Transistor #(.\type ("n")) transistor_562 (.in(1'b0), .out(transistor_561_out), .gate(not_1_out));
  Transistor #(.\type ("n")) transistor_563 (.in(1'b0), .out(transistor_561_out), .gate(not_3_out));
  Transistor #(.\type ("n")) transistor_564 (.in(1'b0), .out(transistor_561_out), .gate(not_4_out));
  Transistor #(.\type ("n")) transistor_565 (.in(1'b0), .out(transistor_561_out), .gate(not_5_out));
  Transistor #(.\type ("n")) transistor_566 (.in(1'b0), .out(transistor_561_out), .gate(not_6_out));
  Transistor #(.\type ("n")) transistor_567 (.in(1'b0), .out(transistor_561_out), .gate(not_7_out));
  Transistor #(.\type ("n")) transistor_568 (.in(1'b0), .out(transistor_561_out), .gate(H3));
  Transistor #(.\type ("n")) transistor_569 (.in(1'b0), .out(transistor_561_out), .gate(not_9_out));
  Transistor #(.\type ("n")) transistor_570 (.in(1'b0), .out(transistor_561_out), .gate(H1));
  Transistor #(.\type ("n")) transistor_571 (.in(1'b0), .out(transistor_561_out), .gate(H0));
  Pull_Resistor #(.pull(1)) pull_resistor_73 (.node(transistor_561_out));
  Transistor #(.\type ("n"), .gate("br")) transistor_572 (
    .in(1'b0), .out(pull_resistor_49_node), .gate(transistor_574_out));
  Transistor #(.\type ("n"), .gate("br")) transistor_573 (
    .in(1'b0), .out(pull_resistor_55_node), .gate(transistor_574_out));
  Transistor #(.\type ("n")) transistor_574 (.in(1'b0), .out(transistor_574_out), .gate(not_23_out));
  Transistor #(.\type ("n")) transistor_575 (.in(1'b0), .out(transistor_574_out), .gate(not_1_out));
  Transistor #(.\type ("n")) transistor_576 (.in(1'b0), .out(transistor_574_out), .gate(not_3_out));
  Transistor #(.\type ("n")) transistor_577 (.in(1'b0), .out(transistor_574_out), .gate(not_4_out));
  Transistor #(.\type ("n")) transistor_578 (.in(1'b0), .out(transistor_574_out), .gate(not_5_out));
  Transistor #(.\type ("n")) transistor_579 (.in(1'b0), .out(transistor_574_out), .gate(not_6_out));
  Transistor #(.\type ("n")) transistor_580 (.in(1'b0), .out(transistor_574_out), .gate(not_7_out));
  Transistor #(.\type ("n")) transistor_581 (.in(1'b0), .out(transistor_574_out), .gate(not_8_out));
  Transistor #(.\type ("n")) transistor_582 (.in(1'b0), .out(transistor_574_out), .gate(not_9_out));
  Transistor #(.\type ("n")) transistor_583 (.in(1'b0), .out(transistor_574_out), .gate(H1));
  Transistor #(.\type ("n")) transistor_584 (.in(1'b0), .out(transistor_574_out), .gate(H0));
  Pull_Resistor #(.pull(1)) pull_resistor_74 (.node(transistor_574_out));
  not not_31 (HPLA_29, pull_resistor_52_node);
  Transistor #(.\type ("n"), .gate("br")) transistor_585 (
    .in(1'b0), .out(pull_resistor_49_node), .gate(transistor_588_out));
  Transistor #(.\type ("n"), .gate("br")) transistor_586 (
    .in(1'b0), .out(pull_resistor_54_node), .gate(transistor_588_out));
  Transistor #(.\type ("n")) transistor_587 (.in(1'b0), .out(transistor_587_out), .gate(not_23_out));
  Transistor #(.\type ("n")) transistor_588 (.in(1'b0), .out(transistor_588_out), .gate(not_23_out));
  Transistor #(.\type ("n")) transistor_589 (.in(1'b0), .out(transistor_587_out), .gate(not_1_out));
  Transistor #(.\type ("n")) transistor_590 (.in(1'b0), .out(transistor_588_out), .gate(not_1_out));
  Transistor #(.\type ("n")) transistor_591 (.in(1'b0), .out(transistor_588_out), .gate(not_3_out));
  Transistor #(.\type ("n")) transistor_592 (.in(1'b0), .out(transistor_587_out), .gate(not_3_out));
  Transistor #(.\type ("n")) transistor_593 (.in(1'b0), .out(transistor_587_out), .gate(not_4_out));
  Transistor #(.\type ("n")) transistor_594 (.in(1'b0), .out(transistor_588_out), .gate(not_4_out));
  Transistor #(.\type ("n")) transistor_595 (.in(1'b0), .out(transistor_588_out), .gate(not_5_out));
  Transistor #(.\type ("n")) transistor_596 (.in(1'b0), .out(transistor_587_out), .gate(not_5_out));
  Transistor #(.\type ("n")) transistor_597 (.in(1'b0), .out(transistor_588_out), .gate(not_6_out));
  Transistor #(.\type ("n")) transistor_598 (.in(1'b0), .out(transistor_587_out), .gate(not_6_out));
  Transistor #(.\type ("n")) transistor_599 (.in(1'b0), .out(transistor_588_out), .gate(not_7_out));
  Transistor #(.\type ("n")) transistor_600 (.in(1'b0), .out(transistor_587_out), .gate(not_7_out));
  Transistor #(.\type ("n")) transistor_601 (.in(1'b0), .out(transistor_588_out), .gate(H3));
  Transistor #(.\type ("n")) transistor_602 (.in(1'b0), .out(transistor_587_out), .gate(not_8_out));
  Transistor #(.\type ("n")) transistor_603 (.in(1'b0), .out(transistor_587_out), .gate(not_9_out));
  Transistor #(.\type ("n")) transistor_604 (.in(1'b0), .out(transistor_588_out), .gate(not_9_out));
  Transistor #(.\type ("n")) transistor_605 (.in(1'b0), .out(transistor_587_out), .gate(not_10_out));
  Transistor #(.\type ("n")) transistor_606 (.in(1'b0), .out(transistor_588_out), .gate(not_10_out));
  Transistor #(.\type ("n")) transistor_607 (.in(1'b0), .out(transistor_588_out), .gate(H0));
  Transistor #(.\type ("n")) transistor_608 (.in(1'b0), .out(transistor_587_out), .gate(H0));
  Pull_Resistor #(.pull(1)) pull_resistor_75 (.node(transistor_587_out));
  Pull_Resistor #(.pull(1)) pull_resistor_76 (.node(transistor_588_out));
  not not_32 (HPLA_30, not_33_out);
  not not_33 (not_33_out, transistor_610_out);
  Transistor #(.\type ("n"), .gate("br")) transistor_609 (
    .in(1'b0), .out(pull_resistor_54_node), .gate(transistor_587_out));
  Transistor #(.\type ("n")) transistor_610 (.in(1'b0), .out(transistor_610_out), .gate(not_11_out));
  Pull_Resistor #(.pull(1)) pull_resistor_77 (.node(transistor_610_out));
  Transistor #(.\type ("n"), .gate("br")) transistor_611 (
    .in(1'b0), .out(pull_resistor_48_node), .gate(transistor_612_out));
  Transistor #(.\type ("n")) transistor_612 (.in(1'b0), .out(transistor_612_out), .gate(not_24_out));
  Transistor #(.\type ("n")) transistor_613 (.in(1'b0), .out(transistor_612_out), .gate(H8));
  Transistor #(.\type ("n")) transistor_614 (.in(1'b0), .out(transistor_612_out), .gate(H1));
  Transistor #(.\type ("n")) transistor_615 (.in(1'b0), .out(transistor_612_out), .gate(H0));
  Pull_Resistor #(.pull(1)) pull_resistor_78 (.node(transistor_612_out));
  Transistor #(.\type ("n"), .gate("br")) transistor_616 (
    .in(1'b0), .out(pull_resistor_49_node), .gate(transistor_618_out));
  Transistor #(.\type ("n"), .gate("br")) transistor_617 (
    .in(1'b0), .out(pull_resistor_50_node), .gate(transistor_618_out));
  Transistor #(.\type ("n")) transistor_618 (.in(1'b0), .out(transistor_618_out), .gate(not_23_out));
  Transistor #(.\type ("n")) transistor_619 (.in(1'b0), .out(transistor_618_out), .gate(M5));
  Transistor #(.\type ("n")) transistor_620 (.in(1'b0), .out(transistor_618_out), .gate(not_3_out));
  Transistor #(.\type ("n")) transistor_621 (.in(1'b0), .out(transistor_618_out), .gate(not_4_out));
  Transistor #(.\type ("n")) transistor_622 (.in(1'b0), .out(transistor_618_out), .gate(not_5_out));
  Transistor #(.\type ("n")) transistor_623 (.in(1'b0), .out(transistor_618_out), .gate(not_6_out));
  Transistor #(.\type ("n")) transistor_624 (.in(1'b0), .out(transistor_618_out), .gate(not_7_out));
  Transistor #(.\type ("n")) transistor_625 (.in(1'b0), .out(transistor_618_out), .gate(H0));
  Pull_Resistor #(.pull(1)) pull_resistor_79 (.node(transistor_618_out));
  Transistor #(.\type ("n"), .gate("br")) transistor_626 (
    .in(1'b0), .out(pull_resistor_49_node), .gate(transistor_628_out));
  Transistor #(.\type ("n"), .gate("br")) transistor_627 (
    .in(1'b0), .out(pull_resistor_50_node), .gate(transistor_628_out));
  Transistor #(.\type ("n")) transistor_628 (.in(1'b0), .out(transistor_628_out), .gate(not_23_out));
  Transistor #(.\type ("n")) transistor_629 (.in(1'b0), .out(transistor_628_out), .gate(M5));
  Transistor #(.\type ("n")) transistor_630 (.in(1'b0), .out(transistor_628_out), .gate(H8));
  Transistor #(.\type ("n")) transistor_631 (.in(1'b0), .out(transistor_628_out), .gate(H4));
  Transistor #(.\type ("n")) transistor_632 (.in(1'b0), .out(transistor_628_out), .gate(not_8_out));
  Transistor #(.\type ("n")) transistor_633 (.in(1'b0), .out(transistor_628_out), .gate(H2));
  Transistor #(.\type ("n")) transistor_634 (.in(1'b0), .out(transistor_628_out), .gate(not_10_out));
  Transistor #(.\type ("n")) transistor_635 (.in(1'b0), .out(transistor_628_out), .gate(H0));
  Pull_Resistor #(.pull(1)) pull_resistor_80 (.node(transistor_628_out));
  Transistor #(.\type ("n"), .gate("br")) transistor_636 (
    .in(1'b0), .out(pull_resistor_49_node), .gate(transistor_638_out));
  Transistor #(.\type ("n"), .gate("br")) transistor_637 (
    .in(1'b0), .out(pull_resistor_50_node), .gate(transistor_638_out));
  Transistor #(.\type ("n")) transistor_638 (.in(1'b0), .out(transistor_638_out), .gate(not_23_out));
  Transistor #(.\type ("n")) transistor_639 (.in(1'b0), .out(transistor_638_out), .gate(M5));
  Transistor #(.\type ("n")) transistor_640 (.in(1'b0), .out(transistor_638_out), .gate(H8));
  Transistor #(.\type ("n")) transistor_641 (.in(1'b0), .out(transistor_638_out), .gate(not_7_out));
  Transistor #(.\type ("n")) transistor_642 (.in(1'b0), .out(transistor_638_out), .gate(H2));
  Transistor #(.\type ("n")) transistor_643 (.in(1'b0), .out(transistor_638_out), .gate(not_10_out));
  Transistor #(.\type ("n")) transistor_644 (.in(1'b0), .out(transistor_638_out), .gate(H0));
  Pull_Resistor #(.pull(1)) pull_resistor_81 (.node(transistor_638_out));
  not not_34 (HPLA_31, pull_resistor_47_node);
  Transistor #(.\type ("n"), .gate("br")) transistor_645 (
    .in(1'b0), .out(pull_resistor_48_node), .gate(transistor_647_out));
  Transistor #(.\type ("n"), .gate("br")) transistor_646 (
    .in(1'b0), .out(pull_resistor_53_node), .gate(transistor_647_out));
  Transistor #(.\type ("n")) transistor_647 (.in(1'b0), .out(transistor_647_out), .gate(not_23_out));
  Transistor #(.\type ("n")) transistor_648 (.in(1'b0), .out(transistor_647_out), .gate(M5));
  Transistor #(.\type ("n")) transistor_649 (.in(1'b0), .out(transistor_647_out), .gate(not_3_out));
  Transistor #(.\type ("n")) transistor_650 (.in(1'b0), .out(transistor_647_out), .gate(H7));
  Transistor #(.\type ("n")) transistor_651 (.in(1'b0), .out(transistor_647_out), .gate(H6));
  Transistor #(.\type ("n")) transistor_652 (.in(1'b0), .out(transistor_647_out), .gate(H5));
  Transistor #(.\type ("n")) transistor_653 (.in(1'b0), .out(transistor_647_out), .gate(H4));
  Transistor #(.\type ("n")) transistor_654 (.in(1'b0), .out(transistor_647_out), .gate(not_8_out));
  Transistor #(.\type ("n")) transistor_655 (.in(1'b0), .out(transistor_647_out), .gate(H2));
  Transistor #(.\type ("n")) transistor_656 (.in(1'b0), .out(transistor_647_out), .gate(H0));
  Pull_Resistor #(.pull(1)) pull_resistor_82 (.node(transistor_647_out));
  Transistor #(.\type ("n"), .gate("br")) transistor_657 (
    .in(1'b0), .out(pull_resistor_48_node), .gate(transistor_659_out));
  Transistor #(.\type ("n"), .gate("br")) transistor_658 (
    .in(1'b0), .out(pull_resistor_53_node), .gate(transistor_659_out));
  Transistor #(.\type ("n")) transistor_659 (.in(1'b0), .out(transistor_659_out), .gate(not_23_out));
  Transistor #(.\type ("n")) transistor_660 (.in(1'b0), .out(transistor_660_out), .gate(not_23_out));
  Transistor #(.\type ("n")) transistor_661 (.in(1'b0), .out(transistor_659_out), .gate(M5));
  Transistor #(.\type ("n")) transistor_662 (.in(1'b0), .out(transistor_660_out), .gate(M5));
  Transistor #(.\type ("n")) transistor_663 (.in(1'b0), .out(transistor_660_out), .gate(not_3_out));
  Transistor #(.\type ("n")) transistor_664 (.in(1'b0), .out(transistor_659_out), .gate(not_3_out));
  Transistor #(.\type ("n")) transistor_665 (.in(1'b0), .out(transistor_659_out), .gate(H7));
  Transistor #(.\type ("n")) transistor_666 (.in(1'b0), .out(transistor_660_out), .gate(not_4_out));
  Transistor #(.\type ("n")) transistor_667 (.in(1'b0), .out(transistor_659_out), .gate(H6));
  Transistor #(.\type ("n")) transistor_668 (.in(1'b0), .out(transistor_660_out), .gate(not_5_out));
  Transistor #(.\type ("n")) transistor_669 (.in(1'b0), .out(transistor_659_out), .gate(H5));
  Transistor #(.\type ("n")) transistor_670 (.in(1'b0), .out(transistor_660_out), .gate(H5));
  Transistor #(.\type ("n")) transistor_671 (.in(1'b0), .out(transistor_660_out), .gate(not_7_out));
  Transistor #(.\type ("n")) transistor_672 (.in(1'b0), .out(transistor_659_out), .gate(not_7_out));
  Transistor #(.\type ("n")) transistor_673 (.in(1'b0), .out(transistor_659_out), .gate(H3));
  Transistor #(.\type ("n")) transistor_674 (.in(1'b0), .out(transistor_660_out), .gate(H3));
  Transistor #(.\type ("n")) transistor_675 (.in(1'b0), .out(transistor_659_out), .gate(not_9_out));
  Transistor #(.\type ("n")) transistor_676 (.in(1'b0), .out(transistor_660_out), .gate(not_9_out));
  Transistor #(.\type ("n")) transistor_677 (.in(1'b0), .out(transistor_660_out), .gate(H0));
  Transistor #(.\type ("n")) transistor_678 (.in(1'b0), .out(transistor_659_out), .gate(H0));
  Pull_Resistor #(.pull(1)) pull_resistor_83 (.node(transistor_659_out));
  Pull_Resistor #(.pull(1)) pull_resistor_84 (.node(transistor_660_out));
  Transistor #(.\type ("n"), .gate("br")) transistor_679 (
    .in(1'b0), .out(pull_resistor_48_node), .gate(transistor_660_out));
  Transistor #(.\type ("n"), .gate("br")) transistor_680 (
    .in(1'b0), .out(pull_resistor_53_node), .gate(transistor_660_out));
  Transistor #(.\type ("n")) transistor_681 (.in(1'b0), .out(transistor_681_out), .gate(not_23_out));
  Transistor #(.\type ("n")) transistor_682 (.in(1'b0), .out(transistor_681_out), .gate(M5));
  Transistor #(.\type ("n")) transistor_683 (.in(1'b0), .out(transistor_681_out), .gate(not_3_out));
  Transistor #(.\type ("n")) transistor_684 (.in(1'b0), .out(transistor_681_out), .gate(not_4_out));
  Transistor #(.\type ("n")) transistor_685 (.in(1'b0), .out(transistor_681_out), .gate(not_5_out));
  Transistor #(.\type ("n")) transistor_686 (.in(1'b0), .out(transistor_681_out), .gate(not_6_out));
  Transistor #(.\type ("n")) transistor_687 (.in(1'b0), .out(transistor_681_out), .gate(H4));
  Transistor #(.\type ("n")) transistor_688 (.in(1'b0), .out(transistor_681_out), .gate(H3));
  Transistor #(.\type ("n")) transistor_689 (.in(1'b0), .out(transistor_681_out), .gate(H2));
  Transistor #(.\type ("n")) transistor_690 (.in(1'b0), .out(transistor_681_out), .gate(H0));
  Pull_Resistor #(.pull(1)) pull_resistor_85 (.node(transistor_681_out));
  not not_35 (HPLA_32, pull_resistor_48_node);
  Transistor #(.\type ("n"), .gate("br")) transistor_691 (
    .in(1'b0), .out(pull_resistor_48_node), .gate(transistor_681_out));
  Transistor #(.\type ("n"), .gate("br")) transistor_692 (
    .in(1'b0), .out(pull_resistor_52_node), .gate(transistor_694_out));
  Transistor #(.\type ("n"), .gate("br")) transistor_693 (
    .in(1'b0), .out(pull_resistor_53_node), .gate(transistor_681_out));
  Transistor #(.\type ("n")) transistor_694 (.in(1'b0), .out(transistor_694_out), .gate(not_23_out));
  Transistor #(.\type ("n")) transistor_695 (.in(1'b0), .out(transistor_694_out), .gate(M5));
  Transistor #(.\type ("n")) transistor_696 (.in(1'b0), .out(transistor_694_out), .gate(not_3_out));
  Transistor #(.\type ("n")) transistor_697 (.in(1'b0), .out(transistor_694_out), .gate(H7));
  Transistor #(.\type ("n")) transistor_698 (.in(1'b0), .out(transistor_694_out), .gate(H6));
  Transistor #(.\type ("n")) transistor_699 (.in(1'b0), .out(transistor_694_out), .gate(H5));
  Transistor #(.\type ("n")) transistor_700 (.in(1'b0), .out(transistor_694_out), .gate(H4));
  Transistor #(.\type ("n")) transistor_701 (.in(1'b0), .out(transistor_694_out), .gate(not_8_out));
  Transistor #(.\type ("n")) transistor_702 (.in(1'b0), .out(transistor_694_out), .gate(not_9_out));
  Transistor #(.\type ("n")) transistor_703 (.in(1'b0), .out(transistor_694_out), .gate(H0));
  Pull_Resistor #(.pull(1)) pull_resistor_86 (.node(transistor_694_out));
  not not_36 (HPLA_33, pull_resistor_50_node);
  Transistor #(.\type ("n"), .gate("br")) transistor_704 (
    .in(1'b0), .out(pull_resistor_52_node), .gate(transistor_705_out));
  Transistor #(.\type ("n")) transistor_705 (.in(1'b0), .out(transistor_705_out), .gate(not_23_out));
  Transistor #(.\type ("n")) transistor_706 (.in(1'b0), .out(transistor_705_out), .gate(M5));
  Transistor #(.\type ("n")) transistor_707 (.in(1'b0), .out(transistor_705_out), .gate(not_3_out));
  Transistor #(.\type ("n")) transistor_708 (.in(1'b0), .out(transistor_705_out), .gate(H7));
  Transistor #(.\type ("n")) transistor_709 (.in(1'b0), .out(transistor_705_out), .gate(H6));
  Transistor #(.\type ("n")) transistor_710 (.in(1'b0), .out(transistor_705_out), .gate(H5));
  Transistor #(.\type ("n")) transistor_711 (.in(1'b0), .out(transistor_705_out), .gate(not_7_out));
  Transistor #(.\type ("n")) transistor_712 (.in(1'b0), .out(transistor_705_out), .gate(not_8_out));
  Transistor #(.\type ("n")) transistor_713 (.in(1'b0), .out(transistor_705_out), .gate(H2));
  Transistor #(.\type ("n")) transistor_714 (.in(1'b0), .out(transistor_705_out), .gate(H0));
  Pull_Resistor #(.pull(1)) pull_resistor_87 (.node(transistor_705_out));
  Transistor #(.\type ("n"), .gate("br")) transistor_715 (
    .in(1'b0), .out(pull_resistor_52_node), .gate(transistor_716_out));
  Transistor #(.\type ("n")) transistor_716 (.in(1'b0), .out(transistor_716_out), .gate(not_23_out));
  Transistor #(.\type ("n")) transistor_717 (.in(1'b0), .out(transistor_716_out), .gate(M5));
  Transistor #(.\type ("n")) transistor_718 (.in(1'b0), .out(transistor_716_out), .gate(not_3_out));
  Transistor #(.\type ("n")) transistor_719 (.in(1'b0), .out(transistor_716_out), .gate(not_4_out));
  Transistor #(.\type ("n")) transistor_720 (.in(1'b0), .out(transistor_716_out), .gate(not_5_out));
  Transistor #(.\type ("n")) transistor_721 (.in(1'b0), .out(transistor_716_out), .gate(H5));
  Transistor #(.\type ("n")) transistor_722 (.in(1'b0), .out(transistor_716_out), .gate(not_7_out));
  Transistor #(.\type ("n")) transistor_723 (.in(1'b0), .out(transistor_716_out), .gate(not_8_out));
  Transistor #(.\type ("n")) transistor_724 (.in(1'b0), .out(transistor_716_out), .gate(H2));
  Transistor #(.\type ("n")) transistor_725 (.in(1'b0), .out(transistor_716_out), .gate(H0));
  Pull_Resistor #(.pull(1)) pull_resistor_88 (.node(transistor_716_out));
  Transistor #(.\type ("n"), .gate("br")) transistor_726 (
    .in(1'b0), .out(pull_resistor_52_node), .gate(transistor_727_out));
  Transistor #(.\type ("n")) transistor_727 (.in(1'b0), .out(transistor_727_out), .gate(not_23_out));
  Transistor #(.\type ("n")) transistor_728 (.in(1'b0), .out(transistor_727_out), .gate(M5));
  Transistor #(.\type ("n")) transistor_729 (.in(1'b0), .out(transistor_727_out), .gate(not_3_out));
  Transistor #(.\type ("n")) transistor_730 (.in(1'b0), .out(transistor_727_out), .gate(not_4_out));
  Transistor #(.\type ("n")) transistor_731 (.in(1'b0), .out(transistor_727_out), .gate(not_5_out));
  Transistor #(.\type ("n")) transistor_732 (.in(1'b0), .out(transistor_727_out), .gate(not_6_out));
  Transistor #(.\type ("n")) transistor_733 (.in(1'b0), .out(transistor_727_out), .gate(H4));
  Transistor #(.\type ("n")) transistor_734 (.in(1'b0), .out(transistor_727_out), .gate(H3));
  Transistor #(.\type ("n")) transistor_735 (.in(1'b0), .out(transistor_727_out), .gate(not_9_out));
  Transistor #(.\type ("n")) transistor_736 (.in(1'b0), .out(transistor_727_out), .gate(H0));
  Pull_Resistor #(.pull(1)) pull_resistor_89 (.node(transistor_727_out));
  not not_37 (HPLA_34, pull_resistor_49_node);
  Transistor #(.\type ("n"), .gate("br")) transistor_737 (
    .in(1'b0), .out(pull_resistor_51_node), .gate(transistor_738_out));
  Transistor #(.\type ("n")) transistor_738 (.in(1'b0), .out(transistor_738_out), .gate(not_23_out));
  Transistor #(.\type ("n")) transistor_739 (.in(1'b0), .out(transistor_738_out), .gate(M5));
  Transistor #(.\type ("n")) transistor_740 (.in(1'b0), .out(transistor_738_out), .gate(not_3_out));
  Transistor #(.\type ("n")) transistor_741 (.in(1'b0), .out(transistor_738_out), .gate(H7));
  Transistor #(.\type ("n")) transistor_742 (.in(1'b0), .out(transistor_738_out), .gate(H6));
  Transistor #(.\type ("n")) transistor_743 (.in(1'b0), .out(transistor_738_out), .gate(H5));
  Transistor #(.\type ("n")) transistor_744 (.in(1'b0), .out(transistor_738_out), .gate(not_7_out));
  Transistor #(.\type ("n")) transistor_745 (.in(1'b0), .out(transistor_738_out), .gate(H3));
  Transistor #(.\type ("n")) transistor_746 (.in(1'b0), .out(transistor_738_out), .gate(H2));
  Transistor #(.\type ("n")) transistor_747 (.in(1'b0), .out(transistor_738_out), .gate(H0));
  Pull_Resistor #(.pull(1)) pull_resistor_90 (.node(transistor_738_out));
  Transistor #(.\type ("n")) transistor_748 (.in(1'b0), .out(transistor_748_out), .gate(not_23_out));
  Transistor #(.\type ("n")) transistor_749 (.in(1'b0), .out(transistor_748_out), .gate(M5));
  Transistor #(.\type ("n")) transistor_750 (.in(1'b0), .out(transistor_748_out), .gate(not_3_out));
  Transistor #(.\type ("n")) transistor_751 (.in(1'b0), .out(transistor_748_out), .gate(H7));
  Transistor #(.\type ("n")) transistor_752 (.in(1'b0), .out(transistor_748_out), .gate(H6));
  Transistor #(.\type ("n")) transistor_753 (.in(1'b0), .out(transistor_748_out), .gate(H5));
  Transistor #(.\type ("n")) transistor_754 (.in(1'b0), .out(transistor_748_out), .gate(not_7_out));
  Transistor #(.\type ("n")) transistor_755 (.in(1'b0), .out(transistor_748_out), .gate(not_8_out));
  Transistor #(.\type ("n")) transistor_756 (.in(1'b0), .out(transistor_748_out), .gate(not_9_out));
  Transistor #(.\type ("n")) transistor_757 (.in(1'b0), .out(transistor_748_out), .gate(H0));
  Pull_Resistor #(.pull(1)) pull_resistor_91 (.node(transistor_748_out));
  Transistor #(.\type ("n"), .gate("br")) transistor_758 (
    .in(1'b0), .out(pull_resistor_51_node), .gate(transistor_760_out));
  Transistor #(.\type ("n"), .gate("br")) transistor_759 (
    .in(1'b0), .out(pull_resistor_51_node), .gate(transistor_748_out));
  Transistor #(.\type ("n")) transistor_760 (.in(1'b0), .out(transistor_760_out), .gate(not_23_out));
  Transistor #(.\type ("n")) transistor_761 (.in(1'b0), .out(transistor_760_out), .gate(M5));
  Transistor #(.\type ("n")) transistor_762 (.in(1'b0), .out(transistor_760_out), .gate(not_3_out));
  Transistor #(.\type ("n")) transistor_763 (.in(1'b0), .out(transistor_760_out), .gate(not_4_out));
  Transistor #(.\type ("n")) transistor_764 (.in(1'b0), .out(transistor_760_out), .gate(not_5_out));
  Transistor #(.\type ("n")) transistor_765 (.in(1'b0), .out(transistor_760_out), .gate(H5));
  Transistor #(.\type ("n")) transistor_766 (.in(1'b0), .out(transistor_760_out), .gate(not_7_out));
  Transistor #(.\type ("n")) transistor_767 (.in(1'b0), .out(transistor_760_out), .gate(not_8_out));
  Transistor #(.\type ("n")) transistor_768 (.in(1'b0), .out(transistor_760_out), .gate(not_9_out));
  Transistor #(.\type ("n")) transistor_769 (.in(1'b0), .out(transistor_760_out), .gate(H0));
  Pull_Resistor #(.pull(1)) pull_resistor_92 (.node(transistor_760_out));
  Transistor #(.\type ("n"), .gate("br")) transistor_770 (
    .in(1'b0), .out(pull_resistor_51_node), .gate(transistor_771_out));
  Transistor #(.\type ("n")) transistor_771 (.in(1'b0), .out(transistor_771_out), .gate(not_23_out));
  Transistor #(.\type ("n")) transistor_772 (.in(1'b0), .out(transistor_771_out), .gate(M5));
  Transistor #(.\type ("n")) transistor_773 (.in(1'b0), .out(transistor_771_out), .gate(not_3_out));
  Transistor #(.\type ("n")) transistor_774 (.in(1'b0), .out(transistor_771_out), .gate(not_4_out));
  Transistor #(.\type ("n")) transistor_775 (.in(1'b0), .out(transistor_771_out), .gate(not_5_out));
  Transistor #(.\type ("n")) transistor_776 (.in(1'b0), .out(transistor_771_out), .gate(not_6_out));
  Transistor #(.\type ("n")) transistor_777 (.in(1'b0), .out(transistor_771_out), .gate(H4));
  Transistor #(.\type ("n")) transistor_778 (.in(1'b0), .out(transistor_771_out), .gate(not_8_out));
  Transistor #(.\type ("n")) transistor_779 (.in(1'b0), .out(transistor_771_out), .gate(H2));
  Transistor #(.\type ("n")) transistor_780 (.in(1'b0), .out(transistor_771_out), .gate(H0));
  Pull_Resistor #(.pull(1)) pull_resistor_93 (.node(transistor_771_out));
  Transistor #(.\type ("n"), .gate("br")) transistor_781 (
    .in(1'b0), .out(pull_resistor_49_node), .gate(transistor_783_out));
  Transistor #(.\type ("n"), .gate("br")) transistor_782 (
    .in(1'b0), .out(pull_resistor_52_node), .gate(transistor_783_out));
  Transistor #(.\type ("n")) transistor_783 (.in(1'b0), .out(transistor_783_out), .gate(not_23_out));
  Transistor #(.\type ("n")) transistor_784 (.in(1'b0), .out(transistor_783_out), .gate(not_1_out));
  Transistor #(.\type ("n")) transistor_785 (.in(1'b0), .out(transistor_783_out), .gate(not_3_out));
  Transistor #(.\type ("n")) transistor_786 (.in(1'b0), .out(transistor_783_out), .gate(not_4_out));
  Transistor #(.\type ("n")) transistor_787 (.in(1'b0), .out(transistor_783_out), .gate(not_5_out));
  Transistor #(.\type ("n")) transistor_788 (.in(1'b0), .out(transistor_783_out), .gate(H5));
  Transistor #(.\type ("n")) transistor_789 (.in(1'b0), .out(transistor_783_out), .gate(not_7_out));
  Transistor #(.\type ("n")) transistor_790 (.in(1'b0), .out(transistor_783_out), .gate(H0));
  Pull_Resistor #(.pull(1)) pull_resistor_94 (.node(transistor_783_out));
  Transistor #(.\type ("n"), .gate("br")) transistor_791 (
    .in(1'b0), .out(pull_resistor_49_node), .gate(transistor_793_out));
  Transistor #(.\type ("n"), .gate("br")) transistor_792 (
    .in(1'b0), .out(pull_resistor_52_node), .gate(transistor_793_out));
  Transistor #(.\type ("n")) transistor_793 (.in(1'b0), .out(transistor_793_out), .gate(not_23_out));
  Transistor #(.\type ("n")) transistor_794 (.in(1'b0), .out(transistor_793_out), .gate(not_1_out));
  Transistor #(.\type ("n")) transistor_795 (.in(1'b0), .out(transistor_793_out), .gate(not_3_out));
  Transistor #(.\type ("n")) transistor_796 (.in(1'b0), .out(transistor_793_out), .gate(not_4_out));
  Transistor #(.\type ("n")) transistor_797 (.in(1'b0), .out(transistor_793_out), .gate(not_5_out));
  Transistor #(.\type ("n")) transistor_798 (.in(1'b0), .out(transistor_793_out), .gate(not_6_out));
  Transistor #(.\type ("n")) transistor_799 (.in(1'b0), .out(transistor_793_out), .gate(H4));
  Transistor #(.\type ("n")) transistor_800 (.in(1'b0), .out(transistor_793_out), .gate(H3));
  Transistor #(.\type ("n")) transistor_801 (.in(1'b0), .out(transistor_793_out), .gate(H2));
  Transistor #(.\type ("n")) transistor_802 (.in(1'b0), .out(transistor_793_out), .gate(H0));
  Pull_Resistor #(.pull(1)) pull_resistor_95 (.node(transistor_793_out));
  Transistor #(.\type ("n"), .gate("br")) transistor_803 (
    .in(1'b0), .out(pull_resistor_49_node), .gate(transistor_805_out));
  Transistor #(.\type ("n"), .gate("br")) transistor_804 (
    .in(1'b0), .out(pull_resistor_52_node), .gate(transistor_805_out));
  Transistor #(.\type ("n")) transistor_805 (.in(1'b0), .out(transistor_805_out), .gate(not_23_out));
  Transistor #(.\type ("n")) transistor_806 (.in(1'b0), .out(transistor_805_out), .gate(not_1_out));
  Transistor #(.\type ("n")) transistor_807 (.in(1'b0), .out(transistor_805_out), .gate(not_3_out));
  Transistor #(.\type ("n")) transistor_808 (.in(1'b0), .out(transistor_805_out), .gate(not_4_out));
  Transistor #(.\type ("n")) transistor_809 (.in(1'b0), .out(transistor_805_out), .gate(not_5_out));
  Transistor #(.\type ("n")) transistor_810 (.in(1'b0), .out(transistor_805_out), .gate(not_6_out));
  Transistor #(.\type ("n")) transistor_811 (.in(1'b0), .out(transistor_805_out), .gate(H4));
  Transistor #(.\type ("n")) transistor_812 (.in(1'b0), .out(transistor_805_out), .gate(not_8_out));
  Transistor #(.\type ("n")) transistor_813 (.in(1'b0), .out(transistor_805_out), .gate(H0));
  Pull_Resistor #(.pull(1)) pull_resistor_96 (.node(transistor_805_out));
  not not_38 (HPLA_35, not_39_out);
  not not_39 (not_39_out, transistor_817_out);
  Transistor #(.\type ("n"), .gate("br")) transistor_814 (
    .in(1'b0), .out(pull_resistor_49_node), .gate(transistor_816_out));
  Transistor #(.\type ("n"), .gate("br")) transistor_815 (
    .in(1'b0), .out(pull_resistor_52_node), .gate(transistor_816_out));
  Transistor #(.\type ("n")) transistor_816 (.in(1'b0), .out(transistor_816_out), .gate(not_23_out));
  Transistor #(.\type ("n")) transistor_817 (.in(1'b0), .out(transistor_817_out), .gate(not_23_out));
  Transistor #(.\type ("n")) transistor_818 (.in(1'b0), .out(transistor_817_out), .gate(not_1_out));
  Transistor #(.\type ("n")) transistor_819 (.in(1'b0), .out(transistor_816_out), .gate(not_1_out));
  Transistor #(.\type ("n")) transistor_820 (.in(1'b0), .out(transistor_817_out), .gate(not_3_out));
  Transistor #(.\type ("n")) transistor_821 (.in(1'b0), .out(transistor_816_out), .gate(not_3_out));
  Transistor #(.\type ("n")) transistor_822 (.in(1'b0), .out(transistor_817_out), .gate(not_4_out));
  Transistor #(.\type ("n")) transistor_823 (.in(1'b0), .out(transistor_816_out), .gate(not_4_out));
  Transistor #(.\type ("n")) transistor_824 (.in(1'b0), .out(transistor_816_out), .gate(not_5_out));
  Transistor #(.\type ("n")) transistor_825 (.in(1'b0), .out(transistor_817_out), .gate(not_5_out));
  Transistor #(.\type ("n")) transistor_826 (.in(1'b0), .out(transistor_816_out), .gate(not_6_out));
  Transistor #(.\type ("n")) transistor_827 (.in(1'b0), .out(transistor_817_out), .gate(not_6_out));
  Transistor #(.\type ("n")) transistor_828 (.in(1'b0), .out(transistor_817_out), .gate(H4));
  Transistor #(.\type ("n")) transistor_829 (.in(1'b0), .out(transistor_816_out), .gate(not_7_out));
  Transistor #(.\type ("n")) transistor_830 (.in(1'b0), .out(transistor_817_out), .gate(H3));
  Transistor #(.\type ("n")) transistor_831 (.in(1'b0), .out(transistor_816_out), .gate(H2));
  Transistor #(.\type ("n")) transistor_832 (.in(1'b0), .out(transistor_817_out), .gate(not_9_out));
  Transistor #(.\type ("n")) transistor_833 (.in(1'b0), .out(transistor_817_out), .gate(not_10_out));
  Transistor #(.\type ("n")) transistor_834 (.in(1'b0), .out(transistor_816_out), .gate(not_10_out));
  Transistor #(.\type ("n")) transistor_835 (.in(1'b0), .out(transistor_817_out), .gate(H0));
  Transistor #(.\type ("n")) transistor_836 (.in(1'b0), .out(transistor_816_out), .gate(H0));
  Pull_Resistor #(.pull(1)) pull_resistor_97 (.node(transistor_816_out));
  Pull_Resistor #(.pull(1)) pull_resistor_98 (.node(transistor_817_out));
  Transistor #(.\type ("n"), .gate("br")) transistor_837 (
    .in(1'b0), .out(pull_resistor_49_node), .gate(transistor_817_out));
  Transistor #(.\type ("n")) transistor_838 (.in(1'b0), .out(transistor_838_out), .gate(not_23_out));
  Transistor #(.\type ("n")) transistor_839 (.in(1'b0), .out(transistor_838_out), .gate(not_1_out));
  Transistor #(.\type ("n")) transistor_840 (.in(1'b0), .out(transistor_838_out), .gate(H40));
  Transistor #(.\type ("n")) transistor_841 (.in(1'b0), .out(transistor_838_out), .gate(not_3_out));
  Transistor #(.\type ("n")) transistor_842 (.in(1'b0), .out(transistor_838_out), .gate(H7));
  Transistor #(.\type ("n")) transistor_843 (.in(1'b0), .out(transistor_838_out), .gate(H6));
  Transistor #(.\type ("n")) transistor_844 (.in(1'b0), .out(transistor_838_out), .gate(H5));
  Transistor #(.\type ("n")) transistor_845 (.in(1'b0), .out(transistor_838_out), .gate(not_7_out));
  Transistor #(.\type ("n")) transistor_846 (.in(1'b0), .out(transistor_838_out), .gate(H3));
  Transistor #(.\type ("n")) transistor_847 (.in(1'b0), .out(transistor_838_out), .gate(H0));
  Pull_Resistor #(.pull(1)) pull_resistor_99 (.node(transistor_838_out));
  not not_40 (HPLA_36, pull_resistor_51_node);
  Transistor #(.\type ("n"), .gate("br")) transistor_848 (
    .in(1'b0), .out(pull_resistor_49_node), .gate(transistor_838_out));
  Transistor #(.\type ("n"), .gate("br")) transistor_849 (
    .in(1'b0), .out(pull_resistor_52_node), .gate(transistor_838_out));
  Transistor #(.\type ("n"), .gate("br")) transistor_850 (
    .in(1'b0), .out(pull_resistor_52_node), .gate(transistor_851_out));
  Transistor #(.\type ("n")) transistor_851 (.in(1'b0), .out(transistor_851_out), .gate(not_23_out));
  Transistor #(.\type ("n")) transistor_852 (.in(1'b0), .out(transistor_851_out), .gate(not_1_out));
  Transistor #(.\type ("n")) transistor_853 (.in(1'b0), .out(transistor_851_out), .gate(H40));
  Transistor #(.\type ("n")) transistor_854 (.in(1'b0), .out(transistor_851_out), .gate(not_3_out));
  Transistor #(.\type ("n")) transistor_855 (.in(1'b0), .out(transistor_851_out), .gate(H7));
  Transistor #(.\type ("n")) transistor_856 (.in(1'b0), .out(transistor_851_out), .gate(H6));
  Transistor #(.\type ("n")) transistor_857 (.in(1'b0), .out(transistor_851_out), .gate(H5));
  Transistor #(.\type ("n")) transistor_858 (.in(1'b0), .out(transistor_851_out), .gate(H4));
  Transistor #(.\type ("n")) transistor_859 (.in(1'b0), .out(transistor_851_out), .gate(H3));
  Transistor #(.\type ("n")) transistor_860 (.in(1'b0), .out(transistor_851_out), .gate(not_9_out));
  Transistor #(.\type ("n")) transistor_861 (.in(1'b0), .out(transistor_851_out), .gate(H0));
  Pull_Resistor #(.pull(1)) pull_resistor_100 (.node(transistor_851_out));
  Transistor #(.\type ("n"), .gate("br")) transistor_862 (
    .in(1'b0), .out(pull_resistor_52_node), .gate(transistor_863_out));
  Transistor #(.\type ("n")) transistor_863 (.in(1'b0), .out(transistor_863_out), .gate(not_23_out));
  Transistor #(.\type ("n")) transistor_864 (.in(1'b0), .out(transistor_863_out), .gate(not_1_out));
  Transistor #(.\type ("n")) transistor_865 (.in(1'b0), .out(transistor_863_out), .gate(H40));
  Transistor #(.\type ("n")) transistor_866 (.in(1'b0), .out(transistor_863_out), .gate(not_3_out));
  Transistor #(.\type ("n")) transistor_867 (.in(1'b0), .out(transistor_863_out), .gate(H7));
  Transistor #(.\type ("n")) transistor_868 (.in(1'b0), .out(transistor_863_out), .gate(H6));
  Transistor #(.\type ("n")) transistor_869 (.in(1'b0), .out(transistor_863_out), .gate(H5));
  Transistor #(.\type ("n")) transistor_870 (.in(1'b0), .out(transistor_863_out), .gate(H4));
  Transistor #(.\type ("n")) transistor_871 (.in(1'b0), .out(transistor_863_out), .gate(not_8_out));
  Transistor #(.\type ("n")) transistor_872 (.in(1'b0), .out(transistor_863_out), .gate(H0));
  Pull_Resistor #(.pull(1)) pull_resistor_101 (.node(transistor_863_out));
  Transistor #(.\type ("n"), .gate("br")) transistor_873 (
    .in(1'b0), .out(pull_resistor_49_node), .gate(transistor_875_out));
  Transistor #(.\type ("n"), .gate("br")) transistor_874 (
    .in(1'b0), .out(pull_resistor_52_node), .gate(transistor_875_out));
  Transistor #(.\type ("n")) transistor_875 (.in(1'b0), .out(transistor_875_out), .gate(not_23_out));
  Transistor #(.\type ("n")) transistor_876 (.in(1'b0), .out(transistor_875_out), .gate(_2));
  Transistor #(.\type ("n")) transistor_877 (.in(1'b0), .out(transistor_875_out), .gate(not_1_out));
  Transistor #(.\type ("n")) transistor_878 (.in(1'b0), .out(transistor_875_out), .gate(H40));
  Transistor #(.\type ("n")) transistor_879 (.in(1'b0), .out(transistor_875_out), .gate(not_3_out));
  Transistor #(.\type ("n")) transistor_880 (.in(1'b0), .out(transistor_875_out), .gate(H7));
  Transistor #(.\type ("n")) transistor_881 (.in(1'b0), .out(transistor_875_out), .gate(H6));
  Transistor #(.\type ("n")) transistor_882 (.in(1'b0), .out(transistor_875_out), .gate(H5));
  Transistor #(.\type ("n")) transistor_883 (.in(1'b0), .out(transistor_875_out), .gate(not_7_out));
  Transistor #(.\type ("n")) transistor_884 (.in(1'b0), .out(transistor_875_out), .gate(not_8_out));
  Transistor #(.\type ("n")) transistor_885 (.in(1'b0), .out(transistor_875_out), .gate(H0));
  Pull_Resistor #(.pull(1)) pull_resistor_102 (.node(transistor_875_out));
  Transistor #(.\type ("n"), .gate("br")) transistor_886 (
    .in(1'b0), .out(pull_resistor_49_node), .gate(transistor_888_out));
  Transistor #(.\type ("n"), .gate("br")) transistor_887 (
    .in(1'b0), .out(pull_resistor_52_node), .gate(transistor_888_out));
  Transistor #(.\type ("n")) transistor_888 (.in(1'b0), .out(transistor_888_out), .gate(not_23_out));
  Transistor #(.\type ("n")) transistor_889 (.in(1'b0), .out(transistor_888_out), .gate(_1));
  Transistor #(.\type ("n")) transistor_890 (.in(1'b0), .out(transistor_888_out), .gate(not_1_out));
  Transistor #(.\type ("n")) transistor_891 (.in(1'b0), .out(transistor_888_out), .gate(H40));
  Transistor #(.\type ("n")) transistor_892 (.in(1'b0), .out(transistor_888_out), .gate(not_3_out));
  Transistor #(.\type ("n")) transistor_893 (.in(1'b0), .out(transistor_888_out), .gate(H7));
  Transistor #(.\type ("n")) transistor_894 (.in(1'b0), .out(transistor_888_out), .gate(H6));
  Transistor #(.\type ("n")) transistor_895 (.in(1'b0), .out(transistor_888_out), .gate(not_6_out));
  Transistor #(.\type ("n")) transistor_896 (.in(1'b0), .out(transistor_888_out), .gate(H4));
  Transistor #(.\type ("n")) transistor_897 (.in(1'b0), .out(transistor_888_out), .gate(H3));
  Transistor #(.\type ("n")) transistor_898 (.in(1'b0), .out(transistor_888_out), .gate(not_9_out));
  Transistor #(.\type ("n")) transistor_899 (.in(1'b0), .out(transistor_888_out), .gate(H0));
  Pull_Resistor #(.pull(1)) pull_resistor_103 (.node(transistor_888_out));
  Transistor #(.\type ("n"), .gate("br")) transistor_900 (
    .in(1'b0), .out(pull_resistor_49_node), .gate(transistor_902_out));
  Transistor #(.\type ("n"), .gate("br")) transistor_901 (
    .in(1'b0), .out(pull_resistor_52_node), .gate(transistor_902_out));
  Transistor #(.\type ("n")) transistor_902 (.in(1'b0), .out(transistor_902_out), .gate(not_23_out));
  Transistor #(.\type ("n")) transistor_903 (.in(1'b0), .out(transistor_902_out), .gate(_1));
  Transistor #(.\type ("n")) transistor_904 (.in(1'b0), .out(transistor_902_out), .gate(not_1_out));
  Transistor #(.\type ("n")) transistor_905 (.in(1'b0), .out(transistor_902_out), .gate(H40));
  Transistor #(.\type ("n")) transistor_906 (.in(1'b0), .out(transistor_902_out), .gate(not_3_out));
  Transistor #(.\type ("n")) transistor_907 (.in(1'b0), .out(transistor_902_out), .gate(H7));
  Transistor #(.\type ("n")) transistor_908 (.in(1'b0), .out(transistor_902_out), .gate(H6));
  Transistor #(.\type ("n")) transistor_909 (.in(1'b0), .out(transistor_902_out), .gate(not_6_out));
  Transistor #(.\type ("n")) transistor_910 (.in(1'b0), .out(transistor_902_out), .gate(H4));
  Transistor #(.\type ("n")) transistor_911 (.in(1'b0), .out(transistor_902_out), .gate(H3));
  Transistor #(.\type ("n")) transistor_912 (.in(1'b0), .out(transistor_902_out), .gate(H2));
  Transistor #(.\type ("n")) transistor_913 (.in(1'b0), .out(transistor_902_out), .gate(not_10_out));
  Transistor #(.\type ("n")) transistor_914 (.in(1'b0), .out(transistor_902_out), .gate(H0));
  Pull_Resistor #(.pull(1)) pull_resistor_104 (.node(transistor_902_out));
  Transistor #(.\type ("n"), .gate("br")) transistor_915 (
    .in(1'b0), .out(pull_resistor_52_node), .gate(transistor_916_out));
  Transistor #(.\type ("n")) transistor_916 (.in(1'b0), .out(transistor_916_out), .gate(not_23_out));
  Transistor #(.\type ("n")) transistor_917 (.in(1'b0), .out(transistor_917_out), .gate(not_23_out));
  Transistor #(.\type ("n")) transistor_918 (.in(1'b0), .out(transistor_916_out), .gate(not_1_out));
  Transistor #(.\type ("n")) transistor_919 (.in(1'b0), .out(transistor_917_out), .gate(not_1_out));
  Transistor #(.\type ("n")) transistor_920 (.in(1'b0), .out(transistor_917_out), .gate(not_2_out));
  Transistor #(.\type ("n")) transistor_921 (.in(1'b0), .out(transistor_916_out), .gate(not_2_out));
  Transistor #(.\type ("n")) transistor_922 (.in(1'b0), .out(transistor_916_out), .gate(not_3_out));
  Transistor #(.\type ("n")) transistor_923 (.in(1'b0), .out(transistor_917_out), .gate(not_3_out));
  Transistor #(.\type ("n")) transistor_924 (.in(1'b0), .out(transistor_917_out), .gate(H7));
  Transistor #(.\type ("n")) transistor_925 (.in(1'b0), .out(transistor_916_out), .gate(H7));
  Transistor #(.\type ("n")) transistor_926 (.in(1'b0), .out(transistor_917_out), .gate(not_5_out));
  Transistor #(.\type ("n")) transistor_927 (.in(1'b0), .out(transistor_916_out), .gate(not_5_out));
  Transistor #(.\type ("n")) transistor_928 (.in(1'b0), .out(transistor_917_out), .gate(H5));
  Transistor #(.\type ("n")) transistor_929 (.in(1'b0), .out(transistor_916_out), .gate(H5));
  Transistor #(.\type ("n")) transistor_930 (.in(1'b0), .out(transistor_916_out), .gate(H4));
  Transistor #(.\type ("n")) transistor_931 (.in(1'b0), .out(transistor_917_out), .gate(H4));
  Transistor #(.\type ("n")) transistor_932 (.in(1'b0), .out(transistor_916_out), .gate(H3));
  Transistor #(.\type ("n")) transistor_933 (.in(1'b0), .out(transistor_917_out), .gate(not_8_out));
  Transistor #(.\type ("n")) transistor_934 (.in(1'b0), .out(transistor_916_out), .gate(not_9_out));
  Transistor #(.\type ("n")) transistor_935 (.in(1'b0), .out(transistor_917_out), .gate(H0));
  Transistor #(.\type ("n")) transistor_936 (.in(1'b0), .out(transistor_916_out), .gate(H0));
  Pull_Resistor #(.pull(1)) pull_resistor_105 (.node(transistor_916_out));
  Pull_Resistor #(.pull(1)) pull_resistor_106 (.node(transistor_917_out));
  Transistor #(.\type ("n"), .gate("br")) transistor_937 (
    .in(1'b0), .out(pull_resistor_52_node), .gate(transistor_917_out));
  Transistor #(.\type ("n")) transistor_938 (.in(1'b0), .out(transistor_938_out), .gate(not_23_out));
  Transistor #(.\type ("n")) transistor_939 (.in(1'b0), .out(transistor_938_out), .gate(not_1_out));
  Transistor #(.\type ("n")) transistor_940 (.in(1'b0), .out(transistor_938_out), .gate(not_2_out));
  Transistor #(.\type ("n")) transistor_941 (.in(1'b0), .out(transistor_938_out), .gate(not_3_out));
  Transistor #(.\type ("n")) transistor_942 (.in(1'b0), .out(transistor_938_out), .gate(H7));
  Transistor #(.\type ("n")) transistor_943 (.in(1'b0), .out(transistor_938_out), .gate(not_5_out));
  Transistor #(.\type ("n")) transistor_944 (.in(1'b0), .out(transistor_938_out), .gate(H5));
  Transistor #(.\type ("n")) transistor_945 (.in(1'b0), .out(transistor_938_out), .gate(not_7_out));
  Transistor #(.\type ("n")) transistor_946 (.in(1'b0), .out(transistor_938_out), .gate(H3));
  Transistor #(.\type ("n")) transistor_947 (.in(1'b0), .out(transistor_938_out), .gate(H0));
  Pull_Resistor #(.pull(1)) pull_resistor_107 (.node(transistor_938_out));
  Transistor #(.\type ("n"), .gate("br")) transistor_948 (
    .in(1'b0), .out(pull_resistor_49_node), .gate(transistor_952_out));
  Transistor #(.\type ("n"), .gate("br")) transistor_949 (
    .in(1'b0), .out(pull_resistor_49_node), .gate(transistor_938_out));
  Transistor #(.\type ("n"), .gate("br")) transistor_950 (
    .in(1'b0), .out(pull_resistor_52_node), .gate(transistor_952_out));
  Transistor #(.\type ("n"), .gate("br")) transistor_951 (
    .in(1'b0), .out(pull_resistor_52_node), .gate(transistor_938_out));
  Transistor #(.\type ("n")) transistor_952 (.in(1'b0), .out(transistor_952_out), .gate(not_23_out));
  Transistor #(.\type ("n")) transistor_953 (.in(1'b0), .out(transistor_952_out), .gate(_1));
  Transistor #(.\type ("n")) transistor_954 (.in(1'b0), .out(transistor_952_out), .gate(not_1_out));
  Transistor #(.\type ("n")) transistor_955 (.in(1'b0), .out(transistor_952_out), .gate(not_2_out));
  Transistor #(.\type ("n")) transistor_956 (.in(1'b0), .out(transistor_952_out), .gate(not_3_out));
  Transistor #(.\type ("n")) transistor_957 (.in(1'b0), .out(transistor_952_out), .gate(H7));
  Transistor #(.\type ("n")) transistor_958 (.in(1'b0), .out(transistor_952_out), .gate(not_5_out));
  Transistor #(.\type ("n")) transistor_959 (.in(1'b0), .out(transistor_952_out), .gate(not_6_out));
  Transistor #(.\type ("n")) transistor_960 (.in(1'b0), .out(transistor_952_out), .gate(H4));
  Transistor #(.\type ("n")) transistor_961 (.in(1'b0), .out(transistor_952_out), .gate(H3));
  Transistor #(.\type ("n")) transistor_962 (.in(1'b0), .out(transistor_952_out), .gate(H0));
  Pull_Resistor #(.pull(1)) pull_resistor_108 (.node(transistor_952_out));
  Transistor #(.\type ("n"), .gate("br")) transistor_963 (
    .in(1'b0), .out(pull_resistor_49_node), .gate(transistor_965_out));
  Transistor #(.\type ("n"), .gate("br")) transistor_964 (
    .in(1'b0), .out(pull_resistor_52_node), .gate(transistor_965_out));
  Transistor #(.\type ("n")) transistor_965 (.in(1'b0), .out(transistor_965_out), .gate(not_23_out));
  Transistor #(.\type ("n")) transistor_966 (.in(1'b0), .out(transistor_965_out), .gate(_1));
  Transistor #(.\type ("n")) transistor_967 (.in(1'b0), .out(transistor_965_out), .gate(not_1_out));
  Transistor #(.\type ("n")) transistor_968 (.in(1'b0), .out(transistor_965_out), .gate(not_2_out));
  Transistor #(.\type ("n")) transistor_969 (.in(1'b0), .out(transistor_965_out), .gate(not_3_out));
  Transistor #(.\type ("n")) transistor_970 (.in(1'b0), .out(transistor_965_out), .gate(H7));
  Transistor #(.\type ("n")) transistor_971 (.in(1'b0), .out(transistor_965_out), .gate(not_5_out));
  Transistor #(.\type ("n")) transistor_972 (.in(1'b0), .out(transistor_965_out), .gate(not_6_out));
  Transistor #(.\type ("n")) transistor_973 (.in(1'b0), .out(transistor_965_out), .gate(H4));
  Transistor #(.\type ("n")) transistor_974 (.in(1'b0), .out(transistor_965_out), .gate(not_8_out));
  Transistor #(.\type ("n")) transistor_975 (.in(1'b0), .out(transistor_965_out), .gate(H2));
  Transistor #(.\type ("n")) transistor_976 (.in(1'b0), .out(transistor_965_out), .gate(H0));
  Pull_Resistor #(.pull(1)) pull_resistor_109 (.node(transistor_965_out));
  Transistor #(.\type ("n"), .gate("br")) transistor_977 (
    .in(1'b0), .out(pull_resistor_49_node), .gate(transistor_979_out));
  Transistor #(.\type ("n"), .gate("br")) transistor_978 (
    .in(1'b0), .out(pull_resistor_52_node), .gate(transistor_979_out));
  Transistor #(.\type ("n")) transistor_979 (.in(1'b0), .out(transistor_979_out), .gate(not_23_out));
  Transistor #(.\type ("n")) transistor_980 (.in(1'b0), .out(transistor_979_out), .gate(_1));
  Transistor #(.\type ("n")) transistor_981 (.in(1'b0), .out(transistor_979_out), .gate(not_1_out));
  Transistor #(.\type ("n")) transistor_982 (.in(1'b0), .out(transistor_979_out), .gate(not_2_out));
  Transistor #(.\type ("n")) transistor_983 (.in(1'b0), .out(transistor_979_out), .gate(not_3_out));
  Transistor #(.\type ("n")) transistor_984 (.in(1'b0), .out(transistor_979_out), .gate(H7));
  Transistor #(.\type ("n")) transistor_985 (.in(1'b0), .out(transistor_979_out), .gate(not_5_out));
  Transistor #(.\type ("n")) transistor_986 (.in(1'b0), .out(transistor_979_out), .gate(not_6_out));
  Transistor #(.\type ("n")) transistor_987 (.in(1'b0), .out(transistor_979_out), .gate(H4));
  Transistor #(.\type ("n")) transistor_988 (.in(1'b0), .out(transistor_979_out), .gate(not_8_out));
  Transistor #(.\type ("n")) transistor_989 (.in(1'b0), .out(transistor_979_out), .gate(not_9_out));
  Transistor #(.\type ("n")) transistor_990 (.in(1'b0), .out(transistor_979_out), .gate(H1));
  Transistor #(.\type ("n")) transistor_991 (.in(1'b0), .out(transistor_979_out), .gate(H0));
  Pull_Resistor #(.pull(1)) pull_resistor_110 (.node(transistor_979_out));
  Transistor #(.\type ("n"), .gate("br")) transistor_992 (
    .in(1'b0), .out(pull_resistor_49_node), .gate(transistor_994_out));
  Transistor #(.\type ("n"), .gate("br")) transistor_993 (
    .in(1'b0), .out(pull_resistor_52_node), .gate(transistor_994_out));
  Transistor #(.\type ("n")) transistor_994 (.in(1'b0), .out(transistor_994_out), .gate(not_23_out));
  Transistor #(.\type ("n")) transistor_995 (.in(1'b0), .out(transistor_994_out), .gate(_2));
  Transistor #(.\type ("n")) transistor_996 (.in(1'b0), .out(transistor_994_out), .gate(not_1_out));
  Transistor #(.\type ("n")) transistor_997 (.in(1'b0), .out(transistor_994_out), .gate(not_2_out));
  Transistor #(.\type ("n")) transistor_998 (.in(1'b0), .out(transistor_994_out), .gate(not_3_out));
  Transistor #(.\type ("n")) transistor_999 (.in(1'b0), .out(transistor_994_out), .gate(H7));
  Transistor #(.\type ("n")) transistor_1000 (.in(1'b0), .out(transistor_994_out), .gate(not_5_out));
  Transistor #(.\type ("n")) transistor_1001 (.in(1'b0), .out(transistor_994_out), .gate(H5));
  Transistor #(.\type ("n")) transistor_1002 (.in(1'b0), .out(transistor_994_out), .gate(not_7_out));
  Transistor #(.\type ("n")) transistor_1003 (.in(1'b0), .out(transistor_994_out), .gate(not_8_out));
  Transistor #(.\type ("n")) transistor_1004 (.in(1'b0), .out(transistor_994_out), .gate(H0));
  Pull_Resistor #(.pull(1)) pull_resistor_111 (.node(transistor_994_out));
  Transistor #(.\type ("n"), .gate("br")) transistor_1005 (
    .in(1'b0), .out(pull_resistor_49_node), .gate(transistor_1007_out));
  Transistor #(.\type ("n"), .gate("br")) transistor_1006 (
    .in(1'b0), .out(pull_resistor_52_node), .gate(transistor_1007_out));
  Transistor #(.\type ("n")) transistor_1007 (.in(1'b0), .out(transistor_1007_out), .gate(not_23_out));
  Transistor #(.\type ("n")) transistor_1008 (.in(1'b0), .out(transistor_1007_out), .gate(not_1_out));
  Transistor #(.\type ("n")) transistor_1009 (.in(1'b0), .out(transistor_1007_out), .gate(not_2_out));
  Transistor #(.\type ("n")) transistor_1010 (.in(1'b0), .out(transistor_1007_out), .gate(not_3_out));
  Transistor #(.\type ("n")) transistor_1011 (.in(1'b0), .out(transistor_1007_out), .gate(not_4_out));
  Transistor #(.\type ("n")) transistor_1012 (.in(1'b0), .out(transistor_1007_out), .gate(not_5_out));
  Transistor #(.\type ("n")) transistor_1013 (.in(1'b0), .out(transistor_1007_out), .gate(H5));
  Transistor #(.\type ("n")) transistor_1014 (.in(1'b0), .out(transistor_1007_out), .gate(H4));
  Transistor #(.\type ("n")) transistor_1015 (.in(1'b0), .out(transistor_1007_out), .gate(not_8_out));
  Transistor #(.\type ("n")) transistor_1016 (.in(1'b0), .out(transistor_1007_out), .gate(H2));
  Transistor #(.\type ("n")) transistor_1017 (.in(1'b0), .out(transistor_1007_out), .gate(not_10_out));
  Transistor #(.\type ("n")) transistor_1018 (.in(1'b0), .out(transistor_1007_out), .gate(H0));
  Pull_Resistor #(.pull(1)) pull_resistor_112 (.node(transistor_1007_out));
  Transistor #(.\type ("n"), .gate("br")) transistor_1019 (
    .in(1'b0), .out(pull_resistor_49_node), .gate(transistor_1021_out));
  Transistor #(.\type ("n"), .gate("br")) transistor_1020 (
    .in(1'b0), .out(pull_resistor_52_node), .gate(transistor_1021_out));
  Transistor #(.\type ("n")) transistor_1021 (.in(1'b0), .out(transistor_1021_out), .gate(not_23_out));
  Transistor #(.\type ("n")) transistor_1022 (.in(1'b0), .out(transistor_1022_out), .gate(not_23_out));
  Transistor #(.\type ("n")) transistor_1023 (.in(1'b0), .out(transistor_1021_out), .gate(not_1_out));
  Transistor #(.\type ("n")) transistor_1024 (.in(1'b0), .out(transistor_1022_out), .gate(not_1_out));
  Transistor #(.\type ("n")) transistor_1025 (.in(1'b0), .out(transistor_1022_out), .gate(not_2_out));
  Transistor #(.\type ("n")) transistor_1026 (.in(1'b0), .out(transistor_1021_out), .gate(not_2_out));
  Transistor #(.\type ("n")) transistor_1027 (.in(1'b0), .out(transistor_1021_out), .gate(not_3_out));
  Transistor #(.\type ("n")) transistor_1028 (.in(1'b0), .out(transistor_1022_out), .gate(not_3_out));
  Transistor #(.\type ("n")) transistor_1029 (.in(1'b0), .out(transistor_1022_out), .gate(not_4_out));
  Transistor #(.\type ("n")) transistor_1030 (.in(1'b0), .out(transistor_1021_out), .gate(not_4_out));
  Transistor #(.\type ("n")) transistor_1031 (.in(1'b0), .out(transistor_1022_out), .gate(not_5_out));
  Transistor #(.\type ("n")) transistor_1032 (.in(1'b0), .out(transistor_1021_out), .gate(not_5_out));
  Transistor #(.\type ("n")) transistor_1033 (.in(1'b0), .out(transistor_1021_out), .gate(H5));
  Transistor #(.\type ("n")) transistor_1034 (.in(1'b0), .out(transistor_1022_out), .gate(not_6_out));
  Transistor #(.\type ("n")) transistor_1035 (.in(1'b0), .out(transistor_1022_out), .gate(H4));
  Transistor #(.\type ("n")) transistor_1036 (.in(1'b0), .out(transistor_1021_out), .gate(H4));
  Transistor #(.\type ("n")) transistor_1037 (.in(1'b0), .out(transistor_1022_out), .gate(H3));
  Transistor #(.\type ("n")) transistor_1038 (.in(1'b0), .out(transistor_1021_out), .gate(not_8_out));
  Transistor #(.\type ("n")) transistor_1039 (.in(1'b0), .out(transistor_1021_out), .gate(not_9_out));
  Transistor #(.\type ("n")) transistor_1040 (.in(1'b0), .out(transistor_1022_out), .gate(not_9_out));
  Transistor #(.\type ("n")) transistor_1041 (.in(1'b0), .out(transistor_1021_out), .gate(H1));
  Transistor #(.\type ("n")) transistor_1042 (.in(1'b0), .out(transistor_1022_out), .gate(H1));
  Transistor #(.\type ("n")) transistor_1043 (.in(1'b0), .out(transistor_1021_out), .gate(H0));
  Transistor #(.\type ("n")) transistor_1044 (.in(1'b0), .out(transistor_1022_out), .gate(H0));
  Pull_Resistor #(.pull(1)) pull_resistor_113 (.node(transistor_1022_out));
  Pull_Resistor #(.pull(1)) pull_resistor_114 (.node(transistor_1021_out));
  Transistor #(.\type ("n"), .gate("br")) transistor_1045 (
    .in(1'b0), .out(pull_resistor_49_node), .gate(transistor_1022_out));
  Transistor #(.\type ("n"), .gate("br")) transistor_1046 (
    .in(1'b0), .out(pull_resistor_52_node), .gate(transistor_1022_out));
  Transistor #(.\type ("n")) transistor_1047 (.in(1'b0), .out(transistor_1047_out), .gate(not_23_out));
  Transistor #(.\type ("n")) transistor_1048 (.in(1'b0), .out(transistor_1047_out), .gate(not_1_out));
  Transistor #(.\type ("n")) transistor_1049 (.in(1'b0), .out(transistor_1047_out), .gate(H8));
  Transistor #(.\type ("n")) transistor_1050 (.in(1'b0), .out(transistor_1047_out), .gate(not_8_out));
  Transistor #(.\type ("n")) transistor_1051 (.in(1'b0), .out(transistor_1047_out), .gate(H2));
  Transistor #(.\type ("n")) transistor_1052 (.in(1'b0), .out(transistor_1047_out), .gate(not_10_out));
  Transistor #(.\type ("n")) transistor_1053 (.in(1'b0), .out(transistor_1047_out), .gate(H0));
  Pull_Resistor #(.pull(1)) pull_resistor_115 (.node(transistor_1047_out));
  Transistor #(.\type ("n"), .gate("br")) transistor_1054 (
    .in(1'b0), .out(pull_resistor_53_node), .gate(transistor_1047_out));
  Transistor #(.\type ("n"), .gate("br")) transistor_1055 (
    .in(1'b0), .out(pull_resistor_53_node), .gate(transistor_1056_out));
  Transistor #(.\type ("n")) transistor_1056 (.in(1'b0), .out(transistor_1056_out), .gate(not_23_out));
  Transistor #(.\type ("n")) transistor_1057 (.in(1'b0), .out(transistor_1056_out), .gate(not_1_out));
  Transistor #(.\type ("n")) transistor_1058 (.in(1'b0), .out(transistor_1056_out), .gate(not_2_out));
  Transistor #(.\type ("n")) transistor_1059 (.in(1'b0), .out(transistor_1056_out), .gate(not_3_out));
  Transistor #(.\type ("n")) transistor_1060 (.in(1'b0), .out(transistor_1056_out), .gate(H7));
  Transistor #(.\type ("n")) transistor_1061 (.in(1'b0), .out(transistor_1056_out), .gate(H6));
  Transistor #(.\type ("n")) transistor_1062 (.in(1'b0), .out(transistor_1056_out), .gate(not_8_out));
  Transistor #(.\type ("n")) transistor_1063 (.in(1'b0), .out(transistor_1056_out), .gate(H2));
  Transistor #(.\type ("n")) transistor_1064 (.in(1'b0), .out(transistor_1056_out), .gate(not_10_out));
  Transistor #(.\type ("n")) transistor_1065 (.in(1'b0), .out(transistor_1056_out), .gate(H0));
  Pull_Resistor #(.pull(1)) pull_resistor_116 (.node(transistor_1056_out));
  Transistor #(.\type ("n"), .gate("br")) transistor_1066 (
    .in(1'b0), .out(pull_resistor_47_node), .gate(transistor_1067_out));
  Transistor #(.\type ("n")) transistor_1067 (.in(1'b0), .out(transistor_1067_out), .gate(not_23_out));
  Transistor #(.\type ("n")) transistor_1068 (.in(1'b0), .out(transistor_1067_out), .gate(M5));
  Transistor #(.\type ("n")) transistor_1069 (.in(1'b0), .out(transistor_1067_out), .gate(not_3_out));
  Transistor #(.\type ("n")) transistor_1070 (.in(1'b0), .out(transistor_1067_out), .gate(H7));
  Transistor #(.\type ("n")) transistor_1071 (.in(1'b0), .out(transistor_1067_out), .gate(H6));
  Transistor #(.\type ("n")) transistor_1072 (.in(1'b0), .out(transistor_1067_out), .gate(H5));
  Transistor #(.\type ("n")) transistor_1073 (.in(1'b0), .out(transistor_1067_out), .gate(not_8_out));
  Transistor #(.\type ("n")) transistor_1074 (.in(1'b0), .out(transistor_1067_out), .gate(not_9_out));
  Transistor #(.\type ("n")) transistor_1075 (.in(1'b0), .out(transistor_1067_out), .gate(H1));
  Transistor #(.\type ("n")) transistor_1076 (.in(1'b0), .out(transistor_1067_out), .gate(H0));
  Pull_Resistor #(.pull(1)) pull_resistor_117 (.node(transistor_1067_out));
  Transistor #(.\type ("n"), .gate("br")) transistor_1077 (
    .in(1'b0), .out(pull_resistor_47_node), .gate(transistor_1078_out));
  Transistor #(.\type ("n")) transistor_1078 (.in(1'b0), .out(transistor_1078_out), .gate(not_23_out));
  Transistor #(.\type ("n")) transistor_1079 (.in(1'b0), .out(transistor_1078_out), .gate(M5));
  Transistor #(.\type ("n")) transistor_1080 (.in(1'b0), .out(transistor_1078_out), .gate(not_3_out));
  Transistor #(.\type ("n")) transistor_1081 (.in(1'b0), .out(transistor_1078_out), .gate(H7));
  Transistor #(.\type ("n")) transistor_1082 (.in(1'b0), .out(transistor_1078_out), .gate(H6));
  Transistor #(.\type ("n")) transistor_1083 (.in(1'b0), .out(transistor_1078_out), .gate(H5));
  Transistor #(.\type ("n")) transistor_1084 (.in(1'b0), .out(transistor_1078_out), .gate(not_7_out));
  Transistor #(.\type ("n")) transistor_1085 (.in(1'b0), .out(transistor_1078_out), .gate(H2));
  Transistor #(.\type ("n")) transistor_1086 (.in(1'b0), .out(transistor_1078_out), .gate(H1));
  Transistor #(.\type ("n")) transistor_1087 (.in(1'b0), .out(transistor_1078_out), .gate(H0));
  Pull_Resistor #(.pull(1)) pull_resistor_118 (.node(transistor_1078_out));
  Transistor #(.\type ("n"), .gate("br")) transistor_1088 (
    .in(1'b0), .out(pull_resistor_47_node), .gate(transistor_1089_out));
  Transistor #(.\type ("n")) transistor_1089 (.in(1'b0), .out(transistor_1089_out), .gate(not_23_out));
  Transistor #(.\type ("n")) transistor_1090 (.in(1'b0), .out(transistor_1089_out), .gate(M5));
  Transistor #(.\type ("n")) transistor_1091 (.in(1'b0), .out(transistor_1089_out), .gate(not_3_out));
  Transistor #(.\type ("n")) transistor_1092 (.in(1'b0), .out(transistor_1089_out), .gate(not_4_out));
  Transistor #(.\type ("n")) transistor_1093 (.in(1'b0), .out(transistor_1089_out), .gate(not_5_out));
  Transistor #(.\type ("n")) transistor_1094 (.in(1'b0), .out(transistor_1089_out), .gate(H5));
  Transistor #(.\type ("n")) transistor_1095 (.in(1'b0), .out(transistor_1089_out), .gate(not_7_out));
  Transistor #(.\type ("n")) transistor_1096 (.in(1'b0), .out(transistor_1089_out), .gate(not_8_out));
  Transistor #(.\type ("n")) transistor_1097 (.in(1'b0), .out(transistor_1089_out), .gate(H1));
  Transistor #(.\type ("n")) transistor_1098 (.in(1'b0), .out(transistor_1089_out), .gate(H0));
  Pull_Resistor #(.pull(1)) pull_resistor_119 (.node(transistor_1089_out));
  Transistor #(.\type ("n"), .gate("br")) transistor_1099 (
    .in(1'b0), .out(pull_resistor_47_node), .gate(transistor_1100_out));
  Transistor #(.\type ("n")) transistor_1100 (.in(1'b0), .out(transistor_1100_out), .gate(not_23_out));
  Transistor #(.\type ("n")) transistor_1101 (.in(1'b0), .out(transistor_1100_out), .gate(M5));
  Transistor #(.\type ("n")) transistor_1102 (.in(1'b0), .out(transistor_1100_out), .gate(not_3_out));
  Transistor #(.\type ("n")) transistor_1103 (.in(1'b0), .out(transistor_1100_out), .gate(not_4_out));
  Transistor #(.\type ("n")) transistor_1104 (.in(1'b0), .out(transistor_1100_out), .gate(not_5_out));
  Transistor #(.\type ("n")) transistor_1105 (.in(1'b0), .out(transistor_1100_out), .gate(not_6_out));
  Transistor #(.\type ("n")) transistor_1106 (.in(1'b0), .out(transistor_1100_out), .gate(H4));
  Transistor #(.\type ("n")) transistor_1107 (.in(1'b0), .out(transistor_1100_out), .gate(H3));
  Transistor #(.\type ("n")) transistor_1108 (.in(1'b0), .out(transistor_1100_out), .gate(not_9_out));
  Transistor #(.\type ("n")) transistor_1109 (.in(1'b0), .out(transistor_1100_out), .gate(H1));
  Transistor #(.\type ("n")) transistor_1110 (.in(1'b0), .out(transistor_1100_out), .gate(H0));
  Pull_Resistor #(.pull(1)) pull_resistor_120 (.node(transistor_1100_out));
  Transistor #(.\type ("n"), .gate("br")) transistor_1111 (
    .in(1'b0), .out(pull_resistor_47_node), .gate(transistor_1112_out));
  Transistor #(.\type ("n")) transistor_1112 (.in(1'b0), .out(transistor_1112_out), .gate(not_23_out));
  Transistor #(.\type ("n")) transistor_1113 (.in(1'b0), .out(transistor_1112_out), .gate(M5));
  Transistor #(.\type ("n")) transistor_1114 (.in(1'b0), .out(transistor_1112_out), .gate(not_3_out));
  Transistor #(.\type ("n")) transistor_1115 (.in(1'b0), .out(transistor_1112_out), .gate(not_4_out));
  Transistor #(.\type ("n")) transistor_1116 (.in(1'b0), .out(transistor_1112_out), .gate(not_5_out));
  Transistor #(.\type ("n")) transistor_1117 (.in(1'b0), .out(transistor_1112_out), .gate(not_6_out));
  Transistor #(.\type ("n")) transistor_1118 (.in(1'b0), .out(transistor_1112_out), .gate(H4));
  Transistor #(.\type ("n")) transistor_1119 (.in(1'b0), .out(transistor_1112_out), .gate(not_8_out));
  Transistor #(.\type ("n")) transistor_1120 (.in(1'b0), .out(transistor_1112_out), .gate(H2));
  Transistor #(.\type ("n")) transistor_1121 (.in(1'b0), .out(transistor_1112_out), .gate(H1));
  Transistor #(.\type ("n")) transistor_1122 (.in(1'b0), .out(transistor_1112_out), .gate(H0));
  Pull_Resistor #(.pull(1)) pull_resistor_121 (.node(transistor_1112_out));

  // Notes on the sheet:
  //   0
  //   A
  //   /A
  //   B
  //   /B
  //   H8
  //   H7
  //   H6
  //   H5
  //   H4
  //   H3
  //   H2
  //   H1
  //   H0
  //   2
  //   1
  //   3
  //   4
  //   5
  //   6
  //   7
  //   8
  //   9
  //   10
  //   11
  //   12
  //   13
  //   14
  //   15
  //   16
  //   17
  //   18
  //   19
  //   20
  //   21
  //   22
  //   23
  //   24
  //   25
  //   26
  //   27
  //   28
  //   29
  //   30
  //   31
  //   32
  //   /C
  //   C
  //   1
  //   2
  //   A
  //   /A
  //   B
  //   /B
  //   H8
  //   H7
  //   H6
  //   H5
  //   H4
  //   H3
  //   H2
  //   H1
  //   H0
  //   33
  //   34
  //   35
  //   36
  //   37
  //   38
  //   39
  //   40
  //   41
  //   42
  //   43
  //   44
  //   45
  //   46
  //   47
  //   48
  //   49
  //   50
  //   51
  //   52
  //   53
  //   54
  //   55
  //   56
  //   57
  //   58
  //   59
  //   60
  //   61
  //   62
  //   63
endmodule

// FSM V LOGIC
module FSM_VLOGIC (
  input  CLK2,
  input  CLK1,
  input  VPLA_0,
  input  _138,
  input  VPLA_8,
  input  VPLA_1,
  input  VPLA_2,
  input  _156,
  input  SYSRES,
  input  VPLA_3,
  input  VPLA_4,
  input  VPLA_5,
  input  VPLA_6,
  input  VPLA_7,
  input  M5,
  input  _154,
  input  _158,
  input  _161,
  input  _157,
  input  _155,
  input  _145,
  output _132,
  output _143,
  output _137,
  output _150,
  output _139,
  output _148,
  output _140,
  output _141,
  output _153,
  output nVSYNC_1,
  output _151,
  output _149,
  output _160,
  output ODD_EVEN
);

  wire _28_out, _29_out, _30_2_out, _30_out, _31_2_out, _31_out, _32_2_out, _32_out, _33_out, _35_out,
       _36_out, _37_out, _38_out, _39_out, _40_out, _42_2_out, _42_out, _43_out, _44_out, _45_out, _46_out,
       _47_out, _48_out, _55_out, _56_2_out, _56_out, _76_2_out, _76_3_out, _76_out, d_ff_1_q,
       d_latch_1_out_4, d_latch_2_out_4, d_latch_3_out_4, d_latch_4_out_4, d_latch_5_out_4, d_latch_6_out_4,
       d_latch_7_out_4, d_latch_8_out_4, d_latch_9_out_4, d_latch_10_out_4, d_latch_11_out_4,
       d_latch_12_out_4, d_latch_13_out_4, d_latch_14_out_4, d_latch_15_out_4, d_latch_18_out_4,
       d_latch_19_out_4, d_latch_20_out_4, d_latch_21_out_4, d_latch_23_out_4, d_latch_24_out_4,
       d_latch_25_out_4, d_latch_26_out_4, d_latch_27_out_4, d_latch_28_out_4, d_latch_29_out_4,
       d_latch_30_out_4, not_1_out, not_2_out, not_3_out, not_4_out, not_5_out, not_7_out, not_8_out,
       not_9_out, not_10_out, not_11_out, not_12_out, not_13_out, not_14_out, s_r_ff_3_q, s_r_ff_4_q,
       s_r_ff_5_q, s_r_ff_6_q;

  or _31 (_31_out, _158, _157);
  not not_1 (not_1_out, _31_2_out);
  or _30 (_30_out, not_1_out, d_latch_28_out_4);
  not not_2 (not_2_out, _37_out);
  not not_3 (not_3_out, VPLA_8);
  not not_4 (not_4_out, VPLA_1);
  nand _31_2 (_31_2_out, _161, _31_out);
  nand _30_2 (_30_2_out, _29_out, _30_out);
  nor _76 (_76_out, not_2_out, ODD_EVEN);
  and _76_2 (_76_2_out, not_2_out, ODD_EVEN);
  not not_5 (not_5_out, _30_2_out);
  nor _76_3 (_76_3_out, _76_out, not_8_out, _76_2_out);
  D_Latch d_latch_1 (.in_1(CLK1), .in_2(VPLA_0), .out_4(d_latch_1_out_4));  // open: out_3
  D_Latch d_latch_2 (.in_1(CLK1), .in_2(not_3_out), .out_4(d_latch_2_out_4));  // open: out_3
  D_Latch d_latch_3 (.in_1(CLK1), .in_2(not_4_out), .out_4(d_latch_3_out_4));  // open: out_3
  D_Latch d_latch_4 (.in_1(CLK1), .in_2(VPLA_2), .out_4(d_latch_4_out_4));  // open: out_3
  D_Latch d_latch_5 (.in_1(CLK1), .in_2(VPLA_3), .out_4(d_latch_5_out_4));  // open: out_3
  D_Latch d_latch_6 (.in_1(CLK1), .in_2(VPLA_4), .out_4(d_latch_6_out_4));  // open: out_3
  D_Latch d_latch_7 (.in_1(CLK1), .in_2(s_r_ff_4_q), .out_4(d_latch_7_out_4));  // open: out_3
  D_Latch d_latch_8 (.in_1(CLK1), .in_2(VPLA_5), .out_4(d_latch_8_out_4));  // open: out_3
  D_Latch d_latch_9 (.in_1(CLK1), .in_2(VPLA_6), .out_4(d_latch_9_out_4));  // open: out_3
  D_Latch d_latch_10 (.in_1(CLK1), .in_2(VPLA_7), .out_4(d_latch_10_out_4));  // open: out_3
  D_Latch d_latch_11 (.in_1(CLK1), .in_2(_158), .out_4(d_latch_11_out_4));  // open: out_3
  nor _29 (_29_out, d_latch_21_out_4, SYSRES);
  D_Latch d_latch_12 (.in_1(CLK1), .in_2(_157), .out_4(d_latch_12_out_4));  // open: out_3
  D_Latch d_latch_13 (.in_1(CLK1), .in_2(not_5_out), .out_4(d_latch_13_out_4));  // open: out_3
  D_Latch d_latch_14 (.in_1(CLK1), .in_2(d_latch_28_out_4), .out_4(d_latch_14_out_4));  // open: out_3
  D_Flip_Flop #(.trigger("high")) d_ff_1 (.clk(CLK1), .D(_76_3_out), .Q(d_ff_1_q));  // open: Qn, preset, en, reset
  D_Latch d_latch_15 (.in_1(CLK1), .in_2(_36_out), .out_4(d_latch_15_out_4));  // open: out_3
  D_Latch d_latch_16 (.in_1(CLK2), .in_2(d_latch_1_out_4), .out_4(_132));  // open: out_3
  D_Latch d_latch_17 (.in_1(CLK2), .in_2(d_latch_2_out_4), .out_4(_139));  // open: out_3
  D_Latch d_latch_18 (.in_1(CLK2), .in_2(d_latch_3_out_4), .out_4(d_latch_18_out_4));  // open: out_3
  D_Latch d_latch_19 (.in_1(CLK2), .in_2(d_latch_4_out_4), .out_4(d_latch_19_out_4));  // open: out_3
  not not_6 (_140, d_latch_19_out_4);
  not not_7 (not_7_out, d_latch_19_out_4);
  D_Latch d_latch_20 (.in_1(CLK2), .in_2(d_latch_5_out_4), .out_4(d_latch_20_out_4));  // open: out_3
  D_Latch d_latch_21 (.in_1(CLK2), .in_2(d_latch_6_out_4), .out_4(d_latch_21_out_4));  // open: out_3
  D_Latch d_latch_22 (.in_1(CLK2), .in_2(d_latch_7_out_4), .out_4(nVSYNC_1));  // open: out_3
  D_Latch d_latch_23 (.in_1(CLK2), .in_2(d_latch_8_out_4), .out_4(d_latch_23_out_4));  // open: out_3
  D_Latch d_latch_24 (.in_1(CLK2), .in_2(d_latch_9_out_4), .out_4(d_latch_24_out_4));  // open: out_3
  D_Latch d_latch_25 (.in_1(CLK2), .in_2(d_latch_10_out_4), .out_4(d_latch_25_out_4));  // open: out_3
  D_Latch d_latch_26 (.in_1(CLK2), .in_2(d_latch_11_out_4), .out_4(d_latch_26_out_4));  // open: out_3
  D_Latch d_latch_27 (.in_1(CLK2), .in_2(d_latch_12_out_4), .out_4(d_latch_27_out_4));  // open: out_3
  D_Latch d_latch_28 (.in_1(CLK2), .in_2(d_latch_13_out_4), .out_4(d_latch_28_out_4));  // open: out_3
  D_Latch d_latch_29 (.in_1(CLK2), .in_2(d_latch_14_out_4), .out_4(d_latch_29_out_4));  // open: out_3
  not not_8 (not_8_out, _42_out);
  D_Flip_Flop #(.trigger("high")) d_ff_2 (
    .clk(CLK2), .D(d_ff_1_q), .Q(ODD_EVEN), .reset(d_latch_30_out_4));  // open: Qn, preset, en
  D_Latch d_latch_30 (.in_1(CLK2), .in_2(d_latch_15_out_4), .out_4(d_latch_30_out_4));  // open: out_3
  and _38 (_38_out, _155, _33_out);
  and _37 (_37_out, _33_out, not_12_out);
  not not_9 (not_9_out, _145);
  or _43 (_43_out, _154, not_11_out);
  not not_10 (not_10_out, d_latch_29_out_4);
  not not_11 (not_11_out, ODD_EVEN);
  not not_12 (not_12_out, _155);
  and _33 (_33_out, not_7_out, _156);
  and _39 (_39_out, d_latch_20_out_4, _43_out);
  and _45 (_45_out, _43_out, d_latch_23_out_4);
  and _47 (_47_out, _43_out, d_latch_24_out_4);
  and _46 (_46_out, _43_out, d_latch_25_out_4);
  and _34 (_160, d_latch_28_out_4, not_10_out, _155);
  nor _42 (_42_out, SYSRES, not_9_out, _42_2_out);
  and _28 (_28_out, d_latch_26_out_4, _160);
  and _32 (_32_out, d_latch_27_out_4, _160);
  and _42_2 (_42_2_out, not_14_out, _38_out);
  and _36 (_36_out, _38_out, s_r_ff_6_q);
  or _35 (_35_out, not_7_out, SYSRES);
  or _40 (_40_out, SYSRES, _39_out);
  or _44 (_44_out, SYSRES, _45_out);
  or _48 (_48_out, SYSRES, _45_out);
  or _55 (_55_out, SYSRES, _46_out);
  nor _32_2 (_32_2_out, SYSRES, _32_out);
  nand _56 (_56_out, _138, _56_2_out);
  or _56_2 (_56_2_out, _139, _148);
  S_R_Flip_Flop s_r_ff_1 (.Q(_148), .preset(d_latch_18_out_4), .reset(_35_out));  // open: S, clk, R, Qn, en
  S_R_Flip_Flop s_r_ff_2 (.Q(_141), .preset(_40_out), .reset(d_latch_21_out_4));  // open: S, clk, R, Qn, en
  S_R_Flip_Flop s_r_ff_3 (.Q(s_r_ff_3_q), .preset(_39_out), .reset(_44_out));  // open: S, clk, R, Qn, en
  S_R_Flip_Flop s_r_ff_4 (.Q(s_r_ff_4_q), .preset(_48_out), .reset(_47_out));  // open: S, clk, R, Qn, en
  S_R_Flip_Flop s_r_ff_5 (.Q(s_r_ff_5_q), .preset(_47_out), .reset(_55_out));  // open: S, clk, R, Qn, en
  S_R_Flip_Flop s_r_ff_6 (.Q(s_r_ff_6_q), .preset(_28_out), .reset(not_13_out));  // open: S, clk, R, Qn, en
  not not_13 (not_13_out, _32_2_out);
  not not_14 (not_14_out, s_r_ff_6_q);
  not not_15 (_143, _56_out);
  not not_16 (_150, _56_out);
  and _41 (_153, s_r_ff_3_q, M5);
  and _49 (_151, M5, s_r_ff_4_q);
  and _54 (_149, M5, s_r_ff_5_q);
  not not_17 (_137, _150);

  // Notes on the sheet:
  //   152
  //   24
  //   53
  //   18
  //   23
  //   R
  //   9
  //   3
  //   10
  //   11
  //   12
  //   8
  //   6
  //   7
  //   5
  //   4
  //   13
  //   16
  //   15
  //   14
  //   76
  //   17
  //   A
  //   19
  //   20
  //   26
  //   1
  //   21
  //   22
  //   27
  //   2A3OI
  //   a
  //   b
  //   c
  //   d
  //   61
  //   62
  //   59
  //   58
  //   57
  //   60
  //   25
  //   2
  //   52
  //   51
  //   50
  //   142
endmodule

// FSM H LOGIC
module FSM_HLOGIC (
  input  CLK2,
  input  CLK1,
  input  _60,
  input  _62,
  input  HPLA_3,
  input  HPLA_4,
  input  _69,
  input  HPLA_5,
  input  HPLA_6,
  input  HPLA_7,
  input  HPLA_8,
  input  HPLA_9,
  input  HPLA_10,
  input  HPLA_11,
  input  _73,
  input  _74,
  input  _72,
  input  _48,
  input  nVSYNC_1,
  input  nHSYNC_IN,
  input  _90,
  input  M5,
  input  _112,
  input  SYSRES,
  input  HPLA_0,
  input  HPLA_1,
  input  HPLA_2,
  input  HPLA_12,
  input  HPLA_13,
  input  _111,
  input  _128,
  input  HPLA_14,
  input  HPLA_15,
  input  HPLA_16,
  input  _26,
  input  HPLA_17,
  input  HPLA_18,
  input  HPLA_19,
  input  HPLA_21,
  input  HPLA_22,
  input  HPLA_20,
  input  HPLA_32,
  input  HPLA_23,
  input  HPLA_24,
  input  _98,
  input  _86,
  input  HPLA_25,
  input  HPLA_26,
  input  _93,
  input  HPLA_27,
  input  HPLA_35,
  input  HPLA_28,
  input  HPLA_29,
  input  HPLA_31,
  input  HPLA_34,
  input  HPLA_36,
  input  HPLA_33,
  input  HPLA_30,
  input  _87,
  input  _107__54,
  input  _103,
  input  _114,
  output _61,
  output _63,
  output _113,
  output VSYNC_OUT,
  output nCSYNC_OUT,
  output _96,
  output nHSYNC_OUT,
  output N307,
  output _52,
  output _68,
  output _49,
  output _43,
  output [15:0] D_OUT,
  output _44,
  output _40,
  output _58,
  output _66,
  output _75,
  output _90_2,
  output _104,
  output _116,
  output _100,
  output _37,
  output _39,
  output _45,
  output _55,
  output _67,
  output _94,
  output _70,
  output _81,
  output _105,
  output _85,
  output _82,
  output _32,
  output _46,
  output _3_HPLA_IN,
  output _1_HPLA_IN,
  output _2_HPLA_IN
);

  wire _243_out, _245_out, _246_out, _247_out, _248_out, _261_out, _262_out, _263_out, _266_out, _267_out,
       _268_out, _269_out, _270_out, _272_out, _276_out, _277_out, _281_2_out, _281_out, _282_2_out,
       _282_out, _285_2_out, _285_out, _286_2_out, _286_out, _287_2_out, _287_out, _288_out, _290_out,
       _292_out, _293_out, _294_out, _295_out, _296_out, _309_out, _310_out, _311_out, _312_out, _313_out,
       d_ff_1_q, d_ff_2_qn, d_ff_3_q, d_ff_3_qn, d_latch_1_out_4, d_latch_2_out_4, d_latch_3_out_4,
       d_latch_4_out_4, d_latch_5_out_4, d_latch_6_out_4, d_latch_7_out_4, d_latch_8_out_4, d_latch_9_out_4,
       d_latch_10_out_4, d_latch_11_out_4, d_latch_12_out_4, d_latch_13_out_4, d_latch_14_out_4,
       d_latch_15_out_4, d_latch_16_out_4, d_latch_17_out_4, d_latch_18_out_4, d_latch_19_out_4,
       d_latch_20_out_4, d_latch_21_out_4, d_latch_22_out_4, d_latch_23_out_4, d_latch_24_out_4,
       d_latch_25_out_4, d_latch_26_out_4, d_latch_27_out_4, d_latch_28_out_4, d_latch_29_out_4,
       d_latch_30_out_4, d_latch_31_out_4, d_latch_32_out_4, d_latch_33_out_4, d_latch_34_out_4,
       d_latch_35_out_4, d_latch_36_out_4, d_latch_37_out_4, d_latch_38_out_4, d_latch_39_out_4,
       d_latch_40_out_4, d_latch_41_out_4, d_latch_42_out_4, d_latch_43_out_4, d_latch_44_out_4,
       d_latch_45_out_4, d_latch_46_out_4, d_latch_47_out_4, d_latch_48_out_4, d_latch_49_out_4,
       d_latch_50_out_4, d_latch_51_out_4, d_latch_52_out_4, d_latch_53_out_4, d_latch_54_out_4,
       d_latch_58_out_4, d_latch_61_out_4, d_latch_62_out_4, d_latch_63_out_4, d_latch_64_out_4,
       d_latch_65_out_4, d_latch_66_out_4, d_latch_67_out_4, d_latch_68_out_4, d_latch_69_out_4,
       d_latch_71_out_4, d_latch_72_out_4, d_latch_73_out_4, d_latch_74_out_4, d_latch_75_out_4,
       d_latch_82_out_4, d_latch_83_out_4, d_latch_84_out_4, d_latch_85_out_4, d_latch_86_out_4,
       d_latch_87_out_4, d_latch_88_out_4, d_latch_89_out_4, d_latch_90_out_4, d_latch_91_out_4,
       d_latch_92_out_4, d_latch_93_out_4, d_latch_94_out_4, d_latch_95_out_4, d_latch_96_out_4,
       d_latch_97_out_4, d_latch_98_out_4, d_latch_99_out_4, d_latch_100_out_4, d_latch_101_out_4,
       d_latch_102_out_4, d_latch_103_out_4, d_latch_104_out_4, d_latch_105_out_4, d_latch_106_out_4,
       d_latch_107_out_4, d_latch_108_out_4, d_latch_109_out_4, d_latch_110_out_4, d_latch_111_out_4,
       d_latch_112_out_4, d_latch_113_out_4, d_latch_114_out_4, d_latch_115_out_4, d_latch_116_out_4,
       d_latch_117_out_4, d_latch_118_out_4, d_latch_119_out_4, d_latch_120_out_4, d_latch_121_out_4,
       d_latch_122_out_4, d_latch_123_out_4, d_latch_124_out_4, d_latch_125_out_4, d_latch_126_out_4,
       d_latch_127_out_4, d_latch_128_out_4, d_latch_129_out_4, d_latch_130_out_4, d_latch_131_out_4,
       d_latch_132_out_4, d_latch_133_out_4, d_latch_134_out_4, d_latch_135_out_4, d_latch_136_out_4,
       d_latch_137_out_4, d_latch_138_out_4, d_latch_139_out_4, d_latch_140_out_4, d_latch_141_out_4,
       d_latch_142_out_4, d_latch_143_out_4, d_latch_144_out_4, d_latch_145_out_4, d_latch_146_out_4,
       d_latch_147_out_4, d_latch_148_out_4, d_latch_149_out_4, d_latch_150_out_4, d_latch_151_out_4,
       d_latch_152_out_4, multiplexer_1_out, multiplexer_2_out, multiplexer_4_out, multiplexer_5_out,
       multiplexer_6_out, nor_1_out, not_1_out, not_2_out, not_3_out, not_4_out, not_5_out, not_6_out,
       not_9_out, not_10_out, not_11_out, not_12_out, not_13_out, not_14_out, not_15_out, not_16_out,
       not_23_out, not_24_out, not_25_out, s_r_ff_1_q, s_r_ff_2_q, s_r_ff_3_q, s_r_ff_4_q, s_r_ff_5_q,
       xor_1_out;

  and _248 (_248_out, _74, _73);
  nor _309 (_309_out, _73, _72, _74);
  not not_1 (not_1_out, _111);
  not not_2 (not_2_out, not_1_out);
  not not_3 (not_3_out, _128);
  not not_4 (not_4_out, not_3_out);
  and _254 (_1_HPLA_IN, _107__54, not_5_out);
  not not_5 (not_5_out, _103);
  not not_6 (not_6_out, _114);
  D_Latch d_latch_1 (.in_1(CLK1), .in_2(_266_out), .out_4(d_latch_1_out_4));  // open: out_3
  and _276 (_276_out, _87, _1_HPLA_IN);
  and _256 (_2_HPLA_IN, _1_HPLA_IN, not_6_out);
  D_Latch d_latch_2 (.in_1(CLK2), .in_2(d_latch_1_out_4), .out_4(d_latch_2_out_4));  // open: out_3
  nor nor_1 (nor_1_out, HPLA_23, HPLA_24, HPLA_25, HPLA_26, HPLA_27, HPLA_35, HPLA_28, HPLA_29, HPLA_36, HPLA_33, HPLA_30);
  D_Latch d_latch_3 (.in_1(CLK1), .in_2(HPLA_3), .out_4(d_latch_3_out_4));  // open: out_3
  D_Latch d_latch_4 (.in_1(CLK1), .in_2(HPLA_4), .out_4(d_latch_4_out_4));  // open: out_3
  D_Latch d_latch_5 (.in_1(CLK1), .in_2(HPLA_5), .out_4(d_latch_5_out_4));  // open: out_3
  D_Latch d_latch_6 (.in_1(CLK1), .in_2(HPLA_6), .out_4(d_latch_6_out_4));  // open: out_3
  D_Latch d_latch_7 (.in_1(CLK1), .in_2(HPLA_7), .out_4(d_latch_7_out_4));  // open: out_3
  D_Latch d_latch_8 (.in_1(CLK1), .in_2(HPLA_8), .out_4(d_latch_8_out_4));  // open: out_3
  D_Latch d_latch_9 (.in_1(CLK1), .in_2(HPLA_9), .out_4(d_latch_9_out_4));  // open: out_3
  D_Latch d_latch_10 (.in_1(CLK1), .in_2(HPLA_10), .out_4(d_latch_10_out_4));  // open: out_3
  D_Latch d_latch_11 (.in_1(CLK1), .in_2(HPLA_11), .out_4(d_latch_11_out_4));  // open: out_3
  D_Latch d_latch_12 (.in_1(CLK1), .in_2(_296_out), .out_4(d_latch_12_out_4));  // open: out_3
  D_Latch d_latch_13 (.in_1(CLK1), .in_2(d_latch_2_out_4), .out_4(d_latch_13_out_4));  // open: out_3
  D_Latch d_latch_14 (.in_1(CLK1), .in_2(_288_out), .out_4(d_latch_14_out_4));  // open: out_3
  D_Latch d_latch_15 (.in_1(CLK1), .in_2(HPLA_0), .out_4(d_latch_15_out_4));  // open: out_3
  D_Latch d_latch_16 (.in_1(CLK1), .in_2(HPLA_1), .out_4(d_latch_16_out_4));  // open: out_3
  D_Latch d_latch_17 (.in_1(CLK1), .in_2(HPLA_2), .out_4(d_latch_17_out_4));  // open: out_3
  D_Latch d_latch_18 (.in_1(CLK1), .in_2(HPLA_12), .out_4(d_latch_18_out_4));  // open: out_3
  D_Latch d_latch_19 (.in_1(CLK1), .in_2(HPLA_13), .out_4(d_latch_19_out_4));  // open: out_3
  D_Latch d_latch_20 (.in_1(CLK1), .in_2(HPLA_14), .out_4(d_latch_20_out_4));  // open: out_3
  D_Latch d_latch_21 (.in_1(CLK1), .in_2(HPLA_15), .out_4(d_latch_21_out_4));  // open: out_3
  D_Latch d_latch_22 (.in_1(CLK1), .in_2(HPLA_16), .out_4(d_latch_22_out_4));  // open: out_3
  D_Latch d_latch_23 (.in_1(CLK1), .in_2(HPLA_17), .out_4(d_latch_23_out_4));  // open: out_3
  D_Latch d_latch_24 (.in_1(CLK1), .in_2(HPLA_18), .out_4(d_latch_24_out_4));  // open: out_3
  D_Latch d_latch_25 (.in_1(CLK1), .in_2(HPLA_19), .out_4(d_latch_25_out_4));  // open: out_3
  D_Latch d_latch_26 (.in_1(CLK1), .in_2(HPLA_21), .out_4(d_latch_26_out_4));  // open: out_3
  D_Latch d_latch_27 (.in_1(CLK1), .in_2(HPLA_22), .out_4(d_latch_27_out_4));  // open: out_3
  D_Latch d_latch_28 (.in_1(CLK1), .in_2(HPLA_20), .out_4(d_latch_28_out_4));  // open: out_3
  D_Latch d_latch_29 (.in_1(CLK1), .in_2(HPLA_32), .out_4(d_latch_29_out_4));  // open: out_3
  D_Latch d_latch_30 (.in_1(CLK1), .in_2(HPLA_23), .out_4(d_latch_30_out_4));  // open: out_3
  D_Latch d_latch_31 (.in_1(CLK1), .in_2(HPLA_24), .out_4(d_latch_31_out_4));  // open: out_3
  D_Latch d_latch_32 (.in_1(CLK1), .in_2(HPLA_25), .out_4(d_latch_32_out_4));  // open: out_3
  D_Latch d_latch_33 (.in_1(CLK1), .in_2(HPLA_26), .out_4(d_latch_33_out_4));  // open: out_3
  D_Latch d_latch_34 (.in_1(CLK1), .in_2(HPLA_27), .out_4(d_latch_34_out_4));  // open: out_3
  D_Latch d_latch_35 (.in_1(CLK1), .in_2(HPLA_35), .out_4(d_latch_35_out_4));  // open: out_3
  D_Latch d_latch_36 (.in_1(CLK1), .in_2(HPLA_28), .out_4(d_latch_36_out_4));  // open: out_3
  D_Latch d_latch_37 (.in_1(CLK1), .in_2(HPLA_29), .out_4(d_latch_37_out_4));  // open: out_3
  D_Latch d_latch_38 (.in_1(CLK1), .in_2(HPLA_31), .out_4(d_latch_38_out_4));  // open: out_3
  D_Latch d_latch_39 (.in_1(CLK1), .in_2(HPLA_34), .out_4(d_latch_39_out_4));  // open: out_3
  D_Latch d_latch_40 (.in_1(CLK1), .in_2(HPLA_36), .out_4(d_latch_40_out_4));  // open: out_3
  D_Latch d_latch_41 (.in_1(CLK1), .in_2(nor_1_out), .out_4(d_latch_41_out_4));  // open: out_3
  D_Latch d_latch_42 (.in_1(CLK1), .in_2(_276_out), .out_4(d_latch_42_out_4));  // open: out_3
  D_Latch d_latch_43 (.in_1(CLK2), .in_2(d_latch_3_out_4), .out_4(d_latch_43_out_4));  // open: out_3
  D_Latch d_latch_44 (.in_1(CLK2), .in_2(d_latch_4_out_4), .out_4(d_latch_44_out_4));  // open: out_3
  D_Latch d_latch_45 (.in_1(CLK2), .in_2(d_latch_5_out_4), .out_4(d_latch_45_out_4));  // open: out_3
  D_Latch d_latch_46 (.in_1(CLK2), .in_2(d_latch_6_out_4), .out_4(d_latch_46_out_4));  // open: out_3
  D_Latch d_latch_47 (.in_1(CLK2), .in_2(d_latch_7_out_4), .out_4(d_latch_47_out_4));  // open: out_3
  D_Latch d_latch_48 (.in_1(CLK2), .in_2(d_latch_8_out_4), .out_4(d_latch_48_out_4));  // open: out_3
  D_Latch d_latch_49 (.in_1(CLK2), .in_2(d_latch_9_out_4), .out_4(d_latch_49_out_4));  // open: out_3
  D_Latch d_latch_50 (.in_1(CLK2), .in_2(d_latch_10_out_4), .out_4(d_latch_50_out_4));  // open: out_3
  D_Latch d_latch_51 (.in_1(CLK2), .in_2(d_latch_11_out_4), .out_4(d_latch_51_out_4));  // open: out_3
  D_Latch d_latch_52 (.in_1(CLK2), .in_2(d_latch_12_out_4), .out_4(d_latch_52_out_4));  // open: out_3
  D_Flip_Flop d_ff_1 (.clk(CLK2), .D(nHSYNC_IN), .Q(d_ff_1_q));  // open: Qn, preset, en, reset
  D_Latch d_latch_53 (.in_1(CLK2), .in_2(d_latch_13_out_4), .out_4(d_latch_53_out_4));  // open: out_3
  D_Latch d_latch_54 (.in_1(CLK2), .in_2(d_latch_14_out_4), .out_4(d_latch_54_out_4));  // open: out_3
  D_Latch d_latch_55 (.in_1(CLK2), .in_2(d_latch_15_out_4), .out_4(N307));  // open: out_3
  D_Latch d_latch_56 (.in_1(CLK2), .in_2(d_latch_16_out_4), .out_4(_52));  // open: out_3
  D_Latch d_latch_57 (.in_1(CLK2), .in_2(d_latch_17_out_4), .out_4(_68));  // open: out_3
  D_Latch d_latch_58 (.in_1(CLK2), .in_2(d_latch_18_out_4), .out_4(d_latch_58_out_4));  // open: out_3
  not not_7 (_49, d_latch_58_out_4);
  D_Latch d_latch_59 (.in_1(CLK2), .in_2(d_latch_19_out_4), .out_4(_43));  // open: out_3
  D_Latch d_latch_60 (.in_1(CLK2), .in_2(d_latch_20_out_4), .out_4(_44));  // open: out_3
  D_Latch d_latch_61 (.in_1(CLK2), .in_2(d_latch_21_out_4), .out_4(d_latch_61_out_4));  // open: out_3
  D_Latch d_latch_62 (.in_1(CLK2), .in_2(d_latch_22_out_4), .out_4(d_latch_62_out_4));  // open: out_3
  D_Latch d_latch_63 (.in_1(CLK2), .in_2(d_latch_23_out_4), .out_4(d_latch_63_out_4));  // open: out_3
  D_Latch d_latch_64 (.in_1(CLK2), .in_2(d_latch_24_out_4), .out_4(d_latch_64_out_4));  // open: out_3
  D_Latch d_latch_65 (.in_1(CLK2), .in_2(d_latch_25_out_4), .out_4(d_latch_65_out_4));  // open: out_3
  D_Latch d_latch_66 (.in_1(CLK2), .in_2(d_latch_26_out_4), .out_4(d_latch_66_out_4));  // open: out_3
  D_Latch d_latch_67 (.in_1(CLK2), .in_2(d_latch_27_out_4), .out_4(d_latch_67_out_4));  // open: out_3
  D_Latch d_latch_68 (.in_1(CLK2), .in_2(d_latch_28_out_4), .out_4(d_latch_68_out_4));  // open: out_3
  D_Latch d_latch_69 (.in_1(CLK2), .in_2(d_latch_29_out_4), .out_4(d_latch_69_out_4));  // open: out_3
  D_Latch d_latch_70 (.in_1(CLK2), .in_2(d_latch_30_out_4), .out_4(_37));  // open: out_3
  D_Latch d_latch_71 (.in_1(CLK2), .in_2(d_latch_31_out_4), .out_4(d_latch_71_out_4));  // open: out_3
  D_Latch d_latch_72 (.in_1(CLK2), .in_2(d_latch_32_out_4), .out_4(d_latch_72_out_4));  // open: out_3
  D_Latch d_latch_73 (.in_1(CLK2), .in_2(d_latch_33_out_4), .out_4(d_latch_73_out_4));  // open: out_3
  D_Latch d_latch_74 (.in_1(CLK2), .in_2(d_latch_34_out_4), .out_4(d_latch_74_out_4));  // open: out_3
  D_Latch d_latch_75 (.in_1(CLK2), .in_2(d_latch_35_out_4), .out_4(d_latch_75_out_4));  // open: out_3
  D_Latch d_latch_76 (.in_1(CLK2), .in_2(d_latch_36_out_4), .out_4(_70));  // open: out_3
  D_Latch d_latch_77 (.in_1(CLK2), .in_2(d_latch_37_out_4), .out_4(_81));  // open: out_3
  D_Latch d_latch_78 (.in_1(CLK2), .in_2(d_latch_38_out_4), .out_4(_105));  // open: out_3
  D_Latch d_latch_79 (.in_1(CLK2), .in_2(d_latch_39_out_4), .out_4(_85));  // open: out_3
  D_Latch d_latch_80 (.in_1(CLK2), .in_2(d_latch_40_out_4), .out_4(_82));  // open: out_3
  D_Latch d_latch_81 (.in_1(CLK2), .in_2(d_latch_41_out_4), .out_4(_32));  // open: out_3
  D_Latch d_latch_82 (.in_1(CLK2), .in_2(d_latch_42_out_4), .out_4(d_latch_82_out_4));  // open: out_3
  or _267 (_267_out, d_latch_44_out_4, d_latch_47_out_4);
  or _269 (_269_out, d_latch_48_out_4, d_latch_50_out_4);
  or _274 (_3_HPLA_IN, d_latch_82_out_4, _276_out);
  or _272 (_272_out, d_latch_44_out_4, SYSRES);
  or _270 (_270_out, d_latch_45_out_4, SYSRES);
  or _268 (_268_out, SYSRES, _269_out);
  or _263 (_263_out, _269_out, SYSRES);
  or _277 (_277_out, SYSRES, d_latch_50_out_4);
  not not_8 (_40, d_latch_61_out_4);
  not not_9 (not_9_out, d_latch_61_out_4);
  Multiplexer #(.disabled(0), .enable("false")) multiplexer_1 (
    .in0(not_9_out), .in1(d_latch_62_out_4), .out(multiplexer_1_out), .sel(_26));
  or _264 (_90_2, d_latch_65_out_4, d_latch_68_out_4);
  or _265 (_100, d_latch_68_out_4, d_latch_69_out_4);
  or _313 (_313_out, _93, _86, _98);
  not not_10 (not_10_out, _98);
  not not_11 (not_11_out, _86);
  not not_12 (not_12_out, _93);
  D_Latch d_latch_83 (.in_1(CLK1), .in_2(_3_HPLA_IN), .out_4(d_latch_83_out_4));  // open: out_3
  S_R_Flip_Flop s_r_ff_1 (.Q(s_r_ff_1_q), .preset(d_latch_43_out_4), .reset(_272_out));  // open: S, clk, R, Qn, en
  S_R_Flip_Flop s_r_ff_2 (.Q(s_r_ff_2_q), .preset(_270_out), .reset(d_latch_46_out_4));  // open: S, clk, R, Qn, en
  S_R_Flip_Flop s_r_ff_3 (.Q(s_r_ff_3_q), .preset(_267_out), .reset(_268_out));  // open: S, clk, R, Qn, en
  S_R_Flip_Flop s_r_ff_4 (.Q(s_r_ff_4_q), .preset(_263_out), .reset(d_latch_49_out_4));  // open: S, clk, R, Qn, en
  S_R_Flip_Flop s_r_ff_5 (.Q(s_r_ff_5_q), .preset(_277_out), .reset(d_latch_51_out_4));  // open: S, clk, R, Qn, en
  xor _288 (_288_out, nVSYNC_1, d_latch_52_out_4);
  not not_13 (not_13_out, d_latch_54_out_4);
  D_Latch d_latch_84 (.in_1(CLK2), .in_2(d_latch_83_out_4), .out_4(d_latch_84_out_4));  // open: out_3
  and _262 (_262_out, _288_out, not_13_out);
  and _290 (_290_out, not_10_out, _86, not_12_out);
  and _292 (_292_out, not_11_out, not_10_out, _93);
  and _293 (_293_out, not_10_out, _86, _93);
  and _294 (_294_out, not_11_out, d_latch_68_out_4, not_12_out);
  and _295 (_295_out, not_12_out, _98, _86);
  not not_14 (not_14_out, d_latch_84_out_4);
  not not_15 (not_15_out, _309_out);
  and _250 (_58, multiplexer_1_out, _313_out);
  and _435 (_66, d_latch_63_out_4, _313_out);
  and _275 (_75, d_latch_64_out_4, _313_out);
  and _255 (_104, _313_out, d_latch_66_out_4);
  and _257 (_116, _313_out, d_latch_67_out_4);
  and _281 (_281_out, d_latch_71_out_4, _313_out);
  and _282 (_282_out, _313_out, d_latch_72_out_4);
  and _285 (_285_out, _313_out, d_latch_73_out_4);
  and _286 (_286_out, _313_out, d_latch_74_out_4);
  and _287 (_287_out, _313_out, d_latch_75_out_4);
  nand _312 (_312_out, HPLA_30, not_14_out);
  and _306 (_61, _60, _62, s_r_ff_1_q);
  and _252 (_63, s_r_ff_1_q, _69);
  and _247 (_247_out, s_r_ff_3_q, _72);
  and _245 (_245_out, _248_out, s_r_ff_4_q);
  and _246 (_246_out, s_r_ff_4_q, not_15_out);
  and _243 (_243_out, _309_out, s_r_ff_5_q);
  and _261 (_261_out, M5, _112);
  xor xor_1 (xor_1_out, _262_out, d_ff_3_qn);
  not not_16 (not_16_out, SYSRES);
  nor _281_2 (_281_2_out, _281_out, _290_out);
  nor _282_2 (_282_2_out, _282_out, _292_out);
  nor _285_2 (_285_2_out, _285_out, _293_out);
  nor _286_2 (_286_2_out, _286_out, _294_out);
  nor _287_2 (_287_2_out, _287_out, _295_out);
  D_Latch d_latch_85 (.in_1(CLK1), .in_2(_312_out), .out_4(d_latch_85_out_4));  // open: out_3
  D_Latch d_latch_86 (.in_1(CLK1), .in_2(s_r_ff_2_q), .out_4(d_latch_86_out_4));  // open: out_3
  D_Flip_Flop #(.trigger("high")) d_ff_2 (
    .clk(CLK1), .D(xor_1_out), .Qn(d_ff_2_qn), .en(not_16_out));  // open: Q, preset, reset
  not not_17 (_39, _281_2_out);
  not not_18 (_45, _282_2_out);
  not not_19 (_55, _285_2_out);
  not not_20 (_67, _286_2_out);
  not not_21 (_94, _287_2_out);
  D_Latch d_latch_87 (.in_1(CLK2), .in_2(d_latch_85_out_4), .out_4(d_latch_87_out_4));  // open: out_3
  D_Latch d_latch_88 (.in_1(CLK2), .in_2(d_latch_86_out_4), .out_4(d_latch_88_out_4));  // open: out_3
  D_Flip_Flop #(.trigger("high")) d_ff_3 (
    .clk(CLK2), .D(d_ff_2_qn), .Q(d_ff_3_q), .Qn(d_ff_3_qn));  // open: preset, en, reset
  assign D_OUT[7] = not_4_out ? ~_44 : 1'bz;  // Controlled_Inverter controlled_inverter_1
  assign D_OUT[6] = not_4_out ? ~_40 : 1'bz;  // Controlled_Inverter controlled_inverter_2
  assign D_OUT[5] = not_4_out ? ~_58 : 1'bz;  // Controlled_Inverter controlled_inverter_3
  assign D_OUT[4] = not_4_out ? ~_66 : 1'bz;  // Controlled_Inverter controlled_inverter_4
  assign D_OUT[3] = not_4_out ? ~_75 : 1'bz;  // Controlled_Inverter controlled_inverter_5
  assign D_OUT[2] = not_4_out ? ~_90_2 : 1'bz;  // Controlled_Inverter controlled_inverter_6
  assign D_OUT[1] = not_4_out ? ~_104 : 1'bz;  // Controlled_Inverter controlled_inverter_7
  assign D_OUT[0] = not_4_out ? ~_116 : 1'bz;  // Controlled_Inverter controlled_inverter_8
  not not_22 (_46, d_latch_87_out_4);
  D_Latch d_latch_89 (.in_1(CLK1), .in_2(d_latch_88_out_4), .out_4(d_latch_89_out_4));  // open: out_3
  or _296 (_296_out, _247_out, _245_out, _243_out);
  or _266 (_266_out, _246_out, _243_out);
  D_Latch d_latch_90 (.in_1(CLK1), .in_2(nVSYNC_1), .out_4(d_latch_90_out_4));  // open: out_3
  D_Latch d_latch_91 (.in_1(CLK1), .in_2(_288_out), .out_4(d_latch_91_out_4));  // open: out_3
  D_Latch d_latch_92 (.in_1(CLK2), .in_2(d_latch_89_out_4), .out_4(d_latch_92_out_4));  // open: out_3
  D_Latch d_latch_93 (.in_1(CLK2), .in_2(d_latch_90_out_4), .out_4(d_latch_93_out_4));  // open: out_3
  D_Latch d_latch_94 (.in_1(CLK2), .in_2(d_latch_91_out_4), .out_4(d_latch_94_out_4));  // open: out_3
  Multiplexer #(.disabled(0), .enable("false")) multiplexer_2 (
    .in0(d_latch_53_out_4), .in1(d_ff_3_q), .out(multiplexer_2_out), .sel(_261_out));
  assign D_OUT[12] = not_2_out ? ~_100 : 1'bz;  // Controlled_Inverter controlled_inverter_9
  assign D_OUT[1] = not_2_out ? ~_37 : 1'bz;  // Controlled_Inverter controlled_inverter_10
  assign D_OUT[2] = not_2_out ? ~_39 : 1'bz;  // Controlled_Inverter controlled_inverter_11
  assign D_OUT[3] = not_2_out ? ~_45 : 1'bz;  // Controlled_Inverter controlled_inverter_12
  assign D_OUT[4] = not_2_out ? ~_55 : 1'bz;  // Controlled_Inverter controlled_inverter_13
  assign D_OUT[5] = not_2_out ? ~_67 : 1'bz;  // Controlled_Inverter controlled_inverter_14
  assign D_OUT[11] = not_2_out ? ~_94 : 1'bz;  // Controlled_Inverter controlled_inverter_15
  assign D_OUT[7] = not_2_out ? ~_70 : 1'bz;  // Controlled_Inverter controlled_inverter_16
  assign D_OUT[8] = not_2_out ? ~_81 : 1'bz;  // Controlled_Inverter controlled_inverter_17
  assign D_OUT[13] = not_2_out ? ~_105 : 1'bz;  // Controlled_Inverter controlled_inverter_18
  assign D_OUT[10] = not_2_out ? ~_85 : 1'bz;  // Controlled_Inverter controlled_inverter_19
  assign D_OUT[9] = not_2_out ? ~_82 : 1'bz;  // Controlled_Inverter controlled_inverter_20
  assign D_OUT[0] = not_2_out ? ~_32 : 1'bz;  // Controlled_Inverter controlled_inverter_21
  assign D_OUT[6] = not_2_out ? ~_46 : 1'bz;  // Controlled_Inverter controlled_inverter_22
  D_Latch d_latch_95 (.in_1(CLK1), .in_2(d_latch_92_out_4), .out_4(d_latch_95_out_4));  // open: out_3
  D_Latch d_latch_96 (.in_1(CLK1), .in_2(d_latch_93_out_4), .out_4(d_latch_96_out_4));  // open: out_3
  D_Latch d_latch_97 (.in_1(CLK1), .in_2(d_latch_94_out_4), .out_4(d_latch_97_out_4));  // open: out_3
  D_Latch d_latch_98 (.in_1(CLK1), .in_2(multiplexer_2_out), .out_4(d_latch_98_out_4));  // open: out_3
  D_Latch d_latch_99 (.in_1(CLK2), .in_2(d_latch_95_out_4), .out_4(d_latch_99_out_4));  // open: out_3
  D_Latch d_latch_100 (.in_1(CLK2), .in_2(d_latch_96_out_4), .out_4(d_latch_100_out_4));  // open: out_3
  D_Latch d_latch_101 (.in_1(CLK2), .in_2(d_latch_97_out_4), .out_4(d_latch_101_out_4));  // open: out_3
  D_Latch d_latch_102 (.in_1(CLK2), .in_2(d_latch_98_out_4), .out_4(d_latch_102_out_4));  // open: out_3
  D_Latch d_latch_103 (.in_1(CLK1), .in_2(d_latch_99_out_4), .out_4(d_latch_103_out_4));  // open: out_3
  D_Latch d_latch_104 (.in_1(CLK1), .in_2(d_latch_100_out_4), .out_4(d_latch_104_out_4));  // open: out_3
  D_Latch d_latch_105 (.in_1(CLK1), .in_2(d_latch_101_out_4), .out_4(d_latch_105_out_4));  // open: out_3
  D_Latch d_latch_106 (.in_1(CLK1), .in_2(d_latch_102_out_4), .out_4(d_latch_106_out_4));  // open: out_3
  D_Latch d_latch_107 (.in_1(CLK2), .in_2(d_latch_103_out_4), .out_4(d_latch_107_out_4));  // open: out_3
  D_Latch d_latch_108 (.in_1(CLK2), .in_2(d_latch_104_out_4), .out_4(d_latch_108_out_4));  // open: out_3
  D_Latch d_latch_109 (.in_1(CLK2), .in_2(d_latch_105_out_4), .out_4(d_latch_109_out_4));  // open: out_3
  D_Latch d_latch_110 (.in_1(CLK2), .in_2(d_latch_106_out_4), .out_4(d_latch_110_out_4));  // open: out_3
  D_Latch d_latch_111 (.in_1(CLK1), .in_2(d_latch_107_out_4), .out_4(d_latch_111_out_4));  // open: out_3
  D_Latch d_latch_112 (.in_1(CLK1), .in_2(d_latch_108_out_4), .out_4(d_latch_112_out_4));  // open: out_3
  D_Latch d_latch_113 (.in_1(CLK1), .in_2(d_latch_109_out_4), .out_4(d_latch_113_out_4));  // open: out_3
  D_Latch d_latch_114 (.in_1(CLK1), .in_2(d_latch_110_out_4), .out_4(d_latch_114_out_4));  // open: out_3
  D_Latch d_latch_115 (.in_1(CLK2), .in_2(d_latch_111_out_4), .out_4(d_latch_115_out_4));  // open: out_3
  D_Latch d_latch_116 (.in_1(CLK2), .in_2(d_latch_112_out_4), .out_4(d_latch_116_out_4));  // open: out_3
  D_Latch d_latch_117 (.in_1(CLK2), .in_2(d_latch_113_out_4), .out_4(d_latch_117_out_4));  // open: out_3
  D_Latch d_latch_118 (.in_1(CLK2), .in_2(d_latch_114_out_4), .out_4(d_latch_118_out_4));  // open: out_3
  D_Latch d_latch_119 (.in_1(CLK1), .in_2(d_latch_115_out_4), .out_4(d_latch_119_out_4));  // open: out_3
  D_Latch d_latch_120 (.in_1(CLK1), .in_2(d_latch_116_out_4), .out_4(d_latch_120_out_4));  // open: out_3
  D_Latch d_latch_121 (.in_1(CLK1), .in_2(d_latch_117_out_4), .out_4(d_latch_121_out_4));  // open: out_3
  D_Latch d_latch_122 (.in_1(CLK1), .in_2(d_latch_118_out_4), .out_4(d_latch_122_out_4));  // open: out_3
  D_Latch d_latch_123 (.in_1(CLK2), .in_2(d_latch_119_out_4), .out_4(d_latch_123_out_4));  // open: out_3
  D_Latch d_latch_124 (.in_1(CLK2), .in_2(d_latch_120_out_4), .out_4(d_latch_124_out_4));  // open: out_3
  D_Latch d_latch_125 (.in_1(CLK2), .in_2(d_latch_121_out_4), .out_4(d_latch_125_out_4));  // open: out_3
  D_Latch d_latch_126 (.in_1(CLK2), .in_2(d_latch_122_out_4), .out_4(d_latch_126_out_4));  // open: out_3
  D_Latch d_latch_127 (.in_1(CLK1), .in_2(d_latch_123_out_4), .out_4(d_latch_127_out_4));  // open: out_3
  D_Latch d_latch_128 (.in_1(CLK1), .in_2(d_latch_124_out_4), .out_4(d_latch_128_out_4));  // open: out_3
  D_Latch d_latch_129 (.in_1(CLK1), .in_2(d_latch_125_out_4), .out_4(d_latch_129_out_4));  // open: out_3
  D_Latch d_latch_130 (.in_1(CLK1), .in_2(d_latch_126_out_4), .out_4(d_latch_130_out_4));  // open: out_3
  D_Latch d_latch_131 (.in_1(CLK2), .in_2(d_latch_127_out_4), .out_4(d_latch_131_out_4));  // open: out_3
  D_Latch d_latch_132 (.in_1(CLK2), .in_2(d_latch_128_out_4), .out_4(d_latch_132_out_4));  // open: out_3
  D_Latch d_latch_133 (.in_1(CLK2), .in_2(d_latch_129_out_4), .out_4(d_latch_133_out_4));  // open: out_3
  D_Latch d_latch_134 (.in_1(CLK2), .in_2(d_latch_130_out_4), .out_4(d_latch_134_out_4));  // open: out_3
  D_Latch d_latch_135 (.in_1(CLK1), .in_2(d_latch_131_out_4), .out_4(d_latch_135_out_4));  // open: out_3
  D_Latch d_latch_136 (.in_1(CLK1), .in_2(d_latch_132_out_4), .out_4(d_latch_136_out_4));  // open: out_3
  D_Latch d_latch_137 (.in_1(CLK1), .in_2(d_latch_133_out_4), .out_4(d_latch_137_out_4));  // open: out_3
  D_Latch d_latch_138 (.in_1(CLK1), .in_2(d_latch_134_out_4), .out_4(d_latch_138_out_4));  // open: out_3
  D_Latch d_latch_139 (.in_1(CLK2), .in_2(d_latch_135_out_4), .out_4(d_latch_139_out_4));  // open: out_3
  D_Latch d_latch_140 (.in_1(CLK2), .in_2(d_latch_136_out_4), .out_4(d_latch_140_out_4));  // open: out_3
  D_Latch d_latch_141 (.in_1(CLK2), .in_2(d_latch_137_out_4), .out_4(d_latch_141_out_4));  // open: out_3
  D_Latch d_latch_142 (.in_1(CLK2), .in_2(d_latch_138_out_4), .out_4(d_latch_142_out_4));  // open: out_3
  D_Latch d_latch_143 (.in_1(CLK1), .in_2(d_latch_139_out_4), .out_4(d_latch_143_out_4));  // open: out_3
  D_Latch d_latch_144 (.in_1(CLK1), .in_2(d_latch_140_out_4), .out_4(d_latch_144_out_4));  // open: out_3
  D_Latch d_latch_145 (.in_1(CLK1), .in_2(d_latch_141_out_4), .out_4(d_latch_145_out_4));  // open: out_3
  D_Latch d_latch_146 (.in_1(CLK1), .in_2(d_latch_142_out_4), .out_4(d_latch_146_out_4));  // open: out_3
  D_Latch d_latch_147 (.in_1(CLK2), .in_2(d_latch_143_out_4), .out_4(d_latch_147_out_4));  // open: out_3
  D_Latch d_latch_148 (.in_1(CLK2), .in_2(d_latch_144_out_4), .out_4(d_latch_148_out_4));  // open: out_3
  D_Latch d_latch_149 (.in_1(CLK2), .in_2(d_latch_145_out_4), .out_4(d_latch_149_out_4));  // open: out_3
  D_Latch d_latch_150 (.in_1(CLK2), .in_2(d_latch_146_out_4), .out_4(d_latch_150_out_4));  // open: out_3
  Multiplexer #(.disabled(0), .enable("false")) multiplexer_3 (
    .in0(d_latch_88_out_4), .in1(d_latch_147_out_4), .out(_113), .sel(M5));
  Multiplexer #(.disabled(0), .enable("false")) multiplexer_4 (
    .in0(nVSYNC_1), .in1(d_latch_148_out_4), .out(multiplexer_4_out), .sel(M5));
  Multiplexer #(.disabled(0), .enable("false")) multiplexer_5 (
    .in0(_288_out), .in1(d_latch_149_out_4), .out(multiplexer_5_out), .sel(M5));
  Multiplexer #(.disabled(0), .enable("false")) multiplexer_6 (
    .in0(multiplexer_2_out), .in1(d_latch_150_out_4), .out(multiplexer_6_out), .sel(M5));
  not not_23 (not_23_out, multiplexer_4_out);
  not not_24 (not_24_out, _107__54);
  not not_25 (not_25_out, _90);
  Multiplexer #(.disabled(0), .enable("false")) multiplexer_7 (
    .in0(not_23_out), .in1(CLK2), .out(VSYNC_OUT), .sel(_48));
  nand _311 (_311_out, multiplexer_5_out, not_24_out);
  and _253 (_96, d_ff_1_q, _90);
  nand _310 (_310_out, not_25_out, multiplexer_6_out);
  D_Latch d_latch_151 (.in_1(CLK1), .in_2(_311_out), .out_4(d_latch_151_out_4));  // open: out_3
  D_Latch d_latch_152 (.in_1(CLK1), .in_2(_310_out), .out_4(d_latch_152_out_4));  // open: out_3
  D_Latch d_latch_153 (.in_1(CLK2), .in_2(d_latch_151_out_4), .out_4(nCSYNC_OUT));  // open: out_3
  D_Latch d_latch_154 (.in_1(CLK2), .in_2(d_latch_152_out_4), .out_4(nHSYNC_OUT));  // open: out_3

  // Notes on the sheet:
  //   34
  //   144
  //   145
  //   29, 38, 144, 152,127
  //   103
  //   279
  //   278
  //   434,308,300,291
  //   89
  //   96
  //   102
  //   106
  //   105
  //   101
  //   95
  //   88
  //   76
  //   104
  //   110
  //   111
  //   66
  //   74
  //   77
  //   75
  //   65
  //   68
  //   72
  //   79
  //   86
  //   93
  //   99
  //   107
  //   112
  //   100
  //   108
  //   69
  //   71
  //   70
  //   80
  //   81
  //   97
  //   85
  //   92
  //   109
  //   98
  //   91
  //   67
  //   94
  //   240
  //   102
  //   POSEDGE DFF
  //   178
  //   95
  //   115
  //   122
  //   123
  //   174
  //   143
  //   141
  //   142
  //   87
  //   183
  //   182
  //   180
  //   181
  //   184
  //   106
  //   140
  //   128
  //   169
  //   243,244
  //   241
  //   CIN
  //   /EN
  //   84
  //   90
  //   AOI21
  //   114
  //   AOI21
  //   124
  //   AOI21
  //   127
  //   AOI21
  //   133
  //   AOI21
  //   139
  //   179
  //   CNT_BIT
  //   188
  //   189
  //   194
  //   197
  //   200
  //   201
  //   206
  //   207
  //   167
  //   166
  //   204
  //   186
  //   190
  //   191
  //   193
  //   192
  //   203
  //   195
  //   199
  //   205
  //   202
  //   198
  //   187
  //   196
  //   319
  //   322
  //   321
  //   320
  //   146
  //   164
  //   113
  //   227
  //   113
  //   228
  //   113
  //   172
  //   227
  //   126
  //   137
  //   125
  //   175
  //   82
  //   83
endmodule

// HV COUNTER
module HV_COUNTER (
  input  CLK1,
  input  CLK2,
  input  CIN,
  input  RES,
  input  LOAD,
  input  [8:0] VAL,
  output [8:0] CNT_OUT
);

  wire d_ff_1_qn, d_ff_2_qn, d_ff_3_qn, d_ff_4_qn, d_ff_5_qn, d_ff_6_qn, d_ff_7_qn, d_ff_8_qn, d_ff_9_qn,
       d_ff_10_qn, d_ff_11_qn, d_ff_12_qn, d_ff_13_qn, d_ff_14_qn, d_ff_15_qn, d_ff_16_qn, d_ff_17_qn,
       d_ff_18_qn, demultiplexer_1_out0, demultiplexer_1_out1, demultiplexer_2_out0, demultiplexer_2_out1,
       demultiplexer_3_out0, demultiplexer_3_out1, demultiplexer_4_out0, demultiplexer_4_out1,
       demultiplexer_5_out0, demultiplexer_5_out1, demultiplexer_6_out0, demultiplexer_6_out1,
       demultiplexer_7_out0, demultiplexer_7_out1, demultiplexer_8_out0, demultiplexer_8_out1,
       demultiplexer_9_out0, demultiplexer_9_out1, nor_1_out, nor_2_out, nor_3_out, nor_4_out, nor_5_out,
       nor_6_out, nor_7_out, nor_8_out, nor_9_out, not_1_out, not_2_out, not_3_out, not_4_out, not_5_out,
       not_6_out, not_7_out, not_8_out, not_9_out, or_1_out, or_2_out, or_3_out, or_4_out, or_5_out,
       or_6_out, or_7_out, or_8_out, or_9_out, xor_1_out, xor_2_out, xor_3_out, xor_4_out, xor_5_out,
       xor_6_out, xor_7_out, xor_8_out, xor_9_out;

  Demultiplexer #(.enable("false")) demultiplexer_1 (
    .out0(demultiplexer_1_out0), .out1(demultiplexer_1_out1), .in(LOAD), .sel(VAL[0]));
  Demultiplexer #(.enable("false")) demultiplexer_2 (
    .out0(demultiplexer_2_out0), .out1(demultiplexer_2_out1), .in(LOAD), .sel(VAL[1]));
  Demultiplexer #(.enable("false")) demultiplexer_3 (
    .out0(demultiplexer_3_out0), .out1(demultiplexer_3_out1), .in(LOAD), .sel(VAL[2]));
  Demultiplexer #(.enable("false")) demultiplexer_4 (
    .out0(demultiplexer_4_out0), .out1(demultiplexer_4_out1), .in(LOAD), .sel(VAL[3]));
  Demultiplexer #(.enable("false")) demultiplexer_5 (
    .out0(demultiplexer_5_out0), .out1(demultiplexer_5_out1), .in(LOAD), .sel(VAL[4]));
  Demultiplexer #(.enable("false")) demultiplexer_6 (
    .out0(demultiplexer_6_out0), .out1(demultiplexer_6_out1), .in(LOAD), .sel(VAL[5]));
  Demultiplexer #(.enable("false")) demultiplexer_7 (
    .out0(demultiplexer_7_out0), .out1(demultiplexer_7_out1), .in(LOAD), .sel(VAL[6]));
  Demultiplexer #(.enable("false")) demultiplexer_8 (
    .out0(demultiplexer_8_out0), .out1(demultiplexer_8_out1), .in(LOAD), .sel(VAL[7]));
  Demultiplexer #(.enable("false")) demultiplexer_9 (
    .out0(demultiplexer_9_out0), .out1(demultiplexer_9_out1), .in(LOAD), .sel(VAL[8]));
  or or_1 (or_1_out, RES, demultiplexer_1_out0);
  or or_2 (or_2_out, RES, demultiplexer_2_out0);
  or or_3 (or_3_out, RES, demultiplexer_3_out0);
  or or_4 (or_4_out, RES, demultiplexer_4_out0);
  or or_5 (or_5_out, RES, demultiplexer_5_out0);
  or or_6 (or_6_out, RES, demultiplexer_6_out0);
  or or_7 (or_7_out, RES, demultiplexer_7_out0);
  or or_8 (or_8_out, RES, demultiplexer_8_out0);
  or or_9 (or_9_out, RES, demultiplexer_9_out0);
  D_Flip_Flop #(.trigger("high")) d_ff_1 (
    .clk(CLK2), .D(d_ff_10_qn), .Q(CNT_OUT[0]), .Qn(d_ff_1_qn), .preset(demultiplexer_1_out1),
    .reset(or_1_out));  // open: en
  D_Flip_Flop #(.trigger("high")) d_ff_2 (
    .clk(CLK2), .D(d_ff_11_qn), .Q(CNT_OUT[1]), .Qn(d_ff_2_qn), .preset(demultiplexer_2_out1),
    .reset(or_2_out));  // open: en
  D_Flip_Flop #(.trigger("high")) d_ff_3 (
    .clk(CLK2), .D(d_ff_12_qn), .Q(CNT_OUT[2]), .Qn(d_ff_3_qn), .preset(demultiplexer_3_out1),
    .reset(or_3_out));  // open: en
  D_Flip_Flop #(.trigger("high")) d_ff_4 (
    .clk(CLK2), .D(d_ff_13_qn), .Q(CNT_OUT[3]), .Qn(d_ff_4_qn), .preset(demultiplexer_4_out1),
    .reset(or_4_out));  // open: en
  D_Flip_Flop #(.trigger("high")) d_ff_5 (
    .clk(CLK2), .D(d_ff_14_qn), .Q(CNT_OUT[4]), .Qn(d_ff_5_qn), .preset(demultiplexer_5_out1),
    .reset(or_5_out));  // open: en
  D_Flip_Flop #(.trigger("high")) d_ff_6 (
    .clk(CLK2), .D(d_ff_15_qn), .Q(CNT_OUT[5]), .Qn(d_ff_6_qn), .preset(demultiplexer_6_out1),
    .reset(or_6_out));  // open: en
  D_Flip_Flop #(.trigger("high")) d_ff_7 (
    .clk(CLK2), .D(d_ff_16_qn), .Q(CNT_OUT[6]), .Qn(d_ff_7_qn), .preset(demultiplexer_7_out1),
    .reset(or_7_out));  // open: en
  D_Flip_Flop #(.trigger("high")) d_ff_8 (
    .clk(CLK2), .D(d_ff_17_qn), .Q(CNT_OUT[7]), .Qn(d_ff_8_qn), .preset(demultiplexer_8_out1),
    .reset(or_8_out));  // open: en
  D_Flip_Flop #(.trigger("high")) d_ff_9 (
    .clk(CLK2), .D(d_ff_18_qn), .Q(CNT_OUT[8]), .Qn(d_ff_9_qn), .preset(demultiplexer_9_out1),
    .reset(or_9_out));  // open: en
  xor xor_1 (xor_1_out, CIN, d_ff_1_qn);
  not not_1 (not_1_out, CIN);
  nor nor_1 (nor_1_out, not_1_out, d_ff_1_qn);
  xor xor_2 (xor_2_out, nor_1_out, d_ff_2_qn);
  not not_2 (not_2_out, nor_1_out);
  nor nor_2 (nor_2_out, not_2_out, d_ff_2_qn);
  xor xor_3 (xor_3_out, nor_2_out, d_ff_3_qn);
  not not_3 (not_3_out, nor_2_out);
  nor nor_3 (nor_3_out, not_3_out, d_ff_3_qn);
  xor xor_4 (xor_4_out, nor_3_out, d_ff_4_qn);
  not not_4 (not_4_out, nor_3_out);
  nor nor_4 (nor_4_out, not_4_out, d_ff_4_qn);
  xor xor_5 (xor_5_out, nor_4_out, d_ff_5_qn);
  not not_5 (not_5_out, nor_4_out);
  nor nor_5 (nor_5_out, not_5_out, d_ff_5_qn);
  xor xor_6 (xor_6_out, nor_5_out, d_ff_6_qn);
  not not_6 (not_6_out, nor_5_out);
  nor nor_6 (nor_6_out, not_6_out, d_ff_6_qn);
  xor xor_7 (xor_7_out, nor_6_out, d_ff_7_qn);
  not not_7 (not_7_out, nor_6_out);
  nor nor_7 (nor_7_out, not_7_out, d_ff_7_qn);
  xor xor_8 (xor_8_out, nor_7_out, d_ff_8_qn);
  not not_8 (not_8_out, nor_7_out);
  nor nor_8 (nor_8_out, not_8_out, d_ff_8_qn);
  xor xor_9 (xor_9_out, nor_8_out, d_ff_9_qn);
  not not_9 (not_9_out, nor_8_out);
  nor nor_9 (nor_9_out, not_9_out, d_ff_9_qn);
  D_Flip_Flop #(.trigger("high")) d_ff_10 (.clk(CLK1), .D(xor_1_out), .Qn(d_ff_10_qn));  // open: Q, preset, en, reset
  D_Flip_Flop #(.trigger("high")) d_ff_11 (.clk(CLK1), .D(xor_2_out), .Qn(d_ff_11_qn));  // open: Q, preset, en, reset
  D_Flip_Flop #(.trigger("high")) d_ff_12 (.clk(CLK1), .D(xor_3_out), .Qn(d_ff_12_qn));  // open: Q, preset, en, reset
  D_Flip_Flop #(.trigger("high")) d_ff_13 (.clk(CLK1), .D(xor_4_out), .Qn(d_ff_13_qn));  // open: Q, preset, en, reset
  D_Flip_Flop #(.trigger("high")) d_ff_14 (.clk(CLK1), .D(xor_5_out), .Qn(d_ff_14_qn));  // open: Q, preset, en, reset
  D_Flip_Flop #(.trigger("high")) d_ff_15 (.clk(CLK1), .D(xor_6_out), .Qn(d_ff_15_qn));  // open: Q, preset, en, reset
  D_Flip_Flop #(.trigger("high")) d_ff_16 (.clk(CLK1), .D(xor_7_out), .Qn(d_ff_16_qn));  // open: Q, preset, en, reset
  D_Flip_Flop #(.trigger("high")) d_ff_17 (.clk(CLK1), .D(xor_8_out), .Qn(d_ff_17_qn));  // open: Q, preset, en, reset
  D_Flip_Flop #(.trigger("high")) d_ff_18 (.clk(CLK1), .D(xor_9_out), .Qn(d_ff_18_qn));  // open: Q, preset, en, reset
endmodule

module VRAM_ADDR_CRTL (
  input  in_1,
  input  [7:0] in_2,
  output RA7,
  output RA6,
  output RA5,
  output RA4,
  output RA3,
  output RA2,
  output RA1,
  output RA0,
  output [22:0] CPU_ADDR
);

  wire _1234_2_out, _1234_3_out, _1234_out, _1235_2_out, _1235_3_out, _1235_out, _1236_2_out, _1236_3_out,
       _1236_out, _1237_2_out, _1237_3_out, _1237_out, _1238_2_out, _1238_3_out, _1238_out, _1239_2_out,
       _1239_3_out, _1239_out, _1240_2_out, _1240_3_out, _1240_out, _1241_2_out, _1241_3_out, _1241_out,
       _1242_2_out, _1242_3_out, _1242_4_out, _1242_out, _1252_out, _1254_out, _1255_out, d_latch_1_out_3,
       d_latch_2_out_3, d_latch_3_out_3, d_latch_4_out_3, d_latch_5_out_3, d_latch_6_out_3, d_latch_7_out_3,
       d_latch_8_out_3, d_latch_9_out_3, not_1_out, not_2_out, not_3_out, not_4_out, not_5_out, undriven,
       undriven_2, undriven_3, undriven_4;

  D_Latch d_latch_1 (.in_1(in_1), .in_2(undriven), .out_3(d_latch_1_out_3));  // open: out_4
  D_Latch d_latch_2 (.in_1(in_1), .in_2(in_2[7]), .out_3(d_latch_2_out_3));  // open: out_4
  D_Latch d_latch_3 (.in_1(in_1), .in_2(in_2[6]), .out_3(d_latch_3_out_3));  // open: out_4
  D_Latch d_latch_4 (.in_1(in_1), .in_2(in_2[5]), .out_3(d_latch_4_out_3));  // open: out_4
  D_Latch d_latch_5 (.in_1(in_1), .in_2(in_2[4]), .out_3(d_latch_5_out_3));  // open: out_4
  D_Latch d_latch_6 (.in_1(in_1), .in_2(in_2[3]), .out_3(d_latch_6_out_3));  // open: out_4
  D_Latch d_latch_7 (.in_1(in_1), .in_2(in_2[2]), .out_3(d_latch_7_out_3));  // open: out_4
  D_Latch d_latch_8 (.in_1(in_1), .in_2(in_2[1]), .out_3(d_latch_8_out_3));  // open: out_4
  D_Latch d_latch_9 (.in_1(in_1), .in_2(in_2[0]), .out_3(d_latch_9_out_3));  // open: out_4
  // OR_Gate _1252 has open pins: out=_1252_out
  not not_1 (not_1_out, d_latch_1_out_3);
  not not_2 (not_2_out, _1252_out);
  nand _1254 (_1254_out, not_1_out, _1252_out);
  nand _1255 (_1255_out, not_1_out, not_2_out);
  not not_3 (not_3_out, not_1_out);
  not not_4 (not_4_out, _1254_out);
  not not_5 (not_5_out, _1255_out);
  and _1234 (_1234_out, CPU_ADDR[7], not_3_out);
  and _1234_2 (_1234_2_out, CPU_ADDR[15], not_4_out);
  and _1234_3 (_1234_3_out, d_latch_2_out_3, not_5_out);
  and _1235 (_1235_out, CPU_ADDR[6], not_3_out);
  and _1235_2 (_1235_2_out, CPU_ADDR[13], not_4_out);
  and _1235_3 (_1235_3_out, d_latch_3_out_3, not_5_out);
  and _1236 (_1236_out, CPU_ADDR[5], not_3_out);
  and _1236_2 (_1236_2_out, CPU_ADDR[12], not_4_out);
  and _1236_3 (_1236_3_out, d_latch_4_out_3, not_5_out);
  and _1237 (_1237_out, CPU_ADDR[4], not_3_out);
  and _1237_2 (_1237_2_out, CPU_ADDR[11], not_4_out);
  and _1237_3 (_1237_3_out, d_latch_5_out_3, not_5_out);
  and _1238 (_1238_out, CPU_ADDR[3], not_3_out);
  and _1238_2 (_1238_2_out, CPU_ADDR[10], not_4_out);
  and _1238_3 (_1238_3_out, d_latch_6_out_3, not_5_out);
  and _1239 (_1239_out, CPU_ADDR[2], not_3_out);
  and _1239_2 (_1239_2_out, CPU_ADDR[9], not_4_out);
  and _1239_3 (_1239_3_out, d_latch_7_out_3, not_5_out);
  and _1240 (_1240_out, CPU_ADDR[1], not_3_out);
  and _1240_2 (_1240_2_out, CPU_ADDR[8], not_4_out);
  and _1240_3 (_1240_3_out, d_latch_8_out_3, not_5_out);
  and _1241 (_1241_out, CPU_ADDR[0], not_3_out);
  and _1241_2 (_1241_2_out, CPU_ADDR[14], not_4_out);
  and _1241_3 (_1241_3_out, d_latch_9_out_3, not_5_out);
  and _1242 (_1242_out, undriven_2, not_3_out);
  and _1242_2 (_1242_2_out, undriven_3, not_4_out);
  and _1242_3 (_1242_3_out, undriven_4, not_5_out);
  or _1234_4 (RA7, _1234_out, _1234_2_out, _1234_3_out);
  or _1235_4 (RA6, _1235_out, _1235_2_out, _1235_3_out);
  or _1236_4 (RA5, _1236_out, _1236_2_out, _1236_3_out);
  or _1237_4 (RA4, _1237_out, _1237_2_out, _1237_3_out);
  or _1238_4 (RA3, _1238_out, _1238_2_out, _1238_3_out);
  or _1239_4 (RA2, _1239_out, _1239_2_out, _1239_3_out);
  or _1240_4 (RA1, _1240_out, _1240_2_out, _1240_3_out);
  or _1241_4 (RA0, _1241_out, _1241_2_out, _1241_3_out);
  or _1242_4 (_1242_4_out, _1242_out, _1242_2_out, _1242_3_out);

  // Notes on the sheet:
  //   1263
  //   1300
  //   1299
  //   1298
  //   1297
  //   1296
  //   1295
  //   1294
  //   1293
  //   1227
  //   1226
  //   1231
  //   1232
  //   1233
endmodule

module DMA (
  input  RCLK1,
  input  RCLK2,
  input  SYSRES,
  input  [7:0] DB,
  input  M5
);

  wire _558_out, _559_out, _562_out, _625_qn, _628_out, _629_out, _660_q, _660_qn, _663_out, _668_out,
       _702_out, _731_out, _736_out, _763_q, _770_out, _798_q, _805_out, _833_q, _840_out, _868_q, _875_out,
       _891_out, _893_out, _894_out, _895_out, _896_out, _898_out, _899_out, _902_out, _904_out, _905_out,
       _906_2_out, _906_out, _907_2_out, _907_out, _908_2_out, _908_out, _909_2_out, _909_out, _910_2_out,
       _910_out, _912_out, _921_out, _923_out, _925_out, _927_out, _929_out, _931_out, _934_out, _936_out,
       _937_out, _938_out, _940_out, _942_2_out, _942_out, _944_out, _945_out, _946_out, _948_out, _950_out,
       _952_out, _954_out, _963_out, _964_out, _965_out, _970_2_out, _970_out, _1011_2_out, _1011_out,
       _1012_2_out, _1012_out, _1013_q, _1014_q, _1015_q, _1016_q, _1017_q, _1018_q, _1022_out, _1023_out,
       _1025_q, _1027_q, _1028_2_out, _1028_out, _1029_2_out, _1029_out, _1031_q, _1034_q, _1037_q, _1040_q,
       _1048_q, _1049_q, _1052_q, _1097_out, _1150_out, _1551_q, adder_1_cout, and_1_out, and_2_out,
       and_3_out, and_4_out, and_5_out, and_6_out, and_7_out, and_8_out, and_9_out, and_10_out, CA0, CA1,
       CA2, CA3, CA4, CA5, CA6, CA7, CA8, CA9, CA10, CA11, CA12, CA13, CA14, CA15, CA16, CA17, CA18, CA19,
       CA20, CA21, CA22, CA_DIR, dma_8bit_cnt_1_co, dma_8bit_cnt_2_co, dma_8bit_cnt_3_co, dma_8bit_cnt_4_co,
       G1019, G1020, G1021, LD0, LD1, LD2, LD3, LD4, LD5, LD6, LD7, LD8, LD9, LD10, LD11, LD12, LD13, LD14,
       LD15, LD16, LD17, LD18, LD19, LD20, LD21, LD22, multiplexer_2_out, multiplexer_3_out,
       multiplexer_4_out, multiplexer_5_out, multiplexer_6_out, multiplexer_7_out, multiplexer_8_out,
       multiplexer_9_out, multiplexer_10_out, nM5, not_3_out, not_4_out, not_5_out, not_6_out, not_7_out,
       undriven, undriven_2, undriven_3, undriven_4, undriven_5, undriven_6, undriven_7, undriven_8,
       undriven_9, undriven_10, undriven_11, undriven_12, undriven_13, undriven_14, undriven_15, undriven_16,
       undriven_17, undriven_18, undriven_19, xor_1_out, xor_2_out, xor_3_out, xor_4_out, xor_5_out,
       xor_6_out, xor_7_out, xor_8_out, xor_9_out;
  wire [7:0] _993_q, _995_q, _996_q, adder_1_out, controlled_buffer_5_out, controlled_buffer_7_out,
       dma_8bit_cnt_1_cnt_out, dma_8bit_cnt_2_cnt_out, dma_8bit_cnt_3_cnt_out, dma_8bit_cnt_4_cnt_out,
       multiplexer_1_out, not_1_out, not_2_out;

  not _1011 (_1011_out, LD5);
  // AND_Gate _1150 has open pins: out=_1150_out
  not _970 (_970_out, _1150_out);
  not _1024 (nM5, M5);
  not _1011_2 (_1011_2_out, _1011_out);
  not _970_2 (_970_2_out, _970_out);
  D_Flip_Flop #(.trigger("high")) _996 (
    .clk(_1011_2_out), .D(_995_q[0]), .Q(_996_q[0]));  // open: Qn, preset, en, reset
  D_Flip_Flop #(.trigger("high")) _998 (
    .clk(_1011_2_out), .D(_995_q[1]), .Q(_996_q[1]));  // open: Qn, preset, en, reset
  D_Flip_Flop #(.trigger("high")) _1000 (
    .clk(_1011_2_out), .D(_995_q[2]), .Q(_996_q[2]));  // open: Qn, preset, en, reset
  D_Flip_Flop #(.trigger("high")) _1002 (
    .clk(_1011_2_out), .D(_995_q[3]), .Q(_996_q[3]));  // open: Qn, preset, en, reset
  D_Flip_Flop #(.trigger("high")) _1004 (
    .clk(_1011_2_out), .D(_995_q[4]), .Q(_996_q[4]));  // open: Qn, preset, en, reset
  D_Flip_Flop #(.trigger("high")) _1006 (
    .clk(_1011_2_out), .D(_995_q[5]), .Q(_996_q[5]));  // open: Qn, preset, en, reset
  D_Flip_Flop #(.trigger("high")) _1008 (
    .clk(_1011_2_out), .D(_995_q[6]), .Q(_996_q[6]));  // open: Qn, preset, en, reset
  D_Flip_Flop #(.trigger("high")) _1010 (
    .clk(_1011_2_out), .D(_995_q[7]), .Q(_996_q[7]));  // open: Qn, preset, en, reset
  D_Flip_Flop #(.trigger("high")) _993 (.clk(_970_2_out), .D(DB[0]), .Q(_993_q[0]));  // open: Qn, preset, en, reset
  D_Flip_Flop #(.trigger("high")) _991 (.clk(_970_2_out), .D(DB[1]), .Q(_993_q[1]));  // open: Qn, preset, en, reset
  D_Flip_Flop #(.trigger("high")) _989 (.clk(_970_2_out), .D(DB[2]), .Q(_993_q[2]));  // open: Qn, preset, en, reset
  D_Flip_Flop #(.trigger("high")) _987 (.clk(_970_2_out), .D(DB[3]), .Q(_993_q[3]));  // open: Qn, preset, en, reset
  D_Flip_Flop #(.trigger("high")) _985 (.clk(_970_2_out), .D(DB[4]), .Q(_993_q[4]));  // open: Qn, preset, en, reset
  D_Flip_Flop #(.trigger("high")) _983 (.clk(_970_2_out), .D(DB[5]), .Q(_993_q[5]));  // open: Qn, preset, en, reset
  D_Flip_Flop #(.trigger("high")) _981 (.clk(_970_2_out), .D(DB[6]), .Q(_993_q[6]));  // open: Qn, preset, en, reset
  D_Flip_Flop #(.trigger("high")) _979 (.clk(_970_2_out), .D(DB[7]), .Q(_993_q[7]));  // open: Qn, preset, en, reset
  not _1012 (_1012_out, undriven);
  not _1012_2 (_1012_2_out, _1012_out);
  Adder adder_1 (.a(_995_q), .b(_996_q), .out(adder_1_out), .cin(nM5), .cout(adder_1_cout));
  xor xor_1 (xor_1_out, G1021, adder_1_cout);
  and and_1 (and_1_out, adder_1_cout, G1021);
  xor xor_2 (xor_2_out, G1020, and_1_out);
  and and_2 (and_2_out, and_1_out, G1020);
  xor xor_3 (xor_3_out, G1019, and_2_out);
  and and_3 (and_3_out, and_2_out, G1019);
  xor xor_4 (xor_4_out, _1018_q, and_3_out);
  and and_4 (and_4_out, and_3_out, _1018_q);
  xor xor_5 (xor_5_out, _1017_q, and_4_out);
  and and_5 (and_5_out, and_4_out, _1017_q);
  xor xor_6 (xor_6_out, _1016_q, and_5_out);
  and and_6 (and_6_out, and_5_out, _1016_q);
  xor xor_7 (xor_7_out, _1015_q, and_6_out);
  and and_7 (and_7_out, and_6_out, _1015_q);
  xor xor_8 (xor_8_out, _1014_q, and_7_out);
  and and_8 (and_8_out, and_7_out, _1014_q);
  xor xor_9 (xor_9_out, _1013_q, and_8_out);
  and and_9 (and_9_out, and_8_out, _1013_q);
  Multiplexer #(.width(8), .disabled(0), .enable("false")) multiplexer_1 (
    .in0(adder_1_out), .in1(_993_q), .out(multiplexer_1_out), .sel(_1012_2_out));
  not _1028 (_1028_out, undriven_11);
  not _1028_2 (_1028_2_out, _1028_out);
  // OR_Gate _1097 has open pins: out=_1097_out
  not _1029 (_1029_out, undriven_12);
  not _1029_2 (_1029_2_out, _1029_out);
  D_Flip_Flop #(.trigger("high")) _1027 (
    .clk(_1028_2_out), .D(undriven_2), .Q(_1027_q));  // open: Qn, preset, en, reset
  D_Flip_Flop #(.trigger("high")) _1025 (
    .clk(_1028_2_out), .D(undriven_3), .Q(_1025_q));  // open: Qn, preset, en, reset
  D_Flip_Flop #(.trigger("high")) _1031 (
    .clk(_1028_2_out), .D(undriven_4), .Q(_1031_q));  // open: Qn, preset, en, reset
  D_Flip_Flop #(.trigger("high")) _1034 (
    .clk(_1028_2_out), .D(undriven_5), .Q(_1034_q));  // open: Qn, preset, en, reset
  D_Flip_Flop #(.trigger("high")) _1037 (
    .clk(_1028_2_out), .D(undriven_6), .Q(_1037_q));  // open: Qn, preset, en, reset
  D_Flip_Flop #(.trigger("high")) _1040 (
    .clk(_1028_2_out), .D(undriven_7), .Q(_1040_q));  // open: Qn, preset, en, reset
  D_Flip_Flop #(.trigger("high")) _1048 (
    .clk(_1028_2_out), .D(undriven_8), .Q(_1048_q), .reset(_1023_out));  // open: Qn, preset, en
  D_Flip_Flop #(.trigger("high")) _1049 (
    .clk(_1028_2_out), .D(undriven_9), .Q(_1049_q), .reset(_1023_out));  // open: Qn, preset, en
  D_Flip_Flop #(.trigger("high")) _1052 (
    .clk(_1028_2_out), .D(undriven_10), .Q(_1052_q), .reset(_1023_out));  // open: Qn, preset, en
  not _1022 (_1022_out, _1097_out);
  Multiplexer #(.disabled(0), .enable("false")) multiplexer_2 (
    .in0(xor_1_out), .in1(_1027_q), .out(multiplexer_2_out), .sel(_1029_2_out));
  Multiplexer #(.disabled(0), .enable("false")) multiplexer_3 (
    .in0(xor_2_out), .in1(_1025_q), .out(multiplexer_3_out), .sel(_1029_2_out));
  Multiplexer #(.disabled(0), .enable("false")) multiplexer_4 (
    .in0(xor_3_out), .in1(_1031_q), .out(multiplexer_4_out), .sel(_1029_2_out));
  Multiplexer #(.disabled(0), .enable("false")) multiplexer_5 (
    .in0(xor_4_out), .in1(_1034_q), .out(multiplexer_5_out), .sel(_1029_2_out));
  Multiplexer #(.disabled(0), .enable("false")) multiplexer_6 (
    .in0(xor_5_out), .in1(_1037_q), .out(multiplexer_6_out), .sel(_1029_2_out));
  Multiplexer #(.disabled(0), .enable("false")) multiplexer_7 (
    .in0(xor_6_out), .in1(_1040_q), .out(multiplexer_7_out), .sel(_1029_2_out));
  Multiplexer #(.disabled(0), .enable("false")) multiplexer_8 (
    .in0(xor_7_out), .in1(_1048_q), .out(multiplexer_8_out), .sel(_1029_2_out));
  Multiplexer #(.disabled(0), .enable("false")) multiplexer_9 (
    .in0(xor_8_out), .in1(_1049_q), .out(multiplexer_9_out), .sel(_1029_2_out));
  Multiplexer #(.disabled(0), .enable("false")) multiplexer_10 (
    .in0(xor_9_out), .in1(_1052_q), .out(multiplexer_10_out), .sel(_1029_2_out));
  D_Flip_Flop _995 (.clk(_1022_out), .D(multiplexer_1_out[0]), .Q(_995_q[0]), .reset(SYSRES));  // open: Qn, preset, en
  D_Flip_Flop _997 (.clk(_1022_out), .D(multiplexer_1_out[1]), .Q(_995_q[1]), .reset(SYSRES));  // open: Qn, preset, en
  D_Flip_Flop _999 (.clk(_1022_out), .D(multiplexer_1_out[2]), .Q(_995_q[2]), .reset(SYSRES));  // open: Qn, preset, en
  D_Flip_Flop _1001 (.clk(_1022_out), .D(multiplexer_1_out[3]), .Q(_995_q[3]), .reset(SYSRES));  // open: Qn, preset, en
  D_Flip_Flop _1003 (.clk(_1022_out), .D(multiplexer_1_out[4]), .Q(_995_q[4]), .reset(SYSRES));  // open: Qn, preset, en
  D_Flip_Flop _1005 (.clk(_1022_out), .D(multiplexer_1_out[5]), .Q(_995_q[5]), .reset(SYSRES));  // open: Qn, preset, en
  D_Flip_Flop _1007 (.clk(_1022_out), .D(multiplexer_1_out[6]), .Q(_995_q[6]), .reset(SYSRES));  // open: Qn, preset, en
  D_Flip_Flop _1009 (.clk(_1022_out), .D(multiplexer_1_out[7]), .Q(_995_q[7]), .reset(SYSRES));  // open: Qn, preset, en
  D_Flip_Flop _1021 (.clk(_1022_out), .D(multiplexer_2_out), .Q(G1021), .reset(SYSRES));  // open: Qn, preset, en
  D_Flip_Flop _1020 (.clk(_1022_out), .D(multiplexer_3_out), .Q(G1020), .reset(SYSRES));  // open: Qn, preset, en
  D_Flip_Flop _1019 (.clk(_1022_out), .D(multiplexer_4_out), .Q(G1019), .reset(SYSRES));  // open: Qn, preset, en
  D_Flip_Flop _1018 (.clk(_1022_out), .D(multiplexer_5_out), .Q(_1018_q), .reset(SYSRES));  // open: Qn, preset, en
  D_Flip_Flop _1017 (.clk(_1022_out), .D(multiplexer_6_out), .Q(_1017_q), .reset(SYSRES));  // open: Qn, preset, en
  D_Flip_Flop _1016 (.clk(_1022_out), .D(multiplexer_7_out), .Q(_1016_q), .reset(SYSRES));  // open: Qn, preset, en
  D_Flip_Flop _1015 (.clk(_1022_out), .D(multiplexer_8_out), .Q(_1015_q), .reset(_1023_out));  // open: Qn, preset, en
  D_Flip_Flop _1014 (.clk(_1022_out), .D(multiplexer_9_out), .Q(_1014_q), .reset(_1023_out));  // open: Qn, preset, en
  D_Flip_Flop _1013 (.clk(_1022_out), .D(multiplexer_10_out), .Q(_1013_q), .reset(_1023_out));  // open: Qn, preset, en
  or _1023 (_1023_out, SYSRES, nM5);
  // AND_Gate _954 has open pins: out=_954_out
  // AND_Gate _905 has open pins: out=_905_out
  // OR_Gate _562 has open pins: out=_562_out
  not _896 (_896_out, undriven_13);
  not _910 (_910_out, LD0);
  not _910_2 (_910_2_out, _910_out);
  assign not_1_out = ~_995_q;  // NOT_Gate not_1, 8 bits wide
  not _909 (_909_out, LD1);
  not _909_2 (_909_2_out, _909_out);
  assign not_2_out = ~_995_q;  // NOT_Gate not_2, 8 bits wide
  not _908 (_908_out, LD2);
  not _908_2 (_908_2_out, _908_out);
  not _907 (_907_out, _907_2_out);
  not _907_2 (_907_2_out, LD3);
  not _906 (_906_out, LD4);
  and _912 (_912_out, _562_out, _896_out);
  DMA_8bit_CNT dma_8bit_cnt_1 (
    .CLK1(RCLK1), .CLK2(RCLK2), .CIN(_912_out), .RES(1'b0), .LOAD(_910_2_out), .VAL(not_1_out),
    .CNT_OUT(dma_8bit_cnt_1_cnt_out), .CO(dma_8bit_cnt_1_co));
  DMA_8bit_CNT dma_8bit_cnt_2 (
    .CLK1(RCLK1), .CLK2(RCLK2), .CIN(_559_out), .RES(1'b0), .LOAD(_909_2_out), .VAL(not_2_out),
    .CNT_OUT(dma_8bit_cnt_2_cnt_out), .CO(dma_8bit_cnt_2_co));
  DMA_8bit_CNT dma_8bit_cnt_3 (
    .CLK1(RCLK1), .CLK2(RCLK2), .CIN(_912_out), .RES(1'b0), .LOAD(_908_2_out), .VAL(_995_q),
    .CNT_OUT(dma_8bit_cnt_3_cnt_out), .CO(dma_8bit_cnt_3_co));
  DMA_8bit_CNT dma_8bit_cnt_4 (
    .CLK1(RCLK1), .CLK2(RCLK2), .CIN(_558_out), .RES(1'b0), .LOAD(_907_out), .VAL(_995_q),
    .CNT_OUT(dma_8bit_cnt_4_cnt_out), .CO(dma_8bit_cnt_4_co));
  not _906_2 (_906_2_out, _906_out);
  not _965 (_965_out, G1021);
  not _963 (_963_out, G1020);
  not _964 (_964_out, G1019);
  D_Flip_Flop _868 (.clk(_906_2_out), .D(_995_q[0]), .Q(_868_q));  // open: Qn, preset, en, reset
  D_Flip_Flop _833 (.clk(_906_2_out), .D(_995_q[1]), .Q(_833_q));  // open: Qn, preset, en, reset
  D_Flip_Flop _694 (.clk(_906_2_out), .D(_995_q[2]), .Q(CA18));  // open: Qn, preset, en, reset
  D_Flip_Flop _728 (.clk(_906_2_out), .D(_995_q[3]), .Q(CA19));  // open: Qn, preset, en, reset
  D_Flip_Flop _763 (.clk(_906_2_out), .D(_995_q[4]), .Q(_763_q));  // open: Qn, preset, en, reset
  D_Flip_Flop _798 (.clk(_906_2_out), .D(_995_q[5]), .Q(_798_q));  // open: Qn, preset, en, reset
  D_Flip_Flop _660 (.clk(_906_2_out), .D(_995_q[6]), .Q(_660_q), .Qn(_660_qn));  // open: preset, en, reset
  D_Flip_Flop _625 (.clk(_906_2_out), .D(_995_q[7]), .Qn(_625_qn));  // open: Q, preset, en, reset
  D_Flip_Flop _1551 (.Q(_1551_q));  // open: clk, D, Qn, preset, en, reset
  and _950 (_950_out, G1021, G1020, _964_out, _954_out);
  and _948 (_948_out, _965_out, _963_out, G1019, _954_out);
  and _902 (_902_out, G1021, _963_out, G1019, _954_out);
  and _944 (_944_out, _965_out, G1020, G1019, _954_out);
  and _904 (_904_out, G1021, G1020, G1019, _954_out);
  and _952 (_952_out, G1021, G1020, G1019, _905_out);
  and _946 (_946_out, G1021, G1020, _964_out, _905_out);
  and _942 (_942_out, _965_out, _963_out, G1019, _905_out);
  and _898 (_898_out, G1021, G1019, _963_out, _905_out);
  and _899 (_899_out, _965_out, G1019, G1020, _905_out);
  // AND_Gate _931 has open pins: out=_931_out
  // AND_Gate _929 has open pins: out=_929_out
  // AND_Gate _927 has open pins: out=_927_out
  // AND_Gate _925 has open pins: out=_925_out
  // AND_Gate _923 has open pins: out=_923_out
  // AND_Gate _921 has open pins: out=_921_out
  // AND_Gate _934 has open pins: out=_934_out
  // AND_Gate _936 has open pins: out=_936_out
  // AND_Gate _937 has open pins: out=_937_out
  // AND_Gate _938 has open pins: out=_938_out
  // AND_Gate _940 has open pins: out=_940_out
  // AND_Gate _942_2 has open pins: out=_942_2_out
  // AND_Gate _945 has open pins: out=_945_out
  not _894 (_894_out, CA_DIR);
  not not_3 (not_3_out, _894_out);
  assign CA16 = not_3_out ? _868_q : 1'bz;  // Controlled_Buffer controlled_buffer_1
  assign CA17 = not_3_out ? _833_q : 1'bz;  // Controlled_Buffer controlled_buffer_2
  assign CA20 = not_3_out ? _763_q : 1'bz;  // Controlled_Buffer controlled_buffer_3
  assign CA21 = not_3_out ? _798_q : 1'bz;  // Controlled_Buffer controlled_buffer_4
  and and_10 (and_10_out, undriven_16, undriven_17);
  or _951 (LD0, _950_out, SYSRES);
  or _949 (LD1, _948_out, SYSRES);
  or _914 (LD2, _902_out, SYSRES);
  or _945_2 (LD3, _944_out, SYSRES);
  or _913 (LD4, _904_out, SYSRES);
  or _953 (LD5, _952_out, SYSRES);
  or _947 (LD6, _946_out, SYSRES);
  or _943 (LD7, _942_out, SYSRES);
  or _919 (LD8, _898_out, SYSRES);
  or _918 (LD9, _899_out, SYSRES);
  or _932 (LD10, _931_out, SYSRES);
  or _930 (LD11, _929_out, SYSRES);
  or _928 (LD12, _927_out, SYSRES);
  or _926 (LD13, _925_out, SYSRES);
  or _924 (LD14, _923_out, SYSRES);
  or _922 (LD15, _921_out, SYSRES);
  or _920 (LD16, _934_out, SYSRES);
  or _933 (LD17, _936_out, SYSRES);
  or _935 (LD18, _937_out, SYSRES);
  or _939 (LD19, _938_out, SYSRES);
  or _941 (LD20, _940_out, SYSRES);
  or _943_2 (LD21, _942_2_out, SYSRES);
  or _944_2 (LD22, _945_out, SYSRES);
  buf _559 (_559_out, dma_8bit_cnt_1_co);  // OR_Gate
  buf _558 (_558_out, dma_8bit_cnt_3_co);  // OR_Gate
  nor nor_1 (CA22, undriven_14, undriven_15, and_10_out);
  not _895 (_895_out, dma_8bit_cnt_1_cnt_out[0]);
  nand _875 (_875_out, _562_out, _895_out, dma_8bit_cnt_1_cnt_out[1]);
  nand _805 (_805_out, dma_8bit_cnt_1_cnt_out[2], dma_8bit_cnt_1_cnt_out[3], dma_8bit_cnt_1_cnt_out[4]);
  nand _668 (_668_out, dma_8bit_cnt_1_cnt_out[5], dma_8bit_cnt_1_cnt_out[6], dma_8bit_cnt_1_cnt_out[7]);
  nand _629 (_629_out, dma_8bit_cnt_2_cnt_out[0], dma_8bit_cnt_2_cnt_out[1]);
  nand _702 (_702_out, dma_8bit_cnt_2_cnt_out[2], dma_8bit_cnt_2_cnt_out[3], dma_8bit_cnt_2_cnt_out[4]);
  nand _840 (_840_out, dma_8bit_cnt_2_cnt_out[5], dma_8bit_cnt_2_cnt_out[6], dma_8bit_cnt_2_cnt_out[7]);
  and _663 (_663_out, _660_q, _1551_q, _625_qn);
  and _628 (_628_out, _660_qn, _1551_q, _625_qn);
  nor _770 (_770_out, _875_out, _805_out, _668_out);
  nor _736 (_736_out, _629_out, _702_out, _840_out);
  not not_4 (not_4_out, undriven_18);
  assign controlled_buffer_5_out = not_4_out ? dma_8bit_cnt_3_cnt_out : 8'bz;  // Controlled_Buffer controlled_buffer_5
  not _893 (_893_out, CA_DIR);
  not not_5 (not_5_out, _893_out);
  assign {CA7, CA6, CA5, CA4, CA3, CA2, CA1, CA0} = not_5_out ? dma_8bit_cnt_3_cnt_out : 8'bz;  // Controlled_Buffer controlled_buffer_6
  not not_6 (not_6_out, undriven_19);
  assign controlled_buffer_7_out = not_6_out ? dma_8bit_cnt_4_cnt_out : 8'bz;  // Controlled_Buffer controlled_buffer_7
  not _891 (_891_out, CA_DIR);
  not not_7 (not_7_out, _891_out);
  assign {CA15, CA14, CA13, CA12, CA11, CA10, CA9, CA8} = not_7_out ? dma_8bit_cnt_4_cnt_out : 8'bz;  // Controlled_Buffer controlled_buffer_8
  or _560 (CA_DIR, _663_out, _628_out);
  and _731 (_731_out, _770_out, _736_out);

  // Notes on the sheet:
  //   8XSLATCH
  //   8XSLATCH
  //   FA
  //   1030
  //   1033
  //   1036
  //   1039
  //   1042
  //   1044
  //   1047
  //   1051
  //   1054
  //   HA
  //   HA
  //   HA
  //   HA
  //   HA
  //   HA
  //   HA
  //   HA
  //   HA
  //   994,992,990,988,986,984,982,980
  //   1026
  //   1032
  //   1035
  //   1038
  //   1041
  //   1043
  //   1046
  //   1050
  //   1053
  //   8XDFF
  //   870,835,800,765,730,696,662,627
  //   626,661,695,729,764,799,834,869
  //   874,839,804,769,735,701,667,633
  //   632,666,700,734,768,803,838,873
  //   not used
  //   872,837,802,767,733,699,665,631
  //   not used
  //   !
  //   876
  //   841
  //   771
  //   806
  //   1609
  //   2A3OI
  //   !
  //   !
  //   !
endmodule
module VID_MUX (
  input  RCLK1,
  input  RCLK2,
  input  SPA_B_IN,
  input  _38,
  input  _77,
  input  _70,
  input  _78,
  input  _85,
  input  _83,
  input  _73,
  input  _84,
  input  _87,
  input  _88,
  input  _86,
  input  _66,
  input  _65,
  input  _64,
  input  _54,
  input  _61,
  input  _62,
  input  _55,
  input  _56,
  input  _57,
  input  _58,
  input  _59,
  input  _60,
  input  _46,
  input  _45,
  input  _52,
  input  _44,
  input  _51,
  input  _43,
  input  _50,
  input  _42,
  input  _49,
  input  _41,
  input  _48,
  input  _40,
  input  _47,
  input  _72,
  input  _81,
  input  _82,
  input  _4,
  input  _17,
  input  _5,
  input  _2,
  input  _3,
  input  M5,
  input  _35,
  input  _34,
  input  _33,
  input  _32,
  input  _31,
  input  _29,
  input  _30,
  input  _28,
  input  _39,
  output _69,
  output _68,
  output _67,
  output SPA_B_OUT,
  output _79,
  output _80,
  output [5:0] out_64,
  output [15:0] DATA_OUT,
  output [8:0] out_66,
  output [16:0] B_DAC,
  output [16:0] G_DAC,
  output [16:0] R_DAC
);

  wire _176_out, _177_out, _187_2_out, _187_3_out, _187_4_out, _187_out, _188_2_out, _188_3_out, _188_4_out,
       _188_out, _189_2_out, _189_3_out, _189_4_out, _189_out, _190_2_out, _190_3_out, _190_4_out, _190_out,
       _191_2_out, _191_3_out, _191_4_out, _191_out, _192_2_out, _192_3_out, _192_4_out, _192_out, _193_out,
       _194_out, _195_out, _196_2_out, _196_3_out, _196_4_out, _196_out, _200_out, _201_out, _202_out,
       _203_out, _204_out, _205_out, _206_out, _207_out, _208_out, _209_out, _211_out, _217_out, _218_out,
       _221_out, _222_out, _223_out, _224_out, _225_out, _226_out, _227_out, _228_out, _229_out, _230_out,
       _231_out, _232_out, _233_out, _234_out, _235_out, _236_out, _237_out, _238_out, _239_out, _240_out,
       _241_out, _244_out, _245_out, _269_out, _270_out, _271_out, _272_out, _273_out, _274_out, _275_out,
       _276_out, _277_out, _278_out, _280_out, _292_out, _300_out, _301_out, _302_out, _303_out, _304_out,
       _305_out, _306_out, _307_out, _308_out, _309_out, _310_out, _311_2_out, _311_out, _312_out,
       d_latch_1_out_3, d_latch_2_out_3, d_latch_3_out_3, d_latch_4_out_3, d_latch_5_out_3, d_latch_6_out_3,
       d_latch_7_out_3, d_latch_8_out_3, d_latch_9_out_4, d_latch_10_out_4, d_latch_11_out_4,
       d_latch_12_out_4, d_latch_13_out_4, d_latch_14_out_4, d_latch_15_out_4, d_latch_16_out_4,
       d_latch_17_out_4, d_latch_18_out_4, d_latch_19_out_4, d_latch_20_out_4, d_latch_21_out_4,
       d_latch_22_out_4, d_latch_23_out_4, d_latch_24_out_4, d_latch_25_out_4, d_latch_26_out_4,
       d_latch_27_out_4, d_latch_28_out_4, d_latch_29_out_4, d_latch_30_out_4, d_latch_31_out_4,
       d_latch_32_out_4, d_latch_33_out_4, d_latch_34_out_4, d_latch_35_out_4, d_latch_36_out_4,
       d_latch_37_out_4, d_latch_38_out_4, d_latch_39_out_4, d_latch_40_out_4, d_latch_41_out_4,
       d_latch_48_out_4, d_latch_49_out_4, d_latch_50_out_4, d_latch_51_out_4, d_latch_52_out_4,
       d_latch_53_out_4, d_latch_54_out_4, d_latch_55_out_4, d_latch_56_out_4, d_latch_57_out_4,
       d_latch_58_out_4, d_latch_59_out_4, d_latch_60_out_4, d_latch_61_out_4, d_latch_62_out_4,
       d_latch_66_out_4, d_latch_67_out_4, d_latch_68_out_4, d_latch_69_out_4, d_latch_70_out_4,
       d_latch_71_out_4, d_latch_72_out_4, d_latch_73_out_4, d_latch_74_out_4, d_latch_75_out_4,
       d_latch_76_out_4, d_latch_77_out_4, d_latch_78_out_4, d_latch_79_out_4, d_latch_80_out_4,
       d_latch_81_out_4, d_latch_82_out_4, d_latch_83_out_4, d_latch_84_out_4, d_latch_85_out_4,
       d_latch_86_out_4, d_latch_87_out_4, d_latch_88_out_4, d_latch_89_out_4, d_latch_90_out_4,
       d_latch_91_out_4, d_latch_92_out_4, d_latch_93_out_4, d_latch_94_out_4, d_latch_95_out_4,
       d_latch_96_out_4, d_latch_97_out_4, d_latch_98_out_4, d_latch_99_out_4, d_latch_100_out_4,
       d_latch_101_out_4, d_latch_102_out_4, d_latch_103_out_4, d_latch_104_out_4, d_latch_105_out_4,
       d_latch_110_out_4, d_latch_111_out_4, d_latch_112_out_4, d_latch_113_out_4, d_latch_114_out_4,
       d_latch_115_out_4, d_latch_116_out_4, d_latch_117_out_4, multiplexer_7_out, multiplexer_8_out,
       multiplexer_9_out, multiplexer_10_out, multiplexer_11_out, multiplexer_12_out, multiplexer_13_out,
       multiplexer_14_out, not_1_out, not_2_out, not_3_out, not_4_out, not_5_out, not_6_out, not_7_out,
       not_8_out, not_9_out, not_10_out, not_11_out, not_12_out, not_13_out, not_14_out, not_15_out,
       not_16_out, not_17_out, not_18_out, not_19_out, not_20_out, not_21_out, not_22_out, not_23_out,
       not_24_out, not_25_out;
  wire [5:0] d_latch_42_out_4;
  wire [8:0] d_latch_63_out_4, ram_1_data;

  and _230 (_230_out, M5, _85);
  not not_1 (not_1_out, _54);
  or _224 (_224_out, _72, _81, _82);
  not not_2 (not_2_out, M5);
  not not_3 (not_3_out, M5);
  not not_4 (not_4_out, not_3_out);
  not not_5 (not_5_out, not_1_out);
  nor _312 (_312_out, _2, _3);
  Multiplexer #(.disabled(0), .enable("false")) multiplexer_1 (
    .in0(_35), .in1(_34), .out(d_latch_63_out_4[8]), .sel(not_4_out));
  Multiplexer #(.disabled(0), .enable("false")) multiplexer_2 (
    .in0(_34), .in1(_33), .out(d_latch_63_out_4[7]), .sel(not_4_out));
  Multiplexer #(.disabled(0), .enable("false")) multiplexer_3 (
    .in0(_33), .in1(_32), .out(d_latch_63_out_4[6]), .sel(not_4_out));
  Multiplexer #(.disabled(0), .enable("false")) multiplexer_4 (
    .in0(_32), .in1(_30), .out(d_latch_63_out_4[5]), .sel(not_4_out));
  Multiplexer #(.disabled(0), .enable("false")) multiplexer_5 (
    .in0(_31), .in1(_29), .out(d_latch_63_out_4[4]), .sel(not_4_out));
  Multiplexer #(.disabled(0), .enable("false")) multiplexer_6 (
    .in0(_30), .in1(_28), .out(d_latch_63_out_4[3]), .sel(not_4_out));
  D_Latch d_latch_1 (.in_1(not_5_out), .in_2(_61), .out_3(d_latch_1_out_3));  // open: out_4
  D_Latch d_latch_2 (.in_1(not_5_out), .in_2(_62), .out_3(d_latch_2_out_3));  // open: out_4
  D_Latch d_latch_3 (.in_1(not_5_out), .in_2(_55), .out_3(d_latch_3_out_3));  // open: out_4
  D_Latch d_latch_4 (.in_1(not_5_out), .in_2(_56), .out_3(d_latch_4_out_3));  // open: out_4
  D_Latch d_latch_5 (.in_1(not_5_out), .in_2(_57), .out_3(d_latch_5_out_3));  // open: out_4
  D_Latch d_latch_6 (.in_1(not_5_out), .in_2(_58), .out_3(d_latch_6_out_3));  // open: out_4
  D_Latch d_latch_7 (.in_1(not_5_out), .in_2(_59), .out_3(d_latch_7_out_3));  // open: out_4
  D_Latch d_latch_8 (.in_1(not_5_out), .in_2(_60), .out_3(d_latch_8_out_3));  // open: out_4
  not not_6 (not_6_out, _224_out);
  not not_7 (not_7_out, _194_out);
  not not_8 (not_8_out, _193_out);
  nand _193 (_193_out, M5, _224_out);
  nand _194 (_194_out, _224_out, not_2_out);
  not not_9 (not_9_out, _4);
  or _177 (_177_out, not_2_out, d_latch_7_out_3);
  and _176 (_176_out, M5, d_latch_8_out_3);
  and _187 (_187_out, _46, not_7_out);
  and _187_2 (_187_2_out, _45, not_8_out);
  and _187_3 (_187_3_out, _52, not_6_out);
  and _188 (_188_out, _45, not_7_out);
  and _188_2 (_188_2_out, _44, not_8_out);
  and _188_3 (_188_3_out, _51, not_6_out);
  and _189 (_189_out, _44, not_7_out);
  and _189_2 (_189_2_out, _43, not_8_out);
  and _189_3 (_189_3_out, _50, not_6_out);
  and _190 (_190_out, _43, not_7_out);
  and _190_2 (_190_2_out, _42, not_8_out);
  and _190_3 (_190_3_out, _49, not_6_out);
  and _191 (_191_out, _42, not_7_out);
  and _191_2 (_191_2_out, _41, not_8_out);
  and _191_3 (_191_3_out, _48, not_6_out);
  and _192 (_192_out, 1'b0, not_7_out);
  and _192_2 (_192_2_out, _40, not_8_out);
  and _192_3 (_192_3_out, _47, not_6_out);
  nor _304 (_304_out, _52, _51, _50, _49);
  or _187_4 (_187_4_out, _187_out, _187_2_out, _187_3_out);
  or _188_4 (_188_4_out, _188_out, _188_2_out, _188_3_out);
  or _189_4 (_189_4_out, _189_out, _189_2_out, _189_3_out);
  or _190_4 (_190_4_out, _190_out, _190_2_out, _190_3_out);
  or _191_4 (_191_4_out, _191_out, _191_2_out, _191_3_out);
  or _192_4 (_192_4_out, _192_out, _192_2_out, _192_3_out);
  D_Latch d_latch_9 (.in_1(RCLK1), .in_2(SPA_B_IN), .out_4(d_latch_9_out_4));  // open: out_3
  D_Latch d_latch_10 (.in_1(RCLK1), .in_2(d_latch_40_out_4), .out_4(d_latch_10_out_4));  // open: out_3
  D_Latch d_latch_11 (.in_1(RCLK1), .in_2(_304_out), .out_4(d_latch_11_out_4));  // open: out_3
  D_Latch d_latch_12 (.in_1(RCLK1), .in_2(_241_out), .out_4(d_latch_12_out_4));  // open: out_3
  D_Latch d_latch_13 (.in_1(RCLK1), .in_2(_187_4_out), .out_4(d_latch_13_out_4));  // open: out_3
  D_Latch d_latch_14 (.in_1(RCLK1), .in_2(_188_4_out), .out_4(d_latch_14_out_4));  // open: out_3
  D_Latch d_latch_15 (.in_1(RCLK1), .in_2(_189_4_out), .out_4(d_latch_15_out_4));  // open: out_3
  D_Latch d_latch_16 (.in_1(RCLK1), .in_2(_190_4_out), .out_4(d_latch_16_out_4));  // open: out_3
  D_Latch d_latch_17 (.in_1(RCLK1), .in_2(_191_4_out), .out_4(d_latch_17_out_4));  // open: out_3
  D_Latch d_latch_18 (.in_1(RCLK1), .in_2(_192_4_out), .out_4(d_latch_18_out_4));  // open: out_3
  D_Latch d_latch_19 (.in_1(RCLK1), .in_2(_5), .out_4(d_latch_19_out_4));  // open: out_3
  D_Latch d_latch_20 (.in_1(RCLK1), .in_2(d_latch_48_out_4), .out_4(d_latch_20_out_4));  // open: out_3
  D_Latch d_latch_21 (.in_1(RCLK1), .in_2(d_latch_49_out_4), .out_4(d_latch_21_out_4));  // open: out_3
  D_Latch d_latch_22 (.in_1(RCLK1), .in_2(ram_1_data[8]), .out_4(d_latch_22_out_4));  // open: out_3
  D_Latch d_latch_23 (.in_1(RCLK1), .in_2(ram_1_data[7]), .out_4(d_latch_23_out_4));  // open: out_3
  D_Latch d_latch_24 (.in_1(RCLK1), .in_2(ram_1_data[6]), .out_4(d_latch_24_out_4));  // open: out_3
  D_Latch d_latch_25 (.in_1(RCLK1), .in_2(ram_1_data[4]), .out_4(d_latch_25_out_4));  // open: out_3
  D_Latch d_latch_26 (.in_1(RCLK1), .in_2(ram_1_data[3]), .out_4(d_latch_26_out_4));  // open: out_3
  D_Latch d_latch_27 (.in_1(RCLK1), .in_2(ram_1_data[1]), .out_4(d_latch_27_out_4));  // open: out_3
  D_Latch d_latch_28 (.in_1(RCLK1), .in_2(ram_1_data[0]), .out_4(d_latch_28_out_4));  // open: out_3
  D_Latch d_latch_29 (.in_1(RCLK1), .in_2(ram_1_data[2]), .out_4(d_latch_29_out_4));  // open: out_3
  D_Latch d_latch_30 (.in_1(RCLK1), .in_2(ram_1_data[5]), .out_4(d_latch_30_out_4));  // open: out_3
  D_Latch d_latch_31 (.in_1(RCLK1), .in_2(_312_out), .out_4(d_latch_31_out_4));  // open: out_3
  D_Latch d_latch_32 (.in_1(RCLK1), .in_2(_82), .out_4(d_latch_32_out_4));  // open: out_3
  D_Latch d_latch_33 (.in_1(RCLK1), .in_2(_81), .out_4(d_latch_33_out_4));  // open: out_3
  D_Latch d_latch_34 (.in_1(RCLK1), .in_2(out_66[0]), .out_4(d_latch_34_out_4));  // open: out_3
  D_Latch d_latch_35 (.in_1(RCLK1), .in_2(out_66[1]), .out_4(d_latch_35_out_4));  // open: out_3
  D_Latch d_latch_36 (.in_1(RCLK1), .in_2(out_66[2]), .out_4(d_latch_36_out_4));  // open: out_3
  D_Latch d_latch_37 (.in_1(RCLK1), .in_2(_39), .out_4(d_latch_37_out_4));  // open: out_3
  D_Latch d_latch_38 (.in_1(RCLK2), .in_2(d_latch_9_out_4), .out_4(d_latch_38_out_4));  // open: out_3
  D_Latch d_latch_39 (.in_1(RCLK2), .in_2(d_latch_10_out_4), .out_4(d_latch_39_out_4));  // open: out_3
  D_Latch d_latch_40 (.in_1(RCLK2), .in_2(d_latch_11_out_4), .out_4(d_latch_40_out_4));  // open: out_3
  D_Latch d_latch_41 (.in_1(RCLK2), .in_2(d_latch_12_out_4), .out_4(d_latch_41_out_4));  // open: out_3
  not not_10 (not_10_out, d_latch_41_out_4);
  assign _52 = not_10_out ? d_latch_3_out_3 : 1'bz;  // Controlled_Buffer controlled_buffer_1
  assign _51 = not_10_out ? d_latch_4_out_3 : 1'bz;  // Controlled_Buffer controlled_buffer_2
  assign _50 = not_10_out ? d_latch_5_out_3 : 1'bz;  // Controlled_Buffer controlled_buffer_3
  assign _49 = not_10_out ? d_latch_6_out_3 : 1'bz;  // Controlled_Buffer controlled_buffer_4
  assign _48 = not_10_out ? _177_out : 1'bz;  // Controlled_Buffer controlled_buffer_5
  assign _47 = not_10_out ? _176_out : 1'bz;  // Controlled_Buffer controlled_buffer_6
  D_Latch d_latch_42 (.in_1(RCLK2), .in_2(d_latch_13_out_4), .out_4(d_latch_42_out_4[0]));  // open: out_3
  D_Latch d_latch_43 (.in_1(RCLK2), .in_2(d_latch_14_out_4), .out_4(d_latch_42_out_4[1]));  // open: out_3
  D_Latch d_latch_44 (.in_1(RCLK2), .in_2(d_latch_15_out_4), .out_4(d_latch_42_out_4[2]));  // open: out_3
  D_Latch d_latch_45 (.in_1(RCLK2), .in_2(d_latch_16_out_4), .out_4(d_latch_42_out_4[3]));  // open: out_3
  D_Latch d_latch_46 (.in_1(RCLK2), .in_2(d_latch_17_out_4), .out_4(d_latch_42_out_4[4]));  // open: out_3
  D_Latch d_latch_47 (.in_1(RCLK2), .in_2(d_latch_18_out_4), .out_4(d_latch_42_out_4[5]));  // open: out_3
  D_Latch d_latch_48 (.in_1(RCLK2), .in_2(d_latch_19_out_4), .out_4(d_latch_48_out_4));  // open: out_3
  D_Latch d_latch_49 (.in_1(RCLK2), .in_2(d_latch_20_out_4), .out_4(d_latch_49_out_4));  // open: out_3
  D_Latch d_latch_50 (.in_1(RCLK2), .in_2(d_latch_21_out_4), .out_4(d_latch_50_out_4));  // open: out_3
  D_Latch d_latch_51 (.in_1(RCLK2), .in_2(d_latch_22_out_4), .out_4(d_latch_51_out_4));  // open: out_3
  D_Latch d_latch_52 (.in_1(RCLK2), .in_2(d_latch_23_out_4), .out_4(d_latch_52_out_4));  // open: out_3
  D_Latch d_latch_53 (.in_1(RCLK2), .in_2(d_latch_24_out_4), .out_4(d_latch_53_out_4));  // open: out_3
  D_Latch d_latch_54 (.in_1(RCLK2), .in_2(d_latch_25_out_4), .out_4(d_latch_54_out_4));  // open: out_3
  D_Latch d_latch_55 (.in_1(RCLK2), .in_2(d_latch_26_out_4), .out_4(d_latch_55_out_4));  // open: out_3
  D_Latch d_latch_56 (.in_1(RCLK2), .in_2(d_latch_27_out_4), .out_4(d_latch_56_out_4));  // open: out_3
  D_Latch d_latch_57 (.in_1(RCLK2), .in_2(d_latch_28_out_4), .out_4(d_latch_57_out_4));  // open: out_3
  D_Latch d_latch_58 (.in_1(RCLK2), .in_2(d_latch_29_out_4), .out_4(d_latch_58_out_4));  // open: out_3
  D_Latch d_latch_59 (.in_1(RCLK2), .in_2(d_latch_30_out_4), .out_4(d_latch_59_out_4));  // open: out_3
  D_Latch d_latch_60 (.in_1(RCLK2), .in_2(d_latch_31_out_4), .out_4(d_latch_60_out_4));  // open: out_3
  D_Latch d_latch_61 (.in_1(RCLK2), .in_2(d_latch_32_out_4), .out_4(d_latch_61_out_4));  // open: out_3
  D_Latch d_latch_62 (.in_1(RCLK2), .in_2(d_latch_33_out_4), .out_4(d_latch_62_out_4));  // open: out_3
  D_Latch d_latch_63 (.in_1(RCLK2), .in_2(d_latch_34_out_4), .out_4(d_latch_63_out_4[0]));  // open: out_3
  D_Latch d_latch_64 (.in_1(RCLK2), .in_2(d_latch_35_out_4), .out_4(d_latch_63_out_4[1]));  // open: out_3
  D_Latch d_latch_65 (.in_1(RCLK2), .in_2(d_latch_36_out_4), .out_4(d_latch_63_out_4[2]));  // open: out_3
  D_Latch d_latch_66 (.in_1(RCLK2), .in_2(d_latch_37_out_4), .out_4(d_latch_66_out_4));  // open: out_3
  and _280 (_280_out, RCLK1, d_latch_48_out_4);
  not not_11 (not_11_out, d_latch_50_out_4);
  D_Latch d_latch_67 (.in_1(RCLK1), .in_2(d_latch_66_out_4), .out_4(d_latch_67_out_4));  // open: out_3
  D_Latch d_latch_68 (.in_1(_280_out), .in_2(ram_1_data[8]), .out_4(d_latch_68_out_4));  // open: out_3
  D_Latch d_latch_69 (.in_1(_280_out), .in_2(ram_1_data[7]), .out_4(d_latch_69_out_4));  // open: out_3
  D_Latch d_latch_70 (.in_1(_280_out), .in_2(ram_1_data[6]), .out_4(d_latch_70_out_4));  // open: out_3
  D_Latch d_latch_71 (.in_1(_280_out), .in_2(ram_1_data[4]), .out_4(d_latch_71_out_4));  // open: out_3
  D_Latch d_latch_72 (.in_1(_280_out), .in_2(ram_1_data[3]), .out_4(d_latch_72_out_4));  // open: out_3
  D_Latch d_latch_73 (.in_1(_280_out), .in_2(ram_1_data[1]), .out_4(d_latch_73_out_4));  // open: out_3
  D_Latch d_latch_74 (.in_1(_280_out), .in_2(ram_1_data[0]), .out_4(d_latch_74_out_4));  // open: out_3
  D_Latch d_latch_75 (.in_1(_280_out), .in_2(ram_1_data[2]), .out_4(d_latch_75_out_4));  // open: out_3
  D_Latch d_latch_76 (.in_1(_280_out), .in_2(ram_1_data[5]), .out_4(d_latch_76_out_4));  // open: out_3
  D_Latch d_latch_77 (.in_1(RCLK2), .in_2(d_latch_67_out_4), .out_4(d_latch_77_out_4));  // open: out_3
  and _269 (_269_out, d_latch_39_out_4, d_latch_60_out_4);
  not not_12 (not_12_out, not_11_out);
  assign out_66[8] = not_12_out ? ~d_latch_68_out_4 : 1'bz;  // Controlled_Inverter controlled_inverter_1
  assign out_66[7] = not_12_out ? ~d_latch_69_out_4 : 1'bz;  // Controlled_Inverter controlled_inverter_2
  assign out_66[6] = not_12_out ? ~d_latch_70_out_4 : 1'bz;  // Controlled_Inverter controlled_inverter_3
  assign out_66[4] = not_12_out ? ~d_latch_71_out_4 : 1'bz;  // Controlled_Inverter controlled_inverter_4
  assign out_66[3] = not_12_out ? ~d_latch_72_out_4 : 1'bz;  // Controlled_Inverter controlled_inverter_5
  assign out_66[1] = not_12_out ? ~d_latch_73_out_4 : 1'bz;  // Controlled_Inverter controlled_inverter_6
  assign out_66[0] = not_12_out ? ~d_latch_74_out_4 : 1'bz;  // Controlled_Inverter controlled_inverter_7
  assign out_66[2] = not_12_out ? ~d_latch_75_out_4 : 1'bz;  // Controlled_Inverter controlled_inverter_8
  assign out_66[5] = not_12_out ? ~d_latch_76_out_4 : 1'bz;  // Controlled_Inverter controlled_inverter_9
  RAM #(.addrWidth(6), .dataWidth(9), .bus("separate")) ram_1 (
    .addr(d_latch_42_out_4), .din(d_latch_63_out_4), .data(ram_1_data), .sel(1'b1));  // open: str, clk, ld, clr
  D_Latch d_latch_78 (.in_1(RCLK1), .in_2(d_latch_77_out_4), .out_4(d_latch_78_out_4));  // open: out_3
  and _241 (_241_out, _245_out, _305_out);
  D_Latch d_latch_79 (.in_1(RCLK2), .in_2(d_latch_78_out_4), .out_4(d_latch_79_out_4));  // open: out_3
  D_Latch d_latch_80 (.in_1(RCLK1), .in_2(d_latch_79_out_4), .out_4(d_latch_80_out_4));  // open: out_3
  and _311 (_311_out, d_latch_38_out_4, _38);
  nor _311_2 (_311_2_out, _311_out, _269_out);
  not not_13 (not_13_out, _73);
  not not_14 (not_14_out, _83);
  not not_15 (not_15_out, _84);
  or _206 (_206_out, _65, _66);
  Multiplexer #(.disabled(0), .enable("false")) multiplexer_7 (
    .in0(d_latch_51_out_4), .in1(d_latch_52_out_4), .out(multiplexer_7_out), .sel(not_4_out));
  Multiplexer #(.disabled(0), .enable("false")) multiplexer_8 (
    .in0(d_latch_52_out_4), .in1(d_latch_53_out_4), .out(multiplexer_8_out), .sel(not_4_out));
  Multiplexer #(.disabled(0), .enable("false")) multiplexer_9 (
    .in0(d_latch_53_out_4), .in1(d_latch_54_out_4), .out(multiplexer_9_out), .sel(not_4_out));
  Multiplexer #(.disabled(0), .enable("false")) multiplexer_10 (
    .in0(d_latch_59_out_4), .in1(d_latch_55_out_4), .out(multiplexer_10_out), .sel(not_4_out));
  Multiplexer #(.disabled(0), .enable("false")) multiplexer_11 (
    .in0(d_latch_54_out_4), .in1(d_latch_56_out_4), .out(multiplexer_11_out), .sel(not_4_out));
  Multiplexer #(.disabled(0), .enable("false")) multiplexer_12 (
    .in0(d_latch_55_out_4), .in1(d_latch_57_out_4), .out(multiplexer_12_out), .sel(not_4_out));
  D_Latch d_latch_81 (.in_1(RCLK2), .in_2(d_latch_80_out_4), .out_4(d_latch_81_out_4));  // open: out_3
  and _236 (_236_out, _230_out, _86, _206_out);
  and _270 (_270_out, d_latch_60_out_4, _17, multiplexer_7_out);
  and _271 (_271_out, d_latch_60_out_4, _17, multiplexer_8_out);
  and _272 (_272_out, d_latch_60_out_4, _17, multiplexer_9_out);
  and _273 (_273_out, d_latch_60_out_4, _17, multiplexer_10_out);
  and _274 (_274_out, d_latch_60_out_4, _17, multiplexer_11_out);
  and _275 (_275_out, d_latch_60_out_4, _17, multiplexer_12_out);
  and _276 (_276_out, d_latch_60_out_4, M5, d_latch_58_out_4);
  and _277 (_277_out, d_latch_60_out_4, M5, d_latch_59_out_4);
  and _278 (_278_out, d_latch_60_out_4, M5, d_latch_51_out_4);
  D_Latch d_latch_82 (.in_1(RCLK1), .in_2(d_latch_81_out_4), .out_4(d_latch_82_out_4));  // open: out_3
  or _245 (_245_out, not_16_out, _239_out);
  and _229 (_229_out, _83, not_13_out, _84);
  and _227 (_227_out, _84, not_13_out, not_14_out);
  and _228 (_228_out, not_13_out, _83, not_15_out);
  and _226 (_226_out, _83, not_15_out, _73);
  Multiplexer #(.disabled(0), .enable("false")) multiplexer_13 (
    .in0(not_14_out), .in1(_73), .out(multiplexer_13_out), .sel(not_15_out));
  and _310 (_310_out, not_15_out, not_13_out, not_14_out, _230_out);
  and _300 (_300_out, not_15_out, not_14_out, _73, _230_out);
  assign DATA_OUT[3] = not_9_out ? ~_270_out : 1'bz;  // Controlled_Inverter controlled_inverter_10
  assign DATA_OUT[4] = not_9_out ? ~_271_out : 1'bz;  // Controlled_Inverter controlled_inverter_11
  assign DATA_OUT[6] = not_9_out ? ~_272_out : 1'bz;  // Controlled_Inverter controlled_inverter_12
  assign DATA_OUT[7] = not_9_out ? ~_273_out : 1'bz;  // Controlled_Inverter controlled_inverter_13
  assign DATA_OUT[9] = not_9_out ? ~_274_out : 1'bz;  // Controlled_Inverter controlled_inverter_14
  assign DATA_OUT[10] = not_9_out ? ~_275_out : 1'bz;  // Controlled_Inverter controlled_inverter_15
  assign DATA_OUT[8] = not_9_out ? ~_276_out : 1'bz;  // Controlled_Inverter controlled_inverter_16
  assign DATA_OUT[5] = not_9_out ? ~_277_out : 1'bz;  // Controlled_Inverter controlled_inverter_17
  assign DATA_OUT[2] = not_9_out ? ~_278_out : 1'bz;  // Controlled_Inverter controlled_inverter_18
  D_Latch d_latch_83 (.in_1(RCLK2), .in_2(d_latch_82_out_4), .out_4(d_latch_83_out_4));  // open: out_3
  not not_16 (not_16_out, _207_out);
  D_Latch d_latch_84 (.in_1(RCLK1), .in_2(d_latch_83_out_4), .out_4(d_latch_84_out_4));  // open: out_3
  and _239 (_239_out, _308_out, _231_out, _306_out);
  nor _201 (_201_out, _310_out, _300_out);
  D_Latch d_latch_85 (.in_1(RCLK2), .in_2(d_latch_84_out_4), .out_4(d_latch_85_out_4));  // open: out_3
  not not_17 (not_17_out, _70);
  or _231 (_231_out, _236_out, not_17_out);
  nand _308 (_308_out, M5, _78);
  D_Latch d_latch_86 (.in_1(RCLK1), .in_2(d_latch_85_out_4), .out_4(d_latch_86_out_4));  // open: out_3
  nor _307 (_307_out, _70, M5);
  nor _306 (_306_out, _307_out, _77);
  nor _305 (_305_out, not_18_out, _88);
  not not_18 (not_18_out, _87);
  not not_19 (not_19_out, _201_out);
  not not_20 (not_20_out, _66);
  D_Latch d_latch_87 (.in_1(RCLK2), .in_2(d_latch_86_out_4), .out_4(d_latch_87_out_4));  // open: out_3
  not not_21 (not_21_out, _306_out);
  not not_22 (not_22_out, _308_out);
  and _202 (_202_out, multiplexer_13_out, _231_out);
  and _233 (_233_out, _226_out, _308_out, _231_out);
  and _234 (_234_out, _308_out, _231_out, _228_out);
  and _209 (_209_out, _229_out, _306_out);
  and _208 (_208_out, _226_out, _231_out);
  and _237 (_237_out, multiplexer_13_out, _306_out, _231_out);
  and _238 (_238_out, _227_out, _306_out, _231_out);
  and _217 (_217_out, _306_out, _227_out);
  and _218 (_218_out, _308_out, _228_out);
  and _225 (_225_out, _306_out, _308_out, _229_out);
  not not_23 (not_23_out, _88);
  not not_24 (not_24_out, _236_out);
  nor _200 (_200_out, _66, _205_out);
  D_Latch d_latch_88 (.in_1(RCLK1), .in_2(d_latch_87_out_4), .out_4(d_latch_88_out_4));  // open: out_3
  and _223 (_223_out, not_18_out, _88);
  and _222 (_222_out, not_18_out, _88);
  and _221 (_221_out, not_23_out, _87);
  and _204 (_204_out, not_24_out, _292_out);
  and _203 (_203_out, _292_out, _236_out);
  and _196 (_196_out, _203_out, _65);
  and _196_2 (_196_2_out, _200_out, not_19_out);
  and _196_3 (_196_3_out, _310_out, not_20_out);
  and _232 (_232_out, _203_out, _66, _201_out);
  RGB_DECODER rgb_decoder_1 (
    .RCLK1(RCLK1), .RCLK2(RCLK2), ._1__36(d_latch_105_out_4), ._93(d_latch_110_out_4),
    ._94(d_latch_115_out_4), .R0(_277_out), .R1(_270_out), .R2(_271_out), .G0(_278_out), .G1(_272_out),
    .G2(_273_out), .B0(_276_out), .B1(_274_out), .B2(_275_out), .B_DAC(B_DAC), .G_DAC(G_DAC), .R_DAC(R_DAC));
  D_Latch d_latch_89 (.in_1(RCLK2), .in_2(d_latch_88_out_4), .out_4(d_latch_89_out_4));  // open: out_3
  or _301 (_301_out, _229_out, _227_out, _202_out, _233_out, _234_out);
  or _302 (_302_out, _228_out, _209_out, _208_out, _237_out, _238_out);
  or _303 (_303_out, _226_out, _217_out, _218_out, _225_out, multiplexer_13_out);
  or _205 (_205_out, _221_out, _204_out);
  or _196_4 (_196_4_out, _196_out, _196_2_out, _196_3_out);
  Multiplexer #(.disabled(0), .enable("false")) multiplexer_14 (
    .in0(_39), .in1(d_latch_89_out_4), .out(multiplexer_14_out), .sel(M5));
  and _207 (_207_out, not_25_out, d_latch_117_out_4);
  not not_25 (not_25_out, _64);
  D_Latch d_latch_90 (.in_1(RCLK1), .in_2(multiplexer_14_out), .out_4(d_latch_90_out_4));  // open: out_3
  and _235 (_235_out, not_21_out, _301_out, _207_out);
  and _240 (_240_out, not_22_out, _302_out, _207_out);
  and _292 (_292_out, _70, _303_out, _207_out);
  and _195 (_195_out, _196_4_out, d_latch_117_out_4);
  D_Latch d_latch_91 (.in_1(RCLK2), .in_2(d_latch_90_out_4), .out_4(d_latch_91_out_4));  // open: out_3
  or _244 (_244_out, _240_out, _223_out);
  or _211 (_211_out, _235_out, _222_out);
  nand _309 (_309_out, _67, _38);
  D_Latch d_latch_92 (.in_1(RCLK1), .in_2(d_latch_91_out_4), .out_4(d_latch_92_out_4));  // open: out_3
  D_Latch d_latch_93 (.in_1(RCLK1), .in_2(_311_2_out), .out_4(d_latch_93_out_4));  // open: out_3
  D_Latch d_latch_94 (.in_1(RCLK1), .in_2(_244_out), .out_4(d_latch_94_out_4));  // open: out_3
  D_Latch d_latch_95 (.in_1(RCLK1), .in_2(_211_out), .out_4(d_latch_95_out_4));  // open: out_3
  D_Latch d_latch_96 (.in_1(RCLK1), .in_2(_205_out), .out_4(d_latch_96_out_4));  // open: out_3
  D_Latch d_latch_97 (.in_1(RCLK1), .in_2(_309_out), .out_4(d_latch_97_out_4));  // open: out_3
  D_Latch d_latch_98 (.in_1(RCLK1), .in_2(d_latch_111_out_4), .out_4(d_latch_98_out_4));  // open: out_3
  D_Latch d_latch_99 (.in_1(RCLK1), .in_2(_79), .out_4(d_latch_99_out_4));  // open: out_3
  D_Latch d_latch_100 (.in_1(RCLK1), .in_2(_195_out), .out_4(d_latch_100_out_4));  // open: out_3
  D_Latch d_latch_101 (.in_1(RCLK1), .in_2(_232_out), .out_4(d_latch_101_out_4));  // open: out_3
  D_Latch d_latch_102 (.in_1(RCLK1), .in_2(_80), .out_4(d_latch_102_out_4));  // open: out_3
  D_Latch d_latch_103 (.in_1(RCLK1), .in_2(d_latch_114_out_4), .out_4(d_latch_103_out_4));  // open: out_3
  D_Latch d_latch_104 (.in_1(RCLK2), .in_2(d_latch_92_out_4), .out_4(d_latch_104_out_4));  // open: out_3
  D_Latch d_latch_105 (.in_1(RCLK2), .in_2(d_latch_93_out_4), .out_4(d_latch_105_out_4));  // open: out_3
  D_Latch d_latch_106 (.in_1(RCLK2), .in_2(d_latch_94_out_4), .out_4(_69));  // open: out_3
  D_Latch d_latch_107 (.in_1(RCLK2), .in_2(d_latch_95_out_4), .out_4(_68));  // open: out_3
  D_Latch d_latch_108 (.in_1(RCLK2), .in_2(d_latch_96_out_4), .out_4(_67));  // open: out_3
  D_Latch d_latch_109 (.in_1(RCLK2), .in_2(d_latch_97_out_4), .out_4(SPA_B_OUT));  // open: out_3
  D_Latch d_latch_110 (.in_1(RCLK2), .in_2(d_latch_98_out_4), .out_4(d_latch_110_out_4));  // open: out_3
  D_Latch d_latch_111 (.in_1(RCLK2), .in_2(d_latch_99_out_4), .out_4(d_latch_111_out_4));  // open: out_3
  D_Latch d_latch_112 (.in_1(RCLK2), .in_2(d_latch_100_out_4), .out_4(d_latch_112_out_4));  // open: out_3
  D_Latch d_latch_113 (.in_1(RCLK2), .in_2(d_latch_101_out_4), .out_4(d_latch_113_out_4));  // open: out_3
  D_Latch d_latch_114 (.in_1(RCLK2), .in_2(d_latch_102_out_4), .out_4(d_latch_114_out_4));  // open: out_3
  D_Latch d_latch_115 (.in_1(RCLK2), .in_2(d_latch_103_out_4), .out_4(d_latch_115_out_4));  // open: out_3
  D_Latch d_latch_116 (.in_1(RCLK1), .in_2(d_latch_104_out_4), .out_4(d_latch_116_out_4));  // open: out_3
  D_Latch d_latch_117 (.in_1(RCLK2), .in_2(d_latch_116_out_4), .out_4(d_latch_117_out_4));  // open: out_3
  assign DATA_OUT[0] = not_9_out ? ~d_latch_110_out_4 : 1'bz;  // Controlled_Inverter controlled_inverter_19
  Multiplexer #(.disabled(0), .enable("false")) multiplexer_15 (
    .in0(d_latch_112_out_4), .in1(d_latch_1_out_3), .out(_79), .sel(_64));
  assign DATA_OUT[1] = not_9_out ? ~d_latch_113_out_4 : 1'bz;  // Controlled_Inverter controlled_inverter_20
  Multiplexer #(.disabled(0), .enable("false")) multiplexer_16 (
    .in0(d_latch_113_out_4), .in1(d_latch_2_out_3), .out(_80), .sel(_64));

  assign out_64 = {_47, _48, _49, _50, _51, _52};

  // Notes on the sheet:
  //   63
  //   76
  //   18
  //   184
  //   181
  //   53
  //   288
  //   266
  //   287
  //   286
  //   285
  //   284
  //   283
  //   282
  //   67
  //   60
  //   66
  //   65
  //   64
  //   63
  //   62
  //   61
  //   182
  //   268
  //   180
  //   179
  //   16
  //   21
  //   26
  //   31
  //   23
  //   24
  //   1
  //   25
  //   27
  //   28
  //   20
  //   19
  //   18
  //   49
  //   48
  //   47
  //   45
  //   44
  //   42
  //   50
  //   43
  //   46
  //   22
  //   40
  //   41
  //   7
  //   6
  //   5
  //   15
  //   183
  //   170
  //   171
  //   172
  //   173
  //   174
  //   175
  //   281
  //   14
  //   59
  //   58
  //   57
  //   55
  //   54
  //   51
  //   52
  //   53
  //   56
  //   CRAM
  //   255
  //   254
  //   253
  //   251
  //   253
  //   248
  //   247
  //   249
  //   250
  //   13
  //   12
  //   AOI21
  //   216
  //   214
  //   215
  //   296
  //   297
  //   295
  //   294
  //   298
  //   299
  //   215
  //   293
  //   11
  //   267
  //   265
  //   264
  //   263
  //   262
  //   261
  //   260
  //   259
  //   258
  //   242
  //   10
  //   9
  //   213
  //   219
  //   197
  //   198
  //   212
  //   243
  //   220
  //   199
  //   8
  //   246
  //   289
  //   185
  //   2
  //   3
  //   17
  //   30
  //   29
  //   39
  //   32
  //   35
  //   36
  //   37
  //   38
  //   34
  //   33
  //   4
  //   36 (1)
  //   291
  //   257
  //   256
  //   290
endmodule

module BG (
  input  RCLK1,
  input  RCLK2,
  input  in_3,
  input  DCLK1,
  input  DCLK2,
  input  [7:0] SD_VRAM_DATA_LATCHED,
  input  _27,
  input  _28,
  input  _30,
  input  _31,
  input  _63,
  input  M5,
  input  in_13,
  input  _67,
  input  _68,
  input  _64,
  input  _65,
  input  _25,
  input  _26,
  output _20,
  output [6:0] PLANE_B_OUT,
  output _73,
  output [6:0] PLANE_A_OUT
);

  wire _497_out, _524_out, _637_2_out, _637_3_out, _637_4_out, _637_out, _638_2_out, _638_3_out, _638_4_out,
       _638_out, _639_2_out, _639_3_out, _639_4_out, _639_out, _640_2_out, _640_3_out, _640_4_out, _640_out,
       _641_out, _647_out, _660_out, _661_out, _662_out, _663_out, _664_out, _665_out, _666_out, _667_out,
       _668_out, _670_out, _671_out, _672_out, _673_out, _674_out, _675_out, _676_out, _677_out, _680_out,
       _682_out, _683_out, _684_out, _686_out, _691_out, _692_out, _697_2_out, _697_out, _698_2_out,
       _698_out, _699_2_out, _699_out, _700_out, _725_out, _726_out, _728_out, _729_out, _730_out, _731_out,
       _732_out, bg_4bit_cnt_1_out0, bg_4bit_cnt_1_out1, bg_4bit_cnt_1_out2, bg_4bit_cnt_1_out3,
       bg_4bit_cnt_2_out0, bg_4bit_cnt_2_out1, bg_4bit_cnt_2_out2, bg_4bit_cnt_2_out3, bg_pipeline_1_1_ou1,
       bg_pipeline_1_1_out0, bg_pipeline_1_1_out2, bg_pipeline_1_1_out3, bg_pipeline_1_2_ou1,
       bg_pipeline_1_2_out0, bg_pipeline_1_2_out2, bg_pipeline_1_2_out3, d_latch_1_out_3, d_latch_2_out_3,
       d_latch_3_out_3, d_latch_4_out_3, d_latch_5_out_4, d_latch_6_out_4, d_latch_7_out_4, d_latch_8_out_4,
       d_latch_9_out_4, d_latch_11_out_4, d_latch_12_out_4, d_latch_13_out_4, d_latch_14_out_4,
       d_latch_15_out_4, d_latch_16_out_4, d_latch_17_out_4, d_latch_18_out_4, d_latch_19_out_4,
       d_latch_20_out_4, d_latch_21_out_4, d_latch_22_out_4, d_latch_23_out_4, d_latch_24_out_4,
       d_latch_25_out_4, d_latch_26_out_4, d_latch_27_out_4, d_latch_28_out_4, d_latch_29_out_4,
       d_latch_30_out_4, d_latch_31_out_4, d_latch_32_out_4, d_latch_33_out_4, d_latch_34_out_4,
       d_latch_35_out_4, d_latch_36_out_4, d_latch_37_out_4, d_latch_38_out_4, d_latch_39_out_4,
       d_latch_40_out_4, d_latch_41_out_4, d_latch_42_out_4, d_latch_43_out_4, d_latch_44_out_4,
       d_latch_45_out_4, d_latch_46_out_4, d_latch_47_out_4, d_latch_48_out_4, d_latch_49_out_4,
       d_latch_50_out_4, d_latch_51_out_4, d_latch_52_out_4, d_latch_53_out_3, d_latch_54_out_3,
       d_latch_55_out_3, d_latch_56_out_3, d_latch_57_out_3, d_latch_58_out_3, d_latch_59_out_3,
       d_latch_60_out_3, d_latch_61_out_3, d_latch_62_out_3, d_latch_63_out_3, d_latch_64_out_3,
       d_latch_65_out_3, d_latch_66_out_3, d_latch_67_out_3, d_latch_68_out_3, d_latch_93_out_3,
       d_latch_94_out_3, d_latch_95_out_3, d_latch_96_out_3, d_latch_97_out_3, d_latch_98_out_3,
       d_latch_99_out_3, d_latch_100_out_3, d_latch_101_out_3, d_latch_102_out_3, d_latch_103_out_3,
       d_latch_104_out_3, d_latch_105_out_3, d_latch_106_out_3, d_latch_107_out_3, d_latch_108_out_3,
       d_latch_109_out_3, d_latch_110_out_3, d_latch_111_out_3, d_latch_112_out_3, d_latch_113_out_3,
       d_latch_114_out_3, d_latch_115_out_3, d_latch_116_out_3, d_latch_117_out_4, d_latch_118_out_4,
       d_latch_119_out_4, d_latch_120_out_4, d_latch_121_out_4, d_latch_122_out_4, d_latch_123_out_4,
       d_latch_124_out_4, d_latch_125_out_4, d_latch_126_out_4, d_latch_127_out_4, d_latch_128_out_4,
       d_latch_129_out_4, d_latch_130_out_4, d_latch_131_out_4, d_latch_132_out_4, d_latch_133_out_4,
       d_latch_134_out_4, d_latch_135_out_4, d_latch_136_out_4, d_latch_137_out_4, d_latch_138_out_4,
       d_latch_139_out_4, d_latch_140_out_4, d_latch_141_out_4, d_latch_142_out_4, d_latch_143_out_4,
       d_latch_144_out_4, d_latch_145_out_4, d_latch_146_out_4, d_latch_147_out_4, d_latch_148_out_4,
       d_latch_149_out_4, d_latch_150_out_4, d_latch_151_out_4, d_latch_152_out_4, d_latch_153_out_4,
       d_latch_154_out_4, d_latch_155_out_4, d_latch_156_out_4, d_latch_157_out_4, d_latch_158_out_4,
       d_latch_159_out_4, d_latch_160_out_4, d_latch_161_out_4, d_latch_162_out_4, d_latch_163_out_4,
       d_latch_164_out_4, d_latch_165_out_4, d_latch_166_out_4, d_latch_167_out_4, d_latch_168_out_4,
       d_latch_169_out_4, d_latch_170_out_4, d_latch_171_out_4, d_latch_172_out_4, multiplexer_1_out,
       multiplexer_2_out, multiplexer_3_out, multiplexer_4_out, multiplexer_5_out, multiplexer_6_out,
       multiplexer_7_out, multiplexer_8_out, multiplexer_9_out, multiplexer_10_out, multiplexer_11_out,
       multiplexer_12_out, multiplexer_13_out, not_1_out, not_2_out, not_3_out, not_4_out, not_5_out,
       not_6_out, not_7_out, not_8_out, not_9_out, not_10_out, not_11_out, not_12_out, not_13_out,
       not_14_out, not_15_out, not_16_out, not_17_out, not_18_out, not_19_out, undriven, undriven_2,
       undriven_3, undriven_4, undriven_5, undriven_8, undriven_9, undriven_10;
  wire [2:0] _518_out, _626_out;
  wire [3:0] undriven_6;
  wire [7:0] decoder_1_out0, decoder_2_out0, undriven_7;
  wire [11:0] bg_pipeline_2_1_out0;

  or _691 (_691_out, _30, _31);
  or _692 (_692_out, _64, _65);
  and _698 (_698_out, _28, _691_out);
  not not_1 (not_1_out, in_13);
  and _697 (_697_out, not_6_out, _67);
  not not_2 (not_2_out, _692_out);
  and _699 (_699_out, not_6_out, _25);
  nor _698_2 (_698_2_out, _27, _698_out);
  not not_3 (not_3_out, _691_out);
  not not_4 (not_4_out, not_3_out);
  not not_5 (not_5_out, undriven_6[3]);
  not not_6 (not_6_out, not_1_out);
  nor _697_2 (_697_2_out, _697_out, _68);
  not not_7 (not_7_out, not_2_out);
  D_Latch d_latch_1 (.in_1(undriven_5), .in_2(undriven), .out_3(d_latch_1_out_3));  // open: out_4
  D_Latch d_latch_2 (.in_1(undriven_5), .in_2(undriven_2), .out_3(d_latch_2_out_3));  // open: out_4
  D_Latch d_latch_3 (.in_1(undriven_5), .in_2(undriven_3), .out_3(d_latch_3_out_3));  // open: out_4
  D_Latch d_latch_4 (.in_1(undriven_5), .in_2(undriven_4), .out_3(d_latch_4_out_3));  // open: out_4
  nor _699_2 (_699_2_out, _699_out, _26);
  not not_8 (not_8_out, _698_2_out);
  not not_9 (not_9_out, _697_2_out);
  and _641 (_641_out, _692_out, d_latch_1_out_3, d_latch_2_out_3, d_latch_3_out_3, d_latch_4_out_3);
  not not_10 (not_10_out, _699_2_out);
  D_Latch d_latch_5 (.in_1(RCLK1), .in_2(not_8_out), .out_4(d_latch_5_out_4));  // open: out_3
  D_Latch d_latch_6 (.in_1(RCLK1), .in_2(d_latch_12_out_4), .out_4(d_latch_6_out_4));  // open: out_3
  D_Latch d_latch_7 (.in_1(RCLK1), .in_2(not_9_out), .out_4(d_latch_7_out_4));  // open: out_3
  D_Latch d_latch_8 (.in_1(RCLK1), .in_2(d_latch_14_out_4), .out_4(d_latch_8_out_4));  // open: out_3
  D_Latch d_latch_9 (.in_1(RCLK1), .in_2(not_10_out), .out_4(d_latch_9_out_4));  // open: out_3
  D_Latch d_latch_10 (.in_1(RCLK1), .in_2(d_latch_16_out_4));  // open: out_3, out_4
  D_Latch d_latch_11 (.in_1(RCLK1), .in_2(d_latch_17_out_4), .out_4(d_latch_11_out_4));  // open: out_3
  D_Latch d_latch_12 (.in_1(RCLK2), .in_2(d_latch_5_out_4), .out_4(d_latch_12_out_4));  // open: out_3
  D_Latch d_latch_13 (.in_1(RCLK2), .in_2(d_latch_6_out_4), .out_4(d_latch_13_out_4));  // open: out_3
  BG_4bit_CNT bg_4bit_cnt_1 (
    .CLK1(RCLK1), .CLK2(RCLK2), .CIN(1'b1), .RES(1'b0), .LOAD(not_4_out), .OUT0(bg_4bit_cnt_1_out0),
    .VAL0(undriven_6[0]), .VAL1(undriven_6[1]), .VAL2(undriven_6[2]), .VAL3(not_5_out),
    .OUT1(bg_4bit_cnt_1_out1), .OUT2(bg_4bit_cnt_1_out2), .OUT3(bg_4bit_cnt_1_out3));
  D_Latch d_latch_14 (.in_1(RCLK2), .in_2(d_latch_7_out_4), .out_4(d_latch_14_out_4));  // open: out_3
  D_Latch d_latch_15 (.in_1(RCLK2), .in_2(d_latch_8_out_4), .out_4(d_latch_15_out_4));  // open: out_3
  BG_4bit_CNT bg_4bit_cnt_2 (
    .CLK1(RCLK1), .CLK2(RCLK2), .CIN(1'b1), .RES(1'b0), .LOAD(not_7_out), .OUT0(bg_4bit_cnt_2_out0),
    .VAL0(d_latch_1_out_3), .VAL1(d_latch_2_out_3), .VAL2(d_latch_3_out_3), .VAL3(d_latch_4_out_3),
    .OUT1(bg_4bit_cnt_2_out1), .OUT2(bg_4bit_cnt_2_out2), .OUT3(bg_4bit_cnt_2_out3));
  D_Latch d_latch_16 (.in_1(RCLK2), .in_2(d_latch_9_out_4), .out_4(d_latch_16_out_4));  // open: out_3
  D_Latch d_latch_17 (.in_1(RCLK2), .out_4(d_latch_17_out_4));  // open: in_2, out_3
  D_Latch d_latch_18 (.in_1(RCLK2), .in_2(d_latch_11_out_4), .out_4(d_latch_18_out_4));  // open: out_3
  nand _726 (_726_out, RCLK1, not_8_out);
  nand _725 (_725_out, RCLK1, d_latch_13_out_4);
  nand _728 (_728_out, RCLK1, not_9_out);
  nand _730 (_730_out, RCLK1, d_latch_15_out_4);
  not not_11 (not_11_out, M5);
  or _671 (_671_out, not_11_out, bg_4bit_cnt_2_out3);
  nand _700 (_700_out, bg_4bit_cnt_1_out0, bg_4bit_cnt_1_out1, bg_4bit_cnt_1_out2, bg_4bit_cnt_1_out3);
  and _647 (_647_out, _671_out, bg_4bit_cnt_2_out0, bg_4bit_cnt_2_out1, bg_4bit_cnt_2_out2);
  D_Latch d_latch_19 (.in_1(DCLK2), .in_2(d_latch_33_out_4), .out_4(d_latch_19_out_4));  // open: out_3
  D_Latch d_latch_20 (.in_1(DCLK2), .in_2(d_latch_34_out_4), .out_4(d_latch_20_out_4));  // open: out_3
  D_Latch d_latch_21 (.in_1(DCLK2), .in_2(d_latch_35_out_4), .out_4(d_latch_21_out_4));  // open: out_3
  D_Latch d_latch_22 (.in_1(DCLK2), .in_2(d_latch_37_out_4), .out_4(d_latch_22_out_4));  // open: out_3
  D_Latch d_latch_23 (.in_1(DCLK2), .in_2(d_latch_38_out_4), .out_4(d_latch_23_out_4));  // open: out_3
  D_Latch d_latch_24 (.in_1(DCLK2), .in_2(d_latch_39_out_4), .out_4(d_latch_24_out_4));  // open: out_3
  D_Latch d_latch_25 (.in_1(DCLK2), .in_2(d_latch_40_out_4), .out_4(d_latch_25_out_4));  // open: out_3
  D_Latch d_latch_26 (.in_1(DCLK2), .in_2(d_latch_43_out_4), .out_4(d_latch_26_out_4));  // open: out_3
  D_Latch d_latch_27 (.in_1(DCLK2), .in_2(d_latch_44_out_4), .out_4(d_latch_27_out_4));  // open: out_3
  D_Latch d_latch_28 (.in_1(DCLK2), .in_2(d_latch_45_out_4), .out_4(d_latch_28_out_4));  // open: out_3
  D_Latch d_latch_29 (.in_1(DCLK2), .in_2(d_latch_47_out_4), .out_4(d_latch_29_out_4));  // open: out_3
  D_Latch d_latch_30 (.in_1(DCLK2), .in_2(d_latch_48_out_4), .out_4(d_latch_30_out_4));  // open: out_3
  D_Latch d_latch_31 (.in_1(DCLK2), .in_2(d_latch_49_out_4), .out_4(d_latch_31_out_4));  // open: out_3
  D_Latch d_latch_32 (.in_1(DCLK2), .in_2(d_latch_50_out_4), .out_4(d_latch_32_out_4));  // open: out_3
  nor _729 (_729_out, _641_out, _647_out);
  D_Latch d_latch_33 (.in_1(DCLK1), .in_2(_726_out), .out_4(d_latch_33_out_4));  // open: out_3
  D_Latch d_latch_34 (.in_1(DCLK1), .in_2(d_latch_19_out_4), .out_4(d_latch_34_out_4));  // open: out_3
  D_Latch d_latch_35 (.in_1(DCLK1), .in_2(d_latch_20_out_4), .out_4(d_latch_35_out_4));  // open: out_3
  D_Latch d_latch_36 (.in_1(DCLK1), .in_2(d_latch_21_out_4), .out_4(d_latch_36_out_4));  // open: out_3
  D_Latch d_latch_37 (.in_1(DCLK1), .in_2(_725_out), .out_4(d_latch_37_out_4));  // open: out_3
  D_Latch d_latch_38 (.in_1(DCLK1), .in_2(d_latch_22_out_4), .out_4(d_latch_38_out_4));  // open: out_3
  D_Latch d_latch_39 (.in_1(DCLK1), .in_2(d_latch_23_out_4), .out_4(d_latch_39_out_4));  // open: out_3
  D_Latch d_latch_40 (.in_1(DCLK1), .in_2(d_latch_24_out_4), .out_4(d_latch_40_out_4));  // open: out_3
  D_Latch d_latch_41 (.in_1(DCLK1), .in_2(d_latch_25_out_4), .out_4(d_latch_41_out_4));  // open: out_3
  D_Latch d_latch_42 (.in_1(RCLK1), .in_2(_700_out), .out_4(d_latch_42_out_4));  // open: out_3
  D_Latch d_latch_43 (.in_1(DCLK1), .in_2(_728_out), .out_4(d_latch_43_out_4));  // open: out_3
  D_Latch d_latch_44 (.in_1(DCLK1), .in_2(d_latch_26_out_4), .out_4(d_latch_44_out_4));  // open: out_3
  D_Latch d_latch_45 (.in_1(DCLK1), .in_2(d_latch_27_out_4), .out_4(d_latch_45_out_4));  // open: out_3
  D_Latch d_latch_46 (.in_1(DCLK1), .in_2(d_latch_28_out_4), .out_4(d_latch_46_out_4));  // open: out_3
  D_Latch d_latch_47 (.in_1(DCLK1), .in_2(_730_out), .out_4(d_latch_47_out_4));  // open: out_3
  D_Latch d_latch_48 (.in_1(DCLK1), .in_2(d_latch_29_out_4), .out_4(d_latch_48_out_4));  // open: out_3
  D_Latch d_latch_49 (.in_1(DCLK1), .in_2(d_latch_30_out_4), .out_4(d_latch_49_out_4));  // open: out_3
  D_Latch d_latch_50 (.in_1(DCLK1), .in_2(d_latch_31_out_4), .out_4(d_latch_50_out_4));  // open: out_3
  D_Latch d_latch_51 (.in_1(DCLK1), .in_2(d_latch_32_out_4), .out_4(d_latch_51_out_4));  // open: out_3
  D_Latch d_latch_52 (.in_1(RCLK1), .in_2(_729_out), .out_4(d_latch_52_out_4));  // open: out_3
  Multiplexer #(.disabled(0), .enable("false")) multiplexer_1 (
    .in0(d_latch_51_out_4), .in1(d_latch_41_out_4), .out(multiplexer_1_out), .sel(M5));
  xor _524 (_524_out, M5, bg_4bit_cnt_2_out1);
  and _660 (_660_out, d_latch_33_out_4, DCLK2);
  and _661 (_661_out, d_latch_34_out_4, DCLK2);
  and _662 (_662_out, d_latch_35_out_4, DCLK2);
  and _663 (_663_out, d_latch_36_out_4, DCLK2);
  and _680 (_680_out, d_latch_37_out_4, DCLK2);
  and _682 (_682_out, d_latch_38_out_4, DCLK2);
  and _683 (_683_out, d_latch_39_out_4, DCLK2);
  and _684 (_684_out, d_latch_40_out_4, DCLK2);
  and _686 (_686_out, DCLK2, d_latch_41_out_4);
  and _668 (_668_out, RCLK2, d_latch_42_out_4);
  and _667 (_667_out, d_latch_43_out_4, DCLK2);
  and _666 (_666_out, d_latch_44_out_4, DCLK2);
  and _665 (_665_out, d_latch_45_out_4, DCLK2);
  and _664 (_664_out, d_latch_46_out_4, DCLK2);
  and _673 (_673_out, d_latch_47_out_4, DCLK2);
  and _674 (_674_out, d_latch_48_out_4, DCLK2);
  and _675 (_675_out, d_latch_49_out_4, DCLK2);
  and _676 (_676_out, d_latch_50_out_4, DCLK2);
  and _672 (_672_out, DCLK2, multiplexer_1_out);
  and _670 (_670_out, RCLK2, d_latch_52_out_4);
  and _677 (_677_out, M5, bg_4bit_cnt_2_out3);
  BG_PIPELINE_1 bg_pipeline_1_1 (
    .EN3(_668_out), .EN2(_686_out), .EN10(_663_out), .EN11(_662_out), .EN12(_661_out), .EN13(_660_out),
    .IN(SD_VRAM_DATA_LATCHED), .SEL(decoder_1_out0), .OUT3(bg_pipeline_1_1_out3),
    .OUT2(bg_pipeline_1_1_out2), .OU1(bg_pipeline_1_1_ou1), .OUT0(bg_pipeline_1_1_out0));
  BG_PIPELINE_1 bg_pipeline_1_2 (
    .EN3(_668_out), .EN2(_686_out), .EN10(_684_out), .EN11(_683_out), .EN12(_682_out), .EN13(_680_out),
    .IN(SD_VRAM_DATA_LATCHED), .SEL(decoder_1_out0), .OUT3(bg_pipeline_1_2_out3),
    .OUT2(bg_pipeline_1_2_out2), .OU1(bg_pipeline_1_2_ou1), .OUT0(bg_pipeline_1_2_out0));
  not not_12 (not_12_out, bg_4bit_cnt_2_out3);
  BG_PIPELINE_2 bg_pipeline_2_1 (
    .EN3(_670_out), .EN2(_672_out), .EN10(_664_out), .EN11(_665_out), .EN12(_666_out), .EN13(_667_out),
    .IN(SD_VRAM_DATA_LATCHED), .SEL(decoder_2_out0), .OUT0(bg_pipeline_2_1_out0[0]),
    .OU1(bg_pipeline_2_1_out0[1]), .OUT2(bg_pipeline_2_1_out0[2]), .OUT3(bg_pipeline_2_1_out0[3]),
    .OUT4(bg_pipeline_2_1_out0[4]), .OUT5(bg_pipeline_2_1_out0[5]));
  BG_PIPELINE_2 bg_pipeline_2_2 (
    .EN3(_670_out), .EN2(_672_out), .EN10(_676_out), .EN11(_675_out), .EN12(_674_out), .EN13(_673_out),
    .IN(SD_VRAM_DATA_LATCHED), .SEL(decoder_2_out0), .OUT0(bg_pipeline_2_1_out0[6]),
    .OU1(bg_pipeline_2_1_out0[7]), .OUT2(bg_pipeline_2_1_out0[8]), .OUT3(bg_pipeline_2_1_out0[9]),
    .OUT4(bg_pipeline_2_1_out0[10]), .OUT5(bg_pipeline_2_1_out0[11]));
  Decoder #(.select(3), .disabled(0), .enable("false")) decoder_1 (
    .out0(decoder_1_out0[0]), .out1(decoder_1_out0[1]), .out2(decoder_1_out0[2]), .out3(decoder_1_out0[3]),
    .out4(decoder_1_out0[4]), .out5(decoder_1_out0[5]), .out6(decoder_1_out0[6]), .out7(decoder_1_out0[7]),
    .sel(_626_out));
  xor _497 (_497_out, bg_4bit_cnt_1_out1, multiplexer_9_out);
  xor _496 (_626_out[1], bg_4bit_cnt_1_out2, multiplexer_9_out);
  xor _498 (_626_out[2], bg_4bit_cnt_1_out0, multiplexer_9_out);
  nand _731 (_731_out, M5, bg_4bit_cnt_2_out3);
  nand _732 (_732_out, M5, not_12_out);
  Decoder #(.select(3), .disabled(0), .enable("false")) decoder_2 (
    .out0(decoder_2_out0[0]), .out1(decoder_2_out0[1]), .out2(decoder_2_out0[2]), .out3(decoder_2_out0[3]),
    .out4(decoder_2_out0[4]), .out5(decoder_2_out0[5]), .out6(decoder_2_out0[6]), .out7(decoder_2_out0[7]),
    .sel(_518_out));
  xor _626 (_626_out[0], 1'b1, _497_out);
  not not_13 (not_13_out, _731_out);
  not not_14 (not_14_out, _732_out);
  not not_15 (not_15_out, M5);
  xor _519 (_518_out[2], bg_4bit_cnt_2_out0, multiplexer_13_out);
  xor _518 (_518_out[0], _524_out, multiplexer_13_out);
  xor _517 (_518_out[1], bg_4bit_cnt_2_out2, multiplexer_13_out);
  D_Latch d_latch_53 (.in_1(_686_out), .in_2(undriven_7[0]), .out_3(d_latch_53_out_3));  // open: out_4
  D_Latch d_latch_54 (.in_1(_686_out), .in_2(undriven_7[1]), .out_3(d_latch_54_out_3));  // open: out_4
  D_Latch d_latch_55 (.in_1(_686_out), .in_2(undriven_7[2]), .out_3(d_latch_55_out_3));  // open: out_4
  D_Latch d_latch_56 (.in_1(_686_out), .in_2(undriven_7[3]), .out_3(d_latch_56_out_3));  // open: out_4
  D_Latch d_latch_57 (.in_1(_686_out), .in_2(undriven_7[4]), .out_3(d_latch_57_out_3));  // open: out_4
  D_Latch d_latch_58 (.in_1(_686_out), .in_2(undriven_7[5]), .out_3(d_latch_58_out_3));  // open: out_4
  D_Latch d_latch_59 (.in_1(_686_out), .in_2(undriven_7[6]), .out_3(d_latch_59_out_3));  // open: out_4
  D_Latch d_latch_60 (.in_1(_686_out), .in_2(undriven_7[7]), .out_3(d_latch_60_out_3));  // open: out_4
  D_Latch d_latch_61 (.in_1(_676_out), .in_2(undriven_7[0]), .out_3(d_latch_61_out_3));  // open: out_4
  D_Latch d_latch_62 (.in_1(_676_out), .in_2(undriven_7[1]), .out_3(d_latch_62_out_3));  // open: out_4
  D_Latch d_latch_63 (.in_1(_676_out), .in_2(undriven_7[2]), .out_3(d_latch_63_out_3));  // open: out_4
  D_Latch d_latch_64 (.in_1(_676_out), .in_2(undriven_7[3]), .out_3(d_latch_64_out_3));  // open: out_4
  D_Latch d_latch_65 (.in_1(_676_out), .in_2(undriven_7[4]), .out_3(d_latch_65_out_3));  // open: out_4
  D_Latch d_latch_66 (.in_1(_676_out), .in_2(undriven_7[5]), .out_3(d_latch_66_out_3));  // open: out_4
  D_Latch d_latch_67 (.in_1(_676_out), .in_2(undriven_7[6]), .out_3(d_latch_67_out_3));  // open: out_4
  D_Latch d_latch_68 (.in_1(_676_out), .in_2(undriven_7[7]), .out_3(d_latch_68_out_3));  // open: out_4
  D_Latch d_latch_69 (.in_1(undriven_8), .in_2(undriven_7[0]));  // open: out_3, out_4
  D_Latch d_latch_70 (.in_1(undriven_8), .in_2(undriven_7[1]));  // open: out_3, out_4
  D_Latch d_latch_71 (.in_1(undriven_8), .in_2(undriven_7[2]));  // open: out_3, out_4
  D_Latch d_latch_72 (.in_1(undriven_8), .in_2(undriven_7[3]));  // open: out_3, out_4
  D_Latch d_latch_73 (.in_1(undriven_8), .in_2(undriven_7[4]));  // open: out_3, out_4
  D_Latch d_latch_74 (.in_1(undriven_8), .in_2(undriven_7[5]));  // open: out_3, out_4
  D_Latch d_latch_75 (.in_1(undriven_8), .in_2(undriven_7[6]));  // open: out_3, out_4
  D_Latch d_latch_76 (.in_1(undriven_8), .in_2(undriven_7[7]));  // open: out_3, out_4
  D_Latch d_latch_77 (.in_1(undriven_9), .in_2(undriven_7[0]));  // open: out_3, out_4
  D_Latch d_latch_78 (.in_1(undriven_9), .in_2(undriven_7[1]));  // open: out_3, out_4
  D_Latch d_latch_79 (.in_1(undriven_9), .in_2(undriven_7[2]));  // open: out_3, out_4
  D_Latch d_latch_80 (.in_1(undriven_9), .in_2(undriven_7[3]));  // open: out_3, out_4
  D_Latch d_latch_81 (.in_1(undriven_9), .in_2(undriven_7[4]));  // open: out_3, out_4
  D_Latch d_latch_82 (.in_1(undriven_9), .in_2(undriven_7[5]));  // open: out_3, out_4
  D_Latch d_latch_83 (.in_1(undriven_9), .in_2(undriven_7[6]));  // open: out_3, out_4
  D_Latch d_latch_84 (.in_1(undriven_9), .in_2(undriven_7[7]));  // open: out_3, out_4
  D_Latch d_latch_85 (.in_1(undriven_10), .in_2(undriven_7[0]));  // open: out_3, out_4
  D_Latch d_latch_86 (.in_1(undriven_10), .in_2(undriven_7[1]));  // open: out_3, out_4
  D_Latch d_latch_87 (.in_1(undriven_10), .in_2(undriven_7[2]));  // open: out_3, out_4
  D_Latch d_latch_88 (.in_1(undriven_10), .in_2(undriven_7[3]));  // open: out_3, out_4
  D_Latch d_latch_89 (.in_1(undriven_10), .in_2(undriven_7[4]));  // open: out_3, out_4
  D_Latch d_latch_90 (.in_1(undriven_10), .in_2(undriven_7[5]));  // open: out_3, out_4
  D_Latch d_latch_91 (.in_1(undriven_10), .in_2(undriven_7[6]));  // open: out_3, out_4
  D_Latch d_latch_92 (.in_1(undriven_10), .in_2(undriven_7[7]));  // open: out_3, out_4
  D_Latch d_latch_93 (.in_1(_668_out), .in_2(d_latch_53_out_3), .out_3(d_latch_93_out_3));  // open: out_4
  D_Latch d_latch_94 (.in_1(_668_out), .in_2(d_latch_54_out_3), .out_3(d_latch_94_out_3));  // open: out_4
  D_Latch d_latch_95 (.in_1(_668_out), .in_2(d_latch_55_out_3), .out_3(d_latch_95_out_3));  // open: out_4
  D_Latch d_latch_96 (.in_1(_668_out), .in_2(d_latch_56_out_3), .out_3(d_latch_96_out_3));  // open: out_4
  D_Latch d_latch_97 (.in_1(_668_out), .in_2(d_latch_57_out_3), .out_3(d_latch_97_out_3));  // open: out_4
  D_Latch d_latch_98 (.in_1(_668_out), .in_2(d_latch_58_out_3), .out_3(d_latch_98_out_3));  // open: out_4
  D_Latch d_latch_99 (.in_1(_668_out), .in_2(d_latch_59_out_3), .out_3(d_latch_99_out_3));  // open: out_4
  D_Latch d_latch_100 (.in_1(_668_out), .in_2(d_latch_60_out_3), .out_3(d_latch_100_out_3));  // open: out_4
  not not_16 (not_16_out, not_17_out);
  not not_17 (not_17_out, bg_4bit_cnt_1_out3);
  and _640 (_640_out, bg_pipeline_2_1_out0[6], not_13_out);
  and _640_2 (_640_2_out, bg_pipeline_2_1_out0[0], not_14_out);
  and _640_3 (_640_3_out, bg_pipeline_2_1_out0[10], not_15_out);
  and _637 (_637_out, bg_pipeline_2_1_out0[7], not_13_out);
  and _637_2 (_637_2_out, bg_pipeline_2_1_out0[1], not_14_out);
  and _637_3 (_637_3_out, bg_pipeline_2_1_out0[11], not_15_out);
  and _639 (_639_out, bg_pipeline_2_1_out0[8], not_13_out);
  and _639_2 (_639_2_out, bg_pipeline_2_1_out0[2], not_14_out);
  and _639_3 (_639_3_out, bg_pipeline_2_1_out0[4], not_15_out);
  and _638 (_638_out, bg_pipeline_2_1_out0[9], not_13_out);
  and _638_2 (_638_2_out, bg_pipeline_2_1_out0[3], not_14_out);
  and _638_3 (_638_3_out, bg_pipeline_2_1_out0[5], not_15_out);
  D_Latch d_latch_101 (.in_1(_672_out), .in_2(d_latch_61_out_3), .out_3(d_latch_101_out_3));  // open: out_4
  D_Latch d_latch_102 (.in_1(_672_out), .in_2(d_latch_62_out_3), .out_3(d_latch_102_out_3));  // open: out_4
  D_Latch d_latch_103 (.in_1(_672_out), .in_2(d_latch_63_out_3), .out_3(d_latch_103_out_3));  // open: out_4
  D_Latch d_latch_104 (.in_1(_672_out), .in_2(d_latch_64_out_3), .out_3(d_latch_104_out_3));  // open: out_4
  D_Latch d_latch_105 (.in_1(_672_out), .in_2(d_latch_65_out_3), .out_3(d_latch_105_out_3));  // open: out_4
  D_Latch d_latch_106 (.in_1(_672_out), .in_2(d_latch_66_out_3), .out_3(d_latch_106_out_3));  // open: out_4
  D_Latch d_latch_107 (.in_1(_672_out), .in_2(d_latch_67_out_3), .out_3(d_latch_107_out_3));  // open: out_4
  D_Latch d_latch_108 (.in_1(_672_out), .in_2(d_latch_68_out_3), .out_3(d_latch_108_out_3));  // open: out_4
  Multiplexer #(.disabled(0), .enable("false")) multiplexer_2 (
    .in0(bg_pipeline_1_1_out3), .in1(bg_pipeline_1_2_out3), .out(multiplexer_2_out), .sel(not_16_out));
  Multiplexer #(.disabled(0), .enable("false")) multiplexer_3 (
    .in0(bg_pipeline_1_1_out2), .in1(bg_pipeline_1_2_out2), .out(multiplexer_3_out), .sel(not_16_out));
  Multiplexer #(.disabled(0), .enable("false")) multiplexer_4 (
    .in0(bg_pipeline_1_1_ou1), .in1(bg_pipeline_1_2_ou1), .out(multiplexer_4_out), .sel(not_16_out));
  Multiplexer #(.disabled(0), .enable("false")) multiplexer_5 (
    .in0(bg_pipeline_1_1_out0), .in1(bg_pipeline_1_2_out0), .out(multiplexer_5_out), .sel(not_16_out));
  Multiplexer #(.disabled(0), .enable("false")) multiplexer_6 (
    .in0(d_latch_93_out_3), .in1(d_latch_94_out_3), .out(multiplexer_6_out), .sel(not_16_out));
  Multiplexer #(.disabled(0), .enable("false")) multiplexer_7 (
    .in0(d_latch_95_out_3), .in1(d_latch_96_out_3), .out(multiplexer_7_out), .sel(not_16_out));
  Multiplexer #(.disabled(0), .enable("false")) multiplexer_8 (
    .in0(d_latch_97_out_3), .in1(d_latch_98_out_3), .out(multiplexer_8_out), .sel(not_16_out));
  Multiplexer #(.disabled(0), .enable("false")) multiplexer_9 (
    .in0(d_latch_99_out_3), .in1(d_latch_100_out_3), .out(multiplexer_9_out), .sel(not_16_out));
  or _640_4 (_640_4_out, _640_out, _640_2_out, _640_3_out);
  or _637_4 (_637_4_out, _637_out, _637_2_out, _637_3_out);
  or _639_4 (_639_4_out, _639_out, _639_2_out, _639_3_out);
  or _638_4 (_638_4_out, _638_out, _638_2_out, _638_3_out);
  D_Latch d_latch_109 (.in_1(_670_out), .in_2(d_latch_101_out_3), .out_3(d_latch_109_out_3));  // open: out_4
  D_Latch d_latch_110 (.in_1(_670_out), .in_2(d_latch_102_out_3), .out_3(d_latch_110_out_3));  // open: out_4
  D_Latch d_latch_111 (.in_1(_670_out), .in_2(d_latch_103_out_3), .out_3(d_latch_111_out_3));  // open: out_4
  D_Latch d_latch_112 (.in_1(_670_out), .in_2(d_latch_104_out_3), .out_3(d_latch_112_out_3));  // open: out_4
  D_Latch d_latch_113 (.in_1(_670_out), .in_2(d_latch_105_out_3), .out_3(d_latch_113_out_3));  // open: out_4
  D_Latch d_latch_114 (.in_1(_670_out), .in_2(d_latch_106_out_3), .out_3(d_latch_114_out_3));  // open: out_4
  D_Latch d_latch_115 (.in_1(_670_out), .in_2(d_latch_107_out_3), .out_3(d_latch_115_out_3));  // open: out_4
  D_Latch d_latch_116 (.in_1(_670_out), .in_2(d_latch_108_out_3), .out_3(d_latch_116_out_3));  // open: out_4
  Multiplexer #(.disabled(0), .enable("false")) multiplexer_10 (
    .in0(d_latch_109_out_3), .in1(d_latch_110_out_3), .out(multiplexer_10_out), .sel(_677_out));
  Multiplexer #(.disabled(0), .enable("false")) multiplexer_11 (
    .in0(d_latch_111_out_3), .in1(d_latch_112_out_3), .out(multiplexer_11_out), .sel(_677_out));
  Multiplexer #(.disabled(0), .enable("false")) multiplexer_12 (
    .in0(d_latch_113_out_3), .in1(d_latch_114_out_3), .out(multiplexer_12_out), .sel(_677_out));
  Multiplexer #(.disabled(0), .enable("false")) multiplexer_13 (
    .in0(d_latch_115_out_3), .in1(d_latch_116_out_3), .out(multiplexer_13_out), .sel(_677_out));
  D_Latch d_latch_117 (.in_1(RCLK1), .in_2(multiplexer_2_out), .out_4(d_latch_117_out_4));  // open: out_3
  D_Latch d_latch_118 (.in_1(RCLK1), .in_2(multiplexer_3_out), .out_4(d_latch_118_out_4));  // open: out_3
  D_Latch d_latch_119 (.in_1(RCLK1), .in_2(multiplexer_4_out), .out_4(d_latch_119_out_4));  // open: out_3
  D_Latch d_latch_120 (.in_1(RCLK1), .in_2(multiplexer_5_out), .out_4(d_latch_120_out_4));  // open: out_3
  D_Latch d_latch_121 (.in_1(RCLK1), .in_2(multiplexer_6_out), .out_4(d_latch_121_out_4));  // open: out_3
  D_Latch d_latch_122 (.in_1(RCLK1), .in_2(multiplexer_7_out), .out_4(d_latch_122_out_4));  // open: out_3
  D_Latch d_latch_123 (.in_1(RCLK1), .in_2(multiplexer_8_out), .out_4(d_latch_123_out_4));  // open: out_3
  D_Latch d_latch_124 (.in_1(RCLK1), .in_2(_640_4_out), .out_4(d_latch_124_out_4));  // open: out_3
  D_Latch d_latch_125 (.in_1(RCLK1), .in_2(_637_4_out), .out_4(d_latch_125_out_4));  // open: out_3
  D_Latch d_latch_126 (.in_1(RCLK1), .in_2(_639_4_out), .out_4(d_latch_126_out_4));  // open: out_3
  D_Latch d_latch_127 (.in_1(RCLK1), .in_2(_638_4_out), .out_4(d_latch_127_out_4));  // open: out_3
  D_Latch d_latch_128 (.in_1(RCLK1), .in_2(multiplexer_10_out), .out_4(d_latch_128_out_4));  // open: out_3
  D_Latch d_latch_129 (.in_1(RCLK1), .in_2(multiplexer_11_out), .out_4(d_latch_129_out_4));  // open: out_3
  D_Latch d_latch_130 (.in_1(RCLK1), .in_2(multiplexer_12_out), .out_4(d_latch_130_out_4));  // open: out_3
  D_Latch d_latch_131 (.in_1(RCLK2), .in_2(d_latch_117_out_4), .out_4(d_latch_131_out_4));  // open: out_3
  D_Latch d_latch_132 (.in_1(RCLK2), .in_2(d_latch_118_out_4), .out_4(d_latch_132_out_4));  // open: out_3
  D_Latch d_latch_133 (.in_1(RCLK2), .in_2(d_latch_119_out_4), .out_4(d_latch_133_out_4));  // open: out_3
  D_Latch d_latch_134 (.in_1(RCLK2), .in_2(d_latch_120_out_4), .out_4(d_latch_134_out_4));  // open: out_3
  D_Latch d_latch_135 (.in_1(RCLK2), .in_2(d_latch_121_out_4), .out_4(d_latch_135_out_4));  // open: out_3
  D_Latch d_latch_136 (.in_1(RCLK2), .in_2(d_latch_122_out_4), .out_4(d_latch_136_out_4));  // open: out_3
  D_Latch d_latch_137 (.in_1(RCLK2), .in_2(d_latch_123_out_4), .out_4(d_latch_137_out_4));  // open: out_3
  D_Latch d_latch_138 (.in_1(RCLK2), .in_2(d_latch_124_out_4), .out_4(d_latch_138_out_4));  // open: out_3
  D_Latch d_latch_139 (.in_1(RCLK2), .in_2(d_latch_125_out_4), .out_4(d_latch_139_out_4));  // open: out_3
  D_Latch d_latch_140 (.in_1(RCLK2), .in_2(d_latch_126_out_4), .out_4(d_latch_140_out_4));  // open: out_3
  D_Latch d_latch_141 (.in_1(RCLK2), .in_2(d_latch_127_out_4), .out_4(d_latch_141_out_4));  // open: out_3
  D_Latch d_latch_142 (.in_1(RCLK2), .in_2(d_latch_128_out_4), .out_4(d_latch_142_out_4));  // open: out_3
  D_Latch d_latch_143 (.in_1(RCLK2), .in_2(d_latch_129_out_4), .out_4(d_latch_143_out_4));  // open: out_3
  D_Latch d_latch_144 (.in_1(RCLK2), .in_2(d_latch_130_out_4), .out_4(d_latch_144_out_4));  // open: out_3
  not not_18 (not_18_out, in_3);
  or _690 (_20, d_latch_134_out_4, d_latch_133_out_4, d_latch_132_out_4, d_latch_131_out_4);
  not not_19 (not_19_out, _63);
  or _693 (_73, d_latch_141_out_4, d_latch_140_out_4, d_latch_139_out_4, d_latch_138_out_4);
  D_Latch d_latch_145 (.in_1(RCLK1), .in_2(d_latch_131_out_4), .out_4(d_latch_145_out_4));  // open: out_3
  D_Latch d_latch_146 (.in_1(RCLK1), .in_2(d_latch_132_out_4), .out_4(d_latch_146_out_4));  // open: out_3
  D_Latch d_latch_147 (.in_1(RCLK1), .in_2(d_latch_133_out_4), .out_4(d_latch_147_out_4));  // open: out_3
  D_Latch d_latch_148 (.in_1(RCLK1), .in_2(d_latch_134_out_4), .out_4(d_latch_148_out_4));  // open: out_3
  D_Latch d_latch_149 (.in_1(RCLK1), .in_2(d_latch_135_out_4), .out_4(d_latch_149_out_4));  // open: out_3
  D_Latch d_latch_150 (.in_1(RCLK1), .in_2(d_latch_136_out_4), .out_4(d_latch_150_out_4));  // open: out_3
  D_Latch d_latch_151 (.in_1(RCLK1), .in_2(d_latch_137_out_4), .out_4(d_latch_151_out_4));  // open: out_3
  D_Latch d_latch_152 (.in_1(RCLK1), .in_2(d_latch_138_out_4), .out_4(d_latch_152_out_4));  // open: out_3
  D_Latch d_latch_153 (.in_1(RCLK1), .in_2(d_latch_139_out_4), .out_4(d_latch_153_out_4));  // open: out_3
  D_Latch d_latch_154 (.in_1(RCLK1), .in_2(d_latch_140_out_4), .out_4(d_latch_154_out_4));  // open: out_3
  D_Latch d_latch_155 (.in_1(RCLK1), .in_2(d_latch_141_out_4), .out_4(d_latch_155_out_4));  // open: out_3
  D_Latch d_latch_156 (.in_1(RCLK1), .in_2(d_latch_142_out_4), .out_4(d_latch_156_out_4));  // open: out_3
  D_Latch d_latch_157 (.in_1(RCLK1), .in_2(d_latch_143_out_4), .out_4(d_latch_157_out_4));  // open: out_3
  D_Latch d_latch_158 (.in_1(RCLK1), .in_2(d_latch_144_out_4), .out_4(d_latch_158_out_4));  // open: out_3
  D_Latch d_latch_159 (.in_1(RCLK2), .in_2(d_latch_145_out_4), .out_4(d_latch_159_out_4));  // open: out_3
  D_Latch d_latch_160 (.in_1(RCLK2), .in_2(d_latch_146_out_4), .out_4(d_latch_160_out_4));  // open: out_3
  D_Latch d_latch_161 (.in_1(RCLK2), .in_2(d_latch_147_out_4), .out_4(d_latch_161_out_4));  // open: out_3
  D_Latch d_latch_162 (.in_1(RCLK2), .in_2(d_latch_148_out_4), .out_4(d_latch_162_out_4));  // open: out_3
  D_Latch d_latch_163 (.in_1(RCLK2), .in_2(d_latch_149_out_4), .out_4(d_latch_163_out_4));  // open: out_3
  D_Latch d_latch_164 (.in_1(RCLK2), .in_2(d_latch_150_out_4), .out_4(d_latch_164_out_4));  // open: out_3
  D_Latch d_latch_165 (.in_1(RCLK2), .in_2(d_latch_151_out_4), .out_4(d_latch_165_out_4));  // open: out_3
  D_Latch d_latch_166 (.in_1(RCLK2), .in_2(d_latch_152_out_4), .out_4(d_latch_166_out_4));  // open: out_3
  D_Latch d_latch_167 (.in_1(RCLK2), .in_2(d_latch_153_out_4), .out_4(d_latch_167_out_4));  // open: out_3
  D_Latch d_latch_168 (.in_1(RCLK2), .in_2(d_latch_154_out_4), .out_4(d_latch_168_out_4));  // open: out_3
  D_Latch d_latch_169 (.in_1(RCLK2), .in_2(d_latch_155_out_4), .out_4(d_latch_169_out_4));  // open: out_3
  D_Latch d_latch_170 (.in_1(RCLK2), .in_2(d_latch_156_out_4), .out_4(d_latch_170_out_4));  // open: out_3
  D_Latch d_latch_171 (.in_1(RCLK2), .in_2(d_latch_157_out_4), .out_4(d_latch_171_out_4));  // open: out_3
  D_Latch d_latch_172 (.in_1(RCLK2), .in_2(d_latch_158_out_4), .out_4(d_latch_172_out_4));  // open: out_3
  assign PLANE_B_OUT[0] = not_18_out ? d_latch_159_out_4 : 1'bz;  // Controlled_Buffer controlled_buffer_1
  assign PLANE_B_OUT[1] = not_18_out ? d_latch_160_out_4 : 1'bz;  // Controlled_Buffer controlled_buffer_2
  assign PLANE_B_OUT[2] = not_18_out ? d_latch_161_out_4 : 1'bz;  // Controlled_Buffer controlled_buffer_3
  assign PLANE_B_OUT[3] = not_18_out ? d_latch_162_out_4 : 1'bz;  // Controlled_Buffer controlled_buffer_4
  assign PLANE_B_OUT[4] = not_18_out ? d_latch_163_out_4 : 1'bz;  // Controlled_Buffer controlled_buffer_5
  assign PLANE_B_OUT[5] = not_18_out ? d_latch_164_out_4 : 1'bz;  // Controlled_Buffer controlled_buffer_6
  assign PLANE_B_OUT[6] = not_18_out ? d_latch_165_out_4 : 1'bz;  // Controlled_Buffer controlled_buffer_7
  assign PLANE_A_OUT[0] = not_19_out ? d_latch_166_out_4 : 1'bz;  // Controlled_Buffer controlled_buffer_8
  assign PLANE_A_OUT[1] = not_19_out ? d_latch_167_out_4 : 1'bz;  // Controlled_Buffer controlled_buffer_9
  assign PLANE_A_OUT[2] = not_19_out ? d_latch_168_out_4 : 1'bz;  // Controlled_Buffer controlled_buffer_10
  assign PLANE_A_OUT[3] = not_19_out ? d_latch_169_out_4 : 1'bz;  // Controlled_Buffer controlled_buffer_11
  assign PLANE_A_OUT[4] = not_19_out ? d_latch_170_out_4 : 1'bz;  // Controlled_Buffer controlled_buffer_12
  assign PLANE_A_OUT[5] = not_19_out ? d_latch_171_out_4 : 1'bz;  // Controlled_Buffer controlled_buffer_13
  assign PLANE_A_OUT[6] = not_19_out ? d_latch_172_out_4 : 1'bz;  // Controlled_Buffer controlled_buffer_14

  // Notes on the sheet:
  //   578
  //   579
  //   653
  //   479
  //   478
  //   477
  //   476
  //   695
  //   AOI21
  //   651
  //   575
  //   AOI21
  //   694
  //   AOI21
  //   576
  //   624
  //   516
  //   515
  //   499
  //   501
  //   625
  //   500
  //   488-491
  //   654
  //   504
  //   503
  //   439
  //   440
  //   442
  //   441
  //   508
  //   509
  //   510
  //   511
  //   512
  //   513
  //   514
  //   655
  //   502
  //   520
  //   522
  //   526
  //   523
  //   443
  //   696
  //   646
  //   707
  //   PIPELINE 1
  //   PIPELINE 0
  //   705
  //   708
  //   PIPELINE 2
  //   PIPELINE 3
  //   706
  //   459
  //   458
  //   457
  //   456
  //   455
  //   454
  //   453
  //   452
  //   451
  //   450
  //   449
  //   448
  //   447
  //   446
  //   445
  //   444
  //   649
  //   650
  //   633
  //   636
  //   634
  //   635
  //   620
  //   621
  //   622
  //   623
  //   645
  //   642
  //   643
  //   644
  //   425
  //   419
  //   424
  //   428
  //   431
  //   429
  //   411
  //   408
  //   417
  //   413
  //   416
  //   422
  //   406
  //   409
  //   710
  //   709
  //   426
  //   420
  //   423
  //   421
  //   427
  //   432
  //   430
  //   412
  //   405
  //   410
  //   407
  //   418
  //   414
  //   415
  //   714
  //   715
  //   716
  //   717
  //   712
  //   711
  //   713
  //   721
  //   722
  //   723
  //   724
  //   719
  //   718
  //   720
endmodule

// BG PIPELINE
module BG_PIPELINE_1 (
  input  EN3,
  input  EN2,
  input  EN10,
  input  EN11,
  input  EN12,
  input  EN13,
  input  [7:0] IN,
  input  [7:0] SEL,
  output OUT0,
  output OU1,
  output OUT2,
  output OUT3
);

  wire _385_2_out, _385_3_out, _385_4_out, _385_5_out, _385_6_out, _385_7_out, _385_8_out, _385_out,
       _387_2_out, _387_3_out, _387_4_out, _387_5_out, _387_6_out, _387_7_out, _387_8_out, _387_out,
       _391_2_out, _391_3_out, _391_4_out, _391_5_out, _391_6_out, _391_7_out, _391_8_out, _391_out,
       _392_2_out, _392_3_out, _392_4_out, _392_5_out, _392_6_out, _392_7_out, _392_8_out, _392_out,
       d_latch_1_out_3, d_latch_2_out_3, d_latch_3_out_3, d_latch_4_out_3, d_latch_5_out_3, d_latch_6_out_3,
       d_latch_7_out_3, d_latch_8_out_3, d_latch_9_out_3, d_latch_10_out_3, d_latch_11_out_3,
       d_latch_12_out_3, d_latch_13_out_3, d_latch_14_out_3, d_latch_15_out_3, d_latch_16_out_3,
       d_latch_17_out_3, d_latch_18_out_3, d_latch_19_out_3, d_latch_20_out_3, d_latch_21_out_3,
       d_latch_22_out_3, d_latch_23_out_3, d_latch_24_out_3, d_latch_25_out_3, d_latch_26_out_3,
       d_latch_27_out_3, d_latch_28_out_3, d_latch_29_out_3, d_latch_30_out_3, d_latch_31_out_3,
       d_latch_32_out_3, d_latch_33_out_3, d_latch_34_out_3, d_latch_35_out_3, d_latch_36_out_3,
       d_latch_37_out_3, d_latch_38_out_3, d_latch_39_out_3, d_latch_40_out_3, d_latch_41_out_3,
       d_latch_42_out_3, d_latch_43_out_3, d_latch_44_out_3, d_latch_45_out_3, d_latch_46_out_3,
       d_latch_47_out_3, d_latch_48_out_3, d_latch_49_out_3, d_latch_50_out_3, d_latch_51_out_3,
       d_latch_52_out_3, d_latch_53_out_3, d_latch_54_out_3, d_latch_55_out_3, d_latch_56_out_3,
       d_latch_57_out_3, d_latch_58_out_3, d_latch_59_out_3, d_latch_60_out_3, d_latch_61_out_3,
       d_latch_62_out_3, d_latch_63_out_3, d_latch_64_out_3, d_latch_65_out_3, d_latch_66_out_3,
       d_latch_67_out_3, d_latch_68_out_3, d_latch_69_out_3, d_latch_70_out_3, d_latch_71_out_3,
       d_latch_72_out_3, d_latch_73_out_3, d_latch_74_out_3, d_latch_75_out_3, d_latch_76_out_3,
       d_latch_77_out_3, d_latch_78_out_3, d_latch_79_out_3, d_latch_80_out_3, d_latch_81_out_3,
       d_latch_82_out_3, d_latch_83_out_3, d_latch_84_out_3, d_latch_85_out_3, d_latch_86_out_3,
       d_latch_87_out_3, d_latch_88_out_3, d_latch_89_out_3, d_latch_90_out_3, d_latch_91_out_3,
       d_latch_92_out_3, d_latch_93_out_3, d_latch_94_out_3, d_latch_95_out_3, d_latch_96_out_3, not_1_out,
       not_2_out, not_3_out, not_4_out, not_5_out, not_6_out, not_7_out, not_8_out, not_9_out, not_10_out,
       not_11_out, not_12_out, not_13_out, not_14_out, not_15_out, not_16_out, not_17_out, not_18_out,
       not_19_out, not_20_out, not_21_out, not_22_out, not_23_out, not_24_out;

  not not_1 (not_1_out, EN3);
  not not_2 (not_2_out, EN3);
  not not_3 (not_3_out, EN3);
  not not_4 (not_4_out, EN3);
  not not_5 (not_5_out, EN2);
  not not_6 (not_6_out, EN2);
  not not_7 (not_7_out, EN2);
  not not_8 (not_8_out, EN2);
  not not_9 (not_9_out, EN10);
  not not_10 (not_10_out, EN11);
  not not_11 (not_11_out, EN12);
  not not_12 (not_12_out, EN13);
  not not_13 (not_13_out, not_1_out);
  not not_14 (not_14_out, not_2_out);
  not not_15 (not_15_out, not_3_out);
  not not_16 (not_16_out, not_4_out);
  not not_17 (not_17_out, not_5_out);
  not not_18 (not_18_out, not_6_out);
  not not_19 (not_19_out, not_7_out);
  not not_20 (not_20_out, not_8_out);
  not not_21 (not_21_out, not_9_out);
  not not_22 (not_22_out, not_10_out);
  not not_23 (not_23_out, not_11_out);
  not not_24 (not_24_out, not_12_out);
  D_Latch d_latch_1 (.in_1(not_21_out), .in_2(IN[3]), .out_3(d_latch_1_out_3));  // open: out_4
  D_Latch d_latch_2 (.in_1(not_22_out), .in_2(IN[3]), .out_3(d_latch_2_out_3));  // open: out_4
  D_Latch d_latch_3 (.in_1(not_23_out), .in_2(IN[3]), .out_3(d_latch_3_out_3));  // open: out_4
  D_Latch d_latch_4 (.in_1(not_24_out), .in_2(IN[3]), .out_3(d_latch_4_out_3));  // open: out_4
  D_Latch d_latch_5 (.in_1(not_21_out), .in_2(IN[7]), .out_3(d_latch_5_out_3));  // open: out_4
  D_Latch d_latch_6 (.in_1(not_22_out), .in_2(IN[7]), .out_3(d_latch_6_out_3));  // open: out_4
  D_Latch d_latch_7 (.in_1(not_23_out), .in_2(IN[7]), .out_3(d_latch_7_out_3));  // open: out_4
  D_Latch d_latch_8 (.in_1(not_24_out), .in_2(IN[7]), .out_3(d_latch_8_out_3));  // open: out_4
  D_Latch d_latch_9 (.in_1(not_21_out), .in_2(IN[2]), .out_3(d_latch_9_out_3));  // open: out_4
  D_Latch d_latch_10 (.in_1(not_22_out), .in_2(IN[2]), .out_3(d_latch_10_out_3));  // open: out_4
  D_Latch d_latch_11 (.in_1(not_23_out), .in_2(IN[2]), .out_3(d_latch_11_out_3));  // open: out_4
  D_Latch d_latch_12 (.in_1(not_24_out), .in_2(IN[2]), .out_3(d_latch_12_out_3));  // open: out_4
  D_Latch d_latch_13 (.in_1(not_21_out), .in_2(IN[6]), .out_3(d_latch_13_out_3));  // open: out_4
  D_Latch d_latch_14 (.in_1(not_22_out), .in_2(IN[6]), .out_3(d_latch_14_out_3));  // open: out_4
  D_Latch d_latch_15 (.in_1(not_23_out), .in_2(IN[6]), .out_3(d_latch_15_out_3));  // open: out_4
  D_Latch d_latch_16 (.in_1(not_24_out), .in_2(IN[6]), .out_3(d_latch_16_out_3));  // open: out_4
  D_Latch d_latch_17 (.in_1(not_21_out), .in_2(IN[1]), .out_3(d_latch_17_out_3));  // open: out_4
  D_Latch d_latch_18 (.in_1(not_22_out), .in_2(IN[1]), .out_3(d_latch_18_out_3));  // open: out_4
  D_Latch d_latch_19 (.in_1(not_23_out), .in_2(IN[1]), .out_3(d_latch_19_out_3));  // open: out_4
  D_Latch d_latch_20 (.in_1(not_24_out), .in_2(IN[1]), .out_3(d_latch_20_out_3));  // open: out_4
  D_Latch d_latch_21 (.in_1(not_21_out), .in_2(IN[5]), .out_3(d_latch_21_out_3));  // open: out_4
  D_Latch d_latch_22 (.in_1(not_22_out), .in_2(IN[5]), .out_3(d_latch_22_out_3));  // open: out_4
  D_Latch d_latch_23 (.in_1(not_23_out), .in_2(IN[5]), .out_3(d_latch_23_out_3));  // open: out_4
  D_Latch d_latch_24 (.in_1(not_24_out), .in_2(IN[5]), .out_3(d_latch_24_out_3));  // open: out_4
  D_Latch d_latch_25 (.in_1(not_21_out), .in_2(IN[0]), .out_3(d_latch_25_out_3));  // open: out_4
  D_Latch d_latch_26 (.in_1(not_22_out), .in_2(IN[0]), .out_3(d_latch_26_out_3));  // open: out_4
  D_Latch d_latch_27 (.in_1(not_23_out), .in_2(IN[0]), .out_3(d_latch_27_out_3));  // open: out_4
  D_Latch d_latch_28 (.in_1(not_24_out), .in_2(IN[0]), .out_3(d_latch_28_out_3));  // open: out_4
  D_Latch d_latch_29 (.in_1(not_21_out), .in_2(IN[4]), .out_3(d_latch_29_out_3));  // open: out_4
  D_Latch d_latch_30 (.in_1(not_22_out), .in_2(IN[4]), .out_3(d_latch_30_out_3));  // open: out_4
  D_Latch d_latch_31 (.in_1(not_23_out), .in_2(IN[4]), .out_3(d_latch_31_out_3));  // open: out_4
  D_Latch d_latch_32 (.in_1(not_24_out), .in_2(IN[4]), .out_3(d_latch_32_out_3));  // open: out_4
  D_Latch d_latch_33 (.in_1(not_20_out), .in_2(d_latch_1_out_3), .out_3(d_latch_33_out_3));  // open: out_4
  D_Latch d_latch_34 (.in_1(not_19_out), .in_2(d_latch_2_out_3), .out_3(d_latch_34_out_3));  // open: out_4
  D_Latch d_latch_35 (.in_1(not_18_out), .in_2(d_latch_3_out_3), .out_3(d_latch_35_out_3));  // open: out_4
  D_Latch d_latch_36 (.in_1(not_17_out), .in_2(d_latch_4_out_3), .out_3(d_latch_36_out_3));  // open: out_4
  D_Latch d_latch_37 (.in_1(not_20_out), .in_2(d_latch_5_out_3), .out_3(d_latch_37_out_3));  // open: out_4
  D_Latch d_latch_38 (.in_1(not_19_out), .in_2(d_latch_6_out_3), .out_3(d_latch_38_out_3));  // open: out_4
  D_Latch d_latch_39 (.in_1(not_18_out), .in_2(d_latch_7_out_3), .out_3(d_latch_39_out_3));  // open: out_4
  D_Latch d_latch_40 (.in_1(not_17_out), .in_2(d_latch_8_out_3), .out_3(d_latch_40_out_3));  // open: out_4
  D_Latch d_latch_41 (.in_1(not_20_out), .in_2(d_latch_9_out_3), .out_3(d_latch_41_out_3));  // open: out_4
  D_Latch d_latch_42 (.in_1(not_19_out), .in_2(d_latch_10_out_3), .out_3(d_latch_42_out_3));  // open: out_4
  D_Latch d_latch_43 (.in_1(not_18_out), .in_2(d_latch_11_out_3), .out_3(d_latch_43_out_3));  // open: out_4
  D_Latch d_latch_44 (.in_1(not_17_out), .in_2(d_latch_12_out_3), .out_3(d_latch_44_out_3));  // open: out_4
  D_Latch d_latch_45 (.in_1(not_20_out), .in_2(d_latch_13_out_3), .out_3(d_latch_45_out_3));  // open: out_4
  D_Latch d_latch_46 (.in_1(not_19_out), .in_2(d_latch_14_out_3), .out_3(d_latch_46_out_3));  // open: out_4
  D_Latch d_latch_47 (.in_1(not_18_out), .in_2(d_latch_15_out_3), .out_3(d_latch_47_out_3));  // open: out_4
  D_Latch d_latch_48 (.in_1(not_17_out), .in_2(d_latch_16_out_3), .out_3(d_latch_48_out_3));  // open: out_4
  D_Latch d_latch_49 (.in_1(not_20_out), .in_2(d_latch_17_out_3), .out_3(d_latch_49_out_3));  // open: out_4
  D_Latch d_latch_50 (.in_1(not_19_out), .in_2(d_latch_18_out_3), .out_3(d_latch_50_out_3));  // open: out_4
  D_Latch d_latch_51 (.in_1(not_18_out), .in_2(d_latch_19_out_3), .out_3(d_latch_51_out_3));  // open: out_4
  D_Latch d_latch_52 (.in_1(not_17_out), .in_2(d_latch_20_out_3), .out_3(d_latch_52_out_3));  // open: out_4
  D_Latch d_latch_53 (.in_1(not_20_out), .in_2(d_latch_21_out_3), .out_3(d_latch_53_out_3));  // open: out_4
  D_Latch d_latch_54 (.in_1(not_19_out), .in_2(d_latch_22_out_3), .out_3(d_latch_54_out_3));  // open: out_4
  D_Latch d_latch_55 (.in_1(not_18_out), .in_2(d_latch_23_out_3), .out_3(d_latch_55_out_3));  // open: out_4
  D_Latch d_latch_56 (.in_1(not_17_out), .in_2(d_latch_24_out_3), .out_3(d_latch_56_out_3));  // open: out_4
  D_Latch d_latch_57 (.in_1(not_20_out), .in_2(d_latch_25_out_3), .out_3(d_latch_57_out_3));  // open: out_4
  D_Latch d_latch_58 (.in_1(not_19_out), .in_2(d_latch_26_out_3), .out_3(d_latch_58_out_3));  // open: out_4
  D_Latch d_latch_59 (.in_1(not_18_out), .in_2(d_latch_27_out_3), .out_3(d_latch_59_out_3));  // open: out_4
  D_Latch d_latch_60 (.in_1(not_17_out), .in_2(d_latch_28_out_3), .out_3(d_latch_60_out_3));  // open: out_4
  D_Latch d_latch_61 (.in_1(not_20_out), .in_2(d_latch_29_out_3), .out_3(d_latch_61_out_3));  // open: out_4
  D_Latch d_latch_62 (.in_1(not_19_out), .in_2(d_latch_30_out_3), .out_3(d_latch_62_out_3));  // open: out_4
  D_Latch d_latch_63 (.in_1(not_18_out), .in_2(d_latch_31_out_3), .out_3(d_latch_63_out_3));  // open: out_4
  D_Latch d_latch_64 (.in_1(not_17_out), .in_2(d_latch_32_out_3), .out_3(d_latch_64_out_3));  // open: out_4
  D_Latch d_latch_65 (.in_1(not_16_out), .in_2(d_latch_33_out_3), .out_3(d_latch_65_out_3));  // open: out_4
  D_Latch d_latch_66 (.in_1(not_15_out), .in_2(d_latch_34_out_3), .out_3(d_latch_66_out_3));  // open: out_4
  D_Latch d_latch_67 (.in_1(not_14_out), .in_2(d_latch_35_out_3), .out_3(d_latch_67_out_3));  // open: out_4
  D_Latch d_latch_68 (.in_1(not_13_out), .in_2(d_latch_36_out_3), .out_3(d_latch_68_out_3));  // open: out_4
  D_Latch d_latch_69 (.in_1(not_16_out), .in_2(d_latch_37_out_3), .out_3(d_latch_69_out_3));  // open: out_4
  D_Latch d_latch_70 (.in_1(not_15_out), .in_2(d_latch_38_out_3), .out_3(d_latch_70_out_3));  // open: out_4
  D_Latch d_latch_71 (.in_1(not_14_out), .in_2(d_latch_39_out_3), .out_3(d_latch_71_out_3));  // open: out_4
  D_Latch d_latch_72 (.in_1(not_13_out), .in_2(d_latch_40_out_3), .out_3(d_latch_72_out_3));  // open: out_4
  D_Latch d_latch_73 (.in_1(not_16_out), .in_2(d_latch_41_out_3), .out_3(d_latch_73_out_3));  // open: out_4
  D_Latch d_latch_74 (.in_1(not_15_out), .in_2(d_latch_42_out_3), .out_3(d_latch_74_out_3));  // open: out_4
  D_Latch d_latch_75 (.in_1(not_14_out), .in_2(d_latch_43_out_3), .out_3(d_latch_75_out_3));  // open: out_4
  D_Latch d_latch_76 (.in_1(not_13_out), .in_2(d_latch_44_out_3), .out_3(d_latch_76_out_3));  // open: out_4
  D_Latch d_latch_77 (.in_1(not_16_out), .in_2(d_latch_45_out_3), .out_3(d_latch_77_out_3));  // open: out_4
  D_Latch d_latch_78 (.in_1(not_15_out), .in_2(d_latch_46_out_3), .out_3(d_latch_78_out_3));  // open: out_4
  D_Latch d_latch_79 (.in_1(not_14_out), .in_2(d_latch_47_out_3), .out_3(d_latch_79_out_3));  // open: out_4
  D_Latch d_latch_80 (.in_1(not_13_out), .in_2(d_latch_48_out_3), .out_3(d_latch_80_out_3));  // open: out_4
  D_Latch d_latch_81 (.in_1(not_16_out), .in_2(d_latch_49_out_3), .out_3(d_latch_81_out_3));  // open: out_4
  D_Latch d_latch_82 (.in_1(not_15_out), .in_2(d_latch_50_out_3), .out_3(d_latch_82_out_3));  // open: out_4
  D_Latch d_latch_83 (.in_1(not_14_out), .in_2(d_latch_51_out_3), .out_3(d_latch_83_out_3));  // open: out_4
  D_Latch d_latch_84 (.in_1(not_13_out), .in_2(d_latch_52_out_3), .out_3(d_latch_84_out_3));  // open: out_4
  D_Latch d_latch_85 (.in_1(not_16_out), .in_2(d_latch_53_out_3), .out_3(d_latch_85_out_3));  // open: out_4
  D_Latch d_latch_86 (.in_1(not_15_out), .in_2(d_latch_54_out_3), .out_3(d_latch_86_out_3));  // open: out_4
  D_Latch d_latch_87 (.in_1(not_14_out), .in_2(d_latch_55_out_3), .out_3(d_latch_87_out_3));  // open: out_4
  D_Latch d_latch_88 (.in_1(not_13_out), .in_2(d_latch_56_out_3), .out_3(d_latch_88_out_3));  // open: out_4
  D_Latch d_latch_89 (.in_1(not_16_out), .in_2(d_latch_57_out_3), .out_3(d_latch_89_out_3));  // open: out_4
  D_Latch d_latch_90 (.in_1(not_15_out), .in_2(d_latch_58_out_3), .out_3(d_latch_90_out_3));  // open: out_4
  D_Latch d_latch_91 (.in_1(not_14_out), .in_2(d_latch_59_out_3), .out_3(d_latch_91_out_3));  // open: out_4
  D_Latch d_latch_92 (.in_1(not_13_out), .in_2(d_latch_60_out_3), .out_3(d_latch_92_out_3));  // open: out_4
  D_Latch d_latch_93 (.in_1(not_16_out), .in_2(d_latch_61_out_3), .out_3(d_latch_93_out_3));  // open: out_4
  D_Latch d_latch_94 (.in_1(not_15_out), .in_2(d_latch_62_out_3), .out_3(d_latch_94_out_3));  // open: out_4
  D_Latch d_latch_95 (.in_1(not_14_out), .in_2(d_latch_63_out_3), .out_3(d_latch_95_out_3));  // open: out_4
  D_Latch d_latch_96 (.in_1(not_13_out), .in_2(d_latch_64_out_3), .out_3(d_latch_96_out_3));  // open: out_4
  and _385 (_385_out, d_latch_65_out_3, SEL[7]);
  and _385_2 (_385_2_out, d_latch_66_out_3, SEL[6]);
  and _385_3 (_385_3_out, d_latch_67_out_3, SEL[5]);
  and _385_4 (_385_4_out, d_latch_68_out_3, SEL[4]);
  and _385_5 (_385_5_out, d_latch_69_out_3, SEL[3]);
  and _385_6 (_385_6_out, d_latch_70_out_3, SEL[2]);
  and _385_7 (_385_7_out, d_latch_71_out_3, SEL[1]);
  and _385_8 (_385_8_out, d_latch_72_out_3, SEL[0]);
  and _387 (_387_out, d_latch_73_out_3, SEL[7]);
  and _387_2 (_387_2_out, d_latch_74_out_3, SEL[6]);
  and _387_3 (_387_3_out, d_latch_75_out_3, SEL[5]);
  and _387_4 (_387_4_out, d_latch_76_out_3, SEL[4]);
  and _387_5 (_387_5_out, d_latch_77_out_3, SEL[3]);
  and _387_6 (_387_6_out, d_latch_78_out_3, SEL[2]);
  and _387_7 (_387_7_out, d_latch_79_out_3, SEL[1]);
  and _387_8 (_387_8_out, d_latch_80_out_3, SEL[0]);
  and _391 (_391_out, d_latch_81_out_3, SEL[7]);
  and _391_2 (_391_2_out, d_latch_82_out_3, SEL[6]);
  and _391_3 (_391_3_out, d_latch_83_out_3, SEL[5]);
  and _391_4 (_391_4_out, d_latch_84_out_3, SEL[4]);
  and _391_5 (_391_5_out, d_latch_85_out_3, SEL[3]);
  and _391_6 (_391_6_out, d_latch_86_out_3, SEL[2]);
  and _391_7 (_391_7_out, d_latch_87_out_3, SEL[1]);
  and _391_8 (_391_8_out, d_latch_88_out_3, SEL[0]);
  and _392 (_392_out, d_latch_89_out_3, SEL[7]);
  and _392_2 (_392_2_out, d_latch_90_out_3, SEL[6]);
  and _392_3 (_392_3_out, d_latch_91_out_3, SEL[5]);
  and _392_4 (_392_4_out, d_latch_92_out_3, SEL[4]);
  and _392_5 (_392_5_out, d_latch_93_out_3, SEL[3]);
  and _392_6 (_392_6_out, d_latch_94_out_3, SEL[2]);
  and _392_7 (_392_7_out, d_latch_95_out_3, SEL[1]);
  and _392_8 (_392_8_out, d_latch_96_out_3, SEL[0]);
  or _385_9 (OUT0, _385_out, _385_2_out, _385_3_out, _385_4_out, _385_5_out, _385_6_out, _385_7_out, _385_8_out);
  or _387_9 (OU1, _387_out, _387_2_out, _387_3_out, _387_4_out, _387_5_out, _387_6_out, _387_7_out, _387_8_out);
  or _391_9 (OUT2, _391_out, _391_2_out, _391_3_out, _391_4_out, _391_5_out, _391_6_out, _391_7_out, _391_8_out);
  or _392_9 (OUT3, _392_out, _392_2_out, _392_3_out, _392_4_out, _392_5_out, _392_6_out, _392_7_out, _392_8_out);

  // Notes on the sheet:
  //   559
  //   560
  //   561
  //   562
endmodule

// BG PIPELINE 2
module BG_PIPELINE_2 (
  input  EN3,
  input  EN2,
  input  EN10,
  input  EN11,
  input  EN12,
  input  EN13,
  input  [7:0] IN,
  input  [7:0] SEL,
  output OUT4,
  output OUT5,
  output OUT0,
  output OU1,
  output OUT2,
  output OUT3
);

  wire and_1_out, and_2_out, and_3_out, and_4_out, and_5_out, and_6_out, and_7_out, and_8_out, and_9_out,
       and_10_out, and_11_out, and_12_out, and_13_out, and_14_out, and_15_out, and_16_out, and_17_out,
       and_18_out, and_19_out, and_20_out, and_21_out, and_22_out, and_23_out, and_24_out, and_25_out,
       and_26_out, and_27_out, and_28_out, and_29_out, and_30_out, and_31_out, and_32_out, and_33_out,
       and_34_out, and_35_out, and_36_out, and_37_out, and_38_out, and_39_out, and_40_out, and_41_out,
       and_42_out, and_43_out, and_44_out, and_45_out, and_46_out, and_47_out, and_48_out, d_latch_1_out_3,
       d_latch_2_out_3, d_latch_3_out_3, d_latch_4_out_3, d_latch_5_out_3, d_latch_6_out_3, d_latch_7_out_3,
       d_latch_8_out_3, d_latch_9_out_3, d_latch_10_out_3, d_latch_11_out_3, d_latch_12_out_3,
       d_latch_13_out_3, d_latch_14_out_3, d_latch_15_out_3, d_latch_16_out_3, d_latch_17_out_3,
       d_latch_18_out_3, d_latch_19_out_3, d_latch_20_out_3, d_latch_21_out_3, d_latch_22_out_3,
       d_latch_23_out_3, d_latch_24_out_3, d_latch_25_out_3, d_latch_26_out_3, d_latch_27_out_3,
       d_latch_28_out_3, d_latch_29_out_3, d_latch_30_out_3, d_latch_31_out_3, d_latch_32_out_3,
       d_latch_33_out_3, d_latch_34_out_3, d_latch_35_out_3, d_latch_36_out_3, d_latch_37_out_3,
       d_latch_38_out_3, d_latch_39_out_3, d_latch_40_out_3, d_latch_41_out_3, d_latch_42_out_3,
       d_latch_43_out_3, d_latch_44_out_3, d_latch_45_out_3, d_latch_46_out_3, d_latch_47_out_3,
       d_latch_48_out_3, d_latch_49_out_3, d_latch_50_out_3, d_latch_51_out_3, d_latch_52_out_3,
       d_latch_53_out_3, d_latch_54_out_3, d_latch_55_out_3, d_latch_56_out_3, d_latch_57_out_3,
       d_latch_58_out_3, d_latch_59_out_3, d_latch_60_out_3, d_latch_61_out_3, d_latch_62_out_3,
       d_latch_63_out_3, d_latch_64_out_3, d_latch_65_out_3, d_latch_66_out_3, d_latch_67_out_3,
       d_latch_68_out_3, d_latch_69_out_3, d_latch_70_out_3, d_latch_71_out_3, d_latch_72_out_3,
       d_latch_73_out_3, d_latch_74_out_3, d_latch_75_out_3, d_latch_76_out_3, d_latch_77_out_3,
       d_latch_78_out_3, d_latch_79_out_3, d_latch_80_out_3, d_latch_81_out_3, d_latch_82_out_3,
       d_latch_83_out_3, d_latch_84_out_3, d_latch_85_out_3, d_latch_86_out_3, d_latch_87_out_3,
       d_latch_88_out_3, d_latch_89_out_3, d_latch_90_out_3, d_latch_91_out_3, d_latch_92_out_3,
       d_latch_93_out_3, d_latch_94_out_3, d_latch_95_out_3, d_latch_96_out_3, not_1_out, not_2_out,
       not_3_out, not_4_out, not_5_out, not_6_out, not_7_out, not_8_out, not_9_out, not_10_out, not_11_out,
       not_12_out, not_13_out, not_14_out, not_15_out, not_16_out, not_17_out, not_18_out, not_19_out,
       not_20_out, not_21_out, not_22_out, not_23_out, not_24_out;

  not not_1 (not_1_out, EN3);
  not not_2 (not_2_out, EN3);
  not not_3 (not_3_out, EN3);
  not not_4 (not_4_out, EN3);
  not not_5 (not_5_out, EN2);
  not not_6 (not_6_out, EN2);
  not not_7 (not_7_out, EN2);
  not not_8 (not_8_out, EN2);
  not not_9 (not_9_out, EN10);
  not not_10 (not_10_out, EN11);
  not not_11 (not_11_out, EN12);
  not not_12 (not_12_out, EN13);
  not not_13 (not_13_out, not_1_out);
  not not_14 (not_14_out, not_2_out);
  not not_15 (not_15_out, not_3_out);
  not not_16 (not_16_out, not_4_out);
  not not_17 (not_17_out, not_5_out);
  not not_18 (not_18_out, not_6_out);
  not not_19 (not_19_out, not_7_out);
  not not_20 (not_20_out, not_8_out);
  not not_21 (not_21_out, not_9_out);
  not not_22 (not_22_out, not_10_out);
  not not_23 (not_23_out, not_11_out);
  not not_24 (not_24_out, not_12_out);
  D_Latch d_latch_1 (.in_1(not_21_out), .in_2(IN[3]), .out_3(d_latch_1_out_3));  // open: out_4
  D_Latch d_latch_2 (.in_1(not_22_out), .in_2(IN[3]), .out_3(d_latch_2_out_3));  // open: out_4
  D_Latch d_latch_3 (.in_1(not_23_out), .in_2(IN[3]), .out_3(d_latch_3_out_3));  // open: out_4
  D_Latch d_latch_4 (.in_1(not_24_out), .in_2(IN[3]), .out_3(d_latch_4_out_3));  // open: out_4
  D_Latch d_latch_5 (.in_1(not_21_out), .in_2(IN[7]), .out_3(d_latch_5_out_3));  // open: out_4
  D_Latch d_latch_6 (.in_1(not_22_out), .in_2(IN[7]), .out_3(d_latch_6_out_3));  // open: out_4
  D_Latch d_latch_7 (.in_1(not_23_out), .in_2(IN[7]), .out_3(d_latch_7_out_3));  // open: out_4
  D_Latch d_latch_8 (.in_1(not_24_out), .in_2(IN[7]), .out_3(d_latch_8_out_3));  // open: out_4
  D_Latch d_latch_9 (.in_1(not_21_out), .in_2(IN[2]), .out_3(d_latch_9_out_3));  // open: out_4
  D_Latch d_latch_10 (.in_1(not_22_out), .in_2(IN[2]), .out_3(d_latch_10_out_3));  // open: out_4
  D_Latch d_latch_11 (.in_1(not_23_out), .in_2(IN[2]), .out_3(d_latch_11_out_3));  // open: out_4
  D_Latch d_latch_12 (.in_1(not_24_out), .in_2(IN[2]), .out_3(d_latch_12_out_3));  // open: out_4
  D_Latch d_latch_13 (.in_1(not_21_out), .in_2(IN[6]), .out_3(d_latch_13_out_3));  // open: out_4
  D_Latch d_latch_14 (.in_1(not_22_out), .in_2(IN[6]), .out_3(d_latch_14_out_3));  // open: out_4
  D_Latch d_latch_15 (.in_1(not_23_out), .in_2(IN[6]), .out_3(d_latch_15_out_3));  // open: out_4
  D_Latch d_latch_16 (.in_1(not_24_out), .in_2(IN[6]), .out_3(d_latch_16_out_3));  // open: out_4
  D_Latch d_latch_17 (.in_1(not_21_out), .in_2(IN[1]), .out_3(d_latch_17_out_3));  // open: out_4
  D_Latch d_latch_18 (.in_1(not_22_out), .in_2(IN[1]), .out_3(d_latch_18_out_3));  // open: out_4
  D_Latch d_latch_19 (.in_1(not_23_out), .in_2(IN[1]), .out_3(d_latch_19_out_3));  // open: out_4
  D_Latch d_latch_20 (.in_1(not_24_out), .in_2(IN[1]), .out_3(d_latch_20_out_3));  // open: out_4
  D_Latch d_latch_21 (.in_1(not_21_out), .in_2(IN[5]), .out_3(d_latch_21_out_3));  // open: out_4
  D_Latch d_latch_22 (.in_1(not_22_out), .in_2(IN[5]), .out_3(d_latch_22_out_3));  // open: out_4
  D_Latch d_latch_23 (.in_1(not_23_out), .in_2(IN[5]), .out_3(d_latch_23_out_3));  // open: out_4
  D_Latch d_latch_24 (.in_1(not_24_out), .in_2(IN[5]), .out_3(d_latch_24_out_3));  // open: out_4
  D_Latch d_latch_25 (.in_1(not_21_out), .in_2(IN[0]), .out_3(d_latch_25_out_3));  // open: out_4
  D_Latch d_latch_26 (.in_1(not_22_out), .in_2(IN[0]), .out_3(d_latch_26_out_3));  // open: out_4
  D_Latch d_latch_27 (.in_1(not_23_out), .in_2(IN[0]), .out_3(d_latch_27_out_3));  // open: out_4
  D_Latch d_latch_28 (.in_1(not_24_out), .in_2(IN[0]), .out_3(d_latch_28_out_3));  // open: out_4
  D_Latch d_latch_29 (.in_1(not_21_out), .in_2(IN[4]), .out_3(d_latch_29_out_3));  // open: out_4
  D_Latch d_latch_30 (.in_1(not_22_out), .in_2(IN[4]), .out_3(d_latch_30_out_3));  // open: out_4
  D_Latch d_latch_31 (.in_1(not_23_out), .in_2(IN[4]), .out_3(d_latch_31_out_3));  // open: out_4
  D_Latch d_latch_32 (.in_1(not_24_out), .in_2(IN[4]), .out_3(d_latch_32_out_3));  // open: out_4
  D_Latch d_latch_33 (.in_1(not_20_out), .in_2(d_latch_1_out_3), .out_3(d_latch_33_out_3));  // open: out_4
  D_Latch d_latch_34 (.in_1(not_19_out), .in_2(d_latch_2_out_3), .out_3(d_latch_34_out_3));  // open: out_4
  D_Latch d_latch_35 (.in_1(not_18_out), .in_2(d_latch_3_out_3), .out_3(d_latch_35_out_3));  // open: out_4
  D_Latch d_latch_36 (.in_1(not_17_out), .in_2(d_latch_4_out_3), .out_3(d_latch_36_out_3));  // open: out_4
  D_Latch d_latch_37 (.in_1(not_20_out), .in_2(d_latch_5_out_3), .out_3(d_latch_37_out_3));  // open: out_4
  D_Latch d_latch_38 (.in_1(not_19_out), .in_2(d_latch_6_out_3), .out_3(d_latch_38_out_3));  // open: out_4
  D_Latch d_latch_39 (.in_1(not_18_out), .in_2(d_latch_7_out_3), .out_3(d_latch_39_out_3));  // open: out_4
  D_Latch d_latch_40 (.in_1(not_17_out), .in_2(d_latch_8_out_3), .out_3(d_latch_40_out_3));  // open: out_4
  D_Latch d_latch_41 (.in_1(not_20_out), .in_2(d_latch_9_out_3), .out_3(d_latch_41_out_3));  // open: out_4
  D_Latch d_latch_42 (.in_1(not_19_out), .in_2(d_latch_10_out_3), .out_3(d_latch_42_out_3));  // open: out_4
  D_Latch d_latch_43 (.in_1(not_18_out), .in_2(d_latch_11_out_3), .out_3(d_latch_43_out_3));  // open: out_4
  D_Latch d_latch_44 (.in_1(not_17_out), .in_2(d_latch_12_out_3), .out_3(d_latch_44_out_3));  // open: out_4
  D_Latch d_latch_45 (.in_1(not_20_out), .in_2(d_latch_13_out_3), .out_3(d_latch_45_out_3));  // open: out_4
  D_Latch d_latch_46 (.in_1(not_19_out), .in_2(d_latch_14_out_3), .out_3(d_latch_46_out_3));  // open: out_4
  D_Latch d_latch_47 (.in_1(not_18_out), .in_2(d_latch_15_out_3), .out_3(d_latch_47_out_3));  // open: out_4
  D_Latch d_latch_48 (.in_1(not_17_out), .in_2(d_latch_16_out_3), .out_3(d_latch_48_out_3));  // open: out_4
  D_Latch d_latch_49 (.in_1(not_20_out), .in_2(d_latch_17_out_3), .out_3(d_latch_49_out_3));  // open: out_4
  D_Latch d_latch_50 (.in_1(not_19_out), .in_2(d_latch_18_out_3), .out_3(d_latch_50_out_3));  // open: out_4
  D_Latch d_latch_51 (.in_1(not_18_out), .in_2(d_latch_19_out_3), .out_3(d_latch_51_out_3));  // open: out_4
  D_Latch d_latch_52 (.in_1(not_17_out), .in_2(d_latch_20_out_3), .out_3(d_latch_52_out_3));  // open: out_4
  D_Latch d_latch_53 (.in_1(not_20_out), .in_2(d_latch_21_out_3), .out_3(d_latch_53_out_3));  // open: out_4
  D_Latch d_latch_54 (.in_1(not_19_out), .in_2(d_latch_22_out_3), .out_3(d_latch_54_out_3));  // open: out_4
  D_Latch d_latch_55 (.in_1(not_18_out), .in_2(d_latch_23_out_3), .out_3(d_latch_55_out_3));  // open: out_4
  D_Latch d_latch_56 (.in_1(not_17_out), .in_2(d_latch_24_out_3), .out_3(d_latch_56_out_3));  // open: out_4
  D_Latch d_latch_57 (.in_1(not_20_out), .in_2(d_latch_25_out_3), .out_3(d_latch_57_out_3));  // open: out_4
  D_Latch d_latch_58 (.in_1(not_19_out), .in_2(d_latch_26_out_3), .out_3(d_latch_58_out_3));  // open: out_4
  D_Latch d_latch_59 (.in_1(not_18_out), .in_2(d_latch_27_out_3), .out_3(d_latch_59_out_3));  // open: out_4
  D_Latch d_latch_60 (.in_1(not_17_out), .in_2(d_latch_28_out_3), .out_3(d_latch_60_out_3));  // open: out_4
  D_Latch d_latch_61 (.in_1(not_20_out), .in_2(d_latch_29_out_3), .out_3(d_latch_61_out_3));  // open: out_4
  D_Latch d_latch_62 (.in_1(not_19_out), .in_2(d_latch_30_out_3), .out_3(d_latch_62_out_3));  // open: out_4
  D_Latch d_latch_63 (.in_1(not_18_out), .in_2(d_latch_31_out_3), .out_3(d_latch_63_out_3));  // open: out_4
  D_Latch d_latch_64 (.in_1(not_17_out), .in_2(d_latch_32_out_3), .out_3(d_latch_64_out_3));  // open: out_4
  D_Latch d_latch_65 (.in_1(not_16_out), .in_2(d_latch_33_out_3), .out_3(d_latch_65_out_3));  // open: out_4
  D_Latch d_latch_66 (.in_1(not_15_out), .in_2(d_latch_34_out_3), .out_3(d_latch_66_out_3));  // open: out_4
  D_Latch d_latch_67 (.in_1(not_14_out), .in_2(d_latch_35_out_3), .out_3(d_latch_67_out_3));  // open: out_4
  D_Latch d_latch_68 (.in_1(not_13_out), .in_2(d_latch_36_out_3), .out_3(d_latch_68_out_3));  // open: out_4
  D_Latch d_latch_69 (.in_1(not_16_out), .in_2(d_latch_37_out_3), .out_3(d_latch_69_out_3));  // open: out_4
  D_Latch d_latch_70 (.in_1(not_15_out), .in_2(d_latch_38_out_3), .out_3(d_latch_70_out_3));  // open: out_4
  D_Latch d_latch_71 (.in_1(not_14_out), .in_2(d_latch_39_out_3), .out_3(d_latch_71_out_3));  // open: out_4
  D_Latch d_latch_72 (.in_1(not_13_out), .in_2(d_latch_40_out_3), .out_3(d_latch_72_out_3));  // open: out_4
  D_Latch d_latch_73 (.in_1(not_16_out), .in_2(d_latch_41_out_3), .out_3(d_latch_73_out_3));  // open: out_4
  D_Latch d_latch_74 (.in_1(not_15_out), .in_2(d_latch_42_out_3), .out_3(d_latch_74_out_3));  // open: out_4
  D_Latch d_latch_75 (.in_1(not_14_out), .in_2(d_latch_43_out_3), .out_3(d_latch_75_out_3));  // open: out_4
  D_Latch d_latch_76 (.in_1(not_13_out), .in_2(d_latch_44_out_3), .out_3(d_latch_76_out_3));  // open: out_4
  D_Latch d_latch_77 (.in_1(not_16_out), .in_2(d_latch_45_out_3), .out_3(d_latch_77_out_3));  // open: out_4
  D_Latch d_latch_78 (.in_1(not_15_out), .in_2(d_latch_46_out_3), .out_3(d_latch_78_out_3));  // open: out_4
  D_Latch d_latch_79 (.in_1(not_14_out), .in_2(d_latch_47_out_3), .out_3(d_latch_79_out_3));  // open: out_4
  D_Latch d_latch_80 (.in_1(not_13_out), .in_2(d_latch_48_out_3), .out_3(d_latch_80_out_3));  // open: out_4
  D_Latch d_latch_81 (.in_1(not_16_out), .in_2(d_latch_49_out_3), .out_3(d_latch_81_out_3));  // open: out_4
  D_Latch d_latch_82 (.in_1(not_15_out), .in_2(d_latch_50_out_3), .out_3(d_latch_82_out_3));  // open: out_4
  D_Latch d_latch_83 (.in_1(not_14_out), .in_2(d_latch_51_out_3), .out_3(d_latch_83_out_3));  // open: out_4
  D_Latch d_latch_84 (.in_1(not_13_out), .in_2(d_latch_52_out_3), .out_3(d_latch_84_out_3));  // open: out_4
  D_Latch d_latch_85 (.in_1(not_16_out), .in_2(d_latch_53_out_3), .out_3(d_latch_85_out_3));  // open: out_4
  D_Latch d_latch_86 (.in_1(not_15_out), .in_2(d_latch_54_out_3), .out_3(d_latch_86_out_3));  // open: out_4
  D_Latch d_latch_87 (.in_1(not_14_out), .in_2(d_latch_55_out_3), .out_3(d_latch_87_out_3));  // open: out_4
  D_Latch d_latch_88 (.in_1(not_13_out), .in_2(d_latch_56_out_3), .out_3(d_latch_88_out_3));  // open: out_4
  D_Latch d_latch_89 (.in_1(not_16_out), .in_2(d_latch_57_out_3), .out_3(d_latch_89_out_3));  // open: out_4
  D_Latch d_latch_90 (.in_1(not_15_out), .in_2(d_latch_58_out_3), .out_3(d_latch_90_out_3));  // open: out_4
  D_Latch d_latch_91 (.in_1(not_14_out), .in_2(d_latch_59_out_3), .out_3(d_latch_91_out_3));  // open: out_4
  D_Latch d_latch_92 (.in_1(not_13_out), .in_2(d_latch_60_out_3), .out_3(d_latch_92_out_3));  // open: out_4
  D_Latch d_latch_93 (.in_1(not_16_out), .in_2(d_latch_61_out_3), .out_3(d_latch_93_out_3));  // open: out_4
  D_Latch d_latch_94 (.in_1(not_15_out), .in_2(d_latch_62_out_3), .out_3(d_latch_94_out_3));  // open: out_4
  D_Latch d_latch_95 (.in_1(not_14_out), .in_2(d_latch_63_out_3), .out_3(d_latch_95_out_3));  // open: out_4
  D_Latch d_latch_96 (.in_1(not_13_out), .in_2(d_latch_64_out_3), .out_3(d_latch_96_out_3));  // open: out_4
  and and_1 (and_1_out, d_latch_67_out_3, SEL[2]);
  and and_2 (and_2_out, d_latch_71_out_3, SEL[0]);
  and and_3 (and_3_out, d_latch_75_out_3, SEL[6]);
  and and_4 (and_4_out, d_latch_79_out_3, SEL[4]);
  and and_5 (and_5_out, d_latch_83_out_3, SEL[3]);
  and and_6 (and_6_out, d_latch_87_out_3, SEL[1]);
  and and_7 (and_7_out, d_latch_91_out_3, SEL[7]);
  and and_8 (and_8_out, d_latch_95_out_3, SEL[5]);
  and and_9 (and_9_out, d_latch_68_out_3, SEL[2]);
  and and_10 (and_10_out, d_latch_72_out_3, SEL[0]);
  and and_11 (and_11_out, d_latch_76_out_3, SEL[6]);
  and and_12 (and_12_out, d_latch_80_out_3, SEL[4]);
  and and_13 (and_13_out, d_latch_84_out_3, SEL[3]);
  and and_14 (and_14_out, d_latch_88_out_3, SEL[1]);
  and and_15 (and_15_out, d_latch_92_out_3, SEL[7]);
  and and_16 (and_16_out, d_latch_96_out_3, SEL[5]);
  and and_17 (and_17_out, d_latch_65_out_3, SEL[7]);
  and and_18 (and_18_out, d_latch_66_out_3, SEL[6]);
  and and_19 (and_19_out, d_latch_67_out_3, SEL[5]);
  and and_20 (and_20_out, d_latch_68_out_3, SEL[4]);
  and and_21 (and_21_out, d_latch_69_out_3, SEL[3]);
  and and_22 (and_22_out, d_latch_70_out_3, SEL[2]);
  and and_23 (and_23_out, d_latch_71_out_3, SEL[1]);
  and and_24 (and_24_out, d_latch_72_out_3, SEL[0]);
  and and_25 (and_25_out, d_latch_73_out_3, SEL[7]);
  and and_26 (and_26_out, d_latch_74_out_3, SEL[6]);
  and and_27 (and_27_out, d_latch_75_out_3, SEL[5]);
  and and_28 (and_28_out, d_latch_76_out_3, SEL[4]);
  and and_29 (and_29_out, d_latch_77_out_3, SEL[3]);
  and and_30 (and_30_out, d_latch_78_out_3, SEL[2]);
  and and_31 (and_31_out, d_latch_79_out_3, SEL[1]);
  and and_32 (and_32_out, d_latch_80_out_3, SEL[0]);
  and and_33 (and_33_out, d_latch_81_out_3, SEL[7]);
  and and_34 (and_34_out, d_latch_82_out_3, SEL[6]);
  and and_35 (and_35_out, d_latch_83_out_3, SEL[5]);
  and and_36 (and_36_out, d_latch_84_out_3, SEL[4]);
  and and_37 (and_37_out, d_latch_85_out_3, SEL[3]);
  and and_38 (and_38_out, d_latch_86_out_3, SEL[2]);
  and and_39 (and_39_out, d_latch_87_out_3, SEL[1]);
  and and_40 (and_40_out, d_latch_88_out_3, SEL[0]);
  and and_41 (and_41_out, d_latch_89_out_3, SEL[7]);
  and and_42 (and_42_out, d_latch_90_out_3, SEL[6]);
  and and_43 (and_43_out, d_latch_91_out_3, SEL[5]);
  and and_44 (and_44_out, d_latch_92_out_3, SEL[4]);
  and and_45 (and_45_out, d_latch_93_out_3, SEL[3]);
  and and_46 (and_46_out, d_latch_94_out_3, SEL[2]);
  and and_47 (and_47_out, d_latch_95_out_3, SEL[1]);
  and and_48 (and_48_out, d_latch_96_out_3, SEL[0]);
  or _395 (OUT4, and_1_out, and_2_out, and_3_out, and_4_out, and_5_out, and_6_out, and_7_out, and_8_out);
  or _400 (OUT5, and_9_out, and_10_out, and_11_out, and_12_out, and_13_out, and_14_out, and_15_out, and_16_out);
  or _393 (OUT0, and_17_out, and_18_out, and_19_out, and_20_out, and_21_out, and_22_out, and_23_out, and_24_out);
  or _394 (OU1, and_25_out, and_26_out, and_27_out, and_28_out, and_29_out, and_30_out, and_31_out, and_32_out);
  or _396 (OUT2, and_33_out, and_34_out, and_35_out, and_36_out, and_37_out, and_38_out, and_39_out, and_40_out);
  or _397 (OUT3, and_41_out, and_42_out, and_43_out, and_44_out, and_45_out, and_46_out, and_47_out, and_48_out);

  // Notes on the sheet:
  //   535
  //   536
  //   538
  //   537
endmodule
module BG_4bit_CNT (
  input  CLK1,
  input  CLK2,
  input  CIN,
  input  RES,
  input  LOAD,
  input  VAL0,
  input  VAL1,
  input  VAL2,
  input  VAL3,
  output OUT0,
  output OUT1,
  output OUT2,
  output OUT3
);

  wire d_ff_1_qn, d_ff_2_qn, d_ff_3_qn, d_ff_4_qn, d_ff_5_qn, d_ff_6_qn, d_ff_7_qn, d_ff_8_qn,
       demultiplexer_1_out0, demultiplexer_1_out1, demultiplexer_2_out0, demultiplexer_2_out1,
       demultiplexer_3_out0, demultiplexer_3_out1, demultiplexer_4_out0, demultiplexer_4_out1, nor_1_out,
       nor_2_out, nor_3_out, nor_4_out, not_1_out, not_2_out, not_3_out, not_4_out, or_1_out, or_2_out,
       or_3_out, or_4_out, xor_1_out, xor_2_out, xor_3_out, xor_4_out;

  Demultiplexer #(.enable("false")) demultiplexer_1 (
    .out0(demultiplexer_1_out0), .out1(demultiplexer_1_out1), .in(LOAD), .sel(VAL0));
  Demultiplexer #(.enable("false")) demultiplexer_2 (
    .out0(demultiplexer_2_out0), .out1(demultiplexer_2_out1), .in(LOAD), .sel(VAL1));
  Demultiplexer #(.enable("false")) demultiplexer_3 (
    .out0(demultiplexer_3_out0), .out1(demultiplexer_3_out1), .in(LOAD), .sel(VAL2));
  Demultiplexer #(.enable("false")) demultiplexer_4 (
    .out0(demultiplexer_4_out0), .out1(demultiplexer_4_out1), .in(LOAD), .sel(VAL3));
  or or_1 (or_1_out, RES, demultiplexer_1_out0);
  or or_2 (or_2_out, RES, demultiplexer_2_out0);
  or or_3 (or_3_out, RES, demultiplexer_3_out0);
  or or_4 (or_4_out, RES, demultiplexer_4_out0);
  D_Flip_Flop #(.trigger("high")) d_ff_1 (
    .clk(CLK2), .D(d_ff_5_qn), .Q(OUT0), .Qn(d_ff_1_qn), .preset(demultiplexer_1_out1), .reset(or_1_out));  // open: en
  D_Flip_Flop #(.trigger("high")) d_ff_2 (
    .clk(CLK2), .D(d_ff_6_qn), .Q(OUT1), .Qn(d_ff_2_qn), .preset(demultiplexer_2_out1), .reset(or_2_out));  // open: en
  D_Flip_Flop #(.trigger("high")) d_ff_3 (
    .clk(CLK2), .D(d_ff_7_qn), .Q(OUT2), .Qn(d_ff_3_qn), .preset(demultiplexer_3_out1), .reset(or_3_out));  // open: en
  D_Flip_Flop #(.trigger("high")) d_ff_4 (
    .clk(CLK2), .D(d_ff_8_qn), .Q(OUT3), .Qn(d_ff_4_qn), .preset(demultiplexer_4_out1), .reset(or_4_out));  // open: en
  xor xor_1 (xor_1_out, CIN, d_ff_1_qn);
  not not_1 (not_1_out, CIN);
  nor nor_1 (nor_1_out, not_1_out, d_ff_1_qn);
  xor xor_2 (xor_2_out, nor_1_out, d_ff_2_qn);
  not not_2 (not_2_out, nor_1_out);
  nor nor_2 (nor_2_out, not_2_out, d_ff_2_qn);
  xor xor_3 (xor_3_out, nor_2_out, d_ff_3_qn);
  not not_3 (not_3_out, nor_2_out);
  nor nor_3 (nor_3_out, not_3_out, d_ff_3_qn);
  xor xor_4 (xor_4_out, nor_3_out, d_ff_4_qn);
  not not_4 (not_4_out, nor_3_out);
  nor nor_4 (nor_4_out, not_4_out, d_ff_4_qn);
  D_Flip_Flop #(.trigger("high")) d_ff_5 (.clk(CLK1), .D(xor_1_out), .Qn(d_ff_5_qn));  // open: Q, preset, en, reset
  D_Flip_Flop #(.trigger("high")) d_ff_6 (.clk(CLK1), .D(xor_2_out), .Qn(d_ff_6_qn));  // open: Q, preset, en, reset
  D_Flip_Flop #(.trigger("high")) d_ff_7 (.clk(CLK1), .D(xor_3_out), .Qn(d_ff_7_qn));  // open: Q, preset, en, reset
  D_Flip_Flop #(.trigger("high")) d_ff_8 (.clk(CLK1), .D(xor_4_out), .Qn(d_ff_8_qn));  // open: Q, preset, en, reset
endmodule

// 8BIT CNT
module DMA_8bit_CNT (
  input  CLK1,
  input  CLK2,
  input  CIN,
  input  RES,
  input  LOAD,
  input  [7:0] VAL,
  output [7:0] CNT_OUT,
  output CO
);

  wire d_ff_1_qn, d_ff_2_qn, d_ff_3_qn, d_ff_4_qn, d_ff_5_qn, d_ff_6_qn, d_ff_7_qn, d_ff_8_qn, d_ff_9_qn,
       d_ff_10_qn, d_ff_11_qn, d_ff_12_qn, d_ff_13_qn, d_ff_14_qn, d_ff_15_qn, d_ff_16_qn,
       demultiplexer_1_out0, demultiplexer_1_out1, demultiplexer_2_out0, demultiplexer_2_out1,
       demultiplexer_3_out0, demultiplexer_3_out1, demultiplexer_4_out0, demultiplexer_4_out1,
       demultiplexer_5_out0, demultiplexer_5_out1, demultiplexer_6_out0, demultiplexer_6_out1,
       demultiplexer_7_out0, demultiplexer_7_out1, demultiplexer_8_out0, demultiplexer_8_out1, nor_1_out,
       nor_2_out, nor_3_out, nor_4_out, nor_5_out, nor_6_out, nor_7_out, not_1_out, not_2_out, not_3_out,
       not_4_out, not_5_out, not_6_out, not_7_out, not_8_out, or_1_out, or_2_out, or_3_out, or_4_out,
       or_5_out, or_6_out, or_7_out, or_8_out, xor_1_out, xor_2_out, xor_3_out, xor_4_out, xor_5_out,
       xor_6_out, xor_7_out, xor_8_out;

  Demultiplexer #(.enable("false")) demultiplexer_1 (
    .out0(demultiplexer_1_out0), .out1(demultiplexer_1_out1), .in(LOAD), .sel(VAL[0]));
  Demultiplexer #(.enable("false")) demultiplexer_2 (
    .out0(demultiplexer_2_out0), .out1(demultiplexer_2_out1), .in(LOAD), .sel(VAL[1]));
  Demultiplexer #(.enable("false")) demultiplexer_3 (
    .out0(demultiplexer_3_out0), .out1(demultiplexer_3_out1), .in(LOAD), .sel(VAL[2]));
  Demultiplexer #(.enable("false")) demultiplexer_4 (
    .out0(demultiplexer_4_out0), .out1(demultiplexer_4_out1), .in(LOAD), .sel(VAL[3]));
  Demultiplexer #(.enable("false")) demultiplexer_5 (
    .out0(demultiplexer_5_out0), .out1(demultiplexer_5_out1), .in(LOAD), .sel(VAL[4]));
  Demultiplexer #(.enable("false")) demultiplexer_6 (
    .out0(demultiplexer_6_out0), .out1(demultiplexer_6_out1), .in(LOAD), .sel(VAL[5]));
  Demultiplexer #(.enable("false")) demultiplexer_7 (
    .out0(demultiplexer_7_out0), .out1(demultiplexer_7_out1), .in(LOAD), .sel(VAL[6]));
  Demultiplexer #(.enable("false")) demultiplexer_8 (
    .out0(demultiplexer_8_out0), .out1(demultiplexer_8_out1), .in(LOAD), .sel(VAL[7]));
  or or_1 (or_1_out, RES, demultiplexer_1_out0);
  or or_2 (or_2_out, RES, demultiplexer_2_out0);
  or or_3 (or_3_out, RES, demultiplexer_3_out0);
  or or_4 (or_4_out, RES, demultiplexer_4_out0);
  or or_5 (or_5_out, RES, demultiplexer_5_out0);
  or or_6 (or_6_out, RES, demultiplexer_6_out0);
  or or_7 (or_7_out, RES, demultiplexer_7_out0);
  or or_8 (or_8_out, RES, demultiplexer_8_out0);
  D_Flip_Flop #(.trigger("high")) d_ff_1 (
    .clk(CLK2), .D(d_ff_9_qn), .Q(CNT_OUT[0]), .Qn(d_ff_1_qn), .preset(demultiplexer_1_out1), .reset(or_1_out));  // open: en
  D_Flip_Flop #(.trigger("high")) d_ff_2 (
    .clk(CLK2), .D(d_ff_10_qn), .Q(CNT_OUT[1]), .Qn(d_ff_2_qn), .preset(demultiplexer_2_out1),
    .reset(or_2_out));  // open: en
  D_Flip_Flop #(.trigger("high")) d_ff_3 (
    .clk(CLK2), .D(d_ff_11_qn), .Q(CNT_OUT[2]), .Qn(d_ff_3_qn), .preset(demultiplexer_3_out1),
    .reset(or_3_out));  // open: en
  D_Flip_Flop #(.trigger("high")) d_ff_4 (
    .clk(CLK2), .D(d_ff_12_qn), .Q(CNT_OUT[3]), .Qn(d_ff_4_qn), .preset(demultiplexer_4_out1),
    .reset(or_4_out));  // open: en
  D_Flip_Flop #(.trigger("high")) d_ff_5 (
    .clk(CLK2), .D(d_ff_13_qn), .Q(CNT_OUT[4]), .Qn(d_ff_5_qn), .preset(demultiplexer_5_out1),
    .reset(or_5_out));  // open: en
  D_Flip_Flop #(.trigger("high")) d_ff_6 (
    .clk(CLK2), .D(d_ff_14_qn), .Q(CNT_OUT[5]), .Qn(d_ff_6_qn), .preset(demultiplexer_6_out1),
    .reset(or_6_out));  // open: en
  D_Flip_Flop #(.trigger("high")) d_ff_7 (
    .clk(CLK2), .D(d_ff_15_qn), .Q(CNT_OUT[6]), .Qn(d_ff_7_qn), .preset(demultiplexer_7_out1),
    .reset(or_7_out));  // open: en
  D_Flip_Flop #(.trigger("high")) d_ff_8 (
    .clk(CLK2), .D(d_ff_16_qn), .Q(CNT_OUT[7]), .Qn(d_ff_8_qn), .preset(demultiplexer_8_out1),
    .reset(or_8_out));  // open: en
  xor xor_1 (xor_1_out, CIN, d_ff_1_qn);
  not not_1 (not_1_out, CIN);
  nor nor_1 (nor_1_out, not_1_out, d_ff_1_qn);
  xor xor_2 (xor_2_out, nor_1_out, d_ff_2_qn);
  not not_2 (not_2_out, nor_1_out);
  nor nor_2 (nor_2_out, not_2_out, d_ff_2_qn);
  xor xor_3 (xor_3_out, nor_2_out, d_ff_3_qn);
  not not_3 (not_3_out, nor_2_out);
  nor nor_3 (nor_3_out, not_3_out, d_ff_3_qn);
  xor xor_4 (xor_4_out, nor_3_out, d_ff_4_qn);
  not not_4 (not_4_out, nor_3_out);
  nor nor_4 (nor_4_out, not_4_out, d_ff_4_qn);
  xor xor_5 (xor_5_out, nor_4_out, d_ff_5_qn);
  not not_5 (not_5_out, nor_4_out);
  nor nor_5 (nor_5_out, not_5_out, d_ff_5_qn);
  xor xor_6 (xor_6_out, nor_5_out, d_ff_6_qn);
  not not_6 (not_6_out, nor_5_out);
  nor nor_6 (nor_6_out, not_6_out, d_ff_6_qn);
  xor xor_7 (xor_7_out, nor_6_out, d_ff_7_qn);
  not not_7 (not_7_out, nor_6_out);
  nor nor_7 (nor_7_out, not_7_out, d_ff_7_qn);
  xor xor_8 (xor_8_out, nor_7_out, d_ff_8_qn);
  not not_8 (not_8_out, nor_7_out);
  nor nor_8 (CO, not_8_out, d_ff_8_qn);
  D_Flip_Flop #(.trigger("high")) d_ff_9 (.clk(CLK1), .D(xor_1_out), .Qn(d_ff_9_qn));  // open: Q, preset, en, reset
  D_Flip_Flop #(.trigger("high")) d_ff_10 (.clk(CLK1), .D(xor_2_out), .Qn(d_ff_10_qn));  // open: Q, preset, en, reset
  D_Flip_Flop #(.trigger("high")) d_ff_11 (.clk(CLK1), .D(xor_3_out), .Qn(d_ff_11_qn));  // open: Q, preset, en, reset
  D_Flip_Flop #(.trigger("high")) d_ff_12 (.clk(CLK1), .D(xor_4_out), .Qn(d_ff_12_qn));  // open: Q, preset, en, reset
  D_Flip_Flop #(.trigger("high")) d_ff_13 (.clk(CLK1), .D(xor_5_out), .Qn(d_ff_13_qn));  // open: Q, preset, en, reset
  D_Flip_Flop #(.trigger("high")) d_ff_14 (.clk(CLK1), .D(xor_6_out), .Qn(d_ff_14_qn));  // open: Q, preset, en, reset
  D_Flip_Flop #(.trigger("high")) d_ff_15 (.clk(CLK1), .D(xor_7_out), .Qn(d_ff_15_qn));  // open: Q, preset, en, reset
  D_Flip_Flop #(.trigger("high")) d_ff_16 (.clk(CLK1), .D(xor_8_out), .Qn(d_ff_16_qn));  // open: Q, preset, en, reset
endmodule
