// Logisim project fc1004_cells.circ as structural Verilog: 6 circuits, main circuit cell95
module cell95 (
  input  in_1,
  input  clk,
  input  in_3,
  input  in_4,
  input  in_5,
  input  in_6,
  output out_7,
  output out_8,
  output out_9,
  output out_10
);

  wire multiplexer_1_out, multiplexer_2_out, nand_1_out, nand_2_out, not_1_out, not_2_out, not_3_out,
       not_7_out, transistor_1_out, transistor_3_out, transistor_6_out, transistor_7_out, transistor_9_out,
       transistor_11_out, transistor_13_out, transistor_16_out, transistor_17_out;

  not not_1 (not_1_out, clk);
  not not_2 (not_2_out, not_1_out);
  Multiplexer multiplexer_1 (.in0(in_4), .in1(not_3_out), .out(multiplexer_1_out), .sel(in_5));
  not not_3 (not_3_out, nand_1_out);
  Transistor transistor_1 (.in(in_3), .out(transistor_1_out), .gate(not_2_out));
  Transistor #(.\type ("n")) transistor_2 (.in(in_3), .out(transistor_1_out), .gate(not_1_out));
  Transistor transistor_3 (.in(1'b1), .out(transistor_3_out), .gate(transistor_7_out));
  Transistor transistor_4 (.in(transistor_3_out), .out(transistor_1_out), .gate(not_1_out));
  Transistor #(.\type ("n")) transistor_5 (.in(transistor_6_out), .out(transistor_1_out), .gate(not_2_out));
  Transistor #(.\type ("n")) transistor_6 (.in(1'b0), .out(transistor_6_out), .gate(transistor_7_out));
  nand nand_1 (nand_1_out, multiplexer_1_out, in_6);
  Transistor transistor_7 (.in(1'b1), .out(transistor_7_out), .gate(in_1));
  Multiplexer multiplexer_2 (.in0(nand_2_out), .in1(nand_1_out), .out(multiplexer_2_out), .sel(in_5));
  Transistor #(.\type ("n")) transistor_8 (.in(transistor_9_out), .out(transistor_7_out), .gate(in_1));
  Transistor #(.\type ("n")) transistor_9 (.in(1'b0), .out(transistor_9_out), .gate(transistor_1_out));
  not not_4 (out_9, multiplexer_2_out);
  Transistor transistor_10 (.in(1'b1), .out(transistor_7_out), .gate(transistor_1_out));
  nand nand_2 (nand_2_out, out_9, in_6);
  Transistor transistor_11 (.in(transistor_7_out), .out(transistor_11_out), .gate(not_1_out));
  Transistor #(.\type ("n")) transistor_12 (.in(transistor_7_out), .out(transistor_11_out), .gate(not_2_out));
  not not_5 (out_10, out_9);
  Transistor transistor_13 (.in(1'b1), .out(transistor_13_out), .gate(in_1));
  Transistor transistor_14 (.in(transistor_13_out), .out(transistor_11_out), .gate(not_2_out));
  Transistor #(.\type ("n")) transistor_15 (.in(transistor_16_out), .out(transistor_11_out), .gate(not_1_out));
  Transistor #(.\type ("n")) transistor_16 (.in(transistor_17_out), .out(transistor_16_out), .gate(not_7_out));
  Transistor #(.\type ("n")) transistor_17 (.in(1'b0), .out(transistor_17_out), .gate(in_1));
  Transistor transistor_18 (.in(1'b1), .out(transistor_13_out), .gate(not_7_out));
  not not_6 (out_8, transistor_11_out);
  not not_7 (not_7_out, transistor_11_out);
  not not_8 (out_7, not_7_out);
endmodule

module cell94 (
  input  in_1,
  input  in_2,
  input  in_3,
  input  in_4,
  input  in_5,
  input  in_6,
  output out_7,
  output out_8,
  output out_9,
  output out_10
);

  wire multiplexer_1_out, multiplexer_2_out, nand_1_out, nand_2_out, not_1_out, not_2_out, not_3_out,
       not_4_out, transistor_1_out, transistor_3_out, transistor_6_out, transistor_7_out, transistor_9_out,
       transistor_11_out, transistor_13_out, transistor_16_out, transistor_17_out, transistor_20_out;

  not not_1 (not_1_out, in_2);
  Multiplexer multiplexer_1 (.in0(in_4), .in1(nand_1_out), .out(multiplexer_1_out), .sel(in_5));
  not not_2 (not_2_out, not_1_out);
  not not_3 (not_3_out, multiplexer_1_out);
  nand nand_1 (nand_1_out, not_3_out, in_6);
  Transistor transistor_1 (.in(in_3), .out(transistor_1_out), .gate(not_2_out));
  Transistor #(.\type ("n")) transistor_2 (.in(in_3), .out(transistor_1_out), .gate(not_1_out));
  Transistor transistor_3 (.in(1'b1), .out(transistor_3_out), .gate(in_1));
  Transistor transistor_4 (.in(transistor_3_out), .out(transistor_1_out), .gate(not_1_out));
  Transistor #(.\type ("n")) transistor_5 (.in(transistor_6_out), .out(transistor_1_out), .gate(not_2_out));
  Transistor #(.\type ("n")) transistor_6 (.in(transistor_7_out), .out(transistor_6_out), .gate(in_1));
  Transistor #(.\type ("n")) transistor_7 (.in(1'b0), .out(transistor_7_out), .gate(transistor_9_out));
  Transistor transistor_8 (.in(1'b1), .out(transistor_3_out), .gate(transistor_9_out));
  not not_4 (not_4_out, nand_2_out);
  Multiplexer multiplexer_2 (.in0(not_4_out), .in1(not_3_out), .out(multiplexer_2_out), .sel(in_5));
  nand nand_2 (nand_2_out, multiplexer_2_out, in_6);
  Transistor transistor_9 (.in(1'b1), .out(transistor_9_out), .gate(transistor_1_out));
  Transistor #(.\type ("n")) transistor_10 (.in(1'b0), .out(transistor_9_out), .gate(transistor_1_out));
  not not_5 (out_9, nand_2_out);
  not not_6 (out_10, multiplexer_2_out);
  Transistor transistor_11 (.in(transistor_9_out), .out(transistor_11_out), .gate(not_1_out));
  Transistor #(.\type ("n")) transistor_12 (.in(transistor_9_out), .out(transistor_11_out), .gate(not_2_out));
  Transistor transistor_13 (.in(1'b1), .out(transistor_13_out), .gate(transistor_17_out));
  Transistor transistor_14 (.in(transistor_13_out), .out(transistor_11_out), .gate(not_2_out));
  Transistor #(.\type ("n")) transistor_15 (.in(transistor_16_out), .out(transistor_11_out), .gate(not_1_out));
  Transistor #(.\type ("n")) transistor_16 (.in(1'b0), .out(transistor_16_out), .gate(transistor_17_out));
  Transistor transistor_17 (.in(1'b1), .out(transistor_17_out), .gate(in_1));
  Transistor transistor_18 (.in(1'b1), .out(transistor_17_out), .gate(transistor_11_out));
  Transistor #(.\type ("n")) transistor_19 (.in(transistor_20_out), .out(transistor_17_out), .gate(transistor_11_out));
  Transistor #(.\type ("n")) transistor_20 (.in(1'b0), .out(transistor_20_out), .gate(in_1));
  not not_7 (out_7, transistor_17_out);
  not not_8 (out_8, transistor_11_out);
endmodule

module cell96 (
  input  clk,
  input  in_2,
  input  in_3,
  input  in_4,
  output out_5,
  output out_6,
  output out_7,
  output out_8
);

  wire multiplexer_1_out, multiplexer_2_out, not_1_out, not_2_out, not_3_out, not_4_out, not_5_out,
       not_6_out, transistor_1_out, transistor_3_out, transistor_6_out, transistor_7_out, transistor_9_out,
       transistor_11_out, transistor_14_out, transistor_15_out;

  not not_1 (not_1_out, clk);
  not not_2 (not_2_out, not_1_out);
  Multiplexer multiplexer_1 (.in0(in_3), .in1(not_3_out), .out(multiplexer_1_out), .sel(in_4));
  not not_3 (not_3_out, not_4_out);
  Transistor transistor_1 (.in(in_2), .out(transistor_1_out), .gate(not_2_out));
  Transistor #(.\type ("n")) transistor_2 (.in(in_2), .out(transistor_1_out), .gate(not_1_out));
  not not_4 (not_4_out, multiplexer_1_out);
  Transistor transistor_3 (.in(1'b1), .out(transistor_3_out), .gate(transistor_7_out));
  Transistor transistor_4 (.in(transistor_3_out), .out(transistor_1_out), .gate(not_1_out));
  Transistor #(.\type ("n")) transistor_5 (.in(transistor_6_out), .out(transistor_1_out), .gate(not_2_out));
  Transistor #(.\type ("n")) transistor_6 (.in(1'b0), .out(transistor_6_out), .gate(transistor_7_out));
  Transistor transistor_7 (.in(1'b1), .out(transistor_7_out), .gate(transistor_1_out));
  Transistor #(.\type ("n")) transistor_8 (.in(1'b0), .out(transistor_7_out), .gate(transistor_1_out));
  not not_5 (not_5_out, not_6_out);
  not not_6 (not_6_out, multiplexer_2_out);
  Multiplexer multiplexer_2 (.in0(not_5_out), .in1(not_4_out), .out(multiplexer_2_out), .sel(in_4));
  Transistor transistor_9 (.in(transistor_7_out), .out(transistor_9_out), .gate(not_1_out));
  Transistor #(.\type ("n")) transistor_10 (.in(transistor_7_out), .out(transistor_9_out), .gate(not_2_out));
  not not_7 (out_7, not_6_out);
  Transistor transistor_11 (.in(1'b1), .out(transistor_11_out), .gate(transistor_15_out));
  Transistor transistor_12 (.in(transistor_11_out), .out(transistor_9_out), .gate(not_2_out));
  Transistor #(.\type ("n")) transistor_13 (.in(transistor_14_out), .out(transistor_9_out), .gate(not_1_out));
  Transistor #(.\type ("n")) transistor_14 (.in(1'b0), .out(transistor_14_out), .gate(transistor_15_out));
  not not_8 (out_8, multiplexer_2_out);
  Transistor transistor_15 (.in(1'b1), .out(transistor_15_out), .gate(transistor_9_out));
  Transistor #(.\type ("n")) transistor_16 (.in(1'b0), .out(transistor_15_out), .gate(transistor_9_out));
  not not_9 (out_5, transistor_15_out);
  not not_10 (out_6, transistor_9_out);
endmodule

module cell93 (
  input  in_1,
  input  in_2,
  input  in_3,
  input  in_4,
  input  in_5,
  input  in_6,
  input  in_7,
  input  in_8,
  input  in_9,
  input  in_10,
  output out_11,
  output out_12,
  output out_13,
  output out_14,
  output out_15,
  output out_16
);

  wire multiplexer_1_out, multiplexer_2_out, multiplexer_3_out, nand_1_out, nand_2_out, nand_3_out,
       not_2_out, not_3_out, not_4_out, not_5_out, not_6_out, not_7_out, not_8_out, not_9_out, not_10_out,
       not_11_out, not_14_out, transistor_1_out, transistor_3_out, transistor_5_out, transistor_7_out,
       transistor_8_out, transistor_11_out, transistor_13_out, transistor_16_out, transistor_17_out,
       transistor_18_out, transistor_20_out, transistor_21_out, transistor_24_out, transistor_25_out,
       transistor_27_out, transistor_29_out, transistor_30_out, transistor_32_out, transistor_33_out,
       transistor_36_out, transistor_37_out, transistor_40_out, xnor_1_out;

  Transistor transistor_1 (.in(1'b1), .out(transistor_1_out), .gate(in_1));
  Transistor #(.\type ("n")) transistor_2 (.in(transistor_3_out), .out(transistor_1_out), .gate(not_14_out));
  Transistor #(.\type ("n")) transistor_3 (.in(1'b0), .out(transistor_3_out), .gate(in_1));
  nand nand_1 (nand_1_out, not_11_out, in_6);
  xnor xnor_1 (xnor_1_out, not_11_out, in_6);
  Transistor transistor_4 (.in(1'b1), .out(transistor_1_out), .gate(not_14_out));
  not not_1 (out_14, nand_1_out);
  not not_2 (not_2_out, in_8);
  Multiplexer multiplexer_1 (.in0(not_2_out), .in1(xnor_1_out), .out(multiplexer_1_out), .sel(in_7));
  Transistor transistor_5 (.in(1'b1), .out(transistor_5_out), .gate(transistor_1_out));
  Transistor #(.\type ("n")) transistor_6 (.in(transistor_7_out), .out(transistor_5_out), .gate(transistor_1_out));
  Transistor #(.\type ("n")) transistor_7 (.in(1'b0), .out(transistor_7_out), .gate(in_1));
  Transistor transistor_8 (.in(1'b1), .out(transistor_8_out), .gate(not_14_out));
  Transistor transistor_9 (.in(transistor_8_out), .out(transistor_5_out), .gate(in_1));
  Transistor #(.\type ("n")) transistor_10 (.in(1'b0), .out(transistor_7_out), .gate(not_14_out));
  not not_3 (not_3_out, multiplexer_1_out);
  not not_4 (not_4_out, nand_2_out);
  Multiplexer multiplexer_2 (.in0(not_3_out), .in1(not_4_out), .out(multiplexer_2_out), .sel(in_9));
  Transistor transistor_11 (.in(transistor_5_out), .out(transistor_11_out), .gate(not_5_out));
  Transistor #(.\type ("n")) transistor_12 (.in(transistor_5_out), .out(transistor_11_out), .gate(in_2));
  not not_5 (not_5_out, in_2);
  not not_6 (not_6_out, in_4);
  not not_7 (not_7_out, in_4);
  nand nand_2 (nand_2_out, multiplexer_2_out, in_10);
  not not_8 (not_8_out, not_7_out);
  Transistor transistor_13 (.in(1'b1), .out(transistor_13_out), .gate(in_3));
  Transistor transistor_14 (.in(transistor_13_out), .out(transistor_11_out), .gate(in_2));
  Transistor #(.\type ("n")) transistor_15 (.in(transistor_16_out), .out(transistor_11_out), .gate(not_5_out));
  Transistor #(.\type ("n")) transistor_16 (.in(1'b0), .out(transistor_16_out), .gate(in_3));
  not not_9 (not_9_out, nand_3_out);
  not not_10 (not_10_out, nand_2_out);
  Transistor transistor_17 (.in(1'b1), .out(transistor_17_out), .gate(transistor_11_out));
  Transistor transistor_18 (.in(transistor_17_out), .out(transistor_18_out), .gate(not_8_out));
  Transistor #(.\type ("n")) transistor_19 (.in(transistor_20_out), .out(transistor_18_out), .gate(not_6_out));
  Transistor #(.\type ("n")) transistor_20 (.in(1'b0), .out(transistor_20_out), .gate(transistor_11_out));
  Multiplexer multiplexer_3 (.in0(not_9_out), .in1(not_10_out), .out(multiplexer_3_out), .sel(in_9));
  nand nand_3 (nand_3_out, multiplexer_3_out, in_10);
  Transistor transistor_21 (.in(1'b1), .out(transistor_21_out), .gate(transistor_25_out));
  Transistor transistor_22 (.in(transistor_21_out), .out(transistor_18_out), .gate(not_6_out));
  Transistor #(.\type ("n")) transistor_23 (.in(transistor_24_out), .out(transistor_18_out), .gate(not_8_out));
  Transistor #(.\type ("n")) transistor_24 (.in(1'b0), .out(transistor_24_out), .gate(transistor_25_out));
  Transistor transistor_25 (.in(1'b1), .out(transistor_25_out), .gate(transistor_18_out));
  Transistor #(.\type ("n")) transistor_26 (.in(transistor_27_out), .out(transistor_25_out), .gate(in_5));
  Transistor #(.\type ("n")) transistor_27 (.in(1'b0), .out(transistor_27_out), .gate(transistor_18_out));
  not not_11 (not_11_out, nand_3_out);
  Transistor transistor_28 (.in(1'b1), .out(transistor_25_out), .gate(in_5));
  not not_12 (out_15, nand_3_out);
  not not_13 (out_16, not_11_out);
  Transistor transistor_29 (.in(1'b1), .out(transistor_29_out), .gate(transistor_25_out));
  Transistor transistor_30 (.in(transistor_29_out), .out(transistor_30_out), .gate(not_6_out));
  Transistor #(.\type ("n")) transistor_31 (.in(transistor_32_out), .out(transistor_30_out), .gate(not_8_out));
  Transistor #(.\type ("n")) transistor_32 (.in(1'b0), .out(transistor_32_out), .gate(transistor_25_out));
  Transistor transistor_33 (.in(1'b1), .out(transistor_33_out), .gate(not_8_out));
  Transistor transistor_34 (.in(transistor_33_out), .out(transistor_30_out), .gate(transistor_37_out));
  Transistor #(.\type ("n")) transistor_35 (.in(transistor_36_out), .out(transistor_30_out), .gate(transistor_37_out));
  Transistor #(.\type ("n")) transistor_36 (.in(1'b0), .out(transistor_36_out), .gate(not_6_out));
  Transistor transistor_37 (.in(1'b1), .out(transistor_37_out), .gate(transistor_30_out));
  Transistor transistor_38 (.in(1'b1), .out(transistor_37_out), .gate(in_5));
  Transistor #(.\type ("n")) transistor_39 (.in(transistor_40_out), .out(transistor_37_out), .gate(in_5));
  Transistor #(.\type ("n")) transistor_40 (.in(1'b0), .out(transistor_40_out), .gate(transistor_30_out));
  not not_14 (not_14_out, transistor_37_out);
  not not_15 (out_13, transistor_1_out);
  not not_16 (out_11, transistor_37_out);
  not not_17 (out_12, not_14_out);
endmodule

module cell97 (
  input  in_1,
  input  in_2,
  output out_3
);

  wire nand_1_out, nor_1_out, not_1_out, not_2_out;

  not not_1 (not_1_out, in_1);
  nand nand_1 (nand_1_out, not_1_out, in_2);
  nor nor_1 (nor_1_out, in_1, in_2);
  not not_2 (not_2_out, nand_1_out);
  assign out_3 = not_2_out ? 1'b1 : 1'bz;  // Controlled_Buffer controlled_buffer_1
  assign out_3 = nor_1_out ? 1'b0 : 1'bz;  // Controlled_Buffer controlled_buffer_2
endmodule

module cell100 (
  input  clk,
  input  val,
  input  reset,
  input  in_4,
  input  in_5,
  input  in_6,
  input  in_7,
  input  in_8,
  output out_9,
  output out_10,
  output out_11,
  output out_12
);

  wire multiplexer_1_out, multiplexer_2_out, nand_1_out, nand_2_out, nand_3_out, nand_4_out, not_1_out,
       not_2_out, transistor_1_out, transistor_3_out, transistor_6_out, transistor_7_out, transistor_9_out,
       transistor_12_out, transistor_13_out, transistor_15_out, transistor_18_out, transistor_19_out,
       transistor_21_out, transistor_23_out;

  not not_1 (not_1_out, clk);
  not not_2 (not_2_out, not_1_out);
  nand nand_1 (nand_1_out, in_7, nand_2_out);
  Multiplexer multiplexer_1 (.in0(in_6), .in1(nand_1_out), .out(multiplexer_1_out), .sel(in_5));
  Transistor transistor_1 (.in(val), .out(transistor_1_out), .gate(not_2_out));
  Transistor #(.\type ("n")) transistor_2 (.in(val), .out(transistor_1_out), .gate(not_1_out));
  nand nand_2 (nand_2_out, multiplexer_1_out, in_8);
  Transistor transistor_3 (.in(1'b1), .out(transistor_3_out), .gate(in_4));
  Transistor transistor_4 (.in(transistor_3_out), .out(transistor_1_out), .gate(not_1_out));
  Transistor #(.\type ("n")) transistor_5 (.in(transistor_6_out), .out(transistor_1_out), .gate(not_2_out));
  Transistor #(.\type ("n")) transistor_6 (.in(transistor_7_out), .out(transistor_6_out), .gate(in_4));
  Transistor #(.\type ("n")) transistor_7 (.in(1'b0), .out(transistor_7_out), .gate(transistor_9_out));
  nand nand_3 (nand_3_out, in_8, nand_4_out);
  Transistor transistor_8 (.in(1'b1), .out(transistor_3_out), .gate(transistor_9_out));
  Multiplexer multiplexer_2 (.in0(nand_3_out), .in1(nand_2_out), .out(multiplexer_2_out), .sel(in_5));
  nand nand_4 (nand_4_out, multiplexer_2_out, in_7);
  Transistor transistor_9 (.in(1'b1), .out(transistor_9_out), .gate(transistor_1_out));
  Transistor transistor_10 (.in(1'b1), .out(transistor_9_out), .gate(reset));
  Transistor #(.\type ("n")) transistor_11 (.in(transistor_12_out), .out(transistor_9_out), .gate(reset));
  Transistor #(.\type ("n")) transistor_12 (.in(1'b0), .out(transistor_12_out), .gate(transistor_1_out));
  not not_3 (out_11, nand_4_out);
  not not_4 (out_12, multiplexer_2_out);
  Transistor transistor_13 (.in(transistor_9_out), .out(transistor_13_out), .gate(not_1_out));
  Transistor #(.\type ("n")) transistor_14 (.in(transistor_9_out), .out(transistor_13_out), .gate(not_2_out));
  Transistor transistor_15 (.in(1'b1), .out(transistor_15_out), .gate(reset));
  Transistor transistor_16 (.in(transistor_15_out), .out(transistor_13_out), .gate(not_2_out));
  Transistor #(.\type ("n")) transistor_17 (.in(transistor_18_out), .out(transistor_13_out), .gate(not_1_out));
  Transistor #(.\type ("n")) transistor_18 (.in(transistor_19_out), .out(transistor_18_out), .gate(reset));
  Transistor #(.\type ("n")) transistor_19 (.in(1'b0), .out(transistor_19_out), .gate(transistor_21_out));
  Transistor transistor_20 (.in(1'b1), .out(transistor_15_out), .gate(transistor_21_out));
  Transistor transistor_21 (.in(1'b1), .out(transistor_21_out), .gate(transistor_13_out));
  Transistor #(.\type ("n")) transistor_22 (.in(transistor_23_out), .out(transistor_21_out), .gate(in_4));
  Transistor #(.\type ("n")) transistor_23 (.in(1'b0), .out(transistor_23_out), .gate(transistor_13_out));
  Transistor transistor_24 (.in(1'b1), .out(transistor_21_out), .gate(in_4));
  not not_5 (out_9, transistor_21_out);
  not not_6 (out_10, transistor_13_out);
endmodule
