// Logisim project ymcells.circ as structural Verilog
module D_LATCH (
  input  EN,
  input  D,
  output Q,
  output nQ
);

  D_Flip_Flop #(.trigger("high")) d_ff_1 (.clk(EN), .D(D), .Q(Q), .Qn(nQ));  // open: preset, en, reset
endmodule

module COMPL_INV (
  input  ne,
  input  A,
  input  ne_2,
  input  A_2,
  output nZ,
  output nZ_2
);

  wire not_1_out, transistor_1_out, transistor_3_out, transistor_6_out;

  Transistor transistor_1 (.in(1'b1), .out(transistor_1_out), .gate(ne_2));
  Transistor #(.\type ("n")) transistor_2 (.in(1'b0), .out(transistor_1_out), .gate(ne_2));
  Transistor transistor_3 (.in(1'b1), .out(transistor_3_out), .gate(A_2));
  Transistor transistor_4 (.in(transistor_3_out), .out(nZ), .gate(ne_2));
  Transistor #(.\type ("n")) transistor_5 (.in(transistor_6_out), .out(nZ), .gate(transistor_1_out));
  Transistor #(.\type ("n")) transistor_6 (.in(1'b0), .out(transistor_6_out), .gate(A_2));
  not not_1 (not_1_out, ne);
  assign nZ_2 = not_1_out ? ~A : 1'bz;  // Controlled_Inverter controlled_inverter_1

  // Notes on the sheet:
  //   A
  //   B
  //   A
  //   ~
endmodule

module cell7_OR (
  input  B,
  input  A,
  input  B_2,
  input  A_2,
  output Z,
  output Z_2
);

  wire transistor_1_out, transistor_2_out;

  Transistor transistor_1 (.in(1'b1), .out(transistor_1_out), .gate(A_2));
  Transistor transistor_2 (.in(transistor_1_out), .out(transistor_2_out), .gate(B_2));
  Transistor #(.\type ("n")) transistor_3 (.in(1'b0), .out(transistor_2_out), .gate(B_2));
  Transistor #(.\type ("n")) transistor_4 (.in(1'b0), .out(transistor_2_out), .gate(A_2));
  Transistor transistor_5 (.in(1'b1), .out(Z), .gate(transistor_2_out));
  Transistor #(.\type ("n")) transistor_6 (.in(1'b0), .out(Z), .gate(transistor_2_out));
  or or_1 (Z_2, B, A);

  // Notes on the sheet:
  //   A
  //   A
  //   B
  //   B
  //   ~
endmodule

module SR_BIT (
  input  nc2,
  input  STEP,
  input  LOAD,
  input  nc1,
  input  D,
  input  D_2,
  input  c1,
  input  c2,
  output Q,
  output Q_2
);

  wire d_latch_1_nq, transistor_1_out, transistor_3_out, transistor_4_out, transistor_6_out;

  Transistor transistor_1 (.in(D), .out(transistor_1_out), .gate(nc1));
  Transistor #(.\type ("n")) transistor_2 (.in(D), .out(transistor_1_out), .gate(c1));
  Transistor transistor_3 (.in(1'b1), .out(transistor_3_out), .gate(transistor_1_out));
  Transistor transistor_4 (.in(transistor_3_out), .out(transistor_4_out), .gate(nc2));
  Transistor #(.\type ("n")) transistor_5 (.in(transistor_6_out), .out(transistor_4_out), .gate(c2));
  Transistor #(.\type ("n")) transistor_6 (.in(1'b0), .out(transistor_6_out), .gate(transistor_1_out));
  Transistor transistor_7 (.in(1'b1), .out(Q), .gate(transistor_4_out));
  Transistor #(.\type ("n")) transistor_8 (.in(1'b0), .out(Q), .gate(transistor_4_out));
  D_LATCH d_latch_1 (.EN(LOAD), .D(D_2), .nQ(d_latch_1_nq));  // open: Q
  D_LATCH d_latch_2 (.EN(STEP), .D(d_latch_1_nq), .nQ(Q_2));  // open: Q

  // Notes on the sheet:
  //   ~
endmodule

module _3_NAND (
  input  C,
  input  B,
  input  C_2,
  input  A,
  input  B_2,
  input  A_2,
  output Z,
  output Z_2
);

  wire transistor_5_out, transistor_6_out;

  Transistor transistor_1 (.in(1'b1), .out(Z), .gate(A_2));
  Transistor transistor_2 (.in(1'b1), .out(Z), .gate(B_2));
  Transistor transistor_3 (.in(1'b1), .out(Z), .gate(C_2));
  Transistor #(.\type ("n")) transistor_4 (.in(transistor_5_out), .out(Z), .gate(C_2));
  Transistor #(.\type ("n")) transistor_5 (.in(transistor_6_out), .out(transistor_5_out), .gate(B_2));
  Transistor #(.\type ("n")) transistor_6 (.in(1'b0), .out(transistor_6_out), .gate(A_2));
  nand nand_1 (Z_2, C, B, A);

  // Notes on the sheet:
  //   A
  //   B
  //   C
  //   C
  //   B
  //   A
  //   ~
endmodule

module DLATCH_CMOS (
  input  nC,
  input  nE,
  input  E,
  input  D,
  input  D_2,
  input  C,
  output Q,
  output Q_2,
  output nQ,
  output nQ_2
);

  wire multiplexer_1_out, not_1_out, not_2_out, transistor_1_out, transistor_2_out, transistor_4_out,
       transistor_5_out, transistor_8_out, transistor_9_out;

  Transistor transistor_1 (.in(1'b1), .out(transistor_1_out), .gate(D));
  Transistor transistor_2 (.in(transistor_1_out), .out(transistor_2_out), .gate(C));
  Transistor #(.\type ("n")) transistor_3 (.in(transistor_4_out), .out(transistor_2_out), .gate(nC));
  Transistor #(.\type ("n")) transistor_4 (.in(1'b0), .out(transistor_4_out), .gate(D));
  Transistor transistor_5 (.in(1'b1), .out(transistor_5_out), .gate(transistor_9_out));
  Transistor transistor_6 (.in(transistor_5_out), .out(transistor_2_out), .gate(nC));
  Transistor #(.\type ("n")) transistor_7 (.in(transistor_8_out), .out(transistor_2_out), .gate(C));
  Transistor #(.\type ("n")) transistor_8 (.in(1'b0), .out(transistor_8_out), .gate(transistor_9_out));
  Transistor transistor_9 (.in(1'b1), .out(transistor_9_out), .gate(transistor_2_out));
  Transistor #(.\type ("n")) transistor_10 (.in(1'b0), .out(transistor_9_out), .gate(transistor_2_out));
  Transistor transistor_11 (.in(1'b1), .out(nQ_2), .gate(transistor_9_out));
  Transistor #(.\type ("n")) transistor_12 (.in(1'b0), .out(nQ_2), .gate(transistor_9_out));
  Transistor transistor_13 (.in(1'b1), .out(Q), .gate(nQ_2));
  Transistor #(.\type ("n")) transistor_14 (.in(1'b0), .out(Q), .gate(nQ_2));
  Multiplexer #(.disabled(0), .enable("false")) multiplexer_1 (
    .in0(not_2_out), .in1(D_2), .out(multiplexer_1_out), .sel(E));
  not not_1 (not_1_out, multiplexer_1_out);
  not not_2 (not_2_out, not_1_out);
  not not_3 (nQ, not_2_out);
  not not_4 (Q_2, nQ);

  // Notes on the sheet:
  //   1
  //   3
  //   4
  //   2
  //   7
  //   5
  //   6
  //   8
  //   9
  //   10
  //   11
  //   12
  //   13
  //   14
  //   ~
endmodule

module _2NOT_CMOS (
  input  A,
  input  A_2,
  output nZ,
  output Z,
  output Z_2,
  output nZ_2
);

  wire transistor_2_out, transistor_3_out, transistor_6_out, transistor_7_out;

  Transistor transistor_1 (.in(1'b1), .out(nZ_2), .gate(A));
  Transistor transistor_2 (.in(nZ_2), .out(transistor_2_out), .gate(A));
  Transistor #(.\type ("n")) transistor_3 (.in(nZ_2), .out(transistor_3_out), .gate(A));
  Transistor #(.\type ("n")) transistor_4 (.in(1'b0), .out(nZ_2), .gate(A));
  Transistor transistor_5 (.in(1'b1), .out(Z), .gate(nZ_2));
  Transistor transistor_6 (.in(Z), .out(transistor_6_out), .gate(nZ_2));
  Transistor #(.\type ("n")) transistor_7 (.in(Z), .out(transistor_7_out), .gate(nZ_2));
  Transistor #(.\type ("n")) transistor_8 (.in(1'b0), .out(Z), .gate(nZ_2));
  not not_1 (nZ, A_2);
  not not_2 (Z_2, nZ);
  // also tied to GND on the sheet: {transistor_3_out, transistor_7_out}
  // also tied to VCC on the sheet: {transistor_2_out, transistor_6_out}

  // Notes on the sheet:
  //   3
  //   4
  //   7
  //   8
  //   1
  //   2
  //   5
  //   6
  //   ~
endmodule

module SUPER_NOT (
  input  A,
  input  A_2,
  output nZ,
  output nZ_2
);

  wire transistor_2_out, transistor_3_out, transistor_6_out, transistor_7_out;

  Transistor transistor_1 (.in(1'b1), .out(nZ), .gate(A));
  Transistor transistor_2 (.in(nZ), .out(transistor_2_out), .gate(A));
  Transistor #(.\type ("n")) transistor_3 (.in(nZ), .out(transistor_3_out), .gate(A));
  Transistor #(.\type ("n")) transistor_4 (.in(1'b0), .out(nZ), .gate(A));
  Transistor transistor_5 (.in(1'b1), .out(nZ), .gate(A));
  Transistor transistor_6 (.in(nZ), .out(transistor_6_out), .gate(A));
  Transistor #(.\type ("n")) transistor_7 (.in(nZ), .out(transistor_7_out), .gate(A));
  Transistor #(.\type ("n")) transistor_8 (.in(1'b0), .out(nZ), .gate(A));
  not not_1 (nZ_2, A_2);
  // also tied to GND on the sheet: {transistor_3_out, transistor_7_out}
  // also tied to VCC on the sheet: {transistor_2_out, transistor_6_out}

  // Notes on the sheet:
  //   A
  //   C
  //   B
  //   D
  //   ~
endmodule

module NAND (
  input  B,
  input  A,
  input  B_2,
  input  A_2,
  output Z,
  output Z_2
);

  wire transistor_4_out;

  Transistor transistor_1 (.in(1'b1), .out(Z), .gate(A_2));
  Transistor transistor_2 (.in(1'b1), .out(Z), .gate(B_2));
  Transistor #(.\type ("n")) transistor_3 (.in(transistor_4_out), .out(Z), .gate(B_2));
  Transistor #(.\type ("n")) transistor_4 (.in(1'b0), .out(transistor_4_out), .gate(A_2));
  nand nand_1 (Z_2, B, A);

  // Notes on the sheet:
  //   A
  //   B
  //   B
  //   A
  //   ~
endmodule

module cell1_NOT (
  input  A,
  input  A_2,
  output nZ,
  output nZ_2
);

  Transistor transistor_1 (.in(1'b1), .out(nZ), .gate(A));
  Transistor #(.\type ("n")) transistor_2 (.in(1'b0), .out(nZ), .gate(A));
  not not_1 (nZ_2, A_2);

  // Notes on the sheet:
  //   ~
endmodule

module cell16_AOI21 (
  input  A1,
  input  A1_2,
  input  a2,
  input  b,
  input  A2_2,
  input  B_2,
  output Z,
  output Z_2
);

  wire and_1_out, transistor_1_out, transistor_3_out;

  Transistor transistor_1 (.in(1'b1), .out(transistor_1_out), .gate(A1));
  Transistor #(.\type ("n")) transistor_2 (.in(transistor_3_out), .out(Z), .gate(A1));
  Transistor #(.\type ("n")) transistor_3 (.in(1'b0), .out(transistor_3_out), .gate(A2_2));
  Transistor transistor_4 (.in(1'b1), .out(transistor_1_out), .gate(A2_2));
  Transistor transistor_5 (.in(transistor_1_out), .out(Z), .gate(B_2));
  Transistor #(.\type ("n")) transistor_6 (.in(1'b0), .out(Z), .gate(B_2));
  and and_1 (and_1_out, A1_2, a2);
  nor nor_1 (Z_2, and_1_out, b);

  // Notes on the sheet:
  //   1
  //   4
  //   5
  //   2
  //   3
  //   6
  //   ~
endmodule

module _3AND (
  input  B,
  input  B_2,
  input  A,
  input  A_2,
  input  C,
  input  C_2,
  output Z,
  output Z_2
);

  wire transistor_1_out, transistor_5_out, transistor_6_out;

  Transistor transistor_1 (.in(1'b1), .out(transistor_1_out), .gate(B_2));
  Transistor transistor_2 (.in(1'b1), .out(transistor_1_out), .gate(A_2));
  Transistor transistor_3 (.in(1'b1), .out(transistor_1_out), .gate(C_2));
  Transistor #(.\type ("n")) transistor_4 (.in(transistor_5_out), .out(transistor_1_out), .gate(B_2));
  Transistor #(.\type ("n")) transistor_5 (.in(transistor_6_out), .out(transistor_5_out), .gate(A_2));
  Transistor #(.\type ("n")) transistor_6 (.in(1'b0), .out(transistor_6_out), .gate(C_2));
  Transistor transistor_7 (.in(1'b1), .out(Z), .gate(transistor_1_out));
  Transistor #(.\type ("n")) transistor_8 (.in(1'b0), .out(Z), .gate(transistor_1_out));
  and and_1 (Z_2, B, A, C);

  // Notes on the sheet:
  //   1
  //   3
  //   2
  //   5
  //   8
  //   6
  //   4
  //   7
  //   ~
endmodule

module XOR (
  input  A,
  input  B,
  input  A_2,
  input  B_2,
  output Z,
  output Z_2
);

  wire transistor_1_out, transistor_2_out, transistor_5_out, transistor_8_out, transistor_9_out;

  Transistor transistor_1 (.in(1'b1), .out(transistor_1_out), .gate(B_2));
  Transistor transistor_2 (.in(transistor_1_out), .out(transistor_2_out), .gate(A_2));
  Transistor #(.\type ("n")) transistor_3 (.in(1'b0), .out(transistor_2_out), .gate(A_2));
  Transistor #(.\type ("n"), .gate("br")) transistor_4 (.in(1'b0), .out(transistor_2_out), .gate(B_2));
  Transistor transistor_5 (.in(1'b1), .out(transistor_5_out), .gate(B_2));
  Transistor transistor_6 (.in(transistor_5_out), .out(Z), .gate(transistor_2_out));
  Transistor #(.\type ("n")) transistor_7 (.in(transistor_8_out), .out(Z), .gate(A_2));
  Transistor #(.\type ("n")) transistor_8 (.in(1'b0), .out(transistor_8_out), .gate(B_2));
  Transistor transistor_9 (.in(1'b1), .out(transistor_9_out), .gate(A_2));
  Transistor transistor_10 (.in(transistor_9_out), .out(Z), .gate(transistor_2_out));
  Transistor #(.\type ("n")) transistor_11 (.in(1'b0), .out(Z), .gate(transistor_2_out));
  xor xor_1 (Z_2, A, B);

  // Notes on the sheet:
  //   2
  //   1
  //   7
  //   8
  //   3
  //   4
  //   10
  //   9
  //   6
  //   5
  //   11
  //   ~
endmodule

module LFSR_BIT (
  input  nC2,
  input  nC1,
  input  a1,
  input  C,
  input  D,
  input  a1_2,
  input  E,
  input  F,
  input  b,
  input  a2,
  input  b_2,
  input  a2_2,
  input  C1,
  input  C2,
  output Q,
  output Q_2
);

  wire and_1_out, and_2_out, d_latch_1_nq, nor_1_out, not_1_out, transistor_1_out, transistor_2_out,
       transistor_4_out, transistor_8_out, transistor_9_out, transistor_10_out, transistor_12_out,
       transistor_13_out, transistor_14_out, transistor_16_out, transistor_17_out;

  Transistor transistor_1 (.in(1'b1), .out(transistor_1_out), .gate(a1));
  Transistor transistor_2 (.in(transistor_1_out), .out(transistor_2_out), .gate(transistor_17_out));
  Transistor #(.\type ("n")) transistor_3 (.in(transistor_4_out), .out(transistor_2_out), .gate(a2_2));
  Transistor #(.\type ("n")) transistor_4 (.in(1'b0), .out(transistor_4_out), .gate(a1));
  Transistor transistor_5 (.in(1'b1), .out(transistor_1_out), .gate(a2_2));
  Transistor transistor_6 (.in(transistor_1_out), .out(transistor_2_out), .gate(b));
  Transistor #(.\type ("n")) transistor_7 (.in(transistor_8_out), .out(transistor_2_out), .gate(b));
  Transistor #(.\type ("n")) transistor_8 (.in(1'b0), .out(transistor_8_out), .gate(transistor_17_out));
  Transistor transistor_9 (.in(1'b1), .out(transistor_9_out), .gate(transistor_2_out));
  Transistor transistor_10 (.in(transistor_9_out), .out(transistor_10_out), .gate(nC1));
  Transistor #(.\type ("n")) transistor_11 (.in(transistor_12_out), .out(transistor_10_out), .gate(C1));
  Transistor #(.\type ("n")) transistor_12 (.in(1'b0), .out(transistor_12_out), .gate(transistor_2_out));
  Transistor transistor_13 (.in(1'b1), .out(transistor_13_out), .gate(transistor_10_out));
  Transistor transistor_14 (.in(transistor_13_out), .out(transistor_14_out), .gate(nC2));
  Transistor #(.\type ("n")) transistor_15 (.in(transistor_16_out), .out(transistor_14_out), .gate(C2));
  Transistor #(.\type ("n")) transistor_16 (.in(1'b0), .out(transistor_16_out), .gate(transistor_10_out));
  Transistor transistor_17 (.in(1'b1), .out(transistor_17_out), .gate(transistor_14_out));
  Transistor #(.\type ("n")) transistor_18 (.in(1'b0), .out(transistor_17_out), .gate(transistor_14_out));
  Transistor transistor_19 (.in(1'b1), .out(Q), .gate(transistor_14_out));
  Transistor #(.\type ("n")) transistor_20 (.in(1'b0), .out(Q), .gate(transistor_14_out));
  and and_1 (and_1_out, a1_2, a2);
  and and_2 (and_2_out, b_2, Q_2);
  not not_1 (not_1_out, nor_1_out);
  nor nor_1 (nor_1_out, and_1_out, and_2_out);
  D_LATCH d_latch_1 (.EN(E), .D(not_1_out), .nQ(d_latch_1_nq));  // open: Q
  D_LATCH d_latch_2 (.EN(F), .D(d_latch_1_nq), .nQ(Q_2));  // open: Q

  // Notes on the sheet:
  //   1
  //   2
  //   12
  //   11
  //   4
  //   3
  //   13
  //   14
  //   5
  //   6
  //   16
  //   15
  //   7
  //   8
  //   18
  //   17
  //   9
  //   19
  //   10
  //   20
  //   ~
  //   COMPL
  //   COMPL
endmodule

module _4AND_OR__AON2222 (
  input  d1,
  input  d1_2,
  input  d2,
  input  d2_2,
  input  c1,
  input  c1_2,
  input  c2,
  input  c2_2,
  input  b1,
  input  b1_2,
  input  b2,
  input  b2_2,
  input  a1,
  input  a1_2,
  input  a2,
  input  a2_2,
  output Z,
  output Z_2
);

  wire and_1_out, and_2_out, and_3_out, and_4_out, transistor_1_out, transistor_2_out, transistor_4_out,
       transistor_6_out, transistor_7_out, transistor_8_out, transistor_9_out, transistor_12_out;

  Transistor #(.\type ("n")) transistor_1 (.in(transistor_2_out), .out(transistor_1_out), .gate(a1_2));
  Transistor #(.\type ("n")) transistor_2 (.in(1'b0), .out(transistor_2_out), .gate(a2_2));
  Transistor #(.\type ("n")) transistor_3 (.in(transistor_4_out), .out(transistor_1_out), .gate(d1));
  Transistor #(.\type ("n")) transistor_4 (.in(1'b0), .out(transistor_4_out), .gate(d2));
  Transistor #(.\type ("n")) transistor_5 (.in(transistor_6_out), .out(transistor_1_out), .gate(c1));
  Transistor #(.\type ("n")) transistor_6 (.in(1'b0), .out(transistor_6_out), .gate(c2));
  Transistor transistor_7 (.in(1'b1), .out(transistor_7_out), .gate(a1_2));
  Transistor transistor_8 (.in(transistor_7_out), .out(transistor_8_out), .gate(d1));
  Transistor transistor_9 (.in(transistor_8_out), .out(transistor_9_out), .gate(c1));
  Transistor transistor_10 (.in(transistor_9_out), .out(transistor_1_out), .gate(b1));
  Transistor #(.\type ("n")) transistor_11 (.in(transistor_12_out), .out(transistor_1_out), .gate(b1));
  Transistor #(.\type ("n")) transistor_12 (.in(1'b0), .out(transistor_12_out), .gate(b2));
  Transistor transistor_13 (.in(1'b1), .out(transistor_7_out), .gate(a2_2));
  Transistor transistor_14 (.in(transistor_7_out), .out(transistor_8_out), .gate(d2));
  Transistor transistor_15 (.in(transistor_8_out), .out(transistor_9_out), .gate(c2));
  Transistor transistor_16 (.in(transistor_9_out), .out(transistor_1_out), .gate(b2));
  Transistor transistor_17 (.in(1'b1), .out(Z_2), .gate(transistor_1_out));
  Transistor #(.\type ("n")) transistor_18 (.in(1'b0), .out(Z_2), .gate(transistor_1_out));
  and and_1 (and_1_out, d1_2, d2_2);
  and and_2 (and_2_out, c1_2, c2_2);
  and and_3 (and_3_out, b1_2, b2_2);
  and and_4 (and_4_out, a1, a2);
  or or_1 (Z, and_1_out, and_2_out, and_3_out, and_4_out);

  // Notes on the sheet:
  //   ~
endmodule

module cell24_SR_FF (
  input  A_SET,
  input  A,
  input  B_RESET,
  input  B,
  output nQ,
  output Q,
  output Q_2,
  output nQ_2
);

  wire transistor_1_out, transistor_2_out, transistor_5_out, transistor_6_out;

  Transistor #(.\type ("n")) transistor_1 (.in(1'b0), .out(transistor_1_out), .gate(A));
  Transistor transistor_2 (.in(1'b1), .out(transistor_2_out), .gate(transistor_5_out));
  Transistor transistor_3 (.in(transistor_2_out), .out(transistor_1_out), .gate(A));
  Transistor #(.\type ("n")) transistor_4 (.in(1'b0), .out(transistor_1_out), .gate(transistor_5_out));
  Transistor #(.\type ("n")) transistor_5 (.in(1'b0), .out(transistor_5_out), .gate(B));
  Transistor transistor_6 (.in(1'b1), .out(transistor_6_out), .gate(transistor_1_out));
  Transistor transistor_7 (.in(transistor_6_out), .out(transistor_5_out), .gate(B));
  Transistor #(.\type ("n")) transistor_8 (.in(1'b0), .out(transistor_5_out), .gate(transistor_1_out));
  Transistor transistor_9 (.in(1'b1), .out(nQ_2), .gate(transistor_5_out));
  Transistor #(.\type ("n")) transistor_10 (.in(1'b0), .out(nQ_2), .gate(transistor_5_out));
  Transistor transistor_11 (.in(1'b1), .out(Q), .gate(transistor_1_out));
  Transistor #(.\type ("n")) transistor_12 (.in(1'b0), .out(Q), .gate(transistor_1_out));
  nor nor_1 (nQ, A_SET, Q_2);
  nor nor_2 (Q_2, nQ, B_RESET);

  // Notes on the sheet:
  //   4
  //   1
  //   2
  //   3
  //   8
  //   5
  //   6
  //   7
  //   9
  //   10
  //   11
  //   12
  //   ~
endmodule

module HALF_SUM (
  input  A,
  input  B,
  input  B_2,
  input  A_2,
  output nSUM,
  output nSUM_2,
  output SUM,
  output SUM_2,
  output CO,
  output CO_2
);

  wire and_1_out, and_2_out, not_1_out, not_2_out, transistor_1_out, transistor_2_out, transistor_4_out,
       transistor_9_out, transistor_12_out;

  Transistor transistor_1 (.in(1'b1), .out(transistor_1_out), .gate(A_2));
  Transistor transistor_2 (.in(transistor_1_out), .out(transistor_2_out), .gate(B_2));
  Transistor #(.\type ("n")) transistor_3 (.in(transistor_4_out), .out(transistor_2_out), .gate(transistor_9_out));
  Transistor #(.\type ("n")) transistor_4 (.in(1'b0), .out(transistor_4_out), .gate(A_2));
  Transistor transistor_5 (.in(1'b1), .out(transistor_2_out), .gate(transistor_9_out));
  Transistor transistor_6 (.in(1'b1), .out(SUM_2), .gate(transistor_2_out));
  Transistor #(.\type ("n")) transistor_7 (.in(1'b0), .out(SUM_2), .gate(transistor_2_out));
  Transistor #(.\type ("n")) transistor_8 (.in(1'b0), .out(transistor_4_out), .gate(B_2));
  Transistor transistor_9 (.in(1'b1), .out(transistor_9_out), .gate(A_2));
  Transistor transistor_10 (.in(1'b1), .out(transistor_9_out), .gate(B_2));
  Transistor #(.\type ("n")) transistor_11 (.in(transistor_12_out), .out(transistor_9_out), .gate(B_2));
  Transistor #(.\type ("n")) transistor_12 (.in(1'b0), .out(transistor_12_out), .gate(A_2));
  Transistor transistor_13 (.in(1'b1), .out(nSUM), .gate(SUM_2));
  Transistor #(.\type ("n")) transistor_14 (.in(1'b0), .out(nSUM), .gate(SUM_2));
  Transistor transistor_15 (.in(1'b1), .out(CO_2), .gate(transistor_9_out));
  Transistor #(.\type ("n")) transistor_16 (.in(1'b0), .out(CO_2), .gate(transistor_9_out));
  not not_1 (not_1_out, B);
  and and_1 (and_1_out, not_1_out, A);
  and and_2 (and_2_out, B, not_2_out);
  not not_2 (not_2_out, A);
  and and_3 (CO, B, A);
  or or_1 (SUM, and_1_out, and_2_out);
  not not_3 (nSUM_2, SUM);

  // Notes on the sheet:
  //   ~
endmodule

module cell9_cgi2a (
  input  A,
  input  A_2,
  input  B1,
  input  B2,
  input  B1_2,
  input  B2_2,
  output Z,
  output Z_2
);

  wire and_1_out, nor_1_out, nor_2_out, transistor_1_out, transistor_3_out, transistor_4_out,
       transistor_6_out, transistor_7_out, transistor_10_out;

  Transistor transistor_1 (.in(1'b1), .out(transistor_1_out), .gate(A_2));
  Transistor #(.\type ("n")) transistor_2 (.in(1'b0), .out(transistor_1_out), .gate(A_2));
  Transistor transistor_3 (.in(1'b1), .out(transistor_3_out), .gate(transistor_1_out));
  Transistor transistor_4 (.in(transistor_3_out), .out(transistor_4_out), .gate(B1_2));
  Transistor #(.\type ("n")) transistor_5 (.in(transistor_6_out), .out(transistor_4_out), .gate(B1_2));
  Transistor #(.\type ("n")) transistor_6 (.in(1'b0), .out(transistor_6_out), .gate(transistor_1_out));
  Transistor transistor_7 (.in(1'b1), .out(transistor_7_out), .gate(transistor_1_out));
  Transistor transistor_8 (.in(transistor_7_out), .out(transistor_4_out), .gate(B2_2));
  Transistor #(.\type ("n")) transistor_9 (.in(transistor_10_out), .out(transistor_4_out), .gate(B2_2));
  Transistor #(.\type ("n")) transistor_10 (.in(1'b0), .out(transistor_10_out), .gate(transistor_1_out));
  Transistor #(.gate("br")) transistor_11 (.in(1'b1), .out(transistor_7_out), .gate(B1_2));
  Transistor #(.\type ("n"), .gate("br")) transistor_12 (.in(1'b0), .out(transistor_10_out), .gate(B1_2));
  Transistor transistor_13 (.in(1'b1), .out(Z), .gate(transistor_4_out));
  Transistor #(.\type ("n")) transistor_14 (.in(1'b0), .out(Z), .gate(transistor_4_out));
  nor nor_1 (nor_1_out, B1, B2);
  and and_1 (and_1_out, B1, B2);
  nor nor_2 (nor_2_out, A, nor_1_out);
  or or_1 (Z_2, nor_2_out, and_1_out);

  // Notes on the sheet:
  //   ~
endmodule

module DFF (
  input  nC2,
  input  nC1,
  input  nC1_2,
  input  C1,
  input  D,
  input  D_2,
  input  C1_2,
  input  C2,
  output Q,
  output Q_2,
  output nQ,
  output nQ_2
);

  wire transistor_1_out, transistor_2_out, transistor_4_out, transistor_5_out, transistor_7_out,
       transistor_10_out, transistor_11_out, transistor_14_out, transistor_15_out, transistor_18_out;

  Transistor transistor_1 (.in(1'b1), .out(transistor_1_out), .gate(D));
  Transistor #(.gate("br")) transistor_2 (.in(transistor_1_out), .out(transistor_2_out), .gate(nC1));
  Transistor #(.\type ("n"), .gate("br")) transistor_3 (.in(transistor_4_out), .out(transistor_2_out), .gate(C1_2));
  Transistor #(.\type ("n")) transistor_4 (.in(1'b0), .out(transistor_4_out), .gate(D));
  Transistor #(.gate("br")) transistor_5 (.in(1'b1), .out(transistor_5_out), .gate(transistor_7_out));
  Transistor transistor_6 (.in(transistor_5_out), .out(transistor_2_out), .gate(C1_2));
  Transistor transistor_7 (.in(1'b1), .out(transistor_7_out), .gate(transistor_2_out));
  Transistor #(.\type ("n")) transistor_8 (.in(1'b0), .out(transistor_7_out), .gate(transistor_2_out));
  Transistor #(.\type ("n")) transistor_9 (.in(transistor_10_out), .out(transistor_2_out), .gate(nC1));
  Transistor #(.\type ("n"), .gate("br")) transistor_10 (.in(1'b0), .out(transistor_10_out), .gate(transistor_7_out));
  Transistor transistor_11 (.in(1'b1), .out(transistor_11_out), .gate(transistor_7_out));
  Transistor #(.gate("br")) transistor_12 (.in(transistor_11_out), .out(nQ_2), .gate(nC2));
  Transistor #(.\type ("n"), .gate("br")) transistor_13 (.in(transistor_14_out), .out(nQ_2), .gate(C2));
  Transistor #(.\type ("n")) transistor_14 (.in(1'b0), .out(transistor_14_out), .gate(transistor_7_out));
  Transistor #(.gate("br")) transistor_15 (.in(1'b1), .out(transistor_15_out), .gate(Q_2));
  Transistor transistor_16 (.in(transistor_15_out), .out(nQ_2), .gate(C2));
  Transistor #(.\type ("n")) transistor_17 (.in(transistor_18_out), .out(nQ_2), .gate(nC2));
  Transistor #(.\type ("n"), .gate("br")) transistor_18 (.in(1'b0), .out(transistor_18_out), .gate(Q_2));
  Transistor transistor_19 (.in(1'b1), .out(Q_2), .gate(nQ_2));
  Transistor #(.\type ("n")) transistor_20 (.in(1'b0), .out(Q_2), .gate(nQ_2));
  D_Flip_Flop d_ff_1 (.clk(C1), .D(D_2), .Q(Q), .Qn(nQ));  // open: preset, en, reset

  // Notes on the sheet:
  //   ~
  //   COMPL
endmodule

module COUNTER_BIT (
  input  nC2,
  input  nC1,
  input  C2,
  input  C1,
  input  CI,
  input  CARRY_IN,
  input  nEN,
  input  nEN_2,
  input  C1_2,
  input  C2_2,
  output Q,
  output Q_2,
  output nQ1,
  output CARRY_OUT,
  output nQ,
  output CO
);

  wire d_ff_1_qn, not_1_out, not_2_out, transistor_1_out, transistor_4_out, transistor_7_out,
       transistor_8_out, transistor_9_out, transistor_12_out, transistor_15_out, transistor_16_out,
       transistor_18_out, transistor_19_out, transistor_20_out, transistor_22_out, transistor_23_out,
       xor_1_out;

  Transistor transistor_1 (.in(1'b1), .out(transistor_1_out), .gate(CI));
  Transistor #(.\type ("n")) transistor_2 (.in(1'b0), .out(transistor_1_out), .gate(CI));
  Transistor #(.\type ("n")) transistor_3 (.in(1'b0), .out(CO), .gate(transistor_23_out));
  Transistor transistor_4 (.in(1'b1), .out(transistor_4_out), .gate(transistor_23_out));
  Transistor transistor_5 (.in(transistor_4_out), .out(CO), .gate(transistor_1_out));
  Transistor #(.\type ("n")) transistor_6 (.in(1'b0), .out(CO), .gate(transistor_1_out));
  Transistor #(.\type ("n")) transistor_7 (.in(transistor_8_out), .out(transistor_7_out), .gate(transistor_23_out));
  Transistor #(.\type ("n")) transistor_8 (.in(1'b0), .out(transistor_8_out), .gate(transistor_1_out));
  Transistor transistor_9 (.in(1'b1), .out(transistor_9_out), .gate(transistor_1_out));
  Transistor #(.\type ("n")) transistor_10 (.in(1'b0), .out(transistor_7_out), .gate(nEN_2));
  Transistor transistor_11 (.in(1'b1), .out(transistor_9_out), .gate(transistor_23_out));
  Transistor transistor_12 (.in(transistor_9_out), .out(transistor_12_out), .gate(nEN_2));
  Transistor transistor_13 (.in(transistor_12_out), .out(transistor_7_out), .gate(CO));
  Transistor #(.\type ("n")) transistor_14 (.in(1'b0), .out(transistor_7_out), .gate(CO));
  Transistor transistor_15 (.in(1'b1), .out(transistor_15_out), .gate(transistor_7_out));
  Transistor transistor_16 (.in(transistor_15_out), .out(transistor_16_out), .gate(nC1));
  Transistor #(.\type ("n")) transistor_17 (.in(transistor_18_out), .out(transistor_16_out), .gate(C1_2));
  Transistor #(.\type ("n")) transistor_18 (.in(1'b0), .out(transistor_18_out), .gate(transistor_7_out));
  Transistor transistor_19 (.in(1'b1), .out(transistor_19_out), .gate(transistor_16_out));
  Transistor transistor_20 (.in(transistor_19_out), .out(transistor_20_out), .gate(nC2));
  Transistor #(.\type ("n")) transistor_21 (.in(transistor_22_out), .out(transistor_20_out), .gate(C2_2));
  Transistor #(.\type ("n")) transistor_22 (.in(1'b0), .out(transistor_22_out), .gate(transistor_16_out));
  Transistor transistor_23 (.in(1'b1), .out(transistor_23_out), .gate(transistor_20_out));
  Transistor #(.\type ("n")) transistor_24 (.in(1'b0), .out(transistor_23_out), .gate(transistor_20_out));
  Transistor transistor_25 (.in(1'b1), .out(nQ), .gate(transistor_20_out));
  Transistor #(.\type ("n")) transistor_26 (.in(1'b0), .out(nQ), .gate(transistor_20_out));
  Transistor transistor_27 (.in(1'b1), .out(Q_2), .gate(nQ));
  Transistor #(.\type ("n")) transistor_28 (.in(1'b0), .out(Q_2), .gate(nQ));
  xor xor_1 (xor_1_out, CARRY_IN, nQ1);
  not not_1 (not_1_out, nEN);
  D_Flip_Flop #(.trigger("high")) d_ff_1 (
    .clk(C1), .D(xor_1_out), .Qn(d_ff_1_qn), .en(not_1_out));  // open: Q, preset, reset
  not not_2 (not_2_out, CARRY_IN);
  D_LATCH d_latch_1 (.EN(C2), .D(d_ff_1_qn), .Q(Q), .nQ(nQ1));
  nor nor_1 (CARRY_OUT, nQ1, not_2_out);

  // Notes on the sheet:
  //   1
  //   2
  //   5
  //   3
  //   4
  //   6
  //   10
  //   8
  //   7
  //   13
  //   9
  //   11
  //   12
  //   14
  //   16
  //   15
  //   17
  //   18
  //   20
  //   19
  //   21
  //   22
  //   23
  //   24
  //   25
  //   26
  //   27
  //   28
  //   ~
endmodule

module FULL_ADDER (
  input  A,
  input  B,
  input  CI,
  input  CI_2,
  input  A_2,
  input  B_2,
  output SUM,
  output SUM_2,
  output CO,
  output CO_2
);

  wire and_1_out, and_2_out, transistor_1_out, transistor_3_out, transistor_5_out, transistor_7_out,
       transistor_10_out, transistor_11_out, transistor_13_out, transistor_15_out, transistor_19_out,
       transistor_20_out, transistor_23_out, transistor_24_out, xor_1_out;

  Transistor transistor_1 (.in(1'b1), .out(transistor_1_out), .gate(A_2));
  Transistor #(.gate("br")) transistor_2 (.in(1'b1), .out(transistor_1_out), .gate(B_2));
  Transistor transistor_3 (.in(transistor_1_out), .out(transistor_3_out), .gate(CI));
  Transistor #(.\type ("n")) transistor_4 (.in(transistor_5_out), .out(transistor_3_out), .gate(CI));
  Transistor #(.\type ("n"), .gate("br")) transistor_5 (.in(1'b0), .out(transistor_5_out), .gate(B_2));
  Transistor #(.\type ("n")) transistor_6 (.in(1'b0), .out(transistor_5_out), .gate(A_2));
  Transistor transistor_7 (.in(1'b1), .out(transistor_7_out), .gate(B_2));
  Transistor transistor_8 (.in(transistor_7_out), .out(transistor_3_out), .gate(A_2));
  Transistor #(.\type ("n")) transistor_9 (.in(transistor_10_out), .out(transistor_3_out), .gate(A_2));
  Transistor #(.\type ("n")) transistor_10 (.in(1'b0), .out(transistor_10_out), .gate(B_2));
  Transistor #(.gate("br")) transistor_11 (.in(1'b1), .out(transistor_11_out), .gate(A_2));
  Transistor transistor_12 (.in(1'b1), .out(transistor_11_out), .gate(CI));
  Transistor transistor_13 (.in(transistor_11_out), .out(transistor_13_out), .gate(transistor_3_out));
  Transistor #(.\type ("n")) transistor_14 (.in(transistor_15_out), .out(transistor_13_out), .gate(transistor_3_out));
  Transistor #(.\type ("n")) transistor_15 (.in(1'b0), .out(transistor_15_out), .gate(CI));
  Transistor #(.\type ("n"), .gate("br")) transistor_16 (.in(1'b0), .out(transistor_15_out), .gate(A_2));
  Transistor #(.gate("br")) transistor_17 (.in(1'b1), .out(transistor_11_out), .gate(B_2));
  Transistor #(.\type ("n"), .gate("br")) transistor_18 (.in(1'b0), .out(transistor_15_out), .gate(B_2));
  Transistor transistor_19 (.in(1'b1), .out(transistor_19_out), .gate(B_2));
  Transistor transistor_20 (.in(transistor_19_out), .out(transistor_20_out), .gate(A_2));
  Transistor transistor_21 (.in(transistor_20_out), .out(transistor_13_out), .gate(CI));
  Transistor #(.\type ("n")) transistor_22 (.in(transistor_23_out), .out(transistor_13_out), .gate(CI));
  Transistor #(.\type ("n")) transistor_23 (.in(transistor_24_out), .out(transistor_23_out), .gate(A_2));
  Transistor #(.\type ("n")) transistor_24 (.in(1'b0), .out(transistor_24_out), .gate(B_2));
  Transistor transistor_25 (.in(1'b1), .out(SUM_2), .gate(transistor_13_out));
  Transistor #(.\type ("n")) transistor_26 (.in(1'b0), .out(SUM_2), .gate(transistor_13_out));
  Transistor transistor_27 (.in(1'b1), .out(CO_2), .gate(transistor_3_out));
  Transistor #(.\type ("n")) transistor_28 (.in(1'b0), .out(CO_2), .gate(transistor_3_out));
  xor xor_1 (xor_1_out, A, B);
  xor xor_2 (SUM, xor_1_out, CI_2);
  and and_1 (and_1_out, xor_1_out, CI_2);
  and and_2 (and_2_out, B, A);
  or or_1 (CO, and_1_out, and_2_out);

  // Notes on the sheet:
  //   ~
endmodule

module AON22 (
  input  a1,
  input  a1_2,
  input  a2,
  input  a2_2,
  input  b1,
  input  b2,
  input  b1_2,
  input  b2_2,
  output Z,
  output Z_2
);

  wire and_1_out, and_2_out, transistor_1_out, transistor_2_out, transistor_4_out, transistor_10_out;

  Transistor transistor_1 (.in(1'b1), .out(transistor_1_out), .gate(a1));
  Transistor transistor_2 (.in(transistor_1_out), .out(transistor_2_out), .gate(b1_2));
  Transistor #(.\type ("n")) transistor_3 (.in(transistor_4_out), .out(transistor_2_out), .gate(a2_2));
  Transistor #(.\type ("n")) transistor_4 (.in(1'b0), .out(transistor_4_out), .gate(a1));
  Transistor transistor_5 (.in(1'b1), .out(transistor_1_out), .gate(a2_2));
  Transistor transistor_6 (.in(transistor_1_out), .out(transistor_2_out), .gate(b2_2));
  Transistor transistor_7 (.in(1'b1), .out(Z), .gate(transistor_2_out));
  Transistor #(.\type ("n")) transistor_8 (.in(transistor_10_out), .out(transistor_2_out), .gate(b1_2));
  Transistor #(.\type ("n")) transistor_9 (.in(1'b0), .out(Z), .gate(transistor_2_out));
  Transistor #(.\type ("n")) transistor_10 (.in(1'b0), .out(transistor_10_out), .gate(b2_2));
  and and_1 (and_1_out, a1_2, a2);
  and and_2 (and_2_out, b1, b2);
  or or_1 (Z_2, and_1_out, and_2_out);

  // Notes on the sheet:
  //   ~
endmodule

module DC (
  input  EN,
  input  _1,
  input  _2,
  output _3,
  output _2_2,
  output _0,
  output _1_2
);

  wire nand_1_out, nand_2_out, nand_3_out, nand_4_out, not_1_out, not_2_out;

  not not_1 (not_1_out, _1);
  not not_2 (not_2_out, _2);
  nand nand_1 (nand_1_out, _1, _2);
  nand nand_2 (nand_2_out, not_1_out, _2);
  nand nand_3 (nand_3_out, not_1_out, not_2_out);
  nand nand_4 (nand_4_out, not_2_out, _1);
  and and_1 (_3, EN, nand_1_out);
  and and_2 (_2_2, EN, nand_2_out);
  and and_3 (_0, EN, nand_3_out);
  and and_4 (_1_2, EN, nand_4_out);
endmodule

module aoi22 (
  input  a1,
  input  a1_2,
  input  a2,
  input  a2_2,
  input  b1,
  input  b2,
  input  b1_2,
  input  b2_2,
  output Z,
  output Z_2
);

  wire and_1_out, and_2_out, transistor_1_out, transistor_4_out, transistor_8_out;

  Transistor transistor_1 (.in(1'b1), .out(transistor_1_out), .gate(a1));
  Transistor transistor_2 (.in(transistor_1_out), .out(Z), .gate(b1_2));
  Transistor #(.\type ("n")) transistor_3 (.in(transistor_4_out), .out(Z), .gate(a2_2));
  Transistor #(.\type ("n")) transistor_4 (.in(1'b0), .out(transistor_4_out), .gate(a1));
  Transistor transistor_5 (.in(1'b1), .out(transistor_1_out), .gate(a2_2));
  Transistor transistor_6 (.in(transistor_1_out), .out(Z), .gate(b2_2));
  Transistor #(.\type ("n")) transistor_7 (.in(transistor_8_out), .out(Z), .gate(b1_2));
  Transistor #(.\type ("n")) transistor_8 (.in(1'b0), .out(transistor_8_out), .gate(b2_2));
  and and_1 (and_1_out, a1_2, a2);
  and and_2 (and_2_out, b1, b2);
  nor nor_1 (Z_2, and_1_out, and_2_out);

  // Notes on the sheet:
  //   ~
endmodule

module cell33 (
  input  a,
  input  a_2,
  output nZ,
  output nZ_2,
  output Z,
  output Z_2
);

  wire not_1_out, transistor_3_out;

  Transistor transistor_1 (.in(1'b1), .out(nZ), .gate(a));
  Transistor #(.\type ("n")) transistor_2 (.in(1'b0), .out(nZ), .gate(a));
  Transistor transistor_3 (.in(1'b1), .out(transistor_3_out), .gate(a));
  Transistor #(.\type ("n")) transistor_4 (.in(1'b0), .out(transistor_3_out), .gate(a));
  Transistor transistor_5 (.in(1'b1), .out(nZ), .gate(a));
  Transistor #(.\type ("n")) transistor_6 (.in(1'b0), .out(nZ), .gate(a));
  Transistor transistor_7 (.in(1'b1), .out(Z_2), .gate(transistor_3_out));
  Transistor transistor_8 (.in(1'b1), .out(Z_2), .gate(transistor_3_out));
  Transistor #(.\type ("n")) transistor_9 (.in(1'b0), .out(Z_2), .gate(transistor_3_out));
  Transistor #(.\type ("n")) transistor_10 (.in(1'b0), .out(Z_2), .gate(transistor_3_out));
  not not_1 (not_1_out, a_2);
  not not_2 (nZ_2, a_2);
  not not_3 (Z, not_1_out);

  // Notes on the sheet:
  //   ~
endmodule

module cell35__OR5 (
  input  a,
  input  b,
  input  a_2,
  input  b_2,
  input  c,
  input  d,
  input  c_2,
  input  e,
  input  d_2,
  input  e_2,
  output Z,
  output Z_2
);

  wire nor_1_out, nor_2_out, transistor_1_out, transistor_2_out, transistor_3_out, transistor_4_out,
       transistor_6_out, transistor_13_out;

  Transistor #(.\type ("n")) transistor_1 (.in(1'b0), .out(transistor_1_out), .gate(a));
  Transistor transistor_2 (.in(1'b1), .out(transistor_2_out), .gate(c_2));
  Transistor transistor_3 (.in(transistor_2_out), .out(transistor_3_out), .gate(d_2));
  Transistor transistor_4 (.in(transistor_3_out), .out(transistor_4_out), .gate(e_2));
  Transistor #(.\type ("n")) transistor_5 (.in(1'b0), .out(transistor_4_out), .gate(c_2));
  Transistor transistor_6 (.in(1'b1), .out(transistor_6_out), .gate(a));
  Transistor transistor_7 (.in(transistor_6_out), .out(transistor_1_out), .gate(b));
  Transistor #(.\type ("n")) transistor_8 (.in(1'b0), .out(transistor_1_out), .gate(b));
  Transistor #(.\type ("n")) transistor_9 (.in(1'b0), .out(transistor_4_out), .gate(e_2));
  Transistor #(.\type ("n")) transistor_10 (.in(1'b0), .out(transistor_4_out), .gate(d_2));
  Transistor transistor_11 (.in(1'b1), .out(Z_2), .gate(transistor_1_out));
  Transistor #(.\type ("n")) transistor_12 (.in(transistor_13_out), .out(Z_2), .gate(transistor_1_out));
  Transistor #(.\type ("n")) transistor_13 (.in(1'b0), .out(transistor_13_out), .gate(transistor_4_out));
  Transistor transistor_14 (.in(1'b1), .out(Z_2), .gate(transistor_4_out));
  nor nor_1 (nor_1_out, a_2, b_2);
  nor nor_2 (nor_2_out, c, d, e);
  nand nand_1 (Z, nor_1_out, nor_2_out);

  // Notes on the sheet:
  //   ~
  //   OR5
endmodule

module cell36__4NOR (
  input  a,
  input  b,
  input  c,
  input  a_2,
  input  d,
  input  b_2,
  input  c_2,
  input  d_2,
  output Z,
  output Z_2
);

  wire transistor_1_out, transistor_2_out, transistor_3_out;

  Transistor transistor_1 (.in(1'b1), .out(transistor_1_out), .gate(a));
  Transistor transistor_2 (.in(transistor_1_out), .out(transistor_2_out), .gate(b));
  Transistor transistor_3 (.in(transistor_2_out), .out(transistor_3_out), .gate(c));
  Transistor transistor_4 (.in(transistor_3_out), .out(Z), .gate(d));
  Transistor #(.\type ("n")) transistor_5 (.in(1'b0), .out(Z), .gate(a));
  Transistor #(.\type ("n")) transistor_6 (.in(1'b0), .out(Z), .gate(b));
  Transistor #(.\type ("n")) transistor_7 (.in(1'b0), .out(Z), .gate(d));
  Transistor #(.\type ("n")) transistor_8 (.in(1'b0), .out(Z), .gate(c));
  nor nor_1 (Z_2, a_2, b_2, c_2, d_2);

  // Notes on the sheet:
  //   ~
  //   4NOR
endmodule

module cell37__4NAND (
  input  a,
  input  b,
  input  c,
  input  a_2,
  input  d,
  input  b_2,
  input  c_2,
  input  d_2,
  output Z,
  output Z_2
);

  wire transistor_3_out, transistor_4_out, transistor_5_out;

  Transistor transistor_1 (.in(1'b1), .out(Z), .gate(d_2));
  Transistor #(.\type ("n")) transistor_2 (.in(transistor_3_out), .out(Z), .gate(a_2));
  Transistor #(.\type ("n")) transistor_3 (.in(transistor_4_out), .out(transistor_3_out), .gate(b_2));
  Transistor #(.\type ("n")) transistor_4 (.in(transistor_5_out), .out(transistor_4_out), .gate(c_2));
  Transistor #(.\type ("n")) transistor_5 (.in(1'b0), .out(transistor_5_out), .gate(d_2));
  Transistor transistor_6 (.in(1'b1), .out(Z), .gate(b_2));
  Transistor transistor_7 (.in(1'b1), .out(Z), .gate(c_2));
  Transistor transistor_8 (.in(1'b1), .out(Z), .gate(a_2));
  nand nand_1 (Z_2, a, b, c, d);

  // Notes on the sheet:
  //   ~
  //   4NAND
endmodule

module cell38__6OR (
  input  a,
  input  b,
  input  c,
  input  a_2,
  input  b_2,
  input  c_2,
  input  d,
  input  d_2,
  input  e,
  input  e_2,
  input  f,
  input  f_2,
  output Z,
  output Z_2
);

  wire nor_1_out, nor_2_out, transistor_1_out, transistor_2_out, transistor_3_out, transistor_6_out,
       transistor_7_out, transistor_8_out, transistor_16_out;

  Transistor transistor_1 (.in(1'b1), .out(transistor_1_out), .gate(a));
  Transistor transistor_2 (.in(transistor_1_out), .out(transistor_2_out), .gate(b));
  Transistor transistor_3 (.in(transistor_2_out), .out(transistor_3_out), .gate(c));
  Transistor #(.\type ("n")) transistor_4 (.in(1'b0), .out(transistor_3_out), .gate(a));
  Transistor #(.\type ("n")) transistor_5 (.in(1'b0), .out(transistor_3_out), .gate(b));
  Transistor transistor_6 (.in(1'b1), .out(transistor_6_out), .gate(d_2));
  Transistor transistor_7 (.in(transistor_6_out), .out(transistor_7_out), .gate(e_2));
  Transistor transistor_8 (.in(transistor_7_out), .out(transistor_8_out), .gate(f_2));
  Transistor #(.\type ("n")) transistor_9 (.in(1'b0), .out(transistor_8_out), .gate(e_2));
  Transistor #(.\type ("n")) transistor_10 (.in(1'b0), .out(transistor_8_out), .gate(d_2));
  Transistor #(.\type ("n")) transistor_11 (.in(1'b0), .out(transistor_3_out), .gate(c));
  Transistor transistor_12 (.in(1'b1), .out(Z), .gate(transistor_3_out));
  Transistor #(.\type ("n")) transistor_13 (.in(1'b0), .out(transistor_8_out), .gate(f_2));
  Transistor transistor_14 (.in(1'b1), .out(Z), .gate(transistor_8_out));
  Transistor #(.\type ("n")) transistor_15 (.in(transistor_16_out), .out(Z), .gate(transistor_3_out));
  Transistor #(.\type ("n")) transistor_16 (.in(1'b0), .out(transistor_16_out), .gate(transistor_8_out));
  nor nor_1 (nor_1_out, a_2, b_2, c_2);
  nor nor_2 (nor_2_out, d, e, f);
  nand nand_1 (Z_2, nor_1_out, nor_2_out);

  // Notes on the sheet:
  //   ~
endmodule

module cell39_6NOR (
  input  a,
  input  b,
  input  c,
  input  a_2,
  input  b_2,
  input  c_2,
  input  d,
  input  d_2,
  input  e,
  input  e_2,
  input  f,
  input  f_2,
  output Z,
  output Z_2
);

  wire nor_1_out, nor_2_out, transistor_1_out, transistor_2_out, transistor_3_out, transistor_6_out,
       transistor_7_out, transistor_8_out, transistor_12_out, transistor_16_out;

  Transistor transistor_1 (.in(1'b1), .out(transistor_1_out), .gate(a));
  Transistor transistor_2 (.in(transistor_1_out), .out(transistor_2_out), .gate(b));
  Transistor transistor_3 (.in(transistor_2_out), .out(transistor_3_out), .gate(c));
  Transistor #(.\type ("n")) transistor_4 (.in(1'b0), .out(transistor_3_out), .gate(a));
  Transistor #(.\type ("n")) transistor_5 (.in(1'b0), .out(transistor_3_out), .gate(b));
  Transistor transistor_6 (.in(1'b1), .out(transistor_6_out), .gate(d_2));
  Transistor transistor_7 (.in(transistor_6_out), .out(transistor_7_out), .gate(e_2));
  Transistor transistor_8 (.in(transistor_7_out), .out(transistor_8_out), .gate(f_2));
  Transistor #(.\type ("n")) transistor_9 (.in(1'b0), .out(transistor_8_out), .gate(d_2));
  Transistor #(.\type ("n")) transistor_10 (.in(1'b0), .out(transistor_8_out), .gate(e_2));
  Transistor #(.\type ("n")) transistor_11 (.in(1'b0), .out(transistor_3_out), .gate(c));
  Transistor transistor_12 (.in(1'b1), .out(transistor_12_out), .gate(transistor_3_out));
  Transistor #(.\type ("n")) transistor_13 (.in(1'b0), .out(transistor_8_out), .gate(f_2));
  Transistor transistor_14 (.in(1'b1), .out(transistor_12_out), .gate(transistor_8_out));
  Transistor #(.\type ("n")) transistor_15 (.in(transistor_16_out), .out(transistor_12_out), .gate(transistor_3_out));
  Transistor #(.\type ("n")) transistor_16 (.in(1'b0), .out(transistor_16_out), .gate(transistor_8_out));
  Transistor transistor_17 (.in(1'b1), .out(Z), .gate(transistor_12_out));
  Transistor #(.\type ("n")) transistor_18 (.in(1'b0), .out(Z), .gate(transistor_12_out));
  nor nor_1 (nor_1_out, a_2, b_2, c_2);
  nor nor_2 (nor_2_out, d, e, f);
  and and_1 (Z_2, nor_1_out, nor_2_out);

  // Notes on the sheet:
  //   ~
endmodule

module cell40__5AND (
  input  a,
  input  b,
  input  b_2,
  input  c,
  input  d,
  input  e,
  input  f,
  input  c_2,
  input  d_2,
  input  e_2,
  output Z,
  output Z_2
);

  wire nand_1_out, nand_2_out, transistor_1_out, transistor_4_out, transistor_5_out, transistor_8_out,
       transistor_9_out, transistor_11_out;

  Transistor transistor_1 (.in(1'b1), .out(transistor_1_out), .gate(b));
  Transistor transistor_2 (.in(1'b1), .out(transistor_1_out), .gate(a));
  Transistor #(.\type ("n")) transistor_3 (.in(transistor_4_out), .out(transistor_1_out), .gate(a));
  Transistor #(.\type ("n")) transistor_4 (.in(1'b0), .out(transistor_4_out), .gate(b));
  Transistor transistor_5 (.in(1'b1), .out(transistor_5_out), .gate(e_2));
  Transistor transistor_6 (.in(1'b1), .out(transistor_5_out), .gate(d_2));
  Transistor #(.\type ("n")) transistor_7 (.in(transistor_8_out), .out(transistor_5_out), .gate(c_2));
  Transistor #(.\type ("n")) transistor_8 (.in(transistor_9_out), .out(transistor_8_out), .gate(d_2));
  Transistor #(.\type ("n")) transistor_9 (.in(1'b0), .out(transistor_9_out), .gate(e_2));
  Transistor transistor_10 (.in(1'b1), .out(transistor_5_out), .gate(c_2));
  Transistor transistor_11 (.in(1'b1), .out(transistor_11_out), .gate(transistor_5_out));
  Transistor transistor_12 (.in(transistor_11_out), .out(Z), .gate(transistor_1_out));
  Transistor #(.\type ("n")) transistor_13 (.in(1'b0), .out(Z), .gate(transistor_5_out));
  Transistor #(.\type ("n")) transistor_14 (.in(1'b0), .out(Z), .gate(transistor_1_out));
  nand nand_1 (nand_1_out, b_2, c);
  nand nand_2 (nand_2_out, d, e, f);
  nor nor_1 (Z_2, nand_1_out, nand_2_out);

  // Notes on the sheet:
  //   ~
  //   5AND
endmodule

module cell41__4OR (
  input  a,
  input  b,
  input  c,
  input  a_2,
  input  d,
  input  b_2,
  input  c_2,
  input  d_2,
  output Z,
  output Z_2
);

  wire transistor_1_out, transistor_2_out, transistor_3_out, transistor_4_out;

  Transistor transistor_1 (.in(1'b1), .out(transistor_1_out), .gate(a));
  Transistor transistor_2 (.in(transistor_1_out), .out(transistor_2_out), .gate(b));
  Transistor transistor_3 (.in(transistor_2_out), .out(transistor_3_out), .gate(c));
  Transistor transistor_4 (.in(transistor_3_out), .out(transistor_4_out), .gate(d));
  Transistor #(.\type ("n")) transistor_5 (.in(1'b0), .out(transistor_4_out), .gate(a));
  Transistor #(.\type ("n")) transistor_6 (.in(1'b0), .out(transistor_4_out), .gate(b));
  Transistor #(.\type ("n")) transistor_7 (.in(1'b0), .out(transistor_4_out), .gate(c));
  Transistor transistor_8 (.in(1'b1), .out(Z), .gate(transistor_4_out));
  Transistor #(.\type ("n")) transistor_9 (.in(1'b0), .out(transistor_4_out), .gate(d));
  Transistor #(.\type ("n")) transistor_10 (.in(1'b0), .out(Z), .gate(transistor_4_out));
  or or_1 (Z_2, a_2, b_2, c_2, d_2);

  // Notes on the sheet:
  //   ~
  //   4OR
endmodule

module cell42__4AND (
  input  a,
  input  b,
  input  c,
  input  a_2,
  input  d,
  input  b_2,
  input  c_2,
  input  d_2,
  output Z,
  output Z_2
);

  wire transistor_1_out, transistor_4_out, transistor_5_out, transistor_6_out;

  Transistor transistor_1 (.in(1'b1), .out(transistor_1_out), .gate(d_2));
  Transistor transistor_2 (.in(1'b1), .out(transistor_1_out), .gate(c_2));
  Transistor #(.\type ("n")) transistor_3 (.in(transistor_4_out), .out(transistor_1_out), .gate(a_2));
  Transistor #(.\type ("n")) transistor_4 (.in(transistor_5_out), .out(transistor_4_out), .gate(b_2));
  Transistor #(.\type ("n")) transistor_5 (.in(transistor_6_out), .out(transistor_5_out), .gate(c_2));
  Transistor #(.\type ("n")) transistor_6 (.in(1'b0), .out(transistor_6_out), .gate(d_2));
  Transistor transistor_7 (.in(1'b1), .out(transistor_1_out), .gate(b_2));
  Transistor transistor_8 (.in(1'b1), .out(transistor_1_out), .gate(a_2));
  Transistor transistor_9 (.in(1'b1), .out(Z), .gate(transistor_1_out));
  Transistor #(.\type ("n")) transistor_10 (.in(1'b0), .out(Z), .gate(transistor_1_out));
  and and_1 (Z_2, a, b, c, d);

  // Notes on the sheet:
  //   ~
  //   4AND
endmodule

module cell43__AOI22 (
  input  a1,
  input  a2,
  input  a1_2,
  input  b1,
  input  a2_2,
  input  b1_2,
  input  b2,
  input  b2_2,
  output Z,
  output Z_2
);

  wire and_1_out, and_2_out, transistor_1_out, transistor_4_out, transistor_8_out;

  Transistor transistor_1 (.in(1'b1), .out(transistor_1_out), .gate(a2));
  Transistor transistor_2 (.in(transistor_1_out), .out(Z), .gate(b1));
  Transistor #(.\type ("n")) transistor_3 (.in(transistor_4_out), .out(Z), .gate(a1));
  Transistor #(.\type ("n")) transistor_4 (.in(1'b0), .out(transistor_4_out), .gate(a2));
  Transistor transistor_5 (.in(1'b1), .out(transistor_1_out), .gate(a1));
  Transistor transistor_6 (.in(transistor_1_out), .out(Z), .gate(b2_2));
  Transistor #(.\type ("n")) transistor_7 (.in(transistor_8_out), .out(Z), .gate(b1));
  Transistor #(.\type ("n")) transistor_8 (.in(1'b0), .out(transistor_8_out), .gate(b2_2));
  and and_1 (and_1_out, a1_2, a2_2);
  and and_2 (and_2_out, b1_2, b2);
  nor nor_1 (Z_2, and_1_out, and_2_out);

  // Notes on the sheet:
  //   ~
  //   AOI22
endmodule

module cell44__AOI2222 (
  input  a1,
  input  a1_2,
  input  a2,
  input  a2_2,
  input  b1,
  input  b1_2,
  input  b2,
  input  b2_2,
  input  c1,
  input  c1_2,
  input  c2,
  input  c2_2,
  input  d1,
  input  d1_2,
  input  d2,
  input  d2_2,
  output a,
  output a_2
);

  wire and_1_out, and_2_out, and_3_out, and_4_out, transistor_2_out, transistor_3_out, transistor_5_out,
       transistor_7_out, transistor_13_out, transistor_14_out, transistor_16_out;

  Transistor #(.\type ("n")) transistor_1 (.in(transistor_2_out), .out(a), .gate(a2));
  Transistor #(.\type ("n")) transistor_2 (.in(1'b0), .out(transistor_2_out), .gate(a1));
  Transistor transistor_3 (.in(1'b1), .out(transistor_3_out), .gate(d2));
  Transistor transistor_4 (.in(1'b1), .out(transistor_3_out), .gate(d1));
  Transistor transistor_5 (.in(transistor_3_out), .out(transistor_5_out), .gate(c2));
  Transistor transistor_6 (.in(transistor_3_out), .out(transistor_5_out), .gate(c1));
  Transistor transistor_7 (.in(transistor_5_out), .out(transistor_7_out), .gate(b1));
  Transistor transistor_8 (.in(transistor_5_out), .out(transistor_7_out), .gate(b2));
  Transistor transistor_9 (.in(transistor_7_out), .out(a), .gate(a2));
  Transistor transistor_10 (.in(transistor_7_out), .out(a), .gate(a1));
  Transistor #(.\type ("n")) transistor_11 (.in(transistor_14_out), .out(a), .gate(c2));
  Transistor #(.\type ("n")) transistor_12 (.in(transistor_13_out), .out(a), .gate(b1));
  Transistor #(.\type ("n")) transistor_13 (.in(1'b0), .out(transistor_13_out), .gate(b2));
  Transistor #(.\type ("n")) transistor_14 (.in(1'b0), .out(transistor_14_out), .gate(c1));
  Transistor #(.\type ("n")) transistor_15 (.in(transistor_16_out), .out(a), .gate(d1));
  Transistor #(.\type ("n")) transistor_16 (.in(1'b0), .out(transistor_16_out), .gate(d2));
  and and_1 (and_1_out, a1_2, a2_2);
  and and_2 (and_2_out, b1_2, b2_2);
  and and_3 (and_3_out, c1_2, c2_2);
  and and_4 (and_4_out, d1_2, d2_2);
  nor nor_1 (a_2, and_1_out, and_2_out, and_3_out, and_4_out);

  // Notes on the sheet:
  //   ~
  //   AOI2222
endmodule

module cell45 (
  input  nC,
  input  a,
  input  C,
  output Q
);

  wire transistor_1_out, transistor_3_out, transistor_5_out;

  Transistor transistor_1 (.in(1'b1), .out(transistor_1_out), .gate(a));
  Transistor #(.\type ("n")) transistor_2 (.in(1'b0), .out(transistor_1_out), .gate(a));
  Transistor transistor_3 (.in(a), .out(transistor_3_out), .gate(nC));
  Transistor #(.\type ("n")) transistor_4 (.in(a), .out(transistor_3_out), .gate(C));
  Transistor transistor_5 (.in(1'b1), .out(transistor_5_out), .gate(transistor_3_out));
  Transistor transistor_6 (.in(transistor_5_out), .out(Q), .gate(transistor_1_out));
  Transistor #(.\type ("n")) transistor_7 (.in(1'b0), .out(Q), .gate(transistor_1_out));
  Transistor #(.\type ("n")) transistor_8 (.in(1'b0), .out(Q), .gate(transistor_3_out));
endmodule

module cell46_7AND (
  input  a,
  input  b,
  input  a_2,
  input  c,
  input  b_2,
  input  d,
  input  c_2,
  input  e,
  input  f,
  input  g,
  input  d_2,
  input  e_2,
  input  f_2,
  input  g_2,
  output Z,
  output Z_2
);

  wire nand_1_out, nand_2_out, transistor_1_out, transistor_3_out, transistor_4_out, transistor_5_out,
       transistor_7_out, transistor_8_out, transistor_9_out, transistor_15_out;

  Transistor transistor_1 (.in(1'b1), .out(transistor_1_out), .gate(c_2));
  Transistor #(.\type ("n")) transistor_2 (.in(transistor_3_out), .out(transistor_1_out), .gate(a_2));
  Transistor #(.\type ("n")) transistor_3 (.in(transistor_4_out), .out(transistor_3_out), .gate(b_2));
  Transistor #(.\type ("n")) transistor_4 (.in(1'b0), .out(transistor_4_out), .gate(c_2));
  Transistor transistor_5 (.in(1'b1), .out(transistor_5_out), .gate(g_2));
  Transistor #(.\type ("n")) transistor_6 (.in(transistor_7_out), .out(transistor_5_out), .gate(d_2));
  Transistor #(.\type ("n")) transistor_7 (.in(transistor_8_out), .out(transistor_7_out), .gate(e_2));
  Transistor #(.\type ("n")) transistor_8 (.in(transistor_9_out), .out(transistor_8_out), .gate(f_2));
  Transistor #(.\type ("n")) transistor_9 (.in(1'b0), .out(transistor_9_out), .gate(g_2));
  Transistor transistor_10 (.in(1'b1), .out(transistor_1_out), .gate(a_2));
  Transistor transistor_11 (.in(1'b1), .out(transistor_1_out), .gate(b_2));
  Transistor transistor_12 (.in(1'b1), .out(transistor_5_out), .gate(f_2));
  Transistor transistor_13 (.in(1'b1), .out(transistor_5_out), .gate(e_2));
  Transistor transistor_14 (.in(1'b1), .out(transistor_5_out), .gate(d_2));
  Transistor transistor_15 (.in(1'b1), .out(transistor_15_out), .gate(transistor_5_out));
  Transistor transistor_16 (.in(transistor_15_out), .out(Z), .gate(transistor_1_out));
  Transistor #(.\type ("n")) transistor_17 (.in(1'b0), .out(Z), .gate(transistor_5_out));
  Transistor #(.\type ("n")) transistor_18 (.in(1'b0), .out(Z), .gate(transistor_1_out));
  nand nand_1 (nand_1_out, a, b, c);
  nand nand_2 (nand_2_out, d, e, f, g);
  nor nor_1 (Z_2, nand_1_out, nand_2_out);

  // Notes on the sheet:
  //   ~
endmodule

module cell47__6AND (
  input  a,
  input  a_2,
  input  b,
  input  b_2,
  input  c,
  input  c_2,
  input  d,
  input  e,
  input  f,
  input  d_2,
  input  e_2,
  input  f_2,
  output Z,
  output Z_2
);

  wire nand_1_out, nand_2_out, transistor_1_out, transistor_4_out, transistor_5_out, transistor_6_out,
       transistor_9_out, transistor_10_out, transistor_13_out;

  Transistor transistor_1 (.in(1'b1), .out(transistor_1_out), .gate(c_2));
  Transistor transistor_2 (.in(1'b1), .out(transistor_1_out), .gate(b_2));
  Transistor #(.\type ("n")) transistor_3 (.in(transistor_4_out), .out(transistor_1_out), .gate(a_2));
  Transistor #(.\type ("n")) transistor_4 (.in(transistor_5_out), .out(transistor_4_out), .gate(b_2));
  Transistor #(.\type ("n")) transistor_5 (.in(1'b0), .out(transistor_5_out), .gate(c_2));
  Transistor transistor_6 (.in(1'b1), .out(transistor_6_out), .gate(e_2));
  Transistor transistor_7 (.in(1'b1), .out(transistor_6_out), .gate(f_2));
  Transistor #(.\type ("n")) transistor_8 (.in(transistor_9_out), .out(transistor_6_out), .gate(d_2));
  Transistor #(.\type ("n")) transistor_9 (.in(transistor_10_out), .out(transistor_9_out), .gate(e_2));
  Transistor #(.\type ("n")) transistor_10 (.in(1'b0), .out(transistor_10_out), .gate(f_2));
  Transistor transistor_11 (.in(1'b1), .out(transistor_1_out), .gate(a_2));
  Transistor transistor_12 (.in(1'b1), .out(transistor_6_out), .gate(d_2));
  Transistor transistor_13 (.in(1'b1), .out(transistor_13_out), .gate(transistor_6_out));
  Transistor transistor_14 (.in(transistor_13_out), .out(Z), .gate(transistor_1_out));
  Transistor #(.\type ("n")) transistor_15 (.in(1'b0), .out(Z), .gate(transistor_1_out));
  Transistor #(.\type ("n")) transistor_16 (.in(1'b0), .out(Z), .gate(transistor_6_out));
  nand nand_1 (nand_1_out, a, c);
  nand nand_2 (nand_2_out, d, f);
  nor nor_1 (Z_2, nand_1_out, nand_2_out);

  // Notes on the sheet:
  //   ~
  //   6AND
endmodule

module cell48__5NOR (
  input  a,
  input  b,
  input  c,
  input  a_2,
  input  b_2,
  input  c_2,
  input  d,
  input  d_2,
  input  e,
  input  e_2,
  output Z,
  output Z_2
);

  wire nor_1_out, nor_2_out, transistor_1_out, transistor_2_out, transistor_3_out, transistor_6_out,
       transistor_7_out, transistor_11_out, transistor_13_out;

  Transistor transistor_1 (.in(1'b1), .out(transistor_1_out), .gate(a));
  Transistor transistor_2 (.in(transistor_1_out), .out(transistor_2_out), .gate(b));
  Transistor transistor_3 (.in(transistor_2_out), .out(transistor_3_out), .gate(c));
  Transistor #(.\type ("n")) transistor_4 (.in(1'b0), .out(transistor_3_out), .gate(a));
  Transistor #(.\type ("n")) transistor_5 (.in(1'b0), .out(transistor_3_out), .gate(b));
  Transistor transistor_6 (.in(1'b1), .out(transistor_6_out), .gate(d_2));
  Transistor transistor_7 (.in(transistor_6_out), .out(transistor_7_out), .gate(e));
  Transistor #(.\type ("n")) transistor_8 (.in(1'b0), .out(transistor_7_out), .gate(e));
  Transistor #(.\type ("n")) transistor_9 (.in(1'b0), .out(transistor_7_out), .gate(d_2));
  Transistor #(.\type ("n")) transistor_10 (.in(1'b0), .out(transistor_3_out), .gate(c));
  Transistor transistor_11 (.in(1'b1), .out(transistor_11_out), .gate(transistor_3_out));
  Transistor #(.\type ("n")) transistor_12 (.in(transistor_13_out), .out(transistor_11_out), .gate(transistor_7_out));
  Transistor #(.\type ("n")) transistor_13 (.in(1'b0), .out(transistor_13_out), .gate(transistor_3_out));
  Transistor transistor_14 (.in(1'b1), .out(transistor_11_out), .gate(transistor_7_out));
  Transistor transistor_15 (.in(1'b1), .out(Z), .gate(transistor_11_out));
  Transistor #(.\type ("n")) transistor_16 (.in(1'b0), .out(Z), .gate(transistor_11_out));
  nor nor_1 (nor_1_out, a_2, b_2, c_2);
  nor nor_2 (nor_2_out, d, e_2);
  and and_1 (Z_2, nor_1_out, nor_2_out);

  // Notes on the sheet:
  //   ~
  //   5NOR
endmodule

module cell49_TRI (
  input  a,
  input  a_2,
  input  e,
  input  e_2,
  output Z,
  output a_3
);

  wire transistor_1_out, transistor_3_out, transistor_4_out, transistor_7_out, transistor_8_out;

  Transistor transistor_1 (.in(1'b1), .out(transistor_1_out), .gate(e_2));
  Transistor #(.\type ("n")) transistor_2 (.in(transistor_3_out), .out(transistor_1_out), .gate(e_2));
  Transistor #(.\type ("n")) transistor_3 (.in(1'b0), .out(transistor_3_out), .gate(a));
  Transistor transistor_4 (.in(1'b1), .out(transistor_4_out), .gate(e_2));
  Transistor #(.\type ("n")) transistor_5 (.in(1'b0), .out(transistor_4_out), .gate(e_2));
  Transistor transistor_6 (.in(1'b1), .out(transistor_1_out), .gate(a));
  Transistor transistor_7 (.in(1'b1), .out(transistor_7_out), .gate(a));
  Transistor transistor_8 (.in(transistor_7_out), .out(transistor_8_out), .gate(transistor_4_out));
  Transistor #(.\type ("n")) transistor_9 (.in(1'b0), .out(transistor_8_out), .gate(a));
  Transistor #(.\type ("n")) transistor_10 (.in(1'b0), .out(transistor_8_out), .gate(transistor_4_out));
  Transistor transistor_11 (.in(1'b1), .out(a_3), .gate(transistor_1_out));
  Transistor transistor_12 (.in(1'b1), .out(a_3), .gate(transistor_1_out));
  Transistor #(.\type ("n")) transistor_13 (.in(1'b0), .out(a_3), .gate(transistor_8_out));
  Transistor #(.\type ("n")) transistor_14 (.in(1'b0), .out(a_3), .gate(transistor_8_out));
  assign Z = e ? a_2 : 1'bz;  // Controlled_Buffer controlled_buffer_1

  // Notes on the sheet:
  //   ~
endmodule

module cell50__N_tran (
  input  a
);

  wire transistor_1_out, undriven;

  Transistor #(.\type ("n")) transistor_1 (.in(undriven), .out(transistor_1_out), .gate(a));
  // also tied to GND on the sheet: transistor_1_out
endmodule

module cell51 (
  input  b,
  input  c,
  input  d,
  input  e,
  input  f,
  output Z
);

  wire transistor_1_out, transistor_3_out, transistor_5_out, transistor_6_out, transistor_8_out,
       transistor_10_out;

  Transistor transistor_1 (.in(1'b1), .out(transistor_1_out), .gate(b));
  Transistor transistor_2 (.in(1'b1), .out(transistor_1_out), .gate(c));
  Transistor transistor_3 (.in(transistor_1_out), .out(transistor_3_out), .gate(e));
  Transistor #(.\type ("n")) transistor_4 (.in(transistor_5_out), .out(transistor_3_out), .gate(d));
  Transistor #(.\type ("n")) transistor_5 (.in(transistor_6_out), .out(transistor_5_out), .gate(c));
  Transistor #(.\type ("n")) transistor_6 (.in(1'b0), .out(transistor_6_out), .gate(b));
  Transistor transistor_7 (.in(1'b1), .out(transistor_1_out), .gate(d));
  Transistor transistor_8 (.in(transistor_1_out), .out(transistor_8_out), .gate(f));
  Transistor #(.\type ("n")) transistor_9 (.in(transistor_10_out), .out(transistor_8_out), .gate(e));
  Transistor #(.\type ("n")) transistor_10 (.in(1'b0), .out(transistor_10_out), .gate(f));
  Transistor transistor_11 (.in(1'b1), .out(Z), .gate(transistor_3_out));
  Transistor #(.\type ("n")) transistor_12 (.in(1'b0), .out(Z), .gate(transistor_3_out));
endmodule

module cell72_POS_EDGE_DFF (
  input  C,
  input  D,
  input  R,
  output Q
);

  wire transistor_1_out, transistor_3_out, transistor_5_out, transistor_7_out, transistor_9_out,
       transistor_10_out, transistor_11_out, transistor_15_out, transistor_16_out, transistor_17_out,
       transistor_19_out, transistor_21_out, transistor_23_out, transistor_24_out, transistor_26_out,
       transistor_27_out, transistor_30_out, transistor_31_out, transistor_33_out;

  Transistor transistor_1 (.in(1'b1), .out(transistor_1_out), .gate(C));
  Transistor #(.\type ("n")) transistor_2 (.in(1'b0), .out(transistor_1_out), .gate(C));
  Transistor transistor_3 (.in(1'b1), .out(transistor_3_out), .gate(C));
  Transistor #(.\type ("n")) transistor_4 (.in(1'b0), .out(transistor_3_out), .gate(C));
  Transistor transistor_5 (.in(1'b1), .out(transistor_5_out), .gate(transistor_3_out));
  Transistor #(.\type ("n")) transistor_6 (.in(1'b0), .out(transistor_5_out), .gate(transistor_3_out));
  Transistor transistor_7 (.in(1'b1), .out(transistor_7_out), .gate(D));
  Transistor #(.\type ("n")) transistor_8 (.in(1'b0), .out(transistor_7_out), .gate(D));
  Transistor transistor_9 (.in(1'b1), .out(transistor_9_out), .gate(transistor_7_out));
  Transistor transistor_10 (.in(1'b1), .out(transistor_10_out), .gate(transistor_19_out));
  Transistor transistor_11 (.in(transistor_10_out), .out(transistor_11_out), .gate(transistor_1_out));
  Transistor transistor_12 (.in(transistor_9_out), .out(transistor_11_out), .gate(transistor_5_out));
  Transistor #(.\type ("n")) transistor_13 (.in(transistor_15_out), .out(transistor_11_out), .gate(transistor_5_out));
  Transistor #(.\type ("n")) transistor_14 (.in(transistor_16_out), .out(transistor_11_out), .gate(transistor_7_out));
  Transistor #(.\type ("n")) transistor_15 (.in(1'b0), .out(transistor_15_out), .gate(transistor_19_out));
  Transistor #(.\type ("n")) transistor_16 (.in(1'b0), .out(transistor_16_out), .gate(transistor_1_out));
  Transistor transistor_17 (.in(1'b1), .out(transistor_17_out), .gate(R));
  Transistor #(.\type ("n")) transistor_18 (.in(1'b0), .out(transistor_17_out), .gate(R));
  Transistor transistor_19 (.in(1'b1), .out(transistor_19_out), .gate(transistor_11_out));
  Transistor #(.\type ("n")) transistor_20 (.in(transistor_21_out), .out(transistor_19_out), .gate(transistor_11_out));
  Transistor #(.\type ("n")) transistor_21 (.in(1'b0), .out(transistor_21_out), .gate(transistor_17_out));
  Transistor transistor_22 (.in(1'b1), .out(transistor_19_out), .gate(transistor_17_out));
  Transistor transistor_23 (.in(1'b1), .out(transistor_23_out), .gate(transistor_19_out));
  Transistor transistor_24 (.in(transistor_23_out), .out(transistor_24_out), .gate(transistor_1_out));
  Transistor #(.\type ("n")) transistor_25 (.in(transistor_26_out), .out(transistor_24_out), .gate(transistor_5_out));
  Transistor #(.\type ("n")) transistor_26 (.in(1'b0), .out(transistor_26_out), .gate(transistor_19_out));
  Transistor transistor_27 (.in(1'b1), .out(transistor_27_out), .gate(transistor_31_out));
  Transistor transistor_28 (.in(transistor_27_out), .out(transistor_24_out), .gate(transistor_5_out));
  Transistor #(.\type ("n")) transistor_29 (.in(transistor_30_out), .out(transistor_24_out), .gate(transistor_1_out));
  Transistor #(.\type ("n")) transistor_30 (.in(1'b0), .out(transistor_30_out), .gate(transistor_31_out));
  Transistor transistor_31 (.in(1'b1), .out(transistor_31_out), .gate(transistor_24_out));
  Transistor #(.\type ("n")) transistor_32 (.in(transistor_33_out), .out(transistor_31_out), .gate(transistor_24_out));
  Transistor #(.\type ("n")) transistor_33 (.in(1'b0), .out(transistor_33_out), .gate(transistor_17_out));
  Transistor transistor_34 (.in(1'b1), .out(transistor_31_out), .gate(transistor_17_out));
  Transistor transistor_35 (.in(1'b1), .out(Q), .gate(transistor_31_out));
  Transistor #(.\type ("n")) transistor_36 (.in(1'b0), .out(Q), .gate(transistor_31_out));
endmodule

module cell52_CNT__BIT_LOAD (
  input  nL,
  input  D,
  input  nc1,
  input  nc2,
  input  L,
  input  CI,
  input  R,
  input  c1,
  input  c2,
  output CO,
  output Q
);

  wire transistor_1_out, transistor_3_out, transistor_7_out, transistor_8_out, transistor_9_out,
       transistor_12_out, transistor_13_out, transistor_16_out, transistor_17_out, transistor_19_out,
       transistor_20_out, transistor_22_out, transistor_25_out, transistor_26_out, transistor_28_out,
       transistor_29_out, transistor_30_out, transistor_32_out;

  Transistor transistor_1 (.in(1'b1), .out(transistor_1_out), .gate(CI));
  Transistor #(.\type ("n")) transistor_2 (.in(1'b0), .out(transistor_1_out), .gate(CI));
  Transistor transistor_3 (.in(1'b1), .out(transistor_3_out), .gate(transistor_26_out));
  Transistor transistor_4 (.in(transistor_3_out), .out(CO), .gate(transistor_1_out));
  Transistor #(.\type ("n")) transistor_5 (.in(1'b0), .out(CO), .gate(transistor_1_out));
  Transistor #(.\type ("n")) transistor_6 (.in(1'b0), .out(CO), .gate(transistor_26_out));
  Transistor transistor_7 (.in(1'b1), .out(transistor_7_out), .gate(transistor_1_out));
  Transistor transistor_8 (.in(transistor_7_out), .out(transistor_8_out), .gate(CO));
  Transistor transistor_9 (.in(transistor_8_out), .out(transistor_9_out), .gate(R));
  Transistor #(.\type ("n")) transistor_10 (.in(1'b0), .out(transistor_9_out), .gate(R));
  Transistor #(.\type ("n")) transistor_11 (.in(1'b0), .out(transistor_9_out), .gate(CO));
  Transistor transistor_12 (.in(1'b1), .out(transistor_12_out), .gate(CO));
  Transistor transistor_13 (.in(transistor_12_out), .out(transistor_13_out), .gate(transistor_26_out));
  Transistor transistor_14 (.in(transistor_13_out), .out(transistor_9_out), .gate(R));
  Transistor #(.\type ("n")) transistor_15 (.in(transistor_16_out), .out(transistor_9_out), .gate(transistor_26_out));
  Transistor #(.\type ("n")) transistor_16 (.in(1'b0), .out(transistor_16_out), .gate(transistor_1_out));
  Transistor transistor_17 (.in(transistor_9_out), .out(transistor_17_out), .gate(nc1));
  Transistor #(.\type ("n")) transistor_18 (.in(transistor_9_out), .out(transistor_17_out), .gate(c1));
  Transistor transistor_19 (.in(1'b1), .out(transistor_19_out), .gate(transistor_17_out));
  Transistor transistor_20 (.in(transistor_19_out), .out(transistor_20_out), .gate(nc2));
  Transistor #(.\type ("n")) transistor_21 (.in(transistor_22_out), .out(transistor_20_out), .gate(c2));
  Transistor #(.\type ("n")) transistor_22 (.in(1'b0), .out(transistor_22_out), .gate(transistor_17_out));
  Transistor transistor_23 (.in(1'b1), .out(Q), .gate(transistor_20_out));
  Transistor #(.\type ("n")) transistor_24 (.in(1'b0), .out(Q), .gate(transistor_20_out));
  Transistor transistor_25 (.in(1'b1), .out(transistor_25_out), .gate(Q));
  Transistor transistor_26 (.in(transistor_25_out), .out(transistor_26_out), .gate(L));
  Transistor #(.\type ("n"), .gate("br")) transistor_27 (.in(transistor_28_out), .out(transistor_26_out), .gate(nL));
  Transistor #(.\type ("n")) transistor_28 (.in(1'b0), .out(transistor_28_out), .gate(Q));
  Transistor transistor_29 (.in(1'b1), .out(transistor_29_out), .gate(D));
  Transistor transistor_30 (.in(transistor_29_out), .out(transistor_30_out), .gate(nL));
  Transistor #(.\type ("n")) transistor_31 (.in(transistor_32_out), .out(transistor_30_out), .gate(L));
  Transistor #(.\type ("n")) transistor_32 (.in(1'b0), .out(transistor_32_out), .gate(D));
endmodule

module cell53__AON222 (
  input  C1,
  input  C2,
  input  C1_2,
  input  C2_2,
  input  B1,
  input  B2,
  input  A1,
  input  A2,
  input  B1_2,
  input  B2_2,
  input  A1_2,
  input  A2_2,
  output Z,
  output Z_2
);

  wire and_1_out, and_2_out, and_3_out, transistor_1_out, transistor_2_out, transistor_3_out,
       transistor_4_out, transistor_7_out, transistor_14_out;

  Transistor #(.\type ("n")) transistor_1 (.in(transistor_2_out), .out(transistor_1_out), .gate(C1));
  Transistor #(.\type ("n")) transistor_2 (.in(1'b0), .out(transistor_2_out), .gate(C2));
  Transistor transistor_3 (.in(1'b1), .out(transistor_3_out), .gate(C2));
  Transistor transistor_4 (.in(transistor_3_out), .out(transistor_4_out), .gate(B2_2));
  Transistor transistor_5 (.in(transistor_4_out), .out(transistor_1_out), .gate(A1_2));
  Transistor #(.\type ("n")) transistor_6 (.in(transistor_7_out), .out(transistor_1_out), .gate(B1_2));
  Transistor #(.\type ("n")) transistor_7 (.in(1'b0), .out(transistor_7_out), .gate(B2_2));
  Transistor transistor_8 (.in(1'b1), .out(transistor_3_out), .gate(C1));
  Transistor transistor_9 (.in(transistor_3_out), .out(transistor_4_out), .gate(B1_2));
  Transistor transistor_10 (.in(transistor_4_out), .out(transistor_1_out), .gate(A2_2));
  Transistor transistor_11 (.in(1'b1), .out(Z), .gate(transistor_1_out));
  Transistor #(.\type ("n")) transistor_12 (.in(transistor_14_out), .out(transistor_1_out), .gate(A1_2));
  Transistor #(.\type ("n")) transistor_13 (.in(1'b0), .out(Z), .gate(transistor_1_out));
  Transistor #(.\type ("n")) transistor_14 (.in(1'b0), .out(transistor_14_out), .gate(A2_2));
  and and_1 (and_1_out, C1_2, C2_2);
  and and_2 (and_2_out, B1, B2);
  and and_3 (and_3_out, A1, A2);
  or or_1 (Z_2, and_1_out, and_2_out, and_3_out);

  // Notes on the sheet:
  //   ~
  //   AON222
endmodule

module cell54__AOI222222 (
  input  a1,
  input  a1_2,
  input  a2,
  input  a2_2,
  input  b1,
  input  b1_2,
  input  b2,
  input  b2_2,
  input  c1,
  input  c1_2,
  input  c2,
  input  c2_2,
  input  d1,
  input  d2,
  input  e1,
  input  e2,
  input  f1,
  input  f2,
  input  d1_2,
  input  d2_2,
  input  e1_2,
  input  e2_2,
  input  f1_2,
  input  f2_2,
  output Z,
  output Z_2
);

  wire and_1_out, and_2_out, and_3_out, and_4_out, and_5_out, and_6_out, nor_1_out, nor_2_out,
       transistor_1_out, transistor_2_out, transistor_3_out, transistor_5_out, transistor_6_out,
       transistor_7_out, transistor_8_out, transistor_10_out, transistor_16_out, transistor_17_out,
       transistor_23_out, transistor_24_out, transistor_25_out, transistor_28_out;

  Transistor transistor_1 (.in(1'b1), .out(transistor_1_out), .gate(c1_2));
  Transistor transistor_2 (.in(transistor_1_out), .out(transistor_2_out), .gate(b2_2));
  Transistor transistor_3 (.in(transistor_2_out), .out(transistor_3_out), .gate(a2_2));
  Transistor #(.\type ("n")) transistor_4 (.in(transistor_5_out), .out(transistor_3_out), .gate(c2_2));
  Transistor #(.\type ("n")) transistor_5 (.in(1'b0), .out(transistor_5_out), .gate(c1_2));
  Transistor transistor_6 (.in(1'b1), .out(transistor_6_out), .gate(d2_2));
  Transistor transistor_7 (.in(transistor_6_out), .out(transistor_7_out), .gate(e1_2));
  Transistor transistor_8 (.in(transistor_7_out), .out(transistor_8_out), .gate(f1_2));
  Transistor #(.\type ("n")) transistor_9 (.in(transistor_10_out), .out(transistor_8_out), .gate(d1_2));
  Transistor #(.\type ("n")) transistor_10 (.in(1'b0), .out(transistor_10_out), .gate(d2_2));
  Transistor transistor_11 (.in(1'b1), .out(transistor_1_out), .gate(c2_2));
  Transistor transistor_12 (.in(transistor_1_out), .out(transistor_2_out), .gate(b1_2));
  Transistor transistor_13 (.in(transistor_2_out), .out(transistor_3_out), .gate(a1_2));
  Transistor #(.\type ("n")) transistor_14 (.in(transistor_17_out), .out(transistor_3_out), .gate(a2_2));
  Transistor #(.\type ("n")) transistor_15 (.in(transistor_16_out), .out(transistor_3_out), .gate(b1_2));
  Transistor #(.\type ("n")) transistor_16 (.in(1'b0), .out(transistor_16_out), .gate(b2_2));
  Transistor #(.\type ("n")) transistor_17 (.in(1'b0), .out(transistor_17_out), .gate(a1_2));
  Transistor transistor_18 (.in(1'b1), .out(transistor_6_out), .gate(d1_2));
  Transistor transistor_19 (.in(transistor_6_out), .out(transistor_7_out), .gate(e2_2));
  Transistor transistor_20 (.in(transistor_7_out), .out(transistor_8_out), .gate(f2_2));
  Transistor #(.\type ("n")) transistor_21 (.in(transistor_23_out), .out(transistor_8_out), .gate(f1_2));
  Transistor #(.\type ("n")) transistor_22 (.in(transistor_24_out), .out(transistor_8_out), .gate(e2_2));
  Transistor #(.\type ("n")) transistor_23 (.in(1'b0), .out(transistor_23_out), .gate(f2_2));
  Transistor #(.\type ("n")) transistor_24 (.in(1'b0), .out(transistor_24_out), .gate(e1_2));
  Transistor transistor_25 (.in(1'b1), .out(transistor_25_out), .gate(transistor_8_out));
  Transistor transistor_26 (.in(1'b1), .out(transistor_25_out), .gate(transistor_3_out));
  Transistor #(.\type ("n")) transistor_27 (.in(transistor_28_out), .out(transistor_25_out), .gate(transistor_3_out));
  Transistor #(.\type ("n")) transistor_28 (.in(1'b0), .out(transistor_28_out), .gate(transistor_8_out));
  Transistor transistor_29 (.in(1'b1), .out(Z_2), .gate(transistor_25_out));
  Transistor #(.\type ("n")) transistor_30 (.in(1'b0), .out(Z_2), .gate(transistor_25_out));
  and and_1 (and_1_out, a1, a2);
  and and_2 (and_2_out, b1, b2);
  and and_3 (and_3_out, c1, c2);
  and and_4 (and_4_out, d1, d2);
  and and_5 (and_5_out, e1, e2);
  and and_6 (and_6_out, f1, f2);
  nor nor_1 (nor_1_out, and_1_out, and_2_out, and_3_out);
  nor nor_2 (nor_2_out, and_4_out, and_5_out, and_6_out);
  and and_7 (Z, nor_1_out, nor_2_out);

  // Notes on the sheet:
  //   ~
  //   AOI222222
endmodule

module cell55__AON22222222 (
  input  a1,
  input  a1_2,
  input  e1,
  input  a2,
  input  a2_2,
  input  e2,
  input  b1,
  input  b1_2,
  input  f1,
  input  b2,
  input  b2_2,
  input  f2,
  input  c1,
  input  c1_2,
  input  g1,
  input  c2,
  input  c2_2,
  input  g2,
  input  d1,
  input  d1_2,
  input  h1,
  input  d2,
  input  d2_2,
  input  h2,
  input  e1_2,
  input  e2_2,
  input  f1_2,
  input  f2_2,
  input  g1_2,
  input  g2_2,
  input  h1_2,
  input  h2_2,
  output Z,
  output Z_2
);

  wire and_1_out, and_2_out, and_3_out, and_4_out, and_5_out, and_6_out, and_7_out, and_8_out, nor_1_out,
       nor_2_out, transistor_1_out, transistor_2_out, transistor_3_out, transistor_5_out, transistor_7_out,
       transistor_13_out, transistor_14_out, transistor_16_out, transistor_17_out, transistor_18_out,
       transistor_19_out, transistor_20_out, transistor_21_out, transistor_24_out, transistor_30_out,
       transistor_32_out, transistor_35_out;

  Transistor #(.\type ("n")) transistor_1 (.in(transistor_2_out), .out(transistor_1_out), .gate(a2_2));
  Transistor #(.\type ("n")) transistor_2 (.in(1'b0), .out(transistor_2_out), .gate(a1_2));
  Transistor transistor_3 (.in(1'b1), .out(transistor_3_out), .gate(d2_2));
  Transistor transistor_4 (.in(1'b1), .out(transistor_3_out), .gate(d1_2));
  Transistor transistor_5 (.in(transistor_3_out), .out(transistor_5_out), .gate(c2_2));
  Transistor transistor_6 (.in(transistor_3_out), .out(transistor_5_out), .gate(c1_2));
  Transistor transistor_7 (.in(transistor_5_out), .out(transistor_7_out), .gate(b1_2));
  Transistor transistor_8 (.in(transistor_5_out), .out(transistor_7_out), .gate(b2_2));
  Transistor transistor_9 (.in(transistor_7_out), .out(transistor_1_out), .gate(a1_2));
  Transistor transistor_10 (.in(transistor_7_out), .out(transistor_1_out), .gate(a2_2));
  Transistor #(.\type ("n")) transistor_11 (.in(transistor_14_out), .out(transistor_1_out), .gate(c2_2));
  Transistor #(.\type ("n")) transistor_12 (.in(transistor_13_out), .out(transistor_1_out), .gate(b1_2));
  Transistor #(.\type ("n")) transistor_13 (.in(1'b0), .out(transistor_13_out), .gate(b2_2));
  Transistor #(.\type ("n")) transistor_14 (.in(1'b0), .out(transistor_14_out), .gate(c1_2));
  Transistor #(.\type ("n")) transistor_15 (.in(transistor_16_out), .out(transistor_1_out), .gate(d1_2));
  Transistor #(.\type ("n")) transistor_16 (.in(1'b0), .out(transistor_16_out), .gate(d2_2));
  Transistor #(.\type ("n")) transistor_17 (.in(transistor_18_out), .out(transistor_17_out), .gate(e2));
  Transistor #(.\type ("n")) transistor_18 (.in(1'b0), .out(transistor_18_out), .gate(e1));
  Transistor transistor_19 (.in(1'b1), .out(transistor_19_out), .gate(h1));
  Transistor transistor_20 (.in(transistor_19_out), .out(transistor_20_out), .gate(g1));
  Transistor transistor_21 (.in(transistor_20_out), .out(transistor_21_out), .gate(f1));
  Transistor transistor_22 (.in(transistor_21_out), .out(transistor_17_out), .gate(e1));
  Transistor #(.\type ("n")) transistor_23 (.in(transistor_24_out), .out(transistor_17_out), .gate(f1));
  Transistor #(.\type ("n")) transistor_24 (.in(1'b0), .out(transistor_24_out), .gate(f2));
  Transistor transistor_25 (.in(1'b1), .out(transistor_19_out), .gate(h2));
  Transistor transistor_26 (.in(transistor_19_out), .out(transistor_20_out), .gate(g2));
  Transistor transistor_27 (.in(transistor_20_out), .out(transistor_21_out), .gate(f2));
  Transistor transistor_28 (.in(transistor_21_out), .out(transistor_17_out), .gate(e2));
  Transistor #(.\type ("n")) transistor_29 (.in(transistor_30_out), .out(transistor_17_out), .gate(g2));
  Transistor #(.\type ("n")) transistor_30 (.in(1'b0), .out(transistor_30_out), .gate(g1));
  Transistor #(.\type ("n")) transistor_31 (.in(transistor_32_out), .out(transistor_17_out), .gate(h1));
  Transistor #(.\type ("n")) transistor_32 (.in(1'b0), .out(transistor_32_out), .gate(h2));
  Transistor transistor_33 (.in(1'b1), .out(Z), .gate(transistor_1_out));
  Transistor #(.\type ("n")) transistor_34 (.in(transistor_35_out), .out(Z), .gate(transistor_1_out));
  Transistor #(.\type ("n")) transistor_35 (.in(1'b0), .out(transistor_35_out), .gate(transistor_17_out));
  Transistor transistor_36 (.in(1'b1), .out(Z), .gate(transistor_17_out));
  and and_1 (and_1_out, a1, a2);
  and and_2 (and_2_out, b1, b2);
  and and_3 (and_3_out, c1, c2);
  and and_4 (and_4_out, d1, d2);
  and and_5 (and_5_out, e1_2, e2_2);
  and and_6 (and_6_out, f1_2, f2_2);
  and and_7 (and_7_out, g1_2, g2_2);
  and and_8 (and_8_out, h1_2, h2_2);
  nor nor_1 (nor_1_out, and_1_out, and_2_out, and_3_out, and_4_out);
  nor nor_2 (nor_2_out, and_5_out, and_6_out, and_7_out, and_8_out);
  nand nand_1 (Z_2, nor_1_out, nor_2_out);

  // Notes on the sheet:
  //   ~
  //   AON22222222
endmodule

module cell56 (
  input  nc2,
  input  nc2_2,
  input  D,
  input  c1,
  input  c2,
  output Q
);

  wire transistor_2_out, transistor_4_out, transistor_6_out, transistor_7_out, transistor_9_out;

  Transistor transistor_1 (.in(1'b1), .out(D), .gate(nc2_2));
  Transistor transistor_2 (.in(1'b1), .out(transistor_2_out), .gate(D));
  Transistor #(.\type ("n")) transistor_3 (.in(1'b0), .out(transistor_2_out), .gate(D));
  Transistor transistor_4 (.in(transistor_2_out), .out(transistor_4_out), .gate(nc2));
  Transistor #(.\type ("n")) transistor_5 (.in(transistor_2_out), .out(transistor_4_out), .gate(c1));
  Transistor transistor_6 (.in(1'b1), .out(transistor_6_out), .gate(transistor_4_out));
  Transistor transistor_7 (.in(transistor_6_out), .out(transistor_7_out), .gate(nc2_2));
  Transistor #(.\type ("n")) transistor_8 (.in(transistor_9_out), .out(transistor_7_out), .gate(c2));
  Transistor #(.\type ("n")) transistor_9 (.in(1'b0), .out(transistor_9_out), .gate(transistor_4_out));
  Transistor transistor_10 (.in(1'b1), .out(Q), .gate(transistor_7_out));
  Transistor #(.\type ("n")) transistor_11 (.in(1'b0), .out(Q), .gate(transistor_7_out));
endmodule

module cell57__AOI33 (
  input  a1,
  input  a2,
  input  a1_2,
  input  a3,
  input  a2_2,
  input  a3_2,
  input  b1,
  input  b1_2,
  input  b2,
  input  b2_2,
  input  b3,
  input  b3_2,
  output g,
  output g_2
);

  wire and_1_out, and_2_out, transistor_1_out, transistor_4_out, transistor_5_out, transistor_11_out,
       transistor_12_out;

  Transistor transistor_1 (.in(1'b1), .out(transistor_1_out), .gate(b1_2));
  Transistor transistor_2 (.in(transistor_1_out), .out(g), .gate(a1));
  Transistor #(.\type ("n")) transistor_3 (.in(transistor_4_out), .out(g), .gate(a3));
  Transistor #(.\type ("n")) transistor_4 (.in(transistor_5_out), .out(transistor_4_out), .gate(a2));
  Transistor #(.\type ("n")) transistor_5 (.in(1'b0), .out(transistor_5_out), .gate(a1));
  Transistor transistor_6 (.in(1'b1), .out(transistor_1_out), .gate(b2_2));
  Transistor transistor_7 (.in(transistor_1_out), .out(g), .gate(a2));
  Transistor transistor_8 (.in(1'b1), .out(transistor_1_out), .gate(b3_2));
  Transistor transistor_9 (.in(transistor_1_out), .out(g), .gate(a3));
  Transistor #(.\type ("n")) transistor_10 (.in(transistor_11_out), .out(g), .gate(b1_2));
  Transistor #(.\type ("n")) transistor_11 (.in(transistor_12_out), .out(transistor_11_out), .gate(b2_2));
  Transistor #(.\type ("n")) transistor_12 (.in(1'b0), .out(transistor_12_out), .gate(b3_2));
  and and_1 (and_1_out, a1_2, a2_2, a3_2);
  and and_2 (and_2_out, b1, b2, b3);
  nor nor_1 (g_2, and_1_out, and_2_out);

  // Notes on the sheet:
  //   ~
  //   AOI33
endmodule

module cell58__AOI333 (
  input  a1,
  input  a1_2,
  input  a2,
  input  a2_2,
  input  a3,
  input  a3_2,
  input  b1,
  input  b1_2,
  input  b2,
  input  b2_2,
  input  b3,
  input  b3_2,
  input  c1,
  input  c1_2,
  input  c2,
  input  c2_2,
  input  c3,
  input  c3_2,
  output j,
  output j_2
);

  wire and_1_out, and_2_out, and_3_out, transistor_1_out, transistor_3_out, transistor_9_out,
       transistor_10_out, transistor_11_out, transistor_12_out, transistor_17_out, transistor_18_out;

  Transistor transistor_1 (.in(1'b1), .out(transistor_1_out), .gate(a2_2));
  Transistor transistor_2 (.in(1'b1), .out(transistor_1_out), .gate(a1_2));
  Transistor transistor_3 (.in(transistor_1_out), .out(transistor_3_out), .gate(b1_2));
  Transistor transistor_4 (.in(transistor_1_out), .out(transistor_3_out), .gate(b2_2));
  Transistor transistor_5 (.in(transistor_3_out), .out(j), .gate(c1_2));
  Transistor transistor_6 (.in(transistor_3_out), .out(j), .gate(c2_2));
  Transistor #(.\type ("n")) transistor_7 (.in(transistor_10_out), .out(j), .gate(b1_2));
  Transistor #(.\type ("n")) transistor_8 (.in(transistor_9_out), .out(j), .gate(a3_2));
  Transistor #(.\type ("n")) transistor_9 (.in(transistor_11_out), .out(transistor_9_out), .gate(a2_2));
  Transistor #(.\type ("n")) transistor_10 (.in(transistor_12_out), .out(transistor_10_out), .gate(b2_2));
  Transistor #(.\type ("n")) transistor_11 (.in(1'b0), .out(transistor_11_out), .gate(a1_2));
  Transistor #(.\type ("n")) transistor_12 (.in(1'b0), .out(transistor_12_out), .gate(b3_2));
  Transistor transistor_13 (.in(1'b1), .out(transistor_1_out), .gate(a3_2));
  Transistor transistor_14 (.in(transistor_1_out), .out(transistor_3_out), .gate(b3_2));
  Transistor transistor_15 (.in(transistor_3_out), .out(j), .gate(c3_2));
  Transistor #(.\type ("n")) transistor_16 (.in(transistor_17_out), .out(j), .gate(c3_2));
  Transistor #(.\type ("n")) transistor_17 (.in(transistor_18_out), .out(transistor_17_out), .gate(c2_2));
  Transistor #(.\type ("n")) transistor_18 (.in(1'b0), .out(transistor_18_out), .gate(c1_2));
  and and_1 (and_1_out, a1, a2, a3);
  and and_2 (and_2_out, b1, b2, b3);
  and and_3 (and_3_out, c1, c2, c3);
  nor nor_1 (j_2, and_1_out, and_2_out, and_3_out);

  // Notes on the sheet:
  //   ~
  //   AOI333
endmodule

module cell59__AON3333 (
  input  a1,
  input  a2,
  input  a1_2,
  input  a3,
  input  a2_2,
  input  b1,
  input  a3_2,
  input  b2,
  input  b1_2,
  input  b3,
  input  b2_2,
  input  c1,
  input  b3_2,
  input  c2,
  input  c1_2,
  input  c3,
  input  c2_2,
  input  d1,
  input  c3_2,
  input  d2,
  input  d1_2,
  input  d3,
  input  d2_2,
  input  d3_2,
  output Z,
  output Z_2
);

  wire and_1_out, and_2_out, and_3_out, and_4_out, transistor_1_out, transistor_2_out, transistor_3_out,
       transistor_4_out, transistor_6_out, transistor_7_out, transistor_14_out, transistor_15_out,
       transistor_16_out, transistor_17_out, transistor_23_out, transistor_24_out;

  Transistor transistor_1 (.in(1'b1), .out(transistor_1_out), .gate(a3));
  Transistor transistor_2 (.in(transistor_1_out), .out(transistor_2_out), .gate(b3));
  Transistor transistor_3 (.in(transistor_2_out), .out(transistor_3_out), .gate(c3));
  Transistor transistor_4 (.in(transistor_3_out), .out(transistor_4_out), .gate(d3));
  Transistor #(.\type ("n")) transistor_5 (.in(transistor_6_out), .out(transistor_4_out), .gate(a3));
  Transistor #(.\type ("n")) transistor_6 (.in(transistor_7_out), .out(transistor_6_out), .gate(a2));
  Transistor #(.\type ("n")) transistor_7 (.in(1'b0), .out(transistor_7_out), .gate(a1));
  Transistor transistor_8 (.in(1'b1), .out(transistor_1_out), .gate(a2));
  Transistor transistor_9 (.in(transistor_1_out), .out(transistor_2_out), .gate(b2));
  Transistor transistor_10 (.in(transistor_2_out), .out(transistor_3_out), .gate(c2));
  Transistor transistor_11 (.in(transistor_3_out), .out(transistor_4_out), .gate(d2));
  Transistor #(.\type ("n")) transistor_12 (.in(transistor_14_out), .out(transistor_4_out), .gate(b1));
  Transistor #(.\type ("n")) transistor_13 (.in(transistor_15_out), .out(transistor_4_out), .gate(c3));
  Transistor #(.\type ("n")) transistor_14 (.in(transistor_17_out), .out(transistor_14_out), .gate(b2));
  Transistor #(.\type ("n")) transistor_15 (.in(transistor_16_out), .out(transistor_15_out), .gate(c2));
  Transistor #(.\type ("n")) transistor_16 (.in(1'b0), .out(transistor_16_out), .gate(c1));
  Transistor #(.\type ("n")) transistor_17 (.in(1'b0), .out(transistor_17_out), .gate(b3));
  Transistor transistor_18 (.in(1'b1), .out(transistor_1_out), .gate(a1));
  Transistor transistor_19 (.in(transistor_1_out), .out(transistor_2_out), .gate(b1));
  Transistor transistor_20 (.in(transistor_2_out), .out(transistor_3_out), .gate(c1));
  Transistor transistor_21 (.in(transistor_3_out), .out(transistor_4_out), .gate(d1));
  Transistor #(.\type ("n")) transistor_22 (.in(transistor_23_out), .out(transistor_4_out), .gate(d1));
  Transistor #(.\type ("n")) transistor_23 (.in(transistor_24_out), .out(transistor_23_out), .gate(d2));
  Transistor #(.\type ("n")) transistor_24 (.in(1'b0), .out(transistor_24_out), .gate(d3));
  Transistor transistor_25 (.in(1'b1), .out(Z), .gate(transistor_4_out));
  Transistor #(.\type ("n")) transistor_26 (.in(1'b0), .out(Z), .gate(transistor_4_out));
  and and_1 (and_1_out, a1_2, a2_2, a3_2);
  and and_2 (and_2_out, b1_2, b2_2, b3_2);
  and and_3 (and_3_out, c1_2, c2_2, c3_2);
  and and_4 (and_4_out, d1_2, d2_2, d3_2);
  or or_1 (Z_2, and_1_out, and_2_out, and_3_out, and_4_out);

  // Notes on the sheet:
  //   ~
  //   AON3333
endmodule

module cell60 (
  input  nc1,
  input  a,
  input  c1,
  output b
);

  wire transistor_1_out;

  Transistor transistor_1 (.in(a), .out(transistor_1_out), .gate(nc1));
  Transistor #(.\type ("n")) transistor_2 (.in(a), .out(transistor_1_out), .gate(c1));
  Transistor transistor_3 (.in(1'b1), .out(b), .gate(transistor_1_out));
  Transistor #(.\type ("n")) transistor_4 (.in(1'b0), .out(b), .gate(transistor_1_out));
  Transistor transistor_5 (.in(1'b1), .out(b), .gate(transistor_1_out));
  Transistor #(.\type ("n")) transistor_6 (.in(1'b0), .out(b), .gate(transistor_1_out));
endmodule

module cell61__AON21SR (
  input  nc1,
  input  nc2,
  input  a1,
  input  a1_2,
  input  c1,
  input  c2,
  input  a2,
  input  a2_2,
  input  b,
  input  c1_2,
  input  c2_2,
  input  b_2,
  output Q,
  output Q_2
);

  wire and_1_out, d_ff_1_qn, nor_1_out, transistor_1_out, transistor_2_out, transistor_3_out,
       transistor_7_out, transistor_8_out, transistor_10_out, transistor_11_out, transistor_12_out,
       transistor_14_out;

  Transistor transistor_1 (.in(1'b1), .out(transistor_1_out), .gate(a1));
  Transistor #(.\type ("n")) transistor_2 (.in(transistor_3_out), .out(transistor_2_out), .gate(a2_2));
  Transistor #(.\type ("n")) transistor_3 (.in(1'b0), .out(transistor_3_out), .gate(a1));
  Transistor transistor_4 (.in(1'b1), .out(transistor_1_out), .gate(a2_2));
  Transistor transistor_5 (.in(transistor_1_out), .out(transistor_2_out), .gate(b_2));
  Transistor #(.\type ("n")) transistor_6 (.in(1'b0), .out(transistor_2_out), .gate(b_2));
  Transistor transistor_7 (.in(1'b1), .out(transistor_7_out), .gate(transistor_2_out));
  Transistor transistor_8 (.in(transistor_7_out), .out(transistor_8_out), .gate(nc1));
  Transistor #(.\type ("n")) transistor_9 (.in(transistor_10_out), .out(transistor_8_out), .gate(c1_2));
  Transistor #(.\type ("n")) transistor_10 (.in(1'b0), .out(transistor_10_out), .gate(transistor_2_out));
  Transistor transistor_11 (.in(1'b1), .out(transistor_11_out), .gate(transistor_8_out));
  Transistor transistor_12 (.in(transistor_11_out), .out(transistor_12_out), .gate(nc2));
  Transistor #(.\type ("n")) transistor_13 (.in(transistor_14_out), .out(transistor_12_out), .gate(c2_2));
  Transistor #(.\type ("n")) transistor_14 (.in(1'b0), .out(transistor_14_out), .gate(transistor_8_out));
  Transistor transistor_15 (.in(1'b1), .out(Q), .gate(transistor_12_out));
  Transistor #(.\type ("n")) transistor_16 (.in(1'b0), .out(Q), .gate(transistor_12_out));
  and and_1 (and_1_out, a1_2, a2);
  D_Flip_Flop #(.trigger("high")) d_ff_1 (.clk(c1), .D(nor_1_out), .Qn(d_ff_1_qn));  // open: Q, preset, en, reset
  nor nor_1 (nor_1_out, and_1_out, b);
  D_Flip_Flop #(.trigger("high")) d_ff_2 (.clk(c2), .D(d_ff_1_qn), .Qn(Q_2));  // open: Q, preset, en, reset

  // Notes on the sheet:
  //   ~
  //   AON21SR
endmodule

module cell62__AOI221 (
  input  b,
  input  c,
  input  d,
  input  b_2,
  input  e,
  input  c_2,
  input  f,
  input  d_2,
  input  e_2,
  input  f_2,
  output Z,
  output Z_2
);

  wire and_1_out, and_2_out, transistor_2_out, transistor_3_out, transistor_6_out, transistor_10_out;

  Transistor #(.\type ("n")) transistor_1 (.in(1'b0), .out(Z_2), .gate(b));
  Transistor transistor_2 (.in(1'b1), .out(transistor_2_out), .gate(c));
  Transistor transistor_3 (.in(transistor_2_out), .out(transistor_3_out), .gate(f));
  Transistor transistor_4 (.in(transistor_3_out), .out(Z_2), .gate(b));
  Transistor #(.\type ("n")) transistor_5 (.in(transistor_6_out), .out(Z_2), .gate(c));
  Transistor #(.\type ("n")) transistor_6 (.in(1'b0), .out(transistor_6_out), .gate(d));
  Transistor transistor_7 (.in(1'b1), .out(transistor_2_out), .gate(d));
  Transistor transistor_8 (.in(transistor_2_out), .out(transistor_3_out), .gate(e));
  Transistor #(.\type ("n")) transistor_9 (.in(transistor_10_out), .out(Z_2), .gate(f));
  Transistor #(.\type ("n")) transistor_10 (.in(1'b0), .out(transistor_10_out), .gate(e));
  and and_1 (and_1_out, c_2, d_2);
  and and_2 (and_2_out, e_2, f_2);
  nor nor_1 (Z, b_2, and_1_out, and_2_out);

  // Notes on the sheet:
  //   ~
  //   AOI221
endmodule

module cell63___NAND5 (
  input  a,
  input  b,
  input  c,
  input  a_2,
  input  b_2,
  input  d,
  input  c_2,
  input  d_2,
  input  e,
  input  e_2,
  output Z,
  output Z_2
);

  wire transistor_1_out, transistor_3_out, transistor_4_out, transistor_5_out, transistor_8_out,
       transistor_10_out, transistor_12_out;

  Transistor transistor_1 (.in(1'b1), .out(transistor_1_out), .gate(c));
  Transistor #(.\type ("n")) transistor_2 (.in(transistor_3_out), .out(transistor_1_out), .gate(a));
  Transistor #(.\type ("n")) transistor_3 (.in(transistor_4_out), .out(transistor_3_out), .gate(b));
  Transistor #(.\type ("n")) transistor_4 (.in(1'b0), .out(transistor_4_out), .gate(c));
  Transistor transistor_5 (.in(1'b1), .out(transistor_5_out), .gate(e));
  Transistor transistor_6 (.in(1'b1), .out(transistor_5_out), .gate(d));
  Transistor #(.\type ("n")) transistor_7 (.in(transistor_8_out), .out(transistor_5_out), .gate(d));
  Transistor #(.\type ("n")) transistor_8 (.in(1'b0), .out(transistor_8_out), .gate(e));
  Transistor transistor_9 (.in(1'b1), .out(transistor_1_out), .gate(b));
  Transistor #(.\type ("n")) transistor_10 (.in(1'b0), .out(transistor_10_out), .gate(transistor_5_out));
  Transistor transistor_11 (.in(1'b1), .out(transistor_1_out), .gate(a));
  Transistor transistor_12 (.in(1'b1), .out(transistor_12_out), .gate(transistor_5_out));
  Transistor transistor_13 (.in(transistor_12_out), .out(transistor_10_out), .gate(transistor_1_out));
  Transistor #(.\type ("n")) transistor_14 (.in(1'b0), .out(transistor_10_out), .gate(transistor_1_out));
  Transistor transistor_15 (.in(1'b1), .out(Z), .gate(transistor_10_out));
  Transistor #(.\type ("n")) transistor_16 (.in(1'b0), .out(Z), .gate(transistor_10_out));
  nand nand_1 (Z_2, a_2, b_2, c_2, d_2, e_2);

  // Notes on the sheet:
  //   ~
  //   NAND5
endmodule

module cell64__AON33 (
  input  a1,
  input  a1_2,
  input  a2,
  input  a2_2,
  input  a3,
  input  a3_2,
  input  b1,
  input  b2,
  input  b3,
  input  b1_2,
  input  b2_2,
  input  b3_2,
  output Z,
  output Z_2
);

  wire and_1_out, and_2_out, transistor_1_out, transistor_3_out, transistor_6_out, transistor_7_out,
       transistor_11_out, transistor_12_out;

  Transistor transistor_1 (.in(1'b1), .out(transistor_1_out), .gate(b2_2));
  Transistor transistor_2 (.in(1'b1), .out(transistor_1_out), .gate(b1_2));
  Transistor transistor_3 (.in(transistor_1_out), .out(transistor_3_out), .gate(a3));
  Transistor transistor_4 (.in(transistor_1_out), .out(transistor_3_out), .gate(a2));
  Transistor #(.\type ("n")) transistor_5 (.in(transistor_6_out), .out(transistor_3_out), .gate(a1));
  Transistor #(.\type ("n")) transistor_6 (.in(transistor_7_out), .out(transistor_6_out), .gate(a2));
  Transistor #(.\type ("n")) transistor_7 (.in(1'b0), .out(transistor_7_out), .gate(a3));
  Transistor transistor_8 (.in(1'b1), .out(transistor_1_out), .gate(b3_2));
  Transistor transistor_9 (.in(transistor_1_out), .out(transistor_3_out), .gate(a1));
  Transistor #(.\type ("n")) transistor_10 (.in(transistor_11_out), .out(transistor_3_out), .gate(b1_2));
  Transistor #(.\type ("n")) transistor_11 (.in(transistor_12_out), .out(transistor_11_out), .gate(b2_2));
  Transistor #(.\type ("n")) transistor_12 (.in(1'b0), .out(transistor_12_out), .gate(b3_2));
  Transistor transistor_13 (.in(1'b1), .out(Z), .gate(transistor_3_out));
  Transistor #(.\type ("n")) transistor_14 (.in(1'b0), .out(Z), .gate(transistor_3_out));
  and and_1 (and_1_out, a1_2, a2_2, a3_2);
  or or_1 (Z_2, and_1_out, and_2_out);
  and and_2 (and_2_out, b1, b2, b3);

  // Notes on the sheet:
  //   ~
  //   AON33
endmodule

module cell65__FA_SR (
  input  nc1,
  input  nc2,
  input  c,
  input  a,
  input  b,
  input  c1,
  input  c2,
  input  C_2,
  input  CI,
  input  A_2,
  input  B_2,
  output ns,
  output s,
  output c_out,
  output nQ,
  output Q,
  output CO
);

  wire adder_1_out, d_ff_1_qn, not_1_out, transistor_1_out, transistor_2_out, transistor_4_out,
       transistor_7_out, transistor_8_out, transistor_11_out, transistor_12_out, transistor_14_out,
       transistor_19_out, transistor_20_out, transistor_23_out, transistor_24_out, transistor_25_out,
       transistor_26_out, transistor_28_out, transistor_31_out, transistor_32_out, transistor_34_out;

  Transistor transistor_1 (.in(1'b1), .out(transistor_1_out), .gate(a));
  Transistor transistor_2 (.in(transistor_1_out), .out(transistor_2_out), .gate(c));
  Transistor #(.\type ("n")) transistor_3 (.in(transistor_4_out), .out(transistor_2_out), .gate(c));
  Transistor #(.\type ("n")) transistor_4 (.in(1'b0), .out(transistor_4_out), .gate(a));
  Transistor transistor_5 (.in(1'b1), .out(transistor_1_out), .gate(b));
  Transistor #(.\type ("n")) transistor_6 (.in(1'b0), .out(transistor_4_out), .gate(b));
  Transistor transistor_7 (.in(1'b1), .out(transistor_7_out), .gate(c));
  Transistor transistor_8 (.in(1'b1), .out(transistor_8_out), .gate(b));
  Transistor transistor_9 (.in(transistor_8_out), .out(transistor_2_out), .gate(a));
  Transistor #(.\type ("n")) transistor_10 (.in(transistor_12_out), .out(transistor_2_out), .gate(a));
  Transistor #(.\type ("n")) transistor_11 (.in(1'b0), .out(transistor_11_out), .gate(c));
  Transistor #(.\type ("n")) transistor_12 (.in(1'b0), .out(transistor_12_out), .gate(b));
  Transistor transistor_13 (.in(1'b1), .out(transistor_7_out), .gate(a));
  Transistor transistor_14 (.in(transistor_7_out), .out(transistor_14_out), .gate(transistor_2_out));
  Transistor #(.\type ("n")) transistor_15 (.in(transistor_11_out), .out(transistor_14_out), .gate(transistor_2_out));
  Transistor #(.\type ("n")) transistor_16 (.in(1'b0), .out(transistor_11_out), .gate(a));
  Transistor transistor_17 (.in(1'b1), .out(transistor_7_out), .gate(b));
  Transistor #(.\type ("n")) transistor_18 (.in(1'b0), .out(transistor_11_out), .gate(b));
  Transistor transistor_19 (.in(1'b1), .out(transistor_19_out), .gate(b));
  Transistor transistor_20 (.in(transistor_19_out), .out(transistor_20_out), .gate(a));
  Transistor transistor_21 (.in(transistor_20_out), .out(transistor_14_out), .gate(c));
  Transistor #(.\type ("n")) transistor_22 (.in(transistor_23_out), .out(transistor_14_out), .gate(c));
  Transistor #(.\type ("n")) transistor_23 (.in(transistor_24_out), .out(transistor_23_out), .gate(a));
  Transistor #(.\type ("n")) transistor_24 (.in(1'b0), .out(transistor_24_out), .gate(b));
  Adder #(.width(1)) adder_1 (.a(A_2), .b(B_2), .out(adder_1_out), .cin(CI), .cout(CO));
  Transistor transistor_25 (.in(1'b1), .out(transistor_25_out), .gate(transistor_14_out));
  Transistor transistor_26 (.in(transistor_25_out), .out(transistor_26_out), .gate(nc1));
  Transistor #(.\type ("n")) transistor_27 (.in(transistor_28_out), .out(transistor_26_out), .gate(c1));
  Transistor #(.\type ("n")) transistor_28 (.in(1'b0), .out(transistor_28_out), .gate(transistor_14_out));
  Transistor transistor_29 (.in(1'b1), .out(c_out), .gate(transistor_2_out));
  Transistor #(.\type ("n")) transistor_30 (.in(1'b0), .out(c_out), .gate(transistor_2_out));
  not not_1 (not_1_out, C_2);
  D_Flip_Flop #(.trigger("high")) d_ff_1 (.clk(C_2), .D(adder_1_out), .Qn(d_ff_1_qn));  // open: Q, preset, en, reset
  D_Flip_Flop #(.trigger("high")) d_ff_2 (.clk(not_1_out), .D(d_ff_1_qn), .Q(nQ), .Qn(Q));  // open: preset, en, reset
  Transistor transistor_31 (.in(1'b1), .out(transistor_31_out), .gate(transistor_26_out));
  Transistor transistor_32 (.in(transistor_31_out), .out(transistor_32_out), .gate(nc2));
  Transistor #(.\type ("n")) transistor_33 (.in(transistor_34_out), .out(transistor_32_out), .gate(c2));
  Transistor #(.\type ("n")) transistor_34 (.in(1'b0), .out(transistor_34_out), .gate(transistor_26_out));
  Transistor transistor_35 (.in(1'b1), .out(s), .gate(transistor_32_out));
  Transistor #(.\type ("n")) transistor_36 (.in(1'b0), .out(s), .gate(transistor_32_out));
  Transistor transistor_37 (.in(1'b1), .out(ns), .gate(s));
  Transistor #(.\type ("n")) transistor_38 (.in(1'b0), .out(ns), .gate(s));

  // Notes on the sheet:
  //   ~
endmodule
module cell66___AOI222 (
  input  a1,
  input  a2,
  input  a1_2,
  input  b1,
  input  a2_2,
  input  b2,
  input  b1_2,
  input  c1,
  input  b2_2,
  input  c2,
  input  c1_2,
  input  c2_2,
  output Z,
  output Z_2
);

  wire and_1_out, and_2_out, and_3_out, transistor_1_out, transistor_2_out, transistor_5_out,
       transistor_11_out, transistor_12_out;

  Transistor transistor_1 (.in(1'b1), .out(transistor_1_out), .gate(a2));
  Transistor transistor_2 (.in(transistor_1_out), .out(transistor_2_out), .gate(b1));
  Transistor transistor_3 (.in(transistor_2_out), .out(Z), .gate(c1));
  Transistor #(.\type ("n")) transistor_4 (.in(transistor_5_out), .out(Z), .gate(a1));
  Transistor #(.\type ("n")) transistor_5 (.in(1'b0), .out(transistor_5_out), .gate(a2));
  Transistor transistor_6 (.in(1'b1), .out(transistor_1_out), .gate(a1));
  Transistor transistor_7 (.in(transistor_1_out), .out(transistor_2_out), .gate(b2));
  Transistor transistor_8 (.in(transistor_2_out), .out(Z), .gate(c2));
  Transistor #(.\type ("n")) transistor_9 (.in(transistor_12_out), .out(Z), .gate(b2));
  Transistor #(.\type ("n")) transistor_10 (.in(transistor_11_out), .out(Z), .gate(c1));
  Transistor #(.\type ("n")) transistor_11 (.in(1'b0), .out(transistor_11_out), .gate(c2));
  Transistor #(.\type ("n")) transistor_12 (.in(1'b0), .out(transistor_12_out), .gate(b1));
  and and_1 (and_1_out, a1_2, a2_2);
  and and_2 (and_2_out, b1_2, b2_2);
  and and_3 (and_3_out, c1_2, c2_2);
  nor nor_1 (Z_2, and_1_out, and_2_out, and_3_out);

  // Notes on the sheet:
  //   ~
  //   AOI222
endmodule

module cell67__OR8 (
  input  b,
  input  c,
  input  d,
  input  e,
  input  b_2,
  input  c_2,
  input  d_2,
  input  e_2,
  input  f,
  input  g,
  input  f_2,
  input  h,
  input  g_2,
  input  i,
  input  h_2,
  input  i_2,
  output Z,
  output Z_2
);

  wire nor_1_out, nor_2_out, transistor_1_out, transistor_2_out, transistor_3_out, transistor_4_out,
       transistor_7_out, transistor_8_out, transistor_9_out, transistor_10_out, transistor_20_out;

  Transistor transistor_1 (.in(1'b1), .out(transistor_1_out), .gate(b));
  Transistor transistor_2 (.in(transistor_1_out), .out(transistor_2_out), .gate(c));
  Transistor transistor_3 (.in(transistor_2_out), .out(transistor_3_out), .gate(d));
  Transistor transistor_4 (.in(transistor_3_out), .out(transistor_4_out), .gate(e));
  Transistor #(.\type ("n")) transistor_5 (.in(1'b0), .out(transistor_4_out), .gate(b));
  Transistor #(.\type ("n")) transistor_6 (.in(1'b0), .out(transistor_4_out), .gate(c));
  Transistor transistor_7 (.in(1'b1), .out(transistor_7_out), .gate(f_2));
  Transistor transistor_8 (.in(transistor_7_out), .out(transistor_8_out), .gate(g_2));
  Transistor transistor_9 (.in(transistor_8_out), .out(transistor_9_out), .gate(h_2));
  Transistor transistor_10 (.in(transistor_9_out), .out(transistor_10_out), .gate(i_2));
  Transistor #(.\type ("n")) transistor_11 (.in(1'b0), .out(transistor_10_out), .gate(g_2));
  Transistor #(.\type ("n")) transistor_12 (.in(1'b0), .out(transistor_10_out), .gate(f_2));
  Transistor #(.\type ("n")) transistor_13 (.in(1'b0), .out(transistor_4_out), .gate(d));
  Transistor #(.\type ("n")) transistor_14 (.in(1'b0), .out(transistor_4_out), .gate(e));
  Transistor #(.\type ("n")) transistor_15 (.in(1'b0), .out(transistor_10_out), .gate(h_2));
  Transistor #(.\type ("n")) transistor_16 (.in(1'b0), .out(transistor_10_out), .gate(i_2));
  Transistor transistor_17 (.in(1'b1), .out(Z), .gate(transistor_10_out));
  Transistor transistor_18 (.in(1'b1), .out(Z), .gate(transistor_4_out));
  Transistor #(.\type ("n")) transistor_19 (.in(transistor_20_out), .out(Z), .gate(transistor_4_out));
  Transistor #(.\type ("n")) transistor_20 (.in(1'b0), .out(transistor_20_out), .gate(transistor_10_out));
  nor nor_1 (nor_1_out, b_2, c_2, d_2, e_2);
  nor nor_2 (nor_2_out, f, g, h, i);
  nand nand_1 (Z_2, nor_1_out, nor_2_out);

  // Notes on the sheet:
  //   ~
  //   OR8
endmodule

module cell68__OR7 (
  input  a,
  input  b,
  input  c,
  input  a_2,
  input  b_2,
  input  c_2,
  input  d,
  input  d_2,
  input  e,
  input  e_2,
  input  f,
  input  f_2,
  input  g,
  input  g_2,
  output Z,
  output Z_2
);

  wire nor_1_out, nor_2_out, transistor_1_out, transistor_3_out, transistor_4_out, transistor_5_out,
       transistor_6_out, transistor_9_out, transistor_10_out, transistor_18_out;

  Transistor #(.\type ("n")) transistor_1 (.in(1'b0), .out(transistor_1_out), .gate(b));
  Transistor #(.\type ("n")) transistor_2 (.in(1'b0), .out(transistor_1_out), .gate(a));
  Transistor transistor_3 (.in(1'b1), .out(transistor_3_out), .gate(d_2));
  Transistor transistor_4 (.in(transistor_3_out), .out(transistor_4_out), .gate(e_2));
  Transistor transistor_5 (.in(transistor_4_out), .out(transistor_5_out), .gate(f_2));
  Transistor transistor_6 (.in(transistor_5_out), .out(transistor_6_out), .gate(g_2));
  Transistor #(.\type ("n")) transistor_7 (.in(1'b0), .out(transistor_6_out), .gate(e_2));
  Transistor #(.\type ("n")) transistor_8 (.in(1'b0), .out(transistor_6_out), .gate(d_2));
  Transistor transistor_9 (.in(1'b1), .out(transistor_9_out), .gate(c));
  Transistor transistor_10 (.in(transistor_9_out), .out(transistor_10_out), .gate(b));
  Transistor transistor_11 (.in(transistor_10_out), .out(transistor_1_out), .gate(a));
  Transistor #(.\type ("n")) transistor_12 (.in(1'b0), .out(transistor_1_out), .gate(c));
  Transistor #(.\type ("n")) transistor_13 (.in(1'b0), .out(transistor_6_out), .gate(g_2));
  Transistor #(.\type ("n")) transistor_14 (.in(1'b0), .out(transistor_6_out), .gate(f_2));
  Transistor transistor_15 (.in(1'b1), .out(Z_2), .gate(transistor_6_out));
  Transistor transistor_16 (.in(1'b1), .out(Z_2), .gate(transistor_1_out));
  Transistor #(.\type ("n")) transistor_17 (.in(transistor_18_out), .out(Z_2), .gate(transistor_1_out));
  Transistor #(.\type ("n")) transistor_18 (.in(1'b0), .out(transistor_18_out), .gate(transistor_6_out));
  nor nor_1 (nor_1_out, a_2, b_2, c_2);
  nor nor_2 (nor_2_out, d, e, f, g);
  nand nand_1 (Z, nor_1_out, nor_2_out);

  // Notes on the sheet:
  //   ~
  //   OR7
endmodule

module cell69__NAND7 (
  input  b,
  input  c,
  input  b_2,
  input  d,
  input  c_2,
  input  e,
  input  f,
  input  d_2,
  input  g,
  input  e_2,
  input  h,
  input  f_2,
  input  g_2,
  input  h_2,
  output Z,
  output Z_2
);

  wire nand_1_out, nand_2_out, transistor_1_out, transistor_4_out, transistor_5_out, transistor_6_out,
       transistor_7_out, transistor_13_out, transistor_14_out, transistor_15_out, transistor_16_out;

  Transistor transistor_1 (.in(1'b1), .out(transistor_1_out), .gate(d_2));
  Transistor transistor_2 (.in(1'b1), .out(transistor_1_out), .gate(e_2));
  Transistor #(.\type ("n")) transistor_3 (.in(transistor_4_out), .out(transistor_1_out), .gate(b_2));
  Transistor #(.\type ("n")) transistor_4 (.in(transistor_5_out), .out(transistor_4_out), .gate(c_2));
  Transistor #(.\type ("n")) transistor_5 (.in(transistor_6_out), .out(transistor_5_out), .gate(d_2));
  Transistor #(.\type ("n")) transistor_6 (.in(1'b0), .out(transistor_6_out), .gate(e_2));
  Transistor transistor_7 (.in(1'b1), .out(transistor_7_out), .gate(g_2));
  Transistor transistor_8 (.in(1'b1), .out(transistor_7_out), .gate(h_2));
  Transistor transistor_9 (.in(1'b1), .out(transistor_1_out), .gate(b_2));
  Transistor transistor_10 (.in(1'b1), .out(transistor_1_out), .gate(c_2));
  Transistor transistor_11 (.in(1'b1), .out(transistor_7_out), .gate(f_2));
  Transistor #(.\type ("n")) transistor_12 (.in(transistor_13_out), .out(transistor_7_out), .gate(h_2));
  Transistor #(.\type ("n")) transistor_13 (.in(transistor_14_out), .out(transistor_13_out), .gate(g_2));
  Transistor #(.\type ("n")) transistor_14 (.in(1'b0), .out(transistor_14_out), .gate(f_2));
  Transistor transistor_15 (.in(1'b1), .out(transistor_15_out), .gate(transistor_7_out));
  Transistor transistor_16 (.in(transistor_15_out), .out(transistor_16_out), .gate(transistor_1_out));
  Transistor #(.\type ("n")) transistor_17 (.in(1'b0), .out(transistor_16_out), .gate(transistor_1_out));
  Transistor #(.\type ("n")) transistor_18 (.in(1'b0), .out(transistor_16_out), .gate(transistor_7_out));
  Transistor transistor_19 (.in(1'b1), .out(Z), .gate(transistor_16_out));
  Transistor #(.\type ("n")) transistor_20 (.in(1'b0), .out(Z), .gate(transistor_16_out));
  nand nand_1 (nand_1_out, b, c, d, e);
  nand nand_2 (nand_2_out, f, g, h);
  or or_1 (Z_2, nand_1_out, nand_2_out);

  // Notes on the sheet:
  //   ~
  //   NAND7
endmodule

module cell70 (
  input  a,
  input  b,
  input  c,
  output e,
  output d
);

  wire transistor_1_out, transistor_3_out, transistor_4_out, transistor_6_out, transistor_7_out,
       transistor_10_out, transistor_13_out, transistor_15_out;

  Transistor transistor_1 (.in(transistor_7_out), .out(transistor_1_out), .gate(a));
  Transistor #(.\type ("n")) transistor_2 (.in(transistor_3_out), .out(transistor_1_out), .gate(b));
  Transistor #(.\type ("n")) transistor_3 (.in(1'b0), .out(transistor_3_out), .gate(a));
  Transistor transistor_4 (.in(transistor_10_out), .out(transistor_4_out), .gate(c));
  Transistor #(.\type ("n")) transistor_5 (.in(transistor_6_out), .out(transistor_4_out), .gate(b));
  Transistor #(.\type ("n")) transistor_6 (.in(1'b0), .out(transistor_6_out), .gate(c));
  Transistor #(.gate("br")) transistor_7 (.in(1'b1), .out(transistor_7_out), .gate(transistor_4_out));
  Transistor transistor_8 (.in(transistor_7_out), .out(transistor_1_out), .gate(b));
  Transistor #(.\type ("n"), .gate("br")) transistor_9 (.in(1'b0), .out(transistor_1_out), .gate(transistor_4_out));
  Transistor #(.gate("br")) transistor_10 (.in(1'b1), .out(transistor_10_out), .gate(transistor_1_out));
  Transistor transistor_11 (.in(transistor_10_out), .out(transistor_4_out), .gate(b));
  Transistor #(.\type ("n"), .gate("br")) transistor_12 (.in(1'b0), .out(transistor_4_out), .gate(transistor_1_out));
  Transistor transistor_13 (.in(1'b1), .out(transistor_13_out), .gate(transistor_1_out));
  Transistor #(.\type ("n")) transistor_14 (.in(1'b0), .out(transistor_13_out), .gate(transistor_1_out));
  Transistor transistor_15 (.in(1'b1), .out(transistor_15_out), .gate(transistor_4_out));
  Transistor #(.\type ("n")) transistor_16 (.in(1'b0), .out(transistor_15_out), .gate(transistor_4_out));
  Transistor transistor_17 (.in(1'b1), .out(e), .gate(transistor_13_out));
  Transistor #(.\type ("n")) transistor_18 (.in(1'b0), .out(e), .gate(transistor_13_out));
  Transistor transistor_19 (.in(1'b1), .out(d), .gate(transistor_15_out));
  Transistor #(.\type ("n")) transistor_20 (.in(1'b0), .out(d), .gate(transistor_15_out));
endmodule

module cell71 (
  input  a,
  input  b,
  output d,
  output e
);

  wire transistor_1_out, transistor_2_out, transistor_4_out, transistor_5_out, transistor_9_out,
       transistor_11_out;

  Transistor #(.gate("br")) transistor_1 (.in(1'b1), .out(transistor_1_out), .gate(transistor_5_out));
  Transistor transistor_2 (.in(transistor_1_out), .out(transistor_2_out), .gate(a));
  Transistor #(.\type ("n")) transistor_3 (.in(1'b0), .out(transistor_2_out), .gate(a));
  Transistor #(.gate("br")) transistor_4 (.in(1'b1), .out(transistor_4_out), .gate(transistor_2_out));
  Transistor transistor_5 (.in(transistor_4_out), .out(transistor_5_out), .gate(b));
  Transistor #(.\type ("n")) transistor_6 (.in(1'b0), .out(transistor_5_out), .gate(b));
  Transistor #(.\type ("n"), .gate("br")) transistor_7 (.in(1'b0), .out(transistor_2_out), .gate(transistor_5_out));
  Transistor #(.\type ("n"), .gate("br")) transistor_8 (.in(1'b0), .out(transistor_5_out), .gate(transistor_2_out));
  Transistor transistor_9 (.in(1'b1), .out(transistor_9_out), .gate(transistor_2_out));
  Transistor #(.\type ("n")) transistor_10 (.in(1'b0), .out(transistor_9_out), .gate(transistor_2_out));
  Transistor transistor_11 (.in(1'b1), .out(transistor_11_out), .gate(transistor_5_out));
  Transistor #(.\type ("n")) transistor_12 (.in(1'b0), .out(transistor_11_out), .gate(transistor_5_out));
  Transistor transistor_13 (.in(1'b1), .out(d), .gate(transistor_9_out));
  Transistor #(.\type ("n")) transistor_14 (.in(1'b0), .out(d), .gate(transistor_9_out));
  Transistor transistor_15 (.in(1'b1), .out(e), .gate(transistor_11_out));
  Transistor #(.\type ("n")) transistor_16 (.in(1'b0), .out(e), .gate(transistor_11_out));
endmodule

module cell73__OAI211 (
  input  a,
  input  c1,
  input  a_2,
  input  b,
  input  c2,
  input  c1_2,
  input  c2_2,
  input  b_2,
  output Z,
  output Z_2
);

  wire and_1_out, or_1_out, transistor_4_out, transistor_5_out, transistor_6_out;

  Transistor transistor_1 (.in(1'b1), .out(Z), .gate(c1));
  Transistor transistor_2 (.in(1'b1), .out(Z), .gate(c2));
  Transistor #(.\type ("n")) transistor_3 (.in(transistor_4_out), .out(Z), .gate(c2));
  Transistor #(.\type ("n"), .gate("br")) transistor_4 (.in(transistor_5_out), .out(transistor_4_out), .gate(c1));
  Transistor #(.\type ("n")) transistor_5 (.in(1'b0), .out(transistor_5_out), .gate(b_2));
  Transistor transistor_6 (.in(1'b1), .out(transistor_6_out), .gate(a));
  Transistor transistor_7 (.in(transistor_6_out), .out(Z), .gate(b_2));
  Transistor #(.\type ("n")) transistor_8 (.in(1'b0), .out(transistor_5_out), .gate(a));
  or or_1 (or_1_out, a_2, b);
  and and_1 (and_1_out, c1_2, c2_2);
  nand nand_1 (Z_2, or_1_out, and_1_out);

  // Notes on the sheet:
  //   ~
  //   OAI211
endmodule

module cell74__BUFIF0 (
  input  a,
  input  a_2,
  input  c,
  input  c_2,
  output Z,
  output Z_2
);

  wire not_1_out, transistor_1_out, transistor_3_out, transistor_5_out, transistor_8_out;

  Transistor transistor_1 (.in(1'b1), .out(transistor_1_out), .gate(a));
  Transistor #(.\type ("n")) transistor_2 (.in(1'b0), .out(transistor_1_out), .gate(a));
  Transistor transistor_3 (.in(1'b1), .out(transistor_3_out), .gate(c_2));
  Transistor #(.\type ("n")) transistor_4 (.in(1'b0), .out(transistor_3_out), .gate(c_2));
  Transistor transistor_5 (.in(1'b1), .out(transistor_5_out), .gate(transistor_3_out));
  Transistor transistor_6 (.in(transistor_5_out), .out(Z), .gate(a));
  Transistor #(.\type ("n")) transistor_7 (.in(transistor_8_out), .out(Z), .gate(transistor_1_out));
  Transistor #(.\type ("n")) transistor_8 (.in(1'b0), .out(transistor_8_out), .gate(transistor_3_out));
  not not_1 (not_1_out, a_2);
  assign Z_2 = not_1_out ? c : 1'bz;  // Controlled_Buffer controlled_buffer_1

  // Notes on the sheet:
  //   ~
  //   BUFIF0
endmodule

module cell75__DLATCH_R (
  input  D,
  input  C,
  input  D_2,
  input  E,
  input  R,
  input  nE,
  input  R_2,
  output Q,
  output Q_2
);

  wire multiplexer_1_out, nor_1_out, not_1_out, not_2_out, transistor_1_out, transistor_2_out,
       transistor_4_out, transistor_5_out, transistor_8_out, transistor_9_out, transistor_10_out,
       transistor_13_out;

  Transistor transistor_1 (.in(1'b1), .out(transistor_1_out), .gate(D));
  Transistor transistor_2 (.in(transistor_1_out), .out(transistor_2_out), .gate(nE));
  Transistor #(.\type ("n")) transistor_3 (.in(transistor_4_out), .out(transistor_2_out), .gate(C));
  Transistor #(.\type ("n")) transistor_4 (.in(1'b0), .out(transistor_4_out), .gate(D));
  Transistor transistor_5 (.in(1'b1), .out(transistor_5_out), .gate(transistor_10_out));
  Transistor transistor_6 (.in(transistor_5_out), .out(transistor_2_out), .gate(C));
  Transistor #(.\type ("n")) transistor_7 (.in(transistor_8_out), .out(transistor_2_out), .gate(nE));
  Transistor #(.\type ("n")) transistor_8 (.in(1'b0), .out(transistor_8_out), .gate(transistor_10_out));
  Transistor #(.gate("br")) transistor_9 (.in(1'b1), .out(transistor_9_out), .gate(transistor_2_out));
  Transistor transistor_10 (.in(transistor_9_out), .out(transistor_10_out), .gate(R_2));
  Transistor #(.\type ("n")) transistor_11 (.in(1'b0), .out(transistor_10_out), .gate(R_2));
  Transistor #(.\type ("n")) transistor_12 (.in(1'b0), .out(transistor_10_out), .gate(transistor_2_out));
  Transistor transistor_13 (.in(1'b1), .out(transistor_13_out), .gate(transistor_10_out));
  Transistor #(.\type ("n")) transistor_14 (.in(1'b0), .out(transistor_13_out), .gate(transistor_10_out));
  Transistor transistor_15 (.in(1'b1), .out(Q_2), .gate(transistor_13_out));
  Transistor #(.\type ("n")) transistor_16 (.in(1'b0), .out(Q_2), .gate(transistor_13_out));
  not not_1 (not_1_out, multiplexer_1_out);
  Multiplexer #(.disabled(0), .enable("false")) multiplexer_1 (
    .in0(nor_1_out), .in1(D_2), .out(multiplexer_1_out), .sel(E));
  nor nor_1 (nor_1_out, not_1_out, R);
  not not_2 (not_2_out, nor_1_out);
  not not_3 (Q, not_2_out);

  // Notes on the sheet:
  //   ~
  //   DLATCH_R
endmodule

module cell76 (
  input  nc1,
  input  nc2,
  input  c_in,
  input  r,
  input  c1,
  input  c2,
  input  a,
  output c_out,
  output ns,
  output s
);

  wire transistor_1_out, transistor_3_out, transistor_7_out, transistor_8_out, transistor_9_out,
       transistor_12_out, transistor_13_out, transistor_16_out, transistor_17_out, transistor_18_out,
       transistor_20_out, transistor_21_out, transistor_22_out, transistor_24_out, transistor_25_out,
       transistor_26_out;

  Transistor transistor_1 (.in(1'b1), .out(transistor_1_out), .gate(c_in));
  Transistor #(.\type ("n")) transistor_2 (.in(1'b0), .out(transistor_1_out), .gate(c_in));
  Transistor #(.gate("br")) transistor_3 (.in(1'b1), .out(transistor_3_out), .gate(transistor_26_out));
  Transistor transistor_4 (.in(transistor_3_out), .out(c_out), .gate(transistor_1_out));
  Transistor #(.\type ("n")) transistor_5 (.in(1'b0), .out(c_out), .gate(transistor_1_out));
  Transistor #(.\type ("n")) transistor_6 (.in(1'b0), .out(c_out), .gate(transistor_26_out));
  Transistor transistor_7 (.in(1'b1), .out(transistor_7_out), .gate(transistor_1_out));
  Transistor transistor_8 (.in(transistor_7_out), .out(transistor_8_out), .gate(c_out));
  Transistor transistor_9 (.in(transistor_8_out), .out(transistor_9_out), .gate(r));
  Transistor #(.\type ("n")) transistor_10 (.in(1'b0), .out(transistor_9_out), .gate(r));
  Transistor #(.\type ("n")) transistor_11 (.in(1'b0), .out(transistor_9_out), .gate(c_out));
  Transistor transistor_12 (.in(1'b1), .out(transistor_12_out), .gate(c_out));
  Transistor transistor_13 (.in(transistor_12_out), .out(transistor_13_out), .gate(transistor_26_out));
  Transistor transistor_14 (.in(transistor_13_out), .out(transistor_9_out), .gate(r));
  Transistor #(.\type ("n")) transistor_15 (.in(transistor_16_out), .out(transistor_9_out), .gate(transistor_26_out));
  Transistor #(.\type ("n")) transistor_16 (.in(1'b0), .out(transistor_16_out), .gate(transistor_1_out));
  Transistor transistor_17 (.in(1'b1), .out(transistor_17_out), .gate(transistor_9_out));
  Transistor transistor_18 (.in(transistor_17_out), .out(transistor_18_out), .gate(nc1));
  Transistor #(.\type ("n")) transistor_19 (.in(transistor_20_out), .out(transistor_18_out), .gate(c1));
  Transistor #(.\type ("n")) transistor_20 (.in(1'b0), .out(transistor_20_out), .gate(transistor_9_out));
  Transistor transistor_21 (.in(1'b1), .out(transistor_21_out), .gate(transistor_18_out));
  Transistor transistor_22 (.in(transistor_21_out), .out(transistor_22_out), .gate(nc2));
  Transistor #(.\type ("n")) transistor_23 (.in(transistor_24_out), .out(transistor_22_out), .gate(c2));
  Transistor #(.\type ("n")) transistor_24 (.in(1'b0), .out(transistor_24_out), .gate(transistor_18_out));
  Transistor transistor_25 (.in(1'b1), .out(transistor_25_out), .gate(a));
  Transistor transistor_26 (.in(transistor_25_out), .out(transistor_26_out), .gate(transistor_22_out));
  Transistor #(.\type ("n")) transistor_27 (.in(1'b0), .out(transistor_26_out), .gate(transistor_22_out));
  Transistor #(.\type ("n")) transistor_28 (.in(1'b0), .out(transistor_26_out), .gate(a));
  Transistor transistor_29 (.in(1'b1), .out(s), .gate(transistor_26_out));
  Transistor #(.\type ("n")) transistor_30 (.in(1'b0), .out(s), .gate(transistor_26_out));
  Transistor transistor_31 (.in(1'b1), .out(ns), .gate(s));
  Transistor #(.\type ("n")) transistor_32 (.in(1'b0), .out(ns), .gate(s));
endmodule

module cell77__CNT_BIT_REV (
  input  r,
  input  nc1,
  input  nc2,
  input  c,
  input  c1,
  input  c2,
  input  a,
  input  R_2,
  input  C_2,
  input  CI,
  input  A_2,
  output s,
  output ns,
  output c_out,
  output Q,
  output CO
);

  wire adder_1_out, d_ff_1_qn, nor_1_out, not_1_out, transistor_1_out, transistor_2_out, transistor_4_out,
       transistor_7_out, transistor_10_out, transistor_11_out, transistor_13_out, transistor_15_out,
       transistor_19_out, transistor_20_out, transistor_23_out, transistor_24_out, transistor_25_out,
       transistor_26_out, transistor_31_out, transistor_32_out, transistor_34_out, transistor_35_out,
       transistor_36_out, transistor_38_out;

  Transistor transistor_1 (.in(1'b1), .out(transistor_1_out), .gate(a));
  Transistor #(.\type ("n")) transistor_2 (.in(1'b0), .out(transistor_2_out), .gate(a));
  Transistor #(.gate("br")) transistor_3 (.in(1'b1), .out(transistor_1_out), .gate(transistor_36_out));
  Transistor transistor_4 (.in(transistor_1_out), .out(transistor_4_out), .gate(c));
  Transistor #(.\type ("n")) transistor_5 (.in(transistor_2_out), .out(transistor_4_out), .gate(c));
  Transistor #(.\type ("n"), .gate("br")) transistor_6 (.in(1'b0), .out(transistor_2_out), .gate(transistor_36_out));
  Transistor transistor_7 (.in(1'b1), .out(transistor_7_out), .gate(transistor_36_out));
  Transistor transistor_8 (.in(transistor_7_out), .out(transistor_4_out), .gate(a));
  Transistor #(.\type ("n")) transistor_9 (.in(transistor_10_out), .out(transistor_4_out), .gate(a));
  Transistor #(.\type ("n")) transistor_10 (.in(1'b0), .out(transistor_10_out), .gate(transistor_36_out));
  Transistor transistor_11 (.in(1'b1), .out(transistor_11_out), .gate(a));
  Transistor transistor_12 (.in(1'b1), .out(transistor_11_out), .gate(c));
  Transistor transistor_13 (.in(transistor_11_out), .out(transistor_13_out), .gate(transistor_4_out));
  Transistor #(.\type ("n")) transistor_14 (.in(transistor_15_out), .out(transistor_13_out), .gate(transistor_4_out));
  Transistor #(.\type ("n")) transistor_15 (.in(1'b0), .out(transistor_15_out), .gate(c));
  Transistor #(.\type ("n")) transistor_16 (.in(1'b0), .out(transistor_15_out), .gate(a));
  Adder #(.width(1)) adder_1 (.a(A_2), .b(Q), .out(adder_1_out), .cin(CI), .cout(CO));
  Transistor transistor_17 (.in(1'b1), .out(transistor_11_out), .gate(transistor_36_out));
  Transistor #(.\type ("n")) transistor_18 (.in(1'b0), .out(transistor_15_out), .gate(transistor_36_out));
  nor nor_1 (nor_1_out, R_2, adder_1_out);
  Transistor transistor_19 (.in(1'b1), .out(transistor_19_out), .gate(transistor_36_out));
  Transistor transistor_20 (.in(transistor_19_out), .out(transistor_20_out), .gate(a));
  Transistor transistor_21 (.in(transistor_20_out), .out(transistor_13_out), .gate(c));
  Transistor #(.\type ("n")) transistor_22 (.in(transistor_23_out), .out(transistor_13_out), .gate(c));
  Transistor #(.\type ("n")) transistor_23 (.in(transistor_24_out), .out(transistor_23_out), .gate(a));
  Transistor #(.\type ("n")) transistor_24 (.in(1'b0), .out(transistor_24_out), .gate(transistor_36_out));
  not not_1 (not_1_out, C_2);
  D_Flip_Flop #(.trigger("high")) d_ff_1 (.clk(C_2), .D(nor_1_out), .Qn(d_ff_1_qn));  // open: Q, preset, en, reset
  Transistor transistor_25 (.in(1'b1), .out(transistor_25_out), .gate(r));
  Transistor transistor_26 (.in(transistor_25_out), .out(transistor_26_out), .gate(transistor_13_out));
  Transistor #(.\type ("n")) transistor_27 (.in(1'b0), .out(transistor_26_out), .gate(r));
  Transistor transistor_28 (.in(1'b1), .out(c_out), .gate(transistor_4_out));
  Transistor #(.\type ("n")) transistor_29 (.in(1'b0), .out(c_out), .gate(transistor_4_out));
  D_Flip_Flop #(.trigger("high")) d_ff_2 (.clk(not_1_out), .D(d_ff_1_qn), .Qn(Q));  // open: Q, preset, en, reset
  Transistor #(.\type ("n")) transistor_30 (.in(1'b0), .out(transistor_26_out), .gate(transistor_13_out));
  Transistor transistor_31 (.in(1'b1), .out(transistor_31_out), .gate(transistor_26_out));
  Transistor transistor_32 (.in(transistor_31_out), .out(transistor_32_out), .gate(nc1));
  Transistor #(.\type ("n")) transistor_33 (.in(transistor_34_out), .out(transistor_32_out), .gate(c1));
  Transistor #(.\type ("n")) transistor_34 (.in(1'b0), .out(transistor_34_out), .gate(transistor_26_out));
  Transistor transistor_35 (.in(1'b1), .out(transistor_35_out), .gate(transistor_32_out));
  Transistor transistor_36 (.in(transistor_35_out), .out(transistor_36_out), .gate(nc2));
  Transistor #(.\type ("n")) transistor_37 (.in(transistor_38_out), .out(transistor_36_out), .gate(c2));
  Transistor #(.\type ("n")) transistor_38 (.in(1'b0), .out(transistor_38_out), .gate(transistor_32_out));
  Transistor transistor_39 (.in(1'b1), .out(ns), .gate(transistor_36_out));
  Transistor #(.\type ("n")) transistor_40 (.in(1'b0), .out(ns), .gate(transistor_36_out));
  Transistor transistor_41 (.in(1'b1), .out(s), .gate(ns));
  Transistor #(.\type ("n")) transistor_42 (.in(1'b0), .out(s), .gate(ns));

  // Notes on the sheet:
  //   ~
  //   CNT_BIT_REV
endmodule

module cell78__AON333 (
  input  a1,
  input  a1_2,
  input  a2,
  input  a2_2,
  input  a3,
  input  a3_2,
  input  b1,
  input  b1_2,
  input  b2,
  input  b2_2,
  input  b3,
  input  b3_2,
  input  c1,
  input  c1_2,
  input  c2,
  input  c2_2,
  input  c3,
  input  c3_2,
  output Z,
  output Z_2
);

  wire and_1_out, and_2_out, and_3_out, transistor_1_out, transistor_2_out, transistor_3_out,
       transistor_5_out, transistor_6_out, transistor_11_out, transistor_12_out, transistor_17_out,
       transistor_18_out;

  Transistor transistor_1 (.in(1'b1), .out(transistor_1_out), .gate(c1_2));
  Transistor transistor_2 (.in(transistor_1_out), .out(transistor_2_out), .gate(b1_2));
  Transistor transistor_3 (.in(transistor_2_out), .out(transistor_3_out), .gate(a1_2));
  Transistor #(.\type ("n")) transistor_4 (.in(transistor_5_out), .out(transistor_3_out), .gate(a1_2));
  Transistor #(.\type ("n")) transistor_5 (.in(transistor_6_out), .out(transistor_5_out), .gate(a2_2));
  Transistor #(.\type ("n")) transistor_6 (.in(1'b0), .out(transistor_6_out), .gate(a3_2));
  Transistor transistor_7 (.in(1'b1), .out(transistor_1_out), .gate(c2_2));
  Transistor transistor_8 (.in(transistor_1_out), .out(transistor_2_out), .gate(b2_2));
  Transistor transistor_9 (.in(transistor_2_out), .out(transistor_3_out), .gate(a2_2));
  Transistor #(.\type ("n")) transistor_10 (.in(transistor_11_out), .out(transistor_3_out), .gate(b3_2));
  Transistor #(.\type ("n")) transistor_11 (.in(transistor_12_out), .out(transistor_11_out), .gate(b2_2));
  Transistor #(.\type ("n")) transistor_12 (.in(1'b0), .out(transistor_12_out), .gate(b1_2));
  Transistor transistor_13 (.in(1'b1), .out(transistor_1_out), .gate(c3_2));
  Transistor transistor_14 (.in(transistor_1_out), .out(transistor_2_out), .gate(b3_2));
  Transistor transistor_15 (.in(transistor_2_out), .out(transistor_3_out), .gate(a3_2));
  Transistor #(.\type ("n")) transistor_16 (.in(transistor_17_out), .out(transistor_3_out), .gate(c1_2));
  Transistor #(.\type ("n")) transistor_17 (.in(transistor_18_out), .out(transistor_17_out), .gate(c2_2));
  Transistor #(.\type ("n")) transistor_18 (.in(1'b0), .out(transistor_18_out), .gate(c3_2));
  Transistor transistor_19 (.in(1'b1), .out(Z), .gate(transistor_3_out));
  Transistor #(.\type ("n")) transistor_20 (.in(1'b0), .out(Z), .gate(transistor_3_out));
  and and_1 (and_1_out, a1, a2, a3);
  and and_2 (and_2_out, b1, b2, b3);
  and and_3 (and_3_out, c1, c2, c3);
  or or_1 (Z_2, and_1_out, and_2_out, and_3_out);

  // Notes on the sheet:
  //   ~
  //   AON333
endmodule

module cell79__OR9 (
  input  c,
  input  b,
  input  a,
  input  a_2,
  input  b_2,
  input  c_2,
  input  d,
  input  d_2,
  input  e,
  input  e_2,
  input  f,
  input  f_2,
  input  h,
  input  i,
  input  j,
  input  h_2,
  input  i_2,
  input  j_2,
  output Z,
  output Z_2
);

  wire nor_1_out, nor_2_out, nor_3_out, transistor_1_out, transistor_2_out, transistor_3_out,
       transistor_5_out, transistor_6_out, transistor_7_out, transistor_10_out, transistor_11_out,
       transistor_12_out, transistor_21_out, transistor_22_out;

  Transistor transistor_1 (.in(1'b1), .out(transistor_1_out), .gate(c));
  Transistor transistor_2 (.in(transistor_1_out), .out(transistor_2_out), .gate(b));
  Transistor transistor_3 (.in(transistor_2_out), .out(transistor_3_out), .gate(a));
  Transistor #(.\type ("n")) transistor_4 (.in(1'b0), .out(transistor_3_out), .gate(a));
  Transistor transistor_5 (.in(1'b1), .out(transistor_5_out), .gate(d));
  Transistor transistor_6 (.in(transistor_5_out), .out(transistor_6_out), .gate(e));
  Transistor transistor_7 (.in(transistor_6_out), .out(transistor_7_out), .gate(f_2));
  Transistor #(.\type ("n")) transistor_8 (.in(1'b0), .out(transistor_7_out), .gate(d));
  Transistor #(.\type ("n")) transistor_9 (.in(1'b0), .out(transistor_7_out), .gate(e));
  Transistor transistor_10 (.in(1'b1), .out(transistor_10_out), .gate(h_2));
  Transistor transistor_11 (.in(transistor_10_out), .out(transistor_11_out), .gate(i_2));
  Transistor transistor_12 (.in(transistor_11_out), .out(transistor_12_out), .gate(j_2));
  Transistor #(.\type ("n")) transistor_13 (.in(1'b0), .out(transistor_12_out), .gate(h_2));
  Transistor #(.\type ("n")) transistor_14 (.in(1'b0), .out(transistor_12_out), .gate(i_2));
  Transistor #(.\type ("n")) transistor_15 (.in(1'b0), .out(transistor_3_out), .gate(b));
  Transistor #(.\type ("n")) transistor_16 (.in(1'b0), .out(transistor_3_out), .gate(c));
  Transistor #(.\type ("n")) transistor_17 (.in(1'b0), .out(transistor_7_out), .gate(f_2));
  Transistor #(.\type ("n")) transistor_18 (.in(1'b0), .out(transistor_12_out), .gate(j_2));
  Transistor transistor_19 (.in(1'b1), .out(Z), .gate(transistor_7_out));
  Transistor #(.\type ("n")) transistor_20 (.in(transistor_21_out), .out(Z), .gate(transistor_12_out));
  Transistor #(.\type ("n")) transistor_21 (.in(transistor_22_out), .out(transistor_21_out), .gate(transistor_3_out));
  Transistor #(.\type ("n")) transistor_22 (.in(1'b0), .out(transistor_22_out), .gate(transistor_7_out));
  Transistor transistor_23 (.in(1'b1), .out(Z), .gate(transistor_12_out));
  Transistor transistor_24 (.in(1'b1), .out(Z), .gate(transistor_3_out));
  nor nor_1 (nor_1_out, a_2, b_2, c_2);
  nor nor_2 (nor_2_out, d_2, e_2, f);
  nor nor_3 (nor_3_out, h, i, j);
  nand nand_1 (Z_2, nor_1_out, nor_2_out, nor_3_out);

  // Notes on the sheet:
  //   ~
  //   OR9
endmodule

module cell80__NOR8 (
  input  b,
  input  c,
  input  d,
  input  e,
  input  b_2,
  input  c_2,
  input  d_2,
  input  e_2,
  input  f,
  input  g,
  input  f_2,
  input  h,
  input  g_2,
  input  i,
  input  h_2,
  input  i_2,
  output Z,
  output Z_2
);

  wire nor_1_out, nor_2_out, transistor_1_out, transistor_2_out, transistor_3_out, transistor_4_out,
       transistor_7_out, transistor_8_out, transistor_9_out, transistor_10_out, transistor_17_out,
       transistor_20_out;

  Transistor transistor_1 (.in(1'b1), .out(transistor_1_out), .gate(b));
  Transistor transistor_2 (.in(transistor_1_out), .out(transistor_2_out), .gate(c));
  Transistor transistor_3 (.in(transistor_2_out), .out(transistor_3_out), .gate(d));
  Transistor transistor_4 (.in(transistor_3_out), .out(transistor_4_out), .gate(e));
  Transistor #(.\type ("n")) transistor_5 (.in(1'b0), .out(transistor_4_out), .gate(c));
  Transistor #(.\type ("n")) transistor_6 (.in(1'b0), .out(transistor_4_out), .gate(b));
  Transistor transistor_7 (.in(1'b1), .out(transistor_7_out), .gate(f_2));
  Transistor transistor_8 (.in(transistor_7_out), .out(transistor_8_out), .gate(g_2));
  Transistor transistor_9 (.in(transistor_8_out), .out(transistor_9_out), .gate(h_2));
  Transistor transistor_10 (.in(transistor_9_out), .out(transistor_10_out), .gate(i_2));
  Transistor #(.\type ("n")) transistor_11 (.in(1'b0), .out(transistor_10_out), .gate(g_2));
  Transistor #(.\type ("n")) transistor_12 (.in(1'b0), .out(transistor_10_out), .gate(f_2));
  Transistor #(.\type ("n")) transistor_13 (.in(1'b0), .out(transistor_4_out), .gate(d));
  Transistor #(.\type ("n")) transistor_14 (.in(1'b0), .out(transistor_4_out), .gate(e));
  Transistor #(.\type ("n")) transistor_15 (.in(1'b0), .out(transistor_10_out), .gate(h_2));
  Transistor #(.\type ("n")) transistor_16 (.in(1'b0), .out(transistor_10_out), .gate(i_2));
  Transistor transistor_17 (.in(1'b1), .out(transistor_17_out), .gate(transistor_10_out));
  Transistor transistor_18 (.in(1'b1), .out(transistor_17_out), .gate(transistor_4_out));
  Transistor #(.\type ("n")) transistor_19 (.in(transistor_20_out), .out(transistor_17_out), .gate(transistor_4_out));
  Transistor #(.\type ("n")) transistor_20 (.in(1'b0), .out(transistor_20_out), .gate(transistor_10_out));
  Transistor transistor_21 (.in(1'b1), .out(Z), .gate(transistor_17_out));
  Transistor #(.\type ("n")) transistor_22 (.in(1'b0), .out(Z), .gate(transistor_17_out));
  nor nor_1 (nor_1_out, b_2, c_2, d_2, e_2);
  nor nor_2 (nor_2_out, f, g, h, i);
  and and_1 (Z_2, nor_1_out, nor_2_out);

  // Notes on the sheet:
  //   ~
  //   NOR8
endmodule

module cell84__2A3OI (
  input  a,
  input  b,
  input  c1,
  input  c2,
  input  a_2,
  input  b_2,
  input  c1_2,
  input  c2_2,
  output Z,
  output Z_2
);

  wire and_1_out, transistor_1_out, transistor_2_out, transistor_8_out;

  Transistor transistor_1 (.in(1'b1), .out(transistor_1_out), .gate(c1_2));
  Transistor transistor_2 (.in(transistor_1_out), .out(transistor_2_out), .gate(b_2));
  Transistor transistor_3 (.in(transistor_2_out), .out(Z_2), .gate(a_2));
  Transistor #(.\type ("n")) transistor_4 (.in(1'b0), .out(Z_2), .gate(a_2));
  Transistor #(.\type ("n")) transistor_5 (.in(1'b0), .out(Z_2), .gate(b_2));
  Transistor transistor_6 (.in(1'b1), .out(transistor_1_out), .gate(c2_2));
  Transistor #(.\type ("n")) transistor_7 (.in(transistor_8_out), .out(Z_2), .gate(c1_2));
  Transistor #(.\type ("n")) transistor_8 (.in(1'b0), .out(transistor_8_out), .gate(c2_2));
  and and_1 (and_1_out, c1, c2);
  nor nor_1 (Z, a, b, and_1_out);

  // Notes on the sheet:
  //   3
  //   2
  //   1
  //   5
  //   6
  //   4
  //   7
  //   8
  //   ~
  //   2A3OI
endmodule

module cell85__AOI31 (
  input  a,
  input  b1,
  input  b2,
  input  b3,
  input  a_2,
  input  b1_2,
  input  b2_2,
  input  b3_2,
  output Z,
  output Z_2
);

  wire and_1_out, transistor_1_out, transistor_7_out, transistor_8_out;

  Transistor transistor_1 (.in(1'b1), .out(transistor_1_out), .gate(b1_2));
  Transistor transistor_2 (.in(transistor_1_out), .out(Z_2), .gate(a_2));
  Transistor #(.\type ("n")) transistor_3 (.in(1'b0), .out(Z_2), .gate(a_2));
  Transistor transistor_4 (.in(1'b1), .out(transistor_1_out), .gate(b2_2));
  Transistor transistor_5 (.in(1'b1), .out(transistor_1_out), .gate(b3_2));
  Transistor #(.\type ("n")) transistor_6 (.in(transistor_7_out), .out(Z_2), .gate(b3_2));
  Transistor #(.\type ("n")) transistor_7 (.in(transistor_8_out), .out(transistor_7_out), .gate(b2_2));
  Transistor #(.\type ("n")) transistor_8 (.in(1'b0), .out(transistor_8_out), .gate(b1_2));
  and and_1 (and_1_out, b1, b2, b3);
  nor nor_1 (Z, a, and_1_out);

  // Notes on the sheet:
  //   ~
  //   AOI31
endmodule

module cell86__COMB1 (
  input  a,
  input  b,
  input  c1,
  input  a_2,
  input  c2,
  input  b_2,
  input  c,
  input  d,
  output Z,
  output Z_2
);

  wire and_1_out, or_1_out, transistor_4_out, transistor_5_out, transistor_8_out;

  Transistor transistor_1 (.in(1'b1), .out(Z_2), .gate(a_2));
  Transistor transistor_2 (.in(transistor_5_out), .out(Z_2), .gate(b_2));
  Transistor #(.\type ("n")) transistor_3 (.in(transistor_4_out), .out(Z_2), .gate(a_2));
  Transistor #(.\type ("n")) transistor_4 (.in(1'b0), .out(transistor_4_out), .gate(b_2));
  Transistor transistor_5 (.in(1'b1), .out(transistor_5_out), .gate(c));
  Transistor transistor_6 (.in(1'b1), .out(transistor_5_out), .gate(d));
  Transistor #(.\type ("n")) transistor_7 (.in(transistor_8_out), .out(transistor_4_out), .gate(d));
  Transistor #(.\type ("n")) transistor_8 (.in(1'b0), .out(transistor_8_out), .gate(c));
  and and_1 (and_1_out, c1, c2);
  or or_1 (or_1_out, b, and_1_out);
  nand nand_1 (Z, a, or_1_out);

  // Notes on the sheet:
  //   ~
  //   COMB1
endmodule

module cell87__DDLATCH (
  input  nC,
  input  D,
  input  C,
  output Q
);

  wire transistor_1_out, transistor_2_out, transistor_4_out;

  Transistor transistor_1 (.in(1'b1), .out(transistor_1_out), .gate(nC));
  Transistor transistor_2 (.in(transistor_1_out), .out(transistor_2_out), .gate(D));
  Transistor #(.\type ("n")) transistor_3 (.in(transistor_4_out), .out(transistor_2_out), .gate(D));
  Transistor #(.\type ("n")) transistor_4 (.in(1'b0), .out(transistor_4_out), .gate(C));
  Transistor transistor_5 (.in(1'b1), .out(Q), .gate(transistor_2_out));
  Transistor #(.\type ("n")) transistor_6 (.in(1'b0), .out(Q), .gate(transistor_2_out));
endmodule

module cell89_COMP_WE_STRONG (
  input  A,
  input  A_2,
  output nZ,
  output nZ_2,
  output Z,
  output Z_2
);

  wire not_3_out, transistor_1_out;

  Transistor transistor_1 (.in(1'b1), .out(transistor_1_out), .gate(A));
  Transistor #(.\type ("n")) transistor_2 (.in(1'b0), .out(transistor_1_out), .gate(A));
  Transistor transistor_3 (.in(1'b1), .out(nZ), .gate(A));
  Transistor #(.\type ("n")) transistor_4 (.in(1'b0), .out(nZ), .gate(A));
  Transistor transistor_5 (.in(1'b1), .out(Z_2), .gate(transistor_1_out));
  Transistor #(.\type ("n")) transistor_6 (.in(1'b0), .out(Z_2), .gate(transistor_1_out));
  not not_1 (nZ_2, A_2);
  not not_2 (Z, not_3_out);
  not not_3 (not_3_out, A_2);

  // Notes on the sheet:
  //   ~
endmodule

module cell90__AND9 (
  input  a,
  input  b,
  input  c,
  input  a_2,
  input  b_2,
  input  c_2,
  input  d,
  input  d_2,
  input  e,
  input  e_2,
  input  f,
  input  f_2,
  input  g,
  input  h,
  input  i,
  input  g_2,
  input  h_2,
  input  i_2,
  output X,
  output X_2
);

  wire nand_1_out, nand_2_out, nand_3_out, transistor_1_out, transistor_4_out, transistor_5_out,
       transistor_6_out, transistor_9_out, transistor_10_out, transistor_11_out, transistor_14_out,
       transistor_15_out, transistor_19_out, transistor_20_out;

  Transistor transistor_1 (.in(1'b1), .out(transistor_1_out), .gate(b));
  Transistor transistor_2 (.in(1'b1), .out(transistor_1_out), .gate(c));
  Transistor #(.\type ("n")) transistor_3 (.in(transistor_4_out), .out(transistor_1_out), .gate(a));
  Transistor #(.\type ("n")) transistor_4 (.in(transistor_5_out), .out(transistor_4_out), .gate(b));
  Transistor #(.\type ("n")) transistor_5 (.in(1'b0), .out(transistor_5_out), .gate(c));
  Transistor transistor_6 (.in(1'b1), .out(transistor_6_out), .gate(f_2));
  Transistor transistor_7 (.in(1'b1), .out(transistor_6_out), .gate(e));
  Transistor #(.\type ("n")) transistor_8 (.in(transistor_9_out), .out(transistor_6_out), .gate(d));
  Transistor #(.\type ("n")) transistor_9 (.in(transistor_10_out), .out(transistor_9_out), .gate(e));
  Transistor #(.\type ("n")) transistor_10 (.in(1'b0), .out(transistor_10_out), .gate(f_2));
  Transistor transistor_11 (.in(1'b1), .out(transistor_11_out), .gate(i_2));
  Transistor transistor_12 (.in(1'b1), .out(transistor_11_out), .gate(h_2));
  Transistor #(.\type ("n")) transistor_13 (.in(transistor_14_out), .out(transistor_11_out), .gate(g_2));
  Transistor #(.\type ("n")) transistor_14 (.in(transistor_15_out), .out(transistor_14_out), .gate(h_2));
  Transistor #(.\type ("n")) transistor_15 (.in(1'b0), .out(transistor_15_out), .gate(i_2));
  Transistor transistor_16 (.in(1'b1), .out(transistor_1_out), .gate(a));
  Transistor transistor_17 (.in(1'b1), .out(transistor_6_out), .gate(d));
  Transistor transistor_18 (.in(1'b1), .out(transistor_11_out), .gate(g_2));
  Transistor transistor_19 (.in(1'b1), .out(transistor_19_out), .gate(transistor_1_out));
  Transistor transistor_20 (.in(transistor_19_out), .out(transistor_20_out), .gate(transistor_6_out));
  Transistor transistor_21 (.in(transistor_20_out), .out(X), .gate(transistor_11_out));
  Transistor #(.\type ("n")) transistor_22 (.in(1'b0), .out(X), .gate(transistor_6_out));
  Transistor #(.\type ("n")) transistor_23 (.in(1'b0), .out(X), .gate(transistor_1_out));
  Transistor #(.\type ("n")) transistor_24 (.in(1'b0), .out(X), .gate(transistor_11_out));
  nand nand_1 (nand_1_out, a_2, b_2, c_2);
  nand nand_2 (nand_2_out, d_2, e_2, f);
  nand nand_3 (nand_3_out, g, h, i);
  nor nor_1 (X_2, nand_1_out, nand_2_out, nand_3_out);

  // Notes on the sheet:
  //   ~
  //   AND9
endmodule

module cell91__XNOR (
  input  B,
  input  A,
  input  A_2,
  input  B_2,
  output Z,
  output Z_2
);

  wire transistor_1_out, transistor_3_out, transistor_5_out, transistor_8_out, transistor_11_out;

  Transistor transistor_1 (.in(1'b1), .out(transistor_1_out), .gate(A));
  Transistor #(.\type ("n")) transistor_2 (.in(transistor_3_out), .out(transistor_1_out), .gate(A));
  Transistor #(.\type ("n")) transistor_3 (.in(1'b0), .out(transistor_3_out), .gate(B));
  Transistor #(.gate("br")) transistor_4 (.in(1'b1), .out(transistor_1_out), .gate(B));
  Transistor transistor_5 (.in(1'b1), .out(transistor_5_out), .gate(B));
  Transistor transistor_6 (.in(transistor_5_out), .out(Z), .gate(A));
  Transistor #(.\type ("n")) transistor_7 (.in(transistor_8_out), .out(Z), .gate(transistor_1_out));
  Transistor #(.\type ("n")) transistor_8 (.in(1'b0), .out(transistor_8_out), .gate(B));
  Transistor transistor_9 (.in(1'b1), .out(Z), .gate(transistor_1_out));
  Transistor #(.\type ("n")) transistor_10 (.in(transistor_11_out), .out(Z), .gate(transistor_1_out));
  Transistor #(.\type ("n")) transistor_11 (.in(1'b0), .out(transistor_11_out), .gate(A));
  xnor xnor_1 (Z_2, A_2, B_2);

  // Notes on the sheet:
  //   7
  //   1
  //   2
  //   8
  //   9
  //   10
  //   4
  //   3
  //   11
  //   5
  //   6
  //   ~
endmodule

module cell34_delay (
  input  CLK1,
  input  A,
  input  CLK2,
  output Q
);

  wire d_ff_1_qn, d_ff_2_qn, d_ff_3_qn, d_ff_4_qn, d_ff_5_qn, d_ff_6_qn, d_ff_7_qn, d_ff_8_qn, d_ff_9_qn,
       d_ff_10_qn, d_ff_11_qn, d_ff_12_qn, d_ff_13_qn, d_ff_14_qn, d_ff_15_qn;

  D_Flip_Flop #(.trigger("high")) d_ff_1 (.clk(CLK1), .D(A), .Qn(d_ff_1_qn));  // open: Q, preset, en, reset
  D_Flip_Flop #(.trigger("high")) d_ff_2 (.clk(CLK2), .D(d_ff_1_qn), .Qn(d_ff_2_qn));  // open: Q, preset, en, reset
  D_Flip_Flop #(.trigger("high")) d_ff_3 (.clk(CLK1), .D(d_ff_2_qn), .Qn(d_ff_3_qn));  // open: Q, preset, en, reset
  D_Flip_Flop #(.trigger("high")) d_ff_4 (.clk(CLK2), .D(d_ff_3_qn), .Qn(d_ff_4_qn));  // open: Q, preset, en, reset
  D_Flip_Flop #(.trigger("high")) d_ff_5 (.clk(CLK1), .D(d_ff_4_qn), .Qn(d_ff_5_qn));  // open: Q, preset, en, reset
  D_Flip_Flop #(.trigger("high")) d_ff_6 (.clk(CLK2), .D(d_ff_5_qn), .Qn(d_ff_6_qn));  // open: Q, preset, en, reset
  D_Flip_Flop #(.trigger("high")) d_ff_7 (.clk(CLK1), .D(d_ff_6_qn), .Qn(d_ff_7_qn));  // open: Q, preset, en, reset
  D_Flip_Flop #(.trigger("high")) d_ff_8 (.clk(CLK2), .D(d_ff_7_qn), .Qn(d_ff_8_qn));  // open: Q, preset, en, reset
  D_Flip_Flop #(.trigger("high")) d_ff_9 (.clk(CLK1), .D(d_ff_8_qn), .Qn(d_ff_9_qn));  // open: Q, preset, en, reset
  D_Flip_Flop #(.trigger("high")) d_ff_10 (.clk(CLK2), .D(d_ff_9_qn), .Qn(d_ff_10_qn));  // open: Q, preset, en, reset
  D_Flip_Flop #(.trigger("high")) d_ff_11 (.clk(CLK1), .D(d_ff_10_qn), .Qn(d_ff_11_qn));  // open: Q, preset, en, reset
  D_Flip_Flop #(.trigger("high")) d_ff_12 (.clk(CLK2), .D(d_ff_11_qn), .Qn(d_ff_12_qn));  // open: Q, preset, en, reset
  D_Flip_Flop #(.trigger("high")) d_ff_13 (.clk(CLK1), .D(d_ff_12_qn), .Qn(d_ff_13_qn));  // open: Q, preset, en, reset
  D_Flip_Flop #(.trigger("high")) d_ff_14 (.clk(CLK2), .D(d_ff_13_qn), .Qn(d_ff_14_qn));  // open: Q, preset, en, reset
  D_Flip_Flop #(.trigger("high")) d_ff_15 (.clk(CLK1), .D(d_ff_14_qn), .Qn(d_ff_15_qn));  // open: Q, preset, en, reset
  D_Flip_Flop #(.trigger("high")) d_ff_16 (.clk(CLK2), .D(d_ff_15_qn), .Qn(Q));  // open: Q, preset, en, reset

  // Notes on the sheet:
  //   D-Latch
  //   D-Latch
  //   D-Latch
  //   D-Latch
  //   D-Latch
  //   D-Latch
  //   D-Latch
  //   D-Latch
  //   D-Latch
  //   D-Latch
  //   D-Latch
  //   D-Latch
  //   D-Latch
  //   D-Latch
  //   D-Latch
  //   D-Latch
endmodule

module cell_32__NOT4 (
  input  in_1,
  input  in_2,
  output out_3,
  output out_4
);

  wire not_1_out, not_2_out, not_3_out, transistor_1_out, transistor_2_out, transistor_5_out;

  Transistor transistor_1 (.in(1'b1), .out(transistor_1_out), .gate(transistor_2_out));
  Transistor transistor_2 (.in(1'b1), .out(transistor_2_out), .gate(in_1));
  Transistor #(.\type ("n")) transistor_3 (.in(1'b0), .out(transistor_2_out), .gate(in_1));
  Transistor #(.\type ("n")) transistor_4 (.in(1'b0), .out(transistor_1_out), .gate(transistor_2_out));
  Transistor transistor_5 (.in(1'b1), .out(transistor_5_out), .gate(transistor_1_out));
  Transistor #(.\type ("n")) transistor_6 (.in(1'b0), .out(transistor_5_out), .gate(transistor_1_out));
  Transistor transistor_7 (.in(1'b1), .out(out_3), .gate(transistor_5_out));
  Transistor #(.\type ("n")) transistor_8 (.in(1'b0), .out(out_3), .gate(transistor_5_out));
  not not_1 (not_1_out, in_2);
  not not_2 (not_2_out, not_1_out);
  not not_3 (not_3_out, not_2_out);
  not not_4 (out_4, not_3_out);

  // Notes on the sheet:
  //   ~
  //   NOT4
endmodule
