// Logisim project Z80.circ as structural Verilog: 14 circuits, main circuit main
module main (
  input  CLK,
  input  [7:0] DB,
  input  in_3,
  input  in_4,
  input  nWAIT,
  input  [7:0] DB_2,
  input  RESET,
  input  INT,
  input  NMI,
  output AB0,
  output AB1,
  output AB2,
  output AB3,
  output AB4,
  output AB5,
  output AB6,
  output AB7,
  output AB8,
  output AB9,
  output AB10,
  output AB11,
  output AB12,
  output AB13,
  output AB14,
  output AB15,
  output [7:0] DB_3
);

  wire ADD_SUB_HL, ADR_Z, and_2_out, CLK_S, CLK_t, COND_DONE, d_latch_1_nq, d_latch_2_nq, d_latch_3_nq,
       DIS_BASE_SET, DL_D, GRP_220, GRP_239, GRP_387, GRP_A_MEM_IO, GRP_BLOCK, GRP_BRANCH, GRP_IDX, GRP_IO,
       GRP_LDI_CPI, GRP_M_HL, GRP_N8, GRP_PREFIX, GRP_R16_DIR, GRP_SHIFT, GRP_SP, HALT, HALT_REQ, IA3, IA4,
       IA5, IDX_SET, IFF2, INT_ACK, INT_CLK, int_logic_1_res2, int_logic_1_reset_pc, INT_REQ, M1, M2, M3, M4,
       M5, M6, nand_1_out, nand_2_out, nCLK, NMI_ACK, NMI_REQ, nor_1_out, nor_2_out, not_1_out, not_2_out,
       not_3_out, not_4_out, not_6_out, nRES_MCLK, nRES_TCLK, pc_control_1_hi_inc_pcr, pc_control_1_inc_pcr,
       pc_control_1_inv_pcr, pc_control_1_r_p, pc_control_1_read_pcr, pc_control_1_write_pcr, PLA1, PLA2,
       PLA3, PLA5, PLA7, PLA8, PLA42, PLA47, PLA50, PLA52, PLA53, PLA54, PLA57, PLA76, PLA88, PLA93, PLA98,
       pla_1_pla0, pla_1_pla1, pla_1_pla2, pla_1_pla3, pla_1_pla4, pla_1_pla5, pla_1_pla6, pla_1_pla7,
       pla_1_pla8, pla_1_pla9, pla_1_pla10, pla_1_pla11, pla_1_pla12, pla_1_pla13, pla_1_pla14, pla_1_pla15,
       pla_1_pla16, pla_1_pla17, pla_1_pla18, pla_1_pla19, pla_1_pla20, pla_1_pla21, pla_1_pla22,
       pla_1_pla23, pla_1_pla24, pla_1_pla25, pla_1_pla26, pla_1_pla27, pla_1_pla28, pla_1_pla29,
       pla_1_pla30, pla_1_pla31, pla_1_pla32, pla_1_pla33, pla_1_pla34, pla_1_pla35, pla_1_pla36,
       pla_1_pla37, pla_1_pla38, pla_1_pla39, pla_1_pla40, pla_1_pla41, pla_1_pla42, pla_1_pla43,
       pla_1_pla44, pla_1_pla45, pla_1_pla46, pla_1_pla47, pla_1_pla48, pla_1_pla49, pla_1_pla50,
       pla_1_pla51, pla_1_pla52, pla_1_pla53, pla_1_pla54, pla_1_pla55, pla_1_pla56, pla_1_pla57,
       pla_1_pla58, pla_1_pla59, pla_1_pla60, pla_1_pla61, pla_1_pla62, pla_1_pla63, pla_1_pla64,
       pla_1_pla65, pla_1_pla66, pla_1_pla67, pla_1_pla68, pla_1_pla69, pla_1_pla70, pla_1_pla71,
       pla_1_pla72, pla_1_pla73, pla_1_pla74, pla_1_pla75, pla_1_pla76, pla_1_pla77, pla_1_pla78,
       pla_1_pla79, pla_1_pla80, pla_1_pla81, pla_1_pla82, pla_1_pla83, pla_1_pla84, pla_1_pla85,
       pla_1_pla86, pla_1_pla87, pla_1_pla88, pla_1_pla89, pla_1_pla90, pla_1_pla91, pla_1_pla92,
       pla_1_pla93, pla_1_pla94, pla_1_pla95, pla_1_pla96, pla_1_pla97, pla_1_pla98, PREF_CLK,
       prefix_1_base_set, prefix_1_cb_set, prefix_1_ed_set, prefix_1_idx_cb_latch, READ_DATA, RES,
       s_r_ff_1_q, SEL_IM1, SEL_IM2, SEL_NMI, SEL_RST_NMI_IM1, state_decode_1_grp_439,
       state_decode_1_grp_488, state_decode_1_grp_flags, state_decode_1_grp_v_if, state_decode_1_req_reg_dst,
       state_decode_1_w148, state_decode_1_w150, state_decode_1_w154, state_decode_1_w156,
       state_decode_1_w160, state_decode_1_w162, state_decode_1_w163, state_decode_1_w165,
       state_decode_1_w166, state_decode_1_w168, state_decode_1_w171, state_decode_1_w174,
       state_decode_1_w175, state_decode_1_w178, state_decode_1_w179, state_decode_1_w180,
       state_decode_1_w181, state_decode_1_w182, state_decode_1_w185, state_decode_1_w188,
       state_decode_1_w189, state_decode_1_w191, state_decode_1_w198, state_decode_1_w199, T1, T2, T3, T4,
       T5, T6, W139, W142, W149, W151, W155, W164, W170, W176, W184, W190, WRITE_DATA;
  wire [7:0] nDBUS, nDLATCH, not_7_out, register_1_q, register_2_q;
  wire [15:0] not_8_out, not_9_out, REG_ADR_q, undriven;

  Clock clock_1 (.out(CLK_t));
  not not_1 (not_1_out, not_2_out);
  not not_2 (not_2_out, CLK_t);
  not not_3 (not_3_out, not_1_out);
  not not_4 (not_4_out, not_3_out);
  not not_5 (nCLK, CLK_t);
  and and_1 (CLK_S, not_4_out, CLK_t);
  PREFIX prefix_1 (
    .CLK(CLK_t), .RES(RES), .T1(T1), .T2(T2), .T3(T3), .M1(M1), .M3(M3), .M4(M4), .GRP_IDX(GRP_IDX),
    .DIS_BASE_SET(DIS_BASE_SET), .PLA47(PLA47), .PLA54(PLA54), .PLA57(PLA57), .PLA76(PLA76),
    .BASE_SET(prefix_1_base_set), .ED_SET(prefix_1_ed_set), .IDX_SET(IDX_SET), .CB_SET(prefix_1_cb_set),
    .PREF_CLK(PREF_CLK), .IDX_CB_LATCH(prefix_1_idx_cb_latch));  // open: SEL_MASK
  SEQUENCER sequencer_1 (
    .CLK(CLK_t), .RES(RES), .BUS_Z(in_3), .INT_ACK(INT_ACK), .DIS_WR_ADR(in_4), .WAIT(nWAIT),
    .COND_DONE(COND_DONE), .IDX_SET(IDX_SET), .GRP_BLOCK(GRP_BLOCK), .GRP_220(GRP_220), .GRP_239(GRP_239),
    .GRP_N8(GRP_N8), .GRP_M_HL(GRP_M_HL), .GRP_IO(GRP_IO), .PLA88(PLA88), .PLA98(PLA98), .w142(W142),
    .w149(W149), .w155(W155), .w164(W164), .w190(W190), .w139(W139), .w151(W151), .M1(M1), .M2(M2), .M3(M3),
    .M4(M4), .M5(M5), .M6(M6), .T1(T1), .T2(T2), .T3(T3), .T4(T4), .T5(T5), .T6(T6), .nRES_MCLK(nRES_MCLK),
    .nRES_TCLK(nRES_TCLK));
  INT_LOGIC int_logic_1 (
    .CLK(CLK_t), .PREF_CLK(PREF_CLK), .RESET(RESET), .INT(INT), .NMI(NMI), .nRES_TCLK(nRES_TCLK),
    .nRES_MCLK(nRES_MCLK), .M1(M1), .T1(T1), .T2(T2), .GRP_PREFIX(GRP_PREFIX), .PLA1(PLA1), .PLA2(PLA2),
    .PLA3(PLA3), .PLA42(PLA42), .PLA52(PLA52), .IA3(IA3), .IA4(IA4), .RES(RES), .RES2(int_logic_1_res2),
    .RESET_PC(int_logic_1_reset_pc), .SEL_RST_NMI_IM1(SEL_RST_NMI_IM1), .SEL_IM1(SEL_IM1), .SEL_IM2(SEL_IM2),
    .SEL_NMI(SEL_NMI), .HALT(HALT), .IFF2(IFF2), .INT_ACK(INT_ACK), .DIS_BASE_SET(DIS_BASE_SET),
    .NMI_ACK(NMI_ACK), .HALT_REQ(HALT_REQ), .INT_CLK(INT_CLK), .INT_REQ(INT_REQ), .NMI_REQ(NMI_REQ));
  PC_CONTROL pc_control_1 (
    .CLK(CLK_t), .RES(RES), .IA3(IA3), .HALT(HALT), .nRES_MCLK(nRES_MCLK), .nRES_TCLK(nRES_TCLK), .M1(M1),
    .M2(M2), .M3(M3), .M4(M4), .M5(M5), .T1(T1), .T2(T2), .T3(T3), .T4(T4), .T5(T5), .W170(W170),
    .W176(W176), .GRP_BLOCK(GRP_BLOCK), .SEL_RST_NMI_IM1(SEL_RST_NMI_IM1), .GRP_LDI_CPI(GRP_LDI_CPI),
    .SEL_IM2(SEL_IM2), .COND_DONE(COND_DONE), .GRP_SP(GRP_SP), .GRP_387(GRP_387), .GRP_220(GRP_220),
    .GRP_M_HL(GRP_M_HL), .GRP_BRANCH(GRP_BRANCH), .GRP_IDX(GRP_IDX), .GRP_N8(GRP_N8), .INT_CLK(INT_CLK),
    .INT_REQ(INT_REQ), .NMI_REQ(NMI_REQ), .HALT_REQ(HALT_REQ), .NMI_ACK(NMI_ACK), .INT_ACK(INT_ACK),
    .PLA88(PLA88), .PLA93(PLA93), .INV_PCR(pc_control_1_inv_pcr), .INC_PCR(pc_control_1_inc_pcr),
    .HI_INC_PCR(pc_control_1_hi_inc_pcr), .R_P(pc_control_1_r_p), .READ_PCR(pc_control_1_read_pcr),
    .WRITE_PCR(pc_control_1_write_pcr));
  nand nand_1 (nand_1_out, T3, M3, prefix_1_idx_cb_latch);
  nand nand_2 (nand_2_out, T2, M1);
  nor nor_1 (nor_1_out, T3, RES);
  D_LATCH d_latch_1 (.EN(CLK_t), .D(nand_1_out), .nQ(d_latch_1_nq));  // open: Q
  D_LATCH d_latch_2 (.EN(CLK_t), .D(nand_2_out), .nQ(d_latch_2_nq));  // open: Q
  not not_6 (not_6_out, CLK_t);
  D_LATCH d_latch_3 (.EN(CLK_t), .D(nor_1_out), .nQ(d_latch_3_nq));  // open: Q
  and and_2 (and_2_out, ~CLK_t, d_latch_1_nq);  // AND_Gate
  S_R_Flip_Flop #(.trigger("high")) s_r_ff_1 (
    .S(d_latch_2_nq), .clk(not_6_out), .R(d_latch_3_nq), .Q(s_r_ff_1_q));  // open: Qn, preset, reset, en
  nor nor_2 (nor_2_out, and_2_out, s_r_ff_1_q);
  assign not_7_out = ~DB;  // NOT_Gate not_7, 8 bits wide
  Register #(.trigger("high")) register_1 (
    .D(not_7_out), .Q({register_1_q[7:6], IA5, IA4, IA3, register_1_q[2:0]}), .clk(nor_2_out));  // open: en, clr
  CONDITION_LOGIC condition_logic_1 (
    .CLK(CLK_t), .M1(M1), .M2(M2), .M3(M3), .PLA5(PLA5), .PLA7(PLA7), .PLA8(PLA8), .PLA50(PLA50),
    .PLA53(PLA53), .W184(W184), .IA4(IA4), .IA5(IA5), .GRP_LDI_CPI(GRP_LDI_CPI), .CONDITION_DONE(COND_DONE));  // open: REG0, F_Z, SEL_ACC, EQUAL0001, LBUS
  REGISTER_CONTROL register_control_1 ();  // open: CLK, RES, M1, M2, M3, M4, M5, M6, T1, T2, T3, T4, T5, T6, IA0, IA1, IA2, IA3, IA4, IA5, W163, W175, W185, W188, W189, W182, W191, W254, IDX_SET, SEL_PCR_DST, SEL_PCR_SRC, REQ_REG_DST, SEL_RST_NMI_IM1, SEL_IM2, SEL_ACC, GRP_M_HL, GRP_A_MEM_IO, GRP_IDX, GRP_220, GRP_387, GRP_488, GRP_BLOCK, GRP_SP, ADD_SUB_HL, R16_TO_DIR, GRP_R16_DIR, GRP_DST_AF, REQ_FLAGS, PLA37, PLA59, PLA66, PLA71, PLA73, PLA75, PLA77, PLA78, PLA80, PLA81, PLA83, PLA88, PLA89, PLA90, PLA91, PLA93, PLA94, PLA95, PLA96, PLA97, SEL_IR, SEL_WZ, SEL_AF, SEL_AF2, SEL_SP, SEL_PC, SEL_BC, SEL_BC2, SEL_DE, SEL_DE2, SEL_HL, SEL_HL2, SEL_IX, SEL_IY, RL_WR, RH_WR, R_L, R_H
  PLA pla_1 (
    .IA0(register_1_q[0]), .IA1(register_1_q[1]), .IA2(register_1_q[2]), .IA3(IA3), .IA4(IA4), .IA5(IA5),
    .IA6(register_1_q[6]), .IA7(register_1_q[7]), .IFF2(IFF2), .BASE_SET(prefix_1_base_set),
    .ED_SET(prefix_1_ed_set), .CB_SET(prefix_1_cb_set), .IDX_SET(IDX_SET), .PLA0(pla_1_pla0),
    .PLA1(pla_1_pla1), .PLA2(pla_1_pla2), .PLA3(pla_1_pla3), .PLA4(pla_1_pla4), .PLA5(pla_1_pla5),
    .PLA6(pla_1_pla6), .PLA7(pla_1_pla7), .PLA8(pla_1_pla8), .PLA9(pla_1_pla9), .PLA10(pla_1_pla10),
    .PLA11(pla_1_pla11), .PLA12(pla_1_pla12), .PLA13(pla_1_pla13), .PLA14(pla_1_pla14), .PLA15(pla_1_pla15),
    .PLA16(pla_1_pla16), .PLA17(pla_1_pla17), .PLA18(pla_1_pla18), .PLA19(pla_1_pla19), .PLA20(pla_1_pla20),
    .PLA21(pla_1_pla21), .PLA22(pla_1_pla22), .PLA23(pla_1_pla23), .PLA24(pla_1_pla24), .PLA25(pla_1_pla25),
    .PLA26(pla_1_pla26), .PLA27(pla_1_pla27), .PLA28(pla_1_pla28), .PLA29(pla_1_pla29), .PLA30(pla_1_pla30),
    .PLA31(pla_1_pla31), .PLA32(pla_1_pla32), .PLA33(pla_1_pla33), .PLA34(pla_1_pla34), .PLA35(pla_1_pla35),
    .PLA36(pla_1_pla36), .PLA37(pla_1_pla37), .PLA38(pla_1_pla38), .PLA39(pla_1_pla39), .PLA40(pla_1_pla40),
    .PLA41(pla_1_pla41), .PLA42(pla_1_pla42), .PLA43(pla_1_pla43), .PLA44(pla_1_pla44), .PLA45(pla_1_pla45),
    .PLA46(pla_1_pla46), .PLA47(pla_1_pla47), .PLA48(pla_1_pla48), .PLA49(pla_1_pla49), .PLA50(pla_1_pla50),
    .PLA51(pla_1_pla51), .PLA52(pla_1_pla52), .PLA53(pla_1_pla53), .PLA54(pla_1_pla54), .PLA55(pla_1_pla55),
    .PLA56(pla_1_pla56), .PLA57(pla_1_pla57), .PLA58(pla_1_pla58), .PLA59(pla_1_pla59), .PLA60(pla_1_pla60),
    .PLA61(pla_1_pla61), .PLA62(pla_1_pla62), .PLA63(pla_1_pla63), .PLA64(pla_1_pla64), .PLA65(pla_1_pla65),
    .PLA66(pla_1_pla66), .PLA67(pla_1_pla67), .PLA68(pla_1_pla68), .PLA69(pla_1_pla69), .PLA70(pla_1_pla70),
    .PLA71(pla_1_pla71), .PLA72(pla_1_pla72), .PLA73(pla_1_pla73), .PLA74(pla_1_pla74), .PLA75(pla_1_pla75),
    .PLA76(pla_1_pla76), .PLA77(pla_1_pla77), .PLA78(pla_1_pla78), .PLA79(pla_1_pla79), .PLA80(pla_1_pla80),
    .PLA81(pla_1_pla81), .PLA82(pla_1_pla82), .PLA83(pla_1_pla83), .PLA84(pla_1_pla84), .PLA85(pla_1_pla85),
    .PLA86(pla_1_pla86), .PLA87(pla_1_pla87), .PLA88(pla_1_pla88), .PLA89(pla_1_pla89), .PLA90(pla_1_pla90),
    .PLA91(pla_1_pla91), .PLA92(pla_1_pla92), .PLA93(pla_1_pla93), .PLA94(pla_1_pla94), .PLA95(pla_1_pla95),
    .PLA96(pla_1_pla96), .PLA97(pla_1_pla97), .PLA98(pla_1_pla98), .PLA98_3(PLA98), .PLA98_2(PLA88),
    .PLA47_2(PLA47), .PLA54_2(PLA54), .PLA57_2(PLA57), .PLA76_2(PLA76), .PLA52_2(PLA52), .PLA1_2(PLA1),
    .PLA2_2(PLA2), .PLA3_2(PLA3), .PLA42_2(PLA42), .PLA93_2(PLA93), .PLA5_2(PLA5), .PLA7_2(PLA7),
    .PLA8_2(PLA8), .PLA53_2(PLA53), .PLA50_2(PLA50));
  STATE_DECODE state_decode_1 (
    .IA3(IA3), .SEL_RST_NMI_IM1(SEL_RST_NMI_IM1), .SEL_IM2(SEL_IM2), .PLA0(pla_1_pla0), .PLA1(pla_1_pla1),
    .PLA2(pla_1_pla2), .PLA3(pla_1_pla3), .PLA4(pla_1_pla4), .PLA5(pla_1_pla5), .PLA6(pla_1_pla6),
    .PLA7(pla_1_pla7), .PLA8(pla_1_pla8), .PLA9(pla_1_pla9), .PLA10(pla_1_pla10), .PLA11(pla_1_pla11),
    .PLA12(pla_1_pla12), .PLA13(pla_1_pla13), .PLA14(pla_1_pla14), .PLA15(pla_1_pla15), .PLA16(pla_1_pla16),
    .PLA17(pla_1_pla17), .PLA18(pla_1_pla18), .PLA19(pla_1_pla19), .PLA20(pla_1_pla20), .PLA21(pla_1_pla21),
    .PLA22(pla_1_pla22), .PLA23(pla_1_pla23), .PLA24(pla_1_pla24), .PLA25(pla_1_pla25), .PLA26(pla_1_pla26),
    .PLA27(pla_1_pla27), .PLA28(pla_1_pla28), .PLA29(pla_1_pla29), .PLA30(pla_1_pla30), .PLA31(pla_1_pla31),
    .PLA32(pla_1_pla32), .PLA33(pla_1_pla33), .PLA34(pla_1_pla34), .PLA35(pla_1_pla35), .PLA36(pla_1_pla36),
    .PLA37(pla_1_pla37), .PLA38(pla_1_pla38), .PLA39(pla_1_pla39), .PLA40(pla_1_pla40), .PLA41(pla_1_pla41),
    .PLA42(pla_1_pla42), .PLA43(pla_1_pla43), .PLA44(pla_1_pla44), .PLA45(pla_1_pla45), .PLA46(pla_1_pla46),
    .PLA47(pla_1_pla47), .PLA48(pla_1_pla48), .PLA49(pla_1_pla49), .PLA50(pla_1_pla50), .PLA51(pla_1_pla51),
    .PLA52(pla_1_pla52), .PLA53(pla_1_pla53), .PLA54(pla_1_pla54), .PLA55(pla_1_pla55), .PLA56(pla_1_pla56),
    .PLA57(pla_1_pla57), .PLA58(pla_1_pla58), .PLA59(pla_1_pla59), .PLA60(pla_1_pla60), .PLA61(pla_1_pla61),
    .PLA62(pla_1_pla62), .PLA63(pla_1_pla63), .PLA64(pla_1_pla64), .PLA65(pla_1_pla65), .PLA66(pla_1_pla66),
    .PLA67(pla_1_pla67), .PLA68(pla_1_pla68), .PLA69(pla_1_pla69), .PLA70(pla_1_pla70), .PLA71(pla_1_pla71),
    .PLA72(pla_1_pla72), .PLA73(pla_1_pla73), .PLA74(pla_1_pla74), .PLA75(pla_1_pla75), .PLA76(pla_1_pla76),
    .PLA77(pla_1_pla77), .PLA78(pla_1_pla78), .PLA79(pla_1_pla79), .PLA80(pla_1_pla80), .PLA81(pla_1_pla81),
    .PLA82(pla_1_pla82), .PLA83(pla_1_pla83), .PLA84(pla_1_pla84), .PLA85(pla_1_pla85), .PLA86(pla_1_pla86),
    .PLA87(pla_1_pla87), .PLA88(pla_1_pla88), .PLA89(pla_1_pla89), .PLA90(pla_1_pla90), .PLA91(pla_1_pla91),
    .PLA92(pla_1_pla92), .PLA93(pla_1_pla93), .PLA94(pla_1_pla94), .PLA95(pla_1_pla95), .PLA96(pla_1_pla96),
    .PLA97(pla_1_pla97), .PLA98(pla_1_pla98), .w171(state_decode_1_w171), .w148(state_decode_1_w148),
    .GRP_V_IF(state_decode_1_grp_v_if), .REQ_REG_DST(state_decode_1_req_reg_dst), .GRP_N8(GRP_N8),
    .w149(W149), .GRP_SP(GRP_SP), .w160(state_decode_1_w160), .w174(state_decode_1_w174),
    .w150(state_decode_1_w150), .w175(state_decode_1_w175), .w176(W176), .GRP_239(GRP_239), .w151(W151),
    .GRP_439(state_decode_1_grp_439), .w178(state_decode_1_w178), .GRP_FLAGS(state_decode_1_grp_flags),
    .w179(state_decode_1_w179), .w162(state_decode_1_w162), .w182(state_decode_1_w182),
    .w163(state_decode_1_w163), .w184(W184), .w185(state_decode_1_w185), .GRP_BRANCH(GRP_BRANCH),
    .GRP_BLOCK(GRP_BLOCK), .w164(W164), .GRP_A_MEM_IO(GRP_A_MEM_IO), .w154(state_decode_1_w154),
    .w188(state_decode_1_w188), .w189(state_decode_1_w189), .w165(state_decode_1_w165), .GRP_DST_AF(W190),
    .w155(W155), .w166(state_decode_1_w166), .w191(state_decode_1_w191), .GRP_LDI_CPI(GRP_LDI_CPI),
    .w199(state_decode_1_w199), .GRP_387(GRP_387), .w156(state_decode_1_w156), .ADD_SUB_HL(ADD_SUB_HL),
    .GRP_R16_DIR(GRP_R16_DIR), .GRP_M_HL(GRP_M_HL), .GRP_SHIFT(GRP_SHIFT), .w170(W170),
    .GRP_PREFIX(GRP_PREFIX), .w139(W139), .GRP_488(state_decode_1_grp_488), .GRP_IO(GRP_IO),
    .w198(state_decode_1_w198), .w180(state_decode_1_w180), .w181(state_decode_1_w181),
    .w168(state_decode_1_w168), .GRP_220(GRP_220), .GRP_IDX(GRP_IDX), .IDX_SET(IDX_SET), .M6(M6), .M4(M4),
    .M3(M3), .M2(M2), .w142(W142));  // open: w254
  assign DB_3 = WRITE_DATA ? ~nDLATCH : 8'bz;  // Controlled_Inverter controlled_inverter_1
  assign nDLATCH = READ_DATA ? ~DB_2 : 8'bz;  // Controlled_Inverter controlled_inverter_2
  Register #(.trigger("high")) register_2 (.D(nDLATCH), .Q(register_2_q));  // open: en, clk, clr
  assign nDBUS = DL_D ? register_2_q : 8'bz;  // Controlled_Buffer controlled_buffer_1
  assign not_8_out = ~undriven;  // NOT_Gate not_8, 16 bits wide
  Register #(.width(16), .trigger("high")) REG_ADR (.D(not_8_out), .Q(REG_ADR_q), .clk(CLK_t));  // open: en, clr
  assign not_9_out = ~REG_ADR_q;  // NOT_Gate not_9, 16 bits wide
  assign {AB15, AB14, AB13, AB12, AB11, AB10, AB9, AB8, AB7, AB6, AB5, AB4, AB3, AB2, AB1, AB0} = ADR_Z ? not_9_out : 16'bz;  // Controlled_Buffer controlled_buffer_2

  // Notes on the sheet:
  //   CLK DELAY
  //   DL17
  //   DL16
  //   DL18
  //   INSTR REG
  //   DATA PORT IN
  //   DATA PORT OUT
  //   REG DATA
endmodule

module D_LATCH (
  input  EN,
  input  D,
  output Q,
  output nQ
);

  D_Flip_Flop #(.trigger("high")) d_ff_1 (.clk(EN), .D(D), .Q(Q), .Qn(nQ));  // open: preset, en, reset
endmodule

// ALU OPS
module ALU_OPS (
  input  DISABLE_CARRY,
  input  FORCE_OR,
  input  DISABLE_XOR,
  input  CIN,
  input  [3:0] O1,
  input  [3:0] O2,
  output [3:0] ALU_COUT,
  output [3:0] ALU_OUT,
  output CARRY_OUT
);

  wire and_1_out, and_2_out, and_3_out, and_4_out, and_5_out, and_6_out, and_7_out, and_8_out, and_9_out,
       and_10_out, and_11_out, and_12_out, and_13_out, and_14_out, and_15_out, and_16_out, and_17_out,
       and_18_out, and_19_out, nor_1_out, nor_2_out, nor_3_out, nor_4_out, or_1_out, or_2_out, or_3_out,
       or_4_out, or_5_out, or_6_out, or_7_out, or_8_out, or_9_out, or_10_out, or_11_out, or_12_out;

  or or_1 (or_1_out, O1[0], O2[0]);
  or or_2 (or_2_out, O1[1], O2[1]);
  or or_3 (or_3_out, O1[2], O2[2]);
  or or_4 (or_4_out, O1[3], O2[3]);
  and and_1 (and_1_out, CIN, O1[0], O2[0]);
  or or_5 (or_5_out, CIN, O1[0], O2[0]);
  and and_2 (and_2_out, CIN, or_1_out);
  and and_3 (and_3_out, O1[0], O2[0]);
  and and_4 (and_4_out, and_17_out, O1[1], O2[1]);
  or or_6 (or_6_out, and_17_out, O1[1], O2[1]);
  and and_5 (and_5_out, and_17_out, or_2_out);
  and and_6 (and_6_out, O1[1], O2[1]);
  and and_7 (and_7_out, and_18_out, O1[2], O2[2]);
  or or_7 (or_7_out, and_18_out, O1[2], O2[2]);
  and and_8 (and_8_out, and_18_out, or_3_out);
  and and_9 (and_9_out, O1[2], O2[2]);
  and and_10 (and_10_out, and_19_out, O1[3], O2[3]);
  or or_8 (or_8_out, and_19_out, O1[3], O2[3]);
  and and_11 (and_11_out, and_19_out, or_4_out);
  and and_12 (and_12_out, O1[3], O2[3]);
  nor nor_1 (nor_1_out, and_2_out, DISABLE_XOR, and_3_out);
  nor nor_2 (nor_2_out, and_5_out, DISABLE_XOR, and_6_out);
  nor nor_3 (nor_3_out, and_8_out, DISABLE_XOR, and_9_out);
  nor nor_4 (nor_4_out, and_11_out, DISABLE_XOR, and_12_out);
  or or_9 (or_9_out, FORCE_OR, nor_1_out);
  or or_10 (or_10_out, FORCE_OR, nor_2_out);
  or or_11 (or_11_out, FORCE_OR, nor_3_out);
  or or_12 (or_12_out, FORCE_OR, nor_4_out);
  and and_13 (and_13_out, or_5_out, or_9_out);
  and and_14 (and_14_out, or_6_out, or_10_out);
  and and_15 (and_15_out, or_7_out, or_11_out);
  and and_16 (and_16_out, or_8_out, or_12_out);
  or or_13 (ALU_OUT[0], and_1_out, and_13_out);
  or or_14 (ALU_OUT[1], and_4_out, and_14_out);
  or or_15 (ALU_OUT[2], and_7_out, and_15_out);
  or or_16 (ALU_OUT[3], and_10_out, and_16_out);
  and and_17 (and_17_out, ~nor_1_out, ~DISABLE_CARRY);  // AND_Gate
  and and_18 (and_18_out, ~nor_2_out, ~DISABLE_CARRY);  // AND_Gate
  and and_19 (and_19_out, ~nor_3_out, ~DISABLE_CARRY);  // AND_Gate
  and and_20 (CARRY_OUT, ~nor_4_out, ~DISABLE_CARRY);  // AND_Gate
endmodule

module PC (
  input  CLK,
  input  RESET_PC,
  output PC_EQUAL_ONE,
  output [15:0] out_4
);

  wire and_1_out, and_17_out, and_18_out, d_latch_1_nq, HI_INC_PCR, INC_PCR, INV_PCR, nor_1_out, not_4_out;
  wire [14:0] multiplexer_1_out, not_1_out, not_2_out;
  wire [15:0] not_3_out, PCR_q, undriven, xnor_1_out;

  // NOR_Gate nor_1 has open pins: out=nor_1_out
  D_LATCH d_latch_1 (.EN(CLK), .D(nor_1_out), .nQ(d_latch_1_nq));  // open: Q
  Register #(.width(16), .trigger("high")) PCR (.D(undriven), .Q(PCR_q), .clk(and_1_out));  // open: en, clr
  and and_1 (and_1_out, ~CLK, d_latch_1_nq);  // AND_Gate
  assign not_1_out = ~PCR_q[14:0];  // NOT_Gate not_1, 15 bits wide
  Multiplexer #(.width(15), .disabled(0), .enable("false")) multiplexer_1 (
    .in0(not_1_out), .in1(PCR_q[14:0]), .out(multiplexer_1_out), .sel(INV_PCR));
  assign not_2_out = ~multiplexer_1_out;  // NOT_Gate not_2, 15 bits wide
  not not_3 (not_3_out[0], INC_PCR);
  not not_4 (not_4_out, HI_INC_PCR);
  and and_2 (not_3_out[1], not_3_out[0], not_2_out[0]);
  and and_3 (not_3_out[2], not_3_out[0], not_2_out[0], not_2_out[1]);
  and and_4 (not_3_out[3], not_3_out[2], not_2_out[2]);
  and and_5 (not_3_out[4], not_3_out[2], not_2_out[2], not_2_out[3]);
  and and_6 (not_3_out[5], not_3_out[4], not_2_out[4]);
  and and_7 (not_3_out[6], not_3_out[4], not_2_out[4], not_2_out[5]);
  and and_8 (not_3_out[8], not_3_out[7], not_2_out[7]);
  and and_9 (not_3_out[9], not_3_out[7], not_2_out[7], not_2_out[8]);
  and and_10 (not_3_out[10], not_3_out[9], not_2_out[9]);
  and and_11 (not_3_out[11], not_3_out[9], not_2_out[9], not_2_out[10]);
  and and_12 (not_3_out[13], not_3_out[12], not_2_out[12]);
  and and_13 (not_3_out[14], not_3_out[12], not_2_out[12], not_2_out[13]);
  and and_14 (not_3_out[7], not_4_out, not_3_out[0], not_2_out[0], not_2_out[1], not_2_out[2], not_2_out[3], not_2_out[4], not_2_out[5], not_2_out[6]);
  and and_15 (not_3_out[12], not_3_out[7], not_2_out[7], not_2_out[8], not_2_out[9], not_2_out[10], not_2_out[11]);
  and and_16 (not_3_out[15], not_3_out[12], not_2_out[12], not_2_out[13], not_2_out[14]);
  assign xnor_1_out = ~(PCR_q ^ not_3_out);  // XNOR_Gate xnor_1, 16 bits wide
  Register #(.width(16), .trigger("high")) PCR2 (.D(xnor_1_out), .Q(out_4), .clk(CLK), .clr(RESET_PC));  // open: en
  and and_17 (and_17_out, CLK, INV_PCR);
  and and_18 (and_18_out, ~PCR_q[0], PCR_q[1], PCR_q[2], PCR_q[3], PCR_q[4], PCR_q[5], PCR_q[6], PCR_q[7], PCR_q[8], PCR_q[9], PCR_q[10], PCR_q[11], PCR_q[12], PCR_q[13], PCR_q[14], PCR_q[15]);  // AND_Gate
  D_LATCH d_latch_2 (.EN(and_17_out), .D(and_18_out), .Q(PC_EQUAL_ONE));  // open: nQ
  Bit_Extender #(.in_width(1), .\type ("sign")) bit_extender_1 ();  // open: in, out

  // Notes on the sheet:
  //   W293
  //   PCI
  //   PCR
  //   EQUAL ONE
endmodule

module PLA (
  input  IA0,
  input  IA1,
  input  IA2,
  input  IA3,
  input  IA4,
  input  IA5,
  input  IA6,
  input  IA7,
  input  IFF2,
  input  BASE_SET,
  input  ED_SET,
  input  CB_SET,
  input  IDX_SET,
  output PLA0,
  output PLA1,
  output PLA2,
  output PLA3,
  output PLA4,
  output PLA5,
  output PLA6,
  output PLA7,
  output PLA8,
  output PLA9,
  output PLA10,
  output PLA11,
  output PLA12,
  output PLA13,
  output PLA14,
  output PLA15,
  output PLA16,
  output PLA17,
  output PLA18,
  output PLA19,
  output PLA20,
  output PLA21,
  output PLA22,
  output PLA23,
  output PLA24,
  output PLA25,
  output PLA26,
  output PLA27,
  output PLA28,
  output PLA29,
  output PLA30,
  output PLA31,
  output PLA32,
  output PLA33,
  output PLA34,
  output PLA35,
  output PLA36,
  output PLA37,
  output PLA38,
  output PLA39,
  output PLA40,
  output PLA41,
  output PLA42,
  output PLA43,
  output PLA44,
  output PLA45,
  output PLA46,
  output PLA47,
  output PLA48,
  output PLA49,
  output PLA50,
  output PLA51,
  output PLA52,
  output PLA53,
  output PLA54,
  output PLA55,
  output PLA56,
  output PLA57,
  output PLA58,
  output PLA59,
  output PLA60,
  output PLA61,
  output PLA62,
  output PLA63,
  output PLA64,
  output PLA65,
  output PLA66,
  output PLA67,
  output PLA68,
  output PLA69,
  output PLA70,
  output PLA71,
  output PLA72,
  output PLA73,
  output PLA74,
  output PLA75,
  output PLA76,
  output PLA77,
  output PLA78,
  output PLA79,
  output PLA80,
  output PLA81,
  output PLA82,
  output PLA83,
  output PLA84,
  output PLA85,
  output PLA86,
  output PLA87,
  output PLA88,
  output PLA89,
  output PLA90,
  output PLA91,
  output PLA92,
  output PLA93,
  output PLA94,
  output PLA95,
  output PLA96,
  output PLA97,
  output PLA98,
  output PLA1_2,
  output PLA2_2,
  output PLA3_2,
  output PLA5_2,
  output PLA7_2,
  output PLA8_2,
  output PLA42_2,
  output PLA47_2,
  output PLA50_2,
  output PLA52_2,
  output PLA53_2,
  output PLA54_2,
  output PLA57_2,
  output PLA76_2,
  output PLA98_2,
  output PLA93_2,
  output PLA98_3
);

  wire nor_1_out, not_1_out, not_2_out, not_3_out, not_4_out, not_5_out, not_6_out, not_7_out, not_8_out,
       not_9_out, not_10_out, not_11_out, not_12_out;

  not not_1 (not_1_out, IA0);
  not not_2 (not_2_out, IA1);
  not not_3 (not_3_out, IA2);
  not not_4 (not_4_out, IA3);
  not not_5 (not_5_out, IA4);
  not not_6 (not_6_out, IA5);
  not not_7 (not_7_out, IA6);
  not not_8 (not_8_out, IA7);
  not not_9 (not_9_out, IFF2);
  not not_10 (not_10_out, BASE_SET);
  not not_11 (not_11_out, ED_SET);
  Pull_Resistor #(.pull(1)) pull_resistor_1 (.node(PLA0));
  Pull_Resistor #(.pull(1)) pull_resistor_2 (.node(PLA1));
  Transistor #(.\type ("n")) transistor_1 (.in(1'b0), .out(PLA1), .gate(not_1_out));
  Transistor #(.\type ("n")) transistor_2 (.in(1'b0), .out(PLA0), .gate(not_1_out));
  Transistor #(.\type ("n")) transistor_3 (.in(1'b0), .out(PLA0), .gate(not_2_out));
  Transistor #(.\type ("n")) transistor_4 (.in(1'b0), .out(PLA1), .gate(not_2_out));
  Transistor #(.\type ("n")) transistor_5 (.in(1'b0), .out(PLA1), .gate(IA2));
  Transistor #(.\type ("n")) transistor_6 (.in(1'b0), .out(PLA0), .gate(IA2));
  Transistor #(.\type ("n")) transistor_7 (.in(1'b0), .out(PLA0), .gate(not_5_out));
  Transistor #(.\type ("n")) transistor_8 (.in(1'b0), .out(PLA1), .gate(not_5_out));
  Transistor #(.\type ("n")) transistor_9 (.in(1'b0), .out(PLA0), .gate(IA5));
  Transistor #(.\type ("n")) transistor_10 (.in(1'b0), .out(PLA1), .gate(not_6_out));
  Transistor #(.\type ("n")) transistor_11 (.in(1'b0), .out(PLA0), .gate(not_7_out));
  Transistor #(.\type ("n")) transistor_12 (.in(1'b0), .out(PLA1), .gate(not_7_out));
  Transistor #(.\type ("n")) transistor_13 (.in(1'b0), .out(PLA0), .gate(not_8_out));
  Transistor #(.\type ("n")) transistor_14 (.in(1'b0), .out(PLA1), .gate(not_8_out));
  Transistor #(.\type ("n")) transistor_15 (.in(1'b0), .out(PLA0), .gate(not_10_out));
  Transistor #(.\type ("n")) transistor_16 (.in(1'b0), .out(PLA1), .gate(not_10_out));
  Pull_Resistor #(.pull(1)) pull_resistor_3 (.node(PLA2));
  Transistor #(.\type ("n")) transistor_17 (.in(1'b0), .out(PLA2), .gate(IA0));
  Transistor #(.\type ("n")) transistor_18 (.in(1'b0), .out(PLA2), .gate(not_2_out));
  Transistor #(.\type ("n")) transistor_19 (.in(1'b0), .out(PLA2), .gate(not_3_out));
  Transistor #(.\type ("n")) transistor_20 (.in(1'b0), .out(PLA2), .gate(not_7_out));
  Transistor #(.\type ("n")) transistor_21 (.in(1'b0), .out(PLA2), .gate(IA7));
  Transistor #(.\type ("n")) transistor_22 (.in(1'b0), .out(PLA2), .gate(not_11_out));
  Pull_Resistor #(.pull(1)) pull_resistor_4 (.node(PLA3));
  Transistor #(.\type ("n")) transistor_23 (.in(1'b0), .out(PLA3), .gate(IA0));
  Transistor #(.\type ("n")) transistor_24 (.in(1'b0), .out(PLA3), .gate(not_2_out));
  Transistor #(.\type ("n")) transistor_25 (.in(1'b0), .out(PLA3), .gate(not_3_out));
  Transistor #(.\type ("n")) transistor_26 (.in(1'b0), .out(PLA3), .gate(IA3));
  Transistor #(.\type ("n")) transistor_27 (.in(1'b0), .out(PLA3), .gate(not_5_out));
  Transistor #(.\type ("n")) transistor_28 (.in(1'b0), .out(PLA3), .gate(not_6_out));
  Transistor #(.\type ("n")) transistor_29 (.in(1'b0), .out(PLA3), .gate(not_7_out));
  Transistor #(.\type ("n")) transistor_30 (.in(1'b0), .out(PLA3), .gate(IA7));
  Transistor #(.\type ("n")) transistor_31 (.in(1'b0), .out(PLA3), .gate(not_10_out));
  not not_12 (not_12_out, PLA3);
  Pull_Resistor #(.pull(1)) pull_resistor_5 (.node(PLA5));
  Pull_Resistor #(.pull(1)) pull_resistor_6 (.node(PLA4));
  Transistor #(.\type ("n")) transistor_32 (.in(1'b0), .out(PLA4), .gate(IA0));
  Transistor #(.\type ("n")) transistor_33 (.in(1'b0), .out(PLA5), .gate(not_1_out));
  Transistor #(.\type ("n")) transistor_34 (.in(1'b0), .out(PLA5), .gate(IA1));
  Transistor #(.\type ("n")) transistor_35 (.in(1'b0), .out(PLA4), .gate(IA1));
  Transistor #(.\type ("n")) transistor_36 (.in(1'b0), .out(PLA5), .gate(IA2));
  Transistor #(.\type ("n")) transistor_37 (.in(1'b0), .out(PLA4), .gate(IA2));
  Transistor #(.\type ("n")) transistor_38 (.in(1'b0), .out(PLA5), .gate(not_6_out));
  Transistor #(.\type ("n")) transistor_39 (.in(1'b0), .out(PLA4), .gate(not_6_out));
  Transistor #(.\type ("n")) transistor_40 (.in(1'b0), .out(PLA5), .gate(IA6));
  Transistor #(.\type ("n")) transistor_41 (.in(1'b0), .out(PLA4), .gate(IA6));
  Transistor #(.\type ("n")) transistor_42 (.in(1'b0), .out(PLA4), .gate(not_8_out));
  Transistor #(.\type ("n")) transistor_43 (.in(1'b0), .out(PLA5), .gate(not_8_out));
  Transistor #(.\type ("n")) transistor_44 (.in(1'b0), .out(PLA4), .gate(not_11_out));
  Transistor #(.\type ("n")) transistor_45 (.in(1'b0), .out(PLA5), .gate(not_11_out));
  Pull_Resistor #(.pull(1)) pull_resistor_7 (.node(PLA6));
  Transistor #(.\type ("n")) transistor_46 (.in(1'b0), .out(PLA6), .gate(not_1_out));
  Transistor #(.\type ("n")) transistor_47 (.in(1'b0), .out(PLA6), .gate(not_2_out));
  Transistor #(.\type ("n")) transistor_48 (.in(1'b0), .out(PLA6), .gate(not_3_out));
  Transistor #(.\type ("n")) transistor_49 (.in(1'b0), .out(PLA6), .gate(IA3));
  Transistor #(.\type ("n")) transistor_50 (.in(1'b0), .out(PLA6), .gate(not_5_out));
  Transistor #(.\type ("n")) transistor_51 (.in(1'b0), .out(PLA6), .gate(not_6_out));
  Transistor #(.\type ("n")) transistor_52 (.in(1'b0), .out(PLA6), .gate(IA6));
  Transistor #(.\type ("n")) transistor_53 (.in(1'b0), .out(PLA6), .gate(IA7));
  Transistor #(.\type ("n")) transistor_54 (.in(1'b0), .out(PLA6), .gate(not_10_out));
  Pull_Resistor #(.pull(1)) pull_resistor_8 (.node(PLA7));
  Transistor #(.\type ("n")) transistor_55 (.in(1'b0), .out(PLA7), .gate(not_2_out));
  Transistor #(.\type ("n")) transistor_56 (.in(1'b0), .out(PLA7), .gate(IA2));
  Transistor #(.\type ("n")) transistor_57 (.in(1'b0), .out(PLA7), .gate(not_6_out));
  Transistor #(.\type ("n")) transistor_58 (.in(1'b0), .out(PLA7), .gate(IA6));
  Transistor #(.\type ("n")) transistor_59 (.in(1'b0), .out(PLA7), .gate(not_8_out));
  Transistor #(.\type ("n")) transistor_60 (.in(1'b0), .out(PLA7), .gate(not_11_out));
  Pull_Resistor #(.pull(1)) pull_resistor_9 (.node(PLA9));
  Pull_Resistor #(.pull(1)) pull_resistor_10 (.node(PLA8));
  Transistor #(.\type ("n")) transistor_61 (.in(1'b0), .out(PLA8), .gate(IA0));
  Transistor #(.\type ("n")) transistor_62 (.in(1'b0), .out(PLA9), .gate(not_1_out));
  Transistor #(.\type ("n")) transistor_63 (.in(1'b0), .out(PLA8), .gate(IA1));
  Transistor #(.\type ("n")) transistor_64 (.in(1'b0), .out(PLA9), .gate(not_2_out));
  Transistor #(.\type ("n")) transistor_65 (.in(1'b0), .out(PLA8), .gate(IA2));
  Transistor #(.\type ("n")) transistor_66 (.in(1'b0), .out(PLA9), .gate(not_3_out));
  Transistor #(.\type ("n")) transistor_67 (.in(1'b0), .out(PLA8), .gate(IA3));
  Transistor #(.\type ("n")) transistor_68 (.in(1'b0), .out(PLA9), .gate(not_4_out));
  Transistor #(.\type ("n")) transistor_69 (.in(1'b0), .out(PLA9), .gate(not_5_out));
  Transistor #(.\type ("n")) transistor_70 (.in(1'b0), .out(PLA8), .gate(not_5_out));
  Transistor #(.\type ("n")) transistor_71 (.in(1'b0), .out(PLA8), .gate(IA5));
  Transistor #(.\type ("n")) transistor_72 (.in(1'b0), .out(PLA9), .gate(not_6_out));
  Transistor #(.\type ("n")) transistor_73 (.in(1'b0), .out(PLA9), .gate(IA6));
  Transistor #(.\type ("n")) transistor_74 (.in(1'b0), .out(PLA8), .gate(IA6));
  Transistor #(.\type ("n")) transistor_75 (.in(1'b0), .out(PLA8), .gate(IA7));
  Transistor #(.\type ("n")) transistor_76 (.in(1'b0), .out(PLA9), .gate(IA7));
  Transistor #(.\type ("n")) transistor_77 (.in(1'b0), .out(PLA8), .gate(not_10_out));
  Transistor #(.\type ("n")) transistor_78 (.in(1'b0), .out(PLA9), .gate(not_10_out));
  Pull_Resistor #(.pull(1)) pull_resistor_11 (.node(PLA10));
  Transistor #(.\type ("n")) transistor_79 (.in(1'b0), .out(PLA10), .gate(not_4_out));
  Transistor #(.\type ("n")) transistor_80 (.in(1'b0), .out(PLA10), .gate(IA4));
  Transistor #(.\type ("n")) transistor_81 (.in(1'b0), .out(PLA10), .gate(not_6_out));
  Transistor #(.\type ("n")) transistor_82 (.in(1'b0), .out(PLA10), .gate(nor_1_out));
  Pull_Resistor #(.pull(1)) pull_resistor_12 (.node(PLA11));
  Transistor #(.\type ("n")) transistor_83 (.in(1'b0), .out(PLA11), .gate(not_1_out));
  Transistor #(.\type ("n")) transistor_84 (.in(1'b0), .out(PLA11), .gate(not_2_out));
  Transistor #(.\type ("n")) transistor_85 (.in(1'b0), .out(PLA11), .gate(not_3_out));
  Transistor #(.\type ("n")) transistor_86 (.in(1'b0), .out(PLA11), .gate(not_5_out));
  Transistor #(.\type ("n")) transistor_87 (.in(1'b0), .out(PLA11), .gate(IA5));
  Transistor #(.\type ("n")) transistor_88 (.in(1'b0), .out(PLA11), .gate(not_7_out));
  Transistor #(.\type ("n")) transistor_89 (.in(1'b0), .out(PLA11), .gate(IA7));
  Transistor #(.\type ("n")) transistor_90 (.in(1'b0), .out(PLA11), .gate(not_11_out));
  Pull_Resistor #(.pull(1)) pull_resistor_13 (.node(PLA13));
  Pull_Resistor #(.pull(1)) pull_resistor_14 (.node(PLA12));
  Transistor #(.\type ("n")) transistor_91 (.in(1'b0), .out(PLA12), .gate(IA3));
  Transistor #(.\type ("n")) transistor_92 (.in(1'b0), .out(PLA13), .gate(IA3));
  Transistor #(.\type ("n")) transistor_93 (.in(1'b0), .out(PLA13), .gate(IA4));
  Transistor #(.\type ("n")) transistor_94 (.in(1'b0), .out(PLA12), .gate(not_5_out));
  Transistor #(.\type ("n")) transistor_95 (.in(1'b0), .out(PLA13), .gate(not_6_out));
  Transistor #(.\type ("n")) transistor_96 (.in(1'b0), .out(PLA12), .gate(not_6_out));
  Transistor #(.\type ("n")) transistor_97 (.in(1'b0), .out(PLA13), .gate(nor_1_out));
  Transistor #(.\type ("n")) transistor_98 (.in(1'b0), .out(PLA12), .gate(nor_1_out));
  Pull_Resistor #(.pull(1)) pull_resistor_15 (.node(PLA14));
  Transistor #(.\type ("n")) transistor_99 (.in(1'b0), .out(PLA14), .gate(IA3));
  Transistor #(.\type ("n")) transistor_100 (.in(1'b0), .out(PLA14), .gate(IA4));
  Transistor #(.\type ("n")) transistor_101 (.in(1'b0), .out(PLA14), .gate(IA5));
  Transistor #(.\type ("n")) transistor_102 (.in(1'b0), .out(PLA14), .gate(nor_1_out));
  Pull_Resistor #(.pull(1)) pull_resistor_16 (.node(PLA15));
  Transistor #(.\type ("n")) transistor_103 (.in(1'b0), .out(PLA15), .gate(not_1_out));
  Transistor #(.\type ("n")) transistor_104 (.in(1'b0), .out(PLA15), .gate(not_2_out));
  Transistor #(.\type ("n")) transistor_105 (.in(1'b0), .out(PLA15), .gate(not_3_out));
  Transistor #(.\type ("n")) transistor_106 (.in(1'b0), .out(PLA15), .gate(not_5_out));
  Transistor #(.\type ("n")) transistor_107 (.in(1'b0), .out(PLA15), .gate(IA5));
  Transistor #(.\type ("n")) transistor_108 (.in(1'b0), .out(PLA15), .gate(not_7_out));
  Transistor #(.\type ("n")) transistor_109 (.in(1'b0), .out(PLA15), .gate(IA7));
  Transistor #(.\type ("n")) transistor_110 (.in(1'b0), .out(PLA15), .gate(not_9_out));
  Transistor #(.\type ("n")) transistor_111 (.in(1'b0), .out(PLA15), .gate(not_11_out));
  Pull_Resistor #(.pull(1)) pull_resistor_17 (.node(PLA17));
  Pull_Resistor #(.pull(1)) pull_resistor_18 (.node(PLA16));
  Transistor #(.\type ("n")) transistor_112 (.in(1'b0), .out(PLA16), .gate(IA0));
  Transistor #(.\type ("n")) transistor_113 (.in(1'b0), .out(PLA17), .gate(not_1_out));
  Transistor #(.\type ("n")) transistor_114 (.in(1'b0), .out(PLA16), .gate(IA1));
  Transistor #(.\type ("n")) transistor_115 (.in(1'b0), .out(PLA17), .gate(not_2_out));
  Transistor #(.\type ("n")) transistor_116 (.in(1'b0), .out(PLA17), .gate(not_3_out));
  Transistor #(.\type ("n")) transistor_117 (.in(1'b0), .out(PLA16), .gate(not_3_out));
  Transistor #(.\type ("n")) transistor_118 (.in(1'b0), .out(PLA17), .gate(not_4_out));
  Transistor #(.\type ("n")) transistor_119 (.in(1'b0), .out(PLA17), .gate(IA4));
  Transistor #(.\type ("n")) transistor_120 (.in(1'b0), .out(PLA17), .gate(not_6_out));
  Transistor #(.\type ("n")) transistor_121 (.in(1'b0), .out(PLA17), .gate(IA6));
  Transistor #(.\type ("n")) transistor_122 (.in(1'b0), .out(PLA16), .gate(not_7_out));
  Transistor #(.\type ("n")) transistor_123 (.in(1'b0), .out(PLA16), .gate(IA7));
  Transistor #(.\type ("n")) transistor_124 (.in(1'b0), .out(PLA17), .gate(IA7));
  Transistor #(.\type ("n")) transistor_125 (.in(1'b0), .out(PLA17), .gate(not_10_out));
  Transistor #(.\type ("n")) transistor_126 (.in(1'b0), .out(PLA16), .gate(not_11_out));
  Pull_Resistor #(.pull(1)) pull_resistor_19 (.node(PLA18));
  Transistor #(.\type ("n")) transistor_127 (.in(1'b0), .out(PLA18), .gate(not_4_out));
  Transistor #(.\type ("n")) transistor_128 (.in(1'b0), .out(PLA18), .gate(IA4));
  Transistor #(.\type ("n")) transistor_129 (.in(1'b0), .out(PLA18), .gate(IA5));
  Transistor #(.\type ("n")) transistor_130 (.in(1'b0), .out(PLA18), .gate(nor_1_out));
  Pull_Resistor #(.pull(1)) pull_resistor_20 (.node(PLA19));
  Transistor #(.\type ("n")) transistor_131 (.in(1'b0), .out(PLA19), .gate(not_4_out));
  Transistor #(.\type ("n")) transistor_132 (.in(1'b0), .out(PLA19), .gate(not_5_out));
  Transistor #(.\type ("n")) transistor_133 (.in(1'b0), .out(PLA19), .gate(IA5));
  Transistor #(.\type ("n")) transistor_134 (.in(1'b0), .out(PLA19), .gate(nor_1_out));
  Pull_Resistor #(.pull(1)) pull_resistor_21 (.node(PLA20));
  Pull_Resistor #(.pull(1)) pull_resistor_22 (.node(PLA21));
  Transistor #(.\type ("n")) transistor_135 (.in(1'b0), .out(PLA21), .gate(not_1_out));
  Transistor #(.\type ("n")) transistor_136 (.in(1'b0), .out(PLA21), .gate(not_2_out));
  Transistor #(.\type ("n")) transistor_137 (.in(1'b0), .out(PLA21), .gate(not_3_out));
  Transistor #(.\type ("n")) transistor_138 (.in(1'b0), .out(PLA21), .gate(IA3));
  Transistor #(.\type ("n")) transistor_139 (.in(1'b0), .out(PLA20), .gate(IA3));
  Transistor #(.\type ("n")) transistor_140 (.in(1'b0), .out(PLA21), .gate(IA4));
  Transistor #(.\type ("n")) transistor_141 (.in(1'b0), .out(PLA20), .gate(not_5_out));
  Transistor #(.\type ("n")) transistor_142 (.in(1'b0), .out(PLA20), .gate(IA5));
  Transistor #(.\type ("n")) transistor_143 (.in(1'b0), .out(PLA21), .gate(not_6_out));
  Transistor #(.\type ("n")) transistor_144 (.in(1'b0), .out(PLA21), .gate(IA6));
  Transistor #(.\type ("n")) transistor_145 (.in(1'b0), .out(PLA21), .gate(IA7));
  Transistor #(.\type ("n")) transistor_146 (.in(1'b0), .out(PLA20), .gate(nor_1_out));
  Transistor #(.\type ("n")) transistor_147 (.in(1'b0), .out(PLA21), .gate(not_10_out));
  Pull_Resistor #(.pull(1)) pull_resistor_23 (.node(PLA22));
  Transistor #(.\type ("n")) transistor_148 (.in(1'b0), .out(PLA22), .gate(not_4_out));
  Transistor #(.\type ("n")) transistor_149 (.in(1'b0), .out(PLA22), .gate(not_5_out));
  Transistor #(.\type ("n")) transistor_150 (.in(1'b0), .out(PLA22), .gate(not_6_out));
  Transistor #(.\type ("n")) transistor_151 (.in(1'b0), .out(PLA22), .gate(nor_1_out));
  Pull_Resistor #(.pull(1)) pull_resistor_24 (.node(PLA23));
  Transistor #(.\type ("n")) transistor_152 (.in(1'b0), .out(PLA23), .gate(not_1_out));
  Transistor #(.\type ("n")) transistor_153 (.in(1'b0), .out(PLA23), .gate(IA1));
  Transistor #(.\type ("n")) transistor_154 (.in(1'b0), .out(PLA23), .gate(not_3_out));
  Transistor #(.\type ("n")) transistor_155 (.in(1'b0), .out(PLA23), .gate(IA6));
  Transistor #(.\type ("n")) transistor_156 (.in(1'b0), .out(PLA23), .gate(IA7));
  Transistor #(.\type ("n")) transistor_157 (.in(1'b0), .out(PLA23), .gate(not_10_out));
  Pull_Resistor #(.pull(1)) pull_resistor_25 (.node(PLA25));
  Pull_Resistor #(.pull(1)) pull_resistor_26 (.node(PLA24));
  Transistor #(.\type ("n")) transistor_158 (.in(1'b0), .out(PLA25), .gate(IA6));
  Transistor #(.\type ("n")) transistor_159 (.in(1'b0), .out(PLA24), .gate(not_7_out));
  Transistor #(.\type ("n")) transistor_160 (.in(1'b0), .out(PLA25), .gate(not_8_out));
  Transistor #(.\type ("n")) transistor_161 (.in(1'b0), .out(PLA24), .gate(not_8_out));
  Transistor #(.\type ("n")) transistor_162 (.in(1'b0), .out(PLA24), .gate(CB_SET));
  Transistor #(.\type ("n")) transistor_163 (.in(1'b0), .out(PLA25), .gate(CB_SET));
  Pull_Resistor #(.pull(1)) pull_resistor_27 (.node(PLA26));
  Transistor #(.\type ("n")) transistor_164 (.in(1'b0), .out(PLA26), .gate(not_7_out));
  Transistor #(.\type ("n")) transistor_165 (.in(1'b0), .out(PLA26), .gate(IA7));
  Transistor #(.\type ("n")) transistor_166 (.in(1'b0), .out(PLA26), .gate(CB_SET));
  Pull_Resistor #(.pull(1)) pull_resistor_28 (.node(PLA27));
  Transistor #(.\type ("n")) transistor_167 (.in(1'b0), .out(PLA27), .gate(not_1_out));
  Transistor #(.\type ("n")) transistor_168 (.in(1'b0), .out(PLA27), .gate(not_2_out));
  Transistor #(.\type ("n")) transistor_169 (.in(1'b0), .out(PLA27), .gate(not_3_out));
  Transistor #(.\type ("n")) transistor_170 (.in(1'b0), .out(PLA27), .gate(IA5));
  Transistor #(.\type ("n")) transistor_171 (.in(1'b0), .out(PLA27), .gate(IA6));
  Transistor #(.\type ("n")) transistor_172 (.in(1'b0), .out(PLA27), .gate(IA7));
  Transistor #(.\type ("n")) transistor_173 (.in(1'b0), .out(PLA27), .gate(not_10_out));
  Pull_Resistor #(.pull(1)) pull_resistor_29 (.node(PLA29));
  Pull_Resistor #(.pull(1)) pull_resistor_30 (.node(PLA28));
  Transistor #(.\type ("n")) transistor_174 (.in(1'b0), .out(PLA29), .gate(not_1_out));
  Transistor #(.\type ("n")) transistor_175 (.in(1'b0), .out(PLA29), .gate(IA1));
  Transistor #(.\type ("n")) transistor_176 (.in(1'b0), .out(PLA29), .gate(IA2));
  Transistor #(.\type ("n")) transistor_177 (.in(1'b0), .out(PLA29), .gate(not_4_out));
  Transistor #(.\type ("n")) transistor_178 (.in(1'b0), .out(PLA29), .gate(IA6));
  Transistor #(.\type ("n")) transistor_179 (.in(1'b0), .out(PLA28), .gate(IA6));
  Transistor #(.\type ("n")) transistor_180 (.in(1'b0), .out(PLA29), .gate(IA7));
  Transistor #(.\type ("n")) transistor_181 (.in(1'b0), .out(PLA28), .gate(IA7));
  Transistor #(.\type ("n")) transistor_182 (.in(1'b0), .out(PLA29), .gate(not_10_out));
  Transistor #(.\type ("n")) transistor_183 (.in(1'b0), .out(PLA28), .gate(CB_SET));
  Pull_Resistor #(.pull(1)) pull_resistor_31 (.node(PLA30));
  Transistor #(.\type ("n")) transistor_184 (.in(1'b0), .out(PLA30), .gate(IA0));
  Transistor #(.\type ("n")) transistor_185 (.in(1'b0), .out(PLA30), .gate(not_2_out));
  Transistor #(.\type ("n")) transistor_186 (.in(1'b0), .out(PLA30), .gate(IA2));
  Transistor #(.\type ("n")) transistor_187 (.in(1'b0), .out(PLA30), .gate(not_7_out));
  Transistor #(.\type ("n")) transistor_188 (.in(1'b0), .out(PLA30), .gate(IA7));
  Transistor #(.\type ("n")) transistor_189 (.in(1'b0), .out(PLA30), .gate(not_11_out));
  Pull_Resistor #(.pull(1)) pull_resistor_32 (.node(PLA31));
  Transistor #(.\type ("n")) transistor_190 (.in(1'b0), .out(PLA31), .gate(IA0));
  Transistor #(.\type ("n")) transistor_191 (.in(1'b0), .out(PLA31), .gate(IA1));
  Transistor #(.\type ("n")) transistor_192 (.in(1'b0), .out(PLA31), .gate(IA2));
  Transistor #(.\type ("n")) transistor_193 (.in(1'b0), .out(PLA31), .gate(not_7_out));
  Transistor #(.\type ("n")) transistor_194 (.in(1'b0), .out(PLA31), .gate(IA7));
  Transistor #(.\type ("n")) transistor_195 (.in(1'b0), .out(PLA31), .gate(not_11_out));
  Pull_Resistor #(.pull(1)) pull_resistor_33 (.node(PLA33));
  Pull_Resistor #(.pull(1)) pull_resistor_34 (.node(PLA32));
  Transistor #(.\type ("n")) transistor_196 (.in(1'b0), .out(PLA32), .gate(IA1));
  Transistor #(.\type ("n")) transistor_197 (.in(1'b0), .out(PLA32), .gate(not_3_out));
  Transistor #(.\type ("n")) transistor_198 (.in(1'b0), .out(PLA33), .gate(IA6));
  Transistor #(.\type ("n")) transistor_199 (.in(1'b0), .out(PLA32), .gate(IA6));
  Transistor #(.\type ("n")) transistor_200 (.in(1'b0), .out(PLA32), .gate(IA7));
  Transistor #(.\type ("n")) transistor_201 (.in(1'b0), .out(PLA33), .gate(not_8_out));
  Transistor #(.\type ("n")) transistor_202 (.in(1'b0), .out(PLA33), .gate(not_10_out));
  Transistor #(.\type ("n")) transistor_203 (.in(1'b0), .out(PLA32), .gate(not_10_out));
  nor nor_1 (nor_1_out, PLA33, PLA34);
  Pull_Resistor #(.pull(1)) pull_resistor_35 (.node(PLA34));
  Transistor #(.\type ("n")) transistor_204 (.in(1'b0), .out(PLA34), .gate(IA0));
  Transistor #(.\type ("n")) transistor_205 (.in(1'b0), .out(PLA34), .gate(not_2_out));
  Transistor #(.\type ("n")) transistor_206 (.in(1'b0), .out(PLA34), .gate(not_3_out));
  Transistor #(.\type ("n")) transistor_207 (.in(1'b0), .out(PLA34), .gate(not_7_out));
  Transistor #(.\type ("n")) transistor_208 (.in(1'b0), .out(PLA34), .gate(not_8_out));
  Transistor #(.\type ("n")) transistor_209 (.in(1'b0), .out(PLA34), .gate(not_10_out));
  Pull_Resistor #(.pull(1)) pull_resistor_36 (.node(PLA35));
  Transistor #(.\type ("n")) transistor_210 (.in(1'b0), .out(PLA35), .gate(IA0));
  Transistor #(.\type ("n")) transistor_211 (.in(1'b0), .out(PLA35), .gate(not_2_out));
  Transistor #(.\type ("n")) transistor_212 (.in(1'b0), .out(PLA35), .gate(not_3_out));
  Transistor #(.\type ("n")) transistor_213 (.in(1'b0), .out(PLA35), .gate(IA6));
  Transistor #(.\type ("n")) transistor_214 (.in(1'b0), .out(PLA35), .gate(IA7));
  Transistor #(.\type ("n")) transistor_215 (.in(1'b0), .out(PLA35), .gate(not_10_out));
  Pull_Resistor #(.pull(1)) pull_resistor_37 (.node(PLA37));
  Pull_Resistor #(.pull(1)) pull_resistor_38 (.node(PLA36));
  Transistor #(.\type ("n")) transistor_216 (.in(1'b0), .out(PLA37), .gate(not_7_out));
  Transistor #(.\type ("n")) transistor_217 (.in(1'b0), .out(PLA37), .gate(IA7));
  Transistor #(.\type ("n")) transistor_218 (.in(1'b0), .out(PLA37), .gate(not_10_out));
  Transistor #(.\type ("n")) transistor_219 (.in(1'b0), .out(PLA36), .gate(CB_SET));
  Pull_Resistor #(.pull(1)) pull_resistor_39 (.node(PLA38));
  Transistor #(.\type ("n")) transistor_220 (.in(1'b0), .out(PLA38), .gate(not_1_out));
  Transistor #(.\type ("n")) transistor_221 (.in(1'b0), .out(PLA38), .gate(not_2_out));
  Transistor #(.\type ("n")) transistor_222 (.in(1'b0), .out(PLA38), .gate(not_3_out));
  Transistor #(.\type ("n")) transistor_223 (.in(1'b0), .out(PLA38), .gate(IA4));
  Transistor #(.\type ("n")) transistor_224 (.in(1'b0), .out(PLA38), .gate(not_6_out));
  Transistor #(.\type ("n")) transistor_225 (.in(1'b0), .out(PLA38), .gate(not_7_out));
  Transistor #(.\type ("n")) transistor_226 (.in(1'b0), .out(PLA38), .gate(IA7));
  Transistor #(.\type ("n")) transistor_227 (.in(1'b0), .out(PLA38), .gate(not_11_out));
  Pull_Resistor #(.pull(1)) pull_resistor_40 (.node(PLA39));
  Transistor #(.\type ("n")) transistor_228 (.in(1'b0), .out(PLA39), .gate(IA3));
  Transistor #(.\type ("n")) transistor_229 (.in(1'b0), .out(PLA39), .gate(not_5_out));
  Transistor #(.\type ("n")) transistor_230 (.in(1'b0), .out(PLA39), .gate(not_6_out));
  Transistor #(.\type ("n")) transistor_231 (.in(1'b0), .out(PLA39), .gate(not_7_out));
  Transistor #(.\type ("n")) transistor_232 (.in(1'b0), .out(PLA39), .gate(IA7));
  Transistor #(.\type ("n")) transistor_233 (.in(1'b0), .out(PLA39), .gate(not_10_out));
  Transistor #(.\type ("n")) transistor_234 (.in(1'b0), .out(PLA39), .gate(not_12_out));
  Pull_Resistor #(.pull(1)) pull_resistor_41 (.node(PLA40));
  Pull_Resistor #(.pull(1)) pull_resistor_42 (.node(PLA41));
  Transistor #(.\type ("n")) transistor_235 (.in(1'b0), .out(PLA40), .gate(IA0));
  Transistor #(.\type ("n")) transistor_236 (.in(1'b0), .out(PLA41), .gate(not_1_out));
  Transistor #(.\type ("n")) transistor_237 (.in(1'b0), .out(PLA40), .gate(not_2_out));
  Transistor #(.\type ("n")) transistor_238 (.in(1'b0), .out(PLA41), .gate(not_2_out));
  Transistor #(.\type ("n")) transistor_239 (.in(1'b0), .out(PLA40), .gate(not_3_out));
  Transistor #(.\type ("n")) transistor_240 (.in(1'b0), .out(PLA41), .gate(not_3_out));
  Transistor #(.\type ("n")) transistor_241 (.in(1'b0), .out(PLA41), .gate(IA4));
  Transistor #(.\type ("n")) transistor_242 (.in(1'b0), .out(PLA41), .gate(IA5));
  Transistor #(.\type ("n")) transistor_243 (.in(1'b0), .out(PLA41), .gate(not_7_out));
  Transistor #(.\type ("n")) transistor_244 (.in(1'b0), .out(PLA40), .gate(not_7_out));
  Transistor #(.\type ("n")) transistor_245 (.in(1'b0), .out(PLA41), .gate(IA7));
  Transistor #(.\type ("n")) transistor_246 (.in(1'b0), .out(PLA40), .gate(IA7));
  Transistor #(.\type ("n")) transistor_247 (.in(1'b0), .out(PLA40), .gate(not_10_out));
  Transistor #(.\type ("n")) transistor_248 (.in(1'b0), .out(PLA41), .gate(not_11_out));
  Transistor #(.\type ("n")) transistor_249 (.in(1'b0), .out(PLA40), .gate(not_12_out));
  Pull_Resistor #(.pull(1)) pull_resistor_43 (.node(PLA42));
  Transistor #(.\type ("n")) transistor_250 (.in(1'b0), .out(PLA42), .gate(not_1_out));
  Transistor #(.\type ("n")) transistor_251 (.in(1'b0), .out(PLA42), .gate(not_2_out));
  Transistor #(.\type ("n")) transistor_252 (.in(1'b0), .out(PLA42), .gate(not_3_out));
  Transistor #(.\type ("n")) transistor_253 (.in(1'b0), .out(PLA42), .gate(not_7_out));
  Transistor #(.\type ("n")) transistor_254 (.in(1'b0), .out(PLA42), .gate(not_8_out));
  Transistor #(.\type ("n")) transistor_255 (.in(1'b0), .out(PLA42), .gate(not_10_out));
  Pull_Resistor #(.pull(1)) pull_resistor_44 (.node(PLA43));
  Transistor #(.\type ("n")) transistor_256 (.in(1'b0), .out(PLA43), .gate(IA0));
  Transistor #(.\type ("n")) transistor_257 (.in(1'b0), .out(PLA43), .gate(not_2_out));
  Transistor #(.\type ("n")) transistor_258 (.in(1'b0), .out(PLA43), .gate(not_3_out));
  Transistor #(.\type ("n")) transistor_259 (.in(1'b0), .out(PLA43), .gate(CB_SET));
  Pull_Resistor #(.pull(1)) pull_resistor_45 (.node(PLA45));
  Pull_Resistor #(.pull(1)) pull_resistor_46 (.node(PLA44));
  Transistor #(.\type ("n")) transistor_260 (.in(1'b0), .out(PLA45), .gate(IA1));
  Transistor #(.\type ("n")) transistor_261 (.in(1'b0), .out(PLA45), .gate(not_3_out));
  Transistor #(.\type ("n")) transistor_262 (.in(1'b0), .out(PLA45), .gate(IA3));
  Transistor #(.\type ("n")) transistor_263 (.in(1'b0), .out(PLA45), .gate(not_5_out));
  Transistor #(.\type ("n")) transistor_264 (.in(1'b0), .out(PLA45), .gate(not_6_out));
  Transistor #(.\type ("n")) transistor_265 (.in(1'b0), .out(PLA45), .gate(IA6));
  Transistor #(.\type ("n")) transistor_266 (.in(1'b0), .out(PLA45), .gate(IA7));
  Transistor #(.\type ("n")) transistor_267 (.in(1'b0), .out(PLA45), .gate(not_10_out));
  Transistor #(.\type ("n")) transistor_268 (.in(1'b0), .out(PLA44), .gate(CB_SET));
  Transistor #(.\type ("n")) transistor_269 (.in(1'b0), .out(PLA44), .gate(IDX_SET));
  Pull_Resistor #(.pull(1)) pull_resistor_47 (.node(PLA46));
  Transistor #(.\type ("n")) transistor_270 (.in(1'b0), .out(PLA46), .gate(IA0));
  Transistor #(.\type ("n")) transistor_271 (.in(1'b0), .out(PLA46), .gate(not_2_out));
  Transistor #(.\type ("n")) transistor_272 (.in(1'b0), .out(PLA46), .gate(not_3_out));
  Transistor #(.\type ("n")) transistor_273 (.in(1'b0), .out(PLA46), .gate(IA6));
  Transistor #(.\type ("n")) transistor_274 (.in(1'b0), .out(PLA46), .gate(not_8_out));
  Transistor #(.\type ("n")) transistor_275 (.in(1'b0), .out(PLA46), .gate(not_10_out));
  Pull_Resistor #(.pull(1)) pull_resistor_48 (.node(PLA47));
  Transistor #(.\type ("n")) transistor_276 (.in(1'b0), .out(PLA47), .gate(not_1_out));
  Transistor #(.\type ("n")) transistor_277 (.in(1'b0), .out(PLA47), .gate(IA1));
  Transistor #(.\type ("n")) transistor_278 (.in(1'b0), .out(PLA47), .gate(not_3_out));
  Transistor #(.\type ("n")) transistor_279 (.in(1'b0), .out(PLA47), .gate(not_4_out));
  Transistor #(.\type ("n")) transistor_280 (.in(1'b0), .out(PLA47), .gate(IA4));
  Transistor #(.\type ("n")) transistor_281 (.in(1'b0), .out(PLA47), .gate(not_6_out));
  Transistor #(.\type ("n")) transistor_282 (.in(1'b0), .out(PLA47), .gate(not_7_out));
  Transistor #(.\type ("n")) transistor_283 (.in(1'b0), .out(PLA47), .gate(not_8_out));
  Transistor #(.\type ("n")) transistor_284 (.in(1'b0), .out(PLA47), .gate(not_10_out));
  Pull_Resistor #(.pull(1)) pull_resistor_49 (.node(PLA48));
  Pull_Resistor #(.pull(1)) pull_resistor_50 (.node(PLA49));
  Transistor #(.\type ("n")) transistor_285 (.in(1'b0), .out(PLA48), .gate(IA0));
  Transistor #(.\type ("n")) transistor_286 (.in(1'b0), .out(PLA49), .gate(not_1_out));
  Transistor #(.\type ("n")) transistor_287 (.in(1'b0), .out(PLA49), .gate(not_2_out));
  Transistor #(.\type ("n")) transistor_288 (.in(1'b0), .out(PLA48), .gate(not_2_out));
  Transistor #(.\type ("n")) transistor_289 (.in(1'b0), .out(PLA49), .gate(IA2));
  Transistor #(.\type ("n")) transistor_290 (.in(1'b0), .out(PLA48), .gate(not_3_out));
  Transistor #(.\type ("n")) transistor_291 (.in(1'b0), .out(PLA48), .gate(IA3));
  Transistor #(.\type ("n")) transistor_292 (.in(1'b0), .out(PLA49), .gate(not_4_out));
  Transistor #(.\type ("n")) transistor_293 (.in(1'b0), .out(PLA49), .gate(IA4));
  Transistor #(.\type ("n")) transistor_294 (.in(1'b0), .out(PLA48), .gate(not_5_out));
  Transistor #(.\type ("n")) transistor_295 (.in(1'b0), .out(PLA49), .gate(IA5));
  Transistor #(.\type ("n")) transistor_296 (.in(1'b0), .out(PLA48), .gate(not_6_out));
  Transistor #(.\type ("n")) transistor_297 (.in(1'b0), .out(PLA48), .gate(IA6));
  Transistor #(.\type ("n")) transistor_298 (.in(1'b0), .out(PLA49), .gate(not_7_out));
  Transistor #(.\type ("n")) transistor_299 (.in(1'b0), .out(PLA48), .gate(IA7));
  Transistor #(.\type ("n")) transistor_300 (.in(1'b0), .out(PLA49), .gate(not_8_out));
  Transistor #(.\type ("n")) transistor_301 (.in(1'b0), .out(PLA48), .gate(not_10_out));
  Transistor #(.\type ("n")) transistor_302 (.in(1'b0), .out(PLA49), .gate(IDX_SET));
  Pull_Resistor #(.pull(1)) pull_resistor_51 (.node(PLA50));
  Transistor #(.\type ("n")) transistor_303 (.in(1'b0), .out(PLA50), .gate(IA0));
  Transistor #(.\type ("n")) transistor_304 (.in(1'b0), .out(PLA50), .gate(IA1));
  Transistor #(.\type ("n")) transistor_305 (.in(1'b0), .out(PLA50), .gate(IA2));
  Transistor #(.\type ("n")) transistor_306 (.in(1'b0), .out(PLA50), .gate(not_6_out));
  Transistor #(.\type ("n")) transistor_307 (.in(1'b0), .out(PLA50), .gate(IA6));
  Transistor #(.\type ("n")) transistor_308 (.in(1'b0), .out(PLA50), .gate(IA7));
  Transistor #(.\type ("n")) transistor_309 (.in(1'b0), .out(PLA50), .gate(not_10_out));
  Pull_Resistor #(.pull(1)) pull_resistor_52 (.node(PLA51));
  Transistor #(.\type ("n")) transistor_310 (.in(1'b0), .out(PLA51), .gate(IA0));
  Transistor #(.\type ("n")) transistor_311 (.in(1'b0), .out(PLA51), .gate(IA1));
  Transistor #(.\type ("n")) transistor_312 (.in(1'b0), .out(PLA51), .gate(IA2));
  Transistor #(.\type ("n")) transistor_313 (.in(1'b0), .out(PLA51), .gate(not_4_out));
  Transistor #(.\type ("n")) transistor_314 (.in(1'b0), .out(PLA51), .gate(not_5_out));
  Transistor #(.\type ("n")) transistor_315 (.in(1'b0), .out(PLA51), .gate(IA5));
  Transistor #(.\type ("n")) transistor_316 (.in(1'b0), .out(PLA51), .gate(IA6));
  Transistor #(.\type ("n")) transistor_317 (.in(1'b0), .out(PLA51), .gate(IA7));
  Transistor #(.\type ("n")) transistor_318 (.in(1'b0), .out(PLA51), .gate(not_10_out));
  Pull_Resistor #(.pull(1)) pull_resistor_53 (.node(PLA52));
  Pull_Resistor #(.pull(1)) pull_resistor_54 (.node(PLA53));
  Transistor #(.\type ("n")) transistor_319 (.in(1'b0), .out(PLA53), .gate(IA0));
  Transistor #(.\type ("n")) transistor_320 (.in(1'b0), .out(PLA52), .gate(not_1_out));
  Transistor #(.\type ("n")) transistor_321 (.in(1'b0), .out(PLA53), .gate(IA1));
  Transistor #(.\type ("n")) transistor_322 (.in(1'b0), .out(PLA52), .gate(IA1));
  Transistor #(.\type ("n")) transistor_323 (.in(1'b0), .out(PLA53), .gate(IA2));
  Transistor #(.\type ("n")) transistor_324 (.in(1'b0), .out(PLA52), .gate(not_3_out));
  Transistor #(.\type ("n")) transistor_325 (.in(1'b0), .out(PLA53), .gate(not_7_out));
  Transistor #(.\type ("n")) transistor_326 (.in(1'b0), .out(PLA52), .gate(not_7_out));
  Transistor #(.\type ("n")) transistor_327 (.in(1'b0), .out(PLA52), .gate(IA7));
  Transistor #(.\type ("n")) transistor_328 (.in(1'b0), .out(PLA53), .gate(not_8_out));
  Transistor #(.\type ("n")) transistor_329 (.in(1'b0), .out(PLA53), .gate(not_10_out));
  Transistor #(.\type ("n")) transistor_330 (.in(1'b0), .out(PLA52), .gate(not_11_out));
  Pull_Resistor #(.pull(1)) pull_resistor_55 (.node(PLA54));
  Transistor #(.\type ("n")) transistor_331 (.in(1'b0), .out(PLA54), .gate(not_1_out));
  Transistor #(.\type ("n")) transistor_332 (.in(1'b0), .out(PLA54), .gate(not_2_out));
  Transistor #(.\type ("n")) transistor_333 (.in(1'b0), .out(PLA54), .gate(IA2));
  Transistor #(.\type ("n")) transistor_334 (.in(1'b0), .out(PLA54), .gate(not_4_out));
  Transistor #(.\type ("n")) transistor_335 (.in(1'b0), .out(PLA54), .gate(IA4));
  Transistor #(.\type ("n")) transistor_336 (.in(1'b0), .out(PLA54), .gate(IA5));
  Transistor #(.\type ("n")) transistor_337 (.in(1'b0), .out(PLA54), .gate(not_7_out));
  Transistor #(.\type ("n")) transistor_338 (.in(1'b0), .out(PLA54), .gate(not_8_out));
  Transistor #(.\type ("n")) transistor_339 (.in(1'b0), .out(PLA54), .gate(not_10_out));
  Pull_Resistor #(.pull(1)) pull_resistor_56 (.node(PLA55));
  Transistor #(.\type ("n")) transistor_340 (.in(1'b0), .out(PLA55), .gate(IA0));
  Transistor #(.\type ("n")) transistor_341 (.in(1'b0), .out(PLA55), .gate(not_2_out));
  Transistor #(.\type ("n")) transistor_342 (.in(1'b0), .out(PLA55), .gate(IA2));
  Transistor #(.\type ("n")) transistor_343 (.in(1'b0), .out(PLA55), .gate(not_7_out));
  Transistor #(.\type ("n")) transistor_344 (.in(1'b0), .out(PLA55), .gate(not_8_out));
  Transistor #(.\type ("n")) transistor_345 (.in(1'b0), .out(PLA55), .gate(not_10_out));
  Pull_Resistor #(.pull(1)) pull_resistor_57 (.node(PLA56));
  Pull_Resistor #(.pull(1)) pull_resistor_58 (.node(PLA57));
  Transistor #(.\type ("n")) transistor_346 (.in(1'b0), .out(PLA56), .gate(IA0));
  Transistor #(.\type ("n")) transistor_347 (.in(1'b0), .out(PLA57), .gate(not_1_out));
  Transistor #(.\type ("n")) transistor_348 (.in(1'b0), .out(PLA56), .gate(IA1));
  Transistor #(.\type ("n")) transistor_349 (.in(1'b0), .out(PLA57), .gate(IA1));
  Transistor #(.\type ("n")) transistor_350 (.in(1'b0), .out(PLA57), .gate(not_3_out));
  Transistor #(.\type ("n")) transistor_351 (.in(1'b0), .out(PLA56), .gate(not_3_out));
  Transistor #(.\type ("n")) transistor_352 (.in(1'b0), .out(PLA57), .gate(not_4_out));
  Transistor #(.\type ("n")) transistor_353 (.in(1'b0), .out(PLA57), .gate(not_5_out));
  Transistor #(.\type ("n")) transistor_354 (.in(1'b0), .out(PLA56), .gate(not_7_out));
  Transistor #(.\type ("n")) transistor_355 (.in(1'b0), .out(PLA57), .gate(not_7_out));
  Transistor #(.\type ("n")) transistor_356 (.in(1'b0), .out(PLA57), .gate(not_8_out));
  Transistor #(.\type ("n")) transistor_357 (.in(1'b0), .out(PLA56), .gate(not_8_out));
  Transistor #(.\type ("n")) transistor_358 (.in(1'b0), .out(PLA56), .gate(not_10_out));
  Transistor #(.\type ("n")) transistor_359 (.in(1'b0), .out(PLA57), .gate(not_10_out));
  Pull_Resistor #(.pull(1)) pull_resistor_59 (.node(PLA58));
  Transistor #(.\type ("n")) transistor_360 (.in(1'b0), .out(PLA58), .gate(IA0));
  Transistor #(.\type ("n")) transistor_361 (.in(1'b0), .out(PLA58), .gate(not_2_out));
  Transistor #(.\type ("n")) transistor_362 (.in(1'b0), .out(PLA58), .gate(not_3_out));
  Transistor #(.\type ("n")) transistor_363 (.in(1'b0), .out(PLA58), .gate(IA3));
  Transistor #(.\type ("n")) transistor_364 (.in(1'b0), .out(PLA58), .gate(not_5_out));
  Transistor #(.\type ("n")) transistor_365 (.in(1'b0), .out(PLA58), .gate(not_6_out));
  Transistor #(.\type ("n")) transistor_366 (.in(1'b0), .out(PLA58), .gate(IA6));
  Transistor #(.\type ("n")) transistor_367 (.in(1'b0), .out(PLA58), .gate(IA7));
  Transistor #(.\type ("n")) transistor_368 (.in(1'b0), .out(PLA58), .gate(not_10_out));
  Transistor #(.\type ("n")) transistor_369 (.in(1'b0), .out(PLA58), .gate(IDX_SET));
  Pull_Resistor #(.pull(1)) pull_resistor_60 (.node(PLA59));
  Transistor #(.\type ("n")) transistor_370 (.in(1'b0), .out(PLA59), .gate(IA0));
  Transistor #(.\type ("n")) transistor_371 (.in(1'b0), .out(PLA59), .gate(IA1));
  Transistor #(.\type ("n")) transistor_372 (.in(1'b0), .out(PLA59), .gate(IA2));
  Transistor #(.\type ("n")) transistor_373 (.in(1'b0), .out(PLA59), .gate(not_4_out));
  Transistor #(.\type ("n")) transistor_374 (.in(1'b0), .out(PLA59), .gate(IA4));
  Transistor #(.\type ("n")) transistor_375 (.in(1'b0), .out(PLA59), .gate(IA5));
  Transistor #(.\type ("n")) transistor_376 (.in(1'b0), .out(PLA59), .gate(IA6));
  Transistor #(.\type ("n")) transistor_377 (.in(1'b0), .out(PLA59), .gate(IA7));
  Transistor #(.\type ("n")) transistor_378 (.in(1'b0), .out(PLA59), .gate(not_10_out));
  Pull_Resistor #(.pull(1)) pull_resistor_61 (.node(PLA60));
  Pull_Resistor #(.pull(1)) pull_resistor_62 (.node(PLA61));
  Transistor #(.\type ("n")) transistor_379 (.in(1'b0), .out(PLA60), .gate(IA0));
  Transistor #(.\type ("n")) transistor_380 (.in(1'b0), .out(PLA61), .gate(not_1_out));
  Transistor #(.\type ("n")) transistor_381 (.in(1'b0), .out(PLA61), .gate(not_2_out));
  Transistor #(.\type ("n")) transistor_382 (.in(1'b0), .out(PLA60), .gate(not_2_out));
  Transistor #(.\type ("n")) transistor_383 (.in(1'b0), .out(PLA61), .gate(IA2));
  Transistor #(.\type ("n")) transistor_384 (.in(1'b0), .out(PLA60), .gate(IA2));
  Transistor #(.\type ("n")) transistor_385 (.in(1'b0), .out(PLA61), .gate(not_5_out));
  Transistor #(.\type ("n")) transistor_386 (.in(1'b0), .out(PLA60), .gate(not_5_out));
  Transistor #(.\type ("n")) transistor_387 (.in(1'b0), .out(PLA61), .gate(IA5));
  Transistor #(.\type ("n")) transistor_388 (.in(1'b0), .out(PLA60), .gate(not_6_out));
  Transistor #(.\type ("n")) transistor_389 (.in(1'b0), .out(PLA60), .gate(IA6));
  Transistor #(.\type ("n")) transistor_390 (.in(1'b0), .out(PLA61), .gate(not_7_out));
  Transistor #(.\type ("n")) transistor_391 (.in(1'b0), .out(PLA60), .gate(IA7));
  Transistor #(.\type ("n")) transistor_392 (.in(1'b0), .out(PLA61), .gate(not_8_out));
  Transistor #(.\type ("n")) transistor_393 (.in(1'b0), .out(PLA60), .gate(not_10_out));
  Transistor #(.\type ("n")) transistor_394 (.in(1'b0), .out(PLA61), .gate(not_10_out));
  Pull_Resistor #(.pull(1)) pull_resistor_63 (.node(PLA62));
  Transistor #(.\type ("n")) transistor_395 (.in(1'b0), .out(PLA62), .gate(IA0));
  Transistor #(.\type ("n")) transistor_396 (.in(1'b0), .out(PLA62), .gate(not_2_out));
  Transistor #(.\type ("n")) transistor_397 (.in(1'b0), .out(PLA62), .gate(IA2));
  Transistor #(.\type ("n")) transistor_398 (.in(1'b0), .out(PLA62), .gate(IA5));
  Transistor #(.\type ("n")) transistor_399 (.in(1'b0), .out(PLA62), .gate(IA6));
  Transistor #(.\type ("n")) transistor_400 (.in(1'b0), .out(PLA62), .gate(IA7));
  Transistor #(.\type ("n")) transistor_401 (.in(1'b0), .out(PLA62), .gate(not_10_out));
  Pull_Resistor #(.pull(1)) pull_resistor_64 (.node(PLA63));
  Transistor #(.\type ("n")) transistor_402 (.in(1'b0), .out(PLA63), .gate(not_1_out));
  Transistor #(.\type ("n")) transistor_403 (.in(1'b0), .out(PLA63), .gate(IA1));
  Transistor #(.\type ("n")) transistor_404 (.in(1'b0), .out(PLA63), .gate(IA2));
  Transistor #(.\type ("n")) transistor_405 (.in(1'b0), .out(PLA63), .gate(not_4_out));
  Transistor #(.\type ("n")) transistor_406 (.in(1'b0), .out(PLA63), .gate(IA4));
  Transistor #(.\type ("n")) transistor_407 (.in(1'b0), .out(PLA63), .gate(IA5));
  Transistor #(.\type ("n")) transistor_408 (.in(1'b0), .out(PLA63), .gate(not_7_out));
  Transistor #(.\type ("n")) transistor_409 (.in(1'b0), .out(PLA63), .gate(not_8_out));
  Transistor #(.\type ("n")) transistor_410 (.in(1'b0), .out(PLA63), .gate(not_10_out));
  Pull_Resistor #(.pull(1)) pull_resistor_65 (.node(PLA64));
  Pull_Resistor #(.pull(1)) pull_resistor_66 (.node(PLA65));
  Transistor #(.\type ("n")) transistor_411 (.in(1'b0), .out(PLA64), .gate(not_1_out));
  Transistor #(.\type ("n")) transistor_412 (.in(1'b0), .out(PLA65), .gate(not_1_out));
  Transistor #(.\type ("n")) transistor_413 (.in(1'b0), .out(PLA64), .gate(IA1));
  Transistor #(.\type ("n")) transistor_414 (.in(1'b0), .out(PLA65), .gate(not_2_out));
  Transistor #(.\type ("n")) transistor_415 (.in(1'b0), .out(PLA65), .gate(IA2));
  Transistor #(.\type ("n")) transistor_416 (.in(1'b0), .out(PLA64), .gate(IA2));
  Transistor #(.\type ("n")) transistor_417 (.in(1'b0), .out(PLA65), .gate(IA3));
  Transistor #(.\type ("n")) transistor_418 (.in(1'b0), .out(PLA65), .gate(not_7_out));
  Transistor #(.\type ("n")) transistor_419 (.in(1'b0), .out(PLA64), .gate(not_7_out));
  Transistor #(.\type ("n")) transistor_420 (.in(1'b0), .out(PLA65), .gate(IA7));
  Transistor #(.\type ("n")) transistor_421 (.in(1'b0), .out(PLA64), .gate(IA7));
  Transistor #(.\type ("n")) transistor_422 (.in(1'b0), .out(PLA64), .gate(not_11_out));
  Transistor #(.\type ("n")) transistor_423 (.in(1'b0), .out(PLA65), .gate(not_11_out));
  Pull_Resistor #(.pull(1)) pull_resistor_67 (.node(PLA66));
  Transistor #(.\type ("n")) transistor_424 (.in(1'b0), .out(PLA66), .gate(not_1_out));
  Transistor #(.\type ("n")) transistor_425 (.in(1'b0), .out(PLA66), .gate(not_2_out));
  Transistor #(.\type ("n")) transistor_426 (.in(1'b0), .out(PLA66), .gate(not_3_out));
  Transistor #(.\type ("n")) transistor_427 (.in(1'b0), .out(PLA66), .gate(IA5));
  Transistor #(.\type ("n")) transistor_428 (.in(1'b0), .out(PLA66), .gate(not_7_out));
  Transistor #(.\type ("n")) transistor_429 (.in(1'b0), .out(PLA66), .gate(IA7));
  Transistor #(.\type ("n")) transistor_430 (.in(1'b0), .out(PLA66), .gate(not_11_out));
  Pull_Resistor #(.pull(1)) pull_resistor_68 (.node(PLA67));
  Transistor #(.\type ("n")) transistor_431 (.in(1'b0), .out(PLA67), .gate(not_1_out));
  Transistor #(.\type ("n")) transistor_432 (.in(1'b0), .out(PLA67), .gate(not_2_out));
  Transistor #(.\type ("n")) transistor_433 (.in(1'b0), .out(PLA67), .gate(IA2));
  Transistor #(.\type ("n")) transistor_434 (.in(1'b0), .out(PLA67), .gate(not_7_out));
  Transistor #(.\type ("n")) transistor_435 (.in(1'b0), .out(PLA67), .gate(IA7));
  Transistor #(.\type ("n")) transistor_436 (.in(1'b0), .out(PLA67), .gate(not_11_out));
  Pull_Resistor #(.pull(1)) pull_resistor_69 (.node(PLA68));
  Pull_Resistor #(.pull(1)) pull_resistor_70 (.node(PLA69));
  Transistor #(.\type ("n")) transistor_437 (.in(1'b0), .out(PLA68), .gate(IA0));
  Transistor #(.\type ("n")) transistor_438 (.in(1'b0), .out(PLA69), .gate(not_1_out));
  Transistor #(.\type ("n")) transistor_439 (.in(1'b0), .out(PLA69), .gate(not_2_out));
  Transistor #(.\type ("n")) transistor_440 (.in(1'b0), .out(PLA68), .gate(not_2_out));
  Transistor #(.\type ("n")) transistor_441 (.in(1'b0), .out(PLA68), .gate(IA2));
  Transistor #(.\type ("n")) transistor_442 (.in(1'b0), .out(PLA69), .gate(IA2));
  Transistor #(.\type ("n")) transistor_443 (.in(1'b0), .out(PLA69), .gate(IA3));
  Transistor #(.\type ("n")) transistor_444 (.in(1'b0), .out(PLA69), .gate(IA4));
  Transistor #(.\type ("n")) transistor_445 (.in(1'b0), .out(PLA68), .gate(IA4));
  Transistor #(.\type ("n")) transistor_446 (.in(1'b0), .out(PLA69), .gate(IA5));
  Transistor #(.\type ("n")) transistor_447 (.in(1'b0), .out(PLA68), .gate(not_6_out));
  Transistor #(.\type ("n")) transistor_448 (.in(1'b0), .out(PLA68), .gate(IA6));
  Transistor #(.\type ("n")) transistor_449 (.in(1'b0), .out(PLA69), .gate(not_7_out));
  Transistor #(.\type ("n")) transistor_450 (.in(1'b0), .out(PLA68), .gate(IA7));
  Transistor #(.\type ("n")) transistor_451 (.in(1'b0), .out(PLA69), .gate(not_8_out));
  Transistor #(.\type ("n")) transistor_452 (.in(1'b0), .out(PLA68), .gate(not_10_out));
  Transistor #(.\type ("n")) transistor_453 (.in(1'b0), .out(PLA69), .gate(not_10_out));
  Pull_Resistor #(.pull(1)) pull_resistor_71 (.node(PLA70));
  Transistor #(.\type ("n")) transistor_454 (.in(1'b0), .out(PLA70), .gate(not_1_out));
  Transistor #(.\type ("n")) transistor_455 (.in(1'b0), .out(PLA70), .gate(not_2_out));
  Transistor #(.\type ("n")) transistor_456 (.in(1'b0), .out(PLA70), .gate(IA2));
  Transistor #(.\type ("n")) transistor_457 (.in(1'b0), .out(PLA70), .gate(IA3));
  Transistor #(.\type ("n")) transistor_458 (.in(1'b0), .out(PLA70), .gate(not_5_out));
  Transistor #(.\type ("n")) transistor_459 (.in(1'b0), .out(PLA70), .gate(IA5));
  Transistor #(.\type ("n")) transistor_460 (.in(1'b0), .out(PLA70), .gate(not_7_out));
  Transistor #(.\type ("n")) transistor_461 (.in(1'b0), .out(PLA70), .gate(not_8_out));
  Transistor #(.\type ("n")) transistor_462 (.in(1'b0), .out(PLA70), .gate(not_10_out));
  Pull_Resistor #(.pull(1)) pull_resistor_72 (.node(PLA71));
  Transistor #(.\type ("n")) transistor_463 (.in(1'b0), .out(PLA71), .gate(IA1));
  Transistor #(.\type ("n")) transistor_464 (.in(1'b0), .out(PLA71), .gate(IA2));
  Transistor #(.\type ("n")) transistor_465 (.in(1'b0), .out(PLA71), .gate(not_7_out));
  Transistor #(.\type ("n")) transistor_466 (.in(1'b0), .out(PLA71), .gate(IA7));
  Transistor #(.\type ("n")) transistor_467 (.in(1'b0), .out(PLA71), .gate(not_11_out));
  Pull_Resistor #(.pull(1)) pull_resistor_73 (.node(PLA72));
  Pull_Resistor #(.pull(1)) pull_resistor_74 (.node(PLA73));
  Transistor #(.\type ("n")) transistor_468 (.in(1'b0), .out(PLA72), .gate(IA0));
  Transistor #(.\type ("n")) transistor_469 (.in(1'b0), .out(PLA73), .gate(not_1_out));
  Transistor #(.\type ("n")) transistor_470 (.in(1'b0), .out(PLA72), .gate(IA1));
  Transistor #(.\type ("n")) transistor_471 (.in(1'b0), .out(PLA73), .gate(not_2_out));
  Transistor #(.\type ("n")) transistor_472 (.in(1'b0), .out(PLA72), .gate(IA2));
  Transistor #(.\type ("n")) transistor_473 (.in(1'b0), .out(PLA73), .gate(not_3_out));
  Transistor #(.\type ("n")) transistor_474 (.in(1'b0), .out(PLA72), .gate(IA3));
  Transistor #(.\type ("n")) transistor_475 (.in(1'b0), .out(PLA72), .gate(not_5_out));
  Transistor #(.\type ("n")) transistor_476 (.in(1'b0), .out(PLA73), .gate(IA5));
  Transistor #(.\type ("n")) transistor_477 (.in(1'b0), .out(PLA72), .gate(IA5));
  Transistor #(.\type ("n")) transistor_478 (.in(1'b0), .out(PLA73), .gate(IA6));
  Transistor #(.\type ("n")) transistor_479 (.in(1'b0), .out(PLA72), .gate(IA6));
  Transistor #(.\type ("n")) transistor_480 (.in(1'b0), .out(PLA73), .gate(IA7));
  Transistor #(.\type ("n")) transistor_481 (.in(1'b0), .out(PLA72), .gate(IA7));
  Transistor #(.\type ("n")) transistor_482 (.in(1'b0), .out(PLA73), .gate(not_10_out));
  Transistor #(.\type ("n")) transistor_483 (.in(1'b0), .out(PLA72), .gate(not_10_out));
  Pull_Resistor #(.pull(1)) pull_resistor_75 (.node(PLA74));
  Transistor #(.\type ("n")) transistor_484 (.in(1'b0), .out(PLA74), .gate(not_1_out));
  Transistor #(.\type ("n")) transistor_485 (.in(1'b0), .out(PLA74), .gate(IA1));
  Transistor #(.\type ("n")) transistor_486 (.in(1'b0), .out(PLA74), .gate(not_3_out));
  Transistor #(.\type ("n")) transistor_487 (.in(1'b0), .out(PLA74), .gate(not_4_out));
  Transistor #(.\type ("n")) transistor_488 (.in(1'b0), .out(PLA74), .gate(IA4));
  Transistor #(.\type ("n")) transistor_489 (.in(1'b0), .out(PLA74), .gate(IA5));
  Transistor #(.\type ("n")) transistor_490 (.in(1'b0), .out(PLA74), .gate(not_7_out));
  Transistor #(.\type ("n")) transistor_491 (.in(1'b0), .out(PLA74), .gate(not_8_out));
  Transistor #(.\type ("n")) transistor_492 (.in(1'b0), .out(PLA74), .gate(not_10_out));
  Pull_Resistor #(.pull(1)) pull_resistor_76 (.node(PLA75));
  Transistor #(.\type ("n")) transistor_493 (.in(1'b0), .out(PLA75), .gate(not_1_out));
  Transistor #(.\type ("n")) transistor_494 (.in(1'b0), .out(PLA75), .gate(IA1));
  Transistor #(.\type ("n")) transistor_495 (.in(1'b0), .out(PLA75), .gate(IA3));
  Transistor #(.\type ("n")) transistor_496 (.in(1'b0), .out(PLA75), .gate(not_7_out));
  Transistor #(.\type ("n")) transistor_497 (.in(1'b0), .out(PLA75), .gate(not_8_out));
  Transistor #(.\type ("n")) transistor_498 (.in(1'b0), .out(PLA75), .gate(not_10_out));
  Pull_Resistor #(.pull(1)) pull_resistor_77 (.node(PLA77));
  Pull_Resistor #(.pull(1)) pull_resistor_78 (.node(PLA76));
  Transistor #(.\type ("n")) transistor_499 (.in(1'b0), .out(PLA77), .gate(IA0));
  Transistor #(.\type ("n")) transistor_500 (.in(1'b0), .out(PLA76), .gate(not_1_out));
  Transistor #(.\type ("n")) transistor_501 (.in(1'b0), .out(PLA77), .gate(not_2_out));
  Transistor #(.\type ("n")) transistor_502 (.in(1'b0), .out(PLA76), .gate(not_2_out));
  Transistor #(.\type ("n")) transistor_503 (.in(1'b0), .out(PLA76), .gate(IA2));
  Transistor #(.\type ("n")) transistor_504 (.in(1'b0), .out(PLA77), .gate(IA2));
  Transistor #(.\type ("n")) transistor_505 (.in(1'b0), .out(PLA76), .gate(not_4_out));
  Transistor #(.\type ("n")) transistor_506 (.in(1'b0), .out(PLA76), .gate(IA4));
  Transistor #(.\type ("n")) transistor_507 (.in(1'b0), .out(PLA76), .gate(IA5));
  Transistor #(.\type ("n")) transistor_508 (.in(1'b0), .out(PLA77), .gate(not_6_out));
  Transistor #(.\type ("n")) transistor_509 (.in(1'b0), .out(PLA77), .gate(IA6));
  Transistor #(.\type ("n")) transistor_510 (.in(1'b0), .out(PLA76), .gate(not_7_out));
  Transistor #(.\type ("n")) transistor_511 (.in(1'b0), .out(PLA76), .gate(not_8_out));
  Transistor #(.\type ("n")) transistor_512 (.in(1'b0), .out(PLA77), .gate(not_8_out));
  Transistor #(.\type ("n")) transistor_513 (.in(1'b0), .out(PLA77), .gate(not_11_out));
  Transistor #(.\type ("n")) transistor_514 (.in(1'b0), .out(PLA76), .gate(IDX_SET));
  Pull_Resistor #(.pull(1)) pull_resistor_79 (.node(PLA78));
  Transistor #(.\type ("n")) transistor_515 (.in(1'b0), .out(PLA78), .gate(not_1_out));
  Transistor #(.\type ("n")) transistor_516 (.in(1'b0), .out(PLA78), .gate(not_2_out));
  Transistor #(.\type ("n")) transistor_517 (.in(1'b0), .out(PLA78), .gate(IA2));
  Transistor #(.\type ("n")) transistor_518 (.in(1'b0), .out(PLA78), .gate(not_6_out));
  Transistor #(.\type ("n")) transistor_519 (.in(1'b0), .out(PLA78), .gate(IA6));
  Transistor #(.\type ("n")) transistor_520 (.in(1'b0), .out(PLA78), .gate(not_8_out));
  Transistor #(.\type ("n")) transistor_521 (.in(1'b0), .out(PLA78), .gate(not_11_out));
  Pull_Resistor #(.pull(1)) pull_resistor_80 (.node(PLA79));
  Transistor #(.\type ("n")) transistor_522 (.in(1'b0), .out(PLA79), .gate(not_1_out));
  Transistor #(.\type ("n")) transistor_523 (.in(1'b0), .out(PLA79), .gate(IA1));
  Transistor #(.\type ("n")) transistor_524 (.in(1'b0), .out(PLA79), .gate(IA2));
  Transistor #(.\type ("n")) transistor_525 (.in(1'b0), .out(PLA79), .gate(not_6_out));
  Transistor #(.\type ("n")) transistor_526 (.in(1'b0), .out(PLA79), .gate(IA6));
  Transistor #(.\type ("n")) transistor_527 (.in(1'b0), .out(PLA79), .gate(not_8_out));
  Transistor #(.\type ("n")) transistor_528 (.in(1'b0), .out(PLA79), .gate(not_11_out));
  Pull_Resistor #(.pull(1)) pull_resistor_81 (.node(PLA80));
  Pull_Resistor #(.pull(1)) pull_resistor_82 (.node(PLA81));
  Transistor #(.\type ("n")) transistor_529 (.in(1'b0), .out(PLA80), .gate(IA0));
  Transistor #(.\type ("n")) transistor_530 (.in(1'b0), .out(PLA81), .gate(IA0));
  Transistor #(.\type ("n")) transistor_531 (.in(1'b0), .out(PLA80), .gate(IA1));
  Transistor #(.\type ("n")) transistor_532 (.in(1'b0), .out(PLA81), .gate(not_2_out));
  Transistor #(.\type ("n")) transistor_533 (.in(1'b0), .out(PLA80), .gate(IA2));
  Transistor #(.\type ("n")) transistor_534 (.in(1'b0), .out(PLA81), .gate(not_3_out));
  Transistor #(.\type ("n")) transistor_535 (.in(1'b0), .out(PLA80), .gate(not_6_out));
  Transistor #(.\type ("n")) transistor_536 (.in(1'b0), .out(PLA80), .gate(IA6));
  Transistor #(.\type ("n")) transistor_537 (.in(1'b0), .out(PLA81), .gate(IA6));
  Transistor #(.\type ("n")) transistor_538 (.in(1'b0), .out(PLA81), .gate(IA7));
  Transistor #(.\type ("n")) transistor_539 (.in(1'b0), .out(PLA80), .gate(not_8_out));
  Transistor #(.\type ("n")) transistor_540 (.in(1'b0), .out(PLA81), .gate(not_10_out));
  Transistor #(.\type ("n")) transistor_541 (.in(1'b0), .out(PLA80), .gate(not_11_out));
  Pull_Resistor #(.pull(1)) pull_resistor_83 (.node(PLA82));
  Transistor #(.\type ("n")) transistor_542 (.in(1'b0), .out(PLA82), .gate(not_1_out));
  Transistor #(.\type ("n")) transistor_543 (.in(1'b0), .out(PLA82), .gate(IA1));
  Transistor #(.\type ("n")) transistor_544 (.in(1'b0), .out(PLA82), .gate(not_3_out));
  Transistor #(.\type ("n")) transistor_545 (.in(1'b0), .out(PLA82), .gate(IA3));
  Transistor #(.\type ("n")) transistor_546 (.in(1'b0), .out(PLA82), .gate(not_7_out));
  Transistor #(.\type ("n")) transistor_547 (.in(1'b0), .out(PLA82), .gate(not_8_out));
  Transistor #(.\type ("n")) transistor_548 (.in(1'b0), .out(PLA82), .gate(not_10_out));
  Pull_Resistor #(.pull(1)) pull_resistor_84 (.node(PLA83));
  Transistor #(.\type ("n")) transistor_549 (.in(1'b0), .out(PLA83), .gate(not_1_out));
  Transistor #(.\type ("n")) transistor_550 (.in(1'b0), .out(PLA83), .gate(not_2_out));
  Transistor #(.\type ("n")) transistor_551 (.in(1'b0), .out(PLA83), .gate(not_3_out));
  Transistor #(.\type ("n")) transistor_552 (.in(1'b0), .out(PLA83), .gate(IA4));
  Transistor #(.\type ("n")) transistor_553 (.in(1'b0), .out(PLA83), .gate(not_6_out));
  Transistor #(.\type ("n")) transistor_554 (.in(1'b0), .out(PLA83), .gate(not_7_out));
  Transistor #(.\type ("n")) transistor_555 (.in(1'b0), .out(PLA83), .gate(IA7));
  Transistor #(.\type ("n")) transistor_556 (.in(1'b0), .out(PLA83), .gate(not_11_out));
  Pull_Resistor #(.pull(1)) pull_resistor_85 (.node(PLA85));
  Pull_Resistor #(.pull(1)) pull_resistor_86 (.node(PLA84));
  Transistor #(.\type ("n")) transistor_557 (.in(1'b0), .out(PLA85), .gate(IA0));
  Transistor #(.\type ("n")) transistor_558 (.in(1'b0), .out(PLA84), .gate(not_1_out));
  Transistor #(.\type ("n")) transistor_559 (.in(1'b0), .out(PLA85), .gate(not_2_out));
  Transistor #(.\type ("n")) transistor_560 (.in(1'b0), .out(PLA84), .gate(not_2_out));
  Transistor #(.\type ("n")) transistor_561 (.in(1'b0), .out(PLA84), .gate(IA2));
  Transistor #(.\type ("n")) transistor_562 (.in(1'b0), .out(PLA85), .gate(IA2));
  Transistor #(.\type ("n")) transistor_563 (.in(1'b0), .out(PLA85), .gate(IA3));
  Transistor #(.\type ("n")) transistor_564 (.in(1'b0), .out(PLA84), .gate(not_4_out));
  Transistor #(.\type ("n")) transistor_565 (.in(1'b0), .out(PLA85), .gate(IA6));
  Transistor #(.\type ("n")) transistor_566 (.in(1'b0), .out(PLA84), .gate(IA6));
  Transistor #(.\type ("n")) transistor_567 (.in(1'b0), .out(PLA85), .gate(IA7));
  Transistor #(.\type ("n")) transistor_568 (.in(1'b0), .out(PLA84), .gate(IA7));
  Transistor #(.\type ("n")) transistor_569 (.in(1'b0), .out(PLA85), .gate(not_10_out));
  Transistor #(.\type ("n")) transistor_570 (.in(1'b0), .out(PLA84), .gate(not_10_out));
  Pull_Resistor #(.pull(1)) pull_resistor_87 (.node(PLA86));
  Transistor #(.\type ("n")) transistor_571 (.in(1'b0), .out(PLA86), .gate(IA0));
  Transistor #(.\type ("n")) transistor_572 (.in(1'b0), .out(PLA86), .gate(IA1));
  Transistor #(.\type ("n")) transistor_573 (.in(1'b0), .out(PLA86), .gate(IA2));
  Transistor #(.\type ("n")) transistor_574 (.in(1'b0), .out(PLA86), .gate(not_6_out));
  Transistor #(.\type ("n")) transistor_575 (.in(1'b0), .out(PLA86), .gate(IA6));
  Transistor #(.\type ("n")) transistor_576 (.in(1'b0), .out(PLA86), .gate(not_8_out));
  Transistor #(.\type ("n")) transistor_577 (.in(1'b0), .out(PLA86), .gate(not_11_out));
  Pull_Resistor #(.pull(1)) pull_resistor_88 (.node(PLA87));
  Transistor #(.\type ("n")) transistor_578 (.in(1'b0), .out(PLA87), .gate(not_1_out));
  Transistor #(.\type ("n")) transistor_579 (.in(1'b0), .out(PLA87), .gate(IA1));
  Transistor #(.\type ("n")) transistor_580 (.in(1'b0), .out(PLA87), .gate(IA2));
  Transistor #(.\type ("n")) transistor_581 (.in(1'b0), .out(PLA87), .gate(not_6_out));
  Transistor #(.\type ("n")) transistor_582 (.in(1'b0), .out(PLA87), .gate(IA6));
  Transistor #(.\type ("n")) transistor_583 (.in(1'b0), .out(PLA87), .gate(not_8_out));
  Transistor #(.\type ("n")) transistor_584 (.in(1'b0), .out(PLA87), .gate(not_11_out));
  Pull_Resistor #(.pull(1)) pull_resistor_89 (.node(PLA89));
  Pull_Resistor #(.pull(1)) pull_resistor_90 (.node(PLA88));
  Transistor #(.\type ("n")) transistor_585 (.in(1'b0), .out(PLA89), .gate(not_1_out));
  Transistor #(.\type ("n")) transistor_586 (.in(1'b0), .out(PLA88), .gate(not_1_out));
  Transistor #(.\type ("n")) transistor_587 (.in(1'b0), .out(PLA89), .gate(not_2_out));
  Transistor #(.\type ("n")) transistor_588 (.in(1'b0), .out(PLA88), .gate(not_2_out));
  Transistor #(.\type ("n")) transistor_589 (.in(1'b0), .out(PLA88), .gate(IA2));
  Transistor #(.\type ("n")) transistor_590 (.in(1'b0), .out(PLA89), .gate(IA2));
  Transistor #(.\type ("n")) transistor_591 (.in(1'b0), .out(PLA88), .gate(IA3));
  Transistor #(.\type ("n")) transistor_592 (.in(1'b0), .out(PLA88), .gate(IA4));
  Transistor #(.\type ("n")) transistor_593 (.in(1'b0), .out(PLA88), .gate(not_6_out));
  Transistor #(.\type ("n")) transistor_594 (.in(1'b0), .out(PLA89), .gate(IA6));
  Transistor #(.\type ("n")) transistor_595 (.in(1'b0), .out(PLA88), .gate(not_7_out));
  Transistor #(.\type ("n")) transistor_596 (.in(1'b0), .out(PLA89), .gate(IA7));
  Transistor #(.\type ("n")) transistor_597 (.in(1'b0), .out(PLA88), .gate(not_8_out));
  Transistor #(.\type ("n")) transistor_598 (.in(1'b0), .out(PLA88), .gate(not_10_out));
  Transistor #(.\type ("n")) transistor_599 (.in(1'b0), .out(PLA89), .gate(not_10_out));
  Pull_Resistor #(.pull(1)) pull_resistor_91 (.node(PLA90));
  Transistor #(.\type ("n")) transistor_600 (.in(1'b0), .out(PLA90), .gate(IA0));
  Transistor #(.\type ("n")) transistor_601 (.in(1'b0), .out(PLA90), .gate(not_2_out));
  Transistor #(.\type ("n")) transistor_602 (.in(1'b0), .out(PLA90), .gate(IA2));
  Transistor #(.\type ("n")) transistor_603 (.in(1'b0), .out(PLA90), .gate(IA5));
  Transistor #(.\type ("n")) transistor_604 (.in(1'b0), .out(PLA90), .gate(IA6));
  Transistor #(.\type ("n")) transistor_605 (.in(1'b0), .out(PLA90), .gate(IA7));
  Transistor #(.\type ("n")) transistor_606 (.in(1'b0), .out(PLA90), .gate(not_10_out));
  Pull_Resistor #(.pull(1)) pull_resistor_92 (.node(PLA91));
  Transistor #(.\type ("n")) transistor_607 (.in(1'b0), .out(PLA91), .gate(not_1_out));
  Transistor #(.\type ("n")) transistor_608 (.in(1'b0), .out(PLA91), .gate(IA1));
  Transistor #(.\type ("n")) transistor_609 (.in(1'b0), .out(PLA91), .gate(IA2));
  Transistor #(.\type ("n")) transistor_610 (.in(1'b0), .out(PLA91), .gate(IA3));
  Transistor #(.\type ("n")) transistor_611 (.in(1'b0), .out(PLA91), .gate(IA6));
  Transistor #(.\type ("n")) transistor_612 (.in(1'b0), .out(PLA91), .gate(IA7));
  Transistor #(.\type ("n")) transistor_613 (.in(1'b0), .out(PLA91), .gate(not_10_out));
  Pull_Resistor #(.pull(1)) pull_resistor_93 (.node(PLA92));
  Pull_Resistor #(.pull(1)) pull_resistor_94 (.node(PLA93));
  Transistor #(.\type ("n")) transistor_614 (.in(1'b0), .out(PLA93), .gate(not_1_out));
  Transistor #(.\type ("n")) transistor_615 (.in(1'b0), .out(PLA92), .gate(not_1_out));
  Transistor #(.\type ("n")) transistor_616 (.in(1'b0), .out(PLA93), .gate(IA1));
  Transistor #(.\type ("n")) transistor_617 (.in(1'b0), .out(PLA92), .gate(IA1));
  Transistor #(.\type ("n")) transistor_618 (.in(1'b0), .out(PLA92), .gate(IA2));
  Transistor #(.\type ("n")) transistor_619 (.in(1'b0), .out(PLA93), .gate(IA2));
  Transistor #(.\type ("n")) transistor_620 (.in(1'b0), .out(PLA92), .gate(not_4_out));
  Transistor #(.\type ("n")) transistor_621 (.in(1'b0), .out(PLA93), .gate(not_4_out));
  Transistor #(.\type ("n")) transistor_622 (.in(1'b0), .out(PLA92), .gate(IA4));
  Transistor #(.\type ("n")) transistor_623 (.in(1'b0), .out(PLA93), .gate(not_5_out));
  Transistor #(.\type ("n")) transistor_624 (.in(1'b0), .out(PLA93), .gate(not_6_out));
  Transistor #(.\type ("n")) transistor_625 (.in(1'b0), .out(PLA92), .gate(not_6_out));
  Transistor #(.\type ("n")) transistor_626 (.in(1'b0), .out(PLA93), .gate(not_7_out));
  Transistor #(.\type ("n")) transistor_627 (.in(1'b0), .out(PLA92), .gate(not_7_out));
  Transistor #(.\type ("n")) transistor_628 (.in(1'b0), .out(PLA92), .gate(not_8_out));
  Transistor #(.\type ("n")) transistor_629 (.in(1'b0), .out(PLA93), .gate(not_8_out));
  Transistor #(.\type ("n")) transistor_630 (.in(1'b0), .out(PLA92), .gate(not_10_out));
  Transistor #(.\type ("n")) transistor_631 (.in(1'b0), .out(PLA93), .gate(not_10_out));
  Pull_Resistor #(.pull(1)) pull_resistor_95 (.node(PLA94));
  Transistor #(.\type ("n")) transistor_632 (.in(1'b0), .out(PLA94), .gate(not_1_out));
  Transistor #(.\type ("n")) transistor_633 (.in(1'b0), .out(PLA94), .gate(not_2_out));
  Transistor #(.\type ("n")) transistor_634 (.in(1'b0), .out(PLA94), .gate(not_3_out));
  Transistor #(.\type ("n")) transistor_635 (.in(1'b0), .out(PLA94), .gate(IA5));
  Transistor #(.\type ("n")) transistor_636 (.in(1'b0), .out(PLA94), .gate(not_7_out));
  Transistor #(.\type ("n")) transistor_637 (.in(1'b0), .out(PLA94), .gate(IA7));
  Transistor #(.\type ("n")) transistor_638 (.in(1'b0), .out(PLA94), .gate(not_11_out));
  Pull_Resistor #(.pull(1)) pull_resistor_96 (.node(PLA95));
  Transistor #(.\type ("n")) transistor_639 (.in(1'b0), .out(PLA95), .gate(not_1_out));
  Transistor #(.\type ("n")) transistor_640 (.in(1'b0), .out(PLA95), .gate(IA1));
  Transistor #(.\type ("n")) transistor_641 (.in(1'b0), .out(PLA95), .gate(not_3_out));
  Transistor #(.\type ("n")) transistor_642 (.in(1'b0), .out(PLA95), .gate(not_4_out));
  Transistor #(.\type ("n")) transistor_643 (.in(1'b0), .out(PLA95), .gate(not_5_out));
  Transistor #(.\type ("n")) transistor_644 (.in(1'b0), .out(PLA95), .gate(not_7_out));
  Transistor #(.\type ("n")) transistor_645 (.in(1'b0), .out(PLA95), .gate(not_8_out));
  Transistor #(.\type ("n")) transistor_646 (.in(1'b0), .out(PLA95), .gate(not_10_out));
  Pull_Resistor #(.pull(1)) pull_resistor_97 (.node(PLA97));
  Pull_Resistor #(.pull(1)) pull_resistor_98 (.node(PLA96));
  Transistor #(.\type ("n")) transistor_647 (.in(1'b0), .out(PLA96), .gate(not_1_out));
  Transistor #(.\type ("n")) transistor_648 (.in(1'b0), .out(PLA97), .gate(not_1_out));
  Transistor #(.\type ("n")) transistor_649 (.in(1'b0), .out(PLA97), .gate(IA1));
  Transistor #(.\type ("n")) transistor_650 (.in(1'b0), .out(PLA96), .gate(not_2_out));
  Transistor #(.\type ("n")) transistor_651 (.in(1'b0), .out(PLA97), .gate(IA2));
  Transistor #(.\type ("n")) transistor_652 (.in(1'b0), .out(PLA96), .gate(IA2));
  Transistor #(.\type ("n")) transistor_653 (.in(1'b0), .out(PLA96), .gate(not_4_out));
  Transistor #(.\type ("n")) transistor_654 (.in(1'b0), .out(PLA97), .gate(not_4_out));
  Transistor #(.\type ("n")) transistor_655 (.in(1'b0), .out(PLA96), .gate(IA4));
  Transistor #(.\type ("n")) transistor_656 (.in(1'b0), .out(PLA97), .gate(not_5_out));
  Transistor #(.\type ("n")) transistor_657 (.in(1'b0), .out(PLA97), .gate(IA5));
  Transistor #(.\type ("n")) transistor_658 (.in(1'b0), .out(PLA96), .gate(not_6_out));
  Transistor #(.\type ("n")) transistor_659 (.in(1'b0), .out(PLA96), .gate(not_7_out));
  Transistor #(.\type ("n")) transistor_660 (.in(1'b0), .out(PLA97), .gate(not_7_out));
  Transistor #(.\type ("n")) transistor_661 (.in(1'b0), .out(PLA97), .gate(not_8_out));
  Transistor #(.\type ("n")) transistor_662 (.in(1'b0), .out(PLA96), .gate(not_8_out));
  Transistor #(.\type ("n")) transistor_663 (.in(1'b0), .out(PLA96), .gate(not_10_out));
  Transistor #(.\type ("n")) transistor_664 (.in(1'b0), .out(PLA97), .gate(not_10_out));
  Pull_Resistor #(.pull(1)) pull_resistor_99 (.node(PLA98));
  Transistor #(.\type ("n")) transistor_665 (.in(1'b0), .out(PLA98), .gate(IA2));
  Transistor #(.\type ("n")) transistor_666 (.in(1'b0), .out(PLA98), .gate(IA4));
  Transistor #(.\type ("n")) transistor_667 (.in(1'b0), .out(PLA98), .gate(not_6_out));
  Transistor #(.\type ("n")) transistor_668 (.in(1'b0), .out(PLA98), .gate(IA6));
  Transistor #(.\type ("n")) transistor_669 (.in(1'b0), .out(PLA98), .gate(not_8_out));
  Transistor #(.\type ("n")) transistor_670 (.in(1'b0), .out(PLA98), .gate(not_11_out));

  assign PLA1_2 = PLA1;
  assign PLA2_2 = PLA2;
  assign PLA3_2 = PLA3;
  assign PLA5_2 = PLA5;
  assign PLA7_2 = PLA7;
  assign PLA8_2 = PLA8;
  assign PLA42_2 = PLA42;
  assign PLA47_2 = PLA47;
  assign PLA50_2 = PLA50;
  assign PLA52_2 = PLA52;
  assign PLA53_2 = PLA53;
  assign PLA54_2 = PLA54;
  assign PLA57_2 = PLA57;
  assign PLA76_2 = PLA76;
  assign PLA93_2 = PLA93;
  assign PLA98_2 = PLA88;
  assign PLA98_3 = PLA98;

  // Notes on the sheet:
  //   W82
  //   X
  //   98
  //   97
  //   X
  //   96
  //   X
  //   X
  //   X
  //   95
  //   X
  //   X
  //   93
  //   94
  //   X
  //   X
  //   92
  //   91
  //   X
  //   X
  //   X
  //   89
  //   90
  //   88
  //   X
  //   X
  //   X
  //   X
  //   X
  //   87
  //   X
  //   X
  //   X
  //   X
  //   X
  //   X
  //   85
  //   86
  //   X
  //   X
  //   X
  //   X
  //   X
  //   84
  //   X
  //   X
  //   X
  //   X
  //   X
  //   83
  //   X
  //   X
  //   X
  //   X
  //   81
  //   82
  //   80
  //   X
  //   X
  //   X
  //   X
  //   X
  //   79
  //   X
  //   X
  //   X
  //   X
  //   X
  //   X
  //   X
  //   X
  //   X
  //   X
  //   78
  //   77
  //   76
  //   X
  //   X
  //   X
  //   X
  //   X
  //   75
  //   X
  //   X
  //   X
  //   X
  //   X
  //   X
  //   X
  //   X
  //   X
  //   73
  //   74
  //   X
  //   X
  //   X
  //   X
  //   X
  //   X
  //   72
  //   X
  //   X
  //   X
  //   X
  //   X
  //   X
  //   71
  //   X
  //   X
  //   X
  //   X
  //   X
  //   X
  //   X
  //   X
  //   70
  //   69
  //   X
  //   X
  //   68
  //   X
  //   X
  //   X
  //   67
  //   X
  //   X
  //   X
  //   X
  //   X
  //   X
  //   X
  //   66
  //   65
  //   X
  //   X
  //   X
  //   X
  //   X
  //   X
  //   64
  //   X
  //   X
  //   X
  //   63
  //   X
  //   X
  //   X
  //   X
  //   X
  //   X
  //   X
  //   X
  //   X
  //   X
  //   X
  //   61
  //   62
  //   X
  //   X
  //   X
  //   X
  //   X
  //   X
  //   60
  //   X
  //   59
  //   X
  //   X
  //   X
  //   X
  //   X
  //   X
  //   58
  //   57
  //   X
  //   56
  //   X
  //   X
  //   X
  //   55
  //   X
  //   X
  //   X
  //   X
  //   X
  //   X
  //   X
  //   X
  //   X
  //   X
  //   X
  //   X
  //   X
  //   53
  //   54
  //   X
  //   52
  //   X
  //   X
  //   X
  //   51
  //   49
  //   50
  //   48
  //   X
  //   X
  //   47
  //   X
  //   X
  //   X
  //   46
  //   45
  //   X
  //   X
  //   X
  //   44
  //   43
  //   X
  //   X
  //   X
  //   X
  //   X
  //   X
  //   41
  //   42
  //   X
  //   40
  //   39
  //   X
  //   37
  //   38
  //   X
  //   36
  //   X
  //   X
  //   35
  //   X
  //   X
  //   X
  //   34
  //   33
  //   X
  //   X
  //   32
  //   X
  //   X
  //   31
  //   X
  //   X
  //   X
  //   X
  //   29
  //   30
  //   28
  //   27
  //   X
  //   X
  //   X
  //   X
  //   26
  //   25
  //   X
  //   X
  //   24
  //   22
  //   23
  //   X
  //   X
  //   X
  //   21
  //   X
  //   X
  //   20
  //   X
  //   X
  //   19
  //   X
  //   X
  //   X
  //   X
  //   17
  //   18
  //   X
  //   X
  //   X
  //   16
  //   X
  //   X
  //   15
  //   14
  //   X
  //   X
  //   X
  //   13
  //   X
  //   X
  //   12
  //   X
  //   X
  //   11
  //   X
  //   X
  //   10
  //   9
  //   X
  //   X
  //   X
  //   8
  //   X
  //   X
  //   7
  //   X
  //   X
  //   5
  //   6
  //   4
  //   X
  //   X
  //   3
  //   2
  //   X
  //   1
  //   0
  //   X
  //   X
  //   X
  //   0
  //   1
  //   2
  //   3
  //   4
  //   5
  //   6
  //   7
  //   w74
  //   w82
  //   w90
  //   w92
  //   w96
  //   w100
endmodule

module STATE_DECODE (
  input  PLA0,
  input  PLA1,
  input  PLA2,
  input  PLA3,
  input  PLA4,
  input  PLA5,
  input  PLA6,
  input  PLA7,
  input  PLA8,
  input  PLA9,
  input  PLA10,
  input  PLA11,
  input  PLA12,
  input  PLA13,
  input  PLA14,
  input  PLA15,
  input  PLA16,
  input  PLA17,
  input  PLA18,
  input  PLA19,
  input  PLA20,
  input  PLA21,
  input  PLA22,
  input  PLA23,
  input  PLA24,
  input  PLA25,
  input  PLA26,
  input  PLA27,
  input  PLA28,
  input  PLA29,
  input  PLA30,
  input  PLA31,
  input  PLA32,
  input  PLA33,
  input  PLA34,
  input  PLA35,
  input  PLA36,
  input  PLA37,
  input  PLA38,
  input  PLA39,
  input  PLA40,
  input  PLA41,
  input  PLA42,
  input  PLA43,
  input  PLA44,
  input  PLA45,
  input  PLA46,
  input  PLA47,
  input  PLA48,
  input  PLA49,
  input  PLA50,
  input  PLA51,
  input  PLA52,
  input  PLA53,
  input  PLA54,
  input  PLA55,
  input  PLA56,
  input  PLA57,
  input  PLA58,
  input  PLA59,
  input  PLA60,
  input  PLA61,
  input  PLA62,
  input  PLA63,
  input  PLA64,
  input  PLA65,
  input  PLA66,
  input  PLA67,
  input  PLA68,
  input  PLA69,
  input  PLA70,
  input  PLA71,
  input  PLA72,
  input  PLA73,
  input  PLA74,
  input  PLA75,
  input  PLA76,
  input  PLA77,
  input  PLA78,
  input  PLA79,
  input  PLA80,
  input  PLA81,
  input  PLA82,
  input  PLA83,
  input  PLA84,
  input  PLA85,
  input  PLA86,
  input  PLA87,
  input  PLA88,
  input  PLA89,
  input  PLA90,
  input  PLA91,
  input  PLA92,
  input  PLA93,
  input  PLA94,
  input  PLA95,
  input  PLA96,
  input  PLA97,
  input  PLA98,
  input  M2,
  input  M3,
  input  M4,
  input  M6,
  input  IA3,
  input  SEL_RST_NMI_IM1,
  input  SEL_IM2,
  input  IDX_SET,
  output GRP_PREFIX,
  output w139,
  output w148,
  output w142,
  output w149,
  output w150,
  output w151,
  output w156,
  output w154,
  output GRP_FLAGS,
  output w155,
  output GRP_BRANCH,
  output GRP_V_IF,
  output GRP_N8,
  output w160,
  output GRP_239,
  output w162,
  output w163,
  output w164,
  output w165,
  output w166,
  output GRP_387,
  output GRP_SP,
  output w174,
  output w175,
  output w176,
  output GRP_439,
  output GRP_488,
  output w178,
  output w179,
  output GRP_IO,
  output w180,
  output w181,
  output w182,
  output w184,
  output w185,
  output GRP_BLOCK,
  output GRP_A_MEM_IO,
  output w188,
  output w189,
  output w168,
  output GRP_DST_AF,
  output GRP_M_HL,
  output w170,
  output w171,
  output REQ_REG_DST,
  output w191,
  output w198,
  output GRP_LDI_CPI,
  output w199,
  output GRP_220,
  output w254,
  output ADD_SUB_HL,
  output GRP_R16_DIR,
  output GRP_SHIFT,
  output GRP_IDX
);

  wire and_3_out, and_6_out, and_7_out, and_8_out, and_9_out, and_10_out, not_1_out, not_2_out, not_3_out,
       not_4_out, not_5_out, not_6_out, not_7_out, not_8_out, not_9_out, not_10_out, not_11_out, not_12_out,
       not_13_out, not_14_out, not_15_out, not_16_out, or_6_out, w157;

  nor nor_1 (GRP_PREFIX, PLA47, PLA54, PLA57);
  not not_1 (not_1_out, SEL_IM2);
  nor nor_2 (w168, PLA10, PLA12, PLA24);
  not not_2 (not_2_out, GRP_M_HL);
  nor nor_3 (GRP_DST_AF, PLA22, w148);
  nor nor_4 (w191, not_2_out, PLA79, PLA80, PLA81, PLA83, PLA92, PLA93);
  and and_1 (w139, w157, GRP_N8, GRP_239, GRP_M_HL);
  nor nor_5 (w157, not_1_out, PLA50, PLA51, PLA55, PLA56, PLA60, PLA67, PLA68, PLA69, PLA72, PLA74, PLA77, PLA78, PLA79, PLA80, PLA83, PLA88, PLA91);
  not not_3 (not_3_out, w199);
  and and_2 (w198, not_3_out, w170);
  nor nor_6 (GRP_M_HL, PLA39, PLA40, PLA43, PLA44, PLA45, PLA46, PLA48, PLA49);
  or or_1 (GRP_LDI_CPI, PLA86, PLA87);
  nor nor_7 (w148, PLA11, PLA16, PLA17, PLA21, PLA27, PLA33, PLA34, PLA38);
  nor nor_8 (w199, PLA87, PLA83, w254);
  not not_4 (not_4_out, w174);
  or or_2 (GRP_220, not_4_out, and_3_out);
  and and_3 (and_3_out, M6, GRP_IDX);
  not not_5 (not_5_out, GRP_220);
  and and_4 (w142, GRP_BLOCK, not_5_out, not_6_out);
  nor nor_9 (w170, PLA49, PLA55, PLA56, PLA44, PLA58, PLA60, PLA67, PLA68, PLA69, PLA74, PLA91);
  not not_6 (not_6_out, ADD_SUB_HL);
  nor nor_10 (w254, GRP_220, GRP_BLOCK);
  nor nor_11 (GRP_V_IF, PLA11, PLA14, PLA16, PLA18, PLA19, PLA20, PLA22, PLA30, PLA32);
  or or_3 (ADD_SUB_HL, PLA29, PLA30);
  not not_7 (not_7_out, SEL_IM2);
  nor nor_12 (w171, PLA6, PLA9, PLA13);
  nor nor_13 (GRP_R16_DIR, PLA67, PLA68);
  nor nor_14 (w149, SEL_RST_NMI_IM1, not_7_out, PLA53, PLA72, PLA77, PLA78, PLA82, PLA89, PLA93, PLA94);
  nor nor_15 (GRP_N8, PLA34, PLA35, PLA50, PLA51, PLA61, PLA72);
  or or_4 (GRP_SHIFT, PLA27, PLA28);
  nor nor_16 (REQ_REG_DST, PLA24, PLA25, PLA28, PLA31, PLA32, PLA35, PLA37);
  not not_8 (not_8_out, IDX_SET);
  and and_5 (GRP_IDX, not_8_out, not_9_out);
  not not_9 (not_9_out, GRP_M_HL);
  nor nor_17 (w150, PLA11, PLA21, PLA27, PLA28, PLA31, PLA33, PLA34, PLA35, PLA37);
  nor nor_18 (w160, PLA5, PLA7, PLA8, PLA16, PLA17, PLA19, PLA20, PLA22, PLA23, PLA25);
  nor nor_19 (GRP_SP, SEL_RST_NMI_IM1, PLA52, PLA53, PLA56, PLA63, PLA74, PLA75, PLA88);
  not not_10 (not_10_out, SEL_IM2);
  nor nor_20 (w151, not_10_out, PLA55, PLA60, PLA67, PLA68, PLA69, PLA77, PLA78, PLA91);
  nor nor_21 (w174, PLA7, PLA8, PLA32, PLA36, PLA50, PLA51);
  nor nor_22 (GRP_239, SEL_RST_NMI_IM1, PLA29, PLA30, PLA48, PLA52, PLA53, PLA61, PLA62, PLA63, PLA71, PLA75);
  nor nor_23 (w175, PLA50, PLA51, PLA72);
  nor nor_24 (w176, PLA82, PLA84);
  nor nor_25 (GRP_FLAGS, PLA4, PLA5, PLA6, PLA7, PLA9, PLA26, PLA28, PLA29, PLA30, PLA31, PLA32, PLA33, PLA34);
  nor nor_26 (GRP_439, PLA4, PLA5, PLA6, PLA7, PLA9);
  nor nor_27 (w162, PLA5, PLA7, PLA8, PLA11, PLA16, PLA21, PLA26, PLA28, PLA30, PLA31, PLA32, PLA33, PLA34, PLA38);
  not not_11 (not_11_out, GRP_R16_DIR);
  not not_12 (not_12_out, GRP_A_MEM_IO);
  and and_6 (and_6_out, not_11_out, IA3);
  not not_13 (not_13_out, SEL_IM2);
  not not_14 (not_14_out, GRP_BRANCH);
  and and_7 (and_7_out, w175, not_14_out);
  nor nor_28 (GRP_488, not_12_out, and_6_out, and_7_out, PLA75, not_15_out, PLA91);
  not not_15 (not_15_out, GRP_SP);
  nor nor_29 (w163, PLA32, PLA33, PLA34, PLA36, PLA37);
  nor nor_30 (w178, PLA7, PLA8);
  nor nor_31 (GRP_BRANCH, SEL_RST_NMI_IM1, not_13_out, PLA50, PLA51, PLA52, PLA53, PLA55, PLA56, PLA63, PLA69, PLA72, PLA74, PLA92);
  nor nor_32 (w179, PLA5, PLA7, PLA8);
  and and_8 (and_8_out, M2, PLA77);
  and and_9 (and_9_out, M3, PLA78);
  or or_5 (GRP_IO, and_8_out, and_9_out, and_10_out);
  and and_10 (and_10_out, M4, or_6_out);
  nor nor_33 (w164, PLA26, PLA39, PLA40, PLA46, PLA48, PLA60, PLA61, PLA62, PLA71, PLA77, PLA78, PLA79, PLA80, PLA83);
  or or_6 (or_6_out, PLA61, PLA71);
  nor nor_34 (w180, PLA12, PLA24);
  nor nor_35 (w154, SEL_RST_NMI_IM1, PLA11, PLA16, PLA17, PLA27, PLA28, PLA31, PLA35, PLA37);
  nor nor_36 (w181, PLA13, PLA25, PLA26);
  not not_16 (not_16_out, SEL_IM2);
  nor nor_37 (w165, PLA7, PLA8, PLA13, PLA17, PLA26, PLA32);
  nor nor_38 (w182, PLA33, PLA36);
  nor nor_39 (w184, PLA55, PLA56);
  nor nor_40 (w155, not_16_out, PLA44, PLA45, PLA49, PLA56, PLA60, PLA67, PLA68, PLA74, PLA77, PLA78, PLA83, PLA88);
  nor nor_41 (w185, PLA56, PLA74);
  nor nor_42 (w166, PLA9, PLA18, PLA19, PLA30);
  nor nor_43 (GRP_BLOCK, PLA77, PLA78, PLA79, PLA80);
  nor nor_44 (GRP_A_MEM_IO, PLA60, PLA61, PLA62);
  nor nor_45 (w188, PLA71, PLA72, PLA77, PLA78);
  nor nor_46 (w156, PLA10, PLA12, PLA14, PLA16, PLA18, PLA19, PLA20, PLA22, PLA29, PLA30);
  nor nor_47 (GRP_387, SEL_RST_NMI_IM1, PLA39, PLA48, PLA56, PLA64, PLA65, PLA70, PLA74, PLA82, PLA83, PLA85, PLA88, PLA89, PLA93);
  nor nor_48 (w189, PLA78, PLA77, PLA72, PLA73);
  // NOT_Gate not_17 is placed but not wired
endmodule
module SEQUENCER (
  input  CLK,
  input  RES,
  input  BUS_Z,
  input  INT_ACK,
  input  DIS_WR_ADR,
  input  WAIT,
  input  COND_DONE,
  input  IDX_SET,
  input  GRP_BLOCK,
  input  GRP_220,
  input  GRP_239,
  input  GRP_N8,
  input  GRP_M_HL,
  input  GRP_IO,
  input  PLA88,
  input  PLA98,
  input  w142,
  input  w149,
  input  w155,
  input  w164,
  input  w190,
  input  w139,
  input  w151,
  output nRES_TCLK,
  output nRES_MCLK,
  output M1,
  output M2,
  output M3,
  output M4,
  output M5,
  output M6,
  output T1,
  output T2,
  output T3,
  output T4,
  output T5,
  output T6
);

  wire and_1_out, and_2_out, and_3_out, and_4_out, and_5_out, and_6_out, and_7_out, and_8_out, and_9_out,
       and_10_out, and_11_out, and_12_out, and_13_out, and_14_out, and_15_out, and_16_out, and_17_out,
       and_18_out, and_19_out, and_20_out, and_21_out, and_22_out, and_23_out, and_24_out, and_25_out,
       and_26_out, and_27_out, and_28_out, and_29_out, and_30_out, and_31_out, and_32_out, and_33_out,
       and_34_out, and_35_out, and_36_out, d_latch_1_q, d_latch_2_q, d_latch_3_q, d_latch_4_q, d_latch_5_q,
       d_latch_6_nq, d_latch_7_q, d_latch_8_q, d_latch_9_q, d_latch_10_q, d_latch_11_q, d_latch_12_q,
       d_latch_13_q, d_latch_14_q, d_latch_15_q, nand_1_out, nand_2_out, nand_3_out, nand_4_out, nand_5_out,
       nand_6_out, nor_1_out, nor_2_out, nor_3_out, nor_4_out, nor_5_out, nor_6_out, not_1_out, not_2_out,
       or_1_out, or_2_out, or_3_out, or_4_out, or_5_out, or_6_out, or_7_out, or_8_out, or_9_out, or_10_out,
       or_11_out, or_12_out, or_13_out, or_14_out, or_15_out, S_LATCH_2_qn, S_LATCH_3_qn, S_LATCH_4_qn,
       S_LATCH_5_qn, S_LATCH_6_qn, S_LATCH_7_q, S_LATCH_8_qn, S_LATCH_9_q, S_LATCH_9_qn, S_LATCH_10_qn,
       S_LATCH_11_qn, S_LATCH_12_qn, S_LATCH_q, s_r_ff_1_q, s_r_ff_1_qn, s_r_ff_2_qn;

  and and_1 (and_1_out, M1, INT_ACK);
  or or_1 (or_1_out, ~S_LATCH_q, T2);  // OR_Gate
  or or_2 (or_2_out, GRP_IO, and_1_out);
  nand nand_1 (nand_1_out, or_1_out, or_2_out);
  D_LATCH d_latch_1 (.EN(CLK), .D(T2), .Q(d_latch_1_q));  // open: nQ
  D_LATCH d_latch_2 (.EN(CLK), .D(nand_1_out), .Q(d_latch_2_q));  // open: nQ
  nand nand_2 (nand_2_out, INT_ACK, d_latch_1_q, M1);
  and and_2 (and_2_out, d_latch_2_q, WAIT);
  nand nand_3 (nand_3_out, WAIT, d_latch_2_q);
  D_Flip_Flop #(.trigger("high")) S_LATCH (.clk(CLK), .D(nand_2_out), .Q(S_LATCH_q));  // open: Qn, preset, en, reset
  S_R_Flip_Flop #(.trigger("high")) s_r_ff_1 (
    .S(and_2_out), .clk(CLK), .R(nand_3_out), .Q(s_r_ff_1_q), .Qn(s_r_ff_1_qn));  // open: preset, reset, en
  or or_3 (or_3_out, CLK, s_r_ff_1_q);
  or or_4 (or_4_out, s_r_ff_1_qn, CLK);
  and and_3 (and_3_out, ~GRP_M_HL, ~IDX_SET);  // AND_Gate
  and and_4 (and_4_out, or_3_out, nand_4_out);
  and and_5 (and_5_out, w151, ~w155, ~GRP_220);  // AND_Gate
  or or_5 (or_5_out, GRP_220, and_3_out);
  nor nor_1 (nor_1_out, DIS_WR_ADR, and_4_out);
  nand nand_4 (nand_4_out, nor_1_out, or_4_out);
  and and_6 (and_6_out, ~IDX_SET, ~GRP_M_HL);  // AND_Gate
  and and_7 (and_7_out, GRP_M_HL, GRP_239);
  and and_8 (and_8_out, M1, GRP_N8);
  nor nor_2 (nor_2_out, and_6_out, and_7_out);
  or or_6 (or_6_out, M2, and_8_out);
  nand nand_5 (nand_5_out, ~T2, ~S_LATCH_9_qn);  // NAND_Gate
  and and_9 (and_9_out, COND_DONE, and_5_out);
  and and_10 (and_10_out, and_5_out, M3);
  nor nor_3 (nor_3_out, ~w164, ~w151);  // NOR_Gate
  not not_1 (not_1_out, nRES_TCLK);
  and and_11 (and_11_out, nor_2_out, or_6_out);
  and and_12 (and_12_out, nRES_TCLK, ~BUS_Z);  // AND_Gate
  and and_13 (and_13_out, ~T3, nand_5_out);  // AND_Gate
  or or_7 (or_7_out, ~w151, and_9_out);  // OR_Gate
  or or_8 (or_8_out, and_10_out, M4);
  or or_9 (or_9_out, nor_3_out, ~w151);  // OR_Gate
  D_LATCH d_latch_3 (.EN(CLK), .D(not_1_out), .Q(d_latch_3_q));  // open: nQ
  D_LATCH d_latch_4 (.EN(CLK), .D(nRES_MCLK), .Q(d_latch_4_q));  // open: nQ
  D_LATCH d_latch_5 (.EN(CLK), .D(M1), .Q(d_latch_5_q));  // open: nQ
  D_LATCH d_latch_6 (.EN(CLK), .D(M2), .nQ(d_latch_6_nq));  // open: Q
  D_LATCH d_latch_7 (.EN(CLK), .D(M3), .Q(d_latch_7_q));  // open: nQ
  D_LATCH d_latch_8 (.EN(CLK), .D(M4), .Q(d_latch_8_q));  // open: nQ
  D_LATCH d_latch_9 (.EN(CLK), .D(and_11_out), .Q(d_latch_9_q));  // open: nQ
  D_LATCH d_latch_10 (.EN(CLK), .D(and_12_out), .Q(d_latch_10_q));  // open: nQ
  D_LATCH d_latch_11 (.EN(CLK), .D(T1), .Q(d_latch_11_q));  // open: nQ
  D_LATCH d_latch_12 (.EN(CLK), .D(and_13_out), .Q(d_latch_12_q));  // open: nQ
  D_LATCH d_latch_13 (.EN(CLK), .D(T3), .Q(d_latch_13_q));  // open: nQ
  D_LATCH d_latch_14 (.EN(CLK), .D(T4), .Q(d_latch_14_q));  // open: nQ
  D_LATCH d_latch_15 (.EN(CLK), .D(T5), .Q(d_latch_15_q));  // open: nQ
  and and_14 (and_14_out, w142, M4);
  and and_15 (and_15_out, ~PLA88, M5);  // AND_Gate
  and and_16 (and_16_out, M3, or_7_out);
  and and_17 (and_17_out, GRP_BLOCK, or_8_out);
  and and_18 (and_18_out, w155, or_9_out);
  or or_10 (or_10_out, d_latch_9_q, d_latch_7_q);
  or or_11 (or_11_out, M2, and_14_out, and_15_out, and_16_out);
  or or_12 (or_12_out, and_18_out, PLA98);
  and and_19 (and_19_out, GRP_239, ~or_5_out);  // AND_Gate
  not not_2 (not_2_out, CLK);
  and and_20 (and_20_out, T5, w190);
  and and_21 (and_21_out, M1, T4, w149);
  and and_22 (and_22_out, T3, or_11_out);
  and and_23 (and_23_out, T4, and_17_out);
  and and_24 (and_24_out, M1, w139);
  and and_25 (and_25_out, M3, or_12_out);
  and and_26 (and_26_out, M4, ~w164);  // AND_Gate
  and and_27 (and_27_out, M2, and_19_out, ~GRP_N8);  // AND_Gate
  and and_28 (and_28_out, ~CLK, d_latch_3_q);  // AND_Gate
  and and_29 (and_29_out, ~d_latch_4_q, ~d_latch_9_q, d_latch_5_q);  // AND_Gate
  nor nor_4 (nor_4_out, d_latch_4_q, d_latch_9_q, d_latch_6_nq);
  and and_30 (and_30_out, ~d_latch_4_q, or_10_out);  // AND_Gate
  and and_31 (and_31_out, ~d_latch_4_q, d_latch_8_q);  // AND_Gate
  and and_32 (and_32_out, M2, or_5_out, T2);
  or or_13 (or_13_out, M1, M4);
  and and_33 (and_33_out, d_latch_10_q, d_latch_11_q);
  nand nand_6 (nand_6_out, d_latch_10_q, d_latch_12_q);
  and and_34 (and_34_out, d_latch_10_q, d_latch_13_q);
  and and_35 (and_35_out, d_latch_10_q, d_latch_14_q);
  and and_36 (and_36_out, d_latch_10_q, d_latch_15_q);
  nor nor_5 (nor_5_out, and_20_out, and_21_out);
  nor nor_6 (nor_6_out, and_22_out, T6, and_23_out);
  D_Flip_Flop #(.trigger("high")) S_LATCH_2 (
    .clk(and_28_out), .D(d_latch_4_q), .Qn(S_LATCH_2_qn));  // open: Q, preset, en, reset
  D_Flip_Flop #(.trigger("high")) S_LATCH_3 (
    .clk(and_28_out), .D(and_29_out), .Qn(S_LATCH_3_qn));  // open: Q, preset, en, reset
  D_Flip_Flop #(.trigger("high")) S_LATCH_4 (
    .clk(and_28_out), .D(nor_4_out), .Qn(S_LATCH_4_qn));  // open: Q, preset, en, reset
  D_Flip_Flop #(.trigger("high")) S_LATCH_5 (
    .clk(and_28_out), .D(and_30_out), .Qn(S_LATCH_5_qn));  // open: Q, preset, en, reset
  D_Flip_Flop #(.trigger("high")) S_LATCH_6 (
    .clk(and_28_out), .D(and_31_out), .Qn(S_LATCH_6_qn));  // open: Q, preset, en, reset
  S_R_Flip_Flop #(.trigger("high")) s_r_ff_2 (
    .S(and_32_out), .clk(CLK), .R(or_13_out), .Qn(s_r_ff_2_qn));  // open: Q, preset, reset, en
  D_Flip_Flop #(.trigger("high")) S_LATCH_7 (
    .clk(not_2_out), .D(d_latch_10_q), .Q(S_LATCH_7_q));  // open: Qn, preset, en, reset
  D_Flip_Flop #(.trigger("high")) S_LATCH_8 (
    .clk(not_2_out), .D(and_33_out), .Qn(S_LATCH_8_qn));  // open: Q, preset, en, reset
  D_Flip_Flop #(.trigger("high")) S_LATCH_9 (
    .clk(not_2_out), .D(nand_6_out), .Q(S_LATCH_9_q), .Qn(S_LATCH_9_qn));  // open: preset, en, reset
  D_Flip_Flop #(.trigger("high")) S_LATCH_10 (
    .clk(not_2_out), .D(and_34_out), .Qn(S_LATCH_10_qn));  // open: Q, preset, en, reset
  D_Flip_Flop #(.trigger("high")) S_LATCH_11 (
    .clk(not_2_out), .D(and_35_out), .Qn(S_LATCH_11_qn));  // open: Q, preset, en, reset
  D_Flip_Flop #(.trigger("high")) S_LATCH_12 (
    .clk(not_2_out), .D(and_36_out), .Qn(S_LATCH_12_qn));  // open: Q, preset, en, reset
  or or_14 (or_14_out, ~nor_5_out, ~nor_6_out);  // OR_Gate
  or or_15 (or_15_out, RES, and_25_out, and_26_out, and_26_out, and_27_out, M5);
  not W131 (M1, S_LATCH_2_qn);
  not W120 (M2, S_LATCH_3_qn);
  not W127 (M3, S_LATCH_4_qn);
  not W123 (M4, S_LATCH_5_qn);
  not W121 (M5, S_LATCH_6_qn);
  not W115 (M6, s_r_ff_2_qn);
  nor nor_7 (T1, BUS_Z, S_LATCH_7_q);
  not not_3 (T2, S_LATCH_8_qn);
  and and_37 (T3, ~nor_1_out, ~S_LATCH_9_q);  // AND_Gate
  not not_4 (T4, S_LATCH_10_qn);
  not not_5 (T5, S_LATCH_11_qn);
  not not_6 (T6, S_LATCH_12_qn);
  and and_38 (nRES_TCLK, ~or_14_out, ~RES);  // AND_Gate
  or or_16 (nRES_MCLK, and_24_out, or_15_out, COND_DONE);
  // NOT_Gate not_7 is placed but not wired

  // Notes on the sheet:
  //   L82
  //   DL W38
  //   RS37
  //   RS39
  //   INT T2 DEL
  //   W140
  //   W126
  //   W40
  //   W40_i
  //   W125
  //   W141
  //   DL36
  //   DW130
  //   DL32
  //   DL35
  //   DL34
  //   DL33
  //   DW134
  //   DW112
  //   L31
  //   DL31
  //   L12
  //   DL12
  //   L30
  //   DL30
  //   L25
  //   DL25
  //   L21
  //   DL21
  //   W138
  //   W143
  //   W132
  //   W130
  //   W119
  //   W128
  //   W124
  //   W122
  //   W112
  //   W532
  //   W34_v
  //   W530
  //   W68_v
  //   W60
  //   W135
  //   W136
  //   W117
  //   RS131
  //   RS120
  //   RS127
  //   RS123
  //   RS121
  //   RS115
  //   RS111
  //   RS114
  //   RS34
  //   RS109
  //   RS68
  //   RS61
  //   W137
endmodule

module FLAGS (
  input  CLK,
  input  KEEP_FLAGS,
  input  SET_PV_Z_S,
  input  [7:0] ALU,
  input  [7:0] LBUS,
  output F_S,
  output F_Z,
  output F_N,
  output F_C,
  output F_H,
  output F_PV
);

  wire and_1_out, and_2_out, and_3_out, and_4_out, and_5_out, and_6_out, and_7_out, and_8_out, and_9_out,
       and_10_out, and_11_out, and_12_out, and_13_out, and_14_out, and_15_out, and_16_out, and_17_out,
       and_18_out, and_19_out, and_20_out, and_21_out, and_22_out, and_23_out, and_24_out, and_25_out,
       and_26_out, and_27_out, d_ff_2_q, d_ff_3_q, d_latch_1_q, IA_3, L62, L75, M3, M6, multiplexer_1_out,
       nand_1_out, nand_2_out, or_1_out, or_2_out, or_3_out, or_4_out, or_5_out, or_6_out, or_7_out,
       or_8_out, or_9_out, or_10_out, or_11_out, or_12_out, or_13_out, or_14_out, or_15_out, or_16_out,
       PLA_30, T3, T4, T5, W160, W423, W436, w436_t, W437, W438, W439, W449, W452, W453, W458, W459, W460,
       W461, W462, W463, w465, w466, W470, W471, W472, W474, W477, W506, W507, W508, xor_1_out, xor_2_out;

  and and_1 (and_1_out, ~CLK, W470);  // AND_Gate
  xor xor_1 (xor_1_out, W506, L62);
  or or_1 (or_1_out, W453, xor_2_out);
  xor xor_2 (xor_2_out, W507, W508);
  Multiplexer #(.disabled(0), .enable("false")) multiplexer_1 (
    .in0(xor_1_out), .in1(or_1_out), .out(multiplexer_1_out), .sel(W452));
  or or_2 (or_2_out, ALU[0], ALU[1], ALU[2], ALU[3], d_ff_2_q, d_ff_2_q, ALU[4], ALU[5], ALU[6], ALU[7]);
  and and_2 (and_2_out, W472, and_1_out);
  and and_3 (and_3_out, W471, and_1_out);
  and and_4 (and_4_out, ~IA_3, PLA_30);  // AND_Gate
  or or_3 (or_3_out, and_4_out, W160);
  and and_5 (and_5_out, SET_PV_Z_S, ~ALU[7]);  // AND_Gate
  and and_6 (and_6_out, KEEP_FLAGS, ~LBUS[7]);  // AND_Gate
  and and_7 (and_7_out, w436_t, 1'b0);
  and and_8 (and_8_out, LBUS[6], KEEP_FLAGS);
  and and_9 (and_9_out, SET_PV_Z_S, or_2_out);
  and and_10 (and_10_out, KEEP_FLAGS, ~LBUS[1]);  // AND_Gate
  and and_11 (and_11_out, w465, ~LBUS[7]);  // AND_Gate
  and and_12 (and_12_out, w466, or_3_out);
  and and_13 (and_13_out, W477, W458);
  and and_14 (and_14_out, 1'b0, W474);
  and and_15 (and_15_out, W471, and_1_out, ~LBUS[7]);  // AND_Gate
  and and_16 (and_16_out, W472, and_1_out, ~LBUS[0]);  // AND_Gate
  and and_17 (and_17_out, KEEP_FLAGS, ~LBUS[0]);  // AND_Gate
  and and_18 (and_18_out, W463, ~F_H);  // AND_Gate
  and and_19 (and_19_out, W459, ~1'b0);  // AND_Gate
  and and_20 (and_20_out, W460, ~1'b1);  // AND_Gate
  and and_21 (and_21_out, W461, ~W423);  // AND_Gate
  and and_22 (and_22_out, W462, L75);
  and and_23 (and_23_out, KEEP_FLAGS, ~LBUS[2]);  // AND_Gate
  and and_24 (and_24_out, W437, ~W438);  // AND_Gate
  and and_25 (and_25_out, SET_PV_Z_S, multiplexer_1_out);
  and and_26 (and_26_out, W436, ~1'b0);  // AND_Gate
  and and_27 (and_27_out, W439, ~W449);  // AND_Gate
  or or_4 (or_4_out, SET_PV_Z_S, KEEP_FLAGS);
  or or_5 (or_5_out, and_5_out, and_6_out);
  or or_6 (or_6_out, SET_PV_Z_S, KEEP_FLAGS, w436_t);
  or or_7 (or_7_out, and_7_out, and_8_out, and_9_out);
  or or_8 (or_8_out, KEEP_FLAGS, w465, w466);
  or or_9 (or_9_out, and_10_out, and_11_out, and_12_out);
  or or_10 (or_10_out, KEEP_FLAGS, W463, and_2_out, and_3_out, W474, W458);
  or or_11 (or_11_out, and_13_out, and_14_out, and_15_out, and_16_out, and_17_out, and_18_out);
  or or_12 (or_12_out, W462, W461, W460, W459);
  or or_13 (or_13_out, and_19_out, and_20_out, and_21_out, and_22_out);
  or or_14 (or_14_out, W439, W436, SET_PV_Z_S, W437, KEEP_FLAGS);
  or or_15 (or_15_out, and_23_out, and_24_out, and_25_out, and_26_out, and_27_out);
  D_Flip_Flop #(.trigger("high")) d_ff_1 (.clk(or_4_out), .D(or_5_out), .Q(F_S));  // open: Qn, preset, en, reset
  D_Flip_Flop #(.trigger("high")) d_ff_2 (.clk(or_6_out), .D(or_7_out), .Q(d_ff_2_q));  // open: Qn, preset, en, reset
  D_Flip_Flop #(.trigger("high")) d_ff_3 (.clk(or_8_out), .D(or_9_out), .Q(d_ff_3_q));  // open: Qn, preset, en, reset
  D_Flip_Flop #(.trigger("high")) d_ff_4 (.clk(or_10_out), .D(or_11_out), .Q(F_C));  // open: Qn, preset, en, reset
  D_Flip_Flop #(.trigger("high")) d_ff_5 (.clk(or_12_out), .D(or_13_out), .Q(F_H));  // open: Qn, preset, en, reset
  D_Flip_Flop #(.trigger("high")) d_ff_6 (.clk(or_14_out), .D(or_15_out), .Q(F_PV));  // open: Qn, preset, en, reset
  or or_16 (or_16_out, T3, T4, T5);
  nand nand_1 (nand_1_out, M3, or_16_out);
  not not_1 (F_Z, d_ff_2_q);
  D_LATCH d_latch_1 (.EN(CLK), .D(nand_1_out), .Q(d_latch_1_q));  // open: nQ
  nand nand_2 (nand_2_out, M6, d_latch_1_q);
  nand nand_3 (F_N, d_ff_3_q, nand_2_out);

  // Other names for the same wires on the sheet: ALU_0 = ALU[0]; ALU_1 = ALU[1]; ALU_2 = ALU[2]; ALU_3 = ALU[3];
  //   ALU_4 = ALU[4]; ALU_5 = ALU[5]; ALU_6 = ALU[6]; ALU_7 = ALU[7]; LBUS_0 = LBUS[0]; LBUS_1 = LBUS[1];
  //   LBUS_2 = LBUS[2]; LBUS_3 = LBUS[3]; LBUS_4 = LBUS[4]; LBUS_5 = LBUS[5]; LBUS_6 = LBUS[6]; LBUS_7 = LBUS[7]

  // Notes on the sheet:
  //   W457
  //   W464
  //   W397
  //   L72
endmodule

module ALU (
);

  ALU_OPS alu_ops_1 ();  // open: DISABLE_CARRY, FORCE_OR, DISABLE_XOR, CIN, O1, O2, ALU_COUT, ALU_OUT, CARRY_OUT
endmodule

module REGISTER_CONTROL (
  input  CLK,
  input  RES,
  input  M1,
  input  M2,
  input  M3,
  input  M4,
  input  M5,
  input  M6,
  input  T1,
  input  T2,
  input  T3,
  input  T4,
  input  T5,
  input  T6,
  input  IA0,
  input  IA1,
  input  IA2,
  input  IA3,
  input  IA4,
  input  IA5,
  input  W163,
  input  W175,
  input  W185,
  input  W188,
  input  W189,
  input  W182,
  input  W191,
  input  W254,
  input  IDX_SET,
  input  SEL_PCR_DST,
  input  SEL_PCR_SRC,
  input  REQ_REG_DST,
  input  SEL_RST_NMI_IM1,
  input  SEL_IM2,
  input  SEL_ACC,
  input  GRP_M_HL,
  input  GRP_A_MEM_IO,
  input  GRP_IDX,
  input  GRP_220,
  input  GRP_387,
  input  GRP_488,
  input  GRP_BLOCK,
  input  GRP_SP,
  input  ADD_SUB_HL,
  input  R16_TO_DIR,
  input  GRP_R16_DIR,
  input  GRP_DST_AF,
  input  REQ_FLAGS,
  input  PLA37,
  input  PLA59,
  input  PLA66,
  input  PLA71,
  input  PLA73,
  input  PLA75,
  input  PLA77,
  input  PLA78,
  input  PLA80,
  input  PLA81,
  input  PLA83,
  input  PLA88,
  input  PLA89,
  input  PLA90,
  input  PLA91,
  input  PLA93,
  input  PLA94,
  input  PLA95,
  input  PLA96,
  input  PLA97,
  output SEL_IR,
  output SEL_WZ,
  output SEL_AF,
  output SEL_AF2,
  output SEL_SP,
  output SEL_PC,
  output SEL_BC,
  output SEL_BC2,
  output SEL_DE,
  output SEL_DE2,
  output SEL_HL,
  output SEL_HL2,
  output SEL_IX,
  output SEL_IY,
  output RL_WR,
  output RH_WR,
  output R_L,
  output R_H
);

  wire and_1_out, and_2_out, and_3_out, and_4_out, and_5_out, and_6_out, and_7_out, and_8_out, and_9_out,
       and_10_out, and_11_out, and_12_out, and_13_out, and_14_out, and_15_out, and_16_out, and_17_out,
       and_18_out, and_19_out, and_20_out, and_21_out, and_22_out, and_23_out, and_24_out, and_25_out,
       and_26_out, and_27_out, and_28_out, and_29_out, and_30_out, and_31_out, and_32_out, and_33_out,
       and_34_out, and_35_out, and_36_out, and_37_out, and_38_out, and_39_out, and_40_out, and_41_out,
       and_42_out, and_43_out, and_44_out, and_45_out, and_46_out, and_47_out, and_48_out, and_49_out,
       and_50_out, and_51_out, and_52_out, and_53_out, and_54_out, and_55_out, and_56_out, and_57_out,
       and_58_out, and_59_out, and_60_out, and_61_out, and_62_out, and_63_out, and_64_out, and_65_out,
       and_66_out, and_67_out, and_68_out, and_69_out, and_70_out, and_71_out, and_72_out, and_73_out,
       and_74_out, and_75_out, and_76_out, and_77_out, and_78_out, and_79_out, and_80_out, and_81_out,
       and_82_out, and_83_out, and_84_out, and_85_out, and_86_out, and_87_out, and_88_out, and_89_out,
       and_90_out, and_91_out, and_92_out, and_93_out, and_94_out, and_95_out, and_96_out, and_97_out,
       and_98_out, and_99_out, and_100_out, and_101_out, and_102_out, and_103_out, d_latch_1_q, d_latch_2_q,
       d_latch_3_q, d_latch_4_q, d_latch_5_q, d_latch_6_q, d_latch_8_q, d_latch_9_q, d_latch_10_q,
       d_latch_11_q, d_latch_12_q, d_latch_13_q, d_latch_15_q, d_latch_16_q, d_latch_17_q, d_latch_18_q,
       d_latch_19_q, d_latch_20_q, d_latch_21_nq, d_latch_22_nq, M1_T2_C, multiplexer_1_out,
       multiplexer_2_out, multiplexer_3_out, nand_4_out, nand_5_out, nand_10_out, nand_11_out, nand_14_out,
       nand_15_out, nand_16_out, nand_17_out, nand_18_out, nand_19_out, nor_1_out, nor_2_out, nor_6_out,
       nor_7_out, nor_8_out, nor_9_out, nor_10_out, nor_11_out, nor_13_out, nor_14_out, nor_17_out,
       nor_18_out, nor_19_out, nor_20_out, nor_21_out, nor_22_out, nor_23_out, nor_24_out, nor_25_out,
       nor_26_out, nor_27_out, nor_28_out, nor_29_out, nor_30_out, nor_31_out, nor_32_out, nor_33_out,
       nor_34_out, nor_35_out, or_1_out, or_2_out, or_3_out, or_4_out, or_5_out, or_6_out, or_7_out,
       or_8_out, or_9_out, or_10_out, or_11_out, or_12_out, or_13_out, or_14_out, or_15_out, or_16_out,
       or_17_out, or_18_out, or_19_out, or_20_out, or_21_out, or_22_out, or_23_out, or_24_out, or_25_out,
       or_26_out, or_27_out, or_28_out, or_29_out, or_30_out, or_31_out, or_32_out, or_33_out, or_34_out,
       or_35_out, or_36_out, or_37_out, or_38_out, or_39_out, or_40_out, or_41_out, or_42_out, or_43_out,
       or_44_out, or_45_out, or_46_out, or_47_out, or_48_out, or_49_out, or_50_out, or_51_out, or_52_out,
       or_56_out, REG0, REG1, REG2, REQ_AF, REQ_BC, REQ_DD, REQ_DE, REQ_HL1, REQ_HL2, REQ_IDX, REQ_PAIR,
       REQ_PC, REQ_QQ, REQ_SP, RS327_q, RS327_qn, RS330_q, RS330_qn, RS332_q, RS332_qn, RS361_q, RS361_qn,
       S_LATCH_q, SEL_REG_DST, SEL_REG_DST_R, SEL_REG_SRC, SEL_REG_SRC_R;

  or or_1 (or_1_out, M3, M4);
  or or_2 (or_2_out, T4, T5);
  or or_3 (or_3_out, PLA89, PLA90);
  or or_4 (or_4_out, M2, M3);
  or or_5 (or_5_out, M4, M5);
  nor nor_1 (nor_1_out, ~GRP_387, GRP_R16_DIR);  // NOR_Gate
  or or_6 (or_6_out, M4, M5);
  nor nor_2 (nor_2_out, GRP_BLOCK, PLA77);
  and and_1 (and_1_out, PLA83, M3);
  and and_2 (and_2_out, ADD_SUB_HL, M4);
  or or_7 (or_7_out, M4, M5);
  or or_8 (or_8_out, ADD_SUB_HL, ~W191);  // OR_Gate
  or or_9 (or_9_out, PLA77, PLA81);
  or or_10 (or_10_out, ~W185, SEL_RST_NMI_IM1);  // OR_Gate
  or or_11 (or_11_out, M4, M5);
  and and_3 (and_3_out, T2, M2);
  and and_4 (and_4_out, T3, M3);
  or or_12 (or_12_out, M2, M3);
  and and_5 (and_5_out, T2, M2, ~SEL_IM2);  // AND_Gate
  or or_13 (or_13_out, ~SEL_IM2, ~GRP_SP);  // OR_Gate
  or or_14 (or_14_out, M1, M3);
  or or_15 (or_15_out, T4, T5);
  or or_16 (or_16_out, ~GRP_SP, PLA93);  // OR_Gate
  and and_6 (and_6_out, ~GRP_SP, or_1_out);  // AND_Gate
  and and_7 (and_7_out, ~GRP_SP, GRP_387, M5);  // AND_Gate
  and and_8 (and_8_out, M1, or_3_out);
  and and_9 (and_9_out, T3, or_4_out, PLA91);
  or or_17 (or_17_out, ADD_SUB_HL, PLA88, R16_TO_DIR);
  and and_10 (and_10_out, nor_1_out, T3, or_6_out);
  and and_11 (and_11_out, T1, ~GRP_A_MEM_IO, M4);  // AND_Gate
  and and_12 (and_12_out, T3, ~GRP_A_MEM_IO, GRP_387, M4);  // AND_Gate
  and and_13 (and_13_out, T4, PLA73, M1);
  and and_14 (and_14_out, T2, GRP_DST_AF, M1);
  and and_15 (and_15_out, nor_2_out, T2, M2);
  or or_18 (or_18_out, and_1_out, and_2_out);
  and and_16 (and_16_out, T3, or_7_out, ADD_SUB_HL);
  and and_17 (and_17_out, T5, PLA78, M1);
  and and_18 (and_18_out, T4, or_8_out, M1);
  and and_19 (and_19_out, T2, PLA77, M3);
  and and_20 (and_20_out, T3, or_9_out, M2);
  and and_21 (and_21_out, M4, T1, ~GRP_BLOCK);  // AND_Gate
  and and_22 (and_22_out, T1, or_10_out, or_11_out);
  or or_19 (or_19_out, and_3_out, and_4_out);
  and and_23 (and_23_out, or_12_out, T1, ~SEL_IM2);  // AND_Gate
  and and_24 (and_24_out, M2, ~PLA78);  // AND_Gate
  or or_20 (or_20_out, and_24_out, and_26_out);
  and and_25 (and_25_out, M2, T1, ~W188);  // AND_Gate
  and and_26 (and_26_out, M3, ~GRP_BLOCK);  // AND_Gate
  and and_27 (and_27_out, M1, T5, PLA77);
  or or_21 (or_21_out, and_26_out, and_28_out);
  and and_28 (and_28_out, M1, ~W188);  // AND_Gate
  and and_29 (and_29_out, or_13_out, or_14_out, or_15_out);
  and and_30 (and_30_out, M1, or_16_out, T5);
  or or_22 (or_22_out, and_6_out, and_7_out);
  or or_23 (or_23_out, M5, and_8_out);
  and and_31 (and_31_out, or_17_out, T1, or_5_out);
  and and_32 (and_32_out, T4, or_18_out);
  and and_33 (and_33_out, ~W175, or_19_out);  // AND_Gate
  and and_34 (and_34_out, T3, or_20_out);
  and and_35 (and_35_out, T4, or_21_out);
  and and_36 (and_36_out, T2, or_22_out);
  and and_37 (and_37_out, or_2_out, or_23_out);
  nor nor_3 (REQ_AF, and_11_out, and_12_out, and_13_out, and_14_out);
  nor nor_4 (REQ_HL1, and_15_out, and_32_out, and_16_out);
  nor nor_5 (REQ_HL2, and_17_out, and_18_out, and_19_out, and_20_out);
  nor nor_6 (nor_6_out, and_21_out, and_22_out);
  nor nor_7 (nor_7_out, and_33_out, and_23_out);
  nor nor_8 (nor_8_out, and_5_out, and_29_out);
  nor nor_9 (nor_9_out, and_30_out, and_36_out);
  nor nor_10 (nor_10_out, and_37_out, and_9_out);
  nor nor_11 (nor_11_out, and_31_out, and_10_out);
  nand nand_1 (REQ_PC, nor_6_out, nor_7_out);
  nor nor_12 (REQ_BC, and_34_out, and_25_out, and_27_out, and_35_out);
  nand nand_2 (REQ_SP, nor_8_out, nor_9_out);
  nand nand_3 (REQ_DD, nor_10_out, nor_11_out);
  nor nor_13 (nor_13_out, REG2, REG1);
  or or_24 (or_24_out, nor_13_out, REG0);
  and and_38 (and_38_out, SEL_REG_SRC_R, nor_14_out);
  and and_39 (and_39_out, SEL_REG_DST_R, nor_14_out);
  nor nor_14 (nor_14_out, REG0, nor_13_out);
  and and_40 (and_40_out, or_24_out, SEL_REG_DST_R);
  and and_41 (and_41_out, or_24_out, SEL_REG_SRC_R);
  and and_42 (and_42_out, T2, M2);
  and and_43 (and_43_out, T3, M3);
  or or_25 (or_25_out, T1, T3);
  or or_26 (or_26_out, M4, M5);
  and and_44 (and_44_out, T3, M2);
  and and_45 (and_45_out, T2, M3);
  or or_27 (or_27_out, PLA71, ~W163);  // OR_Gate
  and and_46 (and_46_out, ~W163, GRP_M_HL);  // AND_Gate
  nand nand_4 (nand_4_out, M1_T2_C, PLA96);
  nand nand_5 (nand_5_out, M1_T2_C, PLA97);
  or or_28 (or_28_out, and_42_out, and_43_out);
  or or_29 (or_29_out, and_44_out, and_45_out);
  and and_47 (and_47_out, T1, or_27_out, M4);
  and and_48 (and_48_out, T4, and_46_out, M1);
  nand nand_6 (REQ_IDX, GRP_IDX, or_28_out);
  nor nor_15 (REQ_PAIR, ~SEL_REG_SRC, ~SEL_REG_DST, ~REQ_QQ, REQ_DD);  // NOR_Gate
  nand nand_7 (REQ_QQ, or_25_out, PLA75, or_26_out);
  nand nand_8 (REQ_DE, or_29_out, PLA80);
  nand nand_9 (SEL_REG_DST, T2, ~REQ_REG_DST, M1);  // NAND_Gate
  nor nor_16 (SEL_REG_SRC, and_47_out, and_48_out);
  nand nand_10 (nand_10_out, T4, PLA66, M1);
  and and_49 (and_49_out, nand_5_out, nand_4_out);
  and and_50 (and_50_out, ~RS327_q, ~nand_4_out);  // AND_Gate
  and and_51 (and_51_out, RS327_q, ~nand_4_out);  // AND_Gate
  and and_52 (and_52_out, ~CLK, and_49_out);  // AND_Gate
  and and_53 (and_53_out, ~CLK, and_50_out);  // AND_Gate
  and and_54 (and_54_out, ~CLK, and_51_out);  // AND_Gate
  and and_55 (and_55_out, ~CLK, ~nand_5_out);  // AND_Gate
  nand nand_11 (nand_11_out, T2, M1);
  and and_56 (and_56_out, GRP_387, ~GRP_488);  // AND_Gate
  or or_30 (or_30_out, ~REG1, nand_10_out);  // OR_Gate
  or or_31 (or_31_out, REG1, nand_10_out);
  or or_32 (or_32_out, ADD_SUB_HL, and_56_out, SEL_RST_NMI_IM1);
  or or_33 (or_33_out, R16_TO_DIR, ADD_SUB_HL);
  or or_34 (or_34_out, ~GRP_488, ~GRP_A_MEM_IO);  // OR_Gate
  nand nand_12 (SEL_REG_DST_R, SEL_REG_DST, or_30_out);
  nand nand_13 (SEL_REG_SRC_R, SEL_REG_SRC, or_31_out);
  D_LATCH d_latch_1 (.EN(and_52_out), .D(RS330_qn), .Q(d_latch_1_q));  // open: nQ
  D_LATCH d_latch_2 (.EN(and_52_out), .D(RS330_q), .Q(d_latch_2_q));  // open: nQ
  D_LATCH d_latch_3 (.EN(and_52_out), .D(RS332_qn), .Q(d_latch_3_q));  // open: nQ
  D_LATCH d_latch_4 (.EN(and_52_out), .D(RS332_q), .Q(d_latch_4_q));  // open: nQ
  D_LATCH d_latch_5 (.EN(and_52_out), .D(RS327_qn), .Q(d_latch_5_q));  // open: nQ
  D_LATCH d_latch_6 (.EN(and_52_out), .D(RS327_q), .Q(d_latch_6_q));  // open: nQ
  D_LATCH d_latch_7 (.EN(CLK), .D(nand_11_out), .nQ(M1_T2_C));  // open: Q
  and and_57 (and_57_out, or_32_out, GRP_A_MEM_IO);
  or or_35 (or_35_out, R16_TO_DIR, ~GRP_488);  // OR_Gate
  S_R_Flip_Flop #(.trigger("high")) RS330 (
    .S(d_latch_1_q), .clk(and_53_out), .R(d_latch_2_q), .Q(RS330_q), .Qn(RS330_qn));  // open: preset, reset, en
  S_R_Flip_Flop #(.trigger("high")) RS332 (
    .S(d_latch_3_q), .clk(and_54_out), .R(d_latch_4_q), .Q(RS332_q), .Qn(RS332_qn));  // open: preset, reset, en
  S_R_Flip_Flop #(.trigger("high")) RS327 (
    .S(d_latch_5_q), .clk(and_55_out), .R(d_latch_6_q), .Q(RS327_q), .Qn(RS327_qn));  // open: preset, reset, en
  and and_58 (and_58_out, M2, ~SEL_IM2);  // AND_Gate
  and and_59 (and_59_out, or_33_out, M4);
  and and_60 (and_60_out, ~W189, M1);  // AND_Gate
  or or_36 (or_36_out, T1, T3);
  and and_61 (and_61_out, M5, or_33_out);
  and and_62 (and_62_out, or_34_out, M4);
  and and_63 (and_63_out, T1, ~GRP_488, M5);  // AND_Gate
  and and_64 (and_64_out, T4, or_33_out, M1);
  and and_65 (and_65_out, T1, or_37_out);
  or or_37 (or_37_out, and_58_out, and_59_out);
  and and_66 (and_66_out, T2, M2);
  and and_67 (and_67_out, ~SEL_ACC, REQ_FLAGS);  // AND_Gate
  and and_68 (and_68_out, T4, or_38_out);
  or or_38 (or_38_out, M4, and_60_out);
  and and_69 (and_69_out, M2, ~SEL_IM2, or_36_out);  // AND_Gate
  and and_70 (and_70_out, T1, or_39_out);
  or or_39 (or_39_out, and_61_out, and_62_out);
  and and_71 (and_71_out, T3, GRP_220, M3);
  Multiplexer #(.disabled(0), .enable("false")) multiplexer_1 (
    .in0(RS330_q), .in1(RS332_q), .out(multiplexer_1_out), .sel(RS327_q));
  and and_72 (and_72_out, and_57_out, M4);
  and and_73 (and_73_out, M2, or_35_out, SEL_IM2);
  and and_74 (and_74_out, M3, or_35_out);
  and and_75 (and_75_out, and_57_out, M5);
  or or_40 (or_40_out, T2, ~PLA37);  // OR_Gate
  and and_76 (and_76_out, T3, M2, ~SEL_IM2);  // AND_Gate
  and and_77 (and_77_out, T4, M1, PLA94);
  nor nor_17 (nor_17_out, REG1, REG2);
  and and_78 (and_78_out, SEL_REG_DST, SEL_REG_SRC);
  or or_41 (or_41_out, and_72_out, and_73_out);
  or or_42 (or_42_out, W254, ~SEL_IM2);  // OR_Gate
  or or_43 (or_43_out, ~GRP_A_MEM_IO, ~W189);  // OR_Gate
  or or_44 (or_44_out, and_74_out, and_75_out);
  nor nor_18 (nor_18_out, and_63_out, and_64_out);
  nor nor_19 (nor_19_out, and_65_out, and_66_out);
  nor nor_20 (nor_20_out, and_68_out, and_69_out);
  nor nor_21 (nor_21_out, and_70_out, and_71_out);
  nand nand_14 (nand_14_out, W182, or_40_out);
  nand nand_15 (nand_15_out, T2, M1);
  nor nor_22 (nor_22_out, and_76_out, and_77_out);
  nand nand_16 (nand_16_out, T3, M1);
  nor nor_23 (nor_23_out, REG0, and_78_out);
  nor nor_24 (nor_24_out, REG1, REG2);
  and and_79 (and_79_out, REG1, ~REG2, or_45_out);  // AND_Gate
  or or_45 (or_45_out, REQ_DD, ~REQ_PAIR);  // OR_Gate
  nor nor_25 (nor_25_out, IDX_SET, ~GRP_M_HL);  // NOR_Gate
  and and_80 (and_80_out, or_41_out, T3);
  and and_81 (and_81_out, T2, or_42_out, M3);
  and and_82 (and_82_out, T2, GRP_DST_AF, M1);
  and and_83 (and_83_out, T3, ~GRP_A_MEM_IO, M4);  // AND_Gate
  and and_84 (and_84_out, T5, GRP_220, M3);
  and and_85 (and_85_out, T1, or_43_out, M2);
  and and_86 (and_86_out, T3, or_44_out);
  nand nand_17 (nand_17_out, nor_18_out, nor_19_out);
  nand nand_18 (nand_18_out, nand_15_out, nor_22_out, nand_16_out);
  nor nor_26 (nor_26_out, REQ_SP, ~REQ_AF, ~REQ_BC, ~REQ_DE, ~REQ_HL1, ~REQ_HL2, ~REQ_IDX, ~SEL_ACC);  // NOR_Gate
  and and_87 (and_87_out, nor_17_out, or_46_out);
  or or_46 (or_46_out, ~REQ_QQ, nor_23_out);  // OR_Gate
  and and_88 (and_88_out, REQ_DD, nor_24_out);
  or or_47 (or_47_out, ~REG1, ~REG2, REQ_PAIR);  // OR_Gate
  or or_48 (or_48_out, REG1, ~REG2, REQ_PAIR);  // OR_Gate
  nor nor_27 (nor_27_out, ~REQ_HL1, and_79_out, ~REQ_HL2);  // NOR_Gate
  and and_89 (and_89_out, M1_T2_C, PLA95);
  and and_90 (and_90_out, ~REQ_FLAGS, ~SEL_ACC);  // AND_Gate
  nor nor_28 (nor_28_out, and_80_out, and_81_out);
  nor nor_29 (nor_29_out, and_82_out, and_83_out, and_84_out);
  nor nor_30 (nor_30_out, and_85_out, and_86_out);
  and and_91 (and_91_out, ~IA0, nand_14_out);  // AND_Gate
  and and_92 (and_92_out, ~nand_14_out, ~IA3);  // AND_Gate
  and and_93 (and_93_out, ~IA1, nand_14_out);  // AND_Gate
  and and_94 (and_94_out, ~nand_14_out, ~IA4);  // AND_Gate
  and and_95 (and_95_out, ~IA2, nand_14_out);  // AND_Gate
  and and_96 (and_96_out, ~nand_14_out, ~IA5);  // AND_Gate
  or or_49 (or_49_out, RES, nand_18_out);
  nand nand_19 (nand_19_out, ~REQ_PC, nor_26_out, REQ_PAIR);  // NAND_Gate
  and and_97 (and_97_out, T1, M1, PLA59);
  nor nor_31 (nor_31_out, ~SEL_ACC, and_87_out, ~REQ_AF);  // NOR_Gate
  nor nor_32 (nor_32_out, REQ_SP, and_88_out);
  nor nor_33 (nor_33_out, ~SEL_PCR_DST, REQ_PC, SEL_PCR_SRC);  // NOR_Gate
  and and_98 (and_98_out, REQ_BC, or_47_out);
  and and_99 (and_99_out, REQ_DE, or_48_out);
  or or_50 (or_50_out, nor_27_out, nor_25_out);
  or or_51 (or_51_out, nor_27_out, ~nor_25_out);  // OR_Gate
  and and_100 (and_100_out, or_51_out, REQ_IDX);
  and and_101 (and_101_out, ~CLK, and_89_out);  // AND_Gate
  nor nor_34 (nor_34_out, and_90_out, ~nor_28_out, and_39_out);  // NOR_Gate
  nor nor_35 (nor_35_out, and_40_out, ~nor_29_out, ~nor_30_out);  // NOR_Gate
  or or_52 (or_52_out, and_38_out, nand_17_out, and_67_out);
  or or_53 (REG0, and_91_out, and_92_out);
  or or_54 (REG1, and_93_out, and_94_out);
  or or_55 (REG2, and_95_out, and_96_out);
  or or_56 (or_56_out, and_41_out, nor_20_out, nor_21_out, ~SEL_ACC);  // OR_Gate
  D_LATCH d_latch_8 (.EN(CLK), .D(or_49_out), .Q(d_latch_8_q));  // open: nQ
  D_LATCH d_latch_9 (.EN(CLK), .D(nand_19_out), .Q(d_latch_9_q));  // open: nQ
  D_LATCH d_latch_10 (.EN(CLK), .D(and_97_out), .Q(d_latch_10_q));  // open: nQ
  D_LATCH d_latch_11 (.EN(and_103_out), .D(RS361_qn), .Q(d_latch_11_q));  // open: nQ
  D_LATCH d_latch_12 (.EN(and_103_out), .D(RS361_q), .Q(d_latch_12_q));  // open: nQ
  D_LATCH d_latch_13 (.EN(CLK), .D(nor_31_out), .Q(d_latch_13_q));  // open: nQ
  D_LATCH d_latch_14 (.EN(CLK), .D(nor_32_out), .Q(SEL_SP));  // open: nQ
  D_LATCH d_latch_15 (.EN(CLK), .D(nor_33_out), .Q(d_latch_15_q));  // open: nQ
  D_LATCH d_latch_16 (.EN(CLK), .D(and_98_out), .Q(d_latch_16_q));  // open: nQ
  D_LATCH d_latch_17 (.EN(CLK), .D(and_99_out), .Q(d_latch_17_q));  // open: nQ
  D_LATCH d_latch_18 (.EN(CLK), .D(or_50_out), .Q(d_latch_18_q));  // open: nQ
  D_LATCH d_latch_19 (.EN(CLK), .D(and_100_out), .Q(d_latch_19_q));  // open: nQ
  D_Flip_Flop #(.trigger("high")) S_LATCH (
    .clk(and_101_out), .D(d_latch_20_q), .Q(S_LATCH_q));  // open: Qn, preset, en, reset
  D_LATCH d_latch_20 (.EN(CLK), .D(REG2), .Q(d_latch_20_q));  // open: nQ
  D_LATCH d_latch_21 (.EN(CLK), .D(nor_34_out), .nQ(d_latch_21_nq));  // open: Q
  D_LATCH d_latch_22 (.EN(CLK), .D(nor_35_out), .nQ(d_latch_22_nq));  // open: Q
  D_LATCH d_latch_23 (.EN(CLK), .D(or_52_out), .nQ(R_L));  // open: Q
  D_LATCH d_latch_24 (.EN(CLK), .D(or_56_out), .nQ(R_H));  // open: Q
  and and_102 (and_102_out, ~CLK, d_latch_10_q);  // AND_Gate
  and and_103 (and_103_out, ~CLK, ~d_latch_10_q);  // AND_Gate
  S_R_Flip_Flop #(.trigger("high")) RS361 (
    .S(d_latch_11_q), .clk(and_102_out), .R(d_latch_12_q), .Q(RS361_q), .Qn(RS361_qn));  // open: preset, reset, en
  Multiplexer #(.disabled(0), .enable("false")) multiplexer_2 (
    .in0(d_latch_17_q), .in1(d_latch_18_q), .out(multiplexer_2_out), .sel(multiplexer_1_out));
  Multiplexer #(.disabled(0), .enable("false")) multiplexer_3 (
    .in0(d_latch_18_q), .in1(d_latch_17_q), .out(multiplexer_3_out), .sel(multiplexer_1_out));
  and and_104 (SEL_IR, ~CLK, d_latch_8_q);  // AND_Gate
  or or_57 (SEL_WZ, d_latch_8_q, d_latch_9_q);
  nand nand_20 (SEL_AF, RS361_q, ~d_latch_13_q);  // NAND_Gate
  nand nand_21 (SEL_AF2, RS361_qn, ~d_latch_13_q);  // NAND_Gate
  and and_105 (SEL_PC, ~CLK, d_latch_15_q);  // AND_Gate
  nand nand_22 (SEL_BC, ~RS327_q, ~d_latch_16_q);  // NAND_Gate
  nand nand_23 (SEL_BC2, RS327_q, ~d_latch_16_q);  // NAND_Gate
  nand nand_24 (SEL_DE, ~RS327_q, ~multiplexer_2_out);  // NAND_Gate
  nand nand_25 (SEL_DE2, RS327_q, ~multiplexer_2_out);  // NAND_Gate
  nand nand_26 (SEL_HL, ~RS327_q, ~multiplexer_3_out);  // NAND_Gate
  nand nand_27 (SEL_HL2, RS327_q, ~multiplexer_3_out);  // NAND_Gate
  nand nand_28 (SEL_IX, ~S_LATCH_q, ~d_latch_19_q);  // NAND_Gate
  nand nand_29 (SEL_IY, S_LATCH_q, ~d_latch_19_q);  // NAND_Gate
  and and_106 (RL_WR, ~CLK, d_latch_21_nq);  // AND_Gate
  and and_107 (RH_WR, ~CLK, d_latch_22_nq);  // AND_Gate
  // NOT_Gate not_1 is placed but not wired

  // Notes on the sheet:
  //   W237
  //   W240
  //   W221
  //   W222
  //   W231
  //   W230
  //   W232
  //   W233
  //   W368
  //   W367
  //   W326
  //   W302
  //   W249
  //   W324
  //   W329
  //   W331
  //   W328
  //   W261
  //   L47_i
  //   L47
  //   L48_i
  //   L48
  //   L46_i
  //   L46
  //   W252
  //   W253
  //   DL42
  //   TFF
  //   TFF
  //   TFF
  //   W327
  //   W333
  //   W312
  //   W260
  //   W262
  //   W263
  //   W264
  //   W183
  //   W227
  //   W229
  //   W228
  //   W412
  //   W343
  //   W251
  //   W258
  //   W257
  //   W411
  //   W410
  //   W414
  //   DW307
  //   DL44
  //   DW359
  //   L49_i
  //   L49
  //   L81
  //   DW319
  //   DW298
  //   DW347
  //   DW346
  //   DW345
  //   DW341
  //   W320
  //   DL45
  //   DL79
  //   DW416
  //   DW417
  //   DW418
  //   W362
  //   W360
  //   TFF
endmodule

module PREFIX (
  input  CLK,
  input  RES,
  input  T1,
  input  T2,
  input  T3,
  input  M1,
  input  M3,
  input  M4,
  input  GRP_IDX,
  input  DIS_BASE_SET,
  input  PLA47,
  input  PLA54,
  input  PLA57,
  input  PLA76,
  output PREF_CLK,
  output IDX_CB_LATCH,
  output BASE_SET,
  output ED_SET,
  output IDX_SET,
  output CB_SET,
  output SEL_MASK
);

  wire and_1_out, and_2_out, and_4_out, and_5_out, and_6_out, and_7_out, and_8_out, d_latch_1_q,
       d_latch_3_nq, d_latch_4_q, d_latch_5_q, nor_1_out, nor_2_out, not_1_out, not_2_out, or_1_out,
       S_LATCH_3_q, S_LATCH_3_qn;

  and and_1 (and_1_out, M1, T2);
  and and_2 (and_2_out, T1, M3, IDX_CB_LATCH);
  nor nor_1 (nor_1_out, and_1_out, and_2_out);
  not not_1 (not_1_out, PLA47);
  not not_2 (not_2_out, PLA57);
  D_LATCH d_latch_1 (.EN(CLK), .D(nor_1_out), .Q(d_latch_1_q));  // open: nQ
  D_LATCH d_latch_2 (.EN(CLK), .D(PLA76), .Q(IDX_CB_LATCH));  // open: nQ
  D_LATCH d_latch_3 (.EN(CLK), .D(not_1_out), .nQ(d_latch_3_nq));  // open: Q
  D_LATCH d_latch_4 (.EN(CLK), .D(PLA54), .Q(d_latch_4_q));  // open: nQ
  D_LATCH d_latch_5 (.EN(CLK), .D(not_2_out), .Q(d_latch_5_q));  // open: nQ
  and and_3 (PREF_CLK, ~CLK, ~d_latch_1_q);  // AND_Gate
  and and_4 (and_4_out, PREF_CLK, ~d_latch_4_q);  // AND_Gate
  and and_5 (and_5_out, PREF_CLK, d_latch_4_q);
  D_Flip_Flop #(.trigger("high")) S_LATCH (
    .clk(PREF_CLK), .D(d_latch_3_nq), .Q(ED_SET), .reset(RES));  // open: Qn, preset, en
  D_Flip_Flop #(.trigger("high")) S_LATCH_2 (
    .clk(and_4_out), .D(d_latch_5_q), .Q(IDX_SET), .preset(RES));  // open: Qn, en, reset
  D_Flip_Flop #(.trigger("high")) S_LATCH_3 (
    .clk(PREF_CLK), .D(d_latch_4_q), .Q(S_LATCH_3_q), .Qn(S_LATCH_3_qn), .reset(RES));  // open: preset, en
  or or_1 (or_1_out, S_LATCH_3_q, and_5_out);
  and and_6 (and_6_out, or_1_out, GRP_IDX);
  nor nor_2 (nor_2_out, S_LATCH_3_q, ED_SET);
  and and_7 (and_7_out, T3, or_1_out, M1);
  and and_8 (and_8_out, T1, and_6_out, M4);
  nor nor_3 (BASE_SET, DIS_BASE_SET, ~nor_2_out);  // NOR_Gate
  or or_2 (CB_SET, PREF_CLK, S_LATCH_3_qn);
  nor nor_4 (SEL_MASK, and_7_out, and_8_out);

  // Notes on the sheet:
  //   W102
  //   DL29
  //   DW107
  //   DL43
  //   DW98
  //   DW99
  //   W95
  //   W287
  //   W91
endmodule

module INT_LOGIC (
  input  CLK,
  input  PREF_CLK,
  input  RESET,
  input  INT,
  input  NMI,
  input  nRES_TCLK,
  input  nRES_MCLK,
  input  M1,
  input  T1,
  input  T2,
  input  GRP_PREFIX,
  input  PLA1,
  input  PLA2,
  input  PLA3,
  input  PLA42,
  input  PLA52,
  input  IA3,
  input  IA4,
  output RES,
  output RES2,
  output RESET_PC,
  output SEL_RST_NMI_IM1,
  output SEL_IM1,
  output SEL_IM2,
  output SEL_NMI,
  output DIS_BASE_SET,
  output INT_ACK,
  output HALT_REQ,
  output INT_REQ,
  output NMI_REQ,
  output NMI_ACK,
  output HALT,
  output INT_CLK,
  output IFF2
);

  wire and_1_out, and_2_out, and_3_out, and_4_out, and_5_out, and_6_out, and_8_out, and_9_out, and_10_out,
       and_11_out, and_12_out, and_13_out, and_14_out, and_15_out, and_16_out, d_latch_1_nq, d_latch_1_q,
       d_latch_2_nq, d_latch_2_q, d_latch_3_nq, d_latch_4_q, d_latch_5_q, d_latch_6_nq, d_latch_7_q,
       d_latch_8_nq, d_latch_9_nq, d_latch_10_nq, d_latch_10_q, HALT_RS_q, IFF1, nand_1_out, nand_2_out,
       nand_3_out, nand_4_out, nand_5_out, nNMI, nor_1_out, nor_2_out, nor_3_out, nor_6_out, nor_7_out,
       nor_8_out, nor_9_out, nor_11_out, not_2_out, not_3_out, not_4_out, not_5_out, not_6_out, not_7_out,
       not_8_out, not_9_out, not_10_out, not_11_out, not_12_out, not_14_out, not_15_out, not_16_out,
       not_17_out, not_18_out, or_1_out, or_2_out, or_3_out, or_5_out, or_6_out, or_7_out, or_8_out,
       or_9_out, or_10_out, or_11_out, or_12_out, or_13_out, RES_M1, RS4_q, RS4_qn, RS5_q, RS6_q, RS7_q,
       RS8_q, RS8_qn, RS50_q, RS51_q, RS54_q, RS56_q, RS63_q, S_LATCH_2_qn, W78, W80;

  not not_1 (nNMI, NMI);
  not not_2 (not_2_out, nNMI);
  S_R_Flip_Flop #(.trigger("high")) RS7 (
    .S(not_2_out), .clk(1'b1), .R(d_latch_6_nq), .Q(RS7_q));  // open: Qn, preset, reset, en
  and and_1 (and_1_out, RS7_q, nNMI);
  and and_2 (and_2_out, nNMI, ~RS7_q);  // AND_Gate
  or or_1 (or_1_out, and_2_out, d_latch_6_nq);
  S_R_Flip_Flop #(.trigger("high")) RS6 (
    .S(and_1_out), .clk(1'b1), .R(or_1_out), .Q(RS6_q));  // open: Qn, preset, reset, en
  and and_3 (and_3_out, d_latch_1_nq, ~CLK, ~RES);  // AND_Gate
  and and_4 (and_4_out, ~RS51_q, d_latch_2_q, and_3_out);  // AND_Gate
  and and_5 (and_5_out, RS51_q, and_3_out);
  not not_3 (not_3_out, CLK);
  not not_4 (not_4_out, INT);
  or or_2 (or_2_out, PLA1, ~IFF1);  // OR_Gate
  not not_5 (not_5_out, CLK);
  not not_6 (not_6_out, RS6_q);
  not not_7 (not_7_out, RESET);
  nand nand_1 (nand_1_out, M1, T2);
  or or_3 (or_3_out, RES, and_4_out);
  nand nand_2 (nand_2_out, M1, PLA2, T1);
  S_R_Flip_Flop #(.trigger("high")) RS4 (
    .S(INT), .clk(not_3_out), .R(not_4_out), .Q(RS4_q), .Qn(RS4_qn));  // open: preset, reset, en
  S_R_Flip_Flop #(.trigger("high")) RS8 (
    .S(RS6_q), .clk(not_5_out), .R(not_6_out), .Q(RS8_q), .Qn(RS8_qn));  // open: preset, reset, en
  nor nor_1 (nor_1_out, NMI_ACK, RES);
  nand nand_3 (nand_3_out, M1, PLA1, T1);
  nand nand_4 (nand_4_out, M1, PLA52, T2);
  not not_8 (not_8_out, RESET);
  not not_9 (not_9_out, CLK);
  not not_10 (not_10_out, not_7_out);
  nor nor_2 (nor_2_out, RES, nRES_TCLK, ~nRES_MCLK, ~GRP_PREFIX);  // NOR_Gate
  S_R_Flip_Flop #(.trigger("high")) RS50 (
    .S(not_8_out), .clk(not_9_out), .R(not_10_out), .Q(RS50_q));  // open: Qn, preset, reset, en
  D_LATCH d_latch_1 (.EN(CLK), .D(nand_1_out), .Q(d_latch_1_q), .nQ(d_latch_1_nq));
  S_R_Flip_Flop #(.trigger("high")) RS56 (.S(or_3_out), .R(and_5_out), .Q(RS56_q));  // open: clk, Qn, preset, reset, en
  D_LATCH d_latch_2 (.EN(CLK), .D(GRP_PREFIX), .Q(d_latch_2_q), .nQ(d_latch_2_nq));
  D_LATCH d_latch_3 (.EN(CLK), .D(nand_2_out), .nQ(d_latch_3_nq));  // open: Q
  D_LATCH d_latch_4 (.EN(CLK), .D(RES_M1), .Q(d_latch_4_q));  // open: nQ
  S_R_Flip_Flop #(.trigger("high")) RS5 (.S(RS4_q), .clk(CLK), .R(RS4_qn), .Q(RS5_q));  // open: Qn, preset, reset, en
  D_LATCH d_latch_5 (.EN(CLK), .D(or_2_out), .Q(d_latch_5_q));  // open: nQ
  S_R_Flip_Flop #(.trigger("high")) RS9 (.S(RS8_q), .clk(CLK), .R(RS8_qn), .Q(NMI_REQ));  // open: Qn, preset, reset, en
  D_LATCH d_latch_6 (.EN(CLK), .D(nor_1_out), .nQ(d_latch_6_nq));  // open: Q
  D_LATCH d_latch_7 (.EN(CLK), .D(nor_2_out), .Q(d_latch_7_q));  // open: nQ
  D_LATCH d_latch_8 (.EN(CLK), .D(nand_3_out), .nQ(d_latch_8_nq));  // open: Q
  D_LATCH d_latch_9 (.EN(CLK), .D(nand_4_out), .nQ(d_latch_9_nq));  // open: Q
  or or_4 (RES_M1, RS56_q, d_latch_2_nq);
  and and_6 (and_6_out, W80, INT_ACK);
  nor nor_3 (nor_3_out, INT_ACK, d_latch_4_q);
  nor nor_4 (INT_REQ, RS5_q, d_latch_5_q, NMI_REQ);
  and and_7 (INT_CLK, ~CLK, d_latch_7_q);  // AND_Gate
  and and_8 (and_8_out, ~CLK, d_latch_8_nq);  // AND_Gate
  and and_9 (and_9_out, ~CLK, d_latch_9_nq, ~NMI_ACK);  // AND_Gate
  or or_5 (or_5_out, and_6_out, HALT, NMI_ACK, RES, nor_3_out);
  and and_10 (and_10_out, and_9_out, IFF2);
  and and_11 (and_11_out, and_8_out, IA3);
  not not_11 (not_11_out, RS50_q);
  and and_12 (and_12_out, ~CLK, ~d_latch_3_nq);  // AND_Gate
  or or_6 (or_6_out, RES, ~INT_REQ);  // OR_Gate
  nor nor_5 (HALT_REQ, INT_REQ, ~PLA3, NMI_REQ);  // NOR_Gate
  or or_7 (or_7_out, RES, ~NMI_REQ);  // OR_Gate
  nor nor_6 (nor_6_out, RES, NMI_ACK, INT_ACK, ~RES_M1);  // NOR_Gate
  and and_13 (and_13_out, INT_CLK, HALT_REQ);
  or or_8 (or_8_out, and_8_out, and_9_out);
  or or_9 (or_9_out, and_10_out, and_11_out);
  S_R_Flip_Flop #(.trigger("high")) RS51 (
    .S(RS50_q), .clk(CLK), .R(not_11_out), .Q(RS51_q));  // open: Qn, preset, reset, en
  D_Flip_Flop #(.trigger("high")) S_LATCH (.clk(and_12_out), .D(IA3), .Qn(W78), .reset(RES));  // open: Q, preset, en
  D_Flip_Flop #(.trigger("high")) S_LATCH_2 (
    .clk(and_12_out), .D(IA4), .Q(W80), .Qn(S_LATCH_2_qn), .reset(RES));  // open: preset, en
  D_Flip_Flop #(.trigger("high")) S_LATCH_3 (
    .clk(PREF_CLK), .D(or_5_out), .Q(DIS_BASE_SET), .preset(RES));  // open: Qn, en, reset
  S_R_Flip_Flop #(.trigger("high")) RS18 (
    .S(or_6_out), .clk(INT_CLK), .R(INT_REQ), .Qn(INT_ACK));  // open: Q, preset, reset, en
  S_R_Flip_Flop #(.trigger("high")) RS19 (
    .S(or_7_out), .clk(INT_CLK), .R(NMI_REQ), .Qn(NMI_ACK));  // open: Q, preset, reset, en
  S_R_Flip_Flop #(.trigger("high")) HALT_RS (
    .S(nor_6_out), .clk(1'b1), .R(and_13_out), .Q(HALT_RS_q));  // open: Qn, preset, reset, en
  D_Flip_Flop #(.trigger("high")) S_LATCH_4 (
    .clk(or_8_out), .D(or_9_out), .Q(IFF1), .reset(or_10_out));  // open: Qn, preset, en
  or or_10 (or_10_out, INT_ACK, RES, NMI_ACK);
  D_Flip_Flop #(.trigger("high")) S_LATCH_5 (
    .clk(and_8_out), .D(IA3), .Q(IFF2), .reset(or_11_out));  // open: Qn, preset, en
  or or_11 (or_11_out, RES, INT_ACK);
  and and_14 (and_14_out, M1, ~RES_M1, T1);  // AND_Gate
  not not_12 (not_12_out, HALT_RS_q);
  not not_13 (HALT, not_12_out);
  not not_14 (not_14_out, d_latch_10_q);
  or or_12 (or_12_out, RES, and_14_out);
  and and_15 (and_15_out, ~RS51_q, d_latch_1_q);  // AND_Gate
  not not_15 (not_15_out, CLK);
  and and_16 (and_16_out, d_latch_1_q, RS51_q);
  not not_16 (not_16_out, not_14_out);
  not not_17 (not_17_out, CLK);
  not not_18 (not_18_out, d_latch_10_q);
  nand nand_5 (nand_5_out, W78, INT_ACK);
  nor nor_7 (nor_7_out, PREF_CLK, ~DIS_BASE_SET);  // NOR_Gate
  S_R_Flip_Flop #(.trigger("high")) RS54 (
    .S(and_15_out), .clk(not_15_out), .R(and_16_out), .Q(RS54_q));  // open: Qn, preset, reset, en
  S_R_Flip_Flop #(.trigger("high")) RS63 (
    .S(not_16_out), .clk(not_17_out), .R(not_18_out), .Q(RS63_q));  // open: Qn, preset, reset, en
  D_LATCH d_latch_10 (.EN(CLK), .D(RES), .Q(d_latch_10_q), .nQ(d_latch_10_nq));
  D_LATCH d_latch_11 (.EN(CLK), .D(or_12_out), .Q(RESET_PC));  // open: nQ
  nor nor_8 (nor_8_out, nand_5_out, S_LATCH_2_qn);
  not not_19 (RES, RS54_q);
  nor nor_9 (nor_9_out, CLK, d_latch_10_nq);
  or or_13 (or_13_out, nor_8_out, NMI_ACK);
  and and_17 (SEL_NMI, nor_7_out, NMI_ACK);
  nor nor_10 (RES2, RS63_q, nor_9_out);
  Multiplexer #(.disabled(0), .enable("false")) multiplexer_1 (
    .in0(PLA42), .in1(or_13_out), .out(SEL_RST_NMI_IM1), .sel(nor_7_out));
  nor nor_11 (nor_11_out, ~W80, W78);  // NOR_Gate
  and and_18 (SEL_IM1, nor_7_out, W80, W78, INT_ACK);
  nand nand_6 (SEL_IM2, INT_ACK, nor_7_out, nor_11_out);

  // Notes on the sheet:
  //   W53
  //   DL19
  //   DL20
  //   DW104
  //   DL28
  //   DL17
  //   IRQ C
  //   DL13
  //   DL12
  //   DL4
  //   DL26
  //   DL27
  //   RESET C
  //   INT REQ
  //   NMI REQ
  //   W28
  //   W71
  //   W75
  //   W78_i
  //   W80
  //   D
  //   E
  //   SLATCH
  //   SLATCH
  //   DL23
  //   DL23
  //   W85
  //   W84
  //   SEL INT
endmodule

module PC_CONTROL (
  input  CLK,
  input  RES,
  input  IA3,
  input  HALT,
  input  nRES_MCLK,
  input  nRES_TCLK,
  input  M1,
  input  M2,
  input  M3,
  input  M4,
  input  M5,
  input  T1,
  input  T2,
  input  T3,
  input  T4,
  input  T5,
  input  W170,
  input  W176,
  input  GRP_BLOCK,
  input  SEL_RST_NMI_IM1,
  input  GRP_LDI_CPI,
  input  SEL_IM2,
  input  COND_DONE,
  input  GRP_SP,
  input  GRP_387,
  input  GRP_220,
  input  GRP_M_HL,
  input  GRP_BRANCH,
  input  GRP_IDX,
  input  GRP_N8,
  input  INT_CLK,
  input  INT_REQ,
  input  NMI_REQ,
  input  HALT_REQ,
  input  NMI_ACK,
  input  INT_ACK,
  input  PLA88,
  input  PLA93,
  output INV_PCR,
  output INC_PCR,
  output HI_INC_PCR,
  output R_P,
  output READ_PCR,
  output WRITE_PCR
);

  wire and_1_out, and_2_out, and_3_out, and_4_out, and_5_out, and_6_out, and_7_out, and_8_out, and_9_out,
       and_10_out, and_11_out, and_12_out, and_13_out, and_14_out, and_15_out, and_16_out, and_17_out,
       and_18_out, and_19_out, and_20_out, and_21_out, and_22_out, and_23_out, and_24_out, and_25_out,
       and_26_out, and_27_out, and_28_out, and_29_out, and_30_out, and_31_out, and_32_out, and_33_out,
       and_34_out, and_35_out, and_36_out, and_37_out, and_38_out, and_39_out, and_41_out, and_42_out,
       d_latch_1_q, d_latch_2_nq, d_latch_3_nq, d_latch_4_nq, d_latch_5_q, d_latch_6_nq, d_latch_7_q,
       d_latch_8_q, nand_1_out, nand_2_out, nand_3_out, nand_4_out, nand_5_out, nand_6_out, nCLK, nor_1_out,
       nor_2_out, nor_3_out, nor_4_out, nor_5_out, nor_6_out, nor_7_out, nor_8_out, nor_9_out, nor_10_out,
       nor_13_out, nor_14_out, nor_15_out, nor_16_out, nor_17_out, nor_18_out, nor_19_out, nor_20_out,
       not_2_out, or_1_out, or_2_out, or_3_out, or_4_out, or_5_out, or_6_out, or_7_out, or_8_out, or_9_out,
       or_10_out, or_11_out, or_12_out, or_13_out, or_14_out, or_15_out, or_16_out, or_17_out, or_18_out,
       S_LATCH_2_q, S_LATCH_qn, s_r_ff_1_q, SEL_PCR_DST, SEL_PCR_SRC;

  not not_1 (nCLK, CLK);
  and and_1 (and_1_out, ~PLA88, SEL_IM2);  // AND_Gate
  or or_1 (or_1_out, GRP_220, ~GRP_M_HL);  // OR_Gate
  nand nand_1 (nand_1_out, and_1_out, GRP_BLOCK);
  nand nand_2 (nand_2_out, GRP_BLOCK, or_1_out);
  and and_2 (and_2_out, SEL_IM2, ~PLA88);  // AND_Gate
  or or_2 (or_2_out, GRP_IDX, ~GRP_N8, ~W170);  // OR_Gate
  or or_3 (or_3_out, ~GRP_SP, ~GRP_BLOCK);  // OR_Gate
  or or_4 (or_4_out, M3, M4);
  and and_3 (and_3_out, or_3_out, or_4_out);
  and and_4 (and_4_out, nand_1_out, M2);
  and and_5 (and_5_out, nand_2_out, M4);
  and and_6 (and_6_out, ~GRP_SP, M5, GRP_387);  // AND_Gate
  and and_7 (and_7_out, ~GRP_BLOCK, M3);  // AND_Gate
  and and_8 (and_8_out, M2, and_2_out);
  and and_9 (and_9_out, M1, or_2_out);
  and and_10 (and_10_out, M2, ~W170);  // AND_Gate
  and and_11 (and_11_out, M3, ~GRP_BLOCK);  // AND_Gate
  and and_12 (and_12_out, M2, or_2_out);
  and and_13 (and_13_out, M3, ~W170);  // AND_Gate
  and and_14 (and_14_out, ~GRP_BLOCK, IA3);  // AND_Gate
  and and_15 (and_15_out, ~GRP_SP, ~COND_DONE);  // AND_Gate
  and and_16 (and_16_out, ~GRP_SP, M3);  // AND_Gate
  and and_17 (and_17_out, M3, ~GRP_BLOCK);  // AND_Gate
  or or_5 (or_5_out, and_3_out, M5);
  or or_6 (or_6_out, and_4_out, and_5_out);
  or or_7 (or_7_out, and_6_out, and_7_out);
  or or_8 (or_8_out, ~SEL_IM2, ~GRP_387);  // OR_Gate
  nor nor_1 (nor_1_out, M1, and_8_out, M3);
  nor nor_2 (nor_2_out, COND_DONE, GRP_BRANCH);
  nor nor_3 (nor_3_out, and_9_out, and_10_out, and_11_out);
  or or_9 (or_9_out, M1, and_12_out, and_13_out);
  or or_10 (or_10_out, and_14_out, ~SEL_IM2);  // OR_Gate
  nor nor_4 (nor_4_out, ~SEL_IM2, SEL_RST_NMI_IM1);  // NOR_Gate
  nor nor_5 (nor_5_out, GRP_LDI_CPI, and_15_out);
  or or_11 (or_11_out, M1, and_16_out);
  or or_12 (or_12_out, M5, and_17_out);
  and and_18 (and_18_out, or_5_out, T4);
  and and_19 (and_19_out, or_6_out, T2);
  and and_20 (and_20_out, or_7_out, T2);
  and and_21 (and_21_out, T5, or_8_out, M1);
  and and_22 (and_22_out, T3, M1);
  or or_13 (or_13_out, nRES_MCLK, nor_1_out);
  or or_14 (or_14_out, ~nRES_MCLK, nor_2_out);  // OR_Gate
  and and_23 (and_23_out, or_10_out, M2);
  and and_24 (and_24_out, and_14_out, M3);
  and and_25 (and_25_out, ~GRP_SP, M4, ~GRP_387);  // AND_Gate
  nand nand_3 (nand_3_out, nor_4_out, W176);
  nor nor_6 (nor_6_out, PLA88, nor_5_out);
  or or_15 (or_15_out, and_23_out, and_24_out, and_25_out);
  and and_26 (and_26_out, M1, nand_3_out, T4);
  or or_16 (or_16_out, T1, T3);
  and and_27 (and_27_out, M4, or_16_out, ~GRP_BLOCK);  // AND_Gate
  and and_28 (and_28_out, M3, nor_6_out, T3);
  and and_29 (and_29_out, T2, or_11_out);
  and and_30 (and_30_out, T3, or_12_out);
  and and_31 (and_31_out, T4, M1);
  nor nor_7 (nor_7_out, and_18_out, and_19_out);
  or or_17 (or_17_out, ~nor_7_out, ~nor_8_out);  // OR_Gate
  nor nor_8 (nor_8_out, and_20_out, and_21_out, and_22_out);
  and and_32 (and_32_out, ~nRES_TCLK, or_13_out);  // AND_Gate
  and and_33 (and_33_out, or_14_out, nor_3_out);
  and and_34 (and_34_out, T1, or_9_out);
  nand nand_4 (nand_4_out, or_15_out, T1);
  nor nor_9 (nor_9_out, and_26_out, and_27_out, and_28_out);
  nor nor_10 (nor_10_out, and_29_out, and_30_out, and_31_out);
  nor nor_11 (SEL_PCR_SRC, nRES_TCLK, and_33_out);
  nor nor_12 (SEL_PCR_DST, RES, and_34_out);
  and and_35 (and_35_out, ~RES, ~T1);  // AND_Gate
  and and_36 (and_36_out, PLA93, T4);
  and and_37 (and_37_out, M5, PLA88, T3);
  and and_38 (and_38_out, T3, M1);
  nand nand_5 (nand_5_out, M1, T2);
  or or_18 (or_18_out, ~nand_4_out, ~nor_9_out);  // OR_Gate
  nor nor_13 (nor_13_out, and_36_out, and_37_out);
  nand nand_6 (nand_6_out, and_38_out, nand_5_out);
  nor nor_14 (nor_14_out, ~SEL_PCR_DST, SEL_PCR_SRC);  // NOR_Gate
  nor nor_15 (nor_15_out, ~nor_10_out, ~SEL_PCR_DST, or_17_out, and_32_out);  // NOR_Gate
  nor nor_16 (nor_16_out, or_17_out, ~SEL_PCR_DST);  // NOR_Gate
  D_LATCH d_latch_1 (.EN(CLK), .D(or_18_out), .Q(d_latch_1_q));  // open: nQ
  D_LATCH d_latch_2 (.EN(CLK), .D(nRES_TCLK), .nQ(d_latch_2_nq));  // open: Q
  D_LATCH d_latch_3 (.EN(CLK), .D(and_35_out), .nQ(d_latch_3_nq));  // open: Q
  D_LATCH d_latch_4 (.EN(CLK), .D(nor_13_out), .nQ(d_latch_4_nq));  // open: Q
  D_LATCH d_latch_5 (.EN(CLK), .D(nand_6_out), .Q(d_latch_5_q));  // open: nQ
  D_LATCH d_latch_6 (.EN(CLK), .D(nor_14_out), .nQ(d_latch_6_nq));  // open: Q
  D_LATCH d_latch_7 (.EN(CLK), .D(nor_15_out), .Q(d_latch_7_q));  // open: nQ
  D_LATCH d_latch_8 (.EN(CLK), .D(nor_16_out), .Q(d_latch_8_q));  // open: nQ
  and and_39 (and_39_out, ~nor_17_out, INT_CLK);  // AND_Gate
  and and_40 (R_P, d_latch_5_q, d_latch_6_nq);
  and and_41 (and_41_out, INT_CLK, nor_17_out);
  nor nor_17 (nor_17_out, INT_REQ, NMI_REQ, HALT_REQ);
  nor nor_18 (nor_18_out, and_39_out, NMI_ACK, ~HALT, INT_ACK);  // NOR_Gate
  not not_2 (not_2_out, d_latch_5_q);
  nor nor_19 (nor_19_out, ~d_latch_5_q, d_latch_7_q);  // NOR_Gate
  D_Flip_Flop #(.trigger("high")) S_LATCH (.clk(nCLK), .D(d_latch_1_q), .Qn(S_LATCH_qn));  // open: Q, preset, en, reset
  nor nor_20 (nor_20_out, and_41_out, nor_18_out);
  S_R_Flip_Flop s_r_ff_1 (
    .S(d_latch_2_nq), .clk(nCLK), .R(d_latch_3_nq), .Q(s_r_ff_1_q));  // open: Qn, preset, reset, en
  D_Flip_Flop #(.trigger("high")) S_LATCH_2 (
    .clk(nCLK), .D(d_latch_4_nq), .Q(S_LATCH_2_q));  // open: Qn, preset, en, reset
  S_R_Flip_Flop #(.trigger("high")) s_r_ff_2 (
    .S(not_2_out), .clk(nCLK), .R(nor_19_out), .Q(HI_INC_PCR));  // open: Qn, preset, reset, en
  not not_3 (INV_PCR, S_LATCH_qn);
  and and_42 (and_42_out, nor_20_out, s_r_ff_1_q);
  or or_19 (INC_PCR, and_42_out, S_LATCH_2_q);
  and and_43 (READ_PCR, ~CLK, ~d_latch_7_q);  // AND_Gate
  and and_44 (WRITE_PCR, ~CLK, ~d_latch_8_q);  // AND_Gate

  // Notes on the sheet:
  //   W218
  //   W213
  //   W212
  //   W218
  //   W224
  //   W209
  //   W217
  //   W296
  //   W223
  //   W207
  //   W195
  //   W211
  //   W214
  //   W219
  //   W216
  //   W208
  //   W206
  //   W204
  //   W300
  //   W290
  //   DL40
  //   DL37
  //   DL38
  //   DL39
  //   DW305
  //   DW301
  //   DW293
  //   DW292
  //   W10
  //   W13
  //   RS210
  //   W14
  //   RS144
  //   RS205
  //   RS321
endmodule

module CONDITION_LOGIC (
  input  CLK,
  input  M1,
  input  M2,
  input  M3,
  input  PLA5,
  input  PLA7,
  input  PLA8,
  input  PLA50,
  input  PLA53,
  input  W184,
  input  IA4,
  input  IA5,
  input  REG0,
  input  F_Z,
  input  SEL_ACC,
  input  EQUAL0001,
  input  GRP_LDI_CPI,
  input  [7:0] LBUS,
  output CONDITION_DONE
);

  wire and_1_out, and_2_out, and_3_out, and_4_out, and_5_out, and_6_out, and_7_out, and_8_out, and_9_out,
       and_10_out, and_11_out, and_12_out, COND0, COND1, COND2, COND3, d_latch_1_q, nand_1_out, nor_5_out,
       nor_6_out, nor_7_out, or_1_out, or_2_out, or_3_out, S_LATCH_q, xnor_1_out;

  or or_1 (or_1_out, PLA50, ~IA5);  // OR_Gate
  nor nor_1 (COND0, IA4, ~or_1_out);  // NOR_Gate
  nor nor_2 (COND1, ~IA4, ~or_1_out);  // NOR_Gate
  nor nor_3 (COND2, IA4, or_1_out);
  nor nor_4 (COND3, ~IA4, or_1_out);  // NOR_Gate
  or or_2 (or_2_out, PLA5, PLA7);
  and and_1 (and_1_out, LBUS[6], COND0);
  and and_2 (and_2_out, LBUS[0], COND1);
  and and_3 (and_3_out, LBUS[2], COND2);
  and and_4 (and_4_out, LBUS[7], COND3);
  and and_5 (and_5_out, M1, PLA53);
  and and_6 (and_6_out, M2, PLA50);
  and and_7 (and_7_out, M3, ~W184);  // AND_Gate
  and and_8 (and_8_out, M2, PLA8);
  and and_9 (and_9_out, or_2_out, M3);
  nand nand_1 (nand_1_out, M3, GRP_LDI_CPI);
  D_LATCH d_latch_1 (.EN(CLK), .D(SEL_ACC), .Q(d_latch_1_q));  // open: nQ
  nor nor_5 (nor_5_out, and_1_out, and_2_out, and_3_out, and_4_out);
  or or_3 (or_3_out, and_5_out, and_6_out, and_7_out);
  nor nor_6 (nor_6_out, and_8_out, and_9_out);
  and and_10 (and_10_out, ~CLK, ~d_latch_1_q);  // AND_Gate
  and and_11 (and_11_out, xnor_1_out, or_3_out);
  nor nor_7 (nor_7_out, ~F_Z, nor_6_out);  // NOR_Gate
  and and_12 (and_12_out, ~nand_1_out, ~EQUAL0001);  // AND_Gate
  D_Flip_Flop #(.trigger("high")) S_LATCH (
    .clk(and_10_out), .D(nor_5_out), .Q(S_LATCH_q));  // open: Qn, preset, en, reset
  or or_4 (CONDITION_DONE, and_11_out, nor_7_out, and_12_out);
  xnor xnor_1 (xnor_1_out, S_LATCH_q, REG0);

  // Notes on the sheet:
  //   CONDITION / SHIFT DECODER
  //   DW419
  //   W265
  //   W279
  //   W220
  //   W383
  //   W420
  //   W448
endmodule
