// Logisim project pad_inout.circ as structural Verilog: 1 circuit, main circuit main
module main (
  input  read,
  input  vout_from_core,
  input  vin_from_pad,
  output set_zero,
  output pad,
  output n_set_one,
  output vin_to_core
);

  wire nand_1_out, nor_1_out, not_1_out, not_2_out, not_3_out, not_4_out, not_5_out, not_6_out;

  not not_1 (not_1_out, read);
  not not_2 (not_2_out, vout_from_core);
  not not_3 (not_3_out, vin_from_pad);
  not not_4 (not_4_out, not_3_out);
  nand nand_1 (nand_1_out, not_1_out, not_2_out);
  nor nor_1 (nor_1_out, not_2_out, not_5_out);
  not not_5 (not_5_out, not_1_out);
  not not_6 (not_6_out, not_4_out);
  not not_7 (vin_to_core, not_6_out);
  not not_8 (set_zero, nand_1_out);
  not not_9 (n_set_one, nor_1_out);
  Transistor #(.\type ("n")) transistor_1 (.in(1'b0), .out(pad), .gate(set_zero));
  Transistor transistor_2 (.in(1'b1), .out(pad), .gate(n_set_one));
endmodule
